// Logisim project IT1601_U201614898_潘翔.circ as structural Verilog: 29 circuits, main circuit ◇单周期MIPS
module \单周期MIPS  (
);

  wire and_1_out, and_2_out, and_4_out, and_5_out, BLEZ, CLK, comparator_1_eq, compare, Go, HW_sel, JMP, JR,
       LOCK, mips_alu_1_equal, multiplexer_1_out, multiplexer_15_out, or_1_out, or_2_out, RST, SH, SignedExt,
       SRLV, Syscall, XORI, \硬布线控制器_1_alu_src , \硬布线控制器_1_beq , \硬布线控制器_1_bne , \硬布线控制器_1_jal ,
       \硬布线控制器_1_memtoreg , \硬布线控制器_1_memwrite , \硬布线控制器_1_regdst , \硬布线控制器_1_regwrite ;
  wire [3:0] multiplexer_18_out, multiplexer_19_out, \硬布线控制器_1_alu_op ;
  wire [4:0] multiplexer_4_out, multiplexer_5_out, multiplexer_7_out, multiplexer_8_out, multiplexer_13_out,
       shamt;
  wire [15:0] \总周期数 , \无条件分支数 , \条件分支成功数 ;
  wire [27:2] rom_1_data;
  wire [31:0] adder_1_out, adder_2_out, bit_extender_1_out, bit_extender_2_out, LedData, mips_alu_1_result,
       mips_ram_1_p7, multiplexer_2_out, multiplexer_3_out, multiplexer_6_out, multiplexer_9_out,
       multiplexer_10_out, multiplexer_11_out, multiplexer_12_out, multiplexer_14_out, multiplexer_16_out,
       multiplexer_17_out, multiplexer_20_out, PC_q, R1, R2, shifter_1_out, undriven;
  wire [31:26] rom_1_data_2;

  Button \u_总复位  (.out(RST));
  Button \u_继续运行  (.out(Go));
  Clock clock_1 (.out(CLK));
  Register #(.width(32)) PC (.D(multiplexer_2_out), .en(multiplexer_1_out), .Q(PC_q), .clk(CLK), .clr(RST));
  Multiplexer #(.enable("false")) multiplexer_1 (.in0(1'b1), .in1(1'b0), .out(multiplexer_1_out), .sel(and_1_out));
  and and_1 (and_1_out, LOCK, ~Go);  // AND_Gate
  Hex_Digit_Display hex_digit_display_1 (.value(LedData[27:24]));  // open: dp
  Hex_Digit_Display hex_digit_display_2 (.value(LedData[31:28]));  // open: dp
  Counter #(.width(16), .max('hffff)) counter_1 (
    .count(JMP), .Q(\无条件分支数 ), .clk(CLK), .clr(RST));  // open: load, D, carry
  Counter #(.width(16), .max('hffff)) counter_2 (
    .count(compare), .Q(\条件分支成功数 ), .clk(CLK), .clr(RST));  // open: load, D, carry
  Counter #(.width(16), .max('hffff)) counter_3 (
    .count(multiplexer_1_out), .Q(\总周期数 ), .clk(CLK), .clr(RST));  // open: load, D, carry
  Multiplexer #(.width(32), .enable("false")) multiplexer_2 (
    .in0(multiplexer_6_out), .in1(multiplexer_3_out), .out(multiplexer_2_out), .sel(JMP));
  Multiplexer #(.width(32), .enable("false")) multiplexer_3 (
    .in0({4'b0000, rom_1_data[27:13], shamt, rom_1_data[7:2], 2'b00}), .in1(R1), .out(multiplexer_3_out),
    .sel(JR));
  Hex_Digit_Display hex_digit_display_3 (.value(LedData[19:16]));  // open: dp
  Hex_Digit_Display hex_digit_display_4 (.value(LedData[23:20]));  // open: dp
  Hex_Digit_Display hex_digit_display_5 (.value(LedData[11:8]));  // open: dp
  Hex_Digit_Display hex_digit_display_6 (.value(LedData[15:12]));  // open: dp
  LED led_1 (.in(XORI));
  ROM #(.addrWidth(10), .dataWidth(32)) rom_1 (
    .addr(PC_q[11:2]), .data({rom_1_data_2, rom_1_data[27:13], shamt, rom_1_data[7:2]}));  // open: sel
  Adder #(.width(32)) adder_1 (.a(PC_q), .b(32'h4), .out(adder_1_out));  // open: cin, cout
  Hex_Digit_Display hex_digit_display_7 (.value(LedData[7:4]));  // open: dp
  Hex_Digit_Display hex_digit_display_8 (.value(LedData[3:0]));  // open: dp
  Multiplexer #(.width(5), .enable("false")) multiplexer_4 (
    .in0(rom_1_data[27:23]), .in1(5'b00010), .out(multiplexer_4_out), .sel(Syscall));
  \硬布线控制器  \u_硬布线控制器_1  (
    .Func(rom_1_data[7:2]), .OP(rom_1_data_2), .ALU_OP(\硬布线控制器_1_alu_op ), .MemToReg(\硬布线控制器_1_memtoreg ),
    .MemWrite(\硬布线控制器_1_memwrite ), .ALU_SRC(\硬布线控制器_1_alu_src ), .RegWrite(\硬布线控制器_1_regwrite ),
    .SysCALL(Syscall), .SignedExt(SignedExt), .RegDst(\硬布线控制器_1_regdst ), .JR(JR), .JMP(JMP),
    .Beq(\硬布线控制器_1_beq ), .JAL(\硬布线控制器_1_jal ), .Bne(\硬布线控制器_1_bne ), .SRLV(SRLV), .XORI(XORI), .SH(SH),
    .BLEZ(BLEZ));  // open: ERET, RS, RD, MFC_0, MTC_0
  Multiplexer #(.width(5), .enable("false")) multiplexer_5 (
    .in0(rom_1_data[22:18]), .in1(5'b00100), .out(multiplexer_5_out), .sel(Syscall));
  Multiplexer #(.width(32), .enable("false")) multiplexer_6 (
    .in0(adder_1_out), .in1(adder_2_out), .out(multiplexer_6_out), .sel(compare));
  Multiplexer #(.width(5), .enable("false")) multiplexer_7 (
    .in0(rom_1_data[22:18]), .in1(rom_1_data[17:13]), .out(multiplexer_7_out), .sel(\硬布线控制器_1_regdst ));
  Multiplexer #(.width(5), .enable("false")) multiplexer_8 (
    .in0(multiplexer_7_out), .in1({5{1'b1}}), .out(multiplexer_8_out), .sel(\硬布线控制器_1_jal ));
  assign bit_extender_1_out = {{16{1'b0}}, {rom_1_data[17:13], shamt, rom_1_data[7:2]}};  // Bit_Extender bit_extender_1
  assign bit_extender_2_out = {{16{rom_1_data[17]}}, {rom_1_data[17:13], shamt, rom_1_data[7:2]}};  // Bit_Extender bit_extender_2
  // Probe on \总周期数 
  // Probe on \无条件分支数 
  // Probe on \条件分支成功数 
  Multiplexer #(.width(32), .enable("false")) multiplexer_9 (
    .in0(multiplexer_20_out), .in1(adder_1_out), .out(multiplexer_9_out), .sel(\硬布线控制器_1_jal ));
  Multiplexer #(.width(32), .enable("false")) multiplexer_10 (
    .in0(bit_extender_1_out), .in1(bit_extender_2_out), .out(multiplexer_10_out), .sel(SignedExt));
  MIPS_Regifile mips_regifile_1 (
    .Din(multiplexer_9_out), .Clk(CLK), .R1(R1), .R2(R2), .WE(\硬布线控制器_1_regwrite ),
    .W_num(multiplexer_8_out), .R1_num(multiplexer_4_out), .R2_num(multiplexer_5_out));
  Multiplexer #(.width(32), .enable("false")) multiplexer_11 (
    .in0(R2), .in1(multiplexer_10_out), .out(multiplexer_11_out), .sel(\硬布线控制器_1_alu_src ));
  Shifter #(.width(32)) shifter_1 (.in(bit_extender_2_out), .\dist (5'b00010), .out(shifter_1_out));
  LED led_2 (.in(\硬布线控制器_1_memwrite ));
  LED led_3 (.in(SH));
  or or_1 (or_1_out, SH, BLEZ);
  Adder #(.width(32)) adder_2 (.a(shifter_1_out), .b(adder_1_out), .out(adder_2_out));  // open: cin, cout
  Comparator #(.width(32)) comparator_1 (.a(R1), .b(32'h22), .eq(comparator_1_eq));  // open: gt, lt
  Multiplexer #(.width(32), .enable("false")) multiplexer_12 (
    .in0(multiplexer_11_out), .in1({32{1'b0}}), .out(multiplexer_12_out), .sel(or_1_out));
  Multiplexer #(.width(5), .enable("false")) multiplexer_13 (
    .in0(shamt), .in1(R1[4:0]), .out(multiplexer_13_out), .sel(SRLV));
  MIPS_ALU mips_alu_1 (
    .X(R1), .Y(multiplexer_12_out), .AluOP(\硬布线控制器_1_alu_op ), .Equal(mips_alu_1_equal),
    .Result({mips_alu_1_result[31:2], HW_sel, mips_alu_1_result[0]}), .shamt(multiplexer_13_out));  // open: Result_2
  and and_2 (and_2_out, comparator_1_eq, Syscall);
  and and_3 (LOCK, ~comparator_1_eq, Syscall);  // AND_Gate
  and and_4 (and_4_out, \硬布线控制器_1_beq , mips_alu_1_equal);
  and and_5 (and_5_out, ~mips_alu_1_equal, \硬布线控制器_1_bne );  // AND_Gate
  or or_2 (or_2_out, mips_alu_1_equal, mips_alu_1_result[0]);
  Multiplexer #(.width(32)) multiplexer_14 (
    .in0(undriven), .in1(R2), .out(multiplexer_14_out), .sel(and_2_out), .en(and_2_out));
  Register #(.width(32)) register_1 (.D(multiplexer_14_out), .Q(LedData), .clk(CLK), .clr(RST));  // open: en
  Multiplexer #(.enable("false")) multiplexer_15 (.in0(1'b0), .in1(or_2_out), .out(multiplexer_15_out), .sel(BLEZ));
  Multiplexer #(.width(32), .enable("false")) multiplexer_16 (
    .in0({{16{1'b0}}, R2[15:0]}), .in1({R2[15:0], {16{1'b0}}}), .out(multiplexer_16_out), .sel(HW_sel));
  or or_3 (compare, and_4_out, and_5_out, multiplexer_15_out);
  Multiplexer #(.width(32), .enable("false")) multiplexer_17 (
    .in0(R2), .in1(multiplexer_16_out), .out(multiplexer_17_out), .sel(SH));
  Multiplexer #(.width(4), .enable("false")) multiplexer_18 (
    .in0(4'b1111), .in1(multiplexer_19_out), .out(multiplexer_18_out), .sel(SH));
  Multiplexer #(.width(4), .enable("false")) multiplexer_19 (
    .in0(4'b0011), .in1(4'b1100), .out(multiplexer_19_out), .sel(HW_sel));
  // MIPS_RAM mips_ram_1: pin names not known; wires that end beside it: mips_alu_1_result[21:2], multiplexer_17_out, \硬布线控制器_1_memwrite , multiplexer_18_out, CLK, RST, mips_ram_1_p7
  Multiplexer #(.width(32), .enable("false")) multiplexer_20 (
    .in0({mips_alu_1_result[31:2], HW_sel, mips_alu_1_result[0]}), .in1(mips_ram_1_p7),
    .out(multiplexer_20_out), .sel(\硬布线控制器_1_memtoreg ));

  // Notes on the sheet:
  //   数码管输出应该用寄存器锁存，否则显示数据只能一闪而过
  //   可以通过项目增加Logisim库的方式将前几次实验完成的电路作为子电路引入到本电路中使用
  //   指令存储器
  //   OP
  //   rs
  //   指令字
  //   contents of rom_1 (hex, n*v repeats v):
  //   20080001 20090003 20110876 118d00 112020 20020022 c 200b0008 1118806 1318806 112020 20020022 c
  //   216bffff 1560fff9 2002000a c
  //   rt
  //   rd
  //   数码管输出
  //   JMP
  //   OP
  //   Func
  //   Func
  //   Beq
  //   Bne
  //   MemToReg
  //   MemWrite
  //   AluOP
  //   AluSrcB
  //   RegWrite
  //   JAL
  //   RegDst
  //   Syscall
  //   总复位信号应将除ROM以外所有存储组件全部清零
endmodule

// 单周期硬布线控制器
module \硬布线控制器  (
  input  [5:0] OP,
  input  [5:0] Func,
  input  [4:0] RS,
  input  [4:0] RD,
  output [3:0] ALU_OP,
  output MFC_0,
  output MTC_0,
  output MemToReg,
  output MemWrite,
  output ALU_SRC,
  output RegWrite,
  output SysCALL,
  output SignedExt,
  output RegDst,
  output Beq,
  output Bne,
  output JR,
  output JMP,
  output JAL,
  output SRLV,
  output XORI,
  output SH,
  output BLEZ,
  output ERET
);

  wire comparator_1_eq, comparator_2_eq, comparator_3_eq, comparator_4_eq, comparator_5_eq, comparator_6_eq;

  \运算控制器  \u_运算控制器_1  (
    .OP0(OP[0]), .OP1(OP[1]), .OP2(OP[2]), .OP3(OP[3]), .OP4(OP[4]), .OP5(OP[5]), .F0(Func[0]), .F1(Func[1]),
    .F2(Func[2]), .F3(Func[3]), .F4(Func[4]), .F5(Func[5]), .S0(ALU_OP[0]), .S1(ALU_OP[1]), .S2(ALU_OP[2]),
    .S3(ALU_OP[3]));
  \控制信号生成  \u_控制信号生成_1  (
    .OP0(OP[0]), .OP1(OP[1]), .OP2(OP[2]), .OP3(OP[3]), .OP4(OP[4]), .OP5(OP[5]), .F0(Func[0]), .F1(Func[1]),
    .F2(Func[2]), .F3(Func[3]), .F4(Func[4]), .F5(Func[5]), .MemToReg(MemToReg), .MemWrite(MemWrite),
    .ALU_SRC(ALU_SRC), .RegWrite(RegWrite), .SysCALL(SysCALL), .SignedExt(SignedExt), .RegDst(RegDst),
    .BEQ(Beq), .BNE(Bne), .JR(JR), .JMP(JMP), .JAL(JAL));
  CCMB_Conrtoller ccmb_conrtoller_1 (
    .OP0(OP[0]), .OP1(OP[1]), .OP2(OP[2]), .OP3(OP[3]), .SRLV(SRLV), .OP4(OP[4]), .OP5(OP[5]), .F0(Func[0]),
    .F1(Func[1]), .XORI(XORI), .F2(Func[2]), .F3(Func[3]), .SH(SH), .F4(Func[4]), .F5(Func[5]), .BLEZ(BLEZ));
  Comparator #(.width(6)) comparator_1 (.a(OP), .b(6'b010000), .eq(comparator_1_eq));  // open: gt, lt
  Comparator #(.width(6)) comparator_2 (.a(Func), .b(6'b011000), .eq(comparator_2_eq));  // open: gt, lt
  Comparator #(.width(6)) comparator_3 (.a(OP), .b(6'b010000), .eq(comparator_3_eq));  // open: gt, lt
  Comparator #(.width(5)) comparator_4 (.a(RS), .b({5{1'b0}}), .eq(comparator_4_eq));  // open: gt, lt
  Comparator #(.width(6)) comparator_5 (.a(OP), .b(6'b010000), .eq(comparator_5_eq));  // open: gt, lt
  Comparator #(.width(5)) comparator_6 (.a(RS), .b(5'b00100), .eq(comparator_6_eq));  // open: gt, lt
  and and_1 (ERET, comparator_1_eq, comparator_2_eq);
  and and_2 (MFC_0, comparator_3_eq, comparator_4_eq);
  and and_3 (MTC_0, comparator_5_eq, comparator_6_eq);

  // Other names for the same wires on the sheet: OP_CODE[5:0] = OP

  // Notes on the sheet:
  //   运算器控制器，根据指令生成运算器功能选择信号
  //   控制信号生成，产生数据通路需要的其他控制信号
endmodule

// 运算器控制器
module \运算控制器  (
  input  OP0,
  input  OP1,
  input  OP2,
  input  OP3,
  input  OP4,
  input  OP5,
  input  F0,
  input  F1,
  input  F2,
  input  F3,
  input  F4,
  input  F5,
  output S0,
  output S1,
  output S2,
  output S3
);

  wire and_1_out, and_2_out, and_3_out, and_4_out, and_5_out, and_6_out, and_7_out, and_8_out, and_9_out,
       and_10_out, and_11_out, and_12_out, and_13_out, and_14_out, and_15_out, and_16_out, and_17_out,
       and_18_out, and_19_out, and_20_out, and_21_out, and_22_out, and_23_out, and_24_out, and_25_out,
       and_26_out, and_27_out, and_28_out, and_29_out, and_30_out, and_31_out, and_32_out, and_33_out,
       and_34_out, and_35_out, and_36_out, and_37_out, and_38_out, and_39_out, and_40_out, and_41_out,
       and_42_out, not_1_out, not_2_out, not_3_out, not_4_out, not_5_out, not_6_out, not_7_out, not_8_out,
       not_9_out, not_10_out, not_11_out, not_12_out, not_13_out, not_14_out, not_15_out, not_16_out,
       not_17_out, not_18_out, not_19_out, not_20_out, not_21_out, not_22_out, not_23_out, not_24_out,
       not_25_out, not_26_out, not_27_out, not_28_out, not_29_out, not_30_out, not_31_out, not_32_out,
       not_33_out, not_34_out, not_35_out, not_36_out, not_37_out, not_38_out, not_39_out, not_40_out,
       not_41_out, not_42_out, not_43_out, not_44_out, not_45_out, not_46_out, not_47_out, not_48_out,
       not_49_out, not_50_out, not_51_out, not_52_out, not_53_out, not_54_out, not_55_out, not_56_out,
       not_57_out, not_58_out, not_59_out, not_60_out, not_61_out, not_62_out, not_63_out, not_64_out,
       not_65_out, not_66_out, not_67_out, not_68_out, not_69_out, not_70_out, not_71_out, not_72_out,
       not_73_out, not_74_out, not_75_out, not_76_out, not_77_out, not_78_out, not_79_out, not_80_out,
       not_81_out, not_82_out, not_83_out, not_84_out, not_85_out, not_86_out, not_87_out, not_88_out,
       not_89_out, not_90_out, not_91_out, not_92_out, not_93_out, not_94_out, not_95_out, not_96_out,
       not_97_out, not_98_out, not_99_out, not_100_out, not_101_out, not_102_out, not_103_out, not_104_out,
       not_105_out, not_106_out, not_107_out, not_108_out, not_109_out, not_110_out, not_111_out,
       not_112_out, not_113_out, not_114_out, not_115_out, not_116_out, not_117_out, not_118_out,
       not_119_out, not_120_out, not_121_out, not_122_out, not_123_out, not_124_out, not_125_out,
       not_126_out, not_127_out, not_128_out, not_129_out, not_130_out, not_131_out, not_132_out,
       not_133_out, not_134_out, not_135_out, not_136_out, not_137_out, not_138_out, not_139_out,
       not_140_out, not_141_out, not_142_out, not_143_out, not_144_out, not_145_out, not_146_out,
       not_147_out, not_148_out, not_149_out, not_150_out, not_151_out, not_152_out, not_153_out,
       not_154_out, not_155_out, not_156_out, not_157_out, not_158_out, not_159_out, not_160_out,
       not_161_out, not_162_out, not_163_out, not_164_out, not_165_out, not_166_out, not_167_out,
       not_168_out, not_169_out, not_170_out, not_171_out, not_172_out, not_173_out, not_174_out,
       not_175_out, not_176_out, not_177_out, not_178_out, not_179_out, not_180_out, not_181_out,
       not_182_out, not_183_out, not_184_out, not_185_out, not_186_out, not_187_out, not_188_out,
       not_189_out, not_190_out, not_191_out, not_192_out, not_193_out, not_194_out, not_195_out,
       not_196_out, not_197_out, not_198_out, not_199_out, not_200_out, not_201_out, not_202_out,
       not_203_out, not_204_out, not_205_out, not_206_out, not_207_out, not_208_out, not_209_out,
       not_210_out, not_211_out, not_212_out, not_213_out, not_214_out, not_215_out, not_216_out,
       not_217_out, not_218_out, not_219_out, not_220_out, not_221_out, not_222_out, not_223_out,
       not_224_out, not_225_out, not_226_out, not_227_out, not_228_out, not_229_out, not_230_out,
       not_231_out, not_232_out, not_233_out, not_234_out, not_235_out, not_236_out, not_237_out,
       not_238_out, not_239_out, not_240_out, not_241_out, not_242_out, not_243_out, not_244_out,
       not_245_out, not_246_out, not_247_out, not_248_out, not_249_out, not_250_out, not_251_out,
       not_252_out, not_253_out, not_254_out, not_255_out, not_256_out, not_257_out, not_258_out,
       not_259_out, not_260_out, not_261_out, not_262_out, not_263_out, not_264_out, not_265_out,
       not_266_out, not_267_out, not_268_out, not_269_out, not_270_out;

  not not_1 (not_1_out, OP5);
  not not_2 (not_2_out, OP4);
  not not_3 (not_3_out, OP3);
  not not_4 (not_4_out, OP2);
  not not_5 (not_5_out, OP1);
  not not_6 (not_6_out, OP0);
  not not_7 (not_7_out, F5);
  not not_8 (not_8_out, F4);
  not not_9 (not_9_out, F3);
  not not_10 (not_10_out, F2);
  not not_11 (not_11_out, OP5);
  not not_12 (not_12_out, OP4);
  not not_13 (not_13_out, OP3);
  not not_14 (not_14_out, OP2);
  not not_15 (not_15_out, OP1);
  not not_16 (not_16_out, OP0);
  not not_17 (not_17_out, F4);
  not not_18 (not_18_out, F3);
  not not_19 (not_19_out, F2);
  not not_20 (not_20_out, F1);
  not not_21 (not_21_out, F0);
  not not_22 (not_22_out, OP5);
  not not_23 (not_23_out, OP4);
  not not_24 (not_24_out, OP3);
  not not_25 (not_25_out, OP2);
  not not_26 (not_26_out, OP1);
  not not_27 (not_27_out, OP0);
  not not_28 (not_28_out, F4);
  not not_29 (not_29_out, F3);
  not not_30 (not_30_out, F2);
  not not_31 (not_31_out, F1);
  not not_32 (not_32_out, OP5);
  not not_33 (not_33_out, OP4);
  not not_34 (not_34_out, OP3);
  not not_35 (not_35_out, OP2);
  not not_36 (not_36_out, OP1);
  not not_37 (not_37_out, OP0);
  not not_38 (not_38_out, F4);
  not not_39 (not_39_out, F3);
  not not_40 (not_40_out, F1);
  not not_41 (not_41_out, F0);
  not not_42 (not_42_out, OP5);
  not not_43 (not_43_out, OP4);
  not not_44 (not_44_out, OP3);
  not not_45 (not_45_out, OP2);
  not not_46 (not_46_out, OP1);
  not not_47 (not_47_out, OP0);
  not not_48 (not_48_out, F4);
  not not_49 (not_49_out, F2);
  not not_50 (not_50_out, F0);
  not not_51 (not_51_out, OP5);
  not not_52 (not_52_out, OP4);
  not not_53 (not_53_out, OP2);
  not not_54 (not_54_out, OP1);
  not not_55 (not_55_out, OP0);
  not not_56 (not_56_out, OP5);
  not not_57 (not_57_out, OP4);
  not not_58 (not_58_out, OP1);
  not not_59 (not_59_out, OP0);
  not not_60 (not_60_out, OP5);
  not not_61 (not_61_out, OP4);
  not not_62 (not_62_out, OP2);
  not not_63 (not_63_out, OP1);
  not not_64 (not_64_out, OP5);
  not not_65 (not_65_out, OP4);
  not not_66 (not_66_out, OP2);
  not not_67 (not_67_out, OP0);
  not not_68 (not_68_out, OP4);
  not not_69 (not_69_out, OP3);
  not not_70 (not_70_out, OP2);
  not not_71 (not_71_out, OP4);
  not not_72 (not_72_out, OP2);
  not not_73 (not_73_out, OP5);
  not not_74 (not_74_out, OP4);
  not not_75 (not_75_out, OP0);
  not not_76 (not_76_out, OP4);
  not not_77 (not_77_out, OP2);
  not not_78 (not_78_out, OP1);
  not not_79 (not_79_out, OP5);
  not not_80 (not_80_out, OP4);
  not not_81 (not_81_out, OP3);
  not not_82 (not_82_out, OP0);
  not not_83 (not_83_out, OP5);
  not not_84 (not_84_out, OP4);
  not not_85 (not_85_out, OP3);
  not not_86 (not_86_out, OP2);
  not not_87 (not_87_out, OP1);
  not not_88 (not_88_out, OP0);
  not not_89 (not_89_out, F5);
  not not_90 (not_90_out, F4);
  not not_91 (not_91_out, F3);
  not not_92 (not_92_out, F2);
  not not_93 (not_93_out, F0);
  not not_94 (not_94_out, OP5);
  not not_95 (not_95_out, OP4);
  not not_96 (not_96_out, OP3);
  not not_97 (not_97_out, OP2);
  not not_98 (not_98_out, OP1);
  not not_99 (not_99_out, OP0);
  not not_100 (not_100_out, F4);
  not not_101 (not_101_out, F3);
  not not_102 (not_102_out, F2);
  not not_103 (not_103_out, F0);
  not not_104 (not_104_out, OP5);
  not not_105 (not_105_out, OP4);
  not not_106 (not_106_out, OP3);
  not not_107 (not_107_out, OP2);
  not not_108 (not_108_out, OP1);
  not not_109 (not_109_out, OP0);
  not not_110 (not_110_out, F4);
  not not_111 (not_111_out, F3);
  not not_112 (not_112_out, F1);
  not not_113 (not_113_out, F0);
  not not_114 (not_114_out, OP5);
  not not_115 (not_115_out, OP4);
  not not_116 (not_116_out, OP3);
  not not_117 (not_117_out, OP2);
  not not_118 (not_118_out, OP1);
  not not_119 (not_119_out, OP0);
  not not_120 (not_120_out, F4);
  not not_121 (not_121_out, F3);
  not not_122 (not_122_out, OP5);
  not not_123 (not_123_out, OP4);
  not not_124 (not_124_out, OP3);
  not not_125 (not_125_out, OP2);
  not not_126 (not_126_out, OP1);
  not not_127 (not_127_out, OP0);
  not not_128 (not_128_out, F4);
  not not_129 (not_129_out, F2);
  not not_130 (not_130_out, F0);
  not not_131 (not_131_out, OP5);
  not not_132 (not_132_out, OP4);
  not not_133 (not_133_out, OP1);
  not not_134 (not_134_out, OP0);
  not not_135 (not_135_out, OP5);
  not not_136 (not_136_out, OP4);
  not not_137 (not_137_out, OP2);
  not not_138 (not_138_out, OP0);
  not not_139 (not_139_out, OP5);
  not not_140 (not_140_out, OP4);
  not not_141 (not_141_out, OP3);
  not not_142 (not_142_out, OP2);
  not not_143 (not_143_out, OP1);
  not not_144 (not_144_out, OP0);
  not not_145 (not_145_out, F5);
  not not_146 (not_146_out, F4);
  not not_147 (not_147_out, F3);
  not not_148 (not_148_out, F0);
  not not_149 (not_149_out, OP5);
  not not_150 (not_150_out, OP4);
  not not_151 (not_151_out, OP3);
  not not_152 (not_152_out, OP0);
  not not_153 (not_153_out, OP5);
  not not_154 (not_154_out, OP4);
  not not_155 (not_155_out, OP3);
  not not_156 (not_156_out, OP2);
  not not_157 (not_157_out, OP1);
  not not_158 (not_158_out, OP0);
  not not_159 (not_159_out, F4);
  not not_160 (not_160_out, F3);
  not not_161 (not_161_out, F2);
  not not_162 (not_162_out, F1);
  not not_163 (not_163_out, F0);
  not not_164 (not_164_out, OP5);
  not not_165 (not_165_out, OP4);
  not not_166 (not_166_out, OP3);
  not not_167 (not_167_out, OP2);
  not not_168 (not_168_out, OP1);
  not not_169 (not_169_out, OP0);
  not not_170 (not_170_out, F4);
  not not_171 (not_171_out, F3);
  not not_172 (not_172_out, F2);
  not not_173 (not_173_out, F1);
  not not_174 (not_174_out, OP5);
  not not_175 (not_175_out, OP4);
  not not_176 (not_176_out, OP3);
  not not_177 (not_177_out, OP2);
  not not_178 (not_178_out, OP1);
  not not_179 (not_179_out, OP0);
  not not_180 (not_180_out, F4);
  not not_181 (not_181_out, F3);
  not not_182 (not_182_out, F2);
  not not_183 (not_183_out, F0);
  not not_184 (not_184_out, OP5);
  not not_185 (not_185_out, OP4);
  not not_186 (not_186_out, OP3);
  not not_187 (not_187_out, OP2);
  not not_188 (not_188_out, OP1);
  not not_189 (not_189_out, OP0);
  not not_190 (not_190_out, F4);
  not not_191 (not_191_out, F3);
  not not_192 (not_192_out, F1);
  not not_193 (not_193_out, F0);
  not not_194 (not_194_out, OP5);
  not not_195 (not_195_out, OP4);
  not not_196 (not_196_out, OP3);
  not not_197 (not_197_out, OP2);
  not not_198 (not_198_out, OP1);
  not not_199 (not_199_out, OP0);
  not not_200 (not_200_out, F4);
  not not_201 (not_201_out, F2);
  not not_202 (not_202_out, OP5);
  not not_203 (not_203_out, OP4);
  not not_204 (not_204_out, OP2);
  not not_205 (not_205_out, OP1);
  not not_206 (not_206_out, OP0);
  not not_207 (not_207_out, OP5);
  not not_208 (not_208_out, OP4);
  not not_209 (not_209_out, OP1);
  not not_210 (not_210_out, OP0);
  not not_211 (not_211_out, OP5);
  not not_212 (not_212_out, OP4);
  not not_213 (not_213_out, OP2);
  not not_214 (not_214_out, OP1);
  not not_215 (not_215_out, OP4);
  not not_216 (not_216_out, OP3);
  not not_217 (not_217_out, OP2);
  not not_218 (not_218_out, OP4);
  not not_219 (not_219_out, OP2);
  not not_220 (not_220_out, OP4);
  not not_221 (not_221_out, OP2);
  not not_222 (not_222_out, OP1);
  not not_223 (not_223_out, OP5);
  not not_224 (not_224_out, OP4);
  not not_225 (not_225_out, OP3);
  not not_226 (not_226_out, OP2);
  not not_227 (not_227_out, OP1);
  not not_228 (not_228_out, OP0);
  not not_229 (not_229_out, F4);
  not not_230 (not_230_out, F3);
  not not_231 (not_231_out, F1);
  not not_232 (not_232_out, OP5);
  not not_233 (not_233_out, OP4);
  not not_234 (not_234_out, OP3);
  not not_235 (not_235_out, OP2);
  not not_236 (not_236_out, OP1);
  not not_237 (not_237_out, OP0);
  not not_238 (not_238_out, F4);
  not not_239 (not_239_out, F3);
  not not_240 (not_240_out, OP5);
  not not_241 (not_241_out, OP4);
  not not_242 (not_242_out, OP3);
  not not_243 (not_243_out, OP2);
  not not_244 (not_244_out, OP1);
  not not_245 (not_245_out, OP0);
  not not_246 (not_246_out, F4);
  not not_247 (not_247_out, F2);
  not not_248 (not_248_out, F0);
  not not_249 (not_249_out, OP5);
  not not_250 (not_250_out, OP4);
  not not_251 (not_251_out, OP3);
  not not_252 (not_252_out, OP2);
  not not_253 (not_253_out, OP1);
  not not_254 (not_254_out, OP0);
  not not_255 (not_255_out, F4);
  not not_256 (not_256_out, F2);
  not not_257 (not_257_out, OP5);
  not not_258 (not_258_out, OP4);
  not not_259 (not_259_out, OP2);
  not not_260 (not_260_out, OP0);
  not not_261 (not_261_out, OP5);
  not not_262 (not_262_out, OP4);
  not not_263 (not_263_out, OP1);
  not not_264 (not_264_out, OP5);
  not not_265 (not_265_out, OP4);
  not not_266 (not_266_out, OP0);
  not not_267 (not_267_out, OP5);
  not not_268 (not_268_out, OP4);
  not not_269 (not_269_out, OP3);
  not not_270 (not_270_out, OP0);
  and and_1 (and_1_out, not_1_out, not_2_out, not_3_out, not_4_out, not_5_out, not_6_out, not_7_out, not_8_out, not_9_out, not_10_out, F1, F0);
  and and_2 (and_2_out, not_11_out, not_12_out, not_13_out, not_14_out, not_15_out, not_16_out, F5, not_17_out, not_18_out, not_19_out, not_20_out, not_21_out);
  and and_3 (and_3_out, not_22_out, not_23_out, not_24_out, not_25_out, not_26_out, not_27_out, F5, not_28_out, not_29_out, not_30_out, not_31_out, F0);
  and and_4 (and_4_out, not_32_out, not_33_out, not_34_out, not_35_out, not_36_out, not_37_out, F5, not_38_out, not_39_out, F2, not_40_out, not_41_out);
  and and_5 (and_5_out, not_42_out, not_43_out, not_44_out, not_45_out, not_46_out, not_47_out, F5, not_48_out, F3, not_49_out, F1, not_50_out);
  and and_6 (and_6_out, not_51_out, not_52_out, OP3, not_53_out, not_54_out, not_55_out);
  and and_7 (and_7_out, not_56_out, not_57_out, OP3, OP2, not_58_out, not_59_out);
  and and_8 (and_8_out, not_60_out, not_61_out, OP3, not_62_out, not_63_out, OP0);
  and and_9 (and_9_out, not_64_out, not_65_out, OP3, not_66_out, OP1, not_67_out);
  and and_10 (and_10_out, OP5, not_68_out, not_69_out, not_70_out, OP1, OP0);
  and and_11 (and_11_out, OP5, not_71_out, OP3, not_72_out, OP1, OP0);
  and and_12 (and_12_out, not_73_out, not_74_out, OP3, OP2, OP1, not_75_out);
  and and_13 (and_13_out, OP5, not_76_out, OP3, not_77_out, not_78_out, OP0);
  and and_14 (and_14_out, not_79_out, not_80_out, not_81_out, OP2, OP1, not_82_out);
  and and_15 (and_15_out, not_83_out, not_84_out, not_85_out, not_86_out, not_87_out, not_88_out, not_89_out, not_90_out, not_91_out, not_92_out, F1, not_93_out);
  and and_16 (and_16_out, not_94_out, not_95_out, not_96_out, not_97_out, not_98_out, not_99_out, F5, not_100_out, not_101_out, not_102_out, F1, not_103_out);
  and and_17 (and_17_out, not_104_out, not_105_out, not_106_out, not_107_out, not_108_out, not_109_out, F5, not_110_out, not_111_out, F2, not_112_out, not_113_out);
  and and_18 (and_18_out, not_114_out, not_115_out, not_116_out, not_117_out, not_118_out, not_119_out, F5, not_120_out, not_121_out, F2, F1, F0);
  and and_19 (and_19_out, not_122_out, not_123_out, not_124_out, not_125_out, not_126_out, not_127_out, F5, not_128_out, F3, not_129_out, F1, not_130_out);
  and and_20 (and_20_out, not_131_out, not_132_out, OP3, OP2, not_133_out, not_134_out);
  and and_21 (and_21_out, not_135_out, not_136_out, OP3, not_137_out, OP1, not_138_out);
  and and_22 (and_22_out, not_139_out, not_140_out, not_141_out, not_142_out, not_143_out, not_144_out, not_145_out, not_146_out, not_147_out, F2, F1, not_148_out);
  and and_23 (and_23_out, not_149_out, not_150_out, not_151_out, OP2, OP1, not_152_out);
  and and_24 (and_24_out, not_153_out, not_154_out, not_155_out, not_156_out, not_157_out, not_158_out, F5, not_159_out, not_160_out, not_161_out, not_162_out, not_163_out);
  and and_25 (and_25_out, not_164_out, not_165_out, not_166_out, not_167_out, not_168_out, not_169_out, F5, not_170_out, not_171_out, not_172_out, not_173_out, F0);
  and and_26 (and_26_out, not_174_out, not_175_out, not_176_out, not_177_out, not_178_out, not_179_out, F5, not_180_out, not_181_out, not_182_out, F1, not_183_out);
  and and_27 (and_27_out, not_184_out, not_185_out, not_186_out, not_187_out, not_188_out, not_189_out, F5, not_190_out, not_191_out, F2, not_192_out, not_193_out);
  and and_28 (and_28_out, not_194_out, not_195_out, not_196_out, not_197_out, not_198_out, not_199_out, F5, not_200_out, F3, not_201_out, F1, F0);
  and and_29 (and_29_out, not_202_out, not_203_out, OP3, not_204_out, not_205_out, not_206_out);
  and and_30 (and_30_out, not_207_out, not_208_out, OP3, OP2, not_209_out, not_210_out);
  and and_31 (and_31_out, not_211_out, not_212_out, OP3, not_213_out, not_214_out, OP0);
  and and_32 (and_32_out, OP5, not_215_out, not_216_out, not_217_out, OP1, OP0);
  and and_33 (and_33_out, OP5, not_218_out, OP3, not_219_out, OP1, OP0);
  and and_34 (and_34_out, OP5, not_220_out, OP3, not_221_out, not_222_out, OP0);
  and and_35 (and_35_out, not_223_out, not_224_out, not_225_out, not_226_out, not_227_out, not_228_out, F5, not_229_out, not_230_out, F2, not_231_out, F0);
  and and_36 (and_36_out, not_232_out, not_233_out, not_234_out, not_235_out, not_236_out, not_237_out, F5, not_238_out, not_239_out, F2, F1, F0);
  and and_37 (and_37_out, not_240_out, not_241_out, not_242_out, not_243_out, not_244_out, not_245_out, F5, not_246_out, F3, not_247_out, F1, not_248_out);
  and and_38 (and_38_out, not_249_out, not_250_out, not_251_out, not_252_out, not_253_out, not_254_out, F5, not_255_out, F3, not_256_out, F1, F0);
  and and_39 (and_39_out, not_257_out, not_258_out, OP3, not_259_out, OP1, not_260_out);
  and and_40 (and_40_out, not_261_out, not_262_out, OP3, OP2, not_263_out, OP0);
  and and_41 (and_41_out, not_264_out, not_265_out, OP3, OP2, OP1, not_266_out);
  and and_42 (and_42_out, not_267_out, not_268_out, not_269_out, OP2, OP1, not_270_out);
  or or_1 (S1, and_15_out, and_16_out, and_17_out, and_18_out, and_19_out, and_20_out, and_21_out, and_22_out, and_23_out);
  or or_2 (S2, and_24_out, and_25_out, and_26_out, and_27_out, and_28_out, and_29_out, and_30_out, and_31_out, and_32_out, and_33_out, and_34_out);
  or or_3 (S3, and_35_out, and_36_out, and_37_out, and_38_out, and_39_out, and_40_out, and_41_out, and_42_out);
  or or_4 (S0, and_1_out, and_2_out, and_3_out, and_4_out, and_5_out, and_6_out, and_7_out, and_8_out, and_9_out, and_10_out, and_11_out, and_12_out, and_13_out, and_14_out);
endmodule

// 控制信号生成
module \控制信号生成  (
  input  OP0,
  input  OP1,
  input  OP2,
  input  OP3,
  input  OP4,
  input  OP5,
  input  F0,
  input  F1,
  input  F2,
  input  F3,
  input  F4,
  input  F5,
  output MemToReg,
  output MemWrite,
  output ALU_SRC,
  output RegWrite,
  output SysCALL,
  output SignedExt,
  output RegDst,
  output BEQ,
  output BNE,
  output JR,
  output JMP,
  output JAL
);

  wire and_2_out, and_3_out, and_4_out, and_5_out, and_6_out, and_7_out, and_8_out, and_9_out, and_10_out,
       and_11_out, and_12_out, and_13_out, and_14_out, and_15_out, and_16_out, and_17_out, and_18_out,
       and_19_out, and_20_out, and_21_out, and_22_out, and_23_out, and_24_out, and_25_out, and_26_out,
       and_27_out, and_28_out, and_29_out, and_30_out, and_31_out, and_32_out, and_33_out, and_35_out,
       and_36_out, and_37_out, and_38_out, and_39_out, and_40_out, and_41_out, and_42_out, and_43_out,
       and_44_out, and_45_out, and_46_out, and_47_out, and_48_out, and_49_out, and_50_out, and_51_out,
       and_52_out, and_56_out, and_57_out, and_58_out, not_1_out, not_2_out, not_3_out, not_4_out, not_5_out,
       not_6_out, not_7_out, not_8_out, not_9_out, not_10_out, not_11_out, not_12_out, not_13_out,
       not_14_out, not_15_out, not_16_out, not_17_out, not_18_out, not_19_out, not_20_out, not_21_out,
       not_22_out, not_23_out, not_24_out, not_25_out, not_26_out, not_27_out, not_28_out, not_29_out,
       not_30_out, not_31_out, not_32_out, not_33_out, not_34_out, not_35_out, not_36_out, not_37_out,
       not_38_out, not_39_out, not_40_out, not_41_out, not_42_out, not_43_out, not_44_out, not_45_out,
       not_46_out, not_47_out, not_48_out, not_49_out, not_50_out, not_51_out, not_52_out, not_53_out,
       not_54_out, not_55_out, not_56_out, not_57_out, not_58_out, not_59_out, not_60_out, not_61_out,
       not_62_out, not_63_out, not_64_out, not_65_out, not_66_out, not_67_out, not_68_out, not_69_out,
       not_70_out, not_71_out, not_72_out, not_73_out, not_74_out, not_75_out, not_76_out, not_77_out,
       not_78_out, not_79_out, not_80_out, not_81_out, not_82_out, not_83_out, not_84_out, not_85_out,
       not_86_out, not_87_out, not_88_out, not_89_out, not_90_out, not_91_out, not_92_out, not_93_out,
       not_94_out, not_95_out, not_96_out, not_97_out, not_98_out, not_99_out, not_100_out, not_101_out,
       not_102_out, not_103_out, not_104_out, not_105_out, not_106_out, not_107_out, not_108_out,
       not_109_out, not_110_out, not_111_out, not_112_out, not_113_out, not_114_out, not_115_out,
       not_116_out, not_117_out, not_118_out, not_119_out, not_120_out, not_121_out, not_122_out,
       not_123_out, not_124_out, not_125_out, not_126_out, not_127_out, not_128_out, not_129_out,
       not_130_out, not_131_out, not_132_out, not_133_out, not_134_out, not_135_out, not_136_out,
       not_137_out, not_138_out, not_139_out, not_140_out, not_141_out, not_142_out, not_143_out,
       not_144_out, not_145_out, not_146_out, not_147_out, not_148_out, not_149_out, not_150_out,
       not_151_out, not_152_out, not_153_out, not_154_out, not_155_out, not_156_out, not_157_out,
       not_158_out, not_159_out, not_160_out, not_161_out, not_162_out, not_163_out, not_164_out,
       not_165_out, not_166_out, not_167_out, not_168_out, not_169_out, not_170_out, not_171_out,
       not_172_out, not_173_out, not_174_out, not_175_out, not_176_out, not_177_out, not_178_out,
       not_179_out, not_180_out, not_181_out, not_182_out, not_183_out, not_184_out, not_185_out,
       not_186_out, not_187_out, not_188_out, not_189_out, not_190_out, not_191_out, not_192_out,
       not_193_out, not_194_out, not_195_out, not_196_out, not_197_out, not_198_out, not_199_out,
       not_200_out, not_201_out, not_202_out, not_203_out, not_204_out, not_205_out, not_206_out,
       not_207_out, not_208_out, not_209_out, not_210_out, not_211_out, not_212_out, not_213_out,
       not_214_out, not_215_out, not_216_out, not_217_out, not_218_out, not_219_out, not_220_out,
       not_221_out, not_222_out, not_223_out, not_224_out, not_225_out, not_226_out, not_227_out,
       not_228_out, not_229_out, not_230_out, not_231_out, not_232_out, not_233_out, not_234_out,
       not_235_out, not_236_out, not_237_out, not_238_out, not_239_out, not_240_out, not_241_out,
       not_242_out, not_243_out, not_244_out, not_245_out, not_246_out, not_247_out, not_248_out,
       not_249_out, not_250_out, not_251_out, not_252_out, not_253_out, not_254_out, not_255_out,
       not_256_out, not_257_out, not_258_out, not_259_out, not_260_out, not_261_out, not_262_out,
       not_263_out, not_264_out, not_265_out, not_266_out, not_267_out, not_268_out, not_269_out,
       not_270_out, not_271_out, not_272_out, not_273_out, not_274_out, not_275_out, not_276_out,
       not_277_out, not_278_out, not_279_out, not_280_out, not_281_out, not_282_out, not_283_out,
       not_284_out, not_285_out, not_286_out, not_287_out, not_288_out, not_289_out, not_290_out,
       not_291_out, not_292_out, not_293_out, not_294_out, not_295_out, not_296_out, not_297_out,
       not_298_out, not_299_out, not_300_out, not_301_out, not_302_out, not_303_out, not_304_out,
       not_305_out, not_306_out, not_307_out, not_308_out, not_309_out, not_310_out, not_311_out,
       not_312_out, not_313_out, not_314_out, not_315_out, not_316_out, not_317_out, not_318_out,
       not_319_out, not_320_out, not_321_out, not_322_out, not_323_out, not_324_out, not_325_out,
       not_326_out, not_327_out, not_328_out, not_329_out, not_330_out, not_331_out, not_332_out,
       not_333_out, not_334_out, not_335_out, not_336_out, not_337_out, not_338_out, not_339_out,
       not_340_out, not_341_out, not_342_out, not_343_out, not_344_out, not_345_out, not_346_out,
       not_347_out, not_348_out, not_349_out, not_350_out, not_351_out, not_352_out, not_353_out,
       not_354_out, not_355_out, not_356_out, not_357_out, not_358_out, not_359_out, not_360_out,
       not_361_out, not_362_out, not_363_out, not_364_out, not_365_out, not_366_out, not_367_out,
       not_368_out, not_369_out, not_370_out, not_371_out, not_372_out, not_373_out, not_374_out,
       not_375_out, not_376_out, not_377_out, not_378_out, not_379_out, not_380_out, not_381_out,
       not_382_out, not_383_out;

  not not_1 (not_1_out, OP4);
  not not_2 (not_2_out, OP3);
  not not_3 (not_3_out, OP2);
  not not_4 (not_4_out, OP4);
  not not_5 (not_5_out, OP2);
  not not_6 (not_6_out, OP5);
  not not_7 (not_7_out, OP4);
  not not_8 (not_8_out, OP0);
  not not_9 (not_9_out, OP4);
  not not_10 (not_10_out, OP2);
  not not_11 (not_11_out, OP1);
  not not_12 (not_12_out, OP5);
  not not_13 (not_13_out, OP4);
  not not_14 (not_14_out, OP2);
  not not_15 (not_15_out, OP1);
  not not_16 (not_16_out, OP0);
  not not_17 (not_17_out, OP5);
  not not_18 (not_18_out, OP4);
  not not_19 (not_19_out, OP1);
  not not_20 (not_20_out, OP0);
  not not_21 (not_21_out, OP5);
  not not_22 (not_22_out, OP4);
  not not_23 (not_23_out, OP2);
  not not_24 (not_24_out, OP1);
  not not_25 (not_25_out, OP5);
  not not_26 (not_26_out, OP4);
  not not_27 (not_27_out, OP2);
  not not_28 (not_28_out, OP0);
  not not_29 (not_29_out, OP5);
  not not_30 (not_30_out, OP4);
  not not_31 (not_31_out, OP1);
  not not_32 (not_32_out, OP4);
  not not_33 (not_33_out, OP3);
  not not_34 (not_34_out, OP2);
  not not_35 (not_35_out, OP4);
  not not_36 (not_36_out, OP2);
  not not_37 (not_37_out, OP5);
  not not_38 (not_38_out, OP4);
  not not_39 (not_39_out, OP0);
  not not_40 (not_40_out, OP4);
  not not_41 (not_41_out, OP2);
  not not_42 (not_42_out, OP1);
  not not_43 (not_43_out, OP5);
  not not_44 (not_44_out, OP4);
  not not_45 (not_45_out, OP3);
  not not_46 (not_46_out, OP2);
  not not_47 (not_47_out, OP1);
  not not_48 (not_48_out, OP0);
  not not_49 (not_49_out, F5);
  not not_50 (not_50_out, F4);
  not not_51 (not_51_out, F3);
  not not_52 (not_52_out, F2);
  not not_53 (not_53_out, F1);
  not not_54 (not_54_out, F0);
  not not_55 (not_55_out, OP5);
  not not_56 (not_56_out, OP4);
  not not_57 (not_57_out, OP3);
  not not_58 (not_58_out, OP2);
  not not_59 (not_59_out, OP1);
  not not_60 (not_60_out, OP0);
  not not_61 (not_61_out, F5);
  not not_62 (not_62_out, F4);
  not not_63 (not_63_out, F3);
  not not_64 (not_64_out, F2);
  not not_65 (not_65_out, OP5);
  not not_66 (not_66_out, OP4);
  not not_67 (not_67_out, OP3);
  not not_68 (not_68_out, OP2);
  not not_69 (not_69_out, OP1);
  not not_70 (not_70_out, OP0);
  not not_71 (not_71_out, F5);
  not not_72 (not_72_out, F4);
  not not_73 (not_73_out, F3);
  not not_74 (not_74_out, F2);
  not not_75 (not_75_out, F0);
  not not_76 (not_76_out, OP5);
  not not_77 (not_77_out, OP4);
  not not_78 (not_78_out, OP3);
  not not_79 (not_79_out, OP2);
  not not_80 (not_80_out, OP1);
  not not_81 (not_81_out, OP0);
  not not_82 (not_82_out, F4);
  not not_83 (not_83_out, F3);
  not not_84 (not_84_out, F2);
  not not_85 (not_85_out, F1);
  not not_86 (not_86_out, F0);
  not not_87 (not_87_out, OP5);
  not not_88 (not_88_out, OP4);
  not not_89 (not_89_out, OP3);
  not not_90 (not_90_out, OP2);
  not not_91 (not_91_out, OP1);
  not not_92 (not_92_out, OP0);
  not not_93 (not_93_out, F4);
  not not_94 (not_94_out, F3);
  not not_95 (not_95_out, F2);
  not not_96 (not_96_out, F1);
  not not_97 (not_97_out, OP5);
  not not_98 (not_98_out, OP4);
  not not_99 (not_99_out, OP3);
  not not_100 (not_100_out, OP2);
  not not_101 (not_101_out, OP1);
  not not_102 (not_102_out, OP0);
  not not_103 (not_103_out, F4);
  not not_104 (not_104_out, F3);
  not not_105 (not_105_out, F2);
  not not_106 (not_106_out, F0);
  not not_107 (not_107_out, OP5);
  not not_108 (not_108_out, OP4);
  not not_109 (not_109_out, OP3);
  not not_110 (not_110_out, OP2);
  not not_111 (not_111_out, OP1);
  not not_112 (not_112_out, OP0);
  not not_113 (not_113_out, F4);
  not not_114 (not_114_out, F3);
  not not_115 (not_115_out, F1);
  not not_116 (not_116_out, F0);
  not not_117 (not_117_out, OP5);
  not not_118 (not_118_out, OP4);
  not not_119 (not_119_out, OP3);
  not not_120 (not_120_out, OP2);
  not not_121 (not_121_out, OP1);
  not not_122 (not_122_out, OP0);
  not not_123 (not_123_out, F4);
  not not_124 (not_124_out, F3);
  not not_125 (not_125_out, F1);
  not not_126 (not_126_out, OP5);
  not not_127 (not_127_out, OP4);
  not not_128 (not_128_out, OP3);
  not not_129 (not_129_out, OP2);
  not not_130 (not_130_out, OP1);
  not not_131 (not_131_out, OP0);
  not not_132 (not_132_out, F4);
  not not_133 (not_133_out, F3);
  not not_134 (not_134_out, OP5);
  not not_135 (not_135_out, OP4);
  not not_136 (not_136_out, OP3);
  not not_137 (not_137_out, OP2);
  not not_138 (not_138_out, OP1);
  not not_139 (not_139_out, OP0);
  not not_140 (not_140_out, F4);
  not not_141 (not_141_out, F2);
  not not_142 (not_142_out, F0);
  not not_143 (not_143_out, OP5);
  not not_144 (not_144_out, OP4);
  not not_145 (not_145_out, OP3);
  not not_146 (not_146_out, OP2);
  not not_147 (not_147_out, OP1);
  not not_148 (not_148_out, OP0);
  not not_149 (not_149_out, F4);
  not not_150 (not_150_out, F2);
  not not_151 (not_151_out, OP5);
  not not_152 (not_152_out, OP4);
  not not_153 (not_153_out, OP3);
  not not_154 (not_154_out, OP2);
  not not_155 (not_155_out, OP5);
  not not_156 (not_156_out, OP4);
  not not_157 (not_157_out, OP2);
  not not_158 (not_158_out, OP1);
  not not_159 (not_159_out, OP0);
  not not_160 (not_160_out, OP5);
  not not_161 (not_161_out, OP4);
  not not_162 (not_162_out, OP1);
  not not_163 (not_163_out, OP0);
  not not_164 (not_164_out, OP5);
  not not_165 (not_165_out, OP4);
  not not_166 (not_166_out, OP2);
  not not_167 (not_167_out, OP1);
  not not_168 (not_168_out, OP5);
  not not_169 (not_169_out, OP4);
  not not_170 (not_170_out, OP2);
  not not_171 (not_171_out, OP0);
  not not_172 (not_172_out, OP5);
  not not_173 (not_173_out, OP4);
  not not_174 (not_174_out, OP1);
  not not_175 (not_175_out, OP4);
  not not_176 (not_176_out, OP3);
  not not_177 (not_177_out, OP2);
  not not_178 (not_178_out, OP5);
  not not_179 (not_179_out, OP4);
  not not_180 (not_180_out, OP3);
  not not_181 (not_181_out, OP2);
  not not_182 (not_182_out, OP1);
  not not_183 (not_183_out, OP0);
  not not_184 (not_184_out, F5);
  not not_185 (not_185_out, F4);
  not not_186 (not_186_out, F3);
  not not_187 (not_187_out, F0);
  not not_188 (not_188_out, OP5);
  not not_189 (not_189_out, OP4);
  not not_190 (not_190_out, OP0);
  not not_191 (not_191_out, OP5);
  not not_192 (not_192_out, OP4);
  not not_193 (not_193_out, OP3);
  not not_194 (not_194_out, OP2);
  not not_195 (not_195_out, OP1);
  not not_196 (not_196_out, OP0);
  not not_197 (not_197_out, F5);
  not not_198 (not_198_out, F4);
  not not_199 (not_199_out, F1);
  not not_200 (not_200_out, F0);
  not not_201 (not_201_out, OP5);
  not not_202 (not_202_out, OP4);
  not not_203 (not_203_out, OP2);
  not not_204 (not_204_out, OP1);
  not not_205 (not_205_out, OP0);
  not not_206 (not_206_out, OP5);
  not not_207 (not_207_out, OP4);
  not not_208 (not_208_out, OP2);
  not not_209 (not_209_out, OP1);
  not not_210 (not_210_out, OP5);
  not not_211 (not_211_out, OP4);
  not not_212 (not_212_out, OP2);
  not not_213 (not_213_out, OP0);
  not not_214 (not_214_out, OP4);
  not not_215 (not_215_out, OP3);
  not not_216 (not_216_out, OP2);
  not not_217 (not_217_out, OP4);
  not not_218 (not_218_out, OP2);
  not not_219 (not_219_out, OP4);
  not not_220 (not_220_out, OP2);
  not not_221 (not_221_out, OP1);
  not not_222 (not_222_out, OP5);
  not not_223 (not_223_out, OP4);
  not not_224 (not_224_out, OP3);
  not not_225 (not_225_out, OP2);
  not not_226 (not_226_out, OP1);
  not not_227 (not_227_out, OP0);
  not not_228 (not_228_out, F5);
  not not_229 (not_229_out, F4);
  not not_230 (not_230_out, F3);
  not not_231 (not_231_out, F2);
  not not_232 (not_232_out, F1);
  not not_233 (not_233_out, F0);
  not not_234 (not_234_out, OP5);
  not not_235 (not_235_out, OP4);
  not not_236 (not_236_out, OP3);
  not not_237 (not_237_out, OP2);
  not not_238 (not_238_out, OP1);
  not not_239 (not_239_out, OP0);
  not not_240 (not_240_out, F5);
  not not_241 (not_241_out, F4);
  not not_242 (not_242_out, F3);
  not not_243 (not_243_out, F2);
  not not_244 (not_244_out, OP5);
  not not_245 (not_245_out, OP4);
  not not_246 (not_246_out, OP3);
  not not_247 (not_247_out, OP2);
  not not_248 (not_248_out, OP1);
  not not_249 (not_249_out, OP0);
  not not_250 (not_250_out, F5);
  not not_251 (not_251_out, F4);
  not not_252 (not_252_out, F3);
  not not_253 (not_253_out, F2);
  not not_254 (not_254_out, F0);
  not not_255 (not_255_out, OP5);
  not not_256 (not_256_out, OP4);
  not not_257 (not_257_out, OP3);
  not not_258 (not_258_out, OP2);
  not not_259 (not_259_out, OP1);
  not not_260 (not_260_out, OP0);
  not not_261 (not_261_out, F4);
  not not_262 (not_262_out, F3);
  not not_263 (not_263_out, F2);
  not not_264 (not_264_out, F1);
  not not_265 (not_265_out, F0);
  not not_266 (not_266_out, OP5);
  not not_267 (not_267_out, OP4);
  not not_268 (not_268_out, OP3);
  not not_269 (not_269_out, OP2);
  not not_270 (not_270_out, OP1);
  not not_271 (not_271_out, OP0);
  not not_272 (not_272_out, F4);
  not not_273 (not_273_out, F3);
  not not_274 (not_274_out, F2);
  not not_275 (not_275_out, F1);
  not not_276 (not_276_out, OP5);
  not not_277 (not_277_out, OP4);
  not not_278 (not_278_out, OP3);
  not not_279 (not_279_out, OP2);
  not not_280 (not_280_out, OP1);
  not not_281 (not_281_out, OP0);
  not not_282 (not_282_out, F4);
  not not_283 (not_283_out, F3);
  not not_284 (not_284_out, F2);
  not not_285 (not_285_out, F0);
  not not_286 (not_286_out, OP5);
  not not_287 (not_287_out, OP4);
  not not_288 (not_288_out, OP3);
  not not_289 (not_289_out, OP2);
  not not_290 (not_290_out, OP1);
  not not_291 (not_291_out, OP0);
  not not_292 (not_292_out, F4);
  not not_293 (not_293_out, F3);
  not not_294 (not_294_out, F1);
  not not_295 (not_295_out, F0);
  not not_296 (not_296_out, OP5);
  not not_297 (not_297_out, OP4);
  not not_298 (not_298_out, OP3);
  not not_299 (not_299_out, OP2);
  not not_300 (not_300_out, OP1);
  not not_301 (not_301_out, OP0);
  not not_302 (not_302_out, F4);
  not not_303 (not_303_out, F3);
  not not_304 (not_304_out, F1);
  not not_305 (not_305_out, OP5);
  not not_306 (not_306_out, OP4);
  not not_307 (not_307_out, OP3);
  not not_308 (not_308_out, OP2);
  not not_309 (not_309_out, OP1);
  not not_310 (not_310_out, OP0);
  not not_311 (not_311_out, F4);
  not not_312 (not_312_out, F3);
  not not_313 (not_313_out, OP5);
  not not_314 (not_314_out, OP4);
  not not_315 (not_315_out, OP3);
  not not_316 (not_316_out, OP2);
  not not_317 (not_317_out, OP1);
  not not_318 (not_318_out, OP0);
  not not_319 (not_319_out, F4);
  not not_320 (not_320_out, F2);
  not not_321 (not_321_out, F0);
  not not_322 (not_322_out, OP5);
  not not_323 (not_323_out, OP4);
  not not_324 (not_324_out, OP3);
  not not_325 (not_325_out, OP2);
  not not_326 (not_326_out, OP1);
  not not_327 (not_327_out, OP0);
  not not_328 (not_328_out, F4);
  not not_329 (not_329_out, F2);
  not not_330 (not_330_out, OP5);
  not not_331 (not_331_out, OP4);
  not not_332 (not_332_out, OP3);
  not not_333 (not_333_out, OP2);
  not not_334 (not_334_out, OP1);
  not not_335 (not_335_out, OP0);
  not not_336 (not_336_out, F5);
  not not_337 (not_337_out, F4);
  not not_338 (not_338_out, F3);
  not not_339 (not_339_out, F0);
  not not_340 (not_340_out, OP5);
  not not_341 (not_341_out, OP4);
  not not_342 (not_342_out, OP3);
  not not_343 (not_343_out, OP1);
  not not_344 (not_344_out, OP0);
  not not_345 (not_345_out, OP5);
  not not_346 (not_346_out, OP4);
  not not_347 (not_347_out, OP3);
  not not_348 (not_348_out, OP1);
  not not_349 (not_349_out, OP5);
  not not_350 (not_350_out, OP4);
  not not_351 (not_351_out, OP3);
  not not_352 (not_352_out, OP2);
  not not_353 (not_353_out, OP1);
  not not_354 (not_354_out, OP0);
  not not_355 (not_355_out, F5);
  not not_356 (not_356_out, F4);
  not not_357 (not_357_out, F2);
  not not_358 (not_358_out, F1);
  not not_359 (not_359_out, F0);
  not not_360 (not_360_out, OP5);
  not not_361 (not_361_out, OP4);
  not not_362 (not_362_out, OP3);
  not not_363 (not_363_out, OP2);
  not not_364 (not_364_out, OP1);
  not not_365 (not_365_out, OP0);
  not not_366 (not_366_out, F5);
  not not_367 (not_367_out, F4);
  not not_368 (not_368_out, F2);
  not not_369 (not_369_out, F1);
  not not_370 (not_370_out, F0);
  not not_371 (not_371_out, OP5);
  not not_372 (not_372_out, OP4);
  not not_373 (not_373_out, OP3);
  not not_374 (not_374_out, OP2);
  not not_375 (not_375_out, OP0);
  not not_376 (not_376_out, OP5);
  not not_377 (not_377_out, OP4);
  not not_378 (not_378_out, OP3);
  not not_379 (not_379_out, OP2);
  not not_380 (not_380_out, OP5);
  not not_381 (not_381_out, OP4);
  not not_382 (not_382_out, OP3);
  not not_383 (not_383_out, OP2);
  and and_1 (MemToReg, OP5, not_1_out, not_2_out, not_3_out, OP1, OP0);
  and and_2 (and_2_out, OP5, not_4_out, OP3, not_5_out, OP1, OP0);
  and and_3 (and_3_out, not_6_out, not_7_out, OP3, OP2, OP1, not_8_out);
  and and_4 (and_4_out, OP5, not_9_out, OP3, not_10_out, not_11_out, OP0);
  and and_5 (and_5_out, not_12_out, not_13_out, OP3, not_14_out, not_15_out, not_16_out);
  and and_6 (and_6_out, not_17_out, not_18_out, OP3, OP2, not_19_out, not_20_out);
  and and_7 (and_7_out, not_21_out, not_22_out, OP3, not_23_out, not_24_out, OP0);
  and and_8 (and_8_out, not_25_out, not_26_out, OP3, not_27_out, OP1, not_28_out);
  and and_9 (and_9_out, not_29_out, not_30_out, OP3, OP2, not_31_out, OP0);
  and and_10 (and_10_out, OP5, not_32_out, not_33_out, not_34_out, OP1, OP0);
  and and_11 (and_11_out, OP5, not_35_out, OP3, not_36_out, OP1, OP0);
  and and_12 (and_12_out, not_37_out, not_38_out, OP3, OP2, OP1, not_39_out);
  and and_13 (and_13_out, OP5, not_40_out, OP3, not_41_out, not_42_out, OP0);
  and and_14 (and_14_out, not_43_out, not_44_out, not_45_out, not_46_out, not_47_out, not_48_out, not_49_out, not_50_out, not_51_out, not_52_out, not_53_out, not_54_out);
  and and_15 (and_15_out, not_55_out, not_56_out, not_57_out, not_58_out, not_59_out, not_60_out, not_61_out, not_62_out, not_63_out, not_64_out, F1, F0);
  and and_16 (and_16_out, not_65_out, not_66_out, not_67_out, not_68_out, not_69_out, not_70_out, not_71_out, not_72_out, not_73_out, not_74_out, F1, not_75_out);
  and and_17 (and_17_out, not_76_out, not_77_out, not_78_out, not_79_out, not_80_out, not_81_out, F5, not_82_out, not_83_out, not_84_out, not_85_out, not_86_out);
  and and_18 (and_18_out, not_87_out, not_88_out, not_89_out, not_90_out, not_91_out, not_92_out, F5, not_93_out, not_94_out, not_95_out, not_96_out, F0);
  and and_19 (and_19_out, not_97_out, not_98_out, not_99_out, not_100_out, not_101_out, not_102_out, F5, not_103_out, not_104_out, not_105_out, F1, not_106_out);
  and and_20 (and_20_out, not_107_out, not_108_out, not_109_out, not_110_out, not_111_out, not_112_out, F5, not_113_out, not_114_out, F2, not_115_out, not_116_out);
  and and_21 (and_21_out, not_117_out, not_118_out, not_119_out, not_120_out, not_121_out, not_122_out, F5, not_123_out, not_124_out, F2, not_125_out, F0);
  and and_22 (and_22_out, not_126_out, not_127_out, not_128_out, not_129_out, not_130_out, not_131_out, F5, not_132_out, not_133_out, F2, F1, F0);
  and and_23 (and_23_out, not_134_out, not_135_out, not_136_out, not_137_out, not_138_out, not_139_out, F5, not_140_out, F3, not_141_out, F1, not_142_out);
  and and_24 (and_24_out, not_143_out, not_144_out, not_145_out, not_146_out, not_147_out, not_148_out, F5, not_149_out, F3, not_150_out, F1, F0);
  and and_25 (and_25_out, not_151_out, not_152_out, not_153_out, not_154_out, OP1, OP0);
  and and_26 (and_26_out, not_155_out, not_156_out, OP3, not_157_out, not_158_out, not_159_out);
  and and_27 (and_27_out, not_160_out, not_161_out, OP3, OP2, not_162_out, not_163_out);
  and and_28 (and_28_out, not_164_out, not_165_out, OP3, not_166_out, not_167_out, OP0);
  and and_29 (and_29_out, not_168_out, not_169_out, OP3, not_170_out, OP1, not_171_out);
  and and_30 (and_30_out, not_172_out, not_173_out, OP3, OP2, not_174_out, OP0);
  and and_31 (and_31_out, OP5, not_175_out, not_176_out, not_177_out, OP1, OP0);
  and and_32 (and_32_out, not_178_out, not_179_out, not_180_out, not_181_out, not_182_out, not_183_out, not_184_out, not_185_out, not_186_out, F2, F1, not_187_out);
  and and_33 (and_33_out, not_188_out, not_189_out, OP3, OP2, OP1, not_190_out);
  and and_34 (SysCALL, not_191_out, not_192_out, not_193_out, not_194_out, not_195_out, not_196_out, not_197_out, not_198_out, F3, F2, not_199_out, not_200_out);
  and and_35 (and_35_out, not_201_out, not_202_out, OP3, not_203_out, not_204_out, not_205_out);
  and and_36 (and_36_out, not_206_out, not_207_out, OP3, not_208_out, not_209_out, OP0);
  and and_37 (and_37_out, not_210_out, not_211_out, OP3, not_212_out, OP1, not_213_out);
  and and_38 (and_38_out, OP5, not_214_out, not_215_out, not_216_out, OP1, OP0);
  and and_39 (and_39_out, OP5, not_217_out, OP3, not_218_out, OP1, OP0);
  and and_40 (and_40_out, OP5, not_219_out, OP3, not_220_out, not_221_out, OP0);
  and and_41 (and_41_out, not_222_out, not_223_out, not_224_out, not_225_out, not_226_out, not_227_out, not_228_out, not_229_out, not_230_out, not_231_out, not_232_out, not_233_out);
  and and_42 (and_42_out, not_234_out, not_235_out, not_236_out, not_237_out, not_238_out, not_239_out, not_240_out, not_241_out, not_242_out, not_243_out, F1, F0);
  and and_43 (and_43_out, not_244_out, not_245_out, not_246_out, not_247_out, not_248_out, not_249_out, not_250_out, not_251_out, not_252_out, not_253_out, F1, not_254_out);
  and and_44 (and_44_out, not_255_out, not_256_out, not_257_out, not_258_out, not_259_out, not_260_out, F5, not_261_out, not_262_out, not_263_out, not_264_out, not_265_out);
  and and_45 (and_45_out, not_266_out, not_267_out, not_268_out, not_269_out, not_270_out, not_271_out, F5, not_272_out, not_273_out, not_274_out, not_275_out, F0);
  and and_46 (and_46_out, not_276_out, not_277_out, not_278_out, not_279_out, not_280_out, not_281_out, F5, not_282_out, not_283_out, not_284_out, F1, not_285_out);
  and and_47 (and_47_out, not_286_out, not_287_out, not_288_out, not_289_out, not_290_out, not_291_out, F5, not_292_out, not_293_out, F2, not_294_out, not_295_out);
  and and_48 (and_48_out, not_296_out, not_297_out, not_298_out, not_299_out, not_300_out, not_301_out, F5, not_302_out, not_303_out, F2, not_304_out, F0);
  and and_49 (and_49_out, not_305_out, not_306_out, not_307_out, not_308_out, not_309_out, not_310_out, F5, not_311_out, not_312_out, F2, F1, F0);
  and and_50 (and_50_out, not_313_out, not_314_out, not_315_out, not_316_out, not_317_out, not_318_out, F5, not_319_out, F3, not_320_out, F1, not_321_out);
  and and_51 (and_51_out, not_322_out, not_323_out, not_324_out, not_325_out, not_326_out, not_327_out, F5, not_328_out, F3, not_329_out, F1, F0);
  and and_52 (and_52_out, not_330_out, not_331_out, not_332_out, not_333_out, not_334_out, not_335_out, not_336_out, not_337_out, not_338_out, F2, F1, not_339_out);
  and and_53 (BEQ, not_340_out, not_341_out, not_342_out, OP2, not_343_out, not_344_out);
  and and_54 (BNE, not_345_out, not_346_out, not_347_out, OP2, not_348_out, OP0);
  and and_55 (JR, not_349_out, not_350_out, not_351_out, not_352_out, not_353_out, not_354_out, not_355_out, not_356_out, F3, not_357_out, not_358_out, not_359_out);
  and and_56 (and_56_out, not_360_out, not_361_out, not_362_out, not_363_out, not_364_out, not_365_out, not_366_out, not_367_out, F3, not_368_out, not_369_out, not_370_out);
  and and_57 (and_57_out, not_371_out, not_372_out, not_373_out, not_374_out, OP1, not_375_out);
  and and_58 (and_58_out, not_376_out, not_377_out, not_378_out, not_379_out, OP1, OP0);
  and and_59 (JAL, not_380_out, not_381_out, not_382_out, not_383_out, OP1, OP0);
  or or_1 (MemWrite, and_2_out, and_3_out, and_4_out);
  or or_2 (ALU_SRC, and_5_out, and_6_out, and_7_out, and_8_out, and_9_out, and_10_out, and_11_out, and_12_out, and_13_out);
  or or_3 (SignedExt, and_35_out, and_36_out, and_37_out, and_38_out, and_39_out, and_40_out);
  or or_4 (JMP, and_56_out, and_57_out, and_58_out);
  or or_5 (RegWrite, and_14_out, and_15_out, and_16_out, and_17_out, and_18_out, and_19_out, and_20_out, and_21_out, and_22_out, and_23_out, and_24_out, and_25_out, and_26_out, and_27_out, and_28_out, and_29_out, and_30_out, and_31_out, and_32_out, and_33_out);
  or or_6 (RegDst, and_41_out, and_42_out, and_43_out, and_44_out, and_45_out, and_46_out, and_47_out, and_48_out, and_49_out, and_50_out, and_51_out, and_52_out);
endmodule

module CCMB_Conrtoller (
  input  OP0,
  input  OP1,
  input  OP2,
  input  OP3,
  input  OP4,
  input  OP5,
  input  F0,
  input  F1,
  input  F2,
  input  F3,
  input  F4,
  input  F5,
  output SRLV,
  output XORI,
  output SH,
  output BLEZ
);

  wire not_1_out, not_2_out, not_3_out, not_4_out, not_5_out, not_6_out, not_7_out, not_8_out, not_9_out,
       not_10_out, not_11_out, not_12_out, not_13_out, not_14_out, not_15_out, not_16_out, not_17_out,
       not_18_out, not_19_out, not_20_out;

  not not_1 (not_1_out, OP5);
  not not_2 (not_2_out, OP4);
  not not_3 (not_3_out, OP3);
  not not_4 (not_4_out, OP2);
  not not_5 (not_5_out, OP1);
  not not_6 (not_6_out, OP0);
  not not_7 (not_7_out, F5);
  not not_8 (not_8_out, F4);
  not not_9 (not_9_out, F3);
  not not_10 (not_10_out, F0);
  not not_11 (not_11_out, OP5);
  not not_12 (not_12_out, OP4);
  not not_13 (not_13_out, OP0);
  not not_14 (not_14_out, OP4);
  not not_15 (not_15_out, OP2);
  not not_16 (not_16_out, OP1);
  not not_17 (not_17_out, OP5);
  not not_18 (not_18_out, OP4);
  not not_19 (not_19_out, OP3);
  not not_20 (not_20_out, OP0);
  and and_1 (SRLV, not_1_out, not_2_out, not_3_out, not_4_out, not_5_out, not_6_out, not_7_out, not_8_out, not_9_out, F2, F1, not_10_out);
  and and_2 (XORI, not_11_out, not_12_out, OP3, OP2, OP1, not_13_out);
  and and_3 (SH, OP5, not_14_out, OP3, not_15_out, not_16_out, OP0);
  and and_4 (BLEZ, not_17_out, not_18_out, not_19_out, OP2, OP1, not_20_out);
endmodule

// ALU
module MIPS_ALU (
  input  [4:0] shamt,
  input  [31:0] X,
  input  [31:0] Y,
  input  [3:0] AluOP,
  output Equal,
  output [31:0] Result,
  output [31:0] Result_2
);

  wire [0:0] comparator_1_lt, comparator_2_lt;
  wire [31:0] adder_1_out, AND_out, divider_1_out, divider_1_rem, multiplier_1_cout, multiplier_1_out,
       NOR_out, OR_out, shifter_1_out, shifter_2_out, shifter_3_out, subtractor_1_out, XOR_out;

  assign AND_out = X & Y;  // AND_Gate AND, 32 bits wide
  assign OR_out = X | Y;  // OR_Gate OR, 32 bits wide
  Shifter #(.width(32)) shifter_1 (.in(Y), .\dist (shamt), .out(shifter_1_out));
  Shifter #(.width(32), .shift("ar")) shifter_2 (.in(Y), .\dist (shamt), .out(shifter_2_out));
  Shifter #(.width(32), .shift("lr")) shifter_3 (.in(Y), .\dist (shamt), .out(shifter_3_out));
  Multiplier #(.width(32)) multiplier_1 (.a(X), .b(Y), .out(multiplier_1_out), .cout(multiplier_1_cout));  // open: cin
  Divider #(.width(32)) divider_1 (.a(X), .b(Y), .out(divider_1_out), .rem(divider_1_rem));  // open: upper
  Adder #(.width(32)) adder_1 (.a(X), .b(Y), .out(adder_1_out));  // open: cin, cout
  Subtractor #(.width(32)) subtractor_1 (.a(X), .b(Y), .out(subtractor_1_out));  // open: bin, bout
  assign XOR_out = X ^ Y;  // XOR_Gate XOR, 32 bits wide
  assign NOR_out = ~(X | Y);  // NOR_Gate NOR, 32 bits wide
  Comparator #(.width(32)) comparator_1 (.a(X), .b(Y), .eq(Equal), .lt(comparator_1_lt[0]));  // open: gt
  Comparator #(.width(32), .mode("unsigned")) comparator_2 (.a(X), .b(Y), .lt(comparator_2_lt[0]));  // open: gt, eq
  Multiplexer #(.select(4), .width(32), .enable("false")) multiplexer_1 (
    .in0(shifter_1_out), .in1(shifter_2_out), .in2(shifter_3_out), .in3(multiplier_1_out),
    .in4(divider_1_out), .in5(adder_1_out), .in6(subtractor_1_out), .in7(AND_out), .in8(OR_out),
    .in9(XOR_out), .in10(NOR_out), .in11({{31{1'b0}}, comparator_1_lt[0]}),
    .in12({{31{1'b0}}, comparator_2_lt[0]}), .in13({32{1'b0}}), .in14({32{1'b0}}), .in15({32{1'b0}}),
    .out(Result), .sel(AluOP));
  Multiplexer #(.select(4), .width(32), .enable("false")) multiplexer_2 (
    .in0({32{1'b0}}), .in1({32{1'b0}}), .in2({32{1'b0}}), .in3(multiplier_1_cout), .in4(divider_1_rem),
    .in5({32{1'b0}}), .in6({32{1'b0}}), .in7({32{1'b0}}), .in8({32{1'b0}}), .in9({32{1'b0}}),
    .in10({32{1'b0}}), .in11({32{1'b0}}), .in12({32{1'b0}}), .in13({32{1'b0}}), .in14({32{1'b0}}),
    .in15({32{1'b0}}), .out(Result_2), .sel(AluOP));

  // Other names for the same wires on the sheet: Result2[31:0] = Result_2; S[3:0] = AluOP

  // Notes on the sheet:
  //   不要改变此引脚区域内容，也不要改变ALU封装形式
  //   输入引脚
  //   输出引脚
endmodule

module MIPS_Regifile (
  input  [31:0] Din,
  input  Clk,
  input  WE,
  input  [4:0] R1_num,
  input  [4:0] W_num,
  input  [4:0] R2_num,
  output [31:0] R1,
  output [31:0] R2
);

  // RegisterFile registerfile_1: pin names not known; wires that end beside it: Din, Clk, WE, W_num, R1_num, R2_num, R1, R2
endmodule

module \理想流水线  (
);

  wire and_1_out, and_2_out, and_3_out, and_4_out, CLK, comparator_1_eq, compare, en, Go, IR1, IR2, IR3, JMP,
       JR, LOCK, mem_wb_1_p1, mips_alu_1_equal, RST, SignedExt, W1, W2, W3, WBJAL, WBRegWrite, WBSyscall;
  wire [4:0] ex_mem_1_wreg_, id_ex_1_shamt_, id_ex_1_wreg_, mem_wb_1_p18, multiplexer_5_out,
       multiplexer_6_out, multiplexer_7_out, multiplexer_8_out;
  wire [12:0] mem_wb_1_p12;
  wire [14:0] ex_mem_1_cont_, id_ex_1_cont_, \硬布线控制器_1_beq ;
  wire [15:0] \LoadUse次数 , \总周期数 , \插入气泡数 , \无条件分支数 , \条件分支成功数 ;
  wire [25:0] id_ex_1_imm26_;
  wire [31:0] adder_1_out, adder_2_out, bit_extender_1_out, bit_extender_2_out, ex_mem_1_aluout_,
       ex_mem_1_rd1_, ex_mem_1_rd2_, EX_PC, EXR1, id_ex_1_imm_, id_ex_1_imme_, id_ex_1_pc_4_, id_ex_1_rd2_,
       ID_PC, if_id_1_instru_, if_id_1_pc_4_, IF_PC, LedData, MEM_PC, mem_wb_1_p15, mem_wb_1_p16,
       mips_alu_1_result, multiplexer_2_out, multiplexer_3_out, multiplexer_4_out, multiplexer_9_out,
       multiplexer_10_out, multiplexer_11_out, multiplexer_12_out, multiplexer_13_out, R1, R2, rom_1_data,
       shifter_1_out, undriven, WB_PC, WBR1, WBR2;

  Button \u_总复位  (.out(RST));
  Button _1 (.out(IR1));
  Button _2 (.out(IR2));
  Button _3 (.out(IR3));
  Button \u_继续运行  (.out(Go));
  LED led_1 (.in(W1));
  LED led_2 (.in(W2));
  LED led_3 (.in(W3));
  Register #(.width(32)) PC (.D(multiplexer_2_out), .en(en), .Q(IF_PC), .clk(CLK), .clr(RST));
  Multiplexer #(.enable("false")) multiplexer_1 (.in0(1'b1), .in1(1'b0), .out(en), .sel(and_1_out));
  and and_1 (and_1_out, LOCK, ~Go);  // AND_Gate
  Counter #(.width(16), .max('hffff)) counter_1 (.count(en), .Q(\总周期数 ), .clk(CLK), .clr(RST));  // open: load, D, carry
  Multiplexer #(.width(32), .enable("false")) multiplexer_2 (
    .in0(multiplexer_4_out), .in1(multiplexer_3_out), .out(multiplexer_2_out), .sel(JMP));
  Multiplexer #(.width(32), .enable("false")) multiplexer_3 (
    .in0({4'b0000, id_ex_1_imm26_, 2'b00}), .in1(EXR1), .out(multiplexer_3_out), .sel(JR));
  Hex_Digit_Display hex_digit_display_1 (.value(LedData[31:28]));  // open: dp
  Counter #(.width(16), .max('hffff)) counter_2 (
    .count(JMP), .Q(\无条件分支数 ), .clk(CLK), .clr(RST));  // open: load, D, carry
  Counter #(.width(16), .max('hffff)) counter_3 (
    .count(compare), .Q(\条件分支成功数 ), .clk(CLK), .clr(RST));  // open: load, D, carry
  Hex_Digit_Display hex_digit_display_2 (.value(LedData[23:20]));  // open: dp
  Hex_Digit_Display hex_digit_display_3 (.value(LedData[27:24]));  // open: dp
  Multiplexer #(.width(32), .enable("false")) multiplexer_4 (
    .in0(adder_1_out), .in1(adder_2_out), .out(multiplexer_4_out), .sel(compare));
  Hex_Digit_Display hex_digit_display_4 (.value(LedData[15:12]));  // open: dp
  Hex_Digit_Display hex_digit_display_5 (.value(LedData[19:16]));  // open: dp
  ROM #(.addrWidth(10), .dataWidth(32)) rom_1 (.addr(IF_PC[11:2]), .data(rom_1_data));  // open: sel
  Adder #(.width(32)) adder_1 (.a(IF_PC), .b(32'h4), .out(adder_1_out));  // open: cin, cout
  Hex_Digit_Display hex_digit_display_6 (.value(LedData[11:8]));  // open: dp
  Hex_Digit_Display hex_digit_display_7 (.value(LedData[7:4]));  // open: dp
  Clock clock_1 (.out(CLK));
  IF_ID if_id_1 (
    .instru(rom_1_data), .PC_4(adder_1_out), .clk(CLK), .instru_(if_id_1_instru_), .PC_4_(if_id_1_pc_4_),
    .PC(IF_PC), .PC_(ID_PC), .en(en), .halt(RST));  // open: rst, 预测跳转, 预测地址, Hit, HitPos, 预测跳转_, 预测地址_, Hit_, HitPos_
  Hex_Digit_Display hex_digit_display_8 (.value(LedData[3:0]));  // open: dp
  \硬布线控制器  \u_硬布线控制器_1  (
    .Func(if_id_1_instru_[5:0]), .OP(if_id_1_instru_[31:26]), .ALU_OP(\硬布线控制器_1_beq [9:6]),
    .MemToReg(\硬布线控制器_1_beq [4]), .MemWrite(\硬布线控制器_1_beq [5]), .ALU_SRC(\硬布线控制器_1_beq [10]),
    .RegWrite(\硬布线控制器_1_beq [14]), .SysCALL(\硬布线控制器_1_beq [13]), .SignedExt(SignedExt),
    .RegDst(\硬布线控制器_1_beq [12]), .JR(\硬布线控制器_1_beq [2]), .JMP(\硬布线控制器_1_beq [3]), .Beq(\硬布线控制器_1_beq [0]),
    .JAL(\硬布线控制器_1_beq [11]), .Bne(\硬布线控制器_1_beq [1]));  // open: SRLV, XORI, SH, BLEZ, ERET, RS, RD, MFC_0, MTC_0
  Multiplexer #(.width(5), .enable("false")) multiplexer_5 (
    .in0(if_id_1_instru_[25:21]), .in1(5'b00010), .out(multiplexer_5_out), .sel(\硬布线控制器_1_beq [13]));
  Multiplexer #(.width(5), .enable("false")) multiplexer_6 (
    .in0(if_id_1_instru_[20:16]), .in1(5'b00100), .out(multiplexer_6_out), .sel(\硬布线控制器_1_beq [13]));
  // Probe on \总周期数 
  // Probe on \无条件分支数 
  // Probe on \条件分支成功数 
  // Probe on \插入气泡数 
  // Probe on \LoadUse次数 
  Multiplexer #(.width(5), .enable("false")) multiplexer_7 (
    .in0(if_id_1_instru_[20:16]), .in1(if_id_1_instru_[15:11]), .out(multiplexer_7_out),
    .sel(\硬布线控制器_1_beq [12]));
  // Probe on IF_PC[11:0]
  Multiplexer #(.width(5), .enable("false")) multiplexer_8 (
    .in0(multiplexer_7_out), .in1({5{1'b1}}), .out(multiplexer_8_out), .sel(\硬布线控制器_1_beq [11]));
  // Probe on ID_PC[11:0]
  Multiplexer #(.width(32), .enable("false")) multiplexer_9 (
    .in0(multiplexer_13_out), .in1(if_id_1_pc_4_), .out(multiplexer_9_out), .sel(WBJAL));
  // Probe on EX_PC[11:0]
  // Probe on MEM_PC[11:0]
  MIPS_Regifile mips_regifile_1 (
    .Din(multiplexer_9_out), .Clk(CLK), .R1(R1), .R2(R2), .WE(WBRegWrite), .W_num(mem_wb_1_p18),
    .R1_num(multiplexer_5_out), .R2_num(multiplexer_6_out));
  assign bit_extender_1_out = {{16{1'b0}}, if_id_1_instru_[15:0]};  // Bit_Extender bit_extender_1
  assign bit_extender_2_out = {{16{if_id_1_instru_[15]}}, if_id_1_instru_[15:0]};  // Bit_Extender bit_extender_2
  // Probe on WB_PC[11:0]
  Multiplexer #(.width(32), .enable("false")) multiplexer_10 (
    .in0(bit_extender_1_out), .in1(bit_extender_2_out), .out(multiplexer_10_out), .sel(SignedExt));
  ID_EX id_ex_1 (
    .RD1(R1), .RD2(R2), .imm(bit_extender_2_out), .PC_4(if_id_1_pc_4_), .clk(CLK), .halt(RST), .RD1_(EXR1),
    .RD2_(id_ex_1_rd2_), .imm_(id_ex_1_imm_), .PC_4_(id_ex_1_pc_4_), .WReg(multiplexer_8_out),
    .WReg_(id_ex_1_wreg_), .immE(multiplexer_10_out), .immE_(id_ex_1_imme_), .cont(\硬布线控制器_1_beq ),
    .cont_({id_ex_1_cont_[14:4], JMP, JR, id_ex_1_cont_[1:0]}), .shamt(if_id_1_instru_[10:6]),
    .shamt_(id_ex_1_shamt_), .PC(ID_PC), .PC_(EX_PC), .en(en), .imm26(if_id_1_instru_[25:0]),
    .imm26_(id_ex_1_imm26_));  // open: IR, IR_, SRLV, SRLV_, SH, SH_, BLEZ, BLEZ_, rst, ERET, ERET_, 预测跳转, 预测跳转_, 预测地址, 预测地址_, Hit, Hit_, HitPos, HitPos_
  Multiplexer #(.width(32), .enable("false")) multiplexer_11 (
    .in0(id_ex_1_rd2_), .in1(id_ex_1_imme_), .out(multiplexer_11_out), .sel(id_ex_1_cont_[10]));
  Shifter #(.width(32)) shifter_1 (.in(id_ex_1_imm_), .\dist (5'b00010), .out(shifter_1_out));
  Comparator #(.width(32)) comparator_1 (.a(WBR1), .b(32'h22), .eq(comparator_1_eq));  // open: gt, lt
  and and_2 (and_2_out, id_ex_1_cont_[0], mips_alu_1_equal);
  and and_3 (and_3_out, ~mips_alu_1_equal, id_ex_1_cont_[1]);  // AND_Gate
  MIPS_ALU mips_alu_1 (
    .X(EXR1), .Y(multiplexer_11_out), .AluOP(id_ex_1_cont_[9:6]), .Equal(mips_alu_1_equal),
    .Result(mips_alu_1_result), .shamt(id_ex_1_shamt_));  // open: Result_2
  Adder #(.width(32)) adder_2 (.a(shifter_1_out), .b(id_ex_1_pc_4_), .out(adder_2_out));  // open: cin, cout
  and and_4 (and_4_out, comparator_1_eq, WBSyscall);
  and and_5 (LOCK, ~comparator_1_eq, WBSyscall);  // AND_Gate
  or or_1 (compare, and_2_out, and_3_out);
  EX_MEM ex_mem_1 (
    .cont({id_ex_1_cont_[14:4], JMP, JR, id_ex_1_cont_[1:0]}), .ALUout(mips_alu_1_result),
    .RD2(id_ex_1_rd2_), .WReg(id_ex_1_wreg_), .clk(CLK), .halt(RST), .cont_(ex_mem_1_cont_),
    .ALUout_(ex_mem_1_aluout_), .RD2_(ex_mem_1_rd2_), .WReg_(ex_mem_1_wreg_), .RD1(EXR1),
    .RD1_(ex_mem_1_rd1_), .PC(EX_PC), .PC_(MEM_PC), .en(en));  // open: IR, IR_, LH, LH_, rst
  Multiplexer #(.width(32)) multiplexer_12 (
    .in0(undriven), .in1(WBR2), .out(multiplexer_12_out), .sel(and_4_out), .en(and_4_out));
  Register #(.width(32)) register_1 (.D(multiplexer_12_out), .Q(LedData), .clk(CLK), .clr(RST));  // open: en
  // MIPS_RAM mips_ram_1: pin names not known; wires that end beside it: ex_mem_1_aluout_[21:2], ex_mem_1_rd2_, ex_mem_1_cont_[5], CLK, RST
  // MEM_WB mem_wb_1: pin names not known; wires that end beside it: mem_wb_1_p1, ex_mem_1_cont_, MEM_PC, ex_mem_1_rd1_, ex_mem_1_aluout_, mem_wb_1_p1, ex_mem_1_rd2_, ex_mem_1_wreg_, en, CLK, RST, {WBRegWrite, WBSyscall, mem_wb_1_p12[12], WBJAL, mem_wb_1_p12[10:0]}, WB_PC, WBR1, mem_wb_1_p15, mem_wb_1_p16, WBR2, mem_wb_1_p18
  Multiplexer #(.width(32), .enable("false")) multiplexer_13 (
    .in0(mem_wb_1_p15), .in1(mem_wb_1_p16), .out(multiplexer_13_out), .sel(mem_wb_1_p12[4]));

  // Notes on the sheet:
  //   中断源
  //   中断等待指示
  //   指令存储器
  //   数码管输出
  //   指令字
  //   contents of rom_1 (hex, n*v repeats v):
  //   2011fff1 112020 20020022 c 22310001 1a20fffb 2002000a c
  //   OP
  //   Func
  //   rs
  //   rt
  //   rd
  //   Beq
  //   JMP
  //   JR
  //   Bne
  //   OP
  //   JAL
  //   Func
  //   Syscall
  //   MemToReg
  //   MemWrite
  //   AluOP
  //   AluSrcB
  //   RegWrite
  //   RegDst
  //   流水调试日志用
endmodule

// 源寄存器使用情况
module \源寄存器使用情况  (
  input  OP0,
  input  OP1,
  input  OP2,
  input  OP3,
  input  OP4,
  input  OP5,
  input  F0,
  input  F1,
  input  F2,
  input  F3,
  input  F4,
  input  F5,
  output R1_Used,
  output R2_Used
);

  wire and_1_out, and_2_out, and_3_out, and_4_out, and_5_out, and_6_out, and_7_out, and_8_out, and_9_out,
       and_10_out, and_11_out, and_12_out, and_13_out, and_14_out, and_15_out, and_16_out, and_17_out,
       and_18_out, and_19_out, and_20_out, and_21_out, and_22_out, and_23_out, and_24_out, and_25_out,
       and_26_out, and_27_out, and_28_out, and_29_out, and_30_out, and_31_out, and_32_out, and_33_out,
       and_34_out, and_35_out, and_36_out, and_37_out, and_38_out, and_39_out, and_40_out, and_41_out,
       and_42_out, and_43_out, not_1_out, not_2_out, not_3_out, not_4_out, not_5_out, not_6_out, not_7_out,
       not_8_out, not_9_out, not_10_out, not_11_out, not_12_out, not_13_out, not_14_out, not_15_out,
       not_16_out, not_17_out, not_18_out, not_19_out, not_20_out, not_21_out, not_22_out, not_23_out,
       not_24_out, not_25_out, not_26_out, not_27_out, not_28_out, not_29_out, not_30_out, not_31_out,
       not_32_out, not_33_out, not_34_out, not_35_out, not_36_out, not_37_out, not_38_out, not_39_out,
       not_40_out, not_41_out, not_42_out, not_43_out, not_44_out, not_45_out, not_46_out, not_47_out,
       not_48_out, not_49_out, not_50_out, not_51_out, not_52_out, not_53_out, not_54_out, not_55_out,
       not_56_out, not_57_out, not_58_out, not_59_out, not_60_out, not_61_out, not_62_out, not_63_out,
       not_64_out, not_65_out, not_66_out, not_67_out, not_68_out, not_69_out, not_70_out, not_71_out,
       not_72_out, not_73_out, not_74_out, not_75_out, not_76_out, not_77_out, not_78_out, not_79_out,
       not_80_out, not_81_out, not_82_out, not_83_out, not_84_out, not_85_out, not_86_out, not_87_out,
       not_88_out, not_89_out, not_90_out, not_91_out, not_92_out, not_93_out, not_94_out, not_95_out,
       not_96_out, not_97_out, not_98_out, not_99_out, not_100_out, not_101_out, not_102_out, not_103_out,
       not_104_out, not_105_out, not_106_out, not_107_out, not_108_out, not_109_out, not_110_out,
       not_111_out, not_112_out, not_113_out, not_114_out, not_115_out, not_116_out, not_117_out,
       not_118_out, not_119_out, not_120_out, not_121_out, not_122_out, not_123_out, not_124_out,
       not_125_out, not_126_out, not_127_out, not_128_out, not_129_out, not_130_out, not_131_out,
       not_132_out, not_133_out, not_134_out, not_135_out, not_136_out, not_137_out, not_138_out,
       not_139_out, not_140_out, not_141_out, not_142_out, not_143_out, not_144_out, not_145_out,
       not_146_out, not_147_out, not_148_out, not_149_out, not_150_out, not_151_out, not_152_out,
       not_153_out, not_154_out, not_155_out, not_156_out, not_157_out, not_158_out, not_159_out,
       not_160_out, not_161_out, not_162_out, not_163_out, not_164_out, not_165_out, not_166_out,
       not_167_out, not_168_out, not_169_out, not_170_out, not_171_out, not_172_out, not_173_out,
       not_174_out, not_175_out, not_176_out, not_177_out, not_178_out, not_179_out, not_180_out,
       not_181_out, not_182_out, not_183_out, not_184_out, not_185_out, not_186_out, not_187_out,
       not_188_out, not_189_out, not_190_out, not_191_out, not_192_out, not_193_out, not_194_out,
       not_195_out, not_196_out, not_197_out, not_198_out, not_199_out, not_200_out, not_201_out,
       not_202_out, not_203_out, not_204_out, not_205_out, not_206_out, not_207_out, not_208_out,
       not_209_out, not_210_out, not_211_out, not_212_out, not_213_out, not_214_out, not_215_out,
       not_216_out, not_217_out, not_218_out, not_219_out, not_220_out, not_221_out, not_222_out,
       not_223_out, not_224_out, not_225_out, not_226_out, not_227_out, not_228_out, not_229_out,
       not_230_out, not_231_out, not_232_out, not_233_out, not_234_out, not_235_out, not_236_out,
       not_237_out, not_238_out, not_239_out, not_240_out, not_241_out, not_242_out, not_243_out,
       not_244_out, not_245_out, not_246_out, not_247_out, not_248_out, not_249_out, not_250_out,
       not_251_out, not_252_out, not_253_out, not_254_out, not_255_out, not_256_out, not_257_out,
       not_258_out, not_259_out, not_260_out, not_261_out, not_262_out, not_263_out, not_264_out,
       not_265_out, not_266_out, not_267_out, not_268_out, not_269_out, not_270_out, not_271_out,
       not_272_out, not_273_out, not_274_out, not_275_out, not_276_out, not_277_out, not_278_out,
       not_279_out, not_280_out, not_281_out, not_282_out, not_283_out, not_284_out, not_285_out,
       not_286_out, not_287_out, not_288_out, not_289_out, not_290_out, not_291_out, not_292_out,
       not_293_out, not_294_out, not_295_out, not_296_out, not_297_out, not_298_out, not_299_out,
       not_300_out, not_301_out, not_302_out, not_303_out, not_304_out, not_305_out, not_306_out,
       not_307_out, not_308_out, not_309_out, not_310_out, not_311_out, not_312_out, not_313_out,
       not_314_out, not_315_out, not_316_out, not_317_out, not_318_out, not_319_out, not_320_out,
       not_321_out, not_322_out, not_323_out, not_324_out, not_325_out;

  not not_1 (not_1_out, OP5);
  not not_2 (not_2_out, OP4);
  not not_3 (not_3_out, OP3);
  not not_4 (not_4_out, OP2);
  not not_5 (not_5_out, OP1);
  not not_6 (not_6_out, OP0);
  not not_7 (not_7_out, F5);
  not not_8 (not_8_out, F4);
  not not_9 (not_9_out, F3);
  not not_10 (not_10_out, F2);
  not not_11 (not_11_out, F1);
  not not_12 (not_12_out, F0);
  not not_13 (not_13_out, OP5);
  not not_14 (not_14_out, OP4);
  not not_15 (not_15_out, OP3);
  not not_16 (not_16_out, OP2);
  not not_17 (not_17_out, OP1);
  not not_18 (not_18_out, OP0);
  not not_19 (not_19_out, F5);
  not not_20 (not_20_out, F4);
  not not_21 (not_21_out, F3);
  not not_22 (not_22_out, F2);
  not not_23 (not_23_out, OP5);
  not not_24 (not_24_out, OP4);
  not not_25 (not_25_out, OP3);
  not not_26 (not_26_out, OP2);
  not not_27 (not_27_out, OP1);
  not not_28 (not_28_out, OP0);
  not not_29 (not_29_out, F5);
  not not_30 (not_30_out, F4);
  not not_31 (not_31_out, F3);
  not not_32 (not_32_out, F2);
  not not_33 (not_33_out, F0);
  not not_34 (not_34_out, OP5);
  not not_35 (not_35_out, OP4);
  not not_36 (not_36_out, OP3);
  not not_37 (not_37_out, OP2);
  not not_38 (not_38_out, OP1);
  not not_39 (not_39_out, OP0);
  not not_40 (not_40_out, F4);
  not not_41 (not_41_out, F3);
  not not_42 (not_42_out, F2);
  not not_43 (not_43_out, F1);
  not not_44 (not_44_out, F0);
  not not_45 (not_45_out, OP5);
  not not_46 (not_46_out, OP4);
  not not_47 (not_47_out, OP3);
  not not_48 (not_48_out, OP2);
  not not_49 (not_49_out, OP1);
  not not_50 (not_50_out, OP0);
  not not_51 (not_51_out, F4);
  not not_52 (not_52_out, F3);
  not not_53 (not_53_out, F2);
  not not_54 (not_54_out, F1);
  not not_55 (not_55_out, OP5);
  not not_56 (not_56_out, OP4);
  not not_57 (not_57_out, OP3);
  not not_58 (not_58_out, OP2);
  not not_59 (not_59_out, OP1);
  not not_60 (not_60_out, OP0);
  not not_61 (not_61_out, F4);
  not not_62 (not_62_out, F3);
  not not_63 (not_63_out, F2);
  not not_64 (not_64_out, F0);
  not not_65 (not_65_out, OP5);
  not not_66 (not_66_out, OP4);
  not not_67 (not_67_out, OP3);
  not not_68 (not_68_out, OP2);
  not not_69 (not_69_out, OP1);
  not not_70 (not_70_out, OP0);
  not not_71 (not_71_out, F4);
  not not_72 (not_72_out, F3);
  not not_73 (not_73_out, F1);
  not not_74 (not_74_out, F0);
  not not_75 (not_75_out, OP5);
  not not_76 (not_76_out, OP4);
  not not_77 (not_77_out, OP3);
  not not_78 (not_78_out, OP2);
  not not_79 (not_79_out, OP1);
  not not_80 (not_80_out, OP0);
  not not_81 (not_81_out, F4);
  not not_82 (not_82_out, F3);
  not not_83 (not_83_out, F1);
  not not_84 (not_84_out, OP5);
  not not_85 (not_85_out, OP4);
  not not_86 (not_86_out, OP3);
  not not_87 (not_87_out, OP2);
  not not_88 (not_88_out, OP1);
  not not_89 (not_89_out, OP0);
  not not_90 (not_90_out, F4);
  not not_91 (not_91_out, F3);
  not not_92 (not_92_out, OP5);
  not not_93 (not_93_out, OP4);
  not not_94 (not_94_out, OP3);
  not not_95 (not_95_out, OP2);
  not not_96 (not_96_out, OP1);
  not not_97 (not_97_out, OP0);
  not not_98 (not_98_out, F4);
  not not_99 (not_99_out, F2);
  not not_100 (not_100_out, F0);
  not not_101 (not_101_out, OP5);
  not not_102 (not_102_out, OP4);
  not not_103 (not_103_out, OP3);
  not not_104 (not_104_out, OP2);
  not not_105 (not_105_out, OP1);
  not not_106 (not_106_out, OP0);
  not not_107 (not_107_out, F4);
  not not_108 (not_108_out, F2);
  not not_109 (not_109_out, OP5);
  not not_110 (not_110_out, OP4);
  not not_111 (not_111_out, OP3);
  not not_112 (not_112_out, OP2);
  not not_113 (not_113_out, OP1);
  not not_114 (not_114_out, OP0);
  not not_115 (not_115_out, F5);
  not not_116 (not_116_out, F4);
  not not_117 (not_117_out, F2);
  not not_118 (not_118_out, F1);
  not not_119 (not_119_out, F0);
  not not_120 (not_120_out, OP5);
  not not_121 (not_121_out, OP4);
  not not_122 (not_122_out, OP3);
  not not_123 (not_123_out, OP2);
  not not_124 (not_124_out, OP1);
  not not_125 (not_125_out, OP0);
  not not_126 (not_126_out, F5);
  not not_127 (not_127_out, F4);
  not not_128 (not_128_out, F1);
  not not_129 (not_129_out, F0);
  not not_130 (not_130_out, OP5);
  not not_131 (not_131_out, OP4);
  not not_132 (not_132_out, OP3);
  not not_133 (not_133_out, OP1);
  not not_134 (not_134_out, OP0);
  not not_135 (not_135_out, OP5);
  not not_136 (not_136_out, OP4);
  not not_137 (not_137_out, OP3);
  not not_138 (not_138_out, OP1);
  not not_139 (not_139_out, OP5);
  not not_140 (not_140_out, OP4);
  not not_141 (not_141_out, OP2);
  not not_142 (not_142_out, OP1);
  not not_143 (not_143_out, OP0);
  not not_144 (not_144_out, OP5);
  not not_145 (not_145_out, OP4);
  not not_146 (not_146_out, OP1);
  not not_147 (not_147_out, OP0);
  not not_148 (not_148_out, OP5);
  not not_149 (not_149_out, OP4);
  not not_150 (not_150_out, OP2);
  not not_151 (not_151_out, OP1);
  not not_152 (not_152_out, OP5);
  not not_153 (not_153_out, OP4);
  not not_154 (not_154_out, OP2);
  not not_155 (not_155_out, OP0);
  not not_156 (not_156_out, OP5);
  not not_157 (not_157_out, OP4);
  not not_158 (not_158_out, OP1);
  not not_159 (not_159_out, OP4);
  not not_160 (not_160_out, OP3);
  not not_161 (not_161_out, OP2);
  not not_162 (not_162_out, OP4);
  not not_163 (not_163_out, OP2);
  not not_164 (not_164_out, OP5);
  not not_165 (not_165_out, OP4);
  not not_166 (not_166_out, OP3);
  not not_167 (not_167_out, OP2);
  not not_168 (not_168_out, OP1);
  not not_169 (not_169_out, OP0);
  not not_170 (not_170_out, F5);
  not not_171 (not_171_out, F4);
  not not_172 (not_172_out, F3);
  not not_173 (not_173_out, F0);
  not not_174 (not_174_out, OP5);
  not not_175 (not_175_out, OP4);
  not not_176 (not_176_out, OP0);
  not not_177 (not_177_out, OP5);
  not not_178 (not_178_out, OP4);
  not not_179 (not_179_out, OP3);
  not not_180 (not_180_out, OP0);
  not not_181 (not_181_out, OP5);
  not not_182 (not_182_out, OP4);
  not not_183 (not_183_out, OP3);
  not not_184 (not_184_out, OP2);
  not not_185 (not_185_out, OP1);
  not not_186 (not_186_out, OP0);
  not not_187 (not_187_out, F5);
  not not_188 (not_188_out, F4);
  not not_189 (not_189_out, F3);
  not not_190 (not_190_out, F2);
  not not_191 (not_191_out, F1);
  not not_192 (not_192_out, F0);
  not not_193 (not_193_out, OP5);
  not not_194 (not_194_out, OP4);
  not not_195 (not_195_out, OP3);
  not not_196 (not_196_out, OP2);
  not not_197 (not_197_out, OP1);
  not not_198 (not_198_out, OP0);
  not not_199 (not_199_out, F5);
  not not_200 (not_200_out, F4);
  not not_201 (not_201_out, F3);
  not not_202 (not_202_out, F2);
  not not_203 (not_203_out, OP5);
  not not_204 (not_204_out, OP4);
  not not_205 (not_205_out, OP3);
  not not_206 (not_206_out, OP2);
  not not_207 (not_207_out, OP1);
  not not_208 (not_208_out, OP0);
  not not_209 (not_209_out, F5);
  not not_210 (not_210_out, F4);
  not not_211 (not_211_out, F3);
  not not_212 (not_212_out, F2);
  not not_213 (not_213_out, F0);
  not not_214 (not_214_out, OP5);
  not not_215 (not_215_out, OP4);
  not not_216 (not_216_out, OP3);
  not not_217 (not_217_out, OP2);
  not not_218 (not_218_out, OP1);
  not not_219 (not_219_out, OP0);
  not not_220 (not_220_out, F4);
  not not_221 (not_221_out, F3);
  not not_222 (not_222_out, F2);
  not not_223 (not_223_out, F1);
  not not_224 (not_224_out, F0);
  not not_225 (not_225_out, OP5);
  not not_226 (not_226_out, OP4);
  not not_227 (not_227_out, OP3);
  not not_228 (not_228_out, OP2);
  not not_229 (not_229_out, OP1);
  not not_230 (not_230_out, OP0);
  not not_231 (not_231_out, F4);
  not not_232 (not_232_out, F3);
  not not_233 (not_233_out, F2);
  not not_234 (not_234_out, F1);
  not not_235 (not_235_out, OP5);
  not not_236 (not_236_out, OP4);
  not not_237 (not_237_out, OP3);
  not not_238 (not_238_out, OP2);
  not not_239 (not_239_out, OP1);
  not not_240 (not_240_out, OP0);
  not not_241 (not_241_out, F4);
  not not_242 (not_242_out, F3);
  not not_243 (not_243_out, F2);
  not not_244 (not_244_out, F0);
  not not_245 (not_245_out, OP5);
  not not_246 (not_246_out, OP4);
  not not_247 (not_247_out, OP3);
  not not_248 (not_248_out, OP2);
  not not_249 (not_249_out, OP1);
  not not_250 (not_250_out, OP0);
  not not_251 (not_251_out, F4);
  not not_252 (not_252_out, F3);
  not not_253 (not_253_out, F1);
  not not_254 (not_254_out, F0);
  not not_255 (not_255_out, OP5);
  not not_256 (not_256_out, OP4);
  not not_257 (not_257_out, OP3);
  not not_258 (not_258_out, OP2);
  not not_259 (not_259_out, OP1);
  not not_260 (not_260_out, OP0);
  not not_261 (not_261_out, F4);
  not not_262 (not_262_out, F3);
  not not_263 (not_263_out, F1);
  not not_264 (not_264_out, OP5);
  not not_265 (not_265_out, OP4);
  not not_266 (not_266_out, OP3);
  not not_267 (not_267_out, OP2);
  not not_268 (not_268_out, OP1);
  not not_269 (not_269_out, OP0);
  not not_270 (not_270_out, F4);
  not not_271 (not_271_out, F3);
  not not_272 (not_272_out, OP5);
  not not_273 (not_273_out, OP4);
  not not_274 (not_274_out, OP3);
  not not_275 (not_275_out, OP2);
  not not_276 (not_276_out, OP1);
  not not_277 (not_277_out, OP0);
  not not_278 (not_278_out, F4);
  not not_279 (not_279_out, F2);
  not not_280 (not_280_out, F0);
  not not_281 (not_281_out, OP5);
  not not_282 (not_282_out, OP4);
  not not_283 (not_283_out, OP3);
  not not_284 (not_284_out, OP2);
  not not_285 (not_285_out, OP1);
  not not_286 (not_286_out, OP0);
  not not_287 (not_287_out, F4);
  not not_288 (not_288_out, F2);
  not not_289 (not_289_out, OP5);
  not not_290 (not_290_out, OP4);
  not not_291 (not_291_out, OP3);
  not not_292 (not_292_out, OP2);
  not not_293 (not_293_out, OP1);
  not not_294 (not_294_out, OP0);
  not not_295 (not_295_out, F5);
  not not_296 (not_296_out, F4);
  not not_297 (not_297_out, F1);
  not not_298 (not_298_out, F0);
  not not_299 (not_299_out, OP5);
  not not_300 (not_300_out, OP4);
  not not_301 (not_301_out, OP3);
  not not_302 (not_302_out, OP1);
  not not_303 (not_303_out, OP0);
  not not_304 (not_304_out, OP5);
  not not_305 (not_305_out, OP4);
  not not_306 (not_306_out, OP3);
  not not_307 (not_307_out, OP1);
  not not_308 (not_308_out, OP4);
  not not_309 (not_309_out, OP2);
  not not_310 (not_310_out, OP5);
  not not_311 (not_311_out, OP4);
  not not_312 (not_312_out, OP3);
  not not_313 (not_313_out, OP2);
  not not_314 (not_314_out, OP1);
  not not_315 (not_315_out, OP0);
  not not_316 (not_316_out, F5);
  not not_317 (not_317_out, F4);
  not not_318 (not_318_out, F3);
  not not_319 (not_319_out, F0);
  not not_320 (not_320_out, OP5);
  not not_321 (not_321_out, OP4);
  not not_322 (not_322_out, OP0);
  not not_323 (not_323_out, OP4);
  not not_324 (not_324_out, OP2);
  not not_325 (not_325_out, OP1);
  and and_1 (and_1_out, not_1_out, not_2_out, not_3_out, not_4_out, not_5_out, not_6_out, not_7_out, not_8_out, not_9_out, not_10_out, not_11_out, not_12_out);
  and and_2 (and_2_out, not_13_out, not_14_out, not_15_out, not_16_out, not_17_out, not_18_out, not_19_out, not_20_out, not_21_out, not_22_out, F1, F0);
  and and_3 (and_3_out, not_23_out, not_24_out, not_25_out, not_26_out, not_27_out, not_28_out, not_29_out, not_30_out, not_31_out, not_32_out, F1, not_33_out);
  and and_4 (and_4_out, not_34_out, not_35_out, not_36_out, not_37_out, not_38_out, not_39_out, F5, not_40_out, not_41_out, not_42_out, not_43_out, not_44_out);
  and and_5 (and_5_out, not_45_out, not_46_out, not_47_out, not_48_out, not_49_out, not_50_out, F5, not_51_out, not_52_out, not_53_out, not_54_out, F0);
  and and_6 (and_6_out, not_55_out, not_56_out, not_57_out, not_58_out, not_59_out, not_60_out, F5, not_61_out, not_62_out, not_63_out, F1, not_64_out);
  and and_7 (and_7_out, not_65_out, not_66_out, not_67_out, not_68_out, not_69_out, not_70_out, F5, not_71_out, not_72_out, F2, not_73_out, not_74_out);
  and and_8 (and_8_out, not_75_out, not_76_out, not_77_out, not_78_out, not_79_out, not_80_out, F5, not_81_out, not_82_out, F2, not_83_out, F0);
  and and_9 (and_9_out, not_84_out, not_85_out, not_86_out, not_87_out, not_88_out, not_89_out, F5, not_90_out, not_91_out, F2, F1, F0);
  and and_10 (and_10_out, not_92_out, not_93_out, not_94_out, not_95_out, not_96_out, not_97_out, F5, not_98_out, F3, not_99_out, F1, not_100_out);
  and and_11 (and_11_out, not_101_out, not_102_out, not_103_out, not_104_out, not_105_out, not_106_out, F5, not_107_out, F3, not_108_out, F1, F0);
  and and_12 (and_12_out, not_109_out, not_110_out, not_111_out, not_112_out, not_113_out, not_114_out, not_115_out, not_116_out, F3, not_117_out, not_118_out, not_119_out);
  and and_13 (and_13_out, not_120_out, not_121_out, not_122_out, not_123_out, not_124_out, not_125_out, not_126_out, not_127_out, F3, F2, not_128_out, not_129_out);
  and and_14 (and_14_out, not_130_out, not_131_out, not_132_out, OP2, not_133_out, not_134_out);
  and and_15 (and_15_out, not_135_out, not_136_out, not_137_out, OP2, not_138_out, OP0);
  and and_16 (and_16_out, not_139_out, not_140_out, OP3, not_141_out, not_142_out, not_143_out);
  and and_17 (and_17_out, not_144_out, not_145_out, OP3, OP2, not_146_out, not_147_out);
  and and_18 (and_18_out, not_148_out, not_149_out, OP3, not_150_out, not_151_out, OP0);
  and and_19 (and_19_out, not_152_out, not_153_out, OP3, not_154_out, OP1, not_155_out);
  and and_20 (and_20_out, not_156_out, not_157_out, OP3, OP2, not_158_out, OP0);
  and and_21 (and_21_out, OP5, not_159_out, not_160_out, not_161_out, OP1, OP0);
  and and_22 (and_22_out, OP5, not_162_out, OP3, not_163_out, OP1, OP0);
  and and_23 (and_23_out, not_164_out, not_165_out, not_166_out, not_167_out, not_168_out, not_169_out, not_170_out, not_171_out, not_172_out, F2, F1, not_173_out);
  and and_24 (and_24_out, not_174_out, not_175_out, OP3, OP2, OP1, not_176_out);
  and and_25 (and_25_out, not_177_out, not_178_out, not_179_out, OP2, OP1, not_180_out);
  and and_26 (and_26_out, not_181_out, not_182_out, not_183_out, not_184_out, not_185_out, not_186_out, not_187_out, not_188_out, not_189_out, not_190_out, not_191_out, not_192_out);
  and and_27 (and_27_out, not_193_out, not_194_out, not_195_out, not_196_out, not_197_out, not_198_out, not_199_out, not_200_out, not_201_out, not_202_out, F1, F0);
  and and_28 (and_28_out, not_203_out, not_204_out, not_205_out, not_206_out, not_207_out, not_208_out, not_209_out, not_210_out, not_211_out, not_212_out, F1, not_213_out);
  and and_29 (and_29_out, not_214_out, not_215_out, not_216_out, not_217_out, not_218_out, not_219_out, F5, not_220_out, not_221_out, not_222_out, not_223_out, not_224_out);
  and and_30 (and_30_out, not_225_out, not_226_out, not_227_out, not_228_out, not_229_out, not_230_out, F5, not_231_out, not_232_out, not_233_out, not_234_out, F0);
  and and_31 (and_31_out, not_235_out, not_236_out, not_237_out, not_238_out, not_239_out, not_240_out, F5, not_241_out, not_242_out, not_243_out, F1, not_244_out);
  and and_32 (and_32_out, not_245_out, not_246_out, not_247_out, not_248_out, not_249_out, not_250_out, F5, not_251_out, not_252_out, F2, not_253_out, not_254_out);
  and and_33 (and_33_out, not_255_out, not_256_out, not_257_out, not_258_out, not_259_out, not_260_out, F5, not_261_out, not_262_out, F2, not_263_out, F0);
  and and_34 (and_34_out, not_264_out, not_265_out, not_266_out, not_267_out, not_268_out, not_269_out, F5, not_270_out, not_271_out, F2, F1, F0);
  and and_35 (and_35_out, not_272_out, not_273_out, not_274_out, not_275_out, not_276_out, not_277_out, F5, not_278_out, F3, not_279_out, F1, not_280_out);
  and and_36 (and_36_out, not_281_out, not_282_out, not_283_out, not_284_out, not_285_out, not_286_out, F5, not_287_out, F3, not_288_out, F1, F0);
  and and_37 (and_37_out, not_289_out, not_290_out, not_291_out, not_292_out, not_293_out, not_294_out, not_295_out, not_296_out, F3, F2, not_297_out, not_298_out);
  and and_38 (and_38_out, not_299_out, not_300_out, not_301_out, OP2, not_302_out, not_303_out);
  and and_39 (and_39_out, not_304_out, not_305_out, not_306_out, OP2, not_307_out, OP0);
  and and_40 (and_40_out, OP5, not_308_out, OP3, not_309_out, OP1, OP0);
  and and_41 (and_41_out, not_310_out, not_311_out, not_312_out, not_313_out, not_314_out, not_315_out, not_316_out, not_317_out, not_318_out, F2, F1, not_319_out);
  and and_42 (and_42_out, not_320_out, not_321_out, OP3, OP2, OP1, not_322_out);
  and and_43 (and_43_out, OP5, not_323_out, OP3, not_324_out, not_325_out, OP0);
  or or_1 (R1_Used, and_1_out, and_2_out, and_3_out, and_4_out, and_5_out, and_6_out, and_7_out, and_8_out, and_9_out, and_10_out, and_11_out, and_12_out, and_13_out, and_14_out, and_15_out, and_16_out, and_17_out, and_18_out, and_19_out, and_20_out, and_21_out, and_22_out, and_23_out, and_24_out, and_25_out);
  or or_2 (R2_Used, and_26_out, and_27_out, and_28_out, and_29_out, and_30_out, and_31_out, and_32_out, and_33_out, and_34_out, and_35_out, and_36_out, and_37_out, and_38_out, and_39_out, and_40_out, and_41_out, and_42_out, and_43_out);
endmodule

module \数据相关检测  (
  input  [5:0] ID_OP,
  input  [4:0] EX_WriteReg_num,
  input  EX_RegWrite,
  input  [4:0] MEM_WriteReg_num,
  input  MEM_RegWrite,
  input  [5:0] ID_FUNC,
  input  [4:0] ID_R1_num,
  input  [4:0] ID_R2_num,
  input  [5:0] EX_OP,
  input  [4:0] WB_WriteReg_num,
  input  WB_RegWrite,
  input  [5:0] EX_FUNC,
  input  [4:0] EX_R1_num,
  input  [4:0] EX_R2_num,
  output \EX相关 ,
  output \数据相关 ,
  output \MEM相关 ,
  output \Load_Use相关 ,
  output [1:0] Forward1,
  output [1:0] Forward2
);

  wire and_1_out, and_2_out, and_3_out, and_4_out, and_10_out, and_11_out, and_12_out, and_13_out,
       comparator_1_eq, comparator_2_eq, comparator_3_eq, comparator_4_eq, comparator_5_eq, comparator_6_eq,
       comparator_7_eq, comparator_8_eq, comparator_9_eq, comparator_10_eq, comparator_11_eq,
       comparator_12_eq, comparator_13_eq, EX_R1_Select, EX_R1_Used, EX_R2_Select, EX_R2_Used, ID_R1_Used,
       ID_R2_Used, multiplexer_1_out, multiplexer_2_out, multiplexer_3_out, multiplexer_4_out, not_1_out,
       not_2_out, not_3_out, not_4_out, or_1_out, or_2_out;
  wire [1:0] multiplexer_5_out, multiplexer_6_out;

  \源寄存器使用情况  \u_源寄存器使用情况_1  (
    .OP0(ID_OP[0]), .OP1(ID_OP[1]), .OP2(ID_OP[2]), .OP3(ID_OP[3]), .OP4(ID_OP[4]), .OP5(ID_OP[5]),
    .F0(ID_FUNC[0]), .F1(ID_FUNC[1]), .F2(ID_FUNC[2]), .F3(ID_FUNC[3]), .F4(ID_FUNC[4]), .F5(ID_FUNC[5]),
    .R1_Used(ID_R1_Used), .R2_Used(ID_R2_Used));
  Comparator #(.width(5)) comparator_1 (.a(ID_R1_num), .b(EX_WriteReg_num), .eq(comparator_1_eq));  // open: gt, lt
  Comparator #(.width(5)) comparator_2 (.a(ID_R2_num), .b(EX_WriteReg_num), .eq(comparator_2_eq));  // open: gt, lt
  Comparator #(.width(5)) comparator_3 (.a(ID_R1_num), .b(MEM_WriteReg_num), .eq(comparator_3_eq));  // open: gt, lt
  Comparator #(.width(5)) comparator_4 (.a(ID_R2_num), .b(MEM_WriteReg_num), .eq(comparator_4_eq));  // open: gt, lt
  and and_1 (and_1_out, ID_R1_Used, comparator_1_eq);
  and and_2 (and_2_out, ID_R2_Used, comparator_2_eq);
  and and_3 (and_3_out, ID_R1_Used, comparator_3_eq);
  and and_4 (and_4_out, ID_R2_Used, comparator_4_eq);
  or or_1 (or_1_out, and_1_out, and_2_out);
  Comparator #(.width(5)) comparator_5 (.a({5{1'b0}}), .b(EX_WriteReg_num), .eq(comparator_5_eq));  // open: gt, lt
  or or_2 (or_2_out, and_3_out, and_4_out);
  Comparator #(.width(5)) comparator_6 (.a({5{1'b0}}), .b(MEM_WriteReg_num), .eq(comparator_6_eq));  // open: gt, lt
  not not_1 (not_1_out, comparator_5_eq);
  not not_2 (not_2_out, comparator_6_eq);
  Comparator #(.width(6)) comparator_7 (.a(EX_OP), .b(6'b100011), .eq(comparator_7_eq));  // open: gt, lt
  and and_5 (\EX相关 , or_1_out, EX_RegWrite, not_1_out);
  and and_6 (\MEM相关 , or_2_out, MEM_RegWrite, not_2_out);
  or or_3 (\数据相关 , \EX相关 , \MEM相关 );
  and and_7 (\Load_Use相关 , comparator_7_eq, \EX相关 );
  Comparator #(.width(5)) comparator_8 (.a(EX_R1_num), .b({5{1'b0}}), .eq(comparator_8_eq));  // open: gt, lt
  Comparator #(.width(5)) comparator_9 (.a(EX_R2_num), .b({5{1'b0}}), .eq(comparator_9_eq));  // open: gt, lt
  Comparator #(.width(5)) comparator_10 (.a(EX_R1_num), .b(MEM_WriteReg_num), .eq(comparator_10_eq));  // open: gt, lt
  Comparator #(.width(5)) comparator_11 (.a(EX_R1_num), .b(WB_WriteReg_num), .eq(comparator_11_eq));  // open: gt, lt
  Comparator #(.width(5)) comparator_12 (.a(EX_R2_num), .b(MEM_WriteReg_num), .eq(comparator_12_eq));  // open: gt, lt
  Comparator #(.width(5)) comparator_13 (.a(EX_R2_num), .b(WB_WriteReg_num), .eq(comparator_13_eq));  // open: gt, lt
  not not_3 (not_3_out, comparator_8_eq);
  not not_4 (not_4_out, comparator_9_eq);
  Multiplexer #(.enable("false")) multiplexer_1 (
    .in0(1'b0), .in1(comparator_10_eq), .out(multiplexer_1_out), .sel(EX_R1_Select));
  Multiplexer #(.enable("false")) multiplexer_2 (
    .in0(1'b0), .in1(comparator_11_eq), .out(multiplexer_2_out), .sel(EX_R1_Select));
  Multiplexer #(.enable("false")) multiplexer_3 (
    .in0(1'b0), .in1(comparator_12_eq), .out(multiplexer_3_out), .sel(EX_R2_Select));
  Multiplexer #(.enable("false")) multiplexer_4 (
    .in0(1'b0), .in1(comparator_13_eq), .out(multiplexer_4_out), .sel(EX_R2_Select));
  \源寄存器使用情况  \u_源寄存器使用情况_2  (
    .OP0(EX_OP[0]), .OP1(EX_OP[1]), .OP2(EX_OP[2]), .OP3(EX_OP[3]), .OP4(EX_OP[4]), .OP5(EX_OP[5]),
    .F0(EX_FUNC[0]), .F1(EX_FUNC[1]), .F2(EX_FUNC[2]), .F3(EX_FUNC[3]), .F4(EX_FUNC[4]), .F5(EX_FUNC[5]),
    .R1_Used(EX_R1_Used), .R2_Used(EX_R2_Used));
  and and_8 (EX_R1_Select, not_3_out, EX_R1_Used);
  and and_9 (EX_R2_Select, not_4_out, EX_R2_Used);
  and and_10 (and_10_out, multiplexer_2_out, WB_RegWrite);
  and and_11 (and_11_out, multiplexer_4_out, WB_RegWrite);
  and and_12 (and_12_out, MEM_RegWrite, multiplexer_1_out);
  Multiplexer #(.width(2), .enable("false")) multiplexer_5 (
    .in0(2'b00), .in1(2'b10), .out(multiplexer_5_out), .sel(and_10_out));
  and and_13 (and_13_out, MEM_RegWrite, multiplexer_3_out);
  Multiplexer #(.width(2), .enable("false")) multiplexer_6 (
    .in0(2'b00), .in1(2'b10), .out(multiplexer_6_out), .sel(and_11_out));
  Multiplexer #(.width(2), .enable("false")) multiplexer_7 (
    .in0(multiplexer_5_out), .in1(2'b01), .out(Forward1), .sel(and_12_out));
  Multiplexer #(.width(2), .enable("false")) multiplexer_8 (
    .in0(multiplexer_6_out), .in1(2'b01), .out(Forward2), .sel(and_13_out));

  // Notes on the sheet:
  //   过滤掉0号寄存器
endmodule
module IF_ID (
  input  [31:0] instru,
  input  [31:0] PC_4,
  input  [31:0] PC,
  input  clk,
  input  rst,
  input  en,
  input  halt,
  input  \预测跳转 ,
  input  [31:0] \预测地址 ,
  input  Hit,
  input  [2:0] HitPos,
  output [31:0] instru_,
  output [31:0] PC_4_,
  output [31:0] PC_,
  output \预测跳转_ ,
  output [31:0] \预测地址_ ,
  output Hit_,
  output [2:0] HitPos_
);

  wire multiplexer_4_out, multiplexer_6_out;
  wire [2:0] multiplexer_7_out;
  wire [31:0] multiplexer_1_out, multiplexer_2_out, multiplexer_3_out, multiplexer_5_out;

  Multiplexer #(.width(32), .enable("false")) multiplexer_1 (
    .in0(instru), .in1({32{1'b0}}), .out(multiplexer_1_out), .sel(halt));
  Multiplexer #(.width(32), .enable("false")) multiplexer_2 (
    .in0(PC_4), .in1({32{1'b0}}), .out(multiplexer_2_out), .sel(halt));
  Multiplexer #(.width(32), .enable("false")) multiplexer_3 (
    .in0(PC), .in1({32{1'b0}}), .out(multiplexer_3_out), .sel(halt));
  Multiplexer #(.enable("false")) multiplexer_4 (.in0(\预测跳转 ), .in1(1'b0), .out(multiplexer_4_out), .sel(halt));
  Multiplexer #(.width(32), .enable("false")) multiplexer_5 (
    .in0(\预测地址 ), .in1({32{1'b0}}), .out(multiplexer_5_out), .sel(halt));
  Multiplexer #(.enable("false")) multiplexer_6 (.in0(Hit), .in1(1'b0), .out(multiplexer_6_out), .sel(halt));
  Multiplexer #(.width(3), .enable("false")) multiplexer_7 (
    .in0(HitPos), .in1(3'b000), .out(multiplexer_7_out), .sel(halt));
  Register #(.width(32)) IR (.D(multiplexer_1_out), .en(en), .Q(instru_), .clk(clk), .clr(rst));
  Register #(.width(32)) IR_2 (.D(multiplexer_2_out), .en(en), .Q(PC_4_), .clk(clk), .clr(rst));
  Register #(.width(32)) IR_3 (.D(multiplexer_3_out), .en(en), .Q(PC_), .clk(clk), .clr(rst));
  Register #(.width(1)) IR_4 (.D(multiplexer_4_out), .en(en), .Q(\预测跳转_ ), .clk(clk), .clr(rst));
  Register #(.width(32)) IR_5 (.D(multiplexer_5_out), .en(en), .Q(\预测地址_ ), .clk(clk), .clr(rst));
  Register #(.width(1)) IR_6 (.D(multiplexer_6_out), .en(en), .Q(Hit_), .clk(clk), .clr(rst));
  Register #(.width(3)) IR_7 (.D(multiplexer_7_out), .en(en), .Q(HitPos_), .clk(clk), .clr(rst));
endmodule

module ID_EX (
  input  [14:0] cont,
  input  [31:0] RD1,
  input  [31:0] RD2,
  input  [31:0] immE,
  input  [31:0] imm,
  input  [31:0] PC_4,
  input  [31:0] PC,
  input  [31:0] IR,
  input  [25:0] imm26,
  input  [4:0] WReg,
  input  [4:0] shamt,
  input  SRLV,
  input  SH,
  input  BLEZ,
  input  ERET,
  input  clk,
  input  halt,
  input  en,
  input  rst,
  input  \预测跳转 ,
  input  [31:0] \预测地址 ,
  input  Hit,
  input  [2:0] HitPos,
  output [14:0] cont_,
  output [31:0] RD1_,
  output [31:0] RD2_,
  output [31:0] immE_,
  output [31:0] imm_,
  output [31:0] PC_4_,
  output [31:0] PC_,
  output [31:0] IR_,
  output [25:0] imm26_,
  output [4:0] WReg_,
  output [4:0] shamt_,
  output SRLV_,
  output SH_,
  output BLEZ_,
  output ERET_,
  output \预测跳转_ ,
  output [31:0] \预测地址_ ,
  output Hit_,
  output [2:0] HitPos_
);

  wire multiplexer_12_out, multiplexer_13_out, multiplexer_14_out, multiplexer_15_out, multiplexer_16_out,
       multiplexer_18_out;
  wire [2:0] multiplexer_19_out;
  wire [4:0] multiplexer_9_out, multiplexer_10_out;
  wire [14:0] multiplexer_1_out;
  wire [25:0] multiplexer_11_out;
  wire [31:0] multiplexer_2_out, multiplexer_3_out, multiplexer_4_out, multiplexer_5_out, multiplexer_6_out,
       multiplexer_7_out, multiplexer_8_out, multiplexer_17_out;

  Multiplexer #(.width(15), .enable("false")) multiplexer_1 (
    .in0(cont), .in1({15{1'b0}}), .out(multiplexer_1_out), .sel(halt));
  Multiplexer #(.width(32), .enable("false")) multiplexer_2 (
    .in0(PC_4), .in1({32{1'b0}}), .out(multiplexer_2_out), .sel(halt));
  Multiplexer #(.width(32), .enable("false")) multiplexer_3 (
    .in0(IR), .in1({32{1'b0}}), .out(multiplexer_3_out), .sel(halt));
  Multiplexer #(.width(32), .enable("false")) multiplexer_4 (
    .in0(RD1), .in1({32{1'b0}}), .out(multiplexer_4_out), .sel(halt));
  Multiplexer #(.width(32), .enable("false")) multiplexer_5 (
    .in0(RD2), .in1({32{1'b0}}), .out(multiplexer_5_out), .sel(halt));
  Multiplexer #(.width(32), .enable("false")) multiplexer_6 (
    .in0(imm), .in1({32{1'b0}}), .out(multiplexer_6_out), .sel(halt));
  Multiplexer #(.width(32), .enable("false")) multiplexer_7 (
    .in0(immE), .in1({32{1'b0}}), .out(multiplexer_7_out), .sel(halt));
  Multiplexer #(.width(32), .enable("false")) multiplexer_8 (
    .in0(PC), .in1({32{1'b0}}), .out(multiplexer_8_out), .sel(halt));
  Multiplexer #(.width(5), .enable("false")) multiplexer_9 (
    .in0(shamt), .in1({5{1'b0}}), .out(multiplexer_9_out), .sel(halt));
  Multiplexer #(.width(5), .enable("false")) multiplexer_10 (
    .in0(WReg), .in1({5{1'b0}}), .out(multiplexer_10_out), .sel(halt));
  Multiplexer #(.width(26), .enable("false")) multiplexer_11 (
    .in0(imm26), .in1({26{1'b0}}), .out(multiplexer_11_out), .sel(halt));
  Multiplexer #(.enable("false")) multiplexer_12 (.in0(SRLV), .in1(1'b0), .out(multiplexer_12_out), .sel(halt));
  Multiplexer #(.enable("false")) multiplexer_13 (.in0(SH), .in1(1'b0), .out(multiplexer_13_out), .sel(halt));
  Multiplexer #(.enable("false")) multiplexer_14 (.in0(BLEZ), .in1(1'b0), .out(multiplexer_14_out), .sel(halt));
  Multiplexer #(.enable("false")) multiplexer_15 (.in0(ERET), .in1(1'b0), .out(multiplexer_15_out), .sel(halt));
  Multiplexer #(.enable("false")) multiplexer_16 (.in0(\预测跳转 ), .in1(1'b0), .out(multiplexer_16_out), .sel(halt));
  Multiplexer #(.width(32), .enable("false")) multiplexer_17 (
    .in0(\预测地址 ), .in1({32{1'b0}}), .out(multiplexer_17_out), .sel(halt));
  Multiplexer #(.enable("false")) multiplexer_18 (.in0(Hit), .in1(1'b0), .out(multiplexer_18_out), .sel(halt));
  Multiplexer #(.width(3), .enable("false")) multiplexer_19 (
    .in0(HitPos), .in1(3'b000), .out(multiplexer_19_out), .sel(halt));
  Register #(.width(15)) u_IR (.D(multiplexer_1_out), .en(en), .Q(cont_), .clk(clk), .clr(rst));
  Register #(.width(32)) IR_2 (.D(multiplexer_2_out), .en(en), .Q(PC_4_), .clk(clk), .clr(rst));
  Register #(.width(32)) IR_3 (.D(multiplexer_3_out), .en(en), .Q(IR_), .clk(clk), .clr(rst));
  Register #(.width(32)) IR_4 (.D(multiplexer_4_out), .en(en), .Q(RD1_), .clk(clk), .clr(rst));
  Register #(.width(32)) IR_5 (.D(multiplexer_5_out), .en(en), .Q(RD2_), .clk(clk), .clr(rst));
  Register #(.width(32)) IR_6 (.D(multiplexer_6_out), .en(en), .Q(imm_), .clk(clk), .clr(rst));
  Register #(.width(32)) IR_7 (.D(multiplexer_7_out), .en(en), .Q(immE_), .clk(clk), .clr(rst));
  Register #(.width(32)) IR_8 (.D(multiplexer_8_out), .en(en), .Q(PC_), .clk(clk), .clr(rst));
  Register #(.width(5)) IR_9 (.D(multiplexer_9_out), .en(en), .Q(shamt_), .clk(clk), .clr(rst));
  Register #(.width(5)) IR_10 (.D(multiplexer_10_out), .en(en), .Q(WReg_), .clk(clk), .clr(rst));
  Register #(.width(26)) IR_11 (.D(multiplexer_11_out), .en(en), .Q(imm26_), .clk(clk), .clr(rst));
  Register #(.width(1)) IR_12 (.D(multiplexer_12_out), .en(en), .Q(SRLV_), .clk(clk), .clr(rst));
  Register #(.width(1)) IR_13 (.D(multiplexer_13_out), .en(en), .Q(SH_), .clk(clk), .clr(rst));
  Register #(.width(1)) IR_14 (.D(multiplexer_14_out), .en(en), .Q(BLEZ_), .clk(clk), .clr(rst));
  Register #(.width(1)) IR_15 (.D(multiplexer_15_out), .en(en), .Q(ERET_), .clk(clk), .clr(rst));
  Register #(.width(1)) IR_16 (.D(multiplexer_16_out), .en(en), .Q(\预测跳转_ ), .clk(clk), .clr(rst));
  Register #(.width(32)) IR_17 (.D(multiplexer_17_out), .en(en), .Q(\预测地址_ ), .clk(clk), .clr(rst));
  Register #(.width(1)) IR_18 (.D(multiplexer_18_out), .en(en), .Q(Hit_), .clk(clk), .clr(rst));
  Register #(.width(3)) IR_19 (.D(multiplexer_19_out), .en(en), .Q(HitPos_), .clk(clk), .clr(rst));
endmodule

module EX_MEM (
  input  [14:0] cont,
  input  [31:0] ALUout,
  input  [31:0] RD1,
  input  [31:0] RD2,
  input  [31:0] IR,
  input  [31:0] PC,
  input  [4:0] WReg,
  input  LH,
  input  clk,
  input  halt,
  input  en,
  input  rst,
  output [14:0] cont_,
  output [31:0] ALUout_,
  output [31:0] RD1_,
  output [31:0] RD2_,
  output [31:0] IR_,
  output [31:0] PC_,
  output [4:0] WReg_,
  output LH_
);

  wire multiplexer_8_out;
  wire [4:0] multiplexer_7_out;
  wire [14:0] multiplexer_1_out;
  wire [31:0] multiplexer_2_out, multiplexer_3_out, multiplexer_4_out, multiplexer_5_out, multiplexer_6_out;

  Multiplexer #(.width(15), .enable("false")) multiplexer_1 (
    .in0(cont), .in1({15{1'b0}}), .out(multiplexer_1_out), .sel(halt));
  Multiplexer #(.width(32), .enable("false")) multiplexer_2 (
    .in0(ALUout), .in1({32{1'b0}}), .out(multiplexer_2_out), .sel(halt));
  Multiplexer #(.width(32), .enable("false")) multiplexer_3 (
    .in0(IR), .in1({32{1'b0}}), .out(multiplexer_3_out), .sel(halt));
  Multiplexer #(.width(32), .enable("false")) multiplexer_4 (
    .in0(RD1), .in1({32{1'b0}}), .out(multiplexer_4_out), .sel(halt));
  Multiplexer #(.width(32), .enable("false")) multiplexer_5 (
    .in0(RD2), .in1({32{1'b0}}), .out(multiplexer_5_out), .sel(halt));
  Multiplexer #(.width(32), .enable("false")) multiplexer_6 (
    .in0(PC), .in1({32{1'b0}}), .out(multiplexer_6_out), .sel(halt));
  Multiplexer #(.width(5), .enable("false")) multiplexer_7 (
    .in0(WReg), .in1({5{1'b0}}), .out(multiplexer_7_out), .sel(halt));
  Multiplexer #(.enable("false")) multiplexer_8 (.in0(LH), .in1(1'b0), .out(multiplexer_8_out), .sel(halt));
  Register #(.width(15)) u_IR (.D(multiplexer_1_out), .en(en), .Q(cont_), .clk(clk), .clr(rst));
  Register #(.width(32)) IR_2 (.D(multiplexer_2_out), .en(en), .Q(ALUout_), .clk(clk), .clr(rst));
  Register #(.width(32)) IR_3 (.D(multiplexer_3_out), .en(en), .Q(IR_), .clk(clk), .clr(rst));
  Register #(.width(32)) IR_4 (.D(multiplexer_4_out), .en(en), .Q(RD1_), .clk(clk), .clr(rst));
  Register #(.width(32)) IR_5 (.D(multiplexer_5_out), .en(en), .Q(RD2_), .clk(clk), .clr(rst));
  Register #(.width(32)) IR_6 (.D(multiplexer_6_out), .en(en), .Q(PC_), .clk(clk), .clr(rst));
  Register #(.width(5)) IR_7 (.D(multiplexer_7_out), .en(en), .Q(WReg_), .clk(clk), .clr(rst));
  Register #(.width(1)) IR_8 (.D(multiplexer_8_out), .en(en), .Q(LH_), .clk(clk), .clr(rst));
endmodule

module MEM_WB (
  input  [14:0] cont,
  input  [31:0] ALUout,
  input  [31:0] MEMout,
  input  [31:0] RD1,
  input  [31:0] RD2,
  input  [31:0] IR,
  input  [31:0] PC,
  input  [4:0] WReg,
  input  clk,
  input  halt,
  input  en,
  input  rst,
  output [14:0] cont_,
  output [31:0] ALUout_,
  output [31:0] MEMout_,
  output [31:0] RD1_,
  output [31:0] RD2_,
  output [31:0] IR_,
  output [31:0] PC_,
  output [4:0] WReg_
);

  wire [4:0] multiplexer_8_out;
  wire [14:0] multiplexer_1_out;
  wire [31:0] multiplexer_2_out, multiplexer_3_out, multiplexer_4_out, multiplexer_5_out, multiplexer_6_out,
       multiplexer_7_out;

  Multiplexer #(.width(15), .enable("false")) multiplexer_1 (
    .in0(cont), .in1({15{1'b0}}), .out(multiplexer_1_out), .sel(halt));
  Multiplexer #(.width(32), .enable("false")) multiplexer_2 (
    .in0(ALUout), .in1({32{1'b0}}), .out(multiplexer_2_out), .sel(halt));
  Multiplexer #(.width(32), .enable("false")) multiplexer_3 (
    .in0(IR), .in1({32{1'b0}}), .out(multiplexer_3_out), .sel(halt));
  Multiplexer #(.width(32), .enable("false")) multiplexer_4 (
    .in0(RD1), .in1({32{1'b0}}), .out(multiplexer_4_out), .sel(halt));
  Multiplexer #(.width(32), .enable("false")) multiplexer_5 (
    .in0(RD2), .in1({32{1'b0}}), .out(multiplexer_5_out), .sel(halt));
  Multiplexer #(.width(32), .enable("false")) multiplexer_6 (
    .in0(PC), .in1({32{1'b0}}), .out(multiplexer_6_out), .sel(halt));
  Multiplexer #(.width(32), .enable("false")) multiplexer_7 (
    .in0(MEMout), .in1({32{1'b0}}), .out(multiplexer_7_out), .sel(halt));
  Multiplexer #(.width(5), .enable("false")) multiplexer_8 (
    .in0(WReg), .in1({5{1'b0}}), .out(multiplexer_8_out), .sel(halt));
  Register #(.width(15)) u_IR (.D(multiplexer_1_out), .en(en), .Q(cont_), .clk(clk), .clr(rst));
  Register #(.width(32)) IR_2 (.D(multiplexer_2_out), .en(en), .Q(ALUout_), .clk(clk), .clr(rst));
  Register #(.width(32)) IR_3 (.D(multiplexer_3_out), .en(en), .Q(IR_), .clk(clk), .clr(rst));
  Register #(.width(32)) IR_4 (.D(multiplexer_4_out), .en(en), .Q(RD1_), .clk(clk), .clr(rst));
  Register #(.width(32)) IR_5 (.D(multiplexer_5_out), .en(en), .Q(RD2_), .clk(clk), .clr(rst));
  Register #(.width(32)) IR_6 (.D(multiplexer_6_out), .en(en), .Q(PC_), .clk(clk), .clr(rst));
  Register #(.width(32)) IR_7 (.D(multiplexer_7_out), .en(en), .Q(MEMout_), .clk(clk), .clr(rst));
  Register #(.width(5)) IR_8 (.D(multiplexer_8_out), .en(en), .Q(WReg_), .clk(clk), .clr(rst));
endmodule

module \分支相关流水线  (
);

  wire and_1_out, and_2_out, and_3_out, and_4_out, and_5_out, and_6_out, CLK, comparator_1_eq, compare, en,
       Go, IR1, IR2, IR3, JMP, JR, LOCK, mem_wb_1_p1, mips_alu_1_equal, nop, or_1_out, or_2_out, RST,
       SignedExt, W1, W2, W3, WBJAL, WBRegWrite, WBSyscall;
  wire [4:0] ex_mem_1_wreg_, id_ex_1_shamt_, id_ex_1_wreg_, mem_wb_1_p18, multiplexer_5_out,
       multiplexer_6_out, multiplexer_7_out, multiplexer_8_out;
  wire [12:0] mem_wb_1_p12;
  wire [14:0] ex_mem_1_cont_, id_ex_1_cont_, \硬布线控制器_1_beq ;
  wire [15:0] \LoadUse次数 , \总周期数 , \插入气泡数 , \无条件分支数 , \条件分支成功数 ;
  wire [25:0] id_ex_1_imm26_;
  wire [31:0] adder_1_out, adder_2_out, adder_3_out, bit_extender_1_out, bit_extender_2_out,
       ex_mem_1_aluout_, ex_mem_1_rd1_, ex_mem_1_rd2_, EX_PC, EXR1, id_ex_1_imm_, id_ex_1_imme_,
       id_ex_1_pc_4_, id_ex_1_rd2_, ID_PC, if_id_1_instru_, if_id_1_pc_4_, IF_PC, LedData, MEM_PC,
       mem_wb_1_p15, mem_wb_1_p16, mips_alu_1_result, multiplexer_2_out, multiplexer_3_out,
       multiplexer_4_out, multiplexer_9_out, multiplexer_10_out, multiplexer_11_out, multiplexer_12_out,
       multiplexer_13_out, R1, R2, rom_1_data, shifter_1_out, undriven, WB_PC, WBR1, WBR2;

  Button \u_总复位  (.out(RST));
  Button _1 (.out(IR1));
  Button _2 (.out(IR2));
  Button _3 (.out(IR3));
  Button \u_继续运行  (.out(Go));
  LED led_1 (.in(W1));
  LED led_2 (.in(W2));
  LED led_3 (.in(W3));
  and and_1 (and_1_out, ~LOCK, JMP);  // AND_Gate
  and and_2 (and_2_out, ~LOCK, compare);  // AND_Gate
  Register #(.width(32)) PC (.D(multiplexer_2_out), .en(en), .Q(IF_PC), .clk(CLK), .clr(RST));
  Multiplexer #(.enable("false")) multiplexer_1 (.in0(1'b1), .in1(1'b0), .out(en), .sel(and_3_out));
  and and_3 (and_3_out, LOCK, ~Go);  // AND_Gate
  Counter #(.width(16), .max('hffff)) counter_1 (.count(en), .Q(\总周期数 ), .clk(CLK), .clr(RST));  // open: load, D, carry
  Multiplexer #(.width(32), .enable("false")) multiplexer_2 (
    .in0(multiplexer_4_out), .in1(multiplexer_3_out), .out(multiplexer_2_out), .sel(JMP));
  Multiplexer #(.width(32), .enable("false")) multiplexer_3 (
    .in0({4'b0000, id_ex_1_imm26_, 2'b00}), .in1(EXR1), .out(multiplexer_3_out), .sel(JR));
  Hex_Digit_Display hex_digit_display_1 (.value(LedData[31:28]));  // open: dp
  Counter #(.width(16), .max('hffff)) counter_2 (
    .count(and_1_out), .Q(\无条件分支数 ), .clk(CLK), .clr(RST));  // open: load, D, carry
  Counter #(.width(16), .max('hffff)) counter_3 (
    .count(and_2_out), .Q(\条件分支成功数 ), .clk(CLK), .clr(RST));  // open: load, D, carry
  Hex_Digit_Display hex_digit_display_2 (.value(LedData[27:24]));  // open: dp
  Hex_Digit_Display hex_digit_display_3 (.value(LedData[23:20]));  // open: dp
  Multiplexer #(.width(32), .enable("false")) multiplexer_4 (
    .in0(adder_1_out), .in1(adder_3_out), .out(multiplexer_4_out), .sel(compare));
  Hex_Digit_Display hex_digit_display_4 (.value(LedData[19:16]));  // open: dp
  Hex_Digit_Display hex_digit_display_5 (.value(LedData[15:12]));  // open: dp
  ROM #(.addrWidth(10), .dataWidth(32)) rom_1 (.addr(IF_PC[11:2]), .data(rom_1_data));  // open: sel
  Adder #(.width(32)) adder_1 (.a(IF_PC), .b(32'h4), .out(adder_1_out));  // open: cin, cout
  Hex_Digit_Display hex_digit_display_6 (.value(LedData[11:8]));  // open: dp
  Hex_Digit_Display hex_digit_display_7 (.value(LedData[7:4]));  // open: dp
  Clock clock_1 (.out(CLK));
  IF_ID if_id_1 (
    .instru(rom_1_data), .PC_4(adder_1_out), .clk(CLK), .instru_(if_id_1_instru_), .PC_4_(if_id_1_pc_4_),
    .PC(IF_PC), .PC_(ID_PC), .en(en), .halt(or_1_out));  // open: rst, 预测跳转, 预测地址, Hit, HitPos, 预测跳转_, 预测地址_, Hit_, HitPos_
  or or_1 (or_1_out, RST, nop);
  Hex_Digit_Display hex_digit_display_8 (.value(LedData[3:0]));  // open: dp
  // Probe on if_id_1_instru_
  \硬布线控制器  \u_硬布线控制器_1  (
    .Func(if_id_1_instru_[5:0]), .OP(if_id_1_instru_[31:26]), .ALU_OP(\硬布线控制器_1_beq [9:6]),
    .MemToReg(\硬布线控制器_1_beq [4]), .MemWrite(\硬布线控制器_1_beq [5]), .ALU_SRC(\硬布线控制器_1_beq [10]),
    .RegWrite(\硬布线控制器_1_beq [14]), .SysCALL(\硬布线控制器_1_beq [13]), .SignedExt(SignedExt),
    .RegDst(\硬布线控制器_1_beq [12]), .JR(\硬布线控制器_1_beq [2]), .JMP(\硬布线控制器_1_beq [3]), .Beq(\硬布线控制器_1_beq [0]),
    .JAL(\硬布线控制器_1_beq [11]), .Bne(\硬布线控制器_1_beq [1]));  // open: SRLV, XORI, SH, BLEZ, ERET, RS, RD, MFC_0, MTC_0
  Multiplexer #(.width(5), .enable("false")) multiplexer_5 (
    .in0(if_id_1_instru_[25:21]), .in1(5'b00010), .out(multiplexer_5_out), .sel(\硬布线控制器_1_beq [13]));
  Multiplexer #(.width(5), .enable("false")) multiplexer_6 (
    .in0(if_id_1_instru_[20:16]), .in1(5'b00100), .out(multiplexer_6_out), .sel(\硬布线控制器_1_beq [13]));
  // Probe on \总周期数 
  // Probe on \无条件分支数 
  // Probe on \条件分支成功数 
  // Probe on \插入气泡数 
  // Probe on \LoadUse次数 
  Multiplexer #(.width(5), .enable("false")) multiplexer_7 (
    .in0(if_id_1_instru_[20:16]), .in1(if_id_1_instru_[15:11]), .out(multiplexer_7_out),
    .sel(\硬布线控制器_1_beq [12]));
  // Probe on IF_PC[11:0]
  Multiplexer #(.width(5), .enable("false")) multiplexer_8 (
    .in0(multiplexer_7_out), .in1({5{1'b1}}), .out(multiplexer_8_out), .sel(\硬布线控制器_1_beq [11]));
  Adder #(.width(32)) adder_2 (.a(WB_PC), .b(32'h4), .out(adder_2_out));  // open: cin, cout
  // Probe on multiplexer_13_out
  // Probe on ID_PC[11:0]
  Multiplexer #(.width(32), .enable("false")) multiplexer_9 (
    .in0(multiplexer_13_out), .in1(adder_2_out), .out(multiplexer_9_out), .sel(WBJAL));
  // Probe on mem_wb_1_p18
  // Probe on EX_PC[11:0]
  // Probe on MEM_PC[11:0]
  MIPS_Regifile mips_regifile_1 (
    .Din(multiplexer_9_out), .Clk(CLK), .R1(R1), .R2(R2), .WE(WBRegWrite), .W_num(mem_wb_1_p18),
    .R1_num(multiplexer_5_out), .R2_num(multiplexer_6_out));
  assign bit_extender_1_out = {{16{1'b0}}, if_id_1_instru_[15:0]};  // Bit_Extender bit_extender_1
  assign bit_extender_2_out = {{16{if_id_1_instru_[15]}}, if_id_1_instru_[15:0]};  // Bit_Extender bit_extender_2
  // Probe on WB_PC[11:0]
  // Probe on R1
  // Probe on R2
  Multiplexer #(.width(32), .enable("false")) multiplexer_10 (
    .in0(bit_extender_1_out), .in1(bit_extender_2_out), .out(multiplexer_10_out), .sel(SignedExt));
  ID_EX id_ex_1 (
    .RD1(R1), .RD2(R2), .imm(bit_extender_2_out), .PC_4(if_id_1_pc_4_), .clk(CLK), .halt(or_2_out),
    .RD1_(EXR1), .RD2_(id_ex_1_rd2_), .imm_(id_ex_1_imm_), .PC_4_(id_ex_1_pc_4_), .WReg(multiplexer_8_out),
    .WReg_(id_ex_1_wreg_), .immE(multiplexer_10_out), .immE_(id_ex_1_imme_), .cont(\硬布线控制器_1_beq ),
    .cont_({id_ex_1_cont_[14:4], JMP, JR, id_ex_1_cont_[1:0]}), .shamt(if_id_1_instru_[10:6]),
    .shamt_(id_ex_1_shamt_), .PC(ID_PC), .PC_(EX_PC), .en(en), .imm26(if_id_1_instru_[25:0]),
    .imm26_(id_ex_1_imm26_));  // open: IR, IR_, SRLV, SRLV_, SH, SH_, BLEZ, BLEZ_, rst, ERET, ERET_, 预测跳转, 预测跳转_, 预测地址, 预测地址_, Hit, Hit_, HitPos, HitPos_
  or or_2 (or_2_out, nop, RST);
  Multiplexer #(.width(32), .enable("false")) multiplexer_11 (
    .in0(id_ex_1_rd2_), .in1(id_ex_1_imme_), .out(multiplexer_11_out), .sel(id_ex_1_cont_[10]));
  Shifter #(.width(32)) shifter_1 (.in(id_ex_1_imm_), .\dist (5'b00010), .out(shifter_1_out));
  Comparator #(.width(32)) comparator_1 (.a(WBR1), .b(32'h22), .eq(comparator_1_eq));  // open: gt, lt
  and and_4 (and_4_out, id_ex_1_cont_[0], mips_alu_1_equal);
  and and_5 (and_5_out, ~mips_alu_1_equal, id_ex_1_cont_[1]);  // AND_Gate
  or or_3 (nop, JMP, JR, compare);
  // Probe on EXR1
  MIPS_ALU mips_alu_1 (
    .X(EXR1), .Y(multiplexer_11_out), .AluOP(id_ex_1_cont_[9:6]), .Equal(mips_alu_1_equal),
    .Result(mips_alu_1_result), .shamt(id_ex_1_shamt_));  // open: Result_2
  // Probe on mips_alu_1_result
  // Probe on id_ex_1_rd2_
  Adder #(.width(32)) adder_3 (.a(shifter_1_out), .b(id_ex_1_pc_4_), .out(adder_3_out));  // open: cin, cout
  and and_6 (and_6_out, comparator_1_eq, WBSyscall);
  and and_7 (LOCK, ~comparator_1_eq, WBSyscall);  // AND_Gate
  or or_4 (compare, and_4_out, and_5_out);
  EX_MEM ex_mem_1 (
    .cont({id_ex_1_cont_[14:4], JMP, JR, id_ex_1_cont_[1:0]}), .ALUout(mips_alu_1_result),
    .RD2(id_ex_1_rd2_), .WReg(id_ex_1_wreg_), .clk(CLK), .halt(RST), .cont_(ex_mem_1_cont_),
    .ALUout_(ex_mem_1_aluout_), .RD2_(ex_mem_1_rd2_), .WReg_(ex_mem_1_wreg_), .RD1(EXR1),
    .RD1_(ex_mem_1_rd1_), .PC(EX_PC), .PC_(MEM_PC), .en(en));  // open: IR, IR_, LH, LH_, rst
  Multiplexer #(.width(32)) multiplexer_12 (
    .in0(undriven), .in1(WBR2), .out(multiplexer_12_out), .sel(and_6_out), .en(and_6_out));
  Register #(.width(32)) register_1 (.D(multiplexer_12_out), .Q(LedData), .clk(CLK), .clr(RST));  // open: en
  // Probe on ex_mem_1_rd1_
  // MIPS_RAM mips_ram_1: pin names not known; wires that end beside it: ex_mem_1_aluout_[21:2], ex_mem_1_rd2_, ex_mem_1_cont_[5], CLK, RST
  // Probe on ex_mem_1_rd2_
  // MEM_WB mem_wb_1: pin names not known; wires that end beside it: mem_wb_1_p1, ex_mem_1_cont_, MEM_PC, ex_mem_1_rd1_, ex_mem_1_aluout_, mem_wb_1_p1, ex_mem_1_rd2_, ex_mem_1_wreg_, en, CLK, RST, {WBRegWrite, WBSyscall, mem_wb_1_p12[12], WBJAL, mem_wb_1_p12[10:0]}, WB_PC, WBR1, mem_wb_1_p15, mem_wb_1_p16, WBR2, mem_wb_1_p18
  // Probe on WBR1
  Multiplexer #(.width(32), .enable("false")) multiplexer_13 (
    .in0(mem_wb_1_p15), .in1(mem_wb_1_p16), .out(multiplexer_13_out), .sel(mem_wb_1_p12[4]));
  // Probe on WBR2

  // Notes on the sheet:
  //   中断源
  //   中断等待指示
  //   指令存储器
  //   数码管输出
  //   指令字
  //   contents of rom_1 (hex, n*v repeats v):
  //   20080001 20090003 20110876 118d00 112020 20020022 c 200b0008 1118806 1318806 112020 20020022 c
  //   216bffff 1560fff9 2002000a c
  //   OP
  //   Func
  //   rs
  //   rt
  //   rd
  //   Beq
  //   JMP
  //   JR
  //   Bne
  //   OP
  //   JAL
  //   Func
  //   Syscall
  //   MemToReg
  //   MemWrite
  //   AluOP
  //   AluSrcB
  //   RegWrite
  //   RegDst
  //   流水调试日志用
endmodule

module \气泡流水线  (
);

  wire and_1_out, and_2_out, and_3_out, and_4_out, and_5_out, and_6_out, and_7_out, and_8_out, and_9_out,
       CLK, comparator_1_eq, compare, en, EX_BLEZ, EX_RegWrite, EX_SH, EX_SRLV, Go, ID_BLEZ, ID_SH, ID_SRLV,
       ID_XORI, IR1, IR2, IR3, JAL, JMP, JR, LOCK, MEM_JAL, MEM_RegDst, MEM_RegWrite, MEM_SH, MemWrite_MEM,
       mips_alu_1_equal, multiplexer_14_out, nop, or_1_out, or_2_out, RegDst, RST, SignedExt, SW_sel, W1, W2,
       W3, WB_JAL, WBRegWrite, WBSyscall, \数据相关 ;
  wire [3:0] multiplexer_17_out, multiplexer_18_out;
  wire [4:0] ex_mem_1_wreg_, EX_rd, EX_rt, EX_WriteReg, id_ex_1_shamt_, id_ex_1_wreg_, ID_R1_num, ID_R2_num,
       MEM_rd, MEM_rt, mem_wb_1_wreg_, MEM_WriteReg, multiplexer_7_out, multiplexer_8_out,
       multiplexer_13_out, multiplexer_21_out, multiplexer_22_out;
  wire [5:0] Func, OP;
  wire [12:0] mem_wb_1_cont_;
  wire [13:0] ex_mem_1_cont_, id_ex_1_cont_;
  wire [14:0] \硬布线控制器_1_beq ;
  wire [15:0] \LoadUse次数 , \总周期数 , \插入气泡数 , \无条件分支数 , \条件分支成功数 ;
  wire [25:0] id_ex_1_imm26_;
  wire [25:6] if_id_1_instru_;
  wire [31:0] adder_1_out, adder_2_out, adder_3_out, ALUOUT, bit_extender_1_out, bit_extender_2_out,
       ex_mem_1_aluout_, ex_mem_1_ir_, ex_mem_1_rd1_, ex_mem_1_rd2_, EX_PC, EXR1, id_ex_1_imm_,
       id_ex_1_imme_, id_ex_1_ir_, id_ex_1_pc_4_, id_ex_1_rd2_, ID_PC, if_id_1_pc_4_, IF_PC, LedData, MEM_PC,
       mem_wb_1_aluout_, mem_wb_1_memout_, mips_ram_1_p7, multiplexer_2_out, multiplexer_3_out,
       multiplexer_4_out, multiplexer_9_out, multiplexer_10_out, multiplexer_11_out, multiplexer_12_out,
       multiplexer_15_out, multiplexer_16_out, multiplexer_19_out, multiplexer_20_out, R1, R2, rom_1_data,
       shifter_1_out, undriven, WB_PC, WBR1, WBR2;

  Button \u_总复位  (.out(RST));
  Button _1 (.out(IR1));
  Button _2 (.out(IR2));
  Button _3 (.out(IR3));
  and and_1 (and_1_out, en, ~\数据相关 );  // AND_Gate
  Button \u_继续运行  (.out(Go));
  LED led_1 (.in(W1));
  LED led_2 (.in(W2));
  LED led_3 (.in(W3));
  Register #(.width(32)) PC (.D(multiplexer_2_out), .en(and_1_out), .Q(IF_PC), .clk(CLK), .clr(RST));
  Multiplexer #(.enable("false")) multiplexer_1 (.in0(1'b1), .in1(1'b0), .out(en), .sel(and_2_out));
  and and_2 (and_2_out, LOCK, ~Go);  // AND_Gate
  Counter #(.width(16), .max('hffff)) counter_1 (.count(en), .Q(\总周期数 ), .clk(CLK), .clr(RST));  // open: load, D, carry
  Multiplexer #(.width(32), .enable("false")) multiplexer_2 (
    .in0(multiplexer_4_out), .in1(multiplexer_3_out), .out(multiplexer_2_out), .sel(JMP));
  Multiplexer #(.width(32), .enable("false")) multiplexer_3 (
    .in0({4'b0000, id_ex_1_imm26_, 2'b00}), .in1(EXR1), .out(multiplexer_3_out), .sel(JR));
  Hex_Digit_Display hex_digit_display_1 (.value(LedData[31:28]));  // open: dp
  and and_3 (and_3_out, ~LOCK, JMP);  // AND_Gate
  and and_4 (and_4_out, ~LOCK, compare);  // AND_Gate
  Hex_Digit_Display hex_digit_display_2 (.value(LedData[27:24]));  // open: dp
  Hex_Digit_Display hex_digit_display_3 (.value(LedData[23:20]));  // open: dp
  Counter #(.width(16), .max('hffff)) counter_2 (
    .count(and_3_out), .Q(\无条件分支数 ), .clk(CLK), .clr(RST));  // open: load, D, carry
  Counter #(.width(16), .max('hffff)) counter_3 (
    .count(and_4_out), .Q(\条件分支成功数 ), .clk(CLK), .clr(RST));  // open: load, D, carry
  ROM #(.addrWidth(10), .dataWidth(32)) rom_1 (.addr(IF_PC[11:2]), .data(rom_1_data));  // open: sel
  Multiplexer #(.width(32), .enable("false")) multiplexer_4 (
    .in0(adder_1_out), .in1(adder_3_out), .out(multiplexer_4_out), .sel(compare));
  Hex_Digit_Display hex_digit_display_4 (.value(LedData[15:12]));  // open: dp
  Hex_Digit_Display hex_digit_display_5 (.value(LedData[19:16]));  // open: dp
  and and_5 (and_5_out, en, ~\数据相关 );  // AND_Gate
  Adder #(.width(32)) adder_1 (.a(IF_PC), .b(32'h4), .out(adder_1_out));  // open: cin, cout
  Hex_Digit_Display hex_digit_display_6 (.value(LedData[7:4]));  // open: dp
  Hex_Digit_Display hex_digit_display_7 (.value(LedData[11:8]));  // open: dp
  Clock clock_1 (.out(CLK));
  IF_ID if_id_1 (
    .instru(rom_1_data), .PC_4(adder_1_out), .clk(CLK), .rst(RST), .instru_({OP, if_id_1_instru_, Func}),
    .PC_4_(if_id_1_pc_4_), .PC(IF_PC), .PC_(ID_PC), .en(and_5_out), .halt(nop));  // open: 预测跳转, 预测地址, Hit, HitPos, 预测跳转_, 预测地址_, Hit_, HitPos_
  Hex_Digit_Display hex_digit_display_8 (.value(LedData[3:0]));  // open: dp
  // Probe on {OP, if_id_1_instru_, Func}
  \硬布线控制器  \u_硬布线控制器_1  (
    .Func(Func), .OP(OP), .ALU_OP(\硬布线控制器_1_beq [9:6]), .MemToReg(\硬布线控制器_1_beq [4]),
    .MemWrite(\硬布线控制器_1_beq [5]), .ALU_SRC(\硬布线控制器_1_beq [10]), .RegWrite(\硬布线控制器_1_beq [14]),
    .SysCALL(\硬布线控制器_1_beq [13]), .SignedExt(SignedExt), .RegDst(\硬布线控制器_1_beq [12]), .JR(\硬布线控制器_1_beq [2]),
    .JMP(\硬布线控制器_1_beq [3]), .Beq(\硬布线控制器_1_beq [0]), .JAL(\硬布线控制器_1_beq [11]), .Bne(\硬布线控制器_1_beq [1]),
    .SRLV(ID_SRLV), .XORI(ID_XORI), .SH(ID_SH), .BLEZ(ID_BLEZ));  // open: ERET, RS, RD, MFC_0, MTC_0
  Multiplexer #(.width(5), .enable("false")) multiplexer_5 (
    .in0(if_id_1_instru_[25:21]), .in1(5'b00010), .out(ID_R1_num), .sel(\硬布线控制器_1_beq [13]));
  Multiplexer #(.width(5), .enable("false")) multiplexer_6 (
    .in0(if_id_1_instru_[20:16]), .in1(5'b00100), .out(ID_R2_num), .sel(\硬布线控制器_1_beq [13]));
  // Probe on \总周期数 
  // Probe on \无条件分支数 
  // Probe on \条件分支成功数 
  // Probe on \插入气泡数 
  // Probe on \LoadUse次数 
  Multiplexer #(.width(5), .enable("false")) multiplexer_7 (
    .in0(if_id_1_instru_[20:16]), .in1(if_id_1_instru_[15:11]), .out(multiplexer_7_out),
    .sel(\硬布线控制器_1_beq [12]));
  // Probe on multiplexer_19_out
  // Probe on IF_PC[11:0]
  // Probe on ID_R1_num
  // Probe on ID_R2_num
  Multiplexer #(.width(5), .enable("false")) multiplexer_8 (
    .in0(multiplexer_7_out), .in1({5{1'b1}}), .out(multiplexer_8_out), .sel(\硬布线控制器_1_beq [11]));
  Adder #(.width(32)) adder_2 (.a(WB_PC), .b(32'h4), .out(adder_2_out));  // open: cin, cout
  // Probe on ID_PC[11:0]
  Multiplexer #(.width(32), .enable("false")) multiplexer_9 (
    .in0(multiplexer_19_out), .in1(adder_2_out), .out(multiplexer_9_out), .sel(WB_JAL));
  // Probe on mem_wb_1_wreg_
  // Probe on EX_PC[11:0]
  // Probe on MEM_PC[11:0]
  MIPS_Regifile mips_regifile_1 (
    .Din(multiplexer_9_out), .Clk(CLK), .R1(R1), .R2(R2), .WE(WBRegWrite), .W_num(mem_wb_1_wreg_),
    .R1_num(ID_R1_num), .R2_num(ID_R2_num));
  assign bit_extender_1_out = {{16{1'b0}}, {if_id_1_instru_[15:6], Func}};  // Bit_Extender bit_extender_1
  assign bit_extender_2_out = {{16{if_id_1_instru_[15]}}, {if_id_1_instru_[15:6], Func}};  // Bit_Extender bit_extender_2
  // Probe on WB_PC[11:0]
  // Probe on R1
  // Probe on R2
  Multiplexer #(.width(32), .enable("false")) multiplexer_10 (
    .in0(bit_extender_1_out), .in1(bit_extender_2_out), .out(multiplexer_10_out), .sel(SignedExt));
  ID_EX id_ex_1 (
    .RD1(R1), .RD2(R2), .imm(bit_extender_2_out), .PC_4(if_id_1_pc_4_), .clk(CLK), .halt(or_1_out),
    .RD1_(EXR1), .RD2_(id_ex_1_rd2_), .imm_(id_ex_1_imm_), .PC_4_(id_ex_1_pc_4_), .WReg(multiplexer_8_out),
    .WReg_(id_ex_1_wreg_), .immE(multiplexer_10_out), .immE_(id_ex_1_imme_), .cont(\硬布线控制器_1_beq ),
    .cont_({EX_RegWrite, id_ex_1_cont_[13], RegDst, JAL, id_ex_1_cont_[10:4], JMP, JR, id_ex_1_cont_[1:0]}),
    .shamt(if_id_1_instru_[10:6]), .shamt_(id_ex_1_shamt_), .PC(ID_PC), .PC_(EX_PC), .en(en),
    .imm26({if_id_1_instru_, Func}), .imm26_(id_ex_1_imm26_), .IR({OP, if_id_1_instru_, Func}),
    .IR_({id_ex_1_ir_[31:21], EX_rt, EX_rd, id_ex_1_ir_[10:0]}), .SRLV(ID_SRLV), .SRLV_(EX_SRLV), .SH(ID_SH),
    .SH_(EX_SH), .BLEZ(ID_BLEZ), .BLEZ_(EX_BLEZ), .rst(RST));  // open: ERET, ERET_, 预测跳转, 预测跳转_, 预测地址, 预测地址_, Hit, Hit_, HitPos, HitPos_
  or or_1 (or_1_out, nop, \数据相关 );
  Multiplexer #(.width(32), .enable("false")) multiplexer_11 (
    .in0(id_ex_1_rd2_), .in1(id_ex_1_imme_), .out(multiplexer_11_out), .sel(id_ex_1_cont_[10]));
  Multiplexer #(.width(32), .enable("false")) multiplexer_12 (
    .in0(multiplexer_11_out), .in1({32{1'b0}}), .out(multiplexer_12_out), .sel(EX_BLEZ));
  Shifter #(.width(32)) shifter_1 (.in(id_ex_1_imm_), .\dist (5'b00010), .out(shifter_1_out));
  MIPS_ALU mips_alu_1 (
    .X(EXR1), .Y(multiplexer_12_out), .AluOP(id_ex_1_cont_[9:6]), .Equal(mips_alu_1_equal), .Result(ALUOUT),
    .shamt(multiplexer_13_out));  // open: Result_2
  Multiplexer #(.width(5), .enable("false")) multiplexer_13 (
    .in0(id_ex_1_shamt_), .in1(EXR1[4:0]), .out(multiplexer_13_out), .sel(EX_SRLV));
  Adder #(.width(32)) adder_3 (.a(shifter_1_out), .b(id_ex_1_pc_4_), .out(adder_3_out));  // open: cin, cout
  and and_6 (and_6_out, id_ex_1_cont_[0], mips_alu_1_equal);
  and and_7 (and_7_out, ~mips_alu_1_equal, id_ex_1_cont_[1]);  // AND_Gate
  or or_2 (or_2_out, mips_alu_1_equal, ALUOUT[0]);
  // Probe on EXR1
  // Probe on ALUOUT
  // Probe on id_ex_1_rd2_
  Multiplexer #(.enable("false")) multiplexer_14 (.in0(1'b0), .in1(or_2_out), .out(multiplexer_14_out), .sel(EX_BLEZ));
  EX_MEM ex_mem_1 (
    .cont({EX_RegWrite, id_ex_1_cont_[13], RegDst, JAL, id_ex_1_cont_[10:4], JMP, JR, id_ex_1_cont_[1:0]}),
    .ALUout(ALUOUT), .RD2(id_ex_1_rd2_), .WReg(id_ex_1_wreg_), .clk(CLK), .halt(RST),
    .cont_({MEM_RegWrite, ex_mem_1_cont_[13], MEM_RegDst, MEM_JAL, ex_mem_1_cont_[10:6], MemWrite_MEM, ex_mem_1_cont_[4:0]}),
    .ALUout_({ex_mem_1_aluout_[31:2], SW_sel, ex_mem_1_aluout_[0]}), .RD2_(ex_mem_1_rd2_),
    .WReg_(ex_mem_1_wreg_), .RD1(EXR1), .RD1_(ex_mem_1_rd1_), .PC(EX_PC), .PC_(MEM_PC), .en(en),
    .IR({id_ex_1_ir_[31:21], EX_rt, EX_rd, id_ex_1_ir_[10:0]}),
    .IR_({ex_mem_1_ir_[31:21], MEM_rt, MEM_rd, ex_mem_1_ir_[10:0]}), .LH(EX_SH), .LH_(MEM_SH), .rst(RST));
  or or_3 (compare, and_6_out, and_7_out, multiplexer_14_out);
  or or_4 (nop, compare, JR, JMP);
  // Probe on ex_mem_1_rd1_
  Multiplexer #(.width(32), .enable("false")) multiplexer_15 (
    .in0({{16{1'b0}}, ex_mem_1_rd2_[15:0]}), .in1({ex_mem_1_rd2_[15:0], {16{1'b0}}}),
    .out(multiplexer_15_out), .sel(SW_sel));
  Multiplexer #(.width(32), .enable("false")) multiplexer_16 (
    .in0(ex_mem_1_rd2_), .in1(multiplexer_15_out), .out(multiplexer_16_out), .sel(MEM_SH));
  Multiplexer #(.width(4), .enable("false")) multiplexer_17 (
    .in0(4'b1111), .in1(multiplexer_18_out), .out(multiplexer_17_out), .sel(MEM_SH));
  Counter #(.width(16), .max('hffff)) counter_4 (
    .count(and_8_out), .Q(\插入气泡数 ), .clk(CLK), .clr(RST));  // open: load, D, carry
  and and_8 (and_8_out, ~LOCK, \数据相关 );  // AND_Gate
  Multiplexer #(.width(4), .enable("false")) multiplexer_18 (
    .in0(4'b0011), .in1(4'b1100), .out(multiplexer_18_out), .sel(SW_sel));
  MEM_WB mem_wb_1 (
    .cont({MEM_RegWrite, ex_mem_1_cont_[13], MEM_RegDst, MEM_JAL, ex_mem_1_cont_[10:6], MemWrite_MEM, ex_mem_1_cont_[4:0]}),
    .ALUout({ex_mem_1_aluout_[31:2], SW_sel, ex_mem_1_aluout_[0]}), .MEMout(mips_ram_1_p7),
    .WReg(ex_mem_1_wreg_), .clk(CLK), .halt(RST),
    .cont_({WBRegWrite, WBSyscall, mem_wb_1_cont_[12], WB_JAL, mem_wb_1_cont_[10:0]}),
    .ALUout_(mem_wb_1_aluout_), .MEMout_(mem_wb_1_memout_), .WReg_(mem_wb_1_wreg_), .RD1(ex_mem_1_rd1_),
    .RD1_(WBR1), .RD2(ex_mem_1_rd2_), .RD2_(WBR2), .PC(MEM_PC), .PC_(WB_PC), .en(en),
    .IR({ex_mem_1_ir_[31:21], MEM_rt, MEM_rd, ex_mem_1_ir_[10:0]}), .rst(RST));  // open: IR_
  // MIPS_RAM mips_ram_1: pin names not known; wires that end beside it: ex_mem_1_aluout_[21:2], multiplexer_16_out, MemWrite_MEM, multiplexer_17_out, CLK, RST, mips_ram_1_p7
  Multiplexer #(.width(32), .enable("false")) multiplexer_19 (
    .in0(mem_wb_1_aluout_), .in1(mem_wb_1_memout_), .out(multiplexer_19_out), .sel(mem_wb_1_cont_[4]));
  // Probe on WBR1
  // Probe on WBR2
  Comparator #(.width(32)) comparator_1 (.a(WBR1), .b(32'h22), .eq(comparator_1_eq));  // open: gt, lt
  \数据相关检测  \u_数据相关检测_1  (
    .ID_OP(OP), .EX_WriteReg_num(EX_WriteReg), .EX_RegWrite(EX_RegWrite), .MEM_WriteReg_num(MEM_WriteReg),
    .MEM_RegWrite(MEM_RegWrite), .\数据相关 (\数据相关 ), .ID_FUNC(Func), .ID_R1_num(ID_R1_num), .ID_R2_num(ID_R2_num));  // open: MEM相关, EX相关, EX_OP, Load_Use相关, WB_WriteReg_num, WB_RegWrite, Forward1, Forward2, EX_R1_num, EX_R2_num, EX_FUNC
  and and_9 (and_9_out, comparator_1_eq, WBSyscall);
  and and_10 (LOCK, ~comparator_1_eq, WBSyscall);  // AND_Gate
  Multiplexer #(.width(32)) multiplexer_20 (
    .in0(undriven), .in1(WBR2), .out(multiplexer_20_out), .sel(and_9_out), .en(and_9_out));
  Register #(.width(32)) register_1 (.D(multiplexer_20_out), .Q(LedData), .clk(CLK), .clr(RST));  // open: en
  Multiplexer #(.width(5), .enable("false")) multiplexer_21 (
    .in0(EX_rt), .in1(EX_rd), .out(multiplexer_21_out), .sel(RegDst));
  Multiplexer #(.width(5), .enable("false")) multiplexer_22 (
    .in0(MEM_rt), .in1(MEM_rd), .out(multiplexer_22_out), .sel(MEM_RegDst));
  Multiplexer #(.width(5), .enable("false")) multiplexer_23 (
    .in0(multiplexer_21_out), .in1({5{1'b1}}), .out(EX_WriteReg), .sel(JAL));
  Multiplexer #(.width(5), .enable("false")) multiplexer_24 (
    .in0(multiplexer_22_out), .in1({5{1'b1}}), .out(MEM_WriteReg), .sel(MEM_JAL));

  // Notes on the sheet:
  //   中断源
  //   中断等待指示
  //   指令存储器
  //   contents of rom_1 (hex, n*v repeats v):
  //   20080001 20090003 20110876 118d00 112020 20020022 c 200b0008 1118806 1318806 112020 20020022 c
  //   216bffff 1560fff9 2002000a c
  //   数码管输出
  //   指令字
  //   OP
  //   Func
  //   rs
  //   rt
  //   rd
  //   Beq
  //   JMP
  //   JR
  //   Bne
  //   OP
  //   JAL
  //   Func
  //   Syscall
  //   MemToReg
  //   MemWrite
  //   AluOP
  //   AluSrcB
  //   RegWrite
  //   RegDst
  //   流水调试日志用
  //   rt
  //   rd
  //   rt
  //   rd
endmodule

// rs
module \重定向流水线  (
  input  in_1
);

  wire and_1_out, and_2_out, and_3_out, and_4_out, and_5_out, and_6_out, and_7_out, and_8_out, and_9_out,
       and_10_out, CLK, comparator_1_eq, comparator_2_eq, compare, en, EX_BLEZ, EX_JMP, EX_RegDst,
       EX_RegWrite, EX_SH, EX_SRLV, EX_Syscall, Go, ID_BLEZ, ID_SH, ID_SRLV, ID_XORI, IR1, IR2, IR3, JAL, JR,
       LOCK, MEM_JAL, Mem_MemWrite, MEM_RegDst, MEM_RegWrite, MEM_SH, mips_alu_1_equal, multiplexer_26_out,
       nop, or_1_out, or_2_out, RST, SignedExt, W1, W2, W3, WB_JAL, WB_RegDst, WB_RegWrite, WB_Syscall,
       \数据相关 ;
  wire [1:0] Forward_A, Forward_B;
  wire [3:0] multiplexer_29_out, multiplexer_30_out;
  wire [4:0] ex_mem_1_wreg_, EX_rd, EX_rs, EX_rt, EX_WriteReg, id_ex_1_shamt_, id_ex_1_wreg_, ID_R1_num,
       ID_R2_num, MEM_rd, MEM_rt, mem_wb_1_wreg_, MEM_WriteReg, multiplexer_7_out, multiplexer_9_out,
       multiplexer_11_out, multiplexer_13_out, multiplexer_19_out, multiplexer_20_out, multiplexer_21_out,
       multiplexer_22_out, WB_rd, WB_rt, WB_WriteReg;
  wire [5:0] EX_Func, EX_OP, Func, OP;
  wire [10:0] id_ex_1_cont_, mem_wb_1_cont_;
  wire [10:6] id_ex_1_ir_;
  wire [13:0] ex_mem_1_cont_;
  wire [14:0] \硬布线控制器_1_beq ;
  wire [15:0] \LoadUse次数 , \总周期数 , \无条件分支数 , \条件分支成功数 ;
  wire [25:0] id_ex_1_imm26_;
  wire [25:6] if_id_1_instru_;
  wire [31:0] adder_1_out, adder_2_out, adder_3_out, ALUOUT, bit_extender_1_out, bit_extender_2_out,
       ex_mem_1_ir_, ex_mem_1_rd1_, ex_mem_1_rd2_, EX_PC, EXR1, id_ex_1_imm_, id_ex_1_imme_, id_ex_1_pc_4_,
       id_ex_1_rd1_, id_ex_1_rd2_, ID_PC, if_id_1_pc_4_, IF_PC, LedData, Mem_ALU_Result, MEM_PC,
       mem_wb_1_ir_, mips_probe_1_p1, mips_ram_1_p7, multiplexer_2_out, multiplexer_3_out, multiplexer_4_out,
       multiplexer_10_out, multiplexer_12_out, multiplexer_14_out, multiplexer_16_out, multiplexer_17_out,
       multiplexer_18_out, multiplexer_27_out, multiplexer_28_out, R1, R2, shifter_1_out, undriven,
       WB_ALU_Result, WB_Mem_ReadData, WB_PC, WB_RegDin, WBR1, WBR2;

  Button \u_总复位  (.out(RST));
  Button _1 (.out(IR1));
  Button _2 (.out(IR2));
  Button _3 (.out(IR3));
  and and_1 (and_1_out, en, ~\数据相关 );  // AND_Gate
  Button \u_继续运行  (.out(Go));
  LED led_1 (.in(W1));
  LED led_2 (.in(W2));
  LED led_3 (.in(W3));
  Register #(.width(32)) PC (.D(multiplexer_2_out), .en(and_1_out), .Q(IF_PC), .clk(CLK), .clr(RST));
  Multiplexer #(.enable("false")) multiplexer_1 (.in0(1'b1), .in1(1'b0), .out(en), .sel(and_2_out));
  and and_2 (and_2_out, LOCK, ~Go);  // AND_Gate
  Counter #(.width(16), .max('hffff)) counter_1 (.count(en), .Q(\总周期数 ), .clk(CLK), .clr(RST));  // open: load, D, carry
  Multiplexer #(.width(32), .enable("false")) multiplexer_2 (
    .in0(multiplexer_4_out), .in1(multiplexer_3_out), .out(multiplexer_2_out), .sel(EX_JMP));
  Multiplexer #(.width(32), .enable("false")) multiplexer_3 (
    .in0({4'b0000, id_ex_1_imm26_, 2'b00}), .in1(EXR1), .out(multiplexer_3_out), .sel(JR));
  Hex_Digit_Display hex_digit_display_1 (.value(LedData[31:28]));  // open: dp
  and and_3 (and_3_out, ~LOCK, EX_JMP);  // AND_Gate
  and and_4 (and_4_out, ~LOCK, compare);  // AND_Gate
  Counter #(.width(16), .max('hffff)) counter_2 (
    .count(and_5_out), .Q(\LoadUse次数 ), .clk(CLK), .clr(RST));  // open: load, D, carry
  and and_5 (and_5_out, ~LOCK, \数据相关 );  // AND_Gate
  Hex_Digit_Display hex_digit_display_2 (.value(LedData[23:20]));  // open: dp
  Hex_Digit_Display hex_digit_display_3 (.value(LedData[27:24]));  // open: dp
  Counter #(.width(16), .max('hffff)) counter_3 (
    .count(and_3_out), .Q(\无条件分支数 ), .clk(CLK), .clr(RST));  // open: load, D, carry
  Counter #(.width(16), .max('hffff)) counter_4 (
    .count(and_4_out), .Q(\条件分支成功数 ), .clk(CLK), .clr(RST));  // open: load, D, carry
  // Mips_Probe mips_probe_1: pin names not known; wires that end beside it: mips_probe_1_p1
  ROM #(.addrWidth(10), .dataWidth(32)) rom_1 (.addr(IF_PC[11:2]), .data(mips_probe_1_p1));  // open: sel
  Multiplexer #(.width(32), .enable("false")) multiplexer_4 (
    .in0(adder_1_out), .in1(adder_3_out), .out(multiplexer_4_out), .sel(compare));
  Hex_Digit_Display hex_digit_display_4 (.value(LedData[19:16]));  // open: dp
  Hex_Digit_Display hex_digit_display_5 (.value(LedData[15:12]));  // open: dp
  and and_6 (and_6_out, en, ~\数据相关 );  // AND_Gate
  Adder #(.width(32)) adder_1 (.a(IF_PC), .b(32'h4), .out(adder_1_out));  // open: cin, cout
  Hex_Digit_Display hex_digit_display_6 (.value(LedData[11:8]));  // open: dp
  Hex_Digit_Display hex_digit_display_7 (.value(LedData[7:4]));  // open: dp
  Clock clock_1 (.out(CLK));
  IF_ID if_id_1 (
    .instru(mips_probe_1_p1), .PC_4(adder_1_out), .clk(CLK), .rst(RST),
    .instru_({OP, if_id_1_instru_, Func}), .PC_4_(if_id_1_pc_4_), .PC(IF_PC), .PC_(ID_PC), .en(and_6_out),
    .halt(nop));  // open: 预测跳转, 预测地址, Hit, HitPos, 预测跳转_, 预测地址_, Hit_, HitPos_
  Hex_Digit_Display hex_digit_display_8 (.value(LedData[3:0]));  // open: dp
  // Probe on {OP, if_id_1_instru_, Func}
  Comparator #(.width(32)) comparator_1 (.a(WBR1), .b(32'h22), .eq(comparator_1_eq));  // open: gt, lt
  \硬布线控制器  \u_硬布线控制器_1  (
    .Func(Func), .OP(OP), .ALU_OP(\硬布线控制器_1_beq [9:6]), .MemToReg(\硬布线控制器_1_beq [4]),
    .MemWrite(\硬布线控制器_1_beq [5]), .ALU_SRC(\硬布线控制器_1_beq [10]), .RegWrite(\硬布线控制器_1_beq [14]),
    .SysCALL(\硬布线控制器_1_beq [13]), .SignedExt(SignedExt), .RegDst(\硬布线控制器_1_beq [12]), .JR(\硬布线控制器_1_beq [2]),
    .JMP(\硬布线控制器_1_beq [3]), .Beq(\硬布线控制器_1_beq [0]), .JAL(\硬布线控制器_1_beq [11]), .Bne(\硬布线控制器_1_beq [1]),
    .SRLV(ID_SRLV), .XORI(ID_XORI), .SH(ID_SH), .BLEZ(ID_BLEZ));  // open: ERET, RS, RD, MFC_0, MTC_0
  Multiplexer #(.width(5), .enable("false")) multiplexer_5 (
    .in0(if_id_1_instru_[25:21]), .in1(5'b00010), .out(ID_R1_num), .sel(\硬布线控制器_1_beq [13]));
  Multiplexer #(.width(5), .enable("false")) multiplexer_6 (
    .in0(if_id_1_instru_[20:16]), .in1(5'b00100), .out(ID_R2_num), .sel(\硬布线控制器_1_beq [13]));
  // Probe on \总周期数 
  // Probe on \无条件分支数 
  // Probe on \条件分支成功数 
  // Probe on \LoadUse次数 
  // Probe on \LoadUse次数 
  Multiplexer #(.width(5), .enable("false")) multiplexer_7 (
    .in0(if_id_1_instru_[20:16]), .in1(if_id_1_instru_[15:11]), .out(multiplexer_7_out),
    .sel(\硬布线控制器_1_beq [12]));
  // Probe on WB_RegDin
  and and_7 (and_7_out, comparator_1_eq, WB_Syscall);
  and and_8 (and_8_out, ~comparator_1_eq, WB_Syscall);  // AND_Gate
  Multiplexer #(.enable("false")) multiplexer_8 (.in0(and_8_out), .in1(comparator_2_eq), .out(LOCK), .sel(in_1));
  Comparator #(.width(32), .mode("unsigned")) comparator_2 (
    .a(EX_PC), .b(32'h3064), .eq(comparator_2_eq));  // open: gt, lt
  // Probe on IF_PC[11:0]
  // Probe on ID_R1_num
  // Probe on ID_R2_num
  Multiplexer #(.width(5), .enable("false")) multiplexer_9 (
    .in0(multiplexer_7_out), .in1({5{1'b1}}), .out(multiplexer_9_out), .sel(\硬布线控制器_1_beq [11]));
  Adder #(.width(32)) adder_2 (.a(WB_PC), .b(32'h4), .out(adder_2_out));  // open: cin, cout
  Multiplexer #(.width(32)) multiplexer_10 (
    .in0(undriven), .in1(WBR2), .out(multiplexer_10_out), .sel(and_7_out), .en(and_7_out));
  Register #(.width(32)) register_1 (.D(multiplexer_10_out), .Q(LedData), .clk(CLK), .clr(RST));  // open: en
  Multiplexer #(.width(5), .enable("false")) multiplexer_11 (
    .in0(EX_rs), .in1(5'b00010), .out(multiplexer_11_out), .sel(EX_Syscall));
  // Probe on ID_PC[11:0]
  Multiplexer #(.width(32), .enable("false")) multiplexer_12 (
    .in0(WB_RegDin), .in1(adder_2_out), .out(multiplexer_12_out), .sel(WB_JAL));
  // Probe on mem_wb_1_wreg_
  Multiplexer #(.width(5), .enable("false")) multiplexer_13 (
    .in0(EX_rt), .in1(5'b00100), .out(multiplexer_13_out), .sel(EX_Syscall));
  // Probe on EX_PC[11:0]
  // Probe on MEM_PC[11:0]
  MIPS_Regifile mips_regifile_1 (
    .Din(multiplexer_12_out), .Clk(CLK), .R1(R1), .R2(R2), .WE(WB_RegWrite), .W_num(mem_wb_1_wreg_),
    .R1_num(ID_R1_num), .R2_num(ID_R2_num));
  assign bit_extender_1_out = {{16{1'b0}}, {if_id_1_instru_[15:6], Func}};  // Bit_Extender bit_extender_1
  assign bit_extender_2_out = {{16{if_id_1_instru_[15]}}, {if_id_1_instru_[15:6], Func}};  // Bit_Extender bit_extender_2
  // Probe on WB_PC[11:0]
  // Probe on R1
  // Probe on R2
  Multiplexer #(.width(32), .enable("false")) multiplexer_14 (
    .in0(bit_extender_1_out), .in1(bit_extender_2_out), .out(multiplexer_14_out), .sel(SignedExt));
  ID_EX id_ex_1 (
    .RD1(R1), .RD2(R2), .imm(bit_extender_2_out), .PC_4(if_id_1_pc_4_), .clk(CLK), .halt(or_1_out),
    .RD1_(id_ex_1_rd1_), .RD2_(id_ex_1_rd2_), .imm_(id_ex_1_imm_), .PC_4_(id_ex_1_pc_4_),
    .WReg(multiplexer_9_out), .WReg_(id_ex_1_wreg_), .immE(multiplexer_14_out), .immE_(id_ex_1_imme_),
    .cont(\硬布线控制器_1_beq ),
    .cont_({EX_RegWrite, EX_Syscall, EX_RegDst, JAL, id_ex_1_cont_[10:4], EX_JMP, JR, id_ex_1_cont_[1:0]}),
    .shamt(if_id_1_instru_[10:6]), .shamt_(id_ex_1_shamt_), .PC(ID_PC), .PC_(EX_PC), .en(en),
    .imm26({if_id_1_instru_, Func}), .imm26_(id_ex_1_imm26_), .IR({OP, if_id_1_instru_, Func}),
    .IR_({EX_OP, EX_rs, EX_rt, EX_rd, id_ex_1_ir_, EX_Func}), .SRLV(ID_SRLV), .SRLV_(EX_SRLV), .SH(ID_SH),
    .SH_(EX_SH), .BLEZ(ID_BLEZ), .BLEZ_(EX_BLEZ), .rst(RST));  // open: ERET, ERET_, 预测跳转, 预测跳转_, 预测地址, 预测地址_, Hit, Hit_, HitPos, HitPos_
  \数据相关检测  \u_数据相关检测_1  (
    .ID_OP(OP), .EX_WriteReg_num(EX_WriteReg), .EX_RegWrite(EX_RegWrite), .MEM_WriteReg_num(MEM_WriteReg),
    .MEM_RegWrite(MEM_RegWrite), .ID_FUNC(Func), .ID_R1_num(ID_R1_num), .ID_R2_num(ID_R2_num), .EX_OP(EX_OP),
    .\Load_Use相关 (\数据相关 ), .WB_WriteReg_num(WB_WriteReg), .WB_RegWrite(WB_RegWrite), .Forward1(Forward_A),
    .Forward2(Forward_B), .EX_R1_num(multiplexer_11_out), .EX_R2_num(multiplexer_13_out), .EX_FUNC(EX_Func));  // open: 数据相关, MEM相关, EX相关
  // Probe on Forward_A
  // Probe on EX_PC
  Multiplexer #(.select(2), .width(32), .enable("false")) multiplexer_15 (
    .in0(id_ex_1_rd1_), .in1(Mem_ALU_Result), .in2(WB_RegDin), .out(EXR1), .sel(Forward_A));  // open: in3
  Multiplexer #(.select(2), .width(32), .enable("false")) multiplexer_16 (
    .in0(id_ex_1_rd2_), .in1(Mem_ALU_Result), .in2(WB_RegDin), .out(multiplexer_16_out), .sel(Forward_B));  // open: in3
  // Probe on EXR1
  Multiplexer #(.width(32), .enable("false")) multiplexer_17 (
    .in0(multiplexer_16_out), .in1(id_ex_1_imme_), .out(multiplexer_17_out), .sel(id_ex_1_cont_[10]));
  or or_1 (or_1_out, nop, \数据相关 );
  Multiplexer #(.width(32), .enable("false")) multiplexer_18 (
    .in0(multiplexer_17_out), .in1({32{1'b0}}), .out(multiplexer_18_out), .sel(EX_BLEZ));
  Shifter #(.width(32)) shifter_1 (.in(id_ex_1_imm_), .\dist (5'b00010), .out(shifter_1_out));
  Multiplexer #(.width(5), .enable("false")) multiplexer_19 (
    .in0(EX_rt), .in1(EX_rd), .out(multiplexer_19_out), .sel(EX_RegDst));
  Multiplexer #(.width(5), .enable("false")) multiplexer_20 (
    .in0(MEM_rt), .in1(MEM_rd), .out(multiplexer_20_out), .sel(MEM_RegDst));
  Multiplexer #(.width(5), .enable("false")) multiplexer_21 (
    .in0(WB_rt), .in1(WB_rd), .out(multiplexer_21_out), .sel(WB_RegDst));
  MIPS_ALU mips_alu_1 (
    .X(EXR1), .Y(multiplexer_18_out), .AluOP(id_ex_1_cont_[9:6]), .Equal(mips_alu_1_equal), .Result(ALUOUT),
    .shamt(multiplexer_22_out));  // open: Result_2
  Multiplexer #(.width(5), .enable("false")) multiplexer_22 (
    .in0(id_ex_1_shamt_), .in1(EXR1[4:0]), .out(multiplexer_22_out), .sel(EX_SRLV));
  Adder #(.width(32)) adder_3 (.a(shifter_1_out), .b(id_ex_1_pc_4_), .out(adder_3_out));  // open: cin, cout
  Multiplexer #(.width(5), .enable("false")) multiplexer_23 (
    .in0(multiplexer_19_out), .in1({5{1'b1}}), .out(EX_WriteReg), .sel(JAL));
  Multiplexer #(.width(5), .enable("false")) multiplexer_24 (
    .in0(multiplexer_20_out), .in1({5{1'b1}}), .out(MEM_WriteReg), .sel(MEM_JAL));
  Multiplexer #(.width(5), .enable("false")) multiplexer_25 (
    .in0(multiplexer_21_out), .in1({5{1'b1}}), .out(WB_WriteReg), .sel(WB_JAL));
  and and_9 (and_9_out, id_ex_1_cont_[0], mips_alu_1_equal);
  and and_10 (and_10_out, ~mips_alu_1_equal, id_ex_1_cont_[1]);  // AND_Gate
  or or_2 (or_2_out, mips_alu_1_equal, ALUOUT[0]);
  // Probe on EXR1
  // Probe on ALUOUT
  // Probe on multiplexer_16_out
  Multiplexer #(.enable("false")) multiplexer_26 (.in0(1'b0), .in1(or_2_out), .out(multiplexer_26_out), .sel(EX_BLEZ));
  EX_MEM ex_mem_1 (
    .cont({EX_RegWrite, EX_Syscall, EX_RegDst, JAL, id_ex_1_cont_[10:4], EX_JMP, JR, id_ex_1_cont_[1:0]}),
    .ALUout(ALUOUT), .RD2(multiplexer_16_out), .WReg(id_ex_1_wreg_), .clk(CLK), .halt(RST),
    .cont_({MEM_RegWrite, ex_mem_1_cont_[13], MEM_RegDst, MEM_JAL, ex_mem_1_cont_[10:6], Mem_MemWrite, ex_mem_1_cont_[4:0]}),
    .ALUout_(Mem_ALU_Result), .RD2_(ex_mem_1_rd2_), .WReg_(ex_mem_1_wreg_), .RD1(EXR1), .RD1_(ex_mem_1_rd1_),
    .PC(EX_PC), .PC_(MEM_PC), .en(en), .IR({EX_OP, EX_rs, EX_rt, EX_rd, id_ex_1_ir_, EX_Func}),
    .IR_({ex_mem_1_ir_[31:21], MEM_rt, MEM_rd, ex_mem_1_ir_[10:0]}), .LH(EX_SH), .LH_(MEM_SH), .rst(RST));
  or or_3 (compare, and_9_out, and_10_out, multiplexer_26_out);
  or or_4 (nop, compare, JR, EX_JMP);
  // Probe on Mem_ALU_Result
  // Probe on ex_mem_1_rd1_
  Multiplexer #(.width(32), .enable("false")) multiplexer_27 (
    .in0({{16{1'b0}}, ex_mem_1_rd2_[15:0]}), .in1({ex_mem_1_rd2_[15:0], {16{1'b0}}}),
    .out(multiplexer_27_out), .sel(Mem_ALU_Result[1]));
  Multiplexer #(.width(32), .enable("false")) multiplexer_28 (
    .in0(ex_mem_1_rd2_), .in1(multiplexer_27_out), .out(multiplexer_28_out), .sel(MEM_SH));
  Multiplexer #(.width(4), .enable("false")) multiplexer_29 (
    .in0(4'b1111), .in1(multiplexer_30_out), .out(multiplexer_29_out), .sel(MEM_SH));
  Multiplexer #(.width(4), .enable("false")) multiplexer_30 (
    .in0(4'b0011), .in1(4'b1100), .out(multiplexer_30_out), .sel(Mem_ALU_Result[1]));
  // MIPS_RAM mips_ram_1: pin names not known; wires that end beside it: Mem_ALU_Result[21:2], multiplexer_28_out, Mem_MemWrite, multiplexer_29_out, CLK, RST, mips_ram_1_p7
  MEM_WB mem_wb_1 (
    .cont({MEM_RegWrite, ex_mem_1_cont_[13], MEM_RegDst, MEM_JAL, ex_mem_1_cont_[10:6], Mem_MemWrite, ex_mem_1_cont_[4:0]}),
    .ALUout(Mem_ALU_Result), .MEMout(mips_ram_1_p7), .WReg(ex_mem_1_wreg_), .clk(CLK), .halt(RST),
    .cont_({WB_RegWrite, WB_Syscall, WB_RegDst, WB_JAL, mem_wb_1_cont_}), .ALUout_(WB_ALU_Result),
    .MEMout_(WB_Mem_ReadData), .WReg_(mem_wb_1_wreg_), .RD1(ex_mem_1_rd1_), .RD1_(WBR1), .RD2(ex_mem_1_rd2_),
    .RD2_(WBR2), .PC(MEM_PC), .PC_(WB_PC), .en(en),
    .IR({ex_mem_1_ir_[31:21], MEM_rt, MEM_rd, ex_mem_1_ir_[10:0]}),
    .IR_({mem_wb_1_ir_[31:21], WB_rt, WB_rd, mem_wb_1_ir_[10:0]}), .rst(RST));
  Multiplexer #(.width(32), .enable("false")) multiplexer_31 (
    .in0(WB_ALU_Result), .in1(WB_Mem_ReadData), .out(WB_RegDin), .sel(mem_wb_1_cont_[4]));
  // Probe on WBR1
  // Probe on WBR2

  // Other names for the same wires on the sheet: CHANGE = in_1; SW_sel = Mem_ALU_Result[1]; 插入气泡数[15:0] = \LoadUse次数 

  // Notes on the sheet:
  //   中断源
  //   中断等待指示
  //   指令存储器
  //   contents of rom_1 (hex, n*v repeats v):
  //   20080001 20090003 20110876 118d00 112020 20020022 c 200b0008 1118806 1318806 112020 20020022 c
  //   216bffff 1560fff9 2002000a c
  //   数码管输出
  //   指令字
  //   OP
  //   Func
  //   rs
  //   rt
  //   rd
  //   Beq
  //   JMP
  //   JR
  //   Bne
  //   OP
  //   JAL
  //   Func
  //   Syscall
  //   MemToReg
  //   MemWrite
  //   AluOP
  //   AluSrcB
  //   RegWrite
  //   RegDst
  //   rs
  //   rt
  //   流水调试日志用
  //   rs
  //   rt
  //   rd
  //   rt
  //   rd
  //   rt
  //   rd
endmodule

module MAX_3 (
  input  [31:0] Y,
  input  [31:0] X,
  input  [2:0] Y_num,
  input  [2:0] X_num,
  output [31:0] MAX,
  output [2:0] Max_num
);

  wire comparator_1_eq, comparator_1_gt, or_1_out;

  Multiplexer #(.width(32), .enable("false")) multiplexer_1 (.in0(Y), .in1(X), .out(MAX), .sel(or_1_out));
  Comparator #(.width(32), .mode("unsigned")) comparator_1 (
    .a(X), .b(Y), .gt(comparator_1_gt), .eq(comparator_1_eq));  // open: lt
  or or_1 (or_1_out, comparator_1_gt, comparator_1_eq);
  Multiplexer #(.width(3), .enable("false")) multiplexer_2 (.in0(Y_num), .in1(X_num), .out(Max_num), .sel(or_1_out));

  // Notes on the sheet:
  //   输出两个输入中的较大值，并输出较大值的3位编号
endmodule

module \重定向流水线_Back  (
);

  wire and_1_out, and_2_out, and_3_out, and_4_out, and_5_out, and_7_out, and_8_out, and_9_out, and_10_out,
       CLK, comparator_1_eq, compare, en, EX_AluSrcB, EX_BLEZ, EX_JMP, EX_JR, EX_RegWrite, EX_SH, EX_SRLV,
       Go, ID_BLEZ, ID_SH, ID_SRLV, ID_XORI, IR1, IR2, IR3, JAL, \Load_Use相关 , LOCK, MEM_JAL, Mem_MemWrite,
       MEM_RegDst, MEM_RegWrite, MEM_SH, mips_alu_1_equal, multiplexer_16_out, nop, not_1_out, or_1_out,
       or_2_out, RegDst, RST, SignedExt, undriven_2, W1, W2, W3, WB_JAL, WB_RegDst, WBJAL, WBRegWrite,
       WBSyscall, \数据相关 ;
  wire [1:0] \数据相关检测_1_forward1 , \数据相关检测_1_forward2 ;
  wire [3:0] multiplexer_25_out, multiplexer_26_out;
  wire [4:0] ex_mem_1_wreg_, EX_rd, EX_rt, EX_WriteReg, id_ex_1_shamt_, id_ex_1_wreg_, ID_R1_num, ID_R2_num,
       MEM_rd, MEM_rt, mem_wb_1_wreg_, MEM_WriteReg, multiplexer_8_out, multiplexer_9_out,
       multiplexer_15_out, multiplexer_19_out, multiplexer_20_out, multiplexer_22_out, undriven_3,
       undriven_4, WB_rd, WB_RegWrite, WB_rt;
  wire [5:0] EX_OP, Func, OP;
  wire [12:0] mem_wb_1_cont_;
  wire [13:0] ex_mem_1_cont_, id_ex_1_cont_;
  wire [14:0] \硬布线控制器_1_beq ;
  wire [15:0] \LoadUse次数 , \总周期数 , \插入气泡数 , \无条件分支数 , \条件分支成功数 ;
  wire [25:0] id_ex_1_imm26_, id_ex_1_ir_;
  wire [25:6] if_id_1_instru_;
  wire [31:0] adder_1_out, adder_2_out, adder_3_out, ALUOUT, bit_extender_1_out, bit_extender_2_out,
       ex_mem_1_ir_, ex_mem_1_rd1_, ex_mem_1_rd2_, EX_PC, EXR1, id_ex_1_imm_, id_ex_1_imme_, id_ex_1_pc_4_,
       id_ex_1_rd2_, ID_PC, if_id_1_pc_4_, IF_PC, LedData, Mem_ALU_Result, MEM_PC, mem_wb_1_ir_,
       mips_ram_1_p7, mips_ram_1_p8, multiplexer_2_out, multiplexer_3_out, multiplexer_4_out,
       multiplexer_5_out, multiplexer_10_out, multiplexer_11_out, multiplexer_13_out, multiplexer_14_out,
       multiplexer_17_out, multiplexer_18_out, multiplexer_27_out, R1, R2, rom_1_data, shifter_1_out,
       undriven, WB_ALU_Result, WB_Mem_ReadData, WB_PC, WBR1, WBR2;

  Button \u_总复位  (.out(RST));
  Button _1 (.out(IR1));
  Button _2 (.out(IR2));
  Button _3 (.out(IR3));
  and and_1 (and_1_out, en, ~\数据相关 );  // AND_Gate
  Button \u_继续运行  (.out(Go));
  LED led_1 (.in(W1));
  LED led_2 (.in(W2));
  LED led_3 (.in(W3));
  Register #(.width(32)) PC (.D(multiplexer_2_out), .en(and_1_out), .Q(IF_PC), .clk(CLK), .clr(RST));
  Multiplexer #(.enable("false")) multiplexer_1 (.in0(1'b1), .in1(1'b0), .out(en), .sel(and_2_out));
  and and_2 (and_2_out, LOCK, ~Go);  // AND_Gate
  Counter #(.width(16), .max('hffff)) counter_1 (.count(en), .Q(\总周期数 ), .clk(CLK), .clr(RST));  // open: load, D, carry
  Multiplexer #(.width(32), .enable("false")) multiplexer_2 (
    .in0(multiplexer_4_out), .in1(multiplexer_3_out), .out(multiplexer_2_out), .sel(EX_JMP));
  Multiplexer #(.width(32), .enable("false")) multiplexer_3 (
    .in0({4'b0000, id_ex_1_imm26_, 2'b00}), .in1(EXR1), .out(multiplexer_3_out), .sel(EX_JR));
  Comparator #(.width(32)) comparator_1 (.a(WBR1), .b(32'h22), .eq(comparator_1_eq));  // open: gt, lt
  Hex_Digit_Display hex_digit_display_1 (.value(LedData[31:28]));  // open: dp
  and and_3 (and_3_out, ~LOCK, EX_JMP);  // AND_Gate
  and and_4 (and_4_out, ~LOCK, compare);  // AND_Gate
  Hex_Digit_Display hex_digit_display_2 (.value(LedData[27:24]));  // open: dp
  Hex_Digit_Display hex_digit_display_3 (.value(LedData[23:20]));  // open: dp
  Counter #(.width(16), .max('hffff)) counter_2 (
    .count(and_3_out), .Q(\无条件分支数 ), .clk(CLK), .clr(RST));  // open: load, D, carry
  Counter #(.width(16), .max('hffff)) counter_3 (
    .count(and_4_out), .Q(\条件分支成功数 ), .clk(CLK), .clr(RST));  // open: load, D, carry
  ROM #(.addrWidth(10), .dataWidth(32)) rom_1 (.addr(IF_PC[11:2]), .data(rom_1_data));  // open: sel
  Multiplexer #(.width(32), .enable("false")) multiplexer_4 (
    .in0(adder_1_out), .in1(adder_3_out), .out(multiplexer_4_out), .sel(compare));
  and and_5 (and_5_out, comparator_1_eq, WBSyscall);
  and and_6 (LOCK, ~comparator_1_eq, WBSyscall);  // AND_Gate
  Hex_Digit_Display hex_digit_display_4 (.value(LedData[19:16]));  // open: dp
  Hex_Digit_Display hex_digit_display_5 (.value(LedData[15:12]));  // open: dp
  and and_7 (and_7_out, en, ~\数据相关 );  // AND_Gate
  Adder #(.width(32)) adder_1 (.a(IF_PC), .b(32'h4), .out(adder_1_out));  // open: cin, cout
  Multiplexer #(.width(32)) multiplexer_5 (
    .in0(undriven), .in1(WBR2), .out(multiplexer_5_out), .sel(and_5_out), .en(and_5_out));
  Hex_Digit_Display hex_digit_display_6 (.value(LedData[7:4]));  // open: dp
  Hex_Digit_Display hex_digit_display_7 (.value(LedData[11:8]));  // open: dp
  Clock clock_1 (.out(CLK));
  IF_ID if_id_1 (
    .instru(rom_1_data), .PC_4(adder_1_out), .clk(CLK), .rst(RST), .instru_({OP, if_id_1_instru_, Func}),
    .PC_4_(if_id_1_pc_4_), .PC(IF_PC), .PC_(ID_PC), .en(and_7_out), .halt(nop));  // open: 预测跳转, 预测地址, Hit, HitPos, 预测跳转_, 预测地址_, Hit_, HitPos_
  Register #(.width(32)) register_1 (.D(multiplexer_5_out), .Q(LedData), .clk(CLK), .clr(RST));  // open: en
  Hex_Digit_Display hex_digit_display_8 (.value(LedData[3:0]));  // open: dp
  // Probe on {OP, if_id_1_instru_, Func}
  \硬布线控制器  \u_硬布线控制器_1  (
    .Func(Func), .OP(OP), .ALU_OP(\硬布线控制器_1_beq [9:6]), .MemToReg(\硬布线控制器_1_beq [4]),
    .MemWrite(\硬布线控制器_1_beq [5]), .ALU_SRC(\硬布线控制器_1_beq [10]), .RegWrite(\硬布线控制器_1_beq [14]),
    .SysCALL(\硬布线控制器_1_beq [13]), .SignedExt(SignedExt), .RegDst(\硬布线控制器_1_beq [12]), .JR(\硬布线控制器_1_beq [2]),
    .JMP(\硬布线控制器_1_beq [3]), .Beq(\硬布线控制器_1_beq [0]), .JAL(\硬布线控制器_1_beq [11]), .Bne(\硬布线控制器_1_beq [1]),
    .SRLV(ID_SRLV), .XORI(ID_XORI), .SH(ID_SH), .BLEZ(ID_BLEZ));  // open: ERET, RS, RD, MFC_0, MTC_0
  Multiplexer #(.width(5), .enable("false")) multiplexer_6 (
    .in0(if_id_1_instru_[25:21]), .in1(5'b00010), .out(ID_R1_num), .sel(\硬布线控制器_1_beq [13]));
  Multiplexer #(.width(5), .enable("false")) multiplexer_7 (
    .in0(if_id_1_instru_[20:16]), .in1(5'b00100), .out(ID_R2_num), .sel(\硬布线控制器_1_beq [13]));
  and and_8 (and_8_out, ~LOCK, \数据相关 );  // AND_Gate
  // Probe on \总周期数 
  // Probe on \无条件分支数 
  // Probe on \条件分支成功数 
  // Probe on \插入气泡数 
  // Probe on \LoadUse次数 
  Multiplexer #(.width(5), .enable("false")) multiplexer_8 (
    .in0(if_id_1_instru_[20:16]), .in1(if_id_1_instru_[15:11]), .out(multiplexer_8_out),
    .sel(\硬布线控制器_1_beq [12]));
  // Probe on multiplexer_27_out
  Counter #(.width(16), .max('hffff)) counter_4 (
    .count(and_8_out), .Q(\插入气泡数 ), .clk(CLK), .clr(RST));  // open: load, D, carry
  // Probe on IF_PC[11:0]
  // Probe on ID_R1_num
  // Probe on ID_R2_num
  Multiplexer #(.width(5), .enable("false")) multiplexer_9 (
    .in0(multiplexer_8_out), .in1({5{1'b1}}), .out(multiplexer_9_out), .sel(\硬布线控制器_1_beq [11]));
  Adder #(.width(32)) adder_2 (.a(WB_PC), .b(32'h4), .out(adder_2_out));  // open: cin, cout
  // Probe on ID_PC[11:0]
  Multiplexer #(.width(32), .enable("false")) multiplexer_10 (
    .in0(multiplexer_27_out), .in1(adder_2_out), .out(multiplexer_10_out), .sel(WBJAL));
  // Probe on mem_wb_1_wreg_
  // Probe on MEM_PC[11:0]
  // Probe on EX_PC[11:0]
  MIPS_Regifile mips_regifile_1 (
    .Din(multiplexer_10_out), .Clk(CLK), .R1(R1), .R2(R2), .WE(WBRegWrite), .W_num(mem_wb_1_wreg_),
    .R1_num(ID_R1_num), .R2_num(ID_R2_num));
  assign bit_extender_1_out = {{16{1'b0}}, {if_id_1_instru_[15:6], Func}};  // Bit_Extender bit_extender_1
  assign bit_extender_2_out = {{16{if_id_1_instru_[15]}}, {if_id_1_instru_[15:6], Func}};  // Bit_Extender bit_extender_2
  // Probe on WB_PC[11:0]
  // Probe on R1
  // Probe on R2
  Multiplexer #(.width(32), .enable("false")) multiplexer_11 (
    .in0(bit_extender_1_out), .in1(bit_extender_2_out), .out(multiplexer_11_out), .sel(SignedExt));
  ID_EX id_ex_1 (
    .RD1(R1), .RD2(R2), .imm(bit_extender_2_out), .PC_4(if_id_1_pc_4_), .clk(CLK), .halt(or_1_out),
    .RD1_(EXR1), .RD2_(id_ex_1_rd2_), .imm_(id_ex_1_imm_), .PC_4_(id_ex_1_pc_4_), .WReg(multiplexer_9_out),
    .WReg_(id_ex_1_wreg_), .immE(multiplexer_11_out), .immE_(id_ex_1_imme_), .cont(\硬布线控制器_1_beq ),
    .cont_({EX_RegWrite, id_ex_1_cont_[13], RegDst, JAL, EX_AluSrcB, id_ex_1_cont_[9:4], EX_JMP, EX_JR, id_ex_1_cont_[1:0]}),
    .shamt(if_id_1_instru_[10:6]), .shamt_(id_ex_1_shamt_), .PC(ID_PC), .PC_(EX_PC), .en(en),
    .imm26({if_id_1_instru_, Func}), .imm26_(id_ex_1_imm26_), .IR({OP, if_id_1_instru_, Func}),
    .IR_({EX_OP, id_ex_1_ir_[25:21], EX_rt, EX_rd, id_ex_1_ir_[10:0]}), .SRLV(ID_SRLV), .SRLV_(EX_SRLV),
    .SH(ID_SH), .SH_(EX_SH), .BLEZ(ID_BLEZ), .BLEZ_(EX_BLEZ), .rst(RST));  // open: ERET, ERET_, 预测跳转, 预测跳转_, 预测地址, 预测地址_, Hit, Hit_, HitPos, HitPos_
  Multiplexer #(.select(2), .width(32), .enable("false")) multiplexer_12 (
    .in1(Mem_ALU_Result), .in2(WB_Mem_ReadData), .in3(WB_ALU_Result), .sel(2'b00));  // open: in0, out
  or or_1 (or_1_out, nop, \数据相关 );
  Multiplexer #(.width(32), .enable("false")) multiplexer_13 (
    .in0(id_ex_1_rd2_), .in1(id_ex_1_imme_), .out(multiplexer_13_out), .sel(EX_AluSrcB));
  Shifter #(.width(32)) shifter_1 (.in(id_ex_1_imm_), .\dist (5'b00010), .out(shifter_1_out));
  Multiplexer #(.width(32), .enable("false")) multiplexer_14 (
    .in0(multiplexer_13_out), .in1({32{1'b0}}), .out(multiplexer_14_out), .sel(EX_BLEZ));
  Multiplexer #(.width(5), .enable("false")) multiplexer_15 (
    .in0(id_ex_1_shamt_), .in1(EXR1[4:0]), .out(multiplexer_15_out), .sel(EX_SRLV));
  \数据相关检测  \u_数据相关检测_1  (
    .ID_OP(OP), .EX_WriteReg_num(EX_WriteReg), .EX_RegWrite(EX_RegWrite), .MEM_WriteReg_num(MEM_WriteReg),
    .MEM_RegWrite(MEM_RegWrite), .\数据相关 (\数据相关 ), .ID_FUNC(Func), .ID_R1_num(ID_R1_num),
    .ID_R2_num(ID_R2_num), .EX_OP(EX_OP), .\Load_Use相关 (\Load_Use相关 ), .WB_WriteReg_num(undriven_3),
    .WB_RegWrite(undriven_2), .Forward1(\数据相关检测_1_forward1 ), .Forward2(\数据相关检测_1_forward2 ),
    .EX_R1_num(undriven_4));  // open: MEM相关, EX相关, EX_R2_num, EX_FUNC
  and and_9 (and_9_out, id_ex_1_cont_[0], mips_alu_1_equal);
  and and_10 (and_10_out, ~mips_alu_1_equal, id_ex_1_cont_[1]);  // AND_Gate
  // Probe on EXR1
  MIPS_ALU mips_alu_1 (
    .X(EXR1), .Y(multiplexer_14_out), .AluOP(id_ex_1_cont_[9:6]), .Equal(mips_alu_1_equal), .Result(ALUOUT),
    .shamt(multiplexer_15_out));  // open: Result_2
  // Probe on ALUOUT
  // Probe on id_ex_1_rd2_
  Adder #(.width(32)) adder_3 (.a(shifter_1_out), .b(id_ex_1_pc_4_), .out(adder_3_out));  // open: cin, cout
  or or_2 (or_2_out, mips_alu_1_equal, ALUOUT[0]);
  not not_1 (not_1_out, or_2_out);
  EX_MEM ex_mem_1 (
    .cont({EX_RegWrite, id_ex_1_cont_[13], RegDst, JAL, EX_AluSrcB, id_ex_1_cont_[9:4], EX_JMP, EX_JR, id_ex_1_cont_[1:0]}),
    .ALUout(ALUOUT), .RD2(id_ex_1_rd2_), .WReg(id_ex_1_wreg_), .clk(CLK), .halt(RST),
    .cont_({MEM_RegWrite, ex_mem_1_cont_[13], MEM_RegDst, MEM_JAL, ex_mem_1_cont_[10:6], Mem_MemWrite, ex_mem_1_cont_[4:0]}),
    .ALUout_(Mem_ALU_Result), .RD2_(ex_mem_1_rd2_), .WReg_(ex_mem_1_wreg_), .RD1(EXR1), .RD1_(ex_mem_1_rd1_),
    .PC(EX_PC), .PC_(MEM_PC), .en(en), .IR({EX_OP, id_ex_1_ir_[25:21], EX_rt, EX_rd, id_ex_1_ir_[10:0]}),
    .IR_({ex_mem_1_ir_[31:21], MEM_rt, MEM_rd, ex_mem_1_ir_[10:0]}), .LH(EX_SH), .LH_(MEM_SH), .rst(RST));
  or or_3 (compare, and_9_out, and_10_out, multiplexer_16_out);
  Multiplexer #(.enable("false")) multiplexer_16 (.in0(1'b0), .in1(not_1_out), .out(multiplexer_16_out), .sel(EX_BLEZ));
  or or_4 (nop, compare, EX_JR, EX_JMP);
  // Probe on ex_mem_1_rd1_
  Multiplexer #(.width(32), .enable("false")) multiplexer_17 (
    .in0(ex_mem_1_rd2_), .in1(multiplexer_18_out), .out(multiplexer_17_out), .sel(MEM_SH));
  Multiplexer #(.width(32), .enable("false")) multiplexer_18 (
    .in0({{16{1'b0}}, ex_mem_1_rd2_[15:0]}), .in1({ex_mem_1_rd2_[15:0], {16{1'b0}}}),
    .out(multiplexer_18_out), .sel(Mem_ALU_Result[1]));
  Multiplexer #(.width(5), .enable("false")) multiplexer_19 (
    .in0(WB_rt), .in1(WB_rd), .out(multiplexer_19_out), .sel(WB_RegDst));
  Multiplexer #(.width(5), .enable("false")) multiplexer_20 (
    .in0(EX_rt), .in1(EX_rd), .out(multiplexer_20_out), .sel(RegDst));
  Multiplexer #(.width(5), .enable("false")) multiplexer_21 (
    .in0(multiplexer_20_out), .in1({5{1'b1}}), .out(EX_WriteReg), .sel(JAL));
  Multiplexer #(.width(5), .enable("false")) multiplexer_22 (
    .in0(MEM_rt), .in1(MEM_rd), .out(multiplexer_22_out), .sel(MEM_RegDst));
  Multiplexer #(.width(5), .enable("false")) multiplexer_23 (
    .in0(multiplexer_22_out), .in1({5{1'b1}}), .out(MEM_WriteReg), .sel(MEM_JAL));
  Multiplexer #(.width(5), .enable("false")) multiplexer_24 (
    .in0(multiplexer_19_out), .in1({5{1'b1}}), .out(WB_RegWrite), .sel(WB_JAL));
  Multiplexer #(.width(4), .enable("false")) multiplexer_25 (
    .in0(4'b1111), .in1(multiplexer_26_out), .out(multiplexer_25_out), .sel(MEM_SH));
  Multiplexer #(.width(4), .enable("false")) multiplexer_26 (
    .in0(4'b0011), .in1(4'b1100), .out(multiplexer_26_out), .sel(Mem_ALU_Result[1]));
  // MIPS_RAM mips_ram_1: pin names not known; wires that end beside it: Mem_ALU_Result[21:2], multiplexer_17_out, Mem_MemWrite, multiplexer_25_out, CLK, RST, mips_ram_1_p7, mips_ram_1_p8, WB_PC
  MEM_WB mem_wb_1 (
    .cont({MEM_RegWrite, ex_mem_1_cont_[13], MEM_RegDst, MEM_JAL, ex_mem_1_cont_[10:6], Mem_MemWrite, ex_mem_1_cont_[4:0]}),
    .ALUout(Mem_ALU_Result), .MEMout(mips_ram_1_p7), .WReg(ex_mem_1_wreg_), .clk(CLK), .halt(RST),
    .cont_({WBRegWrite, WBSyscall, mem_wb_1_cont_[12], WBJAL, mem_wb_1_cont_[10:0]}),
    .ALUout_(WB_ALU_Result), .MEMout_(WB_Mem_ReadData), .WReg_(mem_wb_1_wreg_), .RD1(ex_mem_1_rd1_),
    .RD1_(WBR1), .RD2(ex_mem_1_rd2_), .RD2_(WBR2), .PC(MEM_PC), .PC_(mips_ram_1_p8), .en(en),
    .IR({ex_mem_1_ir_[31:21], MEM_rt, MEM_rd, ex_mem_1_ir_[10:0]}),
    .IR_({mem_wb_1_ir_[31:21], WB_rt, WB_rd, mem_wb_1_ir_[10:0]}), .rst(RST));
  Multiplexer #(.width(32), .enable("false")) multiplexer_27 (
    .in0(WB_ALU_Result), .in1(WB_Mem_ReadData), .out(multiplexer_27_out), .sel(mem_wb_1_cont_[4]));
  // Probe on WBR1
  // Probe on WBR2

  // Other names for the same wires on the sheet: SW_sel = Mem_ALU_Result[1]

  // Notes on the sheet:
  //   中断源
  //   中断等待指示
  //   指令存储器
  //   contents of rom_1 (hex, n*v repeats v):
  //   20110001 8000c05 20110001 20120002 20130003 8000c09 20110001 20120002 20130003 8000c0d 20110001
  //   20120002 20130003 8000c11 20110001 20120002 20130003 c000cbb 20100001 20110001 118fc0 112020
  //   20020022 c 118882 12200001 8000c15 112020 20020022 c 20110001 118880 112020 20020022 c 12200001
  //   8000c1f 20110001 118fc0 112020 20020022 c 1188c3 112020 20020022 c 118903 112020 20020022 c 118903
  //   112020 20020022 c 118903 112020 20020022 c 118903 112020 20020022 c 118903 112020 20020022 c 118903
  //   112020 20020022 c 118903 112020 20020022 c 20100001 109fc0 139fc3 8021 2012000c 24160003 26100001
  //   3210000f 20080008 20090001 139900 2709825 132020 20020022 c 1094022 1500fff9 22100001 2018000f
  //   2188024 108700 20080008 20090001 139902 2709825 132021 20020022 c 1094022 1500fff9 108702 2c9b022
  //   12c00001 8000c50 4020 1084027 84400 3508ffff 82021 20020022 c 2010ffff 20110000 ae300000 22100001
  //   22310004 ae300000 22100001 22310004 ae300000 22100001 22310004 ae300000 22100001 22310004 ae300000
  //   22100001 22310004 ae300000 22100001 22310004 ae300000 22100001 22310004 ae300000 22100001 22310004
  //   ae300000 22100001 22310004 ae300000 22100001 22310004 ae300000 22100001 22310004 ae300000 22100001
  //   22310004 ae300000 22100001 22310004 ae300000 22100001 22310004 ae300000 22100001 22310004 ae300000
  //   22100001 22310004 22100001 8020 2011003c 8e130000 8e340000 274402a 11000002 ae330000 ae140000
  //   2231fffc 1611fff8 102020 20020022 c 22100004 2011003c 1611fff2 20020032 c 8000c00 2002000a c
  //   20100000 22100001 102020 20020022 c 22100002 102020 20020022 c 22100003 102020 20020022 c 22100004
  //   102020 20020022 c 22100005 102020 20020022 c 22100006 102020 20020022 c 22100007 102020 20020022 c
  //   22100008 102020 20020022 20020022 c 3e00008
  //   数码管输出
  //   指令字
  //   OP
  //   Func
  //   rs
  //   rt
  //   rd
  //   Beq
  //   JMP
  //   JR
  //   Bne
  //   OP
  //   JAL
  //   Func
  //   Syscall
  //   MemToReg
  //   MemWrite
  //   AluOP
  //   AluSrcB
  //   RegWrite
  //   RegDst
  //   流水调试日志用
  //   rt
  //   rd
  //   rt
  //   rd
  //   rt
  //   rd
endmodule

module SingleLevel_Interrupt (
  input  clk,
  input  ir1,
  input  [31:0] PC,
  input  ir2,
  input  ir3,
  input  ERET,
  input  [31:0] nextPC,
  output [31:0] PCout,
  output [1:0] out_9,
  output w1,
  output w2,
  output w3
);

  wire and_1_out, and_2_out, and_3_out, and_5_out, comparator_1_eq, d_ff_1_q, d_ff_2_q, d_ff_3_q, d_ff_4_q,
       d_ff_5_q, d_ff_6_q, IE, interrup_unen, multiplexer_1_out, nand_1_out, nand_2_out, nand_3_out,
       not_2_out, or_4_out, or_5_out, or_6_out, or_7_out, priority_encoder_1_gs, \中断状态 ;
  wire [1:0] priority_encoder_1_out;
  wire [31:0] EPC_q, multiplexer_2_out, multiplexer_3_out;

  or or_1 (w1, d_ff_4_q, d_ff_1_q);
  or or_2 (w2, d_ff_5_q, d_ff_2_q);
  or or_3 (w3, d_ff_6_q, d_ff_3_q);
  D_Flip_Flop d_ff_1 (.clk(ir1), .D(1'b1), .Q(d_ff_1_q), .reset(d_ff_4_q));  // open: Qn, preset, en
  D_Flip_Flop d_ff_2 (.clk(ir2), .D(1'b1), .Q(d_ff_2_q), .reset(d_ff_5_q));  // open: Qn, preset, en
  D_Flip_Flop d_ff_3 (.clk(ir3), .D(1'b1), .Q(d_ff_3_q), .reset(d_ff_6_q));  // open: Qn, preset, en
  or or_4 (or_4_out, d_ff_1_q, d_ff_4_q);
  or or_5 (or_5_out, d_ff_2_q, d_ff_5_q);
  or or_6 (or_6_out, d_ff_3_q, d_ff_6_q);
  and and_1 (and_1_out, or_4_out, nand_1_out);
  nand nand_1 (nand_1_out, ERET, out_9[0], ~out_9[1]);  // NAND_Gate
  and and_2 (and_2_out, or_5_out, nand_2_out);
  nand nand_2 (nand_2_out, ERET, ~out_9[0], out_9[1]);  // NAND_Gate
  and and_3 (and_3_out, or_6_out, nand_3_out);
  nand nand_3 (nand_3_out, ERET, out_9[0], out_9[1]);
  or or_7 (or_7_out, interrup_unen, \中断状态 );
  D_Flip_Flop d_ff_4 (.clk(clk), .D(and_1_out), .Q(d_ff_4_q));  // open: Qn, preset, en, reset
  D_Flip_Flop d_ff_5 (.clk(clk), .D(and_2_out), .Q(d_ff_5_q));  // open: Qn, preset, en, reset
  D_Flip_Flop d_ff_6 (.clk(clk), .D(and_3_out), .Q(d_ff_6_q));  // open: Qn, preset, en, reset
  Register #(.width(1)) \u_中断状态  (.D(or_7_out), .Q(\中断状态 ), .clk(clk), .clr(ERET));  // open: en
  not not_1 (IE, \中断状态 );
  Priority_Encoder #(.select(2)) priority_encoder_1 (
    .in0(1'b1), .in1(d_ff_4_q), .in2(d_ff_5_q), .in3(d_ff_6_q), .out(priority_encoder_1_out),
    .gs(priority_encoder_1_gs));  // open: en_out, en_in
  Register #(.width(32)) EPC (.D(PC), .en(interrup_unen), .Q(EPC_q), .clk(clk));  // open: clr
  // Probe on priority_encoder_1_out
  Multiplexer #(.select(2), .enable("false")) multiplexer_1 (
    .in0(1'b0), .in1(priority_encoder_1_gs), .in2(priority_encoder_1_gs), .in3(priority_encoder_1_gs),
    .out(multiplexer_1_out), .sel(priority_encoder_1_out));
  // Probe on EPC_q
  Multiplexer #(.width(32), .enable("false")) multiplexer_2 (
    .in0(nextPC), .in1(multiplexer_3_out), .out(multiplexer_2_out), .sel(interrup_unen));
  Multiplexer #(.select(2), .width(32), .enable("false")) multiplexer_3 (
    .in0(nextPC), .in1(32'h4), .in2(32'h1c8), .in3(32'h38c), .out(multiplexer_3_out),
    .sel(priority_encoder_1_out));
  and and_4 (interrup_unen, multiplexer_1_out, IE);
  // Probe on PCout
  Multiplexer #(.width(32), .enable("false")) multiplexer_4 (
    .in0(multiplexer_2_out), .in1(EPC_q), .out(PCout), .sel(ERET));
  and and_5 (and_5_out, interrup_unen, not_2_out);
  not not_2 (not_2_out, ERET);
  Register #(.width(2)) EPC_2 (.D(priority_encoder_1_out), .en(and_5_out), .Q(out_9), .clk(clk), .clr(comparator_1_eq));
  Comparator #(.width(2)) comparator_1 (.a(priority_encoder_1_out), .b(2'b00), .eq(comparator_1_eq));  // open: gt, lt

  // Other names for the same wires on the sheet: IR_now[1:0] = out_9; pcNext[31:0] = nextPC; will_IR = interrup_unen

  // Notes on the sheet:
  //   由于是单级中断，所以只要处于中断状态，就处于关中断状态
  //   关中断信号
  //   将要中断信号
endmodule

module MutilLevel_Interrupt (
  input  clk,
  input  ir1,
  input  [31:0] PC,
  input  ir2,
  input  ir3,
  input  ERET,
  input  [31:0] nextPC,
  input  [1:0] MFC_sel,
  input  [1:0] MTC_sel,
  input  [31:0] R2,
  output [31:0] PCout,
  output [31:0] siteData2reg,
  output w1,
  output w2,
  output w3
);

  wire _1, _2, _3, and_1_out, and_2_out, and_3_out, and_4_out, and_6_out, and_7_out, and_8_out, d_ff_1_qn,
       d_ff_2_qn, d_ff_3_qn, d_ff_4_qn, d_ff_5_q, d_ff_6_q, d_ff_7_q, d_ff_8_q, decoder_1_out1,
       decoder_1_out2, decoder_1_out3, IE_q, IR1_t, IR2_t, IR3_t, IR_CPU, multiplexer_1_out,
       multiplexer_2_out, multiplexer_3_out, multiplexer_4_out, multiplexer_5_out, multiplexer_6_out,
       not_1_out, not_2_out, not_3_out, not_4_out, or_4_out, or_5_out, or_6_out, or_7_out, or_8_out,
       priority_encoder_1_gs, rst1, rst2, rst3;
  wire [1:0] priority_encoder_1_out, priority_encoder_2_out;
  wire [3:0] \屏蔽字R ;
  wire [31:0] epc, EPC_write, IE_32, multiplexer_7_out, multiplexer_9_out, realpc, \屏蔽字 ;

  Multiplexer #(.enable("false")) multiplexer_1 (.in0(1'b0), .in1(\屏蔽字 [0]), .out(multiplexer_1_out), .sel(_1));
  Multiplexer #(.enable("false")) multiplexer_2 (.in0(1'b0), .in1(\屏蔽字 [1]), .out(multiplexer_2_out), .sel(_1));
  Multiplexer #(.enable("false")) multiplexer_3 (.in0(1'b0), .in1(\屏蔽字 [2]), .out(multiplexer_3_out), .sel(_1));
  Multiplexer #(.enable("false")) multiplexer_4 (.in0(1'b0), .in1(\屏蔽字 [3]), .out(multiplexer_4_out), .sel(_1));
  D_Flip_Flop d_ff_1 (.clk(clk), .D(multiplexer_1_out), .Q(\屏蔽字R [0]), .Qn(d_ff_1_qn), .en(_1));  // open: preset, reset
  D_Flip_Flop d_ff_2 (.clk(clk), .D(multiplexer_2_out), .Q(\屏蔽字R [1]), .Qn(d_ff_2_qn), .en(_1));  // open: preset, reset
  D_Flip_Flop d_ff_3 (.clk(clk), .D(multiplexer_3_out), .Q(\屏蔽字R [2]), .Qn(d_ff_3_qn), .en(_1));  // open: preset, reset
  D_Flip_Flop d_ff_4 (.clk(clk), .D(multiplexer_4_out), .Q(\屏蔽字R [3]), .Qn(d_ff_4_qn), .en(_1));  // open: preset, reset
  D_Flip_Flop d_ff_5 (.clk(ir1), .D(1'b1), .Q(d_ff_5_q), .reset(IR1_t));  // open: Qn, preset, en
  or or_1 (w1, IR1_t, d_ff_5_q);
  D_Flip_Flop d_ff_6 (.clk(ir2), .D(1'b1), .Q(d_ff_6_q), .reset(IR2_t));  // open: Qn, preset, en
  or or_2 (w2, IR2_t, d_ff_6_q);
  D_Flip_Flop d_ff_7 (.clk(ir3), .D(1'b1), .Q(d_ff_7_q), .reset(IR3_t));  // open: Qn, preset, en
  or or_3 (w3, IR3_t, d_ff_7_q);
  Multiplexer #(.select(2), .enable("false")) multiplexer_5 (
    .in0(1'b0), .in1(1'b1), .in2(IE_32[0]), .in3(1'b0), .out(multiplexer_5_out), .sel({_3, ERET}));
  not not_1 (not_1_out, d_ff_8_q);
  D_Flip_Flop d_ff_8 (.clk(clk), .D(1'b1), .Q(d_ff_8_q));  // open: Qn, preset, en, reset
  and and_1 (and_1_out, 1'b0, d_ff_1_qn);
  and and_2 (and_2_out, IR1_t, d_ff_2_qn);
  and and_3 (and_3_out, IR2_t, d_ff_3_qn);
  and and_4 (and_4_out, IR3_t, d_ff_4_qn);
  Multiplexer #(.enable("false")) multiplexer_6 (
    .in0(multiplexer_5_out), .in1(1'b1), .out(multiplexer_6_out), .sel(not_1_out));
  or or_4 (or_4_out, not_1_out, _3, ERET, IR_CPU);
  Multiplexer #(.width(32), .enable("false")) multiplexer_7 (
    .in0(PC), .in1(EPC_write), .out(multiplexer_7_out), .sel(_2));
  or or_5 (or_5_out, d_ff_5_q, IR1_t);
  or or_6 (or_6_out, d_ff_6_q, IR2_t);
  or or_7 (or_7_out, d_ff_7_q, IR3_t);
  Priority_Encoder #(.select(2)) priority_encoder_1 (
    .in0(and_1_out), .in1(and_2_out), .in2(and_3_out), .in3(and_4_out), .out(priority_encoder_1_out),
    .gs(priority_encoder_1_gs));  // open: en_out, en_in
  and and_5 (IR_CPU, priority_encoder_1_gs, IE_q);
  D_Flip_Flop IE (.clk(clk), .D(multiplexer_6_out), .Q(IE_q), .en(or_4_out));  // open: Qn, preset, reset
  Register #(.width(32)) u_EPC (.D(multiplexer_7_out), .en(or_8_out), .Q(epc), .clk(clk));  // open: clr
  or or_8 (or_8_out, _2, IR_CPU);
  and and_6 (and_6_out, or_5_out, not_2_out);
  not not_2 (not_2_out, rst1);
  and and_7 (and_7_out, or_6_out, not_3_out);
  not not_3 (not_3_out, rst2);
  and and_8 (and_8_out, or_7_out, not_4_out);
  not not_4 (not_4_out, rst3);
  D_Flip_Flop u_IR1 (.clk(clk), .D(and_6_out), .Q(IR1_t));  // open: Qn, preset, en, reset
  D_Flip_Flop u_IR2 (.clk(clk), .D(and_7_out), .Q(IR2_t));  // open: Qn, preset, en, reset
  D_Flip_Flop u_IR3 (.clk(clk), .D(and_8_out), .Q(IR3_t));  // open: Qn, preset, en, reset
  // Probe on priority_encoder_1_out
  Multiplexer #(.select(2), .width(32), .enable("false")) multiplexer_8 (
    .in1(32'h4), .in2(32'h20c), .in3(32'h414), .out(realpc), .sel(priority_encoder_1_out));  // open: in0
  Priority_Encoder #(.select(2)) priority_encoder_2 (
    .in0(1'b0), .in1(IR1_t), .in2(IR2_t), .in3(IR3_t), .out(priority_encoder_2_out));  // open: gs, en_out, en_in
  // Probe on R2
  Demultiplexer #(.select(2), .width(32), .enable("false")) demultiplexer_1 (
    .out0(\屏蔽字 ), .out1(EPC_write), .out2(IE_32), .in(R2), .sel(MTC_sel));  // open: out3
  Decoder #(.select(2), .enable("false")) decoder_1 (
    .out1(decoder_1_out1), .out2(decoder_1_out2), .out3(decoder_1_out3), .sel(priority_encoder_2_out));  // open: out0
  // Probe on \屏蔽字 
  // Probe on MTC_sel
  and and_9 (rst1, ERET, decoder_1_out1);
  and and_10 (rst2, decoder_1_out2, ERET);
  and and_11 (rst3, decoder_1_out3, ERET);
  Multiplexer #(.width(32), .enable("false")) multiplexer_9 (
    .in0(nextPC), .in1(realpc), .out(multiplexer_9_out), .sel(IR_CPU));
  Multiplexer #(.width(32), .enable("false")) multiplexer_10 (
    .in0(multiplexer_9_out), .in1(epc), .out(PCout), .sel(ERET));
  Decoder #(.select(2), .enable("false")) decoder_2 (.out0(_1), .out1(_2), .out2(_3), .sel(MTC_sel));  // open: out3
  Multiplexer #(.select(2), .width(32), .enable("false")) multiplexer_11 (
    .in0({{28{1'b0}}, \屏蔽字R }), .in1(epc), .in2({32{1'b0}}), .in3({32{1'b0}}), .out(siteData2reg),
    .sel(MFC_sel));

  // Other names for the same wires on the sheet: IE_sel[1:0] = {_3, ERET}; pcNext[31:0] = nextPC
endmodule

module \单级中断  (
);

  wire \_1号中断 , \_1号中断等待指示 , \_2号中断 , \_2号中断等待指示 , \_3号中断 , \_3号中断等待指示 , and_1_out, and_2_out, and_4_out,
       and_5_out, BLEZ, CLK, comparator_1_eq, compare, ERET, Go, HW_sel, JMP, JR, LOCK, mips_alu_1_equal,
       multiplexer_1_out, multiplexer_15_out, or_1_out, or_2_out, RST, SH, SignedExt, SRLV, Syscall, XORI,
       \硬布线控制器_1_alu_src , \硬布线控制器_1_beq , \硬布线控制器_1_bne , \硬布线控制器_1_jal , \硬布线控制器_1_memtoreg ,
       \硬布线控制器_1_memwrite , \硬布线控制器_1_regdst , \硬布线控制器_1_regwrite ;
  wire [3:0] multiplexer_18_out, multiplexer_19_out, \硬布线控制器_1_alu_op ;
  wire [4:0] multiplexer_5_out, multiplexer_6_out, multiplexer_8_out, multiplexer_9_out, multiplexer_14_out,
       shamt;
  wire [15:0] \总周期数 , \无条件分支数 , \条件分支成功数 ;
  wire [27:2] rom_1_data;
  wire [31:0] adder_1_out, adder_2_out, bit_extender_1_out, bit_extender_2_out, LedData, mips_alu_1_result,
       mips_ram_1_p7, multiplexer_3_out, multiplexer_4_out, multiplexer_7_out, multiplexer_10_out,
       multiplexer_11_out, multiplexer_12_out, multiplexer_13_out, multiplexer_16_out, multiplexer_17_out,
       multiplexer_20_out, PC, PC_in, PC_Ori, R1, R2, shifter_1_out, undriven;
  wire [31:26] rom_1_data_2;

  Button \u_总复位  (.out(RST));
  Button \u_继续运行  (.out(Go));
  Clock clock_1 (.out(CLK));
  Register #(.width(32)) u_PC (.D(PC_in), .en(multiplexer_1_out), .Q(PC), .clk(CLK), .clr(RST));
  Multiplexer #(.enable("false")) multiplexer_1 (.in0(1'b1), .in1(1'b0), .out(multiplexer_1_out), .sel(and_1_out));
  and and_1 (and_1_out, LOCK, ~Go);  // AND_Gate
  Comparator #(.width(32)) comparator_1 (.a(R1), .b(32'h22), .eq(comparator_1_eq));  // open: gt, lt
  Hex_Digit_Display hex_digit_display_1 (.value(LedData[31:28]));  // open: dp
  Hex_Digit_Display hex_digit_display_2 (.value(LedData[27:24]));  // open: dp
  Counter #(.width(16), .max('hffff)) counter_1 (
    .count(JMP), .Q(\无条件分支数 ), .clk(CLK), .clr(RST));  // open: load, D, carry
  Counter #(.width(16), .max('hffff)) counter_2 (
    .count(compare), .Q(\条件分支成功数 ), .clk(CLK), .clr(RST));  // open: load, D, carry
  Counter #(.width(16), .max('hffff)) counter_3 (
    .count(multiplexer_1_out), .Q(\总周期数 ), .clk(CLK), .clr(RST));  // open: load, D, carry
  Multiplexer #(.width(32), .enable("false")) multiplexer_2 (
    .in0(multiplexer_7_out), .in1(multiplexer_3_out), .out(PC_Ori), .sel(JMP));
  Multiplexer #(.width(32), .enable("false")) multiplexer_3 (
    .in0({4'b0000, rom_1_data[27:13], shamt, rom_1_data[7:2], 2'b00}), .in1(R1), .out(multiplexer_3_out),
    .sel(JR));
  Hex_Digit_Display hex_digit_display_3 (.value(LedData[19:16]));  // open: dp
  Hex_Digit_Display hex_digit_display_4 (.value(LedData[23:20]));  // open: dp
  and and_2 (and_2_out, comparator_1_eq, Syscall);
  and and_3 (LOCK, ~comparator_1_eq, Syscall);  // AND_Gate
  Hex_Digit_Display hex_digit_display_5 (.value(LedData[11:8]));  // open: dp
  Hex_Digit_Display hex_digit_display_6 (.value(LedData[15:12]));  // open: dp
  ROM #(.addrWidth(10), .dataWidth(32)) rom_1 (
    .addr(PC[11:2]), .data({rom_1_data_2, rom_1_data[27:13], shamt, rom_1_data[7:2]}));  // open: sel
  Adder #(.width(32)) adder_1 (.a(PC), .b(32'h4), .out(adder_1_out));  // open: cin, cout
  Multiplexer #(.width(32)) multiplexer_4 (
    .in0(undriven), .in1(R2), .out(multiplexer_4_out), .sel(and_2_out), .en(and_2_out));
  Hex_Digit_Display hex_digit_display_7 (.value(LedData[7:4]));  // open: dp
  Hex_Digit_Display hex_digit_display_8 (.value(LedData[3:0]));  // open: dp
  Multiplexer #(.width(5), .enable("false")) multiplexer_5 (
    .in0(rom_1_data[27:23]), .in1(5'b00010), .out(multiplexer_5_out), .sel(Syscall));
  Register #(.width(32)) register_1 (.D(multiplexer_4_out), .Q(LedData), .clk(CLK), .clr(RST));  // open: en
  \硬布线控制器  \u_硬布线控制器_1  (
    .Func(rom_1_data[7:2]), .OP(rom_1_data_2), .ALU_OP(\硬布线控制器_1_alu_op ), .MemToReg(\硬布线控制器_1_memtoreg ),
    .MemWrite(\硬布线控制器_1_memwrite ), .ALU_SRC(\硬布线控制器_1_alu_src ), .RegWrite(\硬布线控制器_1_regwrite ),
    .SysCALL(Syscall), .SignedExt(SignedExt), .RegDst(\硬布线控制器_1_regdst ), .JR(JR), .JMP(JMP),
    .Beq(\硬布线控制器_1_beq ), .JAL(\硬布线控制器_1_jal ), .Bne(\硬布线控制器_1_bne ), .SRLV(SRLV), .XORI(XORI), .SH(SH),
    .BLEZ(BLEZ), .ERET(ERET));  // open: RS, RD, MFC_0, MTC_0
  Multiplexer #(.width(5), .enable("false")) multiplexer_6 (
    .in0(rom_1_data[22:18]), .in1(5'b00100), .out(multiplexer_6_out), .sel(Syscall));
  Multiplexer #(.width(32), .enable("false")) multiplexer_7 (
    .in0(adder_1_out), .in1(adder_2_out), .out(multiplexer_7_out), .sel(compare));
  Multiplexer #(.width(5), .enable("false")) multiplexer_8 (
    .in0(rom_1_data[22:18]), .in1(rom_1_data[17:13]), .out(multiplexer_8_out), .sel(\硬布线控制器_1_regdst ));
  Multiplexer #(.width(5), .enable("false")) multiplexer_9 (
    .in0(multiplexer_8_out), .in1({5{1'b1}}), .out(multiplexer_9_out), .sel(\硬布线控制器_1_jal ));
  assign bit_extender_1_out = {{16{1'b0}}, {rom_1_data[17:13], shamt, rom_1_data[7:2]}};  // Bit_Extender bit_extender_1
  assign bit_extender_2_out = {{16{rom_1_data[17]}}, {rom_1_data[17:13], shamt, rom_1_data[7:2]}};  // Bit_Extender bit_extender_2
  // Probe on \总周期数 
  // Probe on \无条件分支数 
  // Probe on \条件分支成功数 
  Multiplexer #(.width(32), .enable("false")) multiplexer_10 (
    .in0(multiplexer_20_out), .in1(adder_1_out), .out(multiplexer_10_out), .sel(\硬布线控制器_1_jal ));
  SingleLevel_Interrupt singlelevel_interrupt_1 (
    .clk(CLK), .ir1(\_1号中断 ), .PC(PC), .PCout(PC_in), .ir2(\_2号中断 ), .ir3(\_3号中断 ), .ERET(ERET),
    .nextPC(PC_Ori), .w1(\_1号中断等待指示 ), .w2(\_2号中断等待指示 ), .w3(\_3号中断等待指示 ));  // open: out_9
  Button _1 (.out(\_1号中断 ));
  Button _2 (.out(\_2号中断 ));
  Button _3 (.out(\_3号中断 ));
  Multiplexer #(.width(32), .enable("false")) multiplexer_11 (
    .in0(bit_extender_1_out), .in1(bit_extender_2_out), .out(multiplexer_11_out), .sel(SignedExt));
  MIPS_Regifile mips_regifile_1 (
    .Din(multiplexer_10_out), .Clk(CLK), .R1(R1), .R2(R2), .WE(\硬布线控制器_1_regwrite ),
    .W_num(multiplexer_9_out), .R1_num(multiplexer_5_out), .R2_num(multiplexer_6_out));
  Multiplexer #(.width(32), .enable("false")) multiplexer_12 (
    .in0(R2), .in1(multiplexer_11_out), .out(multiplexer_12_out), .sel(\硬布线控制器_1_alu_src ));
  Shifter #(.width(32)) shifter_1 (.in(bit_extender_2_out), .\dist (5'b00010), .out(shifter_1_out));
  LED _1_2 (.in(\_1号中断等待指示 ));
  LED _2_2 (.in(\_2号中断等待指示 ));
  LED _3_2 (.in(\_3号中断等待指示 ));
  LED led_1 (.in(\硬布线控制器_1_memwrite ));
  LED led_2 (.in(SH));
  or or_1 (or_1_out, SH, BLEZ);
  Adder #(.width(32)) adder_2 (.a(shifter_1_out), .b(adder_1_out), .out(adder_2_out));  // open: cin, cout
  Multiplexer #(.width(32), .enable("false")) multiplexer_13 (
    .in0(multiplexer_12_out), .in1({32{1'b0}}), .out(multiplexer_13_out), .sel(or_1_out));
  Multiplexer #(.width(5), .enable("false")) multiplexer_14 (
    .in0(shamt), .in1(R1[4:0]), .out(multiplexer_14_out), .sel(SRLV));
  // Probe on \_1号中断 
  MIPS_ALU mips_alu_1 (
    .X(R1), .Y(multiplexer_13_out), .AluOP(\硬布线控制器_1_alu_op ), .Equal(mips_alu_1_equal),
    .Result({mips_alu_1_result[31:2], HW_sel, mips_alu_1_result[0]}), .shamt(multiplexer_14_out));  // open: Result_2
  and and_4 (and_4_out, \硬布线控制器_1_beq , mips_alu_1_equal);
  and and_5 (and_5_out, ~mips_alu_1_equal, \硬布线控制器_1_bne );  // AND_Gate
  or or_2 (or_2_out, mips_alu_1_equal, mips_alu_1_result[0]);
  Multiplexer #(.enable("false")) multiplexer_15 (.in0(1'b0), .in1(or_2_out), .out(multiplexer_15_out), .sel(BLEZ));
  Multiplexer #(.width(32), .enable("false")) multiplexer_16 (
    .in0({{16{1'b0}}, R2[15:0]}), .in1({R2[15:0], {16{1'b0}}}), .out(multiplexer_16_out), .sel(HW_sel));
  or or_3 (compare, and_4_out, and_5_out, multiplexer_15_out);
  Multiplexer #(.width(32), .enable("false")) multiplexer_17 (
    .in0(R2), .in1(multiplexer_16_out), .out(multiplexer_17_out), .sel(SH));
  Multiplexer #(.width(4), .enable("false")) multiplexer_18 (
    .in0(4'b1111), .in1(multiplexer_19_out), .out(multiplexer_18_out), .sel(SH));
  Multiplexer #(.width(4), .enable("false")) multiplexer_19 (
    .in0(4'b0011), .in1(4'b1100), .out(multiplexer_19_out), .sel(HW_sel));
  // MIPS_RAM mips_ram_1: pin names not known; wires that end beside it: mips_alu_1_result[21:2], multiplexer_17_out, \硬布线控制器_1_memwrite , multiplexer_18_out, CLK, RST, mips_ram_1_p7
  Multiplexer #(.width(32), .enable("false")) multiplexer_20 (
    .in0({mips_alu_1_result[31:2], HW_sel, mips_alu_1_result[0]}), .in1(mips_ram_1_p7),
    .out(multiplexer_20_out), .sel(\硬布线控制器_1_memtoreg ));

  // Notes on the sheet:
  //   数码管输出应该用寄存器锁存，否则显示数据只能一闪而过
  //   可以通过项目增加Logisim库的方式将前几次实验完成的电路作为子电路引入到本电路中使用
  //   指令存储器
  //   OP
  //   rs
  //   指令字
  //   contents of rom_1 (hex, n*v repeats v):
  //   8000d54 23bdfffc afa10000 23bdfffc afa20000 23bdfffc afa30000 23bdfffc afa40000 23bdfffc afa50000
  //   23bdfffc afa60000 23bdfffc afa70000 23bdfffc afa80000 23bdfffc afa90000 23bdfffc afaa0000 23bdfffc
  //   afab0000 23bdfffc afac0000 23bdfffc afad0000 23bdfffc afae0000 23bdfffc afaf0000 23bdfffc afb00000
  //   23bdfffc afb10000 23bdfffc afb20000 23bdfffc afb30000 23bdfffc afb40000 23bdfffc afb50000 23bdfffc
  //   afb60000 23bdfffc afb70000 23bdfffc afb80000 23bdfffc afb90000 20160001 20140006 20150001 168020
  //   108100 2149825 132020 20020022 c 1600fffa 295a022 1680fff7 8fb90000 23bd0004 8fb80000 23bd0004
  //   8fb70000 23bd0004 8fb60000 23bd0004 8fb50000 23bd0004 8fb40000 23bd0004 8fb30000 23bd0004 8fb20000
  //   23bd0004 8fb10000 23bd0004 8fb00000 23bd0004 8faf0000 23bd0004 8fae0000 23bd0004 8fad0000 23bd0004
  //   8fac0000 23bd0004 8fab0000 23bd0004 8faa0000 23bd0004 8fa90000 23bd0004 8fa80000 23bd0004 8fa70000
  //   23bd0004 8fa60000 23bd0004 8fa50000 23bd0004 8fa40000 23bd0004 8fa30000 23bd0004 8fa20000 23bd0004
  //   8fa10000 23bd0004 42000018 23bdfffc afa10000 23bdfffc afa20000 23bdfffc afa30000 23bdfffc afa40000
  //   23bdfffc afa50000 23bdfffc afa60000 23bdfffc afa70000 23bdfffc afa80000 23bdfffc afa90000 23bdfffc
  //   afaa0000 23bdfffc afab0000 23bdfffc afac0000 23bdfffc afad0000 23bdfffc afae0000 23bdfffc afaf0000
  //   23bdfffc afb00000 23bdfffc afb10000 23bdfffc afb20000 23bdfffc afb30000 23bdfffc afb40000 23bdfffc
  //   afb50000 23bdfffc afb60000 23bdfffc afb70000 23bdfffc afb80000 23bdfffc afb90000 20160002 20140006
  //   20150001 168020 108100 2149825 132020 20020022 c 1600fffa 295a022 1680fff7 8fb90000 23bd0004
  //   8fb80000 23bd0004 8fb70000 23bd0004 8fb60000 23bd0004 8fb50000 23bd0004 8fb40000 23bd0004 8fb30000
  //   23bd0004 8fb20000 23bd0004 8fb10000 23bd0004 8fb00000 23bd0004 8faf0000 23bd0004 8fae0000 23bd0004
  //   8fad0000 23bd0004 8fac0000 23bd0004 8fab0000 23bd0004 8faa0000 23bd0004 8fa90000 23bd0004 8fa80000
  //   23bd0004 8fa70000 23bd0004 8fa60000 23bd0004 8fa50000 23bd0004 8fa40000 23bd0004 8fa30000 23bd0004
  //   8fa20000 23bd0004 8fa10000 23bd0004 42000018 23bdfffc afa10000 23bdfffc afa20000 23bdfffc afa30000
  //   23bdfffc afa40000 23bdfffc afa50000 23bdfffc afa60000 23bdfffc afa70000 23bdfffc afa80000 23bdfffc
  //   afa90000 23bdfffc afaa0000 23bdfffc afab0000 23bdfffc afac0000 23bdfffc afad0000 23bdfffc afae0000
  //   23bdfffc afaf0000 23bdfffc afb00000 23bdfffc afb10000 23bdfffc afb20000 23bdfffc afb30000 23bdfffc
  //   afb40000 23bdfffc afb50000 23bdfffc afb60000 23bdfffc afb70000 23bdfffc afb80000 23bdfffc afb90000
  //   20160003 20140006 20150001 168020 108100 2149825 132020 20020022 c 1600fffa 295a022 1680fff7
  //   8fb90000 23bd0004 8fb80000 23bd0004 8fb70000 23bd0004 8fb60000 23bd0004 8fb50000 23bd0004 8fb40000
  //   23bd0004 8fb30000 23bd0004 8fb20000 23bd0004 8fb10000 23bd0004 8fb00000 23bd0004 8faf0000 23bd0004
  //   8fae0000 23bd0004 8fad0000 23bd0004 8fac0000 23bd0004 8fab0000 23bd0004 8faa0000 23bd0004 8fa90000
  //   23bd0004 8fa80000 23bd0004 8fa70000 23bd0004 8fa60000 23bd0004 8fa50000 23bd0004 8fa40000 23bd0004
  //   8fa30000 23bd0004 8fa20000 23bd0004 8fa10000 23bd0004 42000018 20110200 20020022 112020 c 2231ffff
  //   1620fffc 4*0 2002000a c 2002000a c
  //   rt
  //   rd
  //   数码管输出
  //   JMP
  //   OP
  //   Func
  //   Func
  //   Beq
  //   Bne
  //   MemToReg
  //   MemWrite
  //   AluOP
  //   AluSrcB
  //   RegWrite
  //   JAL
  //   RegDst
  //   Syscall
  //   总复位信号应将除ROM以外所有存储组件全部清零
  //   中断信号源及指示电路规范（优先级3>2>1>CPU(0）)
endmodule
module \多级中断  (
);

  wire \_1号中断 , \_1号中断等待指示 , \_2号中断 , \_2号中断等待指示 , \_3号中断 , \_3号中断等待指示 , and_1_out, and_2_out, and_4_out,
       and_5_out, and_6_out, and_7_out, and_8_out, and_9_out, and_10_out, and_11_out, BLEZ, CLK,
       comparator_1_eq, comparator_2_eq, comparator_3_eq, comparator_4_eq, comparator_5_eq, comparator_6_eq,
       comparator_7_eq, comparator_8_gt, comparator_9_gt, compare, ERET, Go, HW_sel, JMP, JR, LOCK, MFC_0,
       mips_alu_1_equal, MTC_0, multiplexer_1_out, multiplexer_16_out, not_1_out, not_2_out, or_1_out,
       or_2_out, or_4_out, or_5_out, RST, SH, SignedExt, SRLV, Syscall, XORI, \硬布线控制器_1_alu_src ,
       \硬布线控制器_1_beq , \硬布线控制器_1_bne , \硬布线控制器_1_jal , \硬布线控制器_1_memtoreg , \硬布线控制器_1_memwrite ,
       \硬布线控制器_1_regdst , \硬布线控制器_1_regwrite ;
  wire [1:0] MFC_sel, MTC_sel;
  wire [3:0] multiplexer_19_out, multiplexer_20_out, \硬布线控制器_1_alu_op ;
  wire [4:0] multiplexer_5_out, multiplexer_6_out, multiplexer_8_out, multiplexer_9_out, multiplexer_15_out,
       RD, shamt;
  wire [15:0] \总周期数 , \无条件分支数 , \条件分支成功数 ;
  wire [27:2] rom_1_data;
  wire [31:0] adder_1_out, adder_2_out, bit_extender_1_out, bit_extender_2_out, LedData, mips_alu_1_result,
       mips_ram_1_p7, multiplexer_3_out, multiplexer_4_out, multiplexer_7_out, multiplexer_10_out,
       multiplexer_11_out, multiplexer_12_out, multiplexer_13_out, multiplexer_14_out, multiplexer_17_out,
       multiplexer_18_out, multiplexer_21_out, PC, PC_in, PC_Ori, R1, R2, shifter_1_out, siteData, undriven;
  wire [31:26] rom_1_data_2;

  Button \u_总复位  (.out(RST));
  Button \u_继续运行  (.out(Go));
  Clock clock_1 (.out(CLK));
  Register #(.width(32)) u_PC (.D(PC_in), .en(multiplexer_1_out), .Q(PC), .clk(CLK), .clr(RST));
  Multiplexer #(.enable("false")) multiplexer_1 (.in0(1'b1), .in1(1'b0), .out(multiplexer_1_out), .sel(and_1_out));
  and and_1 (and_1_out, LOCK, ~Go);  // AND_Gate
  Comparator #(.width(32)) comparator_1 (.a(R1), .b(32'h22), .eq(comparator_1_eq));  // open: gt, lt
  Hex_Digit_Display hex_digit_display_1 (.value(LedData[27:24]));  // open: dp
  Hex_Digit_Display hex_digit_display_2 (.value(LedData[31:28]));  // open: dp
  Counter #(.width(16), .max('hffff)) counter_1 (
    .count(JMP), .Q(\无条件分支数 ), .clk(CLK), .clr(RST));  // open: load, D, carry
  Counter #(.width(16), .max('hffff)) counter_2 (
    .count(compare), .Q(\条件分支成功数 ), .clk(CLK), .clr(RST));  // open: load, D, carry
  Counter #(.width(16), .max('hffff)) counter_3 (
    .count(multiplexer_1_out), .Q(\总周期数 ), .clk(CLK), .clr(RST));  // open: load, D, carry
  Multiplexer #(.width(32), .enable("false")) multiplexer_2 (
    .in0(multiplexer_7_out), .in1(multiplexer_3_out), .out(PC_Ori), .sel(JMP));
  Multiplexer #(.width(32), .enable("false")) multiplexer_3 (
    .in0({4'b0000, rom_1_data[27:18], RD, shamt, rom_1_data[7:2], 2'b00}), .in1(R1), .out(multiplexer_3_out),
    .sel(JR));
  Hex_Digit_Display hex_digit_display_3 (.value(LedData[19:16]));  // open: dp
  Hex_Digit_Display hex_digit_display_4 (.value(LedData[23:20]));  // open: dp
  and and_2 (and_2_out, comparator_1_eq, Syscall);
  and and_3 (LOCK, ~comparator_1_eq, Syscall);  // AND_Gate
  Hex_Digit_Display hex_digit_display_5 (.value(LedData[15:12]));  // open: dp
  Hex_Digit_Display hex_digit_display_6 (.value(LedData[11:8]));  // open: dp
  ROM #(.addrWidth(10), .dataWidth(32)) rom_1 (
    .addr(PC[11:2]), .data({rom_1_data_2, rom_1_data[27:18], RD, shamt, rom_1_data[7:2]}));  // open: sel
  Adder #(.width(32)) adder_1 (.a(PC), .b(32'h4), .out(adder_1_out));  // open: cin, cout
  Multiplexer #(.width(32)) multiplexer_4 (
    .in0(undriven), .in1(R2), .out(multiplexer_4_out), .sel(and_2_out), .en(and_2_out));
  Hex_Digit_Display hex_digit_display_7 (.value(LedData[7:4]));  // open: dp
  Hex_Digit_Display hex_digit_display_8 (.value(LedData[3:0]));  // open: dp
  Multiplexer #(.width(5), .enable("false")) multiplexer_5 (
    .in0(rom_1_data[27:23]), .in1(5'b00010), .out(multiplexer_5_out), .sel(Syscall));
  Register #(.width(32)) register_1 (.D(multiplexer_4_out), .Q(LedData), .clk(CLK), .clr(RST));  // open: en
  \硬布线控制器  \u_硬布线控制器_1  (
    .Func(rom_1_data[7:2]), .OP(rom_1_data_2), .ALU_OP(\硬布线控制器_1_alu_op ), .MemToReg(\硬布线控制器_1_memtoreg ),
    .MemWrite(\硬布线控制器_1_memwrite ), .ALU_SRC(\硬布线控制器_1_alu_src ), .RegWrite(\硬布线控制器_1_regwrite ),
    .SysCALL(Syscall), .SignedExt(SignedExt), .RegDst(\硬布线控制器_1_regdst ), .JR(JR), .JMP(JMP),
    .Beq(\硬布线控制器_1_beq ), .JAL(\硬布线控制器_1_jal ), .Bne(\硬布线控制器_1_bne ), .SRLV(SRLV), .XORI(XORI), .SH(SH),
    .BLEZ(BLEZ), .ERET(ERET), .RS(rom_1_data[27:23]), .RD(RD), .MFC_0(MFC_0), .MTC_0(MTC_0));
  Multiplexer #(.width(5), .enable("false")) multiplexer_6 (
    .in0(rom_1_data[22:18]), .in1(5'b00100), .out(multiplexer_6_out), .sel(Syscall));
  Multiplexer #(.width(32), .enable("false")) multiplexer_7 (
    .in0(adder_1_out), .in1(adder_2_out), .out(multiplexer_7_out), .sel(compare));
  Multiplexer #(.width(5), .enable("false")) multiplexer_8 (
    .in0(rom_1_data[22:18]), .in1(RD), .out(multiplexer_8_out), .sel(\硬布线控制器_1_regdst ));
  Multiplexer #(.width(5), .enable("false")) multiplexer_9 (
    .in0(multiplexer_8_out), .in1({5{1'b1}}), .out(multiplexer_9_out), .sel(\硬布线控制器_1_jal ));
  assign bit_extender_1_out = {{16{1'b0}}, {RD, shamt, rom_1_data[7:2]}};  // Bit_Extender bit_extender_1
  assign bit_extender_2_out = {{16{RD[4]}}, {RD, shamt, rom_1_data[7:2]}};  // Bit_Extender bit_extender_2
  // Probe on PC
  // Probe on \总周期数 
  // Probe on \无条件分支数 
  // Probe on \条件分支成功数 
  Multiplexer #(.width(32), .enable("false")) multiplexer_10 (
    .in0(multiplexer_21_out), .in1(adder_1_out), .out(multiplexer_10_out), .sel(\硬布线控制器_1_jal ));
  MutilLevel_Interrupt mutillevel_interrupt_1 (
    .clk(CLK), .ir1(\_1号中断 ), .PC(PC), .ir2(\_2号中断 ), .ir3(\_3号中断 ), .ERET(ERET), .nextPC(PC_Ori),
    .MFC_sel(MFC_sel), .MTC_sel(MTC_sel), .R2(R2), .PCout(PC_in), .siteData2reg(siteData), .w1(\_1号中断等待指示 ),
    .w2(\_2号中断等待指示 ), .w3(\_3号中断等待指示 ));
  Button _1 (.out(\_1号中断 ));
  Button _2 (.out(\_2号中断 ));
  Button _3 (.out(\_3号中断 ));
  Multiplexer #(.width(32), .enable("false")) multiplexer_11 (
    .in0(multiplexer_10_out), .in1(siteData), .out(multiplexer_11_out), .sel(MFC_0));
  // Probe on PC_in
  Multiplexer #(.width(32), .enable("false")) multiplexer_12 (
    .in0(bit_extender_1_out), .in1(bit_extender_2_out), .out(multiplexer_12_out), .sel(SignedExt));
  LED _1_2 (.in(\_1号中断等待指示 ));
  LED _2_2 (.in(\_2号中断等待指示 ));
  LED _3_2 (.in(\_3号中断等待指示 ));
  MIPS_Regifile mips_regifile_1 (
    .Din(multiplexer_11_out), .Clk(CLK), .R1(R1), .R2(R2), .WE(\硬布线控制器_1_regwrite ),
    .W_num(multiplexer_9_out), .R1_num(multiplexer_5_out), .R2_num(multiplexer_6_out));
  Multiplexer #(.width(32), .enable("false")) multiplexer_13 (
    .in0(R2), .in1(multiplexer_12_out), .out(multiplexer_13_out), .sel(\硬布线控制器_1_alu_src ));
  Shifter #(.width(32)) shifter_1 (.in(bit_extender_2_out), .\dist (5'b00010), .out(shifter_1_out));
  // Probe on \_1号中断 
  LED led_1 (.in(\硬布线控制器_1_memwrite ));
  LED led_2 (.in(SH));
  or or_1 (or_1_out, SH, BLEZ);
  Multiplexer #(.width(32), .enable("false")) multiplexer_14 (
    .in0(multiplexer_13_out), .in1({32{1'b0}}), .out(multiplexer_14_out), .sel(or_1_out));
  Multiplexer #(.width(5), .enable("false")) multiplexer_15 (
    .in0(shamt), .in1(R1[4:0]), .out(multiplexer_15_out), .sel(SRLV));
  Adder #(.width(32)) adder_2 (.a(shifter_1_out), .b(adder_1_out), .out(adder_2_out));  // open: cin, cout
  Comparator #(.width(5)) comparator_2 (.a(RD), .b(5'b00001), .eq(comparator_2_eq));  // open: gt, lt
  and and_4 (and_4_out, comparator_2_eq, MFC_0);
  Comparator #(.width(5)) comparator_3 (.a(RD), .b(5'b00001), .eq(comparator_3_eq));  // open: gt, lt
  MIPS_ALU mips_alu_1 (
    .X(R1), .Y(multiplexer_14_out), .AluOP(\硬布线控制器_1_alu_op ), .Equal(mips_alu_1_equal),
    .Result({mips_alu_1_result[31:2], HW_sel, mips_alu_1_result[0]}), .shamt(multiplexer_15_out));  // open: Result_2
  assign MFC_sel = and_4_out ? 2'b00 : 2'bz;  // Controlled_Buffer controlled_buffer_1
  assign MTC_sel = and_5_out ? 2'b00 : 2'bz;  // Controlled_Buffer controlled_buffer_2
  and and_5 (and_5_out, comparator_3_eq, MTC_0);
  and and_6 (and_6_out, \硬布线控制器_1_beq , mips_alu_1_equal);
  and and_7 (and_7_out, ~mips_alu_1_equal, \硬布线控制器_1_bne );  // AND_Gate
  or or_2 (or_2_out, mips_alu_1_equal, mips_alu_1_result[0]);
  Comparator #(.width(5)) comparator_4 (.a(RD), .b(5'b00010), .eq(comparator_4_eq));  // open: gt, lt
  assign MFC_sel = and_8_out ? 2'b01 : 2'bz;  // Controlled_Buffer controlled_buffer_3
  and and_8 (and_8_out, comparator_4_eq, MFC_0);
  Comparator #(.width(5)) comparator_5 (.a(RD), .b(5'b00010), .eq(comparator_5_eq));  // open: gt, lt
  and and_9 (and_9_out, comparator_5_eq, MTC_0);
  Multiplexer #(.enable("false")) multiplexer_16 (.in0(1'b0), .in1(or_2_out), .out(multiplexer_16_out), .sel(BLEZ));
  Multiplexer #(.width(32), .enable("false")) multiplexer_17 (
    .in0(R2), .in1(multiplexer_18_out), .out(multiplexer_17_out), .sel(SH));
  Multiplexer #(.width(32), .enable("false")) multiplexer_18 (
    .in0({{16{1'b0}}, R2[15:0]}), .in1({R2[15:0], {16{1'b0}}}), .out(multiplexer_18_out), .sel(HW_sel));
  // Probe on MTC_sel
  assign MTC_sel = and_9_out ? 2'b01 : 2'bz;  // Controlled_Buffer controlled_buffer_4
  or or_3 (compare, and_6_out, and_7_out, multiplexer_16_out);
  Comparator #(.width(5)) comparator_6 (.a(RD), .b(5'b00011), .eq(comparator_6_eq));  // open: gt, lt
  Comparator #(.width(5)) comparator_7 (.a(RD), .b(5'b00011), .eq(comparator_7_eq));  // open: gt, lt
  Multiplexer #(.width(4), .enable("false")) multiplexer_19 (
    .in0(4'b1111), .in1(multiplexer_20_out), .out(multiplexer_19_out), .sel(SH));
  Multiplexer #(.width(4), .enable("false")) multiplexer_20 (
    .in0(4'b0011), .in1(4'b1100), .out(multiplexer_20_out), .sel(HW_sel));
  assign MFC_sel = and_10_out ? 2'b10 : 2'bz;  // Controlled_Buffer controlled_buffer_5
  and and_10 (and_10_out, comparator_6_eq, MFC_0);
  assign MTC_sel = and_11_out ? 2'b10 : 2'bz;  // Controlled_Buffer controlled_buffer_6
  and and_11 (and_11_out, comparator_7_eq, MTC_0);
  // MIPS_RAM mips_ram_1: pin names not known; wires that end beside it: mips_alu_1_result[21:2], multiplexer_17_out, \硬布线控制器_1_memwrite , multiplexer_19_out, CLK, RST, mips_ram_1_p7
  Comparator #(.width(5)) comparator_8 (.a(RD), .b(5'b00011), .gt(comparator_8_gt));  // open: eq, lt
  Multiplexer #(.width(32), .enable("false")) multiplexer_21 (
    .in0({mips_alu_1_result[31:2], HW_sel, mips_alu_1_result[0]}), .in1(mips_ram_1_p7),
    .out(multiplexer_21_out), .sel(\硬布线控制器_1_memtoreg ));
  assign MFC_sel = or_4_out ? 2'b11 : 2'bz;  // Controlled_Buffer controlled_buffer_7
  or or_4 (or_4_out, comparator_8_gt, not_1_out);
  not not_1 (not_1_out, MFC_0);
  Comparator #(.width(5)) comparator_9 (.a(RD), .b(5'b00011), .gt(comparator_9_gt));  // open: eq, lt
  or or_5 (or_5_out, comparator_9_gt, not_2_out);
  not not_2 (not_2_out, MTC_0);
  assign MTC_sel = or_5_out ? 2'b11 : 2'bz;  // Controlled_Buffer controlled_buffer_8

  // Notes on the sheet:
  //   数码管输出应该用寄存器锁存，否则显示数据只能一闪而过
  //   可以通过项目增加Logisim库的方式将前几次实验完成的电路作为子电路引入到本电路中使用
  //   指令存储器
  //   OP
  //   rs
  //   指令字
  //   contents of rom_1 (hex, n*v repeats v):
  //   8000d54 23bdfffc afa10000 23bdfffc afa20000 23bdfffc afa30000 23bdfffc afa40000 23bdfffc afa50000
  //   23bdfffc afa60000 23bdfffc afa70000 23bdfffc afa80000 23bdfffc afa90000 23bdfffc afaa0000 23bdfffc
  //   afab0000 23bdfffc afac0000 23bdfffc afad0000 23bdfffc afae0000 23bdfffc afaf0000 23bdfffc afb00000
  //   23bdfffc afb10000 23bdfffc afb20000 23bdfffc afb30000 23bdfffc afb40000 23bdfffc afb50000 23bdfffc
  //   afb60000 23bdfffc afb70000 23bdfffc afb80000 23bdfffc afb90000 20160001 20140006 20150001 168020
  //   108100 2149825 132020 20020022 c 1600fffa 295a022 1680fff7 8fb90000 23bd0004 8fb80000 23bd0004
  //   8fb70000 23bd0004 8fb60000 23bd0004 8fb50000 23bd0004 8fb40000 23bd0004 8fb30000 23bd0004 8fb20000
  //   23bd0004 8fb10000 23bd0004 8fb00000 23bd0004 8faf0000 23bd0004 8fae0000 23bd0004 8fad0000 23bd0004
  //   8fac0000 23bd0004 8fab0000 23bd0004 8faa0000 23bd0004 8fa90000 23bd0004 8fa80000 23bd0004 8fa70000
  //   23bd0004 8fa60000 23bd0004 8fa50000 23bd0004 8fa40000 23bd0004 8fa30000 23bd0004 8fa20000 23bd0004
  //   8fa10000 23bd0004 42000018 23bdfffc afa10000 23bdfffc afa20000 23bdfffc afa30000 23bdfffc afa40000
  //   23bdfffc afa50000 23bdfffc afa60000 23bdfffc afa70000 23bdfffc afa80000 23bdfffc afa90000 23bdfffc
  //   afaa0000 23bdfffc afab0000 23bdfffc afac0000 23bdfffc afad0000 23bdfffc afae0000 23bdfffc afaf0000
  //   23bdfffc afb00000 23bdfffc afb10000 23bdfffc afb20000 23bdfffc afb30000 23bdfffc afb40000 23bdfffc
  //   afb50000 23bdfffc afb60000 23bdfffc afb70000 23bdfffc afb80000 23bdfffc afb90000 20160002 20140006
  //   20150001 168020 108100 2149825 132020 20020022 c 1600fffa 295a022 1680fff7 8fb90000 23bd0004
  //   8fb80000 23bd0004 8fb70000 23bd0004 8fb60000 23bd0004 8fb50000 23bd0004 8fb40000 23bd0004 8fb30000
  //   23bd0004 8fb20000 23bd0004 8fb10000 23bd0004 8fb00000 23bd0004 8faf0000 23bd0004 8fae0000 23bd0004
  //   8fad0000 23bd0004 8fac0000 23bd0004 8fab0000 23bd0004 8faa0000 23bd0004 8fa90000 23bd0004 8fa80000
  //   23bd0004 8fa70000 23bd0004 8fa60000 23bd0004 8fa50000 23bd0004 8fa40000 23bd0004 8fa30000 23bd0004
  //   8fa20000 23bd0004 8fa10000 23bd0004 42000018 23bdfffc afa10000 23bdfffc afa20000 23bdfffc afa30000
  //   23bdfffc afa40000 23bdfffc afa50000 23bdfffc afa60000 23bdfffc afa70000 23bdfffc afa80000 23bdfffc
  //   afa90000 23bdfffc afaa0000 23bdfffc afab0000 23bdfffc afac0000 23bdfffc afad0000 23bdfffc afae0000
  //   23bdfffc afaf0000 23bdfffc afb00000 23bdfffc afb10000 23bdfffc afb20000 23bdfffc afb30000 23bdfffc
  //   afb40000 23bdfffc afb50000 23bdfffc afb60000 23bdfffc afb70000 23bdfffc afb80000 23bdfffc afb90000
  //   20160003 20140006 20150001 168020 108100 2149825 132020 20020022 c 1600fffa 295a022 1680fff7
  //   8fb90000 23bd0004 8fb80000 23bd0004 8fb70000 23bd0004 8fb60000 23bd0004 8fb50000 23bd0004 8fb40000
  //   23bd0004 8fb30000 23bd0004 8fb20000 23bd0004 8fb10000 23bd0004 8fb00000 23bd0004 8faf0000 23bd0004
  //   8fae0000 23bd0004 8fad0000 23bd0004 8fac0000 23bd0004 8fab0000 23bd0004 8faa0000 23bd0004 8fa90000
  //   23bd0004 8fa80000 23bd0004 8fa70000 23bd0004 8fa60000 23bd0004 8fa50000 23bd0004 8fa40000 23bd0004
  //   8fa30000 23bd0004 8fa20000 23bd0004 8fa10000 23bd0004 42000018 20110200 20020022 112020 c 2231ffff
  //   1620fffc 4*0 2002000a c 2002000a c
  //   rt
  //   rd
  //   数码管输出
  //   JMP
  //   OP
  //   Func
  //   Func
  //   Beq
  //   Bne
  //   MemToReg
  //   MemWrite
  //   AluOP
  //   AluSrcB
  //   RegWrite
  //   JAL
  //   RegDst
  //   Syscall
  //   总复位信号应将除ROM以外所有存储组件全部清零
  //   中断信号源及指示电路规范（优先级3>2>1>CPU(0）)
endmodule

module test (
);

  wire \_1号中断 , \_1号中断等待指示 , \_2号中断 , \_2号中断等待指示 , \_3号中断 , \_3号中断等待指示 , and_1_out, and_2_out, and_4_out,
       and_5_out, and_6_out, and_7_out, and_8_out, and_9_out, and_10_out, and_11_out, BLEZ, CLK,
       comparator_1_eq, comparator_2_eq, comparator_3_eq, comparator_4_eq, comparator_5_eq, comparator_6_eq,
       comparator_7_eq, comparator_8_gt, comparator_9_gt, compare, ERET, Go, HW_sel, JMP, JR, LOCK, MFC_0,
       mips_alu_1_equal, MTC_0, multiplexer_1_out, multiplexer_16_out, not_1_out, not_2_out, or_1_out,
       or_2_out, or_4_out, or_5_out, RST, SH, SignedExt, SRLV, Syscall, XORI, \硬布线控制器_1_alu_src ,
       \硬布线控制器_1_beq , \硬布线控制器_1_bne , \硬布线控制器_1_jal , \硬布线控制器_1_memtoreg , \硬布线控制器_1_memwrite ,
       \硬布线控制器_1_regdst , \硬布线控制器_1_regwrite ;
  wire [1:0] MFC_sel, MTC_sel;
  wire [3:0] multiplexer_19_out, multiplexer_20_out, \硬布线控制器_1_alu_op ;
  wire [4:0] multiplexer_5_out, multiplexer_6_out, multiplexer_8_out, multiplexer_9_out, multiplexer_15_out,
       RD, shamt;
  wire [15:0] \总周期数 , \无条件分支数 , \条件分支成功数 ;
  wire [27:2] rom_1_data;
  wire [31:0] adder_1_out, adder_2_out, bit_extender_1_out, bit_extender_2_out, LedData, mips_alu_1_result,
       mips_ram_1_p7, multiplexer_3_out, multiplexer_4_out, multiplexer_7_out, multiplexer_10_out,
       multiplexer_11_out, multiplexer_12_out, multiplexer_13_out, multiplexer_14_out, multiplexer_17_out,
       multiplexer_18_out, multiplexer_21_out, PC, PC_in, PC_Ori, R1, R2, shifter_1_out, siteData, undriven;
  wire [31:26] rom_1_data_2;

  Button \u_总复位  (.out(RST));
  Button \u_继续运行  (.out(Go));
  Clock clock_1 (.out(CLK));
  Register #(.width(32)) u_PC (.D(PC_in), .en(multiplexer_1_out), .Q(PC), .clk(CLK), .clr(RST));
  Multiplexer #(.enable("false")) multiplexer_1 (.in0(1'b1), .in1(1'b0), .out(multiplexer_1_out), .sel(and_1_out));
  and and_1 (and_1_out, LOCK, ~Go);  // AND_Gate
  Comparator #(.width(32)) comparator_1 (.a(R1), .b(32'h22), .eq(comparator_1_eq));  // open: gt, lt
  Hex_Digit_Display hex_digit_display_1 (.value(LedData[31:28]));  // open: dp
  Counter #(.width(16), .max('hffff)) counter_1 (
    .count(JMP), .Q(\无条件分支数 ), .clk(CLK), .clr(RST));  // open: load, D, carry
  Counter #(.width(16), .max('hffff)) counter_2 (
    .count(compare), .Q(\条件分支成功数 ), .clk(CLK), .clr(RST));  // open: load, D, carry
  Counter #(.width(16), .max('hffff)) counter_3 (
    .count(multiplexer_1_out), .Q(\总周期数 ), .clk(CLK), .clr(RST));  // open: load, D, carry
  Multiplexer #(.width(32), .enable("false")) multiplexer_2 (
    .in0(multiplexer_7_out), .in1(multiplexer_3_out), .out(PC_Ori), .sel(JMP));
  Multiplexer #(.width(32), .enable("false")) multiplexer_3 (
    .in0({4'b0000, rom_1_data[27:18], RD, shamt, rom_1_data[7:2], 2'b00}), .in1(R1), .out(multiplexer_3_out),
    .sel(JR));
  Hex_Digit_Display hex_digit_display_2 (.value(LedData[23:20]));  // open: dp
  Hex_Digit_Display hex_digit_display_3 (.value(LedData[27:24]));  // open: dp
  and and_2 (and_2_out, comparator_1_eq, Syscall);
  and and_3 (LOCK, ~comparator_1_eq, Syscall);  // AND_Gate
  Hex_Digit_Display hex_digit_display_4 (.value(LedData[19:16]));  // open: dp
  Hex_Digit_Display hex_digit_display_5 (.value(LedData[15:12]));  // open: dp
  ROM #(.addrWidth(10), .dataWidth(32)) rom_1 (
    .addr(PC[11:2]), .data({rom_1_data_2, rom_1_data[27:18], RD, shamt, rom_1_data[7:2]}));  // open: sel
  Adder #(.width(32)) adder_1 (.a(PC), .b(32'h4), .out(adder_1_out));  // open: cin, cout
  Multiplexer #(.width(32)) multiplexer_4 (
    .in0(undriven), .in1(R2), .out(multiplexer_4_out), .sel(and_2_out), .en(and_2_out));
  Hex_Digit_Display hex_digit_display_6 (.value(LedData[7:4]));  // open: dp
  Hex_Digit_Display hex_digit_display_7 (.value(LedData[11:8]));  // open: dp
  Multiplexer #(.width(5), .enable("false")) multiplexer_5 (
    .in0(rom_1_data[27:23]), .in1(5'b00010), .out(multiplexer_5_out), .sel(Syscall));
  Register #(.width(32)) register_1 (.D(multiplexer_4_out), .Q(LedData), .clk(CLK), .clr(RST));  // open: en
  Hex_Digit_Display hex_digit_display_8 (.value(LedData[3:0]));  // open: dp
  \硬布线控制器  \u_硬布线控制器_1  (
    .Func(rom_1_data[7:2]), .OP(rom_1_data_2), .ALU_OP(\硬布线控制器_1_alu_op ), .MemToReg(\硬布线控制器_1_memtoreg ),
    .MemWrite(\硬布线控制器_1_memwrite ), .ALU_SRC(\硬布线控制器_1_alu_src ), .RegWrite(\硬布线控制器_1_regwrite ),
    .SysCALL(Syscall), .SignedExt(SignedExt), .RegDst(\硬布线控制器_1_regdst ), .JR(JR), .JMP(JMP),
    .Beq(\硬布线控制器_1_beq ), .JAL(\硬布线控制器_1_jal ), .Bne(\硬布线控制器_1_bne ), .SRLV(SRLV), .XORI(XORI), .SH(SH),
    .BLEZ(BLEZ), .ERET(ERET), .RS(rom_1_data[27:23]), .RD(RD), .MFC_0(MFC_0), .MTC_0(MTC_0));
  Multiplexer #(.width(5), .enable("false")) multiplexer_6 (
    .in0(rom_1_data[22:18]), .in1(5'b00100), .out(multiplexer_6_out), .sel(Syscall));
  Multiplexer #(.width(32), .enable("false")) multiplexer_7 (
    .in0(adder_1_out), .in1(adder_2_out), .out(multiplexer_7_out), .sel(compare));
  Multiplexer #(.width(5), .enable("false")) multiplexer_8 (
    .in0(rom_1_data[22:18]), .in1(RD), .out(multiplexer_8_out), .sel(\硬布线控制器_1_regdst ));
  Multiplexer #(.width(5), .enable("false")) multiplexer_9 (
    .in0(multiplexer_8_out), .in1({5{1'b1}}), .out(multiplexer_9_out), .sel(\硬布线控制器_1_jal ));
  assign bit_extender_1_out = {{16{1'b0}}, {RD, shamt, rom_1_data[7:2]}};  // Bit_Extender bit_extender_1
  assign bit_extender_2_out = {{16{RD[4]}}, {RD, shamt, rom_1_data[7:2]}};  // Bit_Extender bit_extender_2
  // Probe on \总周期数 
  // Probe on \无条件分支数 
  // Probe on \条件分支成功数 
  Multiplexer #(.width(32), .enable("false")) multiplexer_10 (
    .in0(multiplexer_21_out), .in1(adder_1_out), .out(multiplexer_10_out), .sel(\硬布线控制器_1_jal ));
  // Probe on PC
  Multiplexer #(.width(32), .enable("false")) multiplexer_11 (
    .in0(multiplexer_10_out), .in1(siteData), .out(multiplexer_11_out), .sel(MFC_0));
  MutilLevel_Interrupt mutillevel_interrupt_1 (
    .clk(CLK), .ir1(\_1号中断 ), .PC(PC), .ir2(\_2号中断 ), .ir3(\_3号中断 ), .ERET(ERET), .nextPC(PC_Ori),
    .MFC_sel(MFC_sel), .MTC_sel(MTC_sel), .R2(R2), .PCout(PC_in), .siteData2reg(siteData), .w1(\_1号中断等待指示 ),
    .w2(\_2号中断等待指示 ), .w3(\_3号中断等待指示 ));
  // Probe on PC_in
  Button _1 (.out(\_1号中断 ));
  Button _2 (.out(\_2号中断 ));
  Button _3 (.out(\_3号中断 ));
  LED _1_2 (.in(\_1号中断等待指示 ));
  LED _2_2 (.in(\_2号中断等待指示 ));
  LED _3_2 (.in(\_3号中断等待指示 ));
  MIPS_Regifile mips_regifile_1 (
    .Din(multiplexer_11_out), .Clk(CLK), .R1(R1), .R2(R2), .WE(\硬布线控制器_1_regwrite ),
    .W_num(multiplexer_9_out), .R1_num(multiplexer_5_out), .R2_num(multiplexer_6_out));
  Multiplexer #(.width(32), .enable("false")) multiplexer_12 (
    .in0(bit_extender_1_out), .in1(bit_extender_2_out), .out(multiplexer_12_out), .sel(SignedExt));
  Multiplexer #(.width(32), .enable("false")) multiplexer_13 (
    .in0(R2), .in1(multiplexer_12_out), .out(multiplexer_13_out), .sel(\硬布线控制器_1_alu_src ));
  Shifter #(.width(32)) shifter_1 (.in(bit_extender_2_out), .\dist (5'b00010), .out(shifter_1_out));
  // Probe on \_1号中断 
  LED led_1 (.in(\硬布线控制器_1_memwrite ));
  LED led_2 (.in(SH));
  or or_1 (or_1_out, SH, BLEZ);
  Multiplexer #(.width(32), .enable("false")) multiplexer_14 (
    .in0(multiplexer_13_out), .in1({32{1'b0}}), .out(multiplexer_14_out), .sel(or_1_out));
  Multiplexer #(.width(5), .enable("false")) multiplexer_15 (
    .in0(shamt), .in1(R1[4:0]), .out(multiplexer_15_out), .sel(SRLV));
  Adder #(.width(32)) adder_2 (.a(shifter_1_out), .b(adder_1_out), .out(adder_2_out));  // open: cin, cout
  Comparator #(.width(5)) comparator_2 (.a(RD), .b(5'b00001), .eq(comparator_2_eq));  // open: gt, lt
  Comparator #(.width(5)) comparator_3 (.a(RD), .b(5'b00001), .eq(comparator_3_eq));  // open: gt, lt
  MIPS_ALU mips_alu_1 (
    .X(R1), .Y(multiplexer_14_out), .AluOP(\硬布线控制器_1_alu_op ), .Equal(mips_alu_1_equal),
    .Result({mips_alu_1_result[31:2], HW_sel, mips_alu_1_result[0]}), .shamt(multiplexer_15_out));  // open: Result_2
  assign MFC_sel = and_4_out ? 2'b00 : 2'bz;  // Controlled_Buffer controlled_buffer_1
  and and_4 (and_4_out, comparator_2_eq, MFC_0);
  assign MTC_sel = and_5_out ? 2'b00 : 2'bz;  // Controlled_Buffer controlled_buffer_2
  and and_5 (and_5_out, comparator_3_eq, MTC_0);
  and and_6 (and_6_out, \硬布线控制器_1_beq , mips_alu_1_equal);
  and and_7 (and_7_out, ~mips_alu_1_equal, \硬布线控制器_1_bne );  // AND_Gate
  or or_2 (or_2_out, mips_alu_1_equal, mips_alu_1_result[0]);
  Comparator #(.width(5)) comparator_4 (.a(RD), .b(5'b00010), .eq(comparator_4_eq));  // open: gt, lt
  assign MFC_sel = and_8_out ? 2'b01 : 2'bz;  // Controlled_Buffer controlled_buffer_3
  and and_8 (and_8_out, comparator_4_eq, MFC_0);
  Comparator #(.width(5)) comparator_5 (.a(RD), .b(5'b00010), .eq(comparator_5_eq));  // open: gt, lt
  and and_9 (and_9_out, comparator_5_eq, MTC_0);
  Multiplexer #(.enable("false")) multiplexer_16 (.in0(1'b0), .in1(or_2_out), .out(multiplexer_16_out), .sel(BLEZ));
  Multiplexer #(.width(32), .enable("false")) multiplexer_17 (
    .in0({{16{1'b0}}, R2[15:0]}), .in1({R2[15:0], {16{1'b0}}}), .out(multiplexer_17_out), .sel(HW_sel));
  // Probe on MTC_sel
  assign MTC_sel = and_9_out ? 2'b01 : 2'bz;  // Controlled_Buffer controlled_buffer_4
  or or_3 (compare, and_6_out, and_7_out, multiplexer_16_out);
  Multiplexer #(.width(32), .enable("false")) multiplexer_18 (
    .in0(R2), .in1(multiplexer_17_out), .out(multiplexer_18_out), .sel(SH));
  Comparator #(.width(5)) comparator_6 (.a(RD), .b(5'b00011), .eq(comparator_6_eq));  // open: gt, lt
  Comparator #(.width(5)) comparator_7 (.a(RD), .b(5'b00011), .eq(comparator_7_eq));  // open: gt, lt
  Multiplexer #(.width(4), .enable("false")) multiplexer_19 (
    .in0(4'b1111), .in1(multiplexer_20_out), .out(multiplexer_19_out), .sel(SH));
  Multiplexer #(.width(4), .enable("false")) multiplexer_20 (
    .in0(4'b0011), .in1(4'b1100), .out(multiplexer_20_out), .sel(HW_sel));
  assign MFC_sel = and_10_out ? 2'b10 : 2'bz;  // Controlled_Buffer controlled_buffer_5
  and and_10 (and_10_out, comparator_6_eq, MFC_0);
  assign MTC_sel = and_11_out ? 2'b10 : 2'bz;  // Controlled_Buffer controlled_buffer_6
  and and_11 (and_11_out, comparator_7_eq, MTC_0);
  // MIPS_RAM mips_ram_1: pin names not known; wires that end beside it: mips_alu_1_result[21:2], multiplexer_18_out, \硬布线控制器_1_memwrite , multiplexer_19_out, CLK, RST, mips_ram_1_p7
  Comparator #(.width(5)) comparator_8 (.a(RD), .b(5'b00011), .gt(comparator_8_gt));  // open: eq, lt
  Multiplexer #(.width(32), .enable("false")) multiplexer_21 (
    .in0({mips_alu_1_result[31:2], HW_sel, mips_alu_1_result[0]}), .in1(mips_ram_1_p7),
    .out(multiplexer_21_out), .sel(\硬布线控制器_1_memtoreg ));
  or or_4 (or_4_out, comparator_8_gt, not_1_out);
  not not_1 (not_1_out, MFC_0);
  Comparator #(.width(5)) comparator_9 (.a(RD), .b(5'b00011), .gt(comparator_9_gt));  // open: eq, lt
  not not_2 (not_2_out, MTC_0);
  assign MFC_sel = or_4_out ? 2'b11 : 2'bz;  // Controlled_Buffer controlled_buffer_7
  assign MTC_sel = or_5_out ? 2'b11 : 2'bz;  // Controlled_Buffer controlled_buffer_8
  or or_5 (or_5_out, comparator_9_gt, not_2_out);

  // Notes on the sheet:
  //   数码管输出应该用寄存器锁存，否则显示数据只能一闪而过
  //   可以通过项目增加Logisim库的方式将前几次实验完成的电路作为子电路引入到本电路中使用
  //   指令存储器
  //   指令字
  //   contents of rom_1 (hex, n*v repeats v):
  //   8000d54 23bdfffc afa10000 23bdfffc afa20000 23bdfffc afa30000 23bdfffc afa40000 23bdfffc afa50000
  //   23bdfffc afa60000 23bdfffc afa70000 23bdfffc afa80000 23bdfffc afa90000 23bdfffc afaa0000 23bdfffc
  //   afab0000 23bdfffc afac0000 23bdfffc afad0000 23bdfffc afae0000 23bdfffc afaf0000 23bdfffc afb00000
  //   23bdfffc afb10000 23bdfffc afb20000 23bdfffc afb30000 23bdfffc afb40000 23bdfffc afb50000 23bdfffc
  //   afb60000 23bdfffc afb70000 23bdfffc afb80000 23bdfffc afb90000 20160001 20140006 20150001 168020
  //   108100 2149825 132020 20020022 c 1600fffa 295a022 1680fff7 8fb90000 23bd0004 8fb80000 23bd0004
  //   8fb70000 23bd0004 8fb60000 23bd0004 8fb50000 23bd0004 8fb40000 23bd0004 8fb30000 23bd0004 8fb20000
  //   23bd0004 8fb10000 23bd0004 8fb00000 23bd0004 8faf0000 23bd0004 8fae0000 23bd0004 8fad0000 23bd0004
  //   8fac0000 23bd0004 8fab0000 23bd0004 8faa0000 23bd0004 8fa90000 23bd0004 8fa80000 23bd0004 8fa70000
  //   23bd0004 8fa60000 23bd0004 8fa50000 23bd0004 8fa40000 23bd0004 8fa30000 23bd0004 8fa20000 23bd0004
  //   8fa10000 23bd0004 42000018 23bdfffc afa10000 23bdfffc afa20000 23bdfffc afa30000 23bdfffc afa40000
  //   23bdfffc afa50000 23bdfffc afa60000 23bdfffc afa70000 23bdfffc afa80000 23bdfffc afa90000 23bdfffc
  //   afaa0000 23bdfffc afab0000 23bdfffc afac0000 23bdfffc afad0000 23bdfffc afae0000 23bdfffc afaf0000
  //   23bdfffc afb00000 23bdfffc afb10000 23bdfffc afb20000 23bdfffc afb30000 23bdfffc afb40000 23bdfffc
  //   afb50000 23bdfffc afb60000 23bdfffc afb70000 23bdfffc afb80000 23bdfffc afb90000 20160002 20140006
  //   20150001 168020 108100 2149825 132020 20020022 c 1600fffa 295a022 1680fff7 8fb90000 23bd0004
  //   8fb80000 23bd0004 8fb70000 23bd0004 8fb60000 23bd0004 8fb50000 23bd0004 8fb40000 23bd0004 8fb30000
  //   23bd0004 8fb20000 23bd0004 8fb10000 23bd0004 8fb00000 23bd0004 8faf0000 23bd0004 8fae0000 23bd0004
  //   8fad0000 23bd0004 8fac0000 23bd0004 8fab0000 23bd0004 8faa0000 23bd0004 8fa90000 23bd0004 8fa80000
  //   23bd0004 8fa70000 23bd0004 8fa60000 23bd0004 8fa50000 23bd0004 8fa40000 23bd0004 8fa30000 23bd0004
  //   8fa20000 23bd0004 8fa10000 23bd0004 42000018 23bdfffc afa10000 23bdfffc afa20000 23bdfffc afa30000
  //   23bdfffc afa40000 23bdfffc afa50000 23bdfffc afa60000 23bdfffc afa70000 23bdfffc afa80000 23bdfffc
  //   afa90000 23bdfffc afaa0000 23bdfffc afab0000 23bdfffc afac0000 23bdfffc afad0000 23bdfffc afae0000
  //   23bdfffc afaf0000 23bdfffc afb00000 23bdfffc afb10000 23bdfffc afb20000 23bdfffc afb30000 23bdfffc
  //   afb40000 23bdfffc afb50000 23bdfffc afb60000 23bdfffc afb70000 23bdfffc afb80000 23bdfffc afb90000
  //   20160003 20140006 20150001 168020 108100 2149825 132020 20020022 c 1600fffa 295a022 1680fff7
  //   8fb90000 23bd0004 8fb80000 23bd0004 8fb70000 23bd0004 8fb60000 23bd0004 8fb50000 23bd0004 8fb40000
  //   23bd0004 8fb30000 23bd0004 8fb20000 23bd0004 8fb10000 23bd0004 8fb00000 23bd0004 8faf0000 23bd0004
  //   8fae0000 23bd0004 8fad0000 23bd0004 8fac0000 23bd0004 8fab0000 23bd0004 8faa0000 23bd0004 8fa90000
  //   23bd0004 8fa80000 23bd0004 8fa70000 23bd0004 8fa60000 23bd0004 8fa50000 23bd0004 8fa40000 23bd0004
  //   8fa30000 23bd0004 8fa20000 23bd0004 8fa10000 23bd0004 42000018 20110200 20020022 112020 c 2231ffff
  //   1620fffc 4*0 2002000a c 2002000a c
  //   数码管输出
  //   JMP
  //   OP
  //   Func
  //   OP
  //   Func
  //   rs
  //   rt
  //   rd
  //   Beq
  //   Bne
  //   MemToReg
  //   MemWrite
  //   AluOP
  //   AluSrcB
  //   RegWrite
  //   JAL
  //   RegDst
  //   Syscall
  //   总复位信号应将除ROM以外所有存储组件全部清零
  //   中断信号源及指示电路规范（优先级3>2>1>CPU(0）)
endmodule

module \流水线中断  (
  input  in_1
);

  wire and_1_out, and_2_out, and_3_out, and_4_out, and_5_out, and_6_out, and_7_out, and_8_out, and_9_out,
       and_10_out, CLK, comparator_1_eq, comparator_2_eq, compare, en, EX_BLEZ, EX_ERET, EX_JMP, EX_RegDst,
       EX_RegWrite, EX_SH, EX_SRLV, EX_Syscall, Go, ID_BLEZ, ID_ERET, ID_SH, ID_SRLV, ID_XORI, IR1, IR2, IR3,
       JAL, JR, LOCK, MEM_JAL, Mem_MemWrite, MEM_RegDst, MEM_RegWrite, MEM_SH, mips_alu_1_equal,
       multiplexer_26_out, nop, not_1_out, or_1_out, or_2_out, RST, SignedExt, W1, W2, W3, WB_JAL, WB_RegDst,
       WB_RegWrite, WB_Syscall, \数据相关 ;
  wire [1:0] Forward_A, Forward_B;
  wire [3:0] multiplexer_29_out, multiplexer_30_out;
  wire [4:0] ex_mem_1_wreg_, EX_rd, EX_rs, EX_rt, EX_WriteReg, id_ex_1_shamt_, id_ex_1_wreg_, ID_R1_num,
       ID_R2_num, MEM_rd, MEM_rt, mem_wb_1_wreg_, MEM_WriteReg, multiplexer_7_out, multiplexer_9_out,
       multiplexer_11_out, multiplexer_13_out, multiplexer_19_out, multiplexer_20_out, multiplexer_21_out,
       multiplexer_22_out, WB_rd, WB_rt, WB_WriteReg;
  wire [5:0] EX_Func, EX_OP, Func, OP;
  wire [10:0] id_ex_1_cont_, mem_wb_1_cont_;
  wire [10:6] id_ex_1_ir_;
  wire [13:0] ex_mem_1_cont_;
  wire [14:0] \硬布线控制器_1_beq ;
  wire [15:0] \LoadUse次数 , \总周期数 , \插入气泡数 , \无条件分支数 , \条件分支成功数 ;
  wire [25:0] id_ex_1_imm26_;
  wire [25:6] if_id_1_instru_;
  wire [31:0] adder_1_out, adder_2_out, adder_3_out, ALUOUT, bit_extender_1_out, bit_extender_2_out,
       ex_mem_1_ir_, ex_mem_1_rd1_, ex_mem_1_rd2_, EX_PC, EXR1, id_ex_1_imm_, id_ex_1_imme_, id_ex_1_pc_4_,
       id_ex_1_rd1_, id_ex_1_rd2_, ID_PC, if_id_1_pc_4_, IF_PC, LedData, Mem_ALU_Result, MEM_PC,
       mem_wb_1_ir_, mips_probe_1_p1, mips_ram_1_p7, multiplexer_3_out, multiplexer_4_out,
       multiplexer_10_out, multiplexer_12_out, multiplexer_14_out, multiplexer_16_out, multiplexer_17_out,
       multiplexer_18_out, multiplexer_27_out, multiplexer_28_out, PC_in, PC_Ori, R1, R2, shifter_1_out,
       undriven, WB_ALU_Result, WB_Mem_ReadData, WB_PC, WB_RegDin, WBR1, WBR2;

  Button \u_总复位  (.out(RST));
  Button _1 (.out(IR1));
  Button _2 (.out(IR2));
  Button _3 (.out(IR3));
  and and_1 (and_1_out, en, ~\数据相关 );  // AND_Gate
  Button \u_继续运行  (.out(Go));
  LED led_1 (.in(W1));
  LED led_2 (.in(W2));
  LED led_3 (.in(W3));
  Register #(.width(32)) PC (.D(PC_in), .en(and_1_out), .Q(IF_PC), .clk(CLK), .clr(RST));
  Multiplexer #(.enable("false")) multiplexer_1 (.in0(1'b1), .in1(1'b0), .out(en), .sel(and_2_out));
  and and_2 (and_2_out, LOCK, ~Go);  // AND_Gate
  Counter #(.width(16), .max('hffff)) counter_1 (.count(en), .Q(\总周期数 ), .clk(CLK), .clr(RST));  // open: load, D, carry
  Multiplexer #(.width(32), .enable("false")) multiplexer_2 (
    .in0(multiplexer_4_out), .in1(multiplexer_3_out), .out(PC_Ori), .sel(EX_JMP));
  Multiplexer #(.width(32), .enable("false")) multiplexer_3 (
    .in0({4'b0000, id_ex_1_imm26_, 2'b00}), .in1(EXR1), .out(multiplexer_3_out), .sel(JR));
  Hex_Digit_Display hex_digit_display_1 (.value(LedData[31:28]));  // open: dp
  and and_3 (and_3_out, ~LOCK, EX_JMP);  // AND_Gate
  and and_4 (and_4_out, ~LOCK, compare);  // AND_Gate
  Counter #(.width(16), .max('hffff)) counter_2 (
    .count(and_5_out), .Q(\插入气泡数 ), .clk(CLK), .clr(RST));  // open: load, D, carry
  and and_5 (and_5_out, ~LOCK, \数据相关 );  // AND_Gate
  SingleLevel_Interrupt singlelevel_interrupt_1 (
    .clk(CLK), .ir1(IR1), .PC(EX_PC), .PCout(PC_in), .ir2(IR2), .ir3(IR3), .ERET(ID_ERET), .nextPC(PC_Ori),
    .w1(W1), .w2(W2), .w3(W3));  // open: out_9
  Hex_Digit_Display hex_digit_display_2 (.value(LedData[27:24]));  // open: dp
  Hex_Digit_Display hex_digit_display_3 (.value(LedData[23:20]));  // open: dp
  Counter #(.width(16), .max('hffff)) counter_3 (
    .count(and_3_out), .Q(\无条件分支数 ), .clk(CLK), .clr(RST));  // open: load, D, carry
  Counter #(.width(16), .max('hffff)) counter_4 (
    .count(and_4_out), .Q(\条件分支成功数 ), .clk(CLK), .clr(RST));  // open: load, D, carry
  // Mips_Probe mips_probe_1: pin names not known; wires that end beside it: mips_probe_1_p1
  ROM #(.addrWidth(10), .dataWidth(32)) rom_1 (.addr(IF_PC[11:2]), .data(mips_probe_1_p1));  // open: sel
  Multiplexer #(.width(32), .enable("false")) multiplexer_4 (
    .in0(adder_1_out), .in1(adder_3_out), .out(multiplexer_4_out), .sel(compare));
  Hex_Digit_Display hex_digit_display_4 (.value(LedData[15:12]));  // open: dp
  Hex_Digit_Display hex_digit_display_5 (.value(LedData[19:16]));  // open: dp
  and and_6 (and_6_out, en, ~\数据相关 );  // AND_Gate
  Adder #(.width(32)) adder_1 (.a(IF_PC), .b(32'h4), .out(adder_1_out));  // open: cin, cout
  Hex_Digit_Display hex_digit_display_6 (.value(LedData[11:8]));  // open: dp
  Hex_Digit_Display hex_digit_display_7 (.value(LedData[7:4]));  // open: dp
  Clock clock_1 (.out(CLK));
  IF_ID if_id_1 (
    .instru(mips_probe_1_p1), .PC_4(adder_1_out), .clk(CLK), .rst(RST),
    .instru_({OP, if_id_1_instru_, Func}), .PC_4_(if_id_1_pc_4_), .PC(IF_PC), .PC_(ID_PC), .en(and_6_out),
    .halt(nop));  // open: 预测跳转, 预测地址, Hit, HitPos, 预测跳转_, 预测地址_, Hit_, HitPos_
  Hex_Digit_Display hex_digit_display_8 (.value(LedData[3:0]));  // open: dp
  // Probe on {OP, if_id_1_instru_, Func}
  Comparator #(.width(32)) comparator_1 (.a(WBR1), .b(32'h22), .eq(comparator_1_eq));  // open: gt, lt
  \硬布线控制器  \u_硬布线控制器_1  (
    .Func(Func), .OP(OP), .ALU_OP(\硬布线控制器_1_beq [9:6]), .MemToReg(\硬布线控制器_1_beq [4]),
    .MemWrite(\硬布线控制器_1_beq [5]), .ALU_SRC(\硬布线控制器_1_beq [10]), .RegWrite(\硬布线控制器_1_beq [14]),
    .SysCALL(\硬布线控制器_1_beq [13]), .SignedExt(SignedExt), .RegDst(\硬布线控制器_1_beq [12]), .JR(\硬布线控制器_1_beq [2]),
    .JMP(\硬布线控制器_1_beq [3]), .Beq(\硬布线控制器_1_beq [0]), .JAL(\硬布线控制器_1_beq [11]), .Bne(\硬布线控制器_1_beq [1]),
    .SRLV(ID_SRLV), .XORI(ID_XORI), .SH(ID_SH), .BLEZ(ID_BLEZ), .ERET(ID_ERET));  // open: RS, RD, MFC_0, MTC_0
  Multiplexer #(.width(5), .enable("false")) multiplexer_5 (
    .in0(if_id_1_instru_[25:21]), .in1(5'b00010), .out(ID_R1_num), .sel(\硬布线控制器_1_beq [13]));
  Multiplexer #(.width(5), .enable("false")) multiplexer_6 (
    .in0(if_id_1_instru_[20:16]), .in1(5'b00100), .out(ID_R2_num), .sel(\硬布线控制器_1_beq [13]));
  // Probe on \总周期数 
  // Probe on \无条件分支数 
  // Probe on \条件分支成功数 
  // Probe on \插入气泡数 
  // Probe on \LoadUse次数 
  Multiplexer #(.width(5), .enable("false")) multiplexer_7 (
    .in0(if_id_1_instru_[20:16]), .in1(if_id_1_instru_[15:11]), .out(multiplexer_7_out),
    .sel(\硬布线控制器_1_beq [12]));
  // Probe on WB_RegDin
  and and_7 (and_7_out, comparator_1_eq, WB_Syscall);
  and and_8 (and_8_out, ~comparator_1_eq, WB_Syscall);  // AND_Gate
  Multiplexer #(.enable("false")) multiplexer_8 (.in0(and_8_out), .in1(comparator_2_eq), .out(LOCK), .sel(in_1));
  Comparator #(.width(32), .mode("unsigned")) comparator_2 (
    .a(EX_PC), .b(32'h3064), .eq(comparator_2_eq));  // open: gt, lt
  // Probe on IF_PC[11:0]
  // Probe on ID_R1_num
  // Probe on ID_R2_num
  Multiplexer #(.width(5), .enable("false")) multiplexer_9 (
    .in0(multiplexer_7_out), .in1({5{1'b1}}), .out(multiplexer_9_out), .sel(\硬布线控制器_1_beq [11]));
  Adder #(.width(32)) adder_2 (.a(WB_PC), .b(32'h4), .out(adder_2_out));  // open: cin, cout
  Register #(.width(32)) register_1 (.D(multiplexer_10_out), .Q(LedData), .clk(CLK), .clr(RST));  // open: en
  Multiplexer #(.width(32)) multiplexer_10 (
    .in0(undriven), .in1(WBR2), .out(multiplexer_10_out), .sel(and_7_out), .en(and_7_out));
  Multiplexer #(.width(5), .enable("false")) multiplexer_11 (
    .in0(EX_rs), .in1(5'b00010), .out(multiplexer_11_out), .sel(EX_Syscall));
  // Probe on ID_PC[11:0]
  Multiplexer #(.width(32), .enable("false")) multiplexer_12 (
    .in0(WB_RegDin), .in1(adder_2_out), .out(multiplexer_12_out), .sel(WB_JAL));
  // Probe on mem_wb_1_wreg_
  Multiplexer #(.width(5), .enable("false")) multiplexer_13 (
    .in0(EX_rt), .in1(5'b00100), .out(multiplexer_13_out), .sel(EX_Syscall));
  // Probe on EX_PC[11:0]
  // Probe on MEM_PC[11:0]
  MIPS_Regifile mips_regifile_1 (
    .Din(multiplexer_12_out), .Clk(CLK), .R1(R1), .R2(R2), .WE(WB_RegWrite), .W_num(mem_wb_1_wreg_),
    .R1_num(ID_R1_num), .R2_num(ID_R2_num));
  assign bit_extender_1_out = {{16{1'b0}}, {if_id_1_instru_[15:6], Func}};  // Bit_Extender bit_extender_1
  assign bit_extender_2_out = {{16{if_id_1_instru_[15]}}, {if_id_1_instru_[15:6], Func}};  // Bit_Extender bit_extender_2
  // Probe on WB_PC[11:0]
  // Probe on R1
  // Probe on R2
  Multiplexer #(.width(32), .enable("false")) multiplexer_14 (
    .in0(bit_extender_1_out), .in1(bit_extender_2_out), .out(multiplexer_14_out), .sel(SignedExt));
  ID_EX id_ex_1 (
    .RD1(R1), .RD2(R2), .imm(bit_extender_2_out), .PC_4(if_id_1_pc_4_), .clk(CLK), .halt(or_1_out),
    .RD1_(id_ex_1_rd1_), .RD2_(id_ex_1_rd2_), .imm_(id_ex_1_imm_), .PC_4_(id_ex_1_pc_4_),
    .WReg(multiplexer_9_out), .WReg_(id_ex_1_wreg_), .immE(multiplexer_14_out), .immE_(id_ex_1_imme_),
    .cont(\硬布线控制器_1_beq ),
    .cont_({EX_RegWrite, EX_Syscall, EX_RegDst, JAL, id_ex_1_cont_[10:4], EX_JMP, JR, id_ex_1_cont_[1:0]}),
    .shamt(if_id_1_instru_[10:6]), .shamt_(id_ex_1_shamt_), .PC(ID_PC), .PC_(EX_PC), .en(en),
    .imm26({if_id_1_instru_, Func}), .imm26_(id_ex_1_imm26_), .IR({OP, if_id_1_instru_, Func}),
    .IR_({EX_OP, EX_rs, EX_rt, EX_rd, id_ex_1_ir_, EX_Func}), .SRLV(ID_SRLV), .SRLV_(EX_SRLV), .SH(ID_SH),
    .SH_(EX_SH), .BLEZ(ID_BLEZ), .BLEZ_(EX_BLEZ), .rst(RST), .ERET(ID_ERET), .ERET_(EX_ERET));  // open: 预测跳转, 预测跳转_, 预测地址, 预测地址_, Hit, Hit_, HitPos, HitPos_
  \数据相关检测  \u_数据相关检测_1  (
    .ID_OP(OP), .EX_WriteReg_num(EX_WriteReg), .EX_RegWrite(EX_RegWrite), .MEM_WriteReg_num(MEM_WriteReg),
    .MEM_RegWrite(MEM_RegWrite), .ID_FUNC(Func), .ID_R1_num(ID_R1_num), .ID_R2_num(ID_R2_num), .EX_OP(EX_OP),
    .\Load_Use相关 (\数据相关 ), .WB_WriteReg_num(WB_WriteReg), .WB_RegWrite(WB_RegWrite), .Forward1(Forward_A),
    .Forward2(Forward_B), .EX_R1_num(multiplexer_11_out), .EX_R2_num(multiplexer_13_out), .EX_FUNC(EX_Func));  // open: 数据相关, MEM相关, EX相关
  // Probe on Forward_A
  // Probe on EX_PC
  Multiplexer #(.select(2), .width(32), .enable("false")) multiplexer_15 (
    .in0(id_ex_1_rd1_), .in1(Mem_ALU_Result), .in2(WB_RegDin), .out(EXR1), .sel(Forward_A));  // open: in3
  Multiplexer #(.select(2), .width(32), .enable("false")) multiplexer_16 (
    .in0(id_ex_1_rd2_), .in1(Mem_ALU_Result), .in2(WB_RegDin), .out(multiplexer_16_out), .sel(Forward_B));  // open: in3
  // Probe on EXR1
  Multiplexer #(.width(32), .enable("false")) multiplexer_17 (
    .in0(multiplexer_16_out), .in1(id_ex_1_imme_), .out(multiplexer_17_out), .sel(id_ex_1_cont_[10]));
  or or_1 (or_1_out, nop, \数据相关 );
  Multiplexer #(.width(32), .enable("false")) multiplexer_18 (
    .in0(multiplexer_17_out), .in1({32{1'b0}}), .out(multiplexer_18_out), .sel(EX_BLEZ));
  Shifter #(.width(32)) shifter_1 (.in(id_ex_1_imm_), .\dist (5'b00010), .out(shifter_1_out));
  Multiplexer #(.width(5), .enable("false")) multiplexer_19 (
    .in0(EX_rt), .in1(EX_rd), .out(multiplexer_19_out), .sel(EX_RegDst));
  Multiplexer #(.width(5), .enable("false")) multiplexer_20 (
    .in0(MEM_rt), .in1(MEM_rd), .out(multiplexer_20_out), .sel(MEM_RegDst));
  Multiplexer #(.width(5), .enable("false")) multiplexer_21 (
    .in0(WB_rt), .in1(WB_rd), .out(multiplexer_21_out), .sel(WB_RegDst));
  MIPS_ALU mips_alu_1 (
    .X(EXR1), .Y(multiplexer_18_out), .AluOP(id_ex_1_cont_[9:6]), .Equal(mips_alu_1_equal), .Result(ALUOUT),
    .shamt(multiplexer_22_out));  // open: Result_2
  Multiplexer #(.width(5), .enable("false")) multiplexer_22 (
    .in0(id_ex_1_shamt_), .in1(EXR1[4:0]), .out(multiplexer_22_out), .sel(EX_SRLV));
  Adder #(.width(32)) adder_3 (.a(shifter_1_out), .b(id_ex_1_pc_4_), .out(adder_3_out));  // open: cin, cout
  Multiplexer #(.width(5), .enable("false")) multiplexer_23 (
    .in0(multiplexer_19_out), .in1({5{1'b1}}), .out(EX_WriteReg), .sel(JAL));
  Multiplexer #(.width(5), .enable("false")) multiplexer_24 (
    .in0(multiplexer_20_out), .in1({5{1'b1}}), .out(MEM_WriteReg), .sel(MEM_JAL));
  Multiplexer #(.width(5), .enable("false")) multiplexer_25 (
    .in0(multiplexer_21_out), .in1({5{1'b1}}), .out(WB_WriteReg), .sel(WB_JAL));
  and and_9 (and_9_out, id_ex_1_cont_[0], mips_alu_1_equal);
  and and_10 (and_10_out, ~mips_alu_1_equal, id_ex_1_cont_[1]);  // AND_Gate
  or or_2 (or_2_out, mips_alu_1_equal, ALUOUT[0]);
  // Probe on EXR1
  // Probe on ALUOUT
  // Probe on multiplexer_16_out
  Multiplexer #(.enable("false")) multiplexer_26 (.in0(1'b0), .in1(not_1_out), .out(multiplexer_26_out), .sel(EX_BLEZ));
  not not_1 (not_1_out, or_2_out);
  EX_MEM ex_mem_1 (
    .cont({EX_RegWrite, EX_Syscall, EX_RegDst, JAL, id_ex_1_cont_[10:4], EX_JMP, JR, id_ex_1_cont_[1:0]}),
    .ALUout(ALUOUT), .RD2(multiplexer_16_out), .WReg(id_ex_1_wreg_), .clk(CLK), .halt(RST),
    .cont_({MEM_RegWrite, ex_mem_1_cont_[13], MEM_RegDst, MEM_JAL, ex_mem_1_cont_[10:6], Mem_MemWrite, ex_mem_1_cont_[4:0]}),
    .ALUout_(Mem_ALU_Result), .RD2_(ex_mem_1_rd2_), .WReg_(ex_mem_1_wreg_), .RD1(EXR1), .RD1_(ex_mem_1_rd1_),
    .PC(EX_PC), .PC_(MEM_PC), .en(en), .IR({EX_OP, EX_rs, EX_rt, EX_rd, id_ex_1_ir_, EX_Func}),
    .IR_({ex_mem_1_ir_[31:21], MEM_rt, MEM_rd, ex_mem_1_ir_[10:0]}), .LH(EX_SH), .LH_(MEM_SH), .rst(RST));
  or or_3 (compare, and_9_out, and_10_out, multiplexer_26_out);
  or or_4 (nop, compare, JR, EX_JMP);
  // Probe on Mem_ALU_Result
  // Probe on ex_mem_1_rd1_
  Multiplexer #(.width(32), .enable("false")) multiplexer_27 (
    .in0({{16{1'b0}}, ex_mem_1_rd2_[15:0]}), .in1({ex_mem_1_rd2_[15:0], {16{1'b0}}}),
    .out(multiplexer_27_out), .sel(Mem_ALU_Result[1]));
  Multiplexer #(.width(32), .enable("false")) multiplexer_28 (
    .in0(ex_mem_1_rd2_), .in1(multiplexer_27_out), .out(multiplexer_28_out), .sel(MEM_SH));
  Multiplexer #(.width(4), .enable("false")) multiplexer_29 (
    .in0(4'b1111), .in1(multiplexer_30_out), .out(multiplexer_29_out), .sel(MEM_SH));
  Multiplexer #(.width(4), .enable("false")) multiplexer_30 (
    .in0(4'b0011), .in1(4'b1100), .out(multiplexer_30_out), .sel(Mem_ALU_Result[1]));
  // MIPS_RAM mips_ram_1: pin names not known; wires that end beside it: Mem_ALU_Result[21:2], multiplexer_28_out, Mem_MemWrite, multiplexer_29_out, CLK, RST, mips_ram_1_p7
  MEM_WB mem_wb_1 (
    .cont({MEM_RegWrite, ex_mem_1_cont_[13], MEM_RegDst, MEM_JAL, ex_mem_1_cont_[10:6], Mem_MemWrite, ex_mem_1_cont_[4:0]}),
    .ALUout(Mem_ALU_Result), .MEMout(mips_ram_1_p7), .WReg(ex_mem_1_wreg_), .clk(CLK), .halt(RST),
    .cont_({WB_RegWrite, WB_Syscall, WB_RegDst, WB_JAL, mem_wb_1_cont_}), .ALUout_(WB_ALU_Result),
    .MEMout_(WB_Mem_ReadData), .WReg_(mem_wb_1_wreg_), .RD1(ex_mem_1_rd1_), .RD1_(WBR1), .RD2(ex_mem_1_rd2_),
    .RD2_(WBR2), .PC(MEM_PC), .PC_(WB_PC), .en(en),
    .IR({ex_mem_1_ir_[31:21], MEM_rt, MEM_rd, ex_mem_1_ir_[10:0]}),
    .IR_({mem_wb_1_ir_[31:21], WB_rt, WB_rd, mem_wb_1_ir_[10:0]}), .rst(RST));
  Multiplexer #(.width(32), .enable("false")) multiplexer_31 (
    .in0(WB_ALU_Result), .in1(WB_Mem_ReadData), .out(WB_RegDin), .sel(mem_wb_1_cont_[4]));
  // Probe on WBR1
  // Probe on WBR2

  // Other names for the same wires on the sheet: CHANGE = in_1; SW_sel = Mem_ALU_Result[1]; PC[31:0] = IF_PC

  // Notes on the sheet:
  //   中断源
  //   中断等待指示
  //   指令存储器
  //   contents of rom_1 (hex, n*v repeats v):
  //   8000d54 23bdfffc afa10000 23bdfffc afa20000 23bdfffc afa30000 23bdfffc afa40000 23bdfffc afa50000
  //   23bdfffc afa60000 23bdfffc afa70000 23bdfffc afa80000 23bdfffc afa90000 23bdfffc afaa0000 23bdfffc
  //   afab0000 23bdfffc afac0000 23bdfffc afad0000 23bdfffc afae0000 23bdfffc afaf0000 23bdfffc afb00000
  //   23bdfffc afb10000 23bdfffc afb20000 23bdfffc afb30000 23bdfffc afb40000 23bdfffc afb50000 23bdfffc
  //   afb60000 23bdfffc afb70000 23bdfffc afb80000 23bdfffc afb90000 20160001 20140006 20150001 168020
  //   108100 2149825 132020 20020022 c 1600fffa 295a022 1680fff7 8fb90000 23bd0004 8fb80000 23bd0004
  //   8fb70000 23bd0004 8fb60000 23bd0004 8fb50000 23bd0004 8fb40000 23bd0004 8fb30000 23bd0004 8fb20000
  //   23bd0004 8fb10000 23bd0004 8fb00000 23bd0004 8faf0000 23bd0004 8fae0000 23bd0004 8fad0000 23bd0004
  //   8fac0000 23bd0004 8fab0000 23bd0004 8faa0000 23bd0004 8fa90000 23bd0004 8fa80000 23bd0004 8fa70000
  //   23bd0004 8fa60000 23bd0004 8fa50000 23bd0004 8fa40000 23bd0004 8fa30000 23bd0004 8fa20000 23bd0004
  //   8fa10000 23bd0004 42000018 23bdfffc afa10000 23bdfffc afa20000 23bdfffc afa30000 23bdfffc afa40000
  //   23bdfffc afa50000 23bdfffc afa60000 23bdfffc afa70000 23bdfffc afa80000 23bdfffc afa90000 23bdfffc
  //   afaa0000 23bdfffc afab0000 23bdfffc afac0000 23bdfffc afad0000 23bdfffc afae0000 23bdfffc afaf0000
  //   23bdfffc afb00000 23bdfffc afb10000 23bdfffc afb20000 23bdfffc afb30000 23bdfffc afb40000 23bdfffc
  //   afb50000 23bdfffc afb60000 23bdfffc afb70000 23bdfffc afb80000 23bdfffc afb90000 20160002 20140006
  //   20150001 168020 108100 2149825 132020 20020022 c 1600fffa 295a022 1680fff7 8fb90000 23bd0004
  //   8fb80000 23bd0004 8fb70000 23bd0004 8fb60000 23bd0004 8fb50000 23bd0004 8fb40000 23bd0004 8fb30000
  //   23bd0004 8fb20000 23bd0004 8fb10000 23bd0004 8fb00000 23bd0004 8faf0000 23bd0004 8fae0000 23bd0004
  //   8fad0000 23bd0004 8fac0000 23bd0004 8fab0000 23bd0004 8faa0000 23bd0004 8fa90000 23bd0004 8fa80000
  //   23bd0004 8fa70000 23bd0004 8fa60000 23bd0004 8fa50000 23bd0004 8fa40000 23bd0004 8fa30000 23bd0004
  //   8fa20000 23bd0004 8fa10000 23bd0004 42000018 23bdfffc afa10000 23bdfffc afa20000 23bdfffc afa30000
  //   23bdfffc afa40000 23bdfffc afa50000 23bdfffc afa60000 23bdfffc afa70000 23bdfffc afa80000 23bdfffc
  //   afa90000 23bdfffc afaa0000 23bdfffc afab0000 23bdfffc afac0000 23bdfffc afad0000 23bdfffc afae0000
  //   23bdfffc afaf0000 23bdfffc afb00000 23bdfffc afb10000 23bdfffc afb20000 23bdfffc afb30000 23bdfffc
  //   afb40000 23bdfffc afb50000 23bdfffc afb60000 23bdfffc afb70000 23bdfffc afb80000 23bdfffc afb90000
  //   20160003 20140006 20150001 168020 108100 2149825 132020 20020022 c 1600fffa 295a022 1680fff7
  //   8fb90000 23bd0004 8fb80000 23bd0004 8fb70000 23bd0004 8fb60000 23bd0004 8fb50000 23bd0004 8fb40000
  //   23bd0004 8fb30000 23bd0004 8fb20000 23bd0004 8fb10000 23bd0004 8fb00000 23bd0004 8faf0000 23bd0004
  //   8fae0000 23bd0004 8fad0000 23bd0004 8fac0000 23bd0004 8fab0000 23bd0004 8faa0000 23bd0004 8fa90000
  //   23bd0004 8fa80000 23bd0004 8fa70000 23bd0004 8fa60000 23bd0004 8fa50000 23bd0004 8fa40000 23bd0004
  //   8fa30000 23bd0004 8fa20000 23bd0004 8fa10000 23bd0004 42000018 20110200 20020022 112020 c 2231ffff
  //   1620fffc 4*0 2002000a c 2002000a c
  //   数码管输出
  //   指令字
  //   OP
  //   Func
  //   rs
  //   rt
  //   rd
  //   Beq
  //   JMP
  //   JR
  //   Bne
  //   OP
  //   JAL
  //   Func
  //   Syscall
  //   MemToReg
  //   MemWrite
  //   AluOP
  //   AluSrcB
  //   RegWrite
  //   RegDst
  //   rs
  //   rt
  //   流水调试日志用
  //   rs
  //   rt
  //   rd
  //   rt
  //   rd
  //   rt
  //   rd
endmodule

module BHT (
  input  Rst,
  input  Clk,
  input  [31:0] PC_3,
  input  [31:0] PC,
  input  [31:0] DstAddr,
  input  \分支成功 ,
  input  Hit_3,
  input  JumpBack_3,
  input  [2:0] HitPos_3,
  output \预测跳转 ,
  output Hit,
  output [31:0] \预测地址 ,
  output [2:0] HitPos
);

  wire Addr_SET0, Addr_SET1, Addr_SET2, Addr_SET3, Addr_SET4, Addr_SET5, Addr_SET6, Addr_SET7, and_1_out,
       and_2_out, and_3_out, and_4_out, and_5_out, and_6_out, and_7_out, and_8_out, decoder_1_out0,
       decoder_1_out1, decoder_1_out2, decoder_1_out3, decoder_1_out4, decoder_1_out5, decoder_1_out6,
       decoder_1_out7, DirAddr0, DirAddr1, DirAddr2, DirAddr3, DirAddr4, DirAddr5, DirAddr6, DirAddr7, Empty,
       Miss, not_2_out, not_3_out, not_4_out, not_5_out, not_6_out, not_7_out, not_8_out, not_9_out,
       not_10_out, priority_encoder_1_gs, SET0, SET1, SET2, SET3, SET4, SET5, SET6, SET7, V0, V1, V2, V3, V4,
       V5, V6, V7;
  wire [0:0] multiplexer_35_out;
  wire [1:0] multiplexer_19_out, multiplexer_20_out, multiplexer_21_out, multiplexer_22_out,
       multiplexer_23_out, multiplexer_24_out, multiplexer_25_out, multiplexer_26_out, State0, State1,
       State2, State3, State4, State5, State6, State7, \预测历史_2_out_4 , \预测历史_3_out_4 , \预测历史_4_out_4 ,
       \预测历史_5_out_4 , \预测历史_6_out_4 , \预测历史_7_out_4 , \预测历史_8_out_4 , \预测历史_out_4 ;
  wire [2:0] Invalid, max_3_1_max_num, max_3_2_max_num, max_3_3_max_num, max_3_4_max_num, max_3_5_max_num,
       max_3_6_max_num, MAX_num, multiplexer_17_out, multiplexer_44_out, multiplexer_45_out;
  wire [31:0] adder_1_out, adder_2_out, adder_3_out, adder_4_out, adder_5_out, adder_6_out, adder_7_out,
       adder_8_out, DstAddr0, DstAddr1, DstAddr2, DstAddr3, DstAddr4, DstAddr5, DstAddr6, DstAddr7, LRU_0,
       LRU_1, LRU_2, LRU_3, LRU_4, LRU_5, LRU_6, LRU_7, max_3_1_max, max_3_2_max, max_3_3_max, max_3_4_max,
       max_3_5_max, max_3_6_max, multiplexer_1_out, multiplexer_2_out, multiplexer_3_out, multiplexer_4_out,
       multiplexer_5_out, multiplexer_6_out, multiplexer_7_out, multiplexer_8_out, multiplexer_9_out,
       multiplexer_10_out, multiplexer_11_out, multiplexer_12_out, multiplexer_13_out, multiplexer_14_out,
       multiplexer_15_out, multiplexer_16_out, multiplexer_27_out, multiplexer_28_out, multiplexer_29_out,
       multiplexer_30_out, multiplexer_31_out, multiplexer_32_out, multiplexer_33_out, multiplexer_34_out,
       multiplexer_36_out, multiplexer_37_out, multiplexer_38_out, multiplexer_39_out, multiplexer_40_out,
       multiplexer_41_out, multiplexer_42_out, multiplexer_43_out, \指令Addr_2_q , \指令Addr_3_q , \指令Addr_4_q ,
       \指令Addr_5_q , \指令Addr_6_q , \指令Addr_7_q , \指令Addr_8_q , \指令Addr_q ;

  Register #(.width(1)) valid (.D(1'b1), .en(SET0), .Q(V0), .clk(Clk));  // open: clr
  Register #(.width(1)) valid_2 (.D(1'b1), .en(SET1), .Q(V1), .clk(Clk));  // open: clr
  Register #(.width(1)) valid_3 (.D(1'b1), .en(SET2), .Q(V2), .clk(Clk));  // open: clr
  Register #(.width(1)) valid_4 (.D(1'b1), .en(SET3), .Q(V3), .clk(Clk));  // open: clr
  Register #(.width(1)) valid_5 (.D(1'b1), .en(SET4), .Q(V4), .clk(Clk));  // open: clr
  Register #(.width(1)) valid_6 (.D(1'b1), .en(SET5), .Q(V5), .clk(Clk));  // open: clr
  Register #(.width(1)) valid_7 (.D(1'b1), .en(SET6), .Q(V6), .clk(Clk));  // open: clr
  Register #(.width(1)) valid_8 (.D(1'b1), .en(SET7), .Q(V7), .clk(Clk));  // open: clr
  MAX_3 max_3_1 (.Y(LRU_0), .X(LRU_1), .Y_num(3'b000), .X_num(3'b001), .MAX(max_3_1_max), .Max_num(max_3_1_max_num));
  MAX_3 max_3_2 (.Y(LRU_2), .X(LRU_3), .Y_num(3'b010), .X_num(3'b011), .MAX(max_3_2_max), .Max_num(max_3_2_max_num));
  MAX_3 max_3_3 (.Y(LRU_4), .X(LRU_5), .Y_num(3'b100), .X_num(3'b101), .MAX(max_3_3_max), .Max_num(max_3_3_max_num));
  MAX_3 max_3_4 (.Y(LRU_6), .X(LRU_7), .Y_num(3'b110), .X_num(3'b111), .MAX(max_3_4_max), .Max_num(max_3_4_max_num));
  MAX_3 max_3_5 (
    .Y(max_3_1_max), .X(max_3_2_max), .Y_num(max_3_1_max_num), .X_num(max_3_2_max_num), .MAX(max_3_5_max),
    .Max_num(max_3_5_max_num));
  MAX_3 max_3_6 (
    .Y(max_3_3_max), .X(max_3_4_max), .Y_num(max_3_3_max_num), .X_num(max_3_4_max_num), .MAX(max_3_6_max),
    .Max_num(max_3_6_max_num));
  Multiplexer #(.width(32), .enable("false")) multiplexer_1 (
    .in0(PC_3), .in1({32{1'b0}}), .out(multiplexer_1_out), .sel(Rst));
  Register #(.width(32)) \u_指令Addr  (.D(multiplexer_1_out), .en(Addr_SET0), .Q(\指令Addr_q ), .clk(Clk));  // open: clr
  Register #(.width(32)) \u_指令Addr_2  (
    .D(multiplexer_2_out), .en(Addr_SET1), .Q(\指令Addr_2_q ), .clk(Clk));  // open: clr
  Multiplexer #(.width(32), .enable("false")) multiplexer_2 (
    .in0(PC_3), .in1({32{1'b0}}), .out(multiplexer_2_out), .sel(Rst));
  Multiplexer #(.width(32), .enable("false")) multiplexer_3 (
    .in0(PC_3), .in1({32{1'b0}}), .out(multiplexer_3_out), .sel(Rst));
  Register #(.width(32)) \u_指令Addr_3  (
    .D(multiplexer_3_out), .en(Addr_SET2), .Q(\指令Addr_3_q ), .clk(Clk));  // open: clr
  Multiplexer #(.width(32), .enable("false")) multiplexer_4 (
    .in0(PC_3), .in1({32{1'b0}}), .out(multiplexer_4_out), .sel(Rst));
  Register #(.width(32)) \u_指令Addr_4  (
    .D(multiplexer_4_out), .en(Addr_SET3), .Q(\指令Addr_4_q ), .clk(Clk));  // open: clr
  Register #(.width(32)) \u_指令Addr_5  (
    .D(multiplexer_5_out), .en(Addr_SET4), .Q(\指令Addr_5_q ), .clk(Clk));  // open: clr
  Multiplexer #(.width(32), .enable("false")) multiplexer_5 (
    .in0(PC_3), .in1({32{1'b0}}), .out(multiplexer_5_out), .sel(Rst));
  Register #(.width(32)) \u_指令Addr_6  (
    .D(multiplexer_6_out), .en(Addr_SET5), .Q(\指令Addr_6_q ), .clk(Clk));  // open: clr
  Multiplexer #(.width(32), .enable("false")) multiplexer_6 (
    .in0(PC_3), .in1({32{1'b0}}), .out(multiplexer_6_out), .sel(Rst));
  Register #(.width(32)) \u_指令Addr_7  (
    .D(multiplexer_7_out), .en(Addr_SET6), .Q(\指令Addr_7_q ), .clk(Clk));  // open: clr
  Multiplexer #(.width(32), .enable("false")) multiplexer_7 (
    .in0(PC_3), .in1({32{1'b0}}), .out(multiplexer_7_out), .sel(Rst));
  Register #(.width(32)) \u_指令Addr_8  (
    .D(multiplexer_8_out), .en(Addr_SET7), .Q(\指令Addr_8_q ), .clk(Clk));  // open: clr
  Multiplexer #(.width(32), .enable("false")) multiplexer_8 (
    .in0(PC_3), .in1({32{1'b0}}), .out(multiplexer_8_out), .sel(Rst));
  MAX_3 max_3_7 (
    .Y(max_3_5_max), .X(max_3_6_max), .Y_num(max_3_5_max_num), .X_num(max_3_6_max_num), .Max_num(MAX_num));  // open: MAX
  Comparator #(.width(32)) comparator_1 (.a(PC), .b(\指令Addr_q ), .eq(DirAddr0));  // open: gt, lt
  Comparator #(.width(32)) comparator_2 (.a(PC), .b(\指令Addr_2_q ), .eq(DirAddr1));  // open: gt, lt
  Comparator #(.width(32)) comparator_3 (.a(PC), .b(\指令Addr_3_q ), .eq(DirAddr2));  // open: gt, lt
  Comparator #(.width(32)) comparator_4 (.a(PC), .b(\指令Addr_4_q ), .eq(DirAddr3));  // open: gt, lt
  Comparator #(.width(32)) comparator_5 (.a(PC), .b(\指令Addr_5_q ), .eq(DirAddr4));  // open: gt, lt
  Comparator #(.width(32)) comparator_6 (.a(PC), .b(\指令Addr_6_q ), .eq(DirAddr5));  // open: gt, lt
  Comparator #(.width(32)) comparator_7 (.a(PC), .b(\指令Addr_7_q ), .eq(DirAddr6));  // open: gt, lt
  Comparator #(.width(32)) comparator_8 (.a(PC), .b(\指令Addr_8_q ), .eq(DirAddr7));  // open: gt, lt
  and and_1 (and_1_out, V0, DirAddr0);
  and and_2 (and_2_out, V1, DirAddr1);
  and and_3 (and_3_out, V2, DirAddr2);
  and and_4 (and_4_out, V3, DirAddr3);
  and and_5 (and_5_out, V4, DirAddr4);
  and and_6 (and_6_out, V5, DirAddr5);
  and and_7 (and_7_out, V6, DirAddr6);
  and and_8 (and_8_out, V7, DirAddr7);
  Register #(.width(32)) Dst_Addr (.D(multiplexer_9_out), .en(Addr_SET0), .Q(DstAddr0), .clk(Clk));  // open: clr
  Multiplexer #(.width(32), .enable("false")) multiplexer_9 (
    .in0(DstAddr), .in1({32{1'b0}}), .out(multiplexer_9_out), .sel(Rst));
  Register #(.width(32)) Dst_Addr_2 (.D(multiplexer_10_out), .en(Addr_SET1), .Q(DstAddr1), .clk(Clk));  // open: clr
  Multiplexer #(.width(32), .enable("false")) multiplexer_10 (
    .in0(DstAddr), .in1({32{1'b0}}), .out(multiplexer_10_out), .sel(Rst));
  Multiplexer #(.width(32), .enable("false")) multiplexer_11 (
    .in0(DstAddr), .in1({32{1'b0}}), .out(multiplexer_11_out), .sel(Rst));
  Register #(.width(32)) Dst_Addr_3 (.D(multiplexer_11_out), .en(Addr_SET2), .Q(DstAddr2), .clk(Clk));  // open: clr
  Register #(.width(32)) Dst_Addr_4 (.D(multiplexer_12_out), .en(Addr_SET3), .Q(DstAddr3), .clk(Clk));  // open: clr
  Multiplexer #(.width(32), .enable("false")) multiplexer_12 (
    .in0(DstAddr), .in1({32{1'b0}}), .out(multiplexer_12_out), .sel(Rst));
  Multiplexer #(.width(32), .enable("false")) multiplexer_13 (
    .in0(DstAddr), .in1({32{1'b0}}), .out(multiplexer_13_out), .sel(Rst));
  Register #(.width(32)) Dst_Addr_5 (.D(multiplexer_13_out), .en(Addr_SET4), .Q(DstAddr4), .clk(Clk));  // open: clr
  Register #(.width(32)) Dst_Addr_6 (.D(multiplexer_14_out), .en(Addr_SET5), .Q(DstAddr5), .clk(Clk));  // open: clr
  Multiplexer #(.width(32), .enable("false")) multiplexer_14 (
    .in0(DstAddr), .in1({32{1'b0}}), .out(multiplexer_14_out), .sel(Rst));
  Register #(.width(32)) Dst_Addr_7 (.D(multiplexer_15_out), .en(Addr_SET6), .Q(DstAddr6), .clk(Clk));  // open: clr
  Multiplexer #(.width(32), .enable("false")) multiplexer_15 (
    .in0(DstAddr), .in1({32{1'b0}}), .out(multiplexer_15_out), .sel(Rst));
  Register #(.width(32)) Dst_Addr_8 (.D(multiplexer_16_out), .en(Addr_SET7), .Q(DstAddr7), .clk(Clk));  // open: clr
  Multiplexer #(.width(32), .enable("false")) multiplexer_16 (
    .in0(DstAddr), .in1({32{1'b0}}), .out(multiplexer_16_out), .sel(Rst));
  or or_1 (Hit, and_1_out, and_2_out, and_3_out, and_4_out, and_5_out, and_6_out, and_7_out, and_8_out);
  Priority_Encoder priority_encoder_1 (
    .in0(and_1_out), .in1(and_2_out), .in2(and_3_out), .in3(and_4_out), .in4(and_5_out), .in5(and_6_out),
    .in6(and_7_out), .in7(and_8_out), .out(HitPos), .gs(priority_encoder_1_gs));  // open: en_in, en_out
  not not_1 (Miss, Hit);
  Multiplexer #(.width(3), .enable("false")) multiplexer_17 (
    .in0(3'b000), .in1(HitPos), .out(multiplexer_17_out), .sel(priority_encoder_1_gs));
  \双位预测状态机  \u_预测历史  (.\分支成功 (\分支成功 ), .Update(Hit_3), .out_4(\预测历史_out_4 ), .in_1(State0));
  \双位预测状态机  \u_预测历史_2  (.\分支成功 (\分支成功 ), .Update(Hit_3), .out_4(\预测历史_2_out_4 ), .in_1(State1));
  \双位预测状态机  \u_预测历史_3  (.\分支成功 (\分支成功 ), .Update(Hit_3), .out_4(\预测历史_3_out_4 ), .in_1(State2));
  \双位预测状态机  \u_预测历史_4  (.\分支成功 (\分支成功 ), .Update(Hit_3), .out_4(\预测历史_4_out_4 ), .in_1(State3));
  \双位预测状态机  \u_预测历史_5  (.\分支成功 (\分支成功 ), .Update(Hit_3), .out_4(\预测历史_5_out_4 ), .in_1(State4));
  \双位预测状态机  \u_预测历史_6  (.\分支成功 (\分支成功 ), .Update(Hit_3), .out_4(\预测历史_6_out_4 ), .in_1(State5));
  \双位预测状态机  \u_预测历史_7  (.\分支成功 (\分支成功 ), .Update(Hit_3), .out_4(\预测历史_7_out_4 ), .in_1(State6));
  \双位预测状态机  \u_预测历史_8  (.\分支成功 (\分支成功 ), .Update(Hit_3), .out_4(\预测历史_8_out_4 ), .in_1(State7));
  Multiplexer #(.select(3), .width(32), .enable("false")) multiplexer_18 (
    .in0(DstAddr0), .in1(DstAddr1), .in2(DstAddr2), .in3(DstAddr3), .in4(DstAddr4), .in5(DstAddr5),
    .in6(DstAddr6), .in7(DstAddr7), .out(\预测地址 ), .sel(multiplexer_17_out));
  Register #(.width(2)) register_1 (.D(multiplexer_19_out), .en(SET0), .Q(State0), .clk(Clk));  // open: clr
  Multiplexer #(.width(2), .enable("false")) multiplexer_19 (
    .in0(\预测历史_out_4 ), .in1(2'b00), .out(multiplexer_19_out), .sel(Rst));
  Multiplexer #(.width(2), .enable("false")) multiplexer_20 (
    .in0(\预测历史_2_out_4 ), .in1(2'b00), .out(multiplexer_20_out), .sel(Rst));
  Register #(.width(2)) register_2 (.D(multiplexer_20_out), .en(SET1), .Q(State1), .clk(Clk));  // open: clr
  Multiplexer #(.width(2), .enable("false")) multiplexer_21 (
    .in0(\预测历史_3_out_4 ), .in1(2'b00), .out(multiplexer_21_out), .sel(Rst));
  Register #(.width(2)) register_3 (.D(multiplexer_21_out), .en(SET2), .Q(State2), .clk(Clk));  // open: clr
  Register #(.width(2)) register_4 (.D(multiplexer_22_out), .en(SET3), .Q(State3), .clk(Clk));  // open: clr
  Multiplexer #(.width(2), .enable("false")) multiplexer_22 (
    .in0(\预测历史_4_out_4 ), .in1(2'b00), .out(multiplexer_22_out), .sel(Rst));
  Multiplexer #(.width(2), .enable("false")) multiplexer_23 (
    .in0(\预测历史_5_out_4 ), .in1(2'b00), .out(multiplexer_23_out), .sel(Rst));
  Register #(.width(2)) register_5 (.D(multiplexer_23_out), .en(SET4), .Q(State4), .clk(Clk));  // open: clr
  Multiplexer #(.width(2), .enable("false")) multiplexer_24 (
    .in0(\预测历史_6_out_4 ), .in1(2'b00), .out(multiplexer_24_out), .sel(Rst));
  Register #(.width(2)) register_6 (.D(multiplexer_24_out), .en(SET5), .Q(State5), .clk(Clk));  // open: clr
  Register #(.width(2)) register_7 (.D(multiplexer_25_out), .en(SET6), .Q(State6), .clk(Clk));  // open: clr
  Multiplexer #(.width(2), .enable("false")) multiplexer_25 (
    .in0(\预测历史_7_out_4 ), .in1(2'b00), .out(multiplexer_25_out), .sel(Rst));
  Register #(.width(2)) register_8 (.D(multiplexer_26_out), .en(SET7), .Q(State7), .clk(Clk));  // open: clr
  Multiplexer #(.width(2), .enable("false")) multiplexer_26 (
    .in0(\预测历史_8_out_4 ), .in1(2'b00), .out(multiplexer_26_out), .sel(Rst));
  Multiplexer #(.width(32), .enable("false")) multiplexer_27 (
    .in0(adder_1_out), .in1({32{1'b0}}), .out(multiplexer_27_out), .sel(SET0));
  Multiplexer #(.width(32), .enable("false")) multiplexer_28 (
    .in0(adder_2_out), .in1({32{1'b0}}), .out(multiplexer_28_out), .sel(SET1));
  Multiplexer #(.width(32), .enable("false")) multiplexer_29 (
    .in0(adder_3_out), .in1({32{1'b0}}), .out(multiplexer_29_out), .sel(SET2));
  Multiplexer #(.width(32), .enable("false")) multiplexer_30 (
    .in0(adder_4_out), .in1({32{1'b0}}), .out(multiplexer_30_out), .sel(SET3));
  Multiplexer #(.width(32), .enable("false")) multiplexer_31 (
    .in0(adder_5_out), .in1({32{1'b0}}), .out(multiplexer_31_out), .sel(SET4));
  Multiplexer #(.width(32), .enable("false")) multiplexer_32 (
    .in0(adder_6_out), .in1({32{1'b0}}), .out(multiplexer_32_out), .sel(SET5));
  Multiplexer #(.width(32), .enable("false")) multiplexer_33 (
    .in0(adder_7_out), .in1({32{1'b0}}), .out(multiplexer_33_out), .sel(SET6));
  Multiplexer #(.width(32), .enable("false")) multiplexer_34 (
    .in0(adder_8_out), .in1({32{1'b0}}), .out(multiplexer_34_out), .sel(SET7));
  Multiplexer #(.select(3), .width(2), .enable("false")) multiplexer_35 (
    .in0(State0), .in1(State1), .in2(State0), .in3(State1), .in4(State0), .in5(State1), .in6(State0),
    .in7(State1), .out({\预测跳转 , multiplexer_35_out[0]}), .sel(multiplexer_17_out));
  Multiplexer #(.width(32), .enable("false")) multiplexer_36 (
    .in0(multiplexer_27_out), .in1({32{1'b0}}), .out(multiplexer_36_out), .sel(Rst));
  Multiplexer #(.width(32), .enable("false")) multiplexer_37 (
    .in0(multiplexer_28_out), .in1({32{1'b0}}), .out(multiplexer_37_out), .sel(Rst));
  Multiplexer #(.width(32), .enable("false")) multiplexer_38 (
    .in0(multiplexer_29_out), .in1({32{1'b0}}), .out(multiplexer_38_out), .sel(Rst));
  Multiplexer #(.width(32), .enable("false")) multiplexer_39 (
    .in0(multiplexer_30_out), .in1({32{1'b0}}), .out(multiplexer_39_out), .sel(Rst));
  Multiplexer #(.width(32), .enable("false")) multiplexer_40 (
    .in0(multiplexer_31_out), .in1({32{1'b0}}), .out(multiplexer_40_out), .sel(Rst));
  Multiplexer #(.width(32), .enable("false")) multiplexer_41 (
    .in0(multiplexer_32_out), .in1({32{1'b0}}), .out(multiplexer_41_out), .sel(Rst));
  Multiplexer #(.width(32), .enable("false")) multiplexer_42 (
    .in0(multiplexer_33_out), .in1({32{1'b0}}), .out(multiplexer_42_out), .sel(Rst));
  Multiplexer #(.width(32), .enable("false")) multiplexer_43 (
    .in0(multiplexer_34_out), .in1({32{1'b0}}), .out(multiplexer_43_out), .sel(Rst));
  Register #(.width(32)) \u_淘汰标志位  (.D(multiplexer_36_out), .en(JumpBack_3), .Q(LRU_0), .clk(Clk));  // open: clr
  Register #(.width(32)) \u_淘汰标志位_2  (.D(multiplexer_37_out), .en(JumpBack_3), .Q(LRU_1), .clk(Clk));  // open: clr
  Register #(.width(32)) \u_淘汰标志位_3  (.D(multiplexer_38_out), .en(JumpBack_3), .Q(LRU_2), .clk(Clk));  // open: clr
  Register #(.width(32)) \u_淘汰标志位_4  (.D(multiplexer_39_out), .en(JumpBack_3), .Q(LRU_3), .clk(Clk));  // open: clr
  Register #(.width(32)) \u_淘汰标志位_5  (.D(multiplexer_40_out), .en(JumpBack_3), .Q(LRU_4), .clk(Clk));  // open: clr
  Register #(.width(32)) \u_淘汰标志位_6  (.D(multiplexer_41_out), .en(JumpBack_3), .Q(LRU_5), .clk(Clk));  // open: clr
  Register #(.width(32)) \u_淘汰标志位_7  (.D(multiplexer_42_out), .en(JumpBack_3), .Q(LRU_6), .clk(Clk));  // open: clr
  Register #(.width(32)) \u_淘汰标志位_8  (.D(multiplexer_43_out), .en(JumpBack_3), .Q(LRU_7), .clk(Clk));  // open: clr
  Adder #(.width(32)) adder_1 (.a(32'h1), .b(LRU_0), .out(adder_1_out));  // open: cin, cout
  Adder #(.width(32)) adder_2 (.a(32'h1), .b(LRU_1), .out(adder_2_out));  // open: cin, cout
  Adder #(.width(32)) adder_3 (.a(32'h1), .b(LRU_2), .out(adder_3_out));  // open: cin, cout
  Adder #(.width(32)) adder_4 (.a(32'h1), .b(LRU_3), .out(adder_4_out));  // open: cin, cout
  Adder #(.width(32)) adder_5 (.a(32'h1), .b(LRU_4), .out(adder_5_out));  // open: cin, cout
  Adder #(.width(32)) adder_6 (.a(32'h1), .b(LRU_5), .out(adder_6_out));  // open: cin, cout
  Adder #(.width(32)) adder_7 (.a(32'h1), .b(LRU_6), .out(adder_7_out));  // open: cin, cout
  Adder #(.width(32)) adder_8 (.a(32'h1), .b(LRU_7), .out(adder_8_out));  // open: cin, cout
  not not_2 (not_2_out, V0);
  not not_3 (not_3_out, V1);
  not not_4 (not_4_out, V2);
  not not_5 (not_5_out, V3);
  not not_6 (not_6_out, V4);
  not not_7 (not_7_out, V5);
  not not_8 (not_8_out, V6);
  not not_9 (not_9_out, V7);
  Priority_Encoder priority_encoder_2 (
    .in0(not_2_out), .in1(not_3_out), .in2(not_4_out), .in3(not_5_out), .in4(not_6_out), .in5(not_7_out),
    .in6(not_8_out), .in7(not_9_out), .out(Invalid), .gs(Empty));  // open: en_in, en_out
  Multiplexer #(.width(3), .enable("false")) multiplexer_44 (
    .in0(MAX_num), .in1(Invalid), .out(multiplexer_44_out), .sel(Empty));
  Decoder #(.select(3), .disabled(0), .enable("false")) decoder_1 (
    .out0(decoder_1_out0), .out1(decoder_1_out1), .out2(decoder_1_out2), .out3(decoder_1_out3),
    .out4(decoder_1_out4), .out5(decoder_1_out5), .out6(decoder_1_out6), .out7(decoder_1_out7),
    .sel(multiplexer_45_out));
  Multiplexer #(.width(3), .enable("false")) multiplexer_45 (
    .in0(multiplexer_44_out), .in1(HitPos_3), .out(multiplexer_45_out), .sel(Hit_3));
  and and_9 (SET0, decoder_1_out0, JumpBack_3);
  and and_10 (SET1, decoder_1_out1, JumpBack_3);
  and and_11 (SET2, decoder_1_out2, JumpBack_3);
  and and_12 (SET3, decoder_1_out3, JumpBack_3);
  and and_13 (SET4, decoder_1_out4, JumpBack_3);
  and and_14 (SET5, decoder_1_out5, JumpBack_3);
  and and_15 (SET6, decoder_1_out6, JumpBack_3);
  and and_16 (SET7, decoder_1_out7, JumpBack_3);
  not not_10 (not_10_out, Hit_3);
  and and_17 (Addr_SET0, SET0, not_10_out);
  and and_18 (Addr_SET1, not_10_out, SET1);
  and and_19 (Addr_SET2, SET2, not_10_out);
  and and_20 (Addr_SET3, SET3, not_10_out);
  and and_21 (Addr_SET4, SET4, not_10_out);
  and and_22 (Addr_SET5, SET5, not_10_out);
  and and_23 (Addr_SET6, SET6, not_10_out);
  and and_24 (Addr_SET7, SET7, not_10_out);

  // Other names for the same wires on the sheet: Jump_Out = \预测跳转 ; DstAddr_Out[31:0] = \预测地址 
endmodule

module \分支预测  (
  input  in_1
);

  wire and_1_out, and_2_out, and_3_out, and_4_out, and_5_out, and_6_out, and_7_out, and_8_out, and_10_out,
       and_11_out, and_12_out, and_13_out, and_14_out, CLK, comparator_1_eq, comparator_2_eq,
       comparator_3_eq, compare, en, EX_BLEZ, EX_Branch, EX_ERET, EX_Hit, EX_JMP, EX_JR, EX_RegDst,
       EX_RegWrite, EX_SH, EX_SRLV, EX_Syscall, \EX_预测跳转 , Go, ID_BLEZ, ID_ERET, ID_Hit, ID_SH, ID_SRLV,
       ID_XORI, \ID_预测跳转 , IF_Hit, \IF_预测跳转 , IR1, IR2, IR3, JAL, LOCK, MEM_JAL, Mem_MemWrite, MEM_RegDst,
       MEM_RegWrite, MEM_SH, mips_alu_1_equal, multiplexer_29_out, nop, not_1_out, not_2_out, or_1_out,
       or_3_out, or_5_out, RST, SignedExt, W1, W2, W3, WB_JAL, WB_RegDst, WB_RegWrite, WB_Syscall, \数据相关 ,
       \预测失败 , \预测成功 ;
  wire [1:0] Forward_A, Forward_B;
  wire [2:0] EX_HitPos, ID_HitPos, IF_HitPos;
  wire [3:0] multiplexer_32_out, multiplexer_33_out, \硬布线控制器_1_alu_op ;
  wire [4:0] ex_mem_1_wreg_, EX_rd, EX_rs, EX_rt, EX_WriteReg, id_ex_1_shamt_, id_ex_1_wreg_, ID_R1_num,
       ID_R2_num, MEM_rd, MEM_rt, mem_wb_1_wreg_, MEM_WriteReg, multiplexer_7_out, multiplexer_9_out,
       multiplexer_11_out, multiplexer_12_out, multiplexer_18_out, multiplexer_19_out, multiplexer_20_out,
       multiplexer_28_out, WB_rd, WB_rt, WB_WriteReg;
  wire [5:0] EX_Func, EX_OP, Func, OP;
  wire [10:0] id_ex_1_cont_, mem_wb_1_cont_;
  wire [10:6] id_ex_1_ir_;
  wire [13:0] ex_mem_1_cont_;
  wire [14:0] \硬布线控制器_1_beq ;
  wire [15:0] \LoadUse次数 , \总周期数 , \无条件分支数 , \条件分支成功数 , \预测失败数 , \预测成功数 ;
  wire [25:0] id_ex_1_imm26_;
  wire [25:6] if_id_1_instru_;
  wire [31:0] adder_1_out, adder_2_out, adder_3_out, adder_4_out, ALUOUT, bit_extender_1_out,
       bit_extender_2_out, DestAddr, ex_mem_1_ir_, ex_mem_1_rd1_, ex_mem_1_rd2_, EX_PC, \EX_预测地址 , EXR1,
       id_ex_1_imm_, id_ex_1_imme_, id_ex_1_pc_4_, id_ex_1_rd1_, id_ex_1_rd2_, ID_PC, \ID_预测地址 ,
       if_id_1_pc_4_, IF_PC, \IF_预测地址 , LedData, Mem_ALU_Result, MEM_PC, mem_wb_1_ir_, mips_probe_1_p1,
       mips_ram_1_p7, multiplexer_2_out, multiplexer_3_out, multiplexer_4_out, multiplexer_6_out,
       multiplexer_13_out, multiplexer_14_out, multiplexer_15_out, multiplexer_16_out, multiplexer_25_out,
       multiplexer_26_out, multiplexer_27_out, multiplexer_30_out, multiplexer_31_out, OUT, R1, R2,
       shifter_1_out, undriven, WB_ALU_Result, WB_Mem_ReadData, WB_PC, WB_RegDin, WBR1, WBR2;

  Button \u_总复位  (.out(RST));
  Button _1 (.out(IR1));
  Button _2 (.out(IR2));
  Button _3 (.out(IR3));
  and and_1 (and_1_out, en, ~\数据相关 );  // AND_Gate
  Multiplexer #(.enable("false")) multiplexer_1 (.in0(1'b1), .in1(1'b0), .out(en), .sel(and_2_out));
  Button \u_继续运行  (.out(Go));
  LED led_1 (.in(W1));
  LED led_2 (.in(W2));
  LED led_3 (.in(W3));
  Register #(.width(32)) PC (.D(multiplexer_2_out), .en(and_1_out), .Q(IF_PC), .clk(CLK), .clr(RST));
  and and_2 (and_2_out, LOCK, ~Go);  // AND_Gate
  Counter #(.width(16), .max('hffff)) counter_1 (.count(en), .Q(\总周期数 ), .clk(CLK), .clr(RST));  // open: load, D, carry
  Multiplexer #(.width(32), .enable("false")) multiplexer_2 (
    .in0(multiplexer_6_out), .in1(multiplexer_3_out), .out(multiplexer_2_out), .sel(EX_JMP));
  and and_3 (and_3_out, ~LOCK, \数据相关 );  // AND_Gate
  Comparator #(.width(32)) comparator_1 (.a(WBR1), .b(32'h22), .eq(comparator_1_eq));  // open: gt, lt
  Hex_Digit_Display hex_digit_display_1 (.value(LedData[31:28]));  // open: dp
  and and_4 (and_4_out, ~LOCK, EX_JMP);  // AND_Gate
  and and_5 (and_5_out, ~LOCK, compare);  // AND_Gate
  Multiplexer #(.width(32), .enable("false")) multiplexer_3 (
    .in0({4'b0000, id_ex_1_imm26_, 2'b00}), .in1(EXR1), .out(multiplexer_3_out), .sel(EX_JR));
  Counter #(.width(16), .max('hffff)) counter_2 (
    .count(and_3_out), .Q(\LoadUse次数 ), .clk(CLK), .clr(RST));  // open: load, D, carry
  Hex_Digit_Display hex_digit_display_2 (.value(LedData[23:20]));  // open: dp
  Hex_Digit_Display hex_digit_display_3 (.value(LedData[27:24]));  // open: dp
  Counter #(.width(16), .max('hffff)) counter_3 (
    .count(and_4_out), .Q(\无条件分支数 ), .clk(CLK), .clr(RST));  // open: load, D, carry
  Counter #(.width(16), .max('hffff)) counter_4 (
    .count(and_5_out), .Q(\条件分支成功数 ), .clk(CLK), .clr(RST));  // open: load, D, carry
  // Mips_Probe mips_probe_1: pin names not known; wires that end beside it: mips_probe_1_p1
  ROM #(.addrWidth(10), .dataWidth(32)) rom_1 (.addr(IF_PC[11:2]), .data(mips_probe_1_p1));  // open: sel
  and and_6 (and_6_out, comparator_1_eq, WB_Syscall);
  and and_7 (and_7_out, ~comparator_1_eq, WB_Syscall);  // AND_Gate
  Comparator #(.width(32), .mode("unsigned")) comparator_2 (
    .a(EX_PC), .b(32'h3064), .eq(comparator_2_eq));  // open: gt, lt
  Hex_Digit_Display hex_digit_display_4 (.value(LedData[19:16]));  // open: dp
  Hex_Digit_Display hex_digit_display_5 (.value(LedData[15:12]));  // open: dp
  and and_8 (and_8_out, en, ~\数据相关 );  // AND_Gate
  Adder #(.width(32)) adder_1 (.a(IF_PC), .b(32'h4), .out(adder_1_out));  // open: cin, cout
  Multiplexer #(.width(32)) multiplexer_4 (
    .in0(undriven), .in1(WBR2), .out(multiplexer_4_out), .sel(and_6_out), .en(and_6_out));
  Multiplexer #(.enable("false")) multiplexer_5 (.in0(and_7_out), .in1(comparator_2_eq), .out(LOCK), .sel(in_1));
  Comparator #(.width(1)) comparator_3 (.a(EX_Branch), .b(\EX_预测跳转 ), .eq(comparator_3_eq));  // open: gt, lt
  Hex_Digit_Display hex_digit_display_6 (.value(LedData[11:8]));  // open: dp
  Hex_Digit_Display hex_digit_display_7 (.value(LedData[7:4]));  // open: dp
  Clock clock_1 (.out(CLK));
  Register #(.width(32)) register_1 (.D(multiplexer_4_out), .Q(LedData), .clk(CLK), .clr(RST));  // open: en
  not not_1 (not_1_out, EX_Hit);
  not not_2 (not_2_out, comparator_3_eq);
  and and_9 (\预测成功 , EX_Hit, comparator_3_eq);
  Hex_Digit_Display hex_digit_display_8 (.value(LedData[3:0]));  // open: dp
  IF_ID if_id_1 (
    .instru(mips_probe_1_p1), .PC_4(adder_1_out), .clk(CLK), .rst(RST),
    .instru_({OP, if_id_1_instru_, Func}), .PC_4_(if_id_1_pc_4_), .PC(IF_PC), .PC_(ID_PC), .en(and_8_out),
    .halt(or_1_out), .\预测跳转 (\IF_预测跳转 ), .\预测地址 (\IF_预测地址 ), .Hit(IF_Hit), .HitPos(IF_HitPos),
    .\预测跳转_ (\ID_预测跳转 ), .\预测地址_ (\ID_预测地址 ), .Hit_(ID_Hit), .HitPos_(ID_HitPos));
  Multiplexer #(.width(32), .enable("false")) multiplexer_6 (
    .in0(adder_1_out), .in1(adder_4_out), .out(multiplexer_6_out), .sel(compare));
  and and_10 (and_10_out, EX_Branch, not_1_out);
  and and_11 (and_11_out, EX_Hit, not_2_out);
  or or_1 (or_1_out, nop, \预测失败 );
  or or_2 (\预测失败 , and_10_out, and_11_out);
  // Probe on \总周期数 
  // Probe on \无条件分支数 
  // Probe on \条件分支成功数 
  // Probe on \LoadUse次数 
  // Probe on \LoadUse次数 
  // Probe on {OP, if_id_1_instru_, Func}
  BHT bht_1 (
    .Rst(RST), .HitPos_3(EX_HitPos), .Clk(CLK), .PC_3(EX_PC), .PC(IF_PC), .DstAddr(DestAddr),
    .\分支成功 (EX_Branch), .Hit_3(EX_Hit), .JumpBack_3(EX_Branch), .\预测跳转 (\IF_预测跳转 ), .\预测地址 (\IF_预测地址 ),
    .Hit(IF_Hit), .HitPos(IF_HitPos));
  Multiplexer #(.width(5), .enable("false")) multiplexer_7 (
    .in0(EX_rs), .in1(5'b00010), .out(multiplexer_7_out), .sel(EX_Syscall));
  Counter #(.width(16), .max('hffff)) counter_5 (.count(\预测失败 ), .Q(\预测失败数 ), .clk(CLK));  // open: load, D, carry, clr
  // Probe on \预测失败数 
  // Probe on \预测成功数 
  Counter #(.width(16), .max('hffff)) counter_6 (.count(\预测成功 ), .Q(\预测成功数 ), .clk(CLK));  // open: load, D, carry, clr
  Multiplexer #(.width(5), .enable("false")) multiplexer_8 (
    .in0(if_id_1_instru_[25:21]), .in1(5'b00010), .out(ID_R1_num), .sel(\硬布线控制器_1_beq [13]));
  Multiplexer #(.width(5), .enable("false")) multiplexer_9 (
    .in0(EX_rt), .in1(5'b00100), .out(multiplexer_9_out), .sel(EX_Syscall));
  // Probe on \预测失败数 
  // Probe on \预测成功数 
  \硬布线控制器  \u_硬布线控制器_1  (
    .Func(Func), .OP(OP), .ALU_OP(\硬布线控制器_1_alu_op ), .MemToReg(\硬布线控制器_1_beq [4]),
    .MemWrite(\硬布线控制器_1_beq [5]), .ALU_SRC(\硬布线控制器_1_beq [10]), .RegWrite(\硬布线控制器_1_beq [14]),
    .SysCALL(\硬布线控制器_1_beq [13]), .SignedExt(SignedExt), .RegDst(\硬布线控制器_1_beq [12]), .JR(\硬布线控制器_1_beq [2]),
    .JMP(\硬布线控制器_1_beq [3]), .Beq(\硬布线控制器_1_beq [0]), .JAL(\硬布线控制器_1_beq [11]), .Bne(\硬布线控制器_1_beq [1]),
    .SRLV(ID_SRLV), .XORI(ID_XORI), .SH(ID_SH), .BLEZ(ID_BLEZ), .ERET(ID_ERET));  // open: RS, RD, MFC_0, MTC_0
  Multiplexer #(.width(5), .enable("false")) multiplexer_10 (
    .in0(if_id_1_instru_[20:16]), .in1(5'b00100), .out(ID_R2_num), .sel(\硬布线控制器_1_beq [13]));
  Multiplexer #(.width(5), .enable("false")) multiplexer_11 (
    .in0(if_id_1_instru_[20:16]), .in1(if_id_1_instru_[15:11]), .out(multiplexer_11_out),
    .sel(\硬布线控制器_1_beq [12]));
  // Probe on ID_PC[11:0]
  // Probe on IF_PC[11:0]
  // Probe on ID_R1_num
  // Probe on ID_R2_num
  Multiplexer #(.width(5), .enable("false")) multiplexer_12 (
    .in0(multiplexer_11_out), .in1({5{1'b1}}), .out(multiplexer_12_out), .sel(\硬布线控制器_1_beq [11]));
  Adder #(.width(32)) adder_2 (.a(WB_PC), .b(32'h4), .out(adder_2_out));  // open: cin, cout
  // Probe on WB_RegDin
  Adder #(.width(32)) adder_3 (.a(IF_PC), .b(32'h4), .out(adder_3_out));  // open: cin, cout
  // Probe on EX_PC[11:0]
  Multiplexer #(.width(32), .enable("false")) multiplexer_13 (
    .in0(WB_RegDin), .in1(adder_2_out), .out(multiplexer_13_out), .sel(WB_JAL));
  \数据相关检测  \u_数据相关检测_1  (
    .ID_OP(OP), .EX_WriteReg_num(EX_WriteReg), .EX_RegWrite(EX_RegWrite), .MEM_WriteReg_num(MEM_WriteReg),
    .MEM_RegWrite(MEM_RegWrite), .ID_FUNC(Func), .ID_R1_num(ID_R1_num), .ID_R2_num(ID_R2_num), .EX_OP(EX_OP),
    .\Load_Use相关 (\数据相关 ), .WB_WriteReg_num(WB_WriteReg), .WB_RegWrite(WB_RegWrite), .Forward1(Forward_A),
    .Forward2(Forward_B), .EX_R1_num(multiplexer_7_out), .EX_R2_num(multiplexer_9_out), .EX_FUNC(EX_Func));  // open: 数据相关, MEM相关, EX相关
  // Probe on WB_PC[11:0]
  // Probe on MEM_PC[11:0]
  // Probe on mem_wb_1_wreg_
  assign bit_extender_1_out = {{16{1'b0}}, {if_id_1_instru_[15:6], Func}};  // Bit_Extender bit_extender_1
  assign bit_extender_2_out = {{16{if_id_1_instru_[15]}}, {if_id_1_instru_[15:6], Func}};  // Bit_Extender bit_extender_2
  and and_12 (and_12_out, \IF_预测跳转 , IF_Hit);
  MIPS_Regifile mips_regifile_1 (
    .Din(multiplexer_13_out), .Clk(CLK), .R1(R1), .R2(R2), .WE(WB_RegWrite), .W_num(mem_wb_1_wreg_),
    .R1_num(ID_R1_num), .R2_num(ID_R2_num));
  Multiplexer #(.width(32), .enable("false")) multiplexer_14 (
    .in0(bit_extender_1_out), .in1(bit_extender_2_out), .out(multiplexer_14_out), .sel(SignedExt));
  Multiplexer #(.width(32), .enable("false")) multiplexer_15 (
    .in0(adder_3_out), .in1(\IF_预测地址 ), .out(multiplexer_15_out), .sel(and_12_out));
  Multiplexer #(.width(32), .enable("false")) multiplexer_16 (
    .in0(EX_PC), .in1(DestAddr), .out(multiplexer_16_out), .sel(EX_Branch));
  Multiplexer #(.width(32), .enable("false")) multiplexer_17 (
    .in0(multiplexer_15_out), .in1(multiplexer_16_out), .out(OUT), .sel(\预测失败 ));
  Multiplexer #(.width(5), .enable("false")) multiplexer_18 (
    .in0(EX_rt), .in1(EX_rd), .out(multiplexer_18_out), .sel(EX_RegDst));
  Multiplexer #(.width(5), .enable("false")) multiplexer_19 (
    .in0(MEM_rt), .in1(MEM_rd), .out(multiplexer_19_out), .sel(MEM_RegDst));
  Multiplexer #(.width(5), .enable("false")) multiplexer_20 (
    .in0(WB_rt), .in1(WB_rd), .out(multiplexer_20_out), .sel(WB_RegDst));
  ID_EX id_ex_1 (
    .RD1(R1), .RD2(R2), .imm(bit_extender_2_out), .PC_4(if_id_1_pc_4_), .clk(CLK), .halt(or_3_out),
    .RD1_(id_ex_1_rd1_), .RD2_(id_ex_1_rd2_), .imm_(id_ex_1_imm_), .PC_4_(id_ex_1_pc_4_),
    .WReg(multiplexer_12_out), .WReg_(id_ex_1_wreg_), .immE(multiplexer_14_out), .immE_(id_ex_1_imme_),
    .cont({\硬布线控制器_1_beq [14:10], \硬布线控制器_1_alu_op , \硬布线控制器_1_beq [5:0]}),
    .cont_({EX_RegWrite, EX_Syscall, EX_RegDst, JAL, id_ex_1_cont_[10:4], EX_JMP, EX_JR, id_ex_1_cont_[1:0]}),
    .shamt(if_id_1_instru_[10:6]), .shamt_(id_ex_1_shamt_), .PC(ID_PC), .PC_(EX_PC), .en(en),
    .imm26({if_id_1_instru_, Func}), .imm26_(id_ex_1_imm26_), .IR({OP, if_id_1_instru_, Func}),
    .IR_({EX_OP, EX_rs, EX_rt, EX_rd, id_ex_1_ir_, EX_Func}), .SRLV(ID_SRLV), .SRLV_(EX_SRLV), .SH(ID_SH),
    .SH_(EX_SH), .BLEZ(ID_BLEZ), .BLEZ_(EX_BLEZ), .rst(RST), .ERET(ID_ERET), .ERET_(EX_ERET),
    .\预测跳转 (\ID_预测跳转 ), .\预测跳转_ (\EX_预测跳转 ), .\预测地址 (\ID_预测地址 ), .\预测地址_ (\EX_预测地址 ), .Hit(ID_Hit),
    .Hit_(EX_Hit), .HitPos(ID_HitPos), .HitPos_(EX_HitPos));
  Multiplexer #(.width(5), .enable("false")) multiplexer_21 (
    .in0(multiplexer_18_out), .in1({5{1'b1}}), .out(EX_WriteReg), .sel(JAL));
  Multiplexer #(.width(5), .enable("false")) multiplexer_22 (
    .in0(multiplexer_19_out), .in1({5{1'b1}}), .out(MEM_WriteReg), .sel(MEM_JAL));
  Multiplexer #(.width(5), .enable("false")) multiplexer_23 (
    .in0(multiplexer_20_out), .in1({5{1'b1}}), .out(WB_WriteReg), .sel(WB_JAL));
  // Probe on Forward_A
  // Probe on EX_PC
  Multiplexer #(.select(2), .width(32), .enable("false")) multiplexer_24 (
    .in0(id_ex_1_rd1_), .in1(Mem_ALU_Result), .in2(WB_RegDin), .out(EXR1), .sel(Forward_A));  // open: in3
  Multiplexer #(.select(2), .width(32), .enable("false")) multiplexer_25 (
    .in0(id_ex_1_rd2_), .in1(Mem_ALU_Result), .in2(WB_RegDin), .out(multiplexer_25_out), .sel(Forward_B));  // open: in3
  or or_3 (or_3_out, nop, \数据相关 , \预测失败 );
  Multiplexer #(.width(32), .enable("false")) multiplexer_26 (
    .in0(multiplexer_25_out), .in1(id_ex_1_imme_), .out(multiplexer_26_out), .sel(id_ex_1_cont_[10]));
  // Probe on EXR1
  Multiplexer #(.width(32), .enable("false")) multiplexer_27 (
    .in0(multiplexer_26_out), .in1({32{1'b0}}), .out(multiplexer_27_out), .sel(EX_BLEZ));
  Shifter #(.width(32)) shifter_1 (.in(id_ex_1_imm_), .\dist (5'b00010), .out(shifter_1_out));
  or or_4 (EX_Branch, EX_JMP, EX_JR, compare);
  MIPS_ALU mips_alu_1 (
    .X(EXR1), .Y(multiplexer_27_out), .AluOP(id_ex_1_cont_[9:6]), .Equal(mips_alu_1_equal), .Result(ALUOUT),
    .shamt(multiplexer_28_out));  // open: Result_2
  Multiplexer #(.width(5), .enable("false")) multiplexer_28 (
    .in0(id_ex_1_shamt_), .in1(EXR1[4:0]), .out(multiplexer_28_out), .sel(EX_SRLV));
  Adder #(.width(32)) adder_4 (.a(shifter_1_out), .b(id_ex_1_pc_4_), .out(adder_4_out));  // open: cin, cout
  and and_13 (and_13_out, id_ex_1_cont_[0], mips_alu_1_equal);
  and and_14 (and_14_out, ~mips_alu_1_equal, id_ex_1_cont_[1]);  // AND_Gate
  or or_5 (or_5_out, mips_alu_1_equal, ALUOUT[0]);
  // Probe on EXR1
  // Probe on ALUOUT
  // Probe on multiplexer_25_out
  Multiplexer #(.enable("false")) multiplexer_29 (.in0(1'b0), .in1(or_5_out), .out(multiplexer_29_out), .sel(EX_BLEZ));
  EX_MEM ex_mem_1 (
    .cont({EX_RegWrite, EX_Syscall, EX_RegDst, JAL, id_ex_1_cont_[10:4], EX_JMP, EX_JR, id_ex_1_cont_[1:0]}),
    .ALUout(ALUOUT), .RD2(multiplexer_25_out), .WReg(id_ex_1_wreg_), .clk(CLK), .halt(RST),
    .cont_({MEM_RegWrite, ex_mem_1_cont_[13], MEM_RegDst, MEM_JAL, ex_mem_1_cont_[10:6], Mem_MemWrite, ex_mem_1_cont_[4:0]}),
    .ALUout_(Mem_ALU_Result), .RD2_(ex_mem_1_rd2_), .WReg_(ex_mem_1_wreg_), .RD1(EXR1), .RD1_(ex_mem_1_rd1_),
    .PC(EX_PC), .PC_(MEM_PC), .en(en), .IR({EX_OP, EX_rs, EX_rt, EX_rd, id_ex_1_ir_, EX_Func}),
    .IR_({ex_mem_1_ir_[31:21], MEM_rt, MEM_rd, ex_mem_1_ir_[10:0]}), .LH(EX_SH), .LH_(MEM_SH), .rst(RST));
  or or_6 (compare, and_13_out, and_14_out, multiplexer_29_out);
  // Probe on Mem_ALU_Result
  or or_7 (nop, compare, EX_JR, EX_JMP);
  // Probe on ex_mem_1_rd1_
  Multiplexer #(.width(32), .enable("false")) multiplexer_30 (
    .in0({{16{1'b0}}, ex_mem_1_rd2_[15:0]}), .in1({ex_mem_1_rd2_[15:0], {16{1'b0}}}),
    .out(multiplexer_30_out), .sel(Mem_ALU_Result[1]));
  Multiplexer #(.width(32), .enable("false")) multiplexer_31 (
    .in0(ex_mem_1_rd2_), .in1(multiplexer_30_out), .out(multiplexer_31_out), .sel(MEM_SH));
  Multiplexer #(.width(4), .enable("false")) multiplexer_32 (
    .in0(4'b1111), .in1(multiplexer_33_out), .out(multiplexer_32_out), .sel(MEM_SH));
  Multiplexer #(.width(4), .enable("false")) multiplexer_33 (
    .in0(4'b0011), .in1(4'b1100), .out(multiplexer_33_out), .sel(Mem_ALU_Result[1]));
  // MIPS_RAM mips_ram_1: pin names not known; wires that end beside it: Mem_ALU_Result[21:2], multiplexer_31_out, Mem_MemWrite, multiplexer_32_out, CLK, RST, mips_ram_1_p7
  MEM_WB mem_wb_1 (
    .cont({MEM_RegWrite, ex_mem_1_cont_[13], MEM_RegDst, MEM_JAL, ex_mem_1_cont_[10:6], Mem_MemWrite, ex_mem_1_cont_[4:0]}),
    .ALUout(Mem_ALU_Result), .MEMout(mips_ram_1_p7), .WReg(ex_mem_1_wreg_), .clk(CLK), .halt(RST),
    .cont_({WB_RegWrite, WB_Syscall, WB_RegDst, WB_JAL, mem_wb_1_cont_}), .ALUout_(WB_ALU_Result),
    .MEMout_(WB_Mem_ReadData), .WReg_(mem_wb_1_wreg_), .RD1(ex_mem_1_rd1_), .RD1_(WBR1), .RD2(ex_mem_1_rd2_),
    .RD2_(WBR2), .PC(MEM_PC), .PC_(WB_PC), .en(en),
    .IR({ex_mem_1_ir_[31:21], MEM_rt, MEM_rd, ex_mem_1_ir_[10:0]}),
    .IR_({mem_wb_1_ir_[31:21], WB_rt, WB_rd, mem_wb_1_ir_[10:0]}), .rst(RST));
  Multiplexer #(.width(32), .enable("false")) multiplexer_34 (
    .in0(WB_ALU_Result), .in1(WB_Mem_ReadData), .out(WB_RegDin), .sel(mem_wb_1_cont_[4]));
  // Probe on WBR1
  // Probe on WBR2

  // Other names for the same wires on the sheet: JR = EX_JR; CHANGE = in_1; IN[31:0] = DestAddr;
  //   SW_sel = Mem_ALU_Result[1]; 插入气泡数[15:0] = \LoadUse次数 

  // Notes on the sheet:
  //   中断源
  //   中断等待指示
  //   指令存储器
  //   contents of rom_1 (hex, n*v repeats v):
  //   20110001 8000c05 20110001 20120002 20130003 8000c09 20110001 20120002 20130003 8000c0d 20110001
  //   20120002 20130003 8000c11 20110001 20120002 20130003 c000cf6 20100001 20110001 118fc0 112020
  //   20020022 c 118882 12200001 8000c15 112020 20020022 c 20110001 118880 112020 20020022 c 12200001
  //   8000c1f 20110001 118fc0 112020 20020022 c 1188c3 112020 20020022 c 118903 112020 20020022 c 118903
  //   112020 20020022 c 118903 112020 20020022 c 118903 112020 20020022 c 118903 112020 20020022 c 118903
  //   112020 20020022 c 118903 112020 20020022 c 20100001 109fc0 139fc3 8021 2012000c 24160003 26100001
  //   3210000f 20080008 20090001 139900 2709825 132020 20020022 c 1094022 1500fff9 22100001 2018000f
  //   2188024 108700 20080008 20090001 139902 2709825 132021 20020022 c 1094022 1500fff9 108702 2c9b022
  //   12c00001 8000c50 4020 1084027 84400 3508ffff 82021 20020022 c 2010ffff 20110000 ae300000 22100001
  //   22310004 ae300000 22100001 22310004 ae300000 22100001 22310004 ae300000 22100001 22310004 ae300000
  //   22100001 22310004 ae300000 22100001 22310004 ae300000 22100001 22310004 ae300000 22100001 22310004
  //   ae300000 22100001 22310004 ae300000 22100001 22310004 ae300000 22100001 22310004 ae300000 22100001
  //   22310004 ae300000 22100001 22310004 ae300000 22100001 22310004 ae300000 22100001 22310004 ae300000
  //   22100001 22310004 22100001 8020 2011003c 8e130000 8e340000 274402a 11000002 ae330000 ae140000
  //   2231fffc 1611fff8 102020 20020022 c 22100004 2011003c 161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
  //   数码管输出
  //   指令字
  //   rs
  //   rt
  //   JMP
  //   JR
  //   OP
  //   Func
  //   Syscall
  //   OP
  //   Func
  //   rs
  //   rt
  //   rd
  //   Beq
  //   Bne
  //   MemToReg
  //   MemWrite
  //   AluOP
  //   AluSrcB
  //   RegWrite
  //   JAL
  //   RegDst
  //   流水调试日志用
  //   rs
  //   rt
  //   rd
  //   rt
  //   rd
  //   rt
  //   rd
endmodule

module \双位预测状态机  (
  input  [1:0] in_1,
  input  \分支成功 ,
  input  Update,
  output [1:0] out_4
);

  wire and_1_out, and_2_out, and_3_out, and_4_out, not_1_out, not_2_out, not_3_out, not_4_out, not_5_out;
  wire [1:0] or_2_out;

  not not_1 (not_1_out, in_1[0]);
  not not_2 (not_2_out, in_1[1]);
  not not_3 (not_3_out, in_1[0]);
  not not_4 (not_4_out, in_1[0]);
  not not_5 (not_5_out, \分支成功 );
  and and_1 (and_1_out, in_1[0], \分支成功 );
  and and_2 (and_2_out, in_1[1], not_1_out);
  and and_3 (and_3_out, not_2_out, not_3_out, \分支成功 );
  and and_4 (and_4_out, in_1[1], not_4_out, not_5_out);
  or or_1 (or_2_out[1], and_1_out, and_2_out);
  or or_2 (or_2_out[0], and_3_out, and_4_out);
  Multiplexer #(.width(2), .enable("false")) multiplexer_1 (.in0(2'b10), .in1(or_2_out), .out(out_4), .sel(Update));
endmodule

module \多级中断_module  (
  input  clk,
  input  ir1,
  input  [31:0] PC,
  input  ir2,
  input  ir3,
  input  ERET,
  input  [31:0] nextPC,
  input  [1:0] MFC_sel,
  input  [1:0] MTC_sel,
  input  [31:0] R2,
  output [31:0] PCout,
  output [31:0] siteData2reg,
  output w1,
  output w2,
  output w3
);

  wire _1, _2, _3, and_1_out, and_2_out, and_3_out, and_4_out, and_6_out, and_7_out, and_8_out, d_ff_1_qn,
       d_ff_2_qn, d_ff_3_qn, d_ff_4_qn, d_ff_5_q, d_ff_6_q, d_ff_7_q, d_ff_8_q, decoder_2_out1,
       decoder_2_out2, decoder_2_out3, IE_q, IR1_t, IR2_t, IR3_t, IR_CPU, multiplexer_1_out,
       multiplexer_2_out, multiplexer_3_out, multiplexer_4_out, multiplexer_5_out, multiplexer_6_out,
       not_1_out, not_2_out, not_3_out, not_4_out, or_4_out, or_5_out, or_6_out, or_7_out, or_8_out,
       priority_encoder_1_gs, rst1, rst2, rst3;
  wire [1:0] priority_encoder_1_out, priority_encoder_2_out;
  wire [3:0] \屏蔽字R ;
  wire [31:0] epc, EPC_write, IE_32, multiplexer_7_out, multiplexer_10_out, realpc, \屏蔽字 ;

  // Probe on R2
  Demultiplexer #(.select(2), .width(32), .enable("false")) demultiplexer_1 (
    .out0(\屏蔽字 ), .out1(EPC_write), .out2(IE_32), .in(R2), .sel(MTC_sel));  // open: out3
  Multiplexer #(.enable("false")) multiplexer_1 (.in0(1'b0), .in1(\屏蔽字 [0]), .out(multiplexer_1_out), .sel(_1));
  Multiplexer #(.enable("false")) multiplexer_2 (.in0(1'b0), .in1(\屏蔽字 [1]), .out(multiplexer_2_out), .sel(_1));
  Multiplexer #(.enable("false")) multiplexer_3 (.in0(1'b0), .in1(\屏蔽字 [2]), .out(multiplexer_3_out), .sel(_1));
  Multiplexer #(.enable("false")) multiplexer_4 (.in0(1'b0), .in1(\屏蔽字 [3]), .out(multiplexer_4_out), .sel(_1));
  // Probe on \屏蔽字 
  // Probe on MTC_sel
  D_Flip_Flop d_ff_1 (.clk(clk), .D(multiplexer_1_out), .Q(\屏蔽字R [0]), .Qn(d_ff_1_qn), .en(_1));  // open: preset, reset
  D_Flip_Flop d_ff_2 (.clk(clk), .D(multiplexer_2_out), .Q(\屏蔽字R [1]), .Qn(d_ff_2_qn), .en(_1));  // open: preset, reset
  D_Flip_Flop d_ff_3 (.clk(clk), .D(multiplexer_3_out), .Q(\屏蔽字R [2]), .Qn(d_ff_3_qn), .en(_1));  // open: preset, reset
  D_Flip_Flop d_ff_4 (.clk(clk), .D(multiplexer_4_out), .Q(\屏蔽字R [3]), .Qn(d_ff_4_qn), .en(_1));  // open: preset, reset
  D_Flip_Flop d_ff_5 (.clk(ir1), .D(1'b1), .Q(d_ff_5_q), .reset(IR1_t));  // open: Qn, preset, en
  or or_1 (w1, IR1_t, d_ff_5_q);
  D_Flip_Flop d_ff_6 (.clk(ir2), .D(1'b1), .Q(d_ff_6_q), .reset(IR2_t));  // open: Qn, preset, en
  or or_2 (w2, IR2_t, d_ff_6_q);
  D_Flip_Flop d_ff_7 (.clk(ir3), .D(1'b1), .Q(d_ff_7_q), .reset(IR3_t));  // open: Qn, preset, en
  or or_3 (w3, IR3_t, d_ff_7_q);
  Multiplexer #(.select(2), .enable("false")) multiplexer_5 (
    .in0(1'b0), .in1(1'b1), .in2(IE_32[0]), .in3(1'b0), .out(multiplexer_5_out), .sel({_3, ERET}));
  not not_1 (not_1_out, d_ff_8_q);
  D_Flip_Flop d_ff_8 (.clk(clk), .D(1'b1), .Q(d_ff_8_q));  // open: Qn, preset, en, reset
  Decoder #(.select(2), .enable("false")) decoder_1 (.out0(_1), .out1(_2), .out2(_3), .sel(MTC_sel));  // open: out3
  and and_1 (and_1_out, 1'b0, d_ff_1_qn);
  and and_2 (and_2_out, IR1_t, d_ff_2_qn);
  and and_3 (and_3_out, IR2_t, d_ff_3_qn);
  and and_4 (and_4_out, IR3_t, d_ff_4_qn);
  Multiplexer #(.enable("false")) multiplexer_6 (
    .in0(multiplexer_5_out), .in1(1'b1), .out(multiplexer_6_out), .sel(not_1_out));
  or or_4 (or_4_out, not_1_out, _3, ERET, IR_CPU);
  Multiplexer #(.width(32), .enable("false")) multiplexer_7 (
    .in0(PC), .in1(EPC_write), .out(multiplexer_7_out), .sel(_2));
  or or_5 (or_5_out, d_ff_5_q, IR1_t);
  or or_6 (or_6_out, d_ff_6_q, IR2_t);
  or or_7 (or_7_out, d_ff_7_q, IR3_t);
  Priority_Encoder #(.select(2)) priority_encoder_1 (
    .in0(and_1_out), .in1(and_2_out), .in2(and_3_out), .in3(and_4_out), .out(priority_encoder_1_out),
    .gs(priority_encoder_1_gs));  // open: en_out, en_in
  and and_5 (IR_CPU, priority_encoder_1_gs, IE_q);
  D_Flip_Flop IE (.clk(clk), .D(multiplexer_6_out), .Q(IE_q), .en(or_4_out));  // open: Qn, preset, reset
  Register #(.width(32)) u_EPC (.D(multiplexer_7_out), .en(or_8_out), .Q(epc), .clk(clk));  // open: clr
  or or_8 (or_8_out, _2, IR_CPU);
  and and_6 (and_6_out, or_5_out, not_2_out);
  not not_2 (not_2_out, rst1);
  and and_7 (and_7_out, or_6_out, not_3_out);
  not not_3 (not_3_out, rst2);
  and and_8 (and_8_out, or_7_out, not_4_out);
  not not_4 (not_4_out, rst3);
  D_Flip_Flop u_IR1 (.clk(clk), .D(and_6_out), .Q(IR1_t));  // open: Qn, preset, en, reset
  D_Flip_Flop u_IR2 (.clk(clk), .D(and_7_out), .Q(IR2_t));  // open: Qn, preset, en, reset
  D_Flip_Flop u_IR3 (.clk(clk), .D(and_8_out), .Q(IR3_t));  // open: Qn, preset, en, reset
  // Probe on priority_encoder_1_out
  Multiplexer #(.select(2), .width(32), .enable("false")) multiplexer_8 (
    .in1(32'h4), .in2(32'h20c), .in3(32'h414), .out(realpc), .sel(priority_encoder_1_out));  // open: in0
  Priority_Encoder #(.select(2)) priority_encoder_2 (
    .in0(1'b0), .in1(IR1_t), .in2(IR2_t), .in3(IR3_t), .out(priority_encoder_2_out));  // open: gs, en_out, en_in
  Multiplexer #(.select(2), .width(32), .enable("false")) multiplexer_9 (
    .in0({{28{1'b0}}, \屏蔽字R }), .in1(epc), .in2({32{1'b0}}), .in3({32{1'b0}}), .out(siteData2reg),
    .sel(MFC_sel));
  Decoder #(.select(2), .enable("false")) decoder_2 (
    .out1(decoder_2_out1), .out2(decoder_2_out2), .out3(decoder_2_out3), .sel(priority_encoder_2_out));  // open: out0
  and and_9 (rst1, ERET, decoder_2_out1);
  and and_10 (rst2, decoder_2_out2, ERET);
  and and_11 (rst3, decoder_2_out3, ERET);
  Multiplexer #(.width(32), .enable("false")) multiplexer_10 (
    .in0(nextPC), .in1(realpc), .out(multiplexer_10_out), .sel(IR_CPU));
  Multiplexer #(.width(32), .enable("false")) multiplexer_11 (
    .in0(multiplexer_10_out), .in1(epc), .out(PCout), .sel(ERET));

  // Other names for the same wires on the sheet: IE_sel[1:0] = {_3, ERET}; pcNext[31:0] = nextPC
endmodule
