// Logisim project cpu24_Hover.circ as structural Verilog: 26 circuits, main circuit ◇单周期MIPS
module \单周期MIPS  (
);

  wire and_1_out, and_2_out, and_3_out, and_4_out, and_5_out, BGTZ, CLK, equal, Go, JAL, LHU, not_1_out, RST,
       SignedExt, SRAV, stop, syscall, \硬布线控制器_1_alu_src , \硬布线控制器_1_beq , \硬布线控制器_1_bne ,
       \硬布线控制器_1_memtoreg , \硬布线控制器_1_memwrite , \硬布线控制器_1_regdst , \硬布线控制器_1_regwrite ;
  wire [2:0] \硬布线控制器_1_jr ;
  wire [3:0] \硬布线控制器_1_alu_op ;
  wire [4:0] multiplexer_2_out, multiplexer_3_out, multiplexer_5_out, multiplexer_6_out, multiplexer_11_out;
  wire [15:0] multiplexer_13_out, \总周期数 , \无条件分支数 , \条件分支成功数 ;
  wire [31:0] a0, adder_1_out, adder_2_out, bit_extender_1_out, bit_extender_2_out, LedData,
       mips_regifile_1_r2, multiplexer_1_out, multiplexer_4_out, multiplexer_8_out, multiplexer_9_out,
       multiplexer_10_out, multiplexer_12_out, multiplexer_14_out, PC_q, ram_1_data, result, rom_1_data,
       shifter_1_out;

  Button \u_总复位  (.out(RST));
  Button \u_继续运行  (.out(Go));
  Clock clock_1 (.out(CLK));
  Multiplexer #(.select(3), .width(32), .enable("false")) multiplexer_1 (
    .in0(adder_1_out), .in1({32{1'b0}}), .in2({PC_q[31:28], rom_1_data[25:0], 2'b00}), .in3(a0),
    .in4(adder_2_out), .in5({32{1'b0}}), .in6({32{1'b0}}), .in7({32{1'b0}}), .out(multiplexer_1_out),
    .sel(\硬布线控制器_1_jr ));
  Register #(.width(32)) PC (.D(multiplexer_1_out), .en(stop), .Q(PC_q), .clk(CLK), .clr(RST));
  Hex_Digit_Display hex_digit_display_1 (.value(LedData[27:24]));  // open: dp
  Hex_Digit_Display hex_digit_display_2 (.value(LedData[31:28]));  // open: dp
  Hex_Digit_Display hex_digit_display_3 (.value(LedData[19:16]));  // open: dp
  Hex_Digit_Display hex_digit_display_4 (.value(LedData[23:20]));  // open: dp
  Adder #(.width(32)) adder_1 (.a(PC_q), .b(32'h4), .out(adder_1_out));  // open: cin, cout
  Register #(.width(32)) register_1 (.D(a0), .en(and_1_out), .Q(LedData), .clk(CLK), .clr(RST));
  and and_1 (and_1_out, syscall, equal);
  Hex_Digit_Display hex_digit_display_5 (.value(LedData[15:12]));  // open: dp
  Hex_Digit_Display hex_digit_display_6 (.value(LedData[11:8]));  // open: dp
  Counter #(.width(16), .max('hffff)) counter_1 (
    .count(\硬布线控制器_1_jr [1]), .Q(\无条件分支数 ), .clk(CLK), .clr(RST));  // open: load, D, carry
  ROM #(.addrWidth(10), .dataWidth(32)) rom_1 (.addr(PC_q[11:2]), .data(rom_1_data));  // open: sel
  Hex_Digit_Display hex_digit_display_7 (.value(LedData[3:0]));  // open: dp
  Hex_Digit_Display hex_digit_display_8 (.value(LedData[7:4]));  // open: dp
  \硬布线控制器  \u_硬布线控制器_1  (
    .Func(rom_1_data[5:0]), .OP(rom_1_data[31:26]), .ALU_OP(\硬布线控制器_1_alu_op ),
    .MemToReg(\硬布线控制器_1_memtoreg ), .MemWrite(\硬布线控制器_1_memwrite ), .ALU_SRC(\硬布线控制器_1_alu_src ),
    .RegWrite(\硬布线控制器_1_regwrite ), .SysCALL(syscall), .SignedExt(SignedExt), .RegDst(\硬布线控制器_1_regdst ),
    .JR(\硬布线控制器_1_jr [0]), .JMP(\硬布线控制器_1_jr [1]), .Beq(\硬布线控制器_1_beq ), .JAL(JAL), .Bne(\硬布线控制器_1_bne ),
    .SRAV(SRAV), .LHU(LHU), .BGTZ(BGTZ));
  Multiplexer #(.width(5), .enable("false")) multiplexer_2 (
    .in0(rom_1_data[25:21]), .in1(5'b00100), .out(multiplexer_2_out), .sel(syscall));
  Multiplexer #(.width(5), .enable("false")) multiplexer_3 (
    .in0(rom_1_data[20:16]), .in1(5'b00010), .out(multiplexer_3_out), .sel(syscall));
  Multiplexer #(.width(32), .enable("false")) multiplexer_4 (
    .in0(multiplexer_12_out), .in1(adder_1_out), .out(multiplexer_4_out), .sel(JAL));
  and and_2 (and_2_out, syscall, ~equal);  // AND_Gate
  Multiplexer #(.width(5), .enable("false")) multiplexer_5 (
    .in0(rom_1_data[20:16]), .in1(rom_1_data[15:11]), .out(multiplexer_5_out), .sel(\硬布线控制器_1_regdst ));
  Multiplexer #(.width(5), .enable("false")) multiplexer_6 (
    .in0(multiplexer_5_out), .in1({5{1'b1}}), .out(multiplexer_6_out), .sel(JAL));
  assign bit_extender_1_out = {{16{1'b0}}, rom_1_data[15:0]};  // Bit_Extender bit_extender_1
  assign bit_extender_2_out = {{16{rom_1_data[15]}}, rom_1_data[15:0]};  // Bit_Extender bit_extender_2
  Multiplexer #(.enable("false")) multiplexer_7 (.in0(1'b1), .in1(Go), .out(stop), .sel(and_2_out));
  // Probe on \总周期数 
  // Probe on \无条件分支数 
  // Probe on \条件分支成功数 
  Multiplexer #(.width(32), .enable("false")) multiplexer_8 (
    .in0(bit_extender_1_out), .in1(bit_extender_2_out), .out(multiplexer_8_out), .sel(SignedExt));
  Counter #(.width(16), .max('hffff)) counter_2 (
    .count(stop), .Q(\总周期数 ), .clk(CLK), .clr(RST));  // open: load, D, carry
  MIPS_Regifile mips_regifile_1 (
    .Din(multiplexer_4_out), .Clk(CLK), .R1(a0), .R2(mips_regifile_1_r2), .WE(\硬布线控制器_1_regwrite ),
    .W_num(multiplexer_6_out), .R1_num(multiplexer_2_out), .R2_num(multiplexer_3_out));
  Shifter #(.width(32)) shifter_1 (.in(bit_extender_2_out), .\dist (5'b00010), .out(shifter_1_out));
  Multiplexer #(.width(32), .enable("false")) multiplexer_9 (
    .in0(a0), .in1(32'h22), .out(multiplexer_9_out), .sel(syscall));
  Multiplexer #(.width(32), .enable("false")) multiplexer_10 (
    .in0(mips_regifile_1_r2), .in1(multiplexer_8_out), .out(multiplexer_10_out), .sel(\硬布线控制器_1_alu_src ));
  Multiplexer #(.width(5), .enable("false")) multiplexer_11 (
    .in0(rom_1_data[10:6]), .in1(a0[4:0]), .out(multiplexer_11_out), .sel(SRAV));
  MIPS_ALU mips_alu_1 (
    .X(multiplexer_9_out), .Y(multiplexer_10_out), .AluOP(\硬布线控制器_1_alu_op ), .Equal(equal), .Result(result),
    .shamt(multiplexer_11_out));  // open: Result_2
  Adder #(.width(32)) adder_2 (.a(shifter_1_out), .b(adder_1_out), .out(adder_2_out));  // open: cin, cout
  and and_3 (and_3_out, \硬布线控制器_1_beq , equal);
  and and_4 (and_4_out, ~equal, \硬布线控制器_1_bne );  // AND_Gate
  and and_5 (and_5_out, ~result[0], ~equal, BGTZ);  // AND_Gate
  Multiplexer #(.width(32), .enable("false")) multiplexer_12 (
    .in0(multiplexer_14_out), .in1({{16{1'b0}}, multiplexer_13_out}), .out(multiplexer_12_out), .sel(LHU));
  or or_1 (\硬布线控制器_1_jr [2], and_3_out, and_4_out, and_5_out);
  not not_1 (not_1_out, \硬布线控制器_1_memwrite );
  RAM #(.addrWidth(10), .dataWidth(32), .bus("separate")) ram_1 (
    .addr(result[11:2]), .din(mips_regifile_1_r2), .data(ram_1_data), .str(\硬布线控制器_1_memwrite ), .clk(CLK),
    .ld(not_1_out), .clr(RST));  // open: sel
  Multiplexer #(.width(16), .enable("false")) multiplexer_13 (
    .in0(multiplexer_14_out[15:0]), .in1(multiplexer_14_out[31:16]), .out(multiplexer_13_out), .sel(result[1]));
  Counter #(.width(16), .max('hffff)) counter_3 (
    .count(\硬布线控制器_1_jr [2]), .Q(\条件分支成功数 ), .clk(CLK), .clr(RST));  // open: load, D, carry
  Multiplexer #(.width(32), .enable("false")) multiplexer_14 (
    .in0(result), .in1(ram_1_data), .out(multiplexer_14_out), .sel(\硬布线控制器_1_memtoreg ));

  // Notes on the sheet:
  //   数码管输出应该用寄存器锁存，否则显示数据只能一闪而过
  //   可以通过项目增加Logisim库的方式将前几次实验完成的电路作为子电路引入到本电路中使用
  //   指令存储器
  //   指令字
  //   contents of rom_1 (hex, n*v repeats v):
  //   20090000 200b0010 34118483 20120404 118c00 129400 36318281 22520404 ad310000 2328820 21290004
  //   216bffff 1560fffb 200b0020 20090000 95310000 112020 20020022 c 21290002 216bffff 1560fff9 2002000a c
  //   shamt
  //   imm
  //   数码管输出
  //   JMP
  //   JR
  //   OP
  //   Func
  //   OP
  //   Func
  //   rs
  //   rt
  //   rd
  //   Beq
  //   Bne
  //   AluOP
  //   AluSrcB
  //   RegWrite
  //   JAL
  //   RegDst
  //   Syscall
  //   MemToReg
  //   MemWrite
  //   总复位信号应将除ROM以外所有存储组件全部清零
endmodule

// 单周期硬布线控制器
module \硬布线控制器  (
  input  [5:0] OP,
  input  [5:0] Func,
  output [3:0] ALU_OP,
  output MemToReg,
  output MemWrite,
  output ALU_SRC,
  output RegWrite,
  output SysCALL,
  output SignedExt,
  output RegDst,
  output Beq,
  output Bne,
  output JR,
  output JMP,
  output JAL,
  output SRAV,
  output LHU,
  output BGTZ
);

  \运算控制器  \u_运算控制器_1  (
    .OP0(OP[0]), .OP1(OP[1]), .OP2(OP[2]), .OP3(OP[3]), .OP4(OP[4]), .OP5(OP[5]), .F0(Func[0]), .F1(Func[1]),
    .F2(Func[2]), .F3(Func[3]), .F4(Func[4]), .F5(Func[5]), .S0(ALU_OP[0]), .S1(ALU_OP[1]), .S2(ALU_OP[2]),
    .S3(ALU_OP[3]));
  \控制信号生成  \u_控制信号生成_1  (
    .OP0(OP[0]), .OP1(OP[1]), .OP2(OP[2]), .OP3(OP[3]), .OP4(OP[4]), .OP5(OP[5]), .F0(Func[0]), .F1(Func[1]),
    .F2(Func[2]), .F3(Func[3]), .F4(Func[4]), .F5(Func[5]), .MemToReg(MemToReg), .MemWrite(MemWrite),
    .ALU_SRC(ALU_SRC), .RegWrite(RegWrite), .SysCALL(SysCALL), .SignedExt(SignedExt), .RegDst(RegDst),
    .BEQ(Beq), .BNE(Bne), .JR(JR), .JMP(JMP), .JAL(JAL), .SRAV(SRAV), .LHU(LHU), .BGTZ(BGTZ));

  // Other names for the same wires on the sheet: OP_CODE[5:0] = OP

  // Notes on the sheet:
  //   运算器控制器，根据指令生成运算器功能选择信号
endmodule

// 运算器控制器
module \运算控制器  (
  input  OP0,
  input  OP1,
  input  OP2,
  input  OP3,
  input  OP4,
  input  OP5,
  input  F0,
  input  F1,
  input  F2,
  input  F3,
  input  F4,
  input  F5,
  output S0,
  output S1,
  output S2,
  output S3
);

  wire and_1_out, and_2_out, and_3_out, and_4_out, and_5_out, and_6_out, and_7_out, and_8_out, and_9_out,
       and_10_out, and_11_out, and_12_out, and_13_out, and_14_out, and_15_out, and_16_out, and_17_out,
       and_18_out, and_19_out, and_20_out, and_21_out, and_22_out, and_23_out, and_24_out, and_25_out,
       and_26_out, and_27_out, and_28_out, and_29_out, and_30_out, and_31_out, and_32_out, and_33_out,
       and_34_out, and_35_out, and_36_out, and_37_out, and_38_out, and_39_out, and_40_out, and_41_out,
       and_42_out, not_1_out, not_2_out, not_3_out, not_4_out, not_5_out, not_6_out, not_7_out, not_8_out,
       not_9_out, not_10_out, not_11_out, not_12_out, not_13_out, not_14_out, not_15_out, not_16_out,
       not_17_out, not_18_out, not_19_out, not_20_out, not_21_out, not_22_out, not_23_out, not_24_out,
       not_25_out, not_26_out, not_27_out, not_28_out, not_29_out, not_30_out, not_31_out, not_32_out,
       not_33_out, not_34_out, not_35_out, not_36_out, not_37_out, not_38_out, not_39_out, not_40_out,
       not_41_out, not_42_out, not_43_out, not_44_out, not_45_out, not_46_out, not_47_out, not_48_out,
       not_49_out, not_50_out, not_51_out, not_52_out, not_53_out, not_54_out, not_55_out, not_56_out,
       not_57_out, not_58_out, not_59_out, not_60_out, not_61_out, not_62_out, not_63_out, not_64_out,
       not_65_out, not_66_out, not_67_out, not_68_out, not_69_out, not_70_out, not_71_out, not_72_out,
       not_73_out, not_74_out, not_75_out, not_76_out, not_77_out, not_78_out, not_79_out, not_80_out,
       not_81_out, not_82_out, not_83_out, not_84_out, not_85_out, not_86_out, not_87_out, not_88_out,
       not_89_out, not_90_out, not_91_out, not_92_out, not_93_out, not_94_out, not_95_out, not_96_out,
       not_97_out, not_98_out, not_99_out, not_100_out, not_101_out, not_102_out, not_103_out, not_104_out,
       not_105_out, not_106_out, not_107_out, not_108_out, not_109_out, not_110_out, not_111_out,
       not_112_out, not_113_out, not_114_out, not_115_out, not_116_out, not_117_out, not_118_out,
       not_119_out, not_120_out, not_121_out, not_122_out, not_123_out, not_124_out, not_125_out,
       not_126_out, not_127_out, not_128_out, not_129_out, not_130_out, not_131_out, not_132_out,
       not_133_out, not_134_out, not_135_out, not_136_out, not_137_out, not_138_out, not_139_out,
       not_140_out, not_141_out, not_142_out, not_143_out, not_144_out, not_145_out, not_146_out,
       not_147_out, not_148_out, not_149_out, not_150_out, not_151_out, not_152_out, not_153_out,
       not_154_out, not_155_out, not_156_out, not_157_out, not_158_out, not_159_out, not_160_out,
       not_161_out, not_162_out, not_163_out, not_164_out, not_165_out, not_166_out, not_167_out,
       not_168_out, not_169_out, not_170_out, not_171_out, not_172_out, not_173_out, not_174_out,
       not_175_out, not_176_out, not_177_out, not_178_out, not_179_out, not_180_out, not_181_out,
       not_182_out, not_183_out, not_184_out, not_185_out, not_186_out, not_187_out, not_188_out,
       not_189_out, not_190_out, not_191_out, not_192_out, not_193_out, not_194_out, not_195_out,
       not_196_out, not_197_out, not_198_out, not_199_out, not_200_out, not_201_out, not_202_out,
       not_203_out, not_204_out, not_205_out, not_206_out, not_207_out, not_208_out, not_209_out,
       not_210_out, not_211_out, not_212_out, not_213_out, not_214_out, not_215_out, not_216_out,
       not_217_out, not_218_out, not_219_out, not_220_out, not_221_out, not_222_out, not_223_out,
       not_224_out, not_225_out, not_226_out, not_227_out, not_228_out, not_229_out, not_230_out,
       not_231_out, not_232_out, not_233_out, not_234_out, not_235_out, not_236_out, not_237_out,
       not_238_out, not_239_out, not_240_out, not_241_out, not_242_out, not_243_out, not_244_out,
       not_245_out, not_246_out, not_247_out, not_248_out, not_249_out, not_250_out, not_251_out,
       not_252_out, not_253_out, not_254_out, not_255_out, not_256_out, not_257_out, not_258_out,
       not_259_out, not_260_out, not_261_out, not_262_out, not_263_out, not_264_out, not_265_out,
       not_266_out, not_267_out, not_268_out, not_269_out, not_270_out, not_271_out, not_272_out,
       not_273_out, not_274_out, not_275_out, not_276_out, not_277_out, not_278_out;

  not not_1 (not_1_out, OP5);
  not not_2 (not_2_out, OP4);
  not not_3 (not_3_out, OP3);
  not not_4 (not_4_out, OP2);
  not not_5 (not_5_out, OP1);
  not not_6 (not_6_out, OP0);
  not not_7 (not_7_out, F5);
  not not_8 (not_8_out, F4);
  not not_9 (not_9_out, F3);
  not not_10 (not_10_out, F2);
  not not_11 (not_11_out, OP5);
  not not_12 (not_12_out, OP4);
  not not_13 (not_13_out, OP3);
  not not_14 (not_14_out, OP2);
  not not_15 (not_15_out, OP1);
  not not_16 (not_16_out, OP0);
  not not_17 (not_17_out, F4);
  not not_18 (not_18_out, F3);
  not not_19 (not_19_out, F2);
  not not_20 (not_20_out, F1);
  not not_21 (not_21_out, F0);
  not not_22 (not_22_out, OP5);
  not not_23 (not_23_out, OP4);
  not not_24 (not_24_out, OP3);
  not not_25 (not_25_out, OP2);
  not not_26 (not_26_out, OP1);
  not not_27 (not_27_out, OP0);
  not not_28 (not_28_out, F4);
  not not_29 (not_29_out, F3);
  not not_30 (not_30_out, F2);
  not not_31 (not_31_out, F1);
  not not_32 (not_32_out, OP5);
  not not_33 (not_33_out, OP4);
  not not_34 (not_34_out, OP3);
  not not_35 (not_35_out, OP2);
  not not_36 (not_36_out, OP1);
  not not_37 (not_37_out, OP0);
  not not_38 (not_38_out, F4);
  not not_39 (not_39_out, F3);
  not not_40 (not_40_out, F1);
  not not_41 (not_41_out, F0);
  not not_42 (not_42_out, OP5);
  not not_43 (not_43_out, OP4);
  not not_44 (not_44_out, OP3);
  not not_45 (not_45_out, OP2);
  not not_46 (not_46_out, OP1);
  not not_47 (not_47_out, OP0);
  not not_48 (not_48_out, F4);
  not not_49 (not_49_out, F2);
  not not_50 (not_50_out, F0);
  not not_51 (not_51_out, OP5);
  not not_52 (not_52_out, OP4);
  not not_53 (not_53_out, OP2);
  not not_54 (not_54_out, OP1);
  not not_55 (not_55_out, OP0);
  not not_56 (not_56_out, OP5);
  not not_57 (not_57_out, OP4);
  not not_58 (not_58_out, OP1);
  not not_59 (not_59_out, OP0);
  not not_60 (not_60_out, OP5);
  not not_61 (not_61_out, OP4);
  not not_62 (not_62_out, OP2);
  not not_63 (not_63_out, OP1);
  not not_64 (not_64_out, OP5);
  not not_65 (not_65_out, OP4);
  not not_66 (not_66_out, OP2);
  not not_67 (not_67_out, OP0);
  not not_68 (not_68_out, OP4);
  not not_69 (not_69_out, OP3);
  not not_70 (not_70_out, OP2);
  not not_71 (not_71_out, OP4);
  not not_72 (not_72_out, OP2);
  not not_73 (not_73_out, OP5);
  not not_74 (not_74_out, OP4);
  not not_75 (not_75_out, OP3);
  not not_76 (not_76_out, OP2);
  not not_77 (not_77_out, OP1);
  not not_78 (not_78_out, OP0);
  not not_79 (not_79_out, F5);
  not not_80 (not_80_out, F4);
  not not_81 (not_81_out, F3);
  not not_82 (not_82_out, OP4);
  not not_83 (not_83_out, OP3);
  not not_84 (not_84_out, OP1);
  not not_85 (not_85_out, OP5);
  not not_86 (not_86_out, OP4);
  not not_87 (not_87_out, OP3);
  not not_88 (not_88_out, OP5);
  not not_89 (not_89_out, OP4);
  not not_90 (not_90_out, OP3);
  not not_91 (not_91_out, OP2);
  not not_92 (not_92_out, OP1);
  not not_93 (not_93_out, OP0);
  not not_94 (not_94_out, F5);
  not not_95 (not_95_out, F4);
  not not_96 (not_96_out, F3);
  not not_97 (not_97_out, F2);
  not not_98 (not_98_out, F0);
  not not_99 (not_99_out, OP5);
  not not_100 (not_100_out, OP4);
  not not_101 (not_101_out, OP3);
  not not_102 (not_102_out, OP2);
  not not_103 (not_103_out, OP1);
  not not_104 (not_104_out, OP0);
  not not_105 (not_105_out, F4);
  not not_106 (not_106_out, F3);
  not not_107 (not_107_out, F2);
  not not_108 (not_108_out, F0);
  not not_109 (not_109_out, OP5);
  not not_110 (not_110_out, OP4);
  not not_111 (not_111_out, OP3);
  not not_112 (not_112_out, OP2);
  not not_113 (not_113_out, OP1);
  not not_114 (not_114_out, OP0);
  not not_115 (not_115_out, F4);
  not not_116 (not_116_out, F3);
  not not_117 (not_117_out, F1);
  not not_118 (not_118_out, F0);
  not not_119 (not_119_out, OP5);
  not not_120 (not_120_out, OP4);
  not not_121 (not_121_out, OP3);
  not not_122 (not_122_out, OP2);
  not not_123 (not_123_out, OP1);
  not not_124 (not_124_out, OP0);
  not not_125 (not_125_out, F4);
  not not_126 (not_126_out, F3);
  not not_127 (not_127_out, OP5);
  not not_128 (not_128_out, OP4);
  not not_129 (not_129_out, OP3);
  not not_130 (not_130_out, OP2);
  not not_131 (not_131_out, OP1);
  not not_132 (not_132_out, OP0);
  not not_133 (not_133_out, F4);
  not not_134 (not_134_out, F2);
  not not_135 (not_135_out, F0);
  not not_136 (not_136_out, OP5);
  not not_137 (not_137_out, OP4);
  not not_138 (not_138_out, OP1);
  not not_139 (not_139_out, OP0);
  not not_140 (not_140_out, OP5);
  not not_141 (not_141_out, OP4);
  not not_142 (not_142_out, OP2);
  not not_143 (not_143_out, OP0);
  not not_144 (not_144_out, OP5);
  not not_145 (not_145_out, OP4);
  not not_146 (not_146_out, OP3);
  not not_147 (not_147_out, OP2);
  not not_148 (not_148_out, OP1);
  not not_149 (not_149_out, OP0);
  not not_150 (not_150_out, F4);
  not not_151 (not_151_out, F3);
  not not_152 (not_152_out, F2);
  not not_153 (not_153_out, OP5);
  not not_154 (not_154_out, OP4);
  not not_155 (not_155_out, OP3);
  not not_156 (not_156_out, OP5);
  not not_157 (not_157_out, OP4);
  not not_158 (not_158_out, OP3);
  not not_159 (not_159_out, OP2);
  not not_160 (not_160_out, OP1);
  not not_161 (not_161_out, OP0);
  not not_162 (not_162_out, F4);
  not not_163 (not_163_out, F3);
  not not_164 (not_164_out, F2);
  not not_165 (not_165_out, F1);
  not not_166 (not_166_out, F0);
  not not_167 (not_167_out, OP5);
  not not_168 (not_168_out, OP4);
  not not_169 (not_169_out, OP3);
  not not_170 (not_170_out, OP2);
  not not_171 (not_171_out, OP1);
  not not_172 (not_172_out, OP0);
  not not_173 (not_173_out, F4);
  not not_174 (not_174_out, F3);
  not not_175 (not_175_out, F2);
  not not_176 (not_176_out, F1);
  not not_177 (not_177_out, OP5);
  not not_178 (not_178_out, OP4);
  not not_179 (not_179_out, OP3);
  not not_180 (not_180_out, OP2);
  not not_181 (not_181_out, OP1);
  not not_182 (not_182_out, OP0);
  not not_183 (not_183_out, F4);
  not not_184 (not_184_out, F3);
  not not_185 (not_185_out, F2);
  not not_186 (not_186_out, F0);
  not not_187 (not_187_out, OP5);
  not not_188 (not_188_out, OP4);
  not not_189 (not_189_out, OP3);
  not not_190 (not_190_out, OP2);
  not not_191 (not_191_out, OP1);
  not not_192 (not_192_out, OP0);
  not not_193 (not_193_out, F4);
  not not_194 (not_194_out, F3);
  not not_195 (not_195_out, F1);
  not not_196 (not_196_out, F0);
  not not_197 (not_197_out, OP5);
  not not_198 (not_198_out, OP4);
  not not_199 (not_199_out, OP3);
  not not_200 (not_200_out, OP2);
  not not_201 (not_201_out, OP1);
  not not_202 (not_202_out, OP0);
  not not_203 (not_203_out, F4);
  not not_204 (not_204_out, F2);
  not not_205 (not_205_out, OP5);
  not not_206 (not_206_out, OP4);
  not not_207 (not_207_out, OP2);
  not not_208 (not_208_out, OP1);
  not not_209 (not_209_out, OP0);
  not not_210 (not_210_out, OP5);
  not not_211 (not_211_out, OP4);
  not not_212 (not_212_out, OP1);
  not not_213 (not_213_out, OP0);
  not not_214 (not_214_out, OP5);
  not not_215 (not_215_out, OP4);
  not not_216 (not_216_out, OP2);
  not not_217 (not_217_out, OP1);
  not not_218 (not_218_out, OP4);
  not not_219 (not_219_out, OP3);
  not not_220 (not_220_out, OP2);
  not not_221 (not_221_out, OP4);
  not not_222 (not_222_out, OP2);
  not not_223 (not_223_out, OP5);
  not not_224 (not_224_out, OP4);
  not not_225 (not_225_out, OP3);
  not not_226 (not_226_out, OP2);
  not not_227 (not_227_out, OP1);
  not not_228 (not_228_out, OP0);
  not not_229 (not_229_out, F4);
  not not_230 (not_230_out, F3);
  not not_231 (not_231_out, F2);
  not not_232 (not_232_out, OP4);
  not not_233 (not_233_out, OP3);
  not not_234 (not_234_out, OP1);
  not not_235 (not_235_out, OP5);
  not not_236 (not_236_out, OP4);
  not not_237 (not_237_out, OP3);
  not not_238 (not_238_out, OP2);
  not not_239 (not_239_out, OP1);
  not not_240 (not_240_out, OP0);
  not not_241 (not_241_out, F4);
  not not_242 (not_242_out, F3);
  not not_243 (not_243_out, F1);
  not not_244 (not_244_out, OP5);
  not not_245 (not_245_out, OP4);
  not not_246 (not_246_out, OP3);
  not not_247 (not_247_out, OP2);
  not not_248 (not_248_out, OP1);
  not not_249 (not_249_out, OP0);
  not not_250 (not_250_out, F4);
  not not_251 (not_251_out, F3);
  not not_252 (not_252_out, OP5);
  not not_253 (not_253_out, OP4);
  not not_254 (not_254_out, OP3);
  not not_255 (not_255_out, OP2);
  not not_256 (not_256_out, OP1);
  not not_257 (not_257_out, OP0);
  not not_258 (not_258_out, F4);
  not not_259 (not_259_out, F2);
  not not_260 (not_260_out, F0);
  not not_261 (not_261_out, OP5);
  not not_262 (not_262_out, OP4);
  not not_263 (not_263_out, OP3);
  not not_264 (not_264_out, OP2);
  not not_265 (not_265_out, OP1);
  not not_266 (not_266_out, OP0);
  not not_267 (not_267_out, F4);
  not not_268 (not_268_out, F2);
  not not_269 (not_269_out, OP5);
  not not_270 (not_270_out, OP4);
  not not_271 (not_271_out, OP2);
  not not_272 (not_272_out, OP0);
  not not_273 (not_273_out, OP5);
  not not_274 (not_274_out, OP4);
  not not_275 (not_275_out, OP1);
  not not_276 (not_276_out, OP5);
  not not_277 (not_277_out, OP4);
  not not_278 (not_278_out, OP3);
  and and_1 (and_1_out, not_1_out, not_2_out, not_3_out, not_4_out, not_5_out, not_6_out, not_7_out, not_8_out, not_9_out, not_10_out, F1, F0);
  and and_2 (and_2_out, not_11_out, not_12_out, not_13_out, not_14_out, not_15_out, not_16_out, F5, not_17_out, not_18_out, not_19_out, not_20_out, not_21_out);
  and and_3 (and_3_out, not_22_out, not_23_out, not_24_out, not_25_out, not_26_out, not_27_out, F5, not_28_out, not_29_out, not_30_out, not_31_out, F0);
  and and_4 (and_4_out, not_32_out, not_33_out, not_34_out, not_35_out, not_36_out, not_37_out, F5, not_38_out, not_39_out, F2, not_40_out, not_41_out);
  and and_5 (and_5_out, not_42_out, not_43_out, not_44_out, not_45_out, not_46_out, not_47_out, F5, not_48_out, F3, not_49_out, F1, not_50_out);
  and and_6 (and_6_out, not_51_out, not_52_out, OP3, not_53_out, not_54_out, not_55_out);
  and and_7 (and_7_out, not_56_out, not_57_out, OP3, OP2, not_58_out, not_59_out);
  and and_8 (and_8_out, not_60_out, not_61_out, OP3, not_62_out, not_63_out, OP0);
  and and_9 (and_9_out, not_64_out, not_65_out, OP3, not_66_out, OP1, not_67_out);
  and and_10 (and_10_out, OP5, not_68_out, not_69_out, not_70_out, OP1, OP0);
  and and_11 (and_11_out, OP5, not_71_out, OP3, not_72_out, OP1, OP0);
  and and_12 (and_12_out, not_73_out, not_74_out, not_75_out, not_76_out, not_77_out, not_78_out, not_79_out, not_80_out, not_81_out, F2, F1, F0);
  and and_13 (and_13_out, OP5, not_82_out, not_83_out, OP2, not_84_out, OP0);
  and and_14 (and_14_out, not_85_out, not_86_out, not_87_out, OP2, OP1, OP0);
  and and_15 (and_15_out, not_88_out, not_89_out, not_90_out, not_91_out, not_92_out, not_93_out, not_94_out, not_95_out, not_96_out, not_97_out, F1, not_98_out);
  and and_16 (and_16_out, not_99_out, not_100_out, not_101_out, not_102_out, not_103_out, not_104_out, F5, not_105_out, not_106_out, not_107_out, F1, not_108_out);
  and and_17 (and_17_out, not_109_out, not_110_out, not_111_out, not_112_out, not_113_out, not_114_out, F5, not_115_out, not_116_out, F2, not_117_out, not_118_out);
  and and_18 (and_18_out, not_119_out, not_120_out, not_121_out, not_122_out, not_123_out, not_124_out, F5, not_125_out, not_126_out, F2, F1, F0);
  and and_19 (and_19_out, not_127_out, not_128_out, not_129_out, not_130_out, not_131_out, not_132_out, F5, not_133_out, F3, not_134_out, F1, not_135_out);
  and and_20 (and_20_out, not_136_out, not_137_out, OP3, OP2, not_138_out, not_139_out);
  and and_21 (and_21_out, not_140_out, not_141_out, OP3, not_142_out, OP1, not_143_out);
  and and_22 (and_22_out, not_144_out, not_145_out, not_146_out, not_147_out, not_148_out, not_149_out, F5, not_150_out, not_151_out, not_152_out, F1, F0);
  and and_23 (and_23_out, not_153_out, not_154_out, not_155_out, OP2, OP1, OP0);
  and and_24 (and_24_out, not_156_out, not_157_out, not_158_out, not_159_out, not_160_out, not_161_out, F5, not_162_out, not_163_out, not_164_out, not_165_out, not_166_out);
  and and_25 (and_25_out, not_167_out, not_168_out, not_169_out, not_170_out, not_171_out, not_172_out, F5, not_173_out, not_174_out, not_175_out, not_176_out, F0);
  and and_26 (and_26_out, not_177_out, not_178_out, not_179_out, not_180_out, not_181_out, not_182_out, F5, not_183_out, not_184_out, not_185_out, F1, not_186_out);
  and and_27 (and_27_out, not_187_out, not_188_out, not_189_out, not_190_out, not_191_out, not_192_out, F5, not_193_out, not_194_out, F2, not_195_out, not_196_out);
  and and_28 (and_28_out, not_197_out, not_198_out, not_199_out, not_200_out, not_201_out, not_202_out, F5, not_203_out, F3, not_204_out, F1, F0);
  and and_29 (and_29_out, not_205_out, not_206_out, OP3, not_207_out, not_208_out, not_209_out);
  and and_30 (and_30_out, not_210_out, not_211_out, OP3, OP2, not_212_out, not_213_out);
  and and_31 (and_31_out, not_214_out, not_215_out, OP3, not_216_out, not_217_out, OP0);
  and and_32 (and_32_out, OP5, not_218_out, not_219_out, not_220_out, OP1, OP0);
  and and_33 (and_33_out, OP5, not_221_out, OP3, not_222_out, OP1, OP0);
  and and_34 (and_34_out, not_223_out, not_224_out, not_225_out, not_226_out, not_227_out, not_228_out, F5, not_229_out, not_230_out, not_231_out, F1, F0);
  and and_35 (and_35_out, OP5, not_232_out, not_233_out, OP2, not_234_out, OP0);
  and and_36 (and_36_out, not_235_out, not_236_out, not_237_out, not_238_out, not_239_out, not_240_out, F5, not_241_out, not_242_out, F2, not_243_out, F0);
  and and_37 (and_37_out, not_244_out, not_245_out, not_246_out, not_247_out, not_248_out, not_249_out, F5, not_250_out, not_251_out, F2, F1, F0);
  and and_38 (and_38_out, not_252_out, not_253_out, not_254_out, not_255_out, not_256_out, not_257_out, F5, not_258_out, F3, not_259_out, F1, not_260_out);
  and and_39 (and_39_out, not_261_out, not_262_out, not_263_out, not_264_out, not_265_out, not_266_out, F5, not_267_out, F3, not_268_out, F1, F0);
  and and_40 (and_40_out, not_269_out, not_270_out, OP3, not_271_out, OP1, not_272_out);
  and and_41 (and_41_out, not_273_out, not_274_out, OP3, OP2, not_275_out, OP0);
  and and_42 (and_42_out, not_276_out, not_277_out, not_278_out, OP2, OP1, OP0);
  or or_1 (S1, and_15_out, and_16_out, and_17_out, and_18_out, and_19_out, and_20_out, and_21_out, and_22_out, and_23_out);
  or or_2 (S3, and_36_out, and_37_out, and_38_out, and_39_out, and_40_out, and_41_out, and_42_out);
  or or_3 (S0, and_1_out, and_2_out, and_3_out, and_4_out, and_5_out, and_6_out, and_7_out, and_8_out, and_9_out, and_10_out, and_11_out, and_12_out, and_13_out, and_14_out);
  or or_4 (S2, and_24_out, and_25_out, and_26_out, and_27_out, and_28_out, and_29_out, and_30_out, and_31_out, and_32_out, and_33_out, and_34_out, and_35_out);
endmodule

// 控制信号生成
module \控制信号生成  (
  input  OP0,
  input  OP1,
  input  OP2,
  input  OP3,
  input  OP4,
  input  OP5,
  input  F0,
  input  F1,
  input  F2,
  input  F3,
  input  F4,
  input  F5,
  output MemToReg,
  output MemWrite,
  output ALU_SRC,
  output RegWrite,
  output SysCALL,
  output SignedExt,
  output RegDst,
  output BEQ,
  output BNE,
  output JR,
  output JMP,
  output JAL,
  output SRAV,
  output LHU,
  output BGTZ
);

  wire and_1_out, and_2_out, and_4_out, and_5_out, and_6_out, and_7_out, and_8_out, and_9_out, and_10_out,
       and_11_out, and_12_out, and_13_out, and_14_out, and_15_out, and_16_out, and_17_out, and_18_out,
       and_19_out, and_20_out, and_21_out, and_22_out, and_23_out, and_24_out, and_25_out, and_26_out,
       and_27_out, and_28_out, and_29_out, and_30_out, and_31_out, and_32_out, and_34_out, and_35_out,
       and_36_out, and_37_out, and_38_out, and_39_out, and_40_out, and_41_out, and_42_out, and_43_out,
       and_44_out, and_45_out, and_46_out, and_47_out, and_48_out, and_49_out, and_50_out, and_51_out,
       and_52_out, and_53_out, and_54_out, and_55_out, and_59_out, and_60_out, and_61_out, not_1_out,
       not_2_out, not_3_out, not_4_out, not_5_out, not_6_out, not_7_out, not_8_out, not_9_out, not_10_out,
       not_11_out, not_12_out, not_13_out, not_14_out, not_15_out, not_16_out, not_17_out, not_18_out,
       not_19_out, not_20_out, not_21_out, not_22_out, not_23_out, not_24_out, not_25_out, not_26_out,
       not_27_out, not_28_out, not_29_out, not_30_out, not_31_out, not_32_out, not_33_out, not_34_out,
       not_35_out, not_36_out, not_37_out, not_38_out, not_39_out, not_40_out, not_41_out, not_42_out,
       not_43_out, not_44_out, not_45_out, not_46_out, not_47_out, not_48_out, not_49_out, not_50_out,
       not_51_out, not_52_out, not_53_out, not_54_out, not_55_out, not_56_out, not_57_out, not_58_out,
       not_59_out, not_60_out, not_61_out, not_62_out, not_63_out, not_64_out, not_65_out, not_66_out,
       not_67_out, not_68_out, not_69_out, not_70_out, not_71_out, not_72_out, not_73_out, not_74_out,
       not_75_out, not_76_out, not_77_out, not_78_out, not_79_out, not_80_out, not_81_out, not_82_out,
       not_83_out, not_84_out, not_85_out, not_86_out, not_87_out, not_88_out, not_89_out, not_90_out,
       not_91_out, not_92_out, not_93_out, not_94_out, not_95_out, not_96_out, not_97_out, not_98_out,
       not_99_out, not_100_out, not_101_out, not_102_out, not_103_out, not_104_out, not_105_out, not_106_out,
       not_107_out, not_108_out, not_109_out, not_110_out, not_111_out, not_112_out, not_113_out,
       not_114_out, not_115_out, not_116_out, not_117_out, not_118_out, not_119_out, not_120_out,
       not_121_out, not_122_out, not_123_out, not_124_out, not_125_out, not_126_out, not_127_out,
       not_128_out, not_129_out, not_130_out, not_131_out, not_132_out, not_133_out, not_134_out,
       not_135_out, not_136_out, not_137_out, not_138_out, not_139_out, not_140_out, not_141_out,
       not_142_out, not_143_out, not_144_out, not_145_out, not_146_out, not_147_out, not_148_out,
       not_149_out, not_150_out, not_151_out, not_152_out, not_153_out, not_154_out, not_155_out,
       not_156_out, not_157_out, not_158_out, not_159_out, not_160_out, not_161_out, not_162_out,
       not_163_out, not_164_out, not_165_out, not_166_out, not_167_out, not_168_out, not_169_out,
       not_170_out, not_171_out, not_172_out, not_173_out, not_174_out, not_175_out, not_176_out,
       not_177_out, not_178_out, not_179_out, not_180_out, not_181_out, not_182_out, not_183_out,
       not_184_out, not_185_out, not_186_out, not_187_out, not_188_out, not_189_out, not_190_out,
       not_191_out, not_192_out, not_193_out, not_194_out, not_195_out, not_196_out, not_197_out,
       not_198_out, not_199_out, not_200_out, not_201_out, not_202_out, not_203_out, not_204_out,
       not_205_out, not_206_out, not_207_out, not_208_out, not_209_out, not_210_out, not_211_out,
       not_212_out, not_213_out, not_214_out, not_215_out, not_216_out, not_217_out, not_218_out,
       not_219_out, not_220_out, not_221_out, not_222_out, not_223_out, not_224_out, not_225_out,
       not_226_out, not_227_out, not_228_out, not_229_out, not_230_out, not_231_out, not_232_out,
       not_233_out, not_234_out, not_235_out, not_236_out, not_237_out, not_238_out, not_239_out,
       not_240_out, not_241_out, not_242_out, not_243_out, not_244_out, not_245_out, not_246_out,
       not_247_out, not_248_out, not_249_out, not_250_out, not_251_out, not_252_out, not_253_out,
       not_254_out, not_255_out, not_256_out, not_257_out, not_258_out, not_259_out, not_260_out,
       not_261_out, not_262_out, not_263_out, not_264_out, not_265_out, not_266_out, not_267_out,
       not_268_out, not_269_out, not_270_out, not_271_out, not_272_out, not_273_out, not_274_out,
       not_275_out, not_276_out, not_277_out, not_278_out, not_279_out, not_280_out, not_281_out,
       not_282_out, not_283_out, not_284_out, not_285_out, not_286_out, not_287_out, not_288_out,
       not_289_out, not_290_out, not_291_out, not_292_out, not_293_out, not_294_out, not_295_out,
       not_296_out, not_297_out, not_298_out, not_299_out, not_300_out, not_301_out, not_302_out,
       not_303_out, not_304_out, not_305_out, not_306_out, not_307_out, not_308_out, not_309_out,
       not_310_out, not_311_out, not_312_out, not_313_out, not_314_out, not_315_out, not_316_out,
       not_317_out, not_318_out, not_319_out, not_320_out, not_321_out, not_322_out, not_323_out,
       not_324_out, not_325_out, not_326_out, not_327_out, not_328_out, not_329_out, not_330_out,
       not_331_out, not_332_out, not_333_out, not_334_out, not_335_out, not_336_out, not_337_out,
       not_338_out, not_339_out, not_340_out, not_341_out, not_342_out, not_343_out, not_344_out,
       not_345_out, not_346_out, not_347_out, not_348_out, not_349_out, not_350_out, not_351_out,
       not_352_out, not_353_out, not_354_out, not_355_out, not_356_out, not_357_out, not_358_out,
       not_359_out, not_360_out, not_361_out, not_362_out, not_363_out, not_364_out, not_365_out,
       not_366_out, not_367_out, not_368_out, not_369_out, not_370_out, not_371_out, not_372_out,
       not_373_out, not_374_out, not_375_out, not_376_out, not_377_out, not_378_out, not_379_out,
       not_380_out, not_381_out, not_382_out, not_383_out, not_384_out, not_385_out, not_386_out,
       not_387_out, not_388_out, not_389_out, not_390_out, not_391_out, not_392_out, not_393_out,
       not_394_out, not_395_out, not_396_out, not_397_out, not_398_out, not_399_out, not_400_out,
       not_401_out, not_402_out, not_403_out, not_404_out, not_405_out, not_406_out, not_407_out,
       not_408_out, not_409_out, not_410_out, not_411_out, not_412_out, not_413_out, not_414_out,
       not_415_out, not_416_out, not_417_out, not_418_out, not_419_out, not_420_out;

  not not_1 (not_1_out, OP4);
  not not_2 (not_2_out, OP3);
  not not_3 (not_3_out, OP2);
  not not_4 (not_4_out, OP4);
  not not_5 (not_5_out, OP3);
  not not_6 (not_6_out, OP1);
  not not_7 (not_7_out, OP4);
  not not_8 (not_8_out, OP2);
  not not_9 (not_9_out, OP5);
  not not_10 (not_10_out, OP4);
  not not_11 (not_11_out, OP2);
  not not_12 (not_12_out, OP1);
  not not_13 (not_13_out, OP0);
  not not_14 (not_14_out, OP5);
  not not_15 (not_15_out, OP4);
  not not_16 (not_16_out, OP1);
  not not_17 (not_17_out, OP0);
  not not_18 (not_18_out, OP5);
  not not_19 (not_19_out, OP4);
  not not_20 (not_20_out, OP2);
  not not_21 (not_21_out, OP1);
  not not_22 (not_22_out, OP5);
  not not_23 (not_23_out, OP4);
  not not_24 (not_24_out, OP2);
  not not_25 (not_25_out, OP0);
  not not_26 (not_26_out, OP5);
  not not_27 (not_27_out, OP4);
  not not_28 (not_28_out, OP1);
  not not_29 (not_29_out, OP4);
  not not_30 (not_30_out, OP3);
  not not_31 (not_31_out, OP2);
  not not_32 (not_32_out, OP4);
  not not_33 (not_33_out, OP2);
  not not_34 (not_34_out, OP4);
  not not_35 (not_35_out, OP3);
  not not_36 (not_36_out, OP1);
  not not_37 (not_37_out, OP5);
  not not_38 (not_38_out, OP4);
  not not_39 (not_39_out, OP3);
  not not_40 (not_40_out, OP2);
  not not_41 (not_41_out, OP1);
  not not_42 (not_42_out, OP0);
  not not_43 (not_43_out, F5);
  not not_44 (not_44_out, F4);
  not not_45 (not_45_out, F3);
  not not_46 (not_46_out, F2);
  not not_47 (not_47_out, F1);
  not not_48 (not_48_out, F0);
  not not_49 (not_49_out, OP5);
  not not_50 (not_50_out, OP4);
  not not_51 (not_51_out, OP3);
  not not_52 (not_52_out, OP2);
  not not_53 (not_53_out, OP1);
  not not_54 (not_54_out, OP0);
  not not_55 (not_55_out, F5);
  not not_56 (not_56_out, F4);
  not not_57 (not_57_out, F3);
  not not_58 (not_58_out, F2);
  not not_59 (not_59_out, OP5);
  not not_60 (not_60_out, OP4);
  not not_61 (not_61_out, OP3);
  not not_62 (not_62_out, OP2);
  not not_63 (not_63_out, OP1);
  not not_64 (not_64_out, OP0);
  not not_65 (not_65_out, F5);
  not not_66 (not_66_out, F4);
  not not_67 (not_67_out, F3);
  not not_68 (not_68_out, F2);
  not not_69 (not_69_out, F0);
  not not_70 (not_70_out, OP5);
  not not_71 (not_71_out, OP4);
  not not_72 (not_72_out, OP3);
  not not_73 (not_73_out, OP2);
  not not_74 (not_74_out, OP1);
  not not_75 (not_75_out, OP0);
  not not_76 (not_76_out, F4);
  not not_77 (not_77_out, F3);
  not not_78 (not_78_out, F2);
  not not_79 (not_79_out, F1);
  not not_80 (not_80_out, F0);
  not not_81 (not_81_out, OP5);
  not not_82 (not_82_out, OP4);
  not not_83 (not_83_out, OP3);
  not not_84 (not_84_out, OP2);
  not not_85 (not_85_out, OP1);
  not not_86 (not_86_out, OP0);
  not not_87 (not_87_out, F4);
  not not_88 (not_88_out, F3);
  not not_89 (not_89_out, F2);
  not not_90 (not_90_out, F1);
  not not_91 (not_91_out, OP5);
  not not_92 (not_92_out, OP4);
  not not_93 (not_93_out, OP3);
  not not_94 (not_94_out, OP2);
  not not_95 (not_95_out, OP1);
  not not_96 (not_96_out, OP0);
  not not_97 (not_97_out, F4);
  not not_98 (not_98_out, F3);
  not not_99 (not_99_out, F2);
  not not_100 (not_100_out, F0);
  not not_101 (not_101_out, OP5);
  not not_102 (not_102_out, OP4);
  not not_103 (not_103_out, OP3);
  not not_104 (not_104_out, OP2);
  not not_105 (not_105_out, OP1);
  not not_106 (not_106_out, OP0);
  not not_107 (not_107_out, F4);
  not not_108 (not_108_out, F3);
  not not_109 (not_109_out, F1);
  not not_110 (not_110_out, F0);
  not not_111 (not_111_out, OP5);
  not not_112 (not_112_out, OP4);
  not not_113 (not_113_out, OP3);
  not not_114 (not_114_out, OP2);
  not not_115 (not_115_out, OP1);
  not not_116 (not_116_out, OP0);
  not not_117 (not_117_out, F4);
  not not_118 (not_118_out, F3);
  not not_119 (not_119_out, F1);
  not not_120 (not_120_out, OP5);
  not not_121 (not_121_out, OP4);
  not not_122 (not_122_out, OP3);
  not not_123 (not_123_out, OP2);
  not not_124 (not_124_out, OP1);
  not not_125 (not_125_out, OP0);
  not not_126 (not_126_out, F4);
  not not_127 (not_127_out, F3);
  not not_128 (not_128_out, OP5);
  not not_129 (not_129_out, OP4);
  not not_130 (not_130_out, OP3);
  not not_131 (not_131_out, OP2);
  not not_132 (not_132_out, OP1);
  not not_133 (not_133_out, OP0);
  not not_134 (not_134_out, F4);
  not not_135 (not_135_out, F2);
  not not_136 (not_136_out, F0);
  not not_137 (not_137_out, OP5);
  not not_138 (not_138_out, OP4);
  not not_139 (not_139_out, OP3);
  not not_140 (not_140_out, OP2);
  not not_141 (not_141_out, OP1);
  not not_142 (not_142_out, OP0);
  not not_143 (not_143_out, F4);
  not not_144 (not_144_out, F2);
  not not_145 (not_145_out, OP5);
  not not_146 (not_146_out, OP4);
  not not_147 (not_147_out, OP3);
  not not_148 (not_148_out, OP2);
  not not_149 (not_149_out, OP5);
  not not_150 (not_150_out, OP4);
  not not_151 (not_151_out, OP2);
  not not_152 (not_152_out, OP1);
  not not_153 (not_153_out, OP0);
  not not_154 (not_154_out, OP5);
  not not_155 (not_155_out, OP4);
  not not_156 (not_156_out, OP1);
  not not_157 (not_157_out, OP0);
  not not_158 (not_158_out, OP5);
  not not_159 (not_159_out, OP4);
  not not_160 (not_160_out, OP2);
  not not_161 (not_161_out, OP1);
  not not_162 (not_162_out, OP5);
  not not_163 (not_163_out, OP4);
  not not_164 (not_164_out, OP2);
  not not_165 (not_165_out, OP0);
  not not_166 (not_166_out, OP5);
  not not_167 (not_167_out, OP4);
  not not_168 (not_168_out, OP1);
  not not_169 (not_169_out, OP4);
  not not_170 (not_170_out, OP3);
  not not_171 (not_171_out, OP2);
  not not_172 (not_172_out, OP5);
  not not_173 (not_173_out, OP4);
  not not_174 (not_174_out, OP3);
  not not_175 (not_175_out, OP2);
  not not_176 (not_176_out, OP1);
  not not_177 (not_177_out, OP0);
  not not_178 (not_178_out, F5);
  not not_179 (not_179_out, F4);
  not not_180 (not_180_out, F3);
  not not_181 (not_181_out, OP5);
  not not_182 (not_182_out, OP4);
  not not_183 (not_183_out, OP3);
  not not_184 (not_184_out, OP2);
  not not_185 (not_185_out, OP1);
  not not_186 (not_186_out, OP0);
  not not_187 (not_187_out, F4);
  not not_188 (not_188_out, F3);
  not not_189 (not_189_out, F2);
  not not_190 (not_190_out, OP4);
  not not_191 (not_191_out, OP3);
  not not_192 (not_192_out, OP1);
  not not_193 (not_193_out, OP5);
  not not_194 (not_194_out, OP4);
  not not_195 (not_195_out, OP3);
  not not_196 (not_196_out, OP2);
  not not_197 (not_197_out, OP1);
  not not_198 (not_198_out, OP0);
  not not_199 (not_199_out, F5);
  not not_200 (not_200_out, F4);
  not not_201 (not_201_out, F1);
  not not_202 (not_202_out, F0);
  not not_203 (not_203_out, OP5);
  not not_204 (not_204_out, OP4);
  not not_205 (not_205_out, OP3);
  not not_206 (not_206_out, OP1);
  not not_207 (not_207_out, OP0);
  not not_208 (not_208_out, OP5);
  not not_209 (not_209_out, OP4);
  not not_210 (not_210_out, OP3);
  not not_211 (not_211_out, OP1);
  not not_212 (not_212_out, OP5);
  not not_213 (not_213_out, OP4);
  not not_214 (not_214_out, OP2);
  not not_215 (not_215_out, OP1);
  not not_216 (not_216_out, OP0);
  not not_217 (not_217_out, OP5);
  not not_218 (not_218_out, OP4);
  not not_219 (not_219_out, OP2);
  not not_220 (not_220_out, OP1);
  not not_221 (not_221_out, OP5);
  not not_222 (not_222_out, OP4);
  not not_223 (not_223_out, OP2);
  not not_224 (not_224_out, OP0);
  not not_225 (not_225_out, OP4);
  not not_226 (not_226_out, OP3);
  not not_227 (not_227_out, OP2);
  not not_228 (not_228_out, OP4);
  not not_229 (not_229_out, OP2);
  not not_230 (not_230_out, OP5);
  not not_231 (not_231_out, OP4);
  not not_232 (not_232_out, OP3);
  not not_233 (not_233_out, OP4);
  not not_234 (not_234_out, OP3);
  not not_235 (not_235_out, OP1);
  not not_236 (not_236_out, OP5);
  not not_237 (not_237_out, OP4);
  not not_238 (not_238_out, OP3);
  not not_239 (not_239_out, OP2);
  not not_240 (not_240_out, OP1);
  not not_241 (not_241_out, OP0);
  not not_242 (not_242_out, F5);
  not not_243 (not_243_out, F4);
  not not_244 (not_244_out, F3);
  not not_245 (not_245_out, F2);
  not not_246 (not_246_out, F1);
  not not_247 (not_247_out, F0);
  not not_248 (not_248_out, OP5);
  not not_249 (not_249_out, OP4);
  not not_250 (not_250_out, OP3);
  not not_251 (not_251_out, OP2);
  not not_252 (not_252_out, OP1);
  not not_253 (not_253_out, OP0);
  not not_254 (not_254_out, F5);
  not not_255 (not_255_out, F4);
  not not_256 (not_256_out, F3);
  not not_257 (not_257_out, F2);
  not not_258 (not_258_out, OP5);
  not not_259 (not_259_out, OP4);
  not not_260 (not_260_out, OP3);
  not not_261 (not_261_out, OP2);
  not not_262 (not_262_out, OP1);
  not not_263 (not_263_out, OP0);
  not not_264 (not_264_out, F5);
  not not_265 (not_265_out, F4);
  not not_266 (not_266_out, F3);
  not not_267 (not_267_out, F2);
  not not_268 (not_268_out, F0);
  not not_269 (not_269_out, OP5);
  not not_270 (not_270_out, OP4);
  not not_271 (not_271_out, OP3);
  not not_272 (not_272_out, OP2);
  not not_273 (not_273_out, OP1);
  not not_274 (not_274_out, OP0);
  not not_275 (not_275_out, F4);
  not not_276 (not_276_out, F3);
  not not_277 (not_277_out, F2);
  not not_278 (not_278_out, F1);
  not not_279 (not_279_out, F0);
  not not_280 (not_280_out, OP5);
  not not_281 (not_281_out, OP4);
  not not_282 (not_282_out, OP3);
  not not_283 (not_283_out, OP2);
  not not_284 (not_284_out, OP1);
  not not_285 (not_285_out, OP0);
  not not_286 (not_286_out, F4);
  not not_287 (not_287_out, F3);
  not not_288 (not_288_out, F2);
  not not_289 (not_289_out, F1);
  not not_290 (not_290_out, OP5);
  not not_291 (not_291_out, OP4);
  not not_292 (not_292_out, OP3);
  not not_293 (not_293_out, OP2);
  not not_294 (not_294_out, OP1);
  not not_295 (not_295_out, OP0);
  not not_296 (not_296_out, F4);
  not not_297 (not_297_out, F3);
  not not_298 (not_298_out, F2);
  not not_299 (not_299_out, F0);
  not not_300 (not_300_out, OP5);
  not not_301 (not_301_out, OP4);
  not not_302 (not_302_out, OP3);
  not not_303 (not_303_out, OP2);
  not not_304 (not_304_out, OP1);
  not not_305 (not_305_out, OP0);
  not not_306 (not_306_out, F4);
  not not_307 (not_307_out, F3);
  not not_308 (not_308_out, F1);
  not not_309 (not_309_out, F0);
  not not_310 (not_310_out, OP5);
  not not_311 (not_311_out, OP4);
  not not_312 (not_312_out, OP3);
  not not_313 (not_313_out, OP2);
  not not_314 (not_314_out, OP1);
  not not_315 (not_315_out, OP0);
  not not_316 (not_316_out, F4);
  not not_317 (not_317_out, F3);
  not not_318 (not_318_out, F1);
  not not_319 (not_319_out, OP5);
  not not_320 (not_320_out, OP4);
  not not_321 (not_321_out, OP3);
  not not_322 (not_322_out, OP2);
  not not_323 (not_323_out, OP1);
  not not_324 (not_324_out, OP0);
  not not_325 (not_325_out, F4);
  not not_326 (not_326_out, F3);
  not not_327 (not_327_out, OP5);
  not not_328 (not_328_out, OP4);
  not not_329 (not_329_out, OP3);
  not not_330 (not_330_out, OP2);
  not not_331 (not_331_out, OP1);
  not not_332 (not_332_out, OP0);
  not not_333 (not_333_out, F4);
  not not_334 (not_334_out, F2);
  not not_335 (not_335_out, F0);
  not not_336 (not_336_out, OP5);
  not not_337 (not_337_out, OP4);
  not not_338 (not_338_out, OP3);
  not not_339 (not_339_out, OP2);
  not not_340 (not_340_out, OP1);
  not not_341 (not_341_out, OP0);
  not not_342 (not_342_out, F4);
  not not_343 (not_343_out, F2);
  not not_344 (not_344_out, OP5);
  not not_345 (not_345_out, OP4);
  not not_346 (not_346_out, OP3);
  not not_347 (not_347_out, OP2);
  not not_348 (not_348_out, OP1);
  not not_349 (not_349_out, OP0);
  not not_350 (not_350_out, F5);
  not not_351 (not_351_out, F4);
  not not_352 (not_352_out, F3);
  not not_353 (not_353_out, OP5);
  not not_354 (not_354_out, OP4);
  not not_355 (not_355_out, OP3);
  not not_356 (not_356_out, OP2);
  not not_357 (not_357_out, OP1);
  not not_358 (not_358_out, OP0);
  not not_359 (not_359_out, F4);
  not not_360 (not_360_out, F3);
  not not_361 (not_361_out, F2);
  not not_362 (not_362_out, OP5);
  not not_363 (not_363_out, OP4);
  not not_364 (not_364_out, OP3);
  not not_365 (not_365_out, OP1);
  not not_366 (not_366_out, OP0);
  not not_367 (not_367_out, OP5);
  not not_368 (not_368_out, OP4);
  not not_369 (not_369_out, OP3);
  not not_370 (not_370_out, OP1);
  not not_371 (not_371_out, OP5);
  not not_372 (not_372_out, OP4);
  not not_373 (not_373_out, OP3);
  not not_374 (not_374_out, OP2);
  not not_375 (not_375_out, OP1);
  not not_376 (not_376_out, OP0);
  not not_377 (not_377_out, F5);
  not not_378 (not_378_out, F4);
  not not_379 (not_379_out, F2);
  not not_380 (not_380_out, F1);
  not not_381 (not_381_out, F0);
  not not_382 (not_382_out, OP5);
  not not_383 (not_383_out, OP4);
  not not_384 (not_384_out, OP3);
  not not_385 (not_385_out, OP2);
  not not_386 (not_386_out, OP1);
  not not_387 (not_387_out, OP0);
  not not_388 (not_388_out, F5);
  not not_389 (not_389_out, F4);
  not not_390 (not_390_out, F2);
  not not_391 (not_391_out, F1);
  not not_392 (not_392_out, F0);
  not not_393 (not_393_out, OP5);
  not not_394 (not_394_out, OP4);
  not not_395 (not_395_out, OP3);
  not not_396 (not_396_out, OP2);
  not not_397 (not_397_out, OP0);
  not not_398 (not_398_out, OP5);
  not not_399 (not_399_out, OP4);
  not not_400 (not_400_out, OP3);
  not not_401 (not_401_out, OP2);
  not not_402 (not_402_out, OP5);
  not not_403 (not_403_out, OP4);
  not not_404 (not_404_out, OP3);
  not not_405 (not_405_out, OP2);
  not not_406 (not_406_out, OP5);
  not not_407 (not_407_out, OP4);
  not not_408 (not_408_out, OP3);
  not not_409 (not_409_out, OP2);
  not not_410 (not_410_out, OP1);
  not not_411 (not_411_out, OP0);
  not not_412 (not_412_out, F5);
  not not_413 (not_413_out, F4);
  not not_414 (not_414_out, F3);
  not not_415 (not_415_out, OP4);
  not not_416 (not_416_out, OP3);
  not not_417 (not_417_out, OP1);
  not not_418 (not_418_out, OP5);
  not not_419 (not_419_out, OP4);
  not not_420 (not_420_out, OP3);
  and and_1 (and_1_out, OP5, not_1_out, not_2_out, not_3_out, OP1, OP0);
  and and_2 (and_2_out, OP5, not_4_out, not_5_out, OP2, not_6_out, OP0);
  and and_3 (MemWrite, OP5, not_7_out, OP3, not_8_out, OP1, OP0);
  and and_4 (and_4_out, not_9_out, not_10_out, OP3, not_11_out, not_12_out, not_13_out);
  and and_5 (and_5_out, not_14_out, not_15_out, OP3, OP2, not_16_out, not_17_out);
  and and_6 (and_6_out, not_18_out, not_19_out, OP3, not_20_out, not_21_out, OP0);
  and and_7 (and_7_out, not_22_out, not_23_out, OP3, not_24_out, OP1, not_25_out);
  and and_8 (and_8_out, not_26_out, not_27_out, OP3, OP2, not_28_out, OP0);
  and and_9 (and_9_out, OP5, not_29_out, not_30_out, not_31_out, OP1, OP0);
  and and_10 (and_10_out, OP5, not_32_out, OP3, not_33_out, OP1, OP0);
  and and_11 (and_11_out, OP5, not_34_out, not_35_out, OP2, not_36_out, OP0);
  and and_12 (and_12_out, not_37_out, not_38_out, not_39_out, not_40_out, not_41_out, not_42_out, not_43_out, not_44_out, not_45_out, not_46_out, not_47_out, not_48_out);
  and and_13 (and_13_out, not_49_out, not_50_out, not_51_out, not_52_out, not_53_out, not_54_out, not_55_out, not_56_out, not_57_out, not_58_out, F1, F0);
  and and_14 (and_14_out, not_59_out, not_60_out, not_61_out, not_62_out, not_63_out, not_64_out, not_65_out, not_66_out, not_67_out, not_68_out, F1, not_69_out);
  and and_15 (and_15_out, not_70_out, not_71_out, not_72_out, not_73_out, not_74_out, not_75_out, F5, not_76_out, not_77_out, not_78_out, not_79_out, not_80_out);
  and and_16 (and_16_out, not_81_out, not_82_out, not_83_out, not_84_out, not_85_out, not_86_out, F5, not_87_out, not_88_out, not_89_out, not_90_out, F0);
  and and_17 (and_17_out, not_91_out, not_92_out, not_93_out, not_94_out, not_95_out, not_96_out, F5, not_97_out, not_98_out, not_99_out, F1, not_100_out);
  and and_18 (and_18_out, not_101_out, not_102_out, not_103_out, not_104_out, not_105_out, not_106_out, F5, not_107_out, not_108_out, F2, not_109_out, not_110_out);
  and and_19 (and_19_out, not_111_out, not_112_out, not_113_out, not_114_out, not_115_out, not_116_out, F5, not_117_out, not_118_out, F2, not_119_out, F0);
  and and_20 (and_20_out, not_120_out, not_121_out, not_122_out, not_123_out, not_124_out, not_125_out, F5, not_126_out, not_127_out, F2, F1, F0);
  and and_21 (and_21_out, not_128_out, not_129_out, not_130_out, not_131_out, not_132_out, not_133_out, F5, not_134_out, F3, not_135_out, F1, not_136_out);
  and and_22 (and_22_out, not_137_out, not_138_out, not_139_out, not_140_out, not_141_out, not_142_out, F5, not_143_out, F3, not_144_out, F1, F0);
  and and_23 (and_23_out, not_145_out, not_146_out, not_147_out, not_148_out, OP1, OP0);
  and and_24 (and_24_out, not_149_out, not_150_out, OP3, not_151_out, not_152_out, not_153_out);
  and and_25 (and_25_out, not_154_out, not_155_out, OP3, OP2, not_156_out, not_157_out);
  and and_26 (and_26_out, not_158_out, not_159_out, OP3, not_160_out, not_161_out, OP0);
  and and_27 (and_27_out, not_162_out, not_163_out, OP3, not_164_out, OP1, not_165_out);
  and and_28 (and_28_out, not_166_out, not_167_out, OP3, OP2, not_168_out, OP0);
  and and_29 (and_29_out, OP5, not_169_out, not_170_out, not_171_out, OP1, OP0);
  and and_30 (and_30_out, not_172_out, not_173_out, not_174_out, not_175_out, not_176_out, not_177_out, not_178_out, not_179_out, not_180_out, F2, F1, F0);
  and and_31 (and_31_out, not_181_out, not_182_out, not_183_out, not_184_out, not_185_out, not_186_out, F5, not_187_out, not_188_out, not_189_out, F1, F0);
  and and_32 (and_32_out, OP5, not_190_out, not_191_out, OP2, not_192_out, OP0);
  and and_33 (SysCALL, not_193_out, not_194_out, not_195_out, not_196_out, not_197_out, not_198_out, not_199_out, not_200_out, F3, F2, not_201_out, not_202_out);
  and and_34 (and_34_out, not_203_out, not_204_out, not_205_out, OP2, not_206_out, not_207_out);
  and and_35 (and_35_out, not_208_out, not_209_out, not_210_out, OP2, not_211_out, OP0);
  and and_36 (and_36_out, not_212_out, not_213_out, OP3, not_214_out, not_215_out, not_216_out);
  and and_37 (and_37_out, not_217_out, not_218_out, OP3, not_219_out, not_220_out, OP0);
  and and_38 (and_38_out, not_221_out, not_222_out, OP3, not_223_out, OP1, not_224_out);
  and and_39 (and_39_out, OP5, not_225_out, not_226_out, not_227_out, OP1, OP0);
  and and_40 (and_40_out, OP5, not_228_out, OP3, not_229_out, OP1, OP0);
  and and_41 (and_41_out, not_230_out, not_231_out, not_232_out, OP2, OP1, OP0);
  and and_42 (and_42_out, OP5, not_233_out, not_234_out, OP2, not_235_out, OP0);
  and and_43 (and_43_out, not_236_out, not_237_out, not_238_out, not_239_out, not_240_out, not_241_out, not_242_out, not_243_out, not_244_out, not_245_out, not_246_out, not_247_out);
  and and_44 (and_44_out, not_248_out, not_249_out, not_250_out, not_251_out, not_252_out, not_253_out, not_254_out, not_255_out, not_256_out, not_257_out, F1, F0);
  and and_45 (and_45_out, not_258_out, not_259_out, not_260_out, not_261_out, not_262_out, not_263_out, not_264_out, not_265_out, not_266_out, not_267_out, F1, not_268_out);
  and and_46 (and_46_out, not_269_out, not_270_out, not_271_out, not_272_out, not_273_out, not_274_out, F5, not_275_out, not_276_out, not_277_out, not_278_out, not_279_out);
  and and_47 (and_47_out, not_280_out, not_281_out, not_282_out, not_283_out, not_284_out, not_285_out, F5, not_286_out, not_287_out, not_288_out, not_289_out, F0);
  and and_48 (and_48_out, not_290_out, not_291_out, not_292_out, not_293_out, not_294_out, not_295_out, F5, not_296_out, not_297_out, not_298_out, F1, not_299_out);
  and and_49 (and_49_out, not_300_out, not_301_out, not_302_out, not_303_out, not_304_out, not_305_out, F5, not_306_out, not_307_out, F2, not_308_out, not_309_out);
  and and_50 (and_50_out, not_310_out, not_311_out, not_312_out, not_313_out, not_314_out, not_315_out, F5, not_316_out, not_317_out, F2, not_318_out, F0);
  and and_51 (and_51_out, not_319_out, not_320_out, not_321_out, not_322_out, not_323_out, not_324_out, F5, not_325_out, not_326_out, F2, F1, F0);
  and and_52 (and_52_out, not_327_out, not_328_out, not_329_out, not_330_out, not_331_out, not_332_out, F5, not_333_out, F3, not_334_out, F1, not_335_out);
  and and_53 (and_53_out, not_336_out, not_337_out, not_338_out, not_339_out, not_340_out, not_341_out, F5, not_342_out, F3, not_343_out, F1, F0);
  and and_54 (and_54_out, not_344_out, not_345_out, not_346_out, not_347_out, not_348_out, not_349_out, not_350_out, not_351_out, not_352_out, F2, F1, F0);
  and and_55 (and_55_out, not_353_out, not_354_out, not_355_out, not_356_out, not_357_out, not_358_out, F5, not_359_out, not_360_out, not_361_out, F1, F0);
  and and_56 (BEQ, not_362_out, not_363_out, not_364_out, OP2, not_365_out, not_366_out);
  and and_57 (BNE, not_367_out, not_368_out, not_369_out, OP2, not_370_out, OP0);
  and and_58 (JR, not_371_out, not_372_out, not_373_out, not_374_out, not_375_out, not_376_out, not_377_out, not_378_out, F3, not_379_out, not_380_out, not_381_out);
  and and_59 (and_59_out, not_382_out, not_383_out, not_384_out, not_385_out, not_386_out, not_387_out, not_388_out, not_389_out, F3, not_390_out, not_391_out, not_392_out);
  and and_60 (and_60_out, not_393_out, not_394_out, not_395_out, not_396_out, OP1, not_397_out);
  and and_61 (and_61_out, not_398_out, not_399_out, not_400_out, not_401_out, OP1, OP0);
  and and_62 (JAL, not_402_out, not_403_out, not_404_out, not_405_out, OP1, OP0);
  and and_63 (SRAV, not_406_out, not_407_out, not_408_out, not_409_out, not_410_out, not_411_out, not_412_out, not_413_out, not_414_out, F2, F1, F0);
  and and_64 (LHU, OP5, not_415_out, not_416_out, OP2, not_417_out, OP0);
  and and_65 (BGTZ, not_418_out, not_419_out, not_420_out, OP2, OP1, OP0);
  or or_1 (MemToReg, and_1_out, and_2_out);
  or or_2 (ALU_SRC, and_4_out, and_5_out, and_6_out, and_7_out, and_8_out, and_9_out, and_10_out, and_11_out);
  or or_3 (SignedExt, and_34_out, and_35_out, and_36_out, and_37_out, and_38_out, and_39_out, and_40_out, and_41_out, and_42_out);
  or or_4 (JMP, and_59_out, and_60_out, and_61_out);
  or or_5 (RegWrite, and_12_out, and_13_out, and_14_out, and_15_out, and_16_out, and_17_out, and_18_out, and_19_out, and_20_out, and_21_out, and_22_out, and_23_out, and_24_out, and_25_out, and_26_out, and_27_out, and_28_out, and_29_out, and_30_out, and_31_out, and_32_out);
  or or_6 (RegDst, and_43_out, and_44_out, and_45_out, and_46_out, and_47_out, and_48_out, and_49_out, and_50_out, and_51_out, and_52_out, and_53_out, and_54_out, and_55_out);
endmodule

// ALU
module MIPS_ALU (
  input  [4:0] shamt,
  input  [31:0] X,
  input  [31:0] Y,
  input  [3:0] AluOP,
  output Equal,
  output [31:0] Result,
  output [31:0] Result_2
);

  wire [0:0] comparator_1_lt, comparator_2_lt;
  wire [31:0] adder_1_out, AND_out, divider_1_out, divider_1_rem, multiplier_1_cout, multiplier_1_out,
       NOR_out, OR_out, shifter_1_out, shifter_2_out, shifter_3_out, subtractor_1_out, XOR_out;

  assign AND_out = X & Y;  // AND_Gate AND, 32 bits wide
  assign OR_out = X | Y;  // OR_Gate OR, 32 bits wide
  Shifter #(.width(32)) shifter_1 (.in(Y), .\dist (shamt), .out(shifter_1_out));
  Shifter #(.width(32), .shift("ar")) shifter_2 (.in(Y), .\dist (shamt), .out(shifter_2_out));
  Shifter #(.width(32), .shift("lr")) shifter_3 (.in(Y), .\dist (shamt), .out(shifter_3_out));
  Multiplier #(.width(32)) multiplier_1 (.a(X), .b(Y), .out(multiplier_1_out), .cout(multiplier_1_cout));  // open: cin
  Divider #(.width(32)) divider_1 (.a(X), .b(Y), .out(divider_1_out), .rem(divider_1_rem));  // open: upper
  Adder #(.width(32)) adder_1 (.a(X), .b(Y), .out(adder_1_out));  // open: cin, cout
  Subtractor #(.width(32)) subtractor_1 (.a(X), .b(Y), .out(subtractor_1_out));  // open: bin, bout
  assign XOR_out = X ^ Y;  // XOR_Gate XOR, 32 bits wide
  assign NOR_out = ~(X | Y);  // NOR_Gate NOR, 32 bits wide
  Comparator #(.width(32)) comparator_1 (.a(X), .b(Y), .eq(Equal), .lt(comparator_1_lt[0]));  // open: gt
  Comparator #(.width(32), .mode("unsigned")) comparator_2 (.a(X), .b(Y), .lt(comparator_2_lt[0]));  // open: gt, eq
  Multiplexer #(.select(4), .width(32), .enable("false")) multiplexer_1 (
    .in0(shifter_1_out), .in1(shifter_2_out), .in2(shifter_3_out), .in3(multiplier_1_out),
    .in4(divider_1_out), .in5(adder_1_out), .in6(subtractor_1_out), .in7(AND_out), .in8(OR_out),
    .in9(XOR_out), .in10(NOR_out), .in11({{31{1'b0}}, comparator_1_lt[0]}),
    .in12({{31{1'b0}}, comparator_2_lt[0]}), .in13({32{1'b0}}), .in14({32{1'b0}}), .in15({32{1'b0}}),
    .out(Result), .sel(AluOP));
  Multiplexer #(.select(4), .width(32), .enable("false")) multiplexer_2 (
    .in0({32{1'b0}}), .in1({32{1'b0}}), .in2({32{1'b0}}), .in3(multiplier_1_cout), .in4(divider_1_rem),
    .in5({32{1'b0}}), .in6({32{1'b0}}), .in7({32{1'b0}}), .in8({32{1'b0}}), .in9({32{1'b0}}),
    .in10({32{1'b0}}), .in11({32{1'b0}}), .in12({32{1'b0}}), .in13({32{1'b0}}), .in14({32{1'b0}}),
    .in15({32{1'b0}}), .out(Result_2), .sel(AluOP));

  // Other names for the same wires on the sheet: Result2[31:0] = Result_2; S[3:0] = AluOP

  // Notes on the sheet:
  //   不要改变此引脚区域内容，也不要改变ALU封装形式
  //   输入引脚
  //   输出引脚
endmodule

module MIPS_Regifile (
  input  [31:0] Din,
  input  Clk,
  input  WE,
  input  [4:0] R1_num,
  input  [4:0] W_num,
  input  [4:0] R2_num,
  output [31:0] R1,
  output [31:0] R2
);

  // RegisterFile registerfile_1: pin names not known; wires that end beside it: Din, Clk, WE, W_num, R1_num, R2_num, R1, R2
endmodule

module \理想流水线  (
);

  wire and_1_out, and_2_out, and_3_out, and_4_out, and_5_out, CLK, equal5, ex_mem_1_equal_2, Go, IR1, IR2,
       IR3, mips_alu_1_equal, not_1_out, or_1_out, regdst5, regwrite5, RST, SignedExt, stop, syscall3,
       syscall5, W1, W2, W3;
  wire [3:0] \硬布线控制器_1_alu_op ;
  wire [4:0] id_ex_1_shamt_2, multiplexer_3_out, multiplexer_4_out, multiplexer_5_out, rd5, rt5;
  wire [15:0] \LoadUse次数 , \总周期数 , \插入气泡数 , \无条件分支数 , \条件分支成功数 ;
  wire [18:0] ex_mem_1_control_2, id_ex_1_control_2, mem_wb_1_control_2, \硬布线控制器_1_jmp ;
  wire [31:0] a0, adder_1_out, adder_2_out, bit_extender_1_out, bit_extender_2_out, ex_mem_1_alu_2,
       ex_mem_1_instruction_2, ex_mem_1_r2_2, EX_PC, id_ex_1_imm_2, id_ex_1_instruction_2, id_ex_1_r2_2,
       id_ex_1_signimm_2, ID_PC, if_id_1_instruction_2, IF_PC, LedData, MEM_PC, mem_wb_1_alu_2,
       mem_wb_1_instruction_2, mem_wb_1_md_2, mips_alu_1_result, mips_regifile_1_r1, mips_regifile_1_r2,
       multiplexer_1_out, multiplexer_6_out, multiplexer_7_out, multiplexer_8_out, multiplexer_9_out,
       ram_1_data, rom_1_data, shifter_1_out, WB_PC;

  Button \u_总复位  (.out(RST));
  Button _1 (.out(IR1));
  Button _2 (.out(IR2));
  Button _3 (.out(IR3));
  Button \u_继续运行  (.out(Go));
  LED led_1 (.in(W1));
  LED led_2 (.in(W2));
  LED led_3 (.in(W3));
  Multiplexer #(.width(32), .enable("false")) multiplexer_1 (
    .in0(adder_1_out), .in1(adder_2_out), .out(multiplexer_1_out), .sel(or_1_out));
  Hex_Digit_Display hex_digit_display_1 (.value(LedData[31:28]));  // open: dp
  Register #(.width(32)) PC (.D(multiplexer_1_out), .en(stop), .Q(IF_PC), .clk(CLK), .clr(RST));
  Hex_Digit_Display hex_digit_display_2 (.value(LedData[27:24]));  // open: dp
  Hex_Digit_Display hex_digit_display_3 (.value(LedData[23:20]));  // open: dp
  Adder #(.width(32)) adder_1 (.a(IF_PC), .b(32'h4), .out(adder_1_out));  // open: cin, cout
  and and_1 (and_1_out, syscall5, equal5);
  Hex_Digit_Display hex_digit_display_4 (.value(LedData[19:16]));  // open: dp
  Hex_Digit_Display hex_digit_display_5 (.value(LedData[15:12]));  // open: dp
  ROM #(.addrWidth(10), .dataWidth(32)) rom_1 (.addr(IF_PC[11:2]), .data(rom_1_data));  // open: sel
  Register #(.width(32)) register_1 (.D(a0), .en(and_1_out), .Q(LedData), .clk(CLK), .clr(RST));
  Hex_Digit_Display hex_digit_display_6 (.value(LedData[11:8]));  // open: dp
  Hex_Digit_Display hex_digit_display_7 (.value(LedData[7:4]));  // open: dp
  Clock clock_1 (.out(CLK));
  IF_ID if_id_1 (
    .instruction(rom_1_data), .pc4(adder_1_out), .instruction_2(if_id_1_instruction_2), .pc4_2(ID_PC),
    .rst(RST), .clk(CLK), .stop(stop));  // open: hit, hit_2, jump_att, jump_att_2, hit_pos, hit_pos_2, pc, pc_2
  Hex_Digit_Display hex_digit_display_8 (.value(LedData[3:0]));  // open: dp
  Multiplexer #(.enable("false")) multiplexer_2 (.in0(1'b1), .in1(Go), .out(stop), .sel(and_2_out));
  and and_2 (and_2_out, syscall5, ~equal5);  // AND_Gate
  // Probe on \总周期数 
  // Probe on \无条件分支数 
  // Probe on \条件分支成功数 
  // Probe on \插入气泡数 
  // Probe on \LoadUse次数 
  \硬布线控制器  \u_硬布线控制器_1  (
    .Func(if_id_1_instruction_2[5:0]), .OP(if_id_1_instruction_2[31:26]), .ALU_OP(\硬布线控制器_1_alu_op ),
    .MemToReg(\硬布线控制器_1_jmp [5]), .MemWrite(\硬布线控制器_1_jmp [6]), .ALU_SRC(\硬布线控制器_1_jmp [11]),
    .RegWrite(\硬布线控制器_1_jmp [12]), .SysCALL(\硬布线控制器_1_jmp [16]), .SignedExt(SignedExt),
    .RegDst(\硬布线控制器_1_jmp [14]), .JR(\硬布线控制器_1_jmp [1]), .JMP(\硬布线控制器_1_jmp [0]), .Beq(\硬布线控制器_1_jmp [3]),
    .JAL(\硬布线控制器_1_jmp [13]), .Bne(\硬布线控制器_1_jmp [4]), .SRAV(\硬布线控制器_1_jmp [15]), .LHU(\硬布线控制器_1_jmp [18]),
    .BGTZ(\硬布线控制器_1_jmp [17]));
  Multiplexer #(.width(5), .enable("false")) multiplexer_3 (
    .in0(if_id_1_instruction_2[25:21]), .in1(5'b00100), .out(multiplexer_3_out), .sel(\硬布线控制器_1_jmp [16]));
  Multiplexer #(.width(5), .enable("false")) multiplexer_4 (
    .in0(if_id_1_instruction_2[20:16]), .in1(5'b00010), .out(multiplexer_4_out), .sel(\硬布线控制器_1_jmp [16]));
  Counter #(.width(16), .max('hffff)) counter_1 (
    .count(stop), .Q(\总周期数 ), .clk(CLK), .clr(RST));  // open: load, D, carry
  // Probe on IF_PC[11:0]
  Multiplexer #(.width(5), .enable("false")) multiplexer_5 (
    .in0(rt5), .in1(rd5), .out(multiplexer_5_out), .sel(regdst5));
  assign bit_extender_1_out = {{16{1'b0}}, if_id_1_instruction_2[15:0]};  // Bit_Extender bit_extender_1
  assign bit_extender_2_out = {{16{if_id_1_instruction_2[15]}}, if_id_1_instruction_2[15:0]};  // Bit_Extender bit_extender_2
  // Probe on ID_PC[11:0]
  Multiplexer #(.width(32), .enable("false")) multiplexer_6 (
    .in0(bit_extender_1_out), .in1(bit_extender_2_out), .out(multiplexer_6_out), .sel(SignedExt));
  // Probe on EX_PC[11:0]
  // Probe on MEM_PC[11:0]
  MIPS_Regifile mips_regifile_1 (
    .Din(multiplexer_9_out), .Clk(CLK), .R1(mips_regifile_1_r1), .R2(mips_regifile_1_r2), .WE(regwrite5),
    .W_num(multiplexer_5_out), .R1_num(multiplexer_3_out), .R2_num(multiplexer_4_out));
  // Probe on WB_PC[11:0]
  ID_EX id_ex_1 (
    .control({\硬布线控制器_1_jmp [18:11], \硬布线控制器_1_alu_op , \硬布线控制器_1_jmp [6:3], SignedExt, \硬布线控制器_1_jmp [1:0]}),
    .instruction(if_id_1_instruction_2), .pc4(ID_PC), .R1(mips_regifile_1_r1), .R2(mips_regifile_1_r2),
    .imm(multiplexer_6_out), .control_2({id_ex_1_control_2[18:17], syscall3, id_ex_1_control_2[15:0]}),
    .instruction_2(id_ex_1_instruction_2), .pc4_2(EX_PC), .R1_2(a0), .R2_2(id_ex_1_r2_2),
    .imm_2(id_ex_1_imm_2), .rst(RST), .stop(stop), .clk(CLK), .shamt(if_id_1_instruction_2[10:6]),
    .shamt_2(id_ex_1_shamt_2), .signimm(bit_extender_2_out), .signimm_2(id_ex_1_signimm_2));  // open: hit, hit_2, jump_att, jump_att_2, hit_pos, hit_pos_2, pc, pc_2
  Multiplexer #(.width(32), .enable("false")) multiplexer_7 (
    .in0(a0), .in1(32'h22), .out(multiplexer_7_out), .sel(syscall3));
  Multiplexer #(.width(32), .enable("false")) multiplexer_8 (
    .in0(id_ex_1_r2_2), .in1(id_ex_1_imm_2), .out(multiplexer_8_out), .sel(id_ex_1_control_2[11]));
  Shifter #(.width(32)) shifter_1 (.in(id_ex_1_signimm_2), .\dist (5'b00010), .out(shifter_1_out));
  MIPS_ALU mips_alu_1 (
    .X(multiplexer_7_out), .Y(multiplexer_8_out), .AluOP(id_ex_1_control_2[10:7]), .Equal(mips_alu_1_equal),
    .Result(mips_alu_1_result), .shamt(id_ex_1_shamt_2));  // open: Result_2
  Adder #(.width(32)) adder_2 (.a(EX_PC), .b(shifter_1_out), .out(adder_2_out));  // open: cin, cout
  and and_3 (and_3_out, id_ex_1_control_2[3], mips_alu_1_equal);
  and and_4 (and_4_out, id_ex_1_control_2[4], ~mips_alu_1_equal);  // AND_Gate
  or or_1 (or_1_out, and_3_out, and_4_out, and_5_out);
  and and_5 (and_5_out, id_ex_1_control_2[17], ~mips_alu_1_equal, ~mips_alu_1_result[0]);  // AND_Gate
  EX_MEM ex_mem_1 (
    .control({id_ex_1_control_2[18:17], syscall3, id_ex_1_control_2[15:0]}),
    .instruction(id_ex_1_instruction_2), .pc4(EX_PC), .R2(id_ex_1_r2_2), .alu(mips_alu_1_result),
    .control_2(ex_mem_1_control_2), .instruction_2(ex_mem_1_instruction_2), .pc4_2(MEM_PC),
    .R2_2(ex_mem_1_r2_2), .alu_2(ex_mem_1_alu_2), .rst(RST), .stop(stop), .clk(CLK),
    .equal(mips_alu_1_equal), .equal_2(ex_mem_1_equal_2));  // open: R1, R1_2
  not not_1 (not_1_out, ex_mem_1_control_2[6]);
  RAM #(.addrWidth(10), .dataWidth(32), .bus("separate")) ram_1 (
    .addr(ex_mem_1_alu_2[11:2]), .din(ex_mem_1_r2_2), .data(ram_1_data), .str(ex_mem_1_control_2[6]),
    .clk(CLK), .ld(not_1_out), .clr(RST));  // open: sel
  MEM_WB mem_wb_1 (
    .control(ex_mem_1_control_2), .instruction(ex_mem_1_instruction_2), .pc4(MEM_PC), .md(ram_1_data),
    .alu(ex_mem_1_alu_2),
    .control_2({mem_wb_1_control_2[18:17], syscall5, mem_wb_1_control_2[15], regdst5, mem_wb_1_control_2[13], regwrite5, mem_wb_1_control_2[11:0]}),
    .instruction_2({mem_wb_1_instruction_2[31:21], rt5, rd5, mem_wb_1_instruction_2[10:0]}), .pc4_2(WB_PC),
    .md_2(mem_wb_1_md_2), .alu_2(mem_wb_1_alu_2), .rst(RST), .stop(stop), .clk(CLK),
    .equal(ex_mem_1_equal_2), .equal_2(equal5));  // open: R1, R1_2
  Multiplexer #(.width(32), .enable("false")) multiplexer_9 (
    .in0(mem_wb_1_alu_2), .in1(mem_wb_1_md_2), .out(multiplexer_9_out), .sel(mem_wb_1_control_2[5]));

  // Notes on the sheet:
  //   中断源
  //   中断等待指示
  //   指令存储器
  //   数码管输出
  //   contents of rom_1 (hex, n*v repeats v):
  //   20100000 20110001 20120002 20130003 36100000 36310001 36520002 36730003 ae100000 ae110004 ae120008
  //   ae13000c 2002000a 0 0 0 c
  //   指令字
  //   OP
  //   Func
  //   rs
  //   rt
  //   rd
  //   shamt
  //   imm
  //   Beq
  //   JMP
  //   JR
  //   Bne
  //   OP
  //   JAL
  //   Func
  //   MemToReg
  //   MemWrite
  //   AluOP
  //   AluSrcB
  //   RegWrite
  //   RegDst
  //   流水调试日志用
  //   rt
  //   rd
endmodule

// 源寄存器使用情况
module \源寄存器使用情况  (
  input  OP0,
  input  OP1,
  input  OP2,
  input  OP3,
  input  OP4,
  input  OP5,
  input  F0,
  input  F1,
  input  F2,
  input  F3,
  input  F4,
  input  F5,
  output R1_Used,
  output R2_Used
);

  wire and_1_out, and_2_out, and_3_out, and_4_out, and_5_out, and_6_out, and_7_out, and_8_out, and_9_out,
       and_10_out, and_11_out, and_12_out, and_13_out, and_14_out, and_15_out, and_16_out, and_17_out,
       and_18_out, and_19_out, and_20_out, and_21_out, and_22_out, and_23_out, and_24_out, and_25_out,
       and_26_out, and_27_out, and_28_out, and_29_out, and_30_out, and_31_out, and_32_out, and_33_out,
       and_34_out, and_35_out, and_36_out, and_37_out, and_38_out, and_39_out, and_40_out, and_41_out,
       and_42_out, and_43_out, and_44_out, not_1_out, not_2_out, not_3_out, not_4_out, not_5_out, not_6_out,
       not_7_out, not_8_out, not_9_out, not_10_out, not_11_out, not_12_out, not_13_out, not_14_out,
       not_15_out, not_16_out, not_17_out, not_18_out, not_19_out, not_20_out, not_21_out, not_22_out,
       not_23_out, not_24_out, not_25_out, not_26_out, not_27_out, not_28_out, not_29_out, not_30_out,
       not_31_out, not_32_out, not_33_out, not_34_out, not_35_out, not_36_out, not_37_out, not_38_out,
       not_39_out, not_40_out, not_41_out, not_42_out, not_43_out, not_44_out, not_45_out, not_46_out,
       not_47_out, not_48_out, not_49_out, not_50_out, not_51_out, not_52_out, not_53_out, not_54_out,
       not_55_out, not_56_out, not_57_out, not_58_out, not_59_out, not_60_out, not_61_out, not_62_out,
       not_63_out, not_64_out, not_65_out, not_66_out, not_67_out, not_68_out, not_69_out, not_70_out,
       not_71_out, not_72_out, not_73_out, not_74_out, not_75_out, not_76_out, not_77_out, not_78_out,
       not_79_out, not_80_out, not_81_out, not_82_out, not_83_out, not_84_out, not_85_out, not_86_out,
       not_87_out, not_88_out, not_89_out, not_90_out, not_91_out, not_92_out, not_93_out, not_94_out,
       not_95_out, not_96_out, not_97_out, not_98_out, not_99_out, not_100_out, not_101_out, not_102_out,
       not_103_out, not_104_out, not_105_out, not_106_out, not_107_out, not_108_out, not_109_out,
       not_110_out, not_111_out, not_112_out, not_113_out, not_114_out, not_115_out, not_116_out,
       not_117_out, not_118_out, not_119_out, not_120_out, not_121_out, not_122_out, not_123_out,
       not_124_out, not_125_out, not_126_out, not_127_out, not_128_out, not_129_out, not_130_out,
       not_131_out, not_132_out, not_133_out, not_134_out, not_135_out, not_136_out, not_137_out,
       not_138_out, not_139_out, not_140_out, not_141_out, not_142_out, not_143_out, not_144_out,
       not_145_out, not_146_out, not_147_out, not_148_out, not_149_out, not_150_out, not_151_out,
       not_152_out, not_153_out, not_154_out, not_155_out, not_156_out, not_157_out, not_158_out,
       not_159_out, not_160_out, not_161_out, not_162_out, not_163_out, not_164_out, not_165_out,
       not_166_out, not_167_out, not_168_out, not_169_out, not_170_out, not_171_out, not_172_out,
       not_173_out, not_174_out, not_175_out, not_176_out, not_177_out, not_178_out, not_179_out,
       not_180_out, not_181_out, not_182_out, not_183_out, not_184_out, not_185_out, not_186_out,
       not_187_out, not_188_out, not_189_out, not_190_out, not_191_out, not_192_out, not_193_out,
       not_194_out, not_195_out, not_196_out, not_197_out, not_198_out, not_199_out, not_200_out,
       not_201_out, not_202_out, not_203_out, not_204_out, not_205_out, not_206_out, not_207_out,
       not_208_out, not_209_out, not_210_out, not_211_out, not_212_out, not_213_out, not_214_out,
       not_215_out, not_216_out, not_217_out, not_218_out, not_219_out, not_220_out, not_221_out,
       not_222_out, not_223_out, not_224_out, not_225_out, not_226_out, not_227_out, not_228_out,
       not_229_out, not_230_out, not_231_out, not_232_out, not_233_out, not_234_out, not_235_out,
       not_236_out, not_237_out, not_238_out, not_239_out, not_240_out, not_241_out, not_242_out,
       not_243_out, not_244_out, not_245_out, not_246_out, not_247_out, not_248_out, not_249_out,
       not_250_out, not_251_out, not_252_out, not_253_out, not_254_out, not_255_out, not_256_out,
       not_257_out, not_258_out, not_259_out, not_260_out, not_261_out, not_262_out, not_263_out,
       not_264_out, not_265_out, not_266_out, not_267_out, not_268_out, not_269_out, not_270_out,
       not_271_out, not_272_out, not_273_out, not_274_out, not_275_out, not_276_out, not_277_out,
       not_278_out, not_279_out, not_280_out, not_281_out, not_282_out, not_283_out, not_284_out,
       not_285_out, not_286_out, not_287_out, not_288_out, not_289_out, not_290_out, not_291_out,
       not_292_out, not_293_out, not_294_out, not_295_out, not_296_out, not_297_out, not_298_out,
       not_299_out, not_300_out, not_301_out, not_302_out, not_303_out, not_304_out, not_305_out,
       not_306_out, not_307_out, not_308_out, not_309_out, not_310_out, not_311_out, not_312_out,
       not_313_out, not_314_out, not_315_out, not_316_out, not_317_out, not_318_out, not_319_out,
       not_320_out, not_321_out, not_322_out, not_323_out, not_324_out, not_325_out, not_326_out,
       not_327_out, not_328_out, not_329_out, not_330_out, not_331_out, not_332_out, not_333_out,
       not_334_out, not_335_out, not_336_out, not_337_out;

  not not_1 (not_1_out, OP5);
  not not_2 (not_2_out, OP4);
  not not_3 (not_3_out, OP3);
  not not_4 (not_4_out, OP2);
  not not_5 (not_5_out, OP1);
  not not_6 (not_6_out, OP0);
  not not_7 (not_7_out, F5);
  not not_8 (not_8_out, F4);
  not not_9 (not_9_out, F3);
  not not_10 (not_10_out, F2);
  not not_11 (not_11_out, F1);
  not not_12 (not_12_out, F0);
  not not_13 (not_13_out, OP5);
  not not_14 (not_14_out, OP4);
  not not_15 (not_15_out, OP3);
  not not_16 (not_16_out, OP2);
  not not_17 (not_17_out, OP1);
  not not_18 (not_18_out, OP0);
  not not_19 (not_19_out, F5);
  not not_20 (not_20_out, F4);
  not not_21 (not_21_out, F3);
  not not_22 (not_22_out, F2);
  not not_23 (not_23_out, OP5);
  not not_24 (not_24_out, OP4);
  not not_25 (not_25_out, OP3);
  not not_26 (not_26_out, OP2);
  not not_27 (not_27_out, OP1);
  not not_28 (not_28_out, OP0);
  not not_29 (not_29_out, F5);
  not not_30 (not_30_out, F4);
  not not_31 (not_31_out, F3);
  not not_32 (not_32_out, F2);
  not not_33 (not_33_out, F0);
  not not_34 (not_34_out, OP5);
  not not_35 (not_35_out, OP4);
  not not_36 (not_36_out, OP3);
  not not_37 (not_37_out, OP2);
  not not_38 (not_38_out, OP1);
  not not_39 (not_39_out, OP0);
  not not_40 (not_40_out, F4);
  not not_41 (not_41_out, F3);
  not not_42 (not_42_out, F2);
  not not_43 (not_43_out, F1);
  not not_44 (not_44_out, F0);
  not not_45 (not_45_out, OP5);
  not not_46 (not_46_out, OP4);
  not not_47 (not_47_out, OP3);
  not not_48 (not_48_out, OP2);
  not not_49 (not_49_out, OP1);
  not not_50 (not_50_out, OP0);
  not not_51 (not_51_out, F4);
  not not_52 (not_52_out, F3);
  not not_53 (not_53_out, F2);
  not not_54 (not_54_out, F1);
  not not_55 (not_55_out, OP5);
  not not_56 (not_56_out, OP4);
  not not_57 (not_57_out, OP3);
  not not_58 (not_58_out, OP2);
  not not_59 (not_59_out, OP1);
  not not_60 (not_60_out, OP0);
  not not_61 (not_61_out, F4);
  not not_62 (not_62_out, F3);
  not not_63 (not_63_out, F2);
  not not_64 (not_64_out, F0);
  not not_65 (not_65_out, OP5);
  not not_66 (not_66_out, OP4);
  not not_67 (not_67_out, OP3);
  not not_68 (not_68_out, OP2);
  not not_69 (not_69_out, OP1);
  not not_70 (not_70_out, OP0);
  not not_71 (not_71_out, F4);
  not not_72 (not_72_out, F3);
  not not_73 (not_73_out, F1);
  not not_74 (not_74_out, F0);
  not not_75 (not_75_out, OP5);
  not not_76 (not_76_out, OP4);
  not not_77 (not_77_out, OP3);
  not not_78 (not_78_out, OP2);
  not not_79 (not_79_out, OP1);
  not not_80 (not_80_out, OP0);
  not not_81 (not_81_out, F4);
  not not_82 (not_82_out, F3);
  not not_83 (not_83_out, F1);
  not not_84 (not_84_out, OP5);
  not not_85 (not_85_out, OP4);
  not not_86 (not_86_out, OP3);
  not not_87 (not_87_out, OP2);
  not not_88 (not_88_out, OP1);
  not not_89 (not_89_out, OP0);
  not not_90 (not_90_out, F4);
  not not_91 (not_91_out, F3);
  not not_92 (not_92_out, OP5);
  not not_93 (not_93_out, OP4);
  not not_94 (not_94_out, OP3);
  not not_95 (not_95_out, OP2);
  not not_96 (not_96_out, OP1);
  not not_97 (not_97_out, OP0);
  not not_98 (not_98_out, F4);
  not not_99 (not_99_out, F2);
  not not_100 (not_100_out, F0);
  not not_101 (not_101_out, OP5);
  not not_102 (not_102_out, OP4);
  not not_103 (not_103_out, OP3);
  not not_104 (not_104_out, OP2);
  not not_105 (not_105_out, OP1);
  not not_106 (not_106_out, OP0);
  not not_107 (not_107_out, F4);
  not not_108 (not_108_out, F2);
  not not_109 (not_109_out, OP5);
  not not_110 (not_110_out, OP4);
  not not_111 (not_111_out, OP3);
  not not_112 (not_112_out, OP2);
  not not_113 (not_113_out, OP1);
  not not_114 (not_114_out, OP0);
  not not_115 (not_115_out, F5);
  not not_116 (not_116_out, F4);
  not not_117 (not_117_out, F2);
  not not_118 (not_118_out, F1);
  not not_119 (not_119_out, F0);
  not not_120 (not_120_out, OP5);
  not not_121 (not_121_out, OP4);
  not not_122 (not_122_out, OP3);
  not not_123 (not_123_out, OP2);
  not not_124 (not_124_out, OP1);
  not not_125 (not_125_out, OP0);
  not not_126 (not_126_out, F5);
  not not_127 (not_127_out, F4);
  not not_128 (not_128_out, F1);
  not not_129 (not_129_out, F0);
  not not_130 (not_130_out, OP5);
  not not_131 (not_131_out, OP4);
  not not_132 (not_132_out, OP3);
  not not_133 (not_133_out, OP1);
  not not_134 (not_134_out, OP0);
  not not_135 (not_135_out, OP5);
  not not_136 (not_136_out, OP4);
  not not_137 (not_137_out, OP3);
  not not_138 (not_138_out, OP1);
  not not_139 (not_139_out, OP5);
  not not_140 (not_140_out, OP4);
  not not_141 (not_141_out, OP2);
  not not_142 (not_142_out, OP1);
  not not_143 (not_143_out, OP0);
  not not_144 (not_144_out, OP5);
  not not_145 (not_145_out, OP4);
  not not_146 (not_146_out, OP1);
  not not_147 (not_147_out, OP0);
  not not_148 (not_148_out, OP5);
  not not_149 (not_149_out, OP4);
  not not_150 (not_150_out, OP2);
  not not_151 (not_151_out, OP1);
  not not_152 (not_152_out, OP5);
  not not_153 (not_153_out, OP4);
  not not_154 (not_154_out, OP2);
  not not_155 (not_155_out, OP0);
  not not_156 (not_156_out, OP5);
  not not_157 (not_157_out, OP4);
  not not_158 (not_158_out, OP1);
  not not_159 (not_159_out, OP4);
  not not_160 (not_160_out, OP3);
  not not_161 (not_161_out, OP2);
  not not_162 (not_162_out, OP4);
  not not_163 (not_163_out, OP2);
  not not_164 (not_164_out, OP5);
  not not_165 (not_165_out, OP4);
  not not_166 (not_166_out, OP3);
  not not_167 (not_167_out, OP2);
  not not_168 (not_168_out, OP1);
  not not_169 (not_169_out, OP0);
  not not_170 (not_170_out, F5);
  not not_171 (not_171_out, F4);
  not not_172 (not_172_out, F3);
  not not_173 (not_173_out, OP5);
  not not_174 (not_174_out, OP4);
  not not_175 (not_175_out, OP3);
  not not_176 (not_176_out, OP2);
  not not_177 (not_177_out, OP1);
  not not_178 (not_178_out, OP0);
  not not_179 (not_179_out, F4);
  not not_180 (not_180_out, F3);
  not not_181 (not_181_out, F2);
  not not_182 (not_182_out, OP4);
  not not_183 (not_183_out, OP3);
  not not_184 (not_184_out, OP1);
  not not_185 (not_185_out, OP5);
  not not_186 (not_186_out, OP4);
  not not_187 (not_187_out, OP3);
  not not_188 (not_188_out, OP5);
  not not_189 (not_189_out, OP4);
  not not_190 (not_190_out, OP3);
  not not_191 (not_191_out, OP2);
  not not_192 (not_192_out, OP1);
  not not_193 (not_193_out, OP0);
  not not_194 (not_194_out, F5);
  not not_195 (not_195_out, F4);
  not not_196 (not_196_out, F3);
  not not_197 (not_197_out, F2);
  not not_198 (not_198_out, F1);
  not not_199 (not_199_out, F0);
  not not_200 (not_200_out, OP5);
  not not_201 (not_201_out, OP4);
  not not_202 (not_202_out, OP3);
  not not_203 (not_203_out, OP2);
  not not_204 (not_204_out, OP1);
  not not_205 (not_205_out, OP0);
  not not_206 (not_206_out, F5);
  not not_207 (not_207_out, F4);
  not not_208 (not_208_out, F3);
  not not_209 (not_209_out, F2);
  not not_210 (not_210_out, OP5);
  not not_211 (not_211_out, OP4);
  not not_212 (not_212_out, OP3);
  not not_213 (not_213_out, OP2);
  not not_214 (not_214_out, OP1);
  not not_215 (not_215_out, OP0);
  not not_216 (not_216_out, F5);
  not not_217 (not_217_out, F4);
  not not_218 (not_218_out, F3);
  not not_219 (not_219_out, F2);
  not not_220 (not_220_out, F0);
  not not_221 (not_221_out, OP5);
  not not_222 (not_222_out, OP4);
  not not_223 (not_223_out, OP3);
  not not_224 (not_224_out, OP2);
  not not_225 (not_225_out, OP1);
  not not_226 (not_226_out, OP0);
  not not_227 (not_227_out, F4);
  not not_228 (not_228_out, F3);
  not not_229 (not_229_out, F2);
  not not_230 (not_230_out, F1);
  not not_231 (not_231_out, F0);
  not not_232 (not_232_out, OP5);
  not not_233 (not_233_out, OP4);
  not not_234 (not_234_out, OP3);
  not not_235 (not_235_out, OP2);
  not not_236 (not_236_out, OP1);
  not not_237 (not_237_out, OP0);
  not not_238 (not_238_out, F4);
  not not_239 (not_239_out, F3);
  not not_240 (not_240_out, F2);
  not not_241 (not_241_out, F1);
  not not_242 (not_242_out, OP5);
  not not_243 (not_243_out, OP4);
  not not_244 (not_244_out, OP3);
  not not_245 (not_245_out, OP2);
  not not_246 (not_246_out, OP1);
  not not_247 (not_247_out, OP0);
  not not_248 (not_248_out, F4);
  not not_249 (not_249_out, F3);
  not not_250 (not_250_out, F2);
  not not_251 (not_251_out, F0);
  not not_252 (not_252_out, OP5);
  not not_253 (not_253_out, OP4);
  not not_254 (not_254_out, OP3);
  not not_255 (not_255_out, OP2);
  not not_256 (not_256_out, OP1);
  not not_257 (not_257_out, OP0);
  not not_258 (not_258_out, F4);
  not not_259 (not_259_out, F3);
  not not_260 (not_260_out, F1);
  not not_261 (not_261_out, F0);
  not not_262 (not_262_out, OP5);
  not not_263 (not_263_out, OP4);
  not not_264 (not_264_out, OP3);
  not not_265 (not_265_out, OP2);
  not not_266 (not_266_out, OP1);
  not not_267 (not_267_out, OP0);
  not not_268 (not_268_out, F4);
  not not_269 (not_269_out, F3);
  not not_270 (not_270_out, F1);
  not not_271 (not_271_out, OP5);
  not not_272 (not_272_out, OP4);
  not not_273 (not_273_out, OP3);
  not not_274 (not_274_out, OP2);
  not not_275 (not_275_out, OP1);
  not not_276 (not_276_out, OP0);
  not not_277 (not_277_out, F4);
  not not_278 (not_278_out, F3);
  not not_279 (not_279_out, OP5);
  not not_280 (not_280_out, OP4);
  not not_281 (not_281_out, OP3);
  not not_282 (not_282_out, OP2);
  not not_283 (not_283_out, OP1);
  not not_284 (not_284_out, OP0);
  not not_285 (not_285_out, F4);
  not not_286 (not_286_out, F2);
  not not_287 (not_287_out, F0);
  not not_288 (not_288_out, OP5);
  not not_289 (not_289_out, OP4);
  not not_290 (not_290_out, OP3);
  not not_291 (not_291_out, OP2);
  not not_292 (not_292_out, OP1);
  not not_293 (not_293_out, OP0);
  not not_294 (not_294_out, F4);
  not not_295 (not_295_out, F2);
  not not_296 (not_296_out, OP5);
  not not_297 (not_297_out, OP4);
  not not_298 (not_298_out, OP3);
  not not_299 (not_299_out, OP2);
  not not_300 (not_300_out, OP1);
  not not_301 (not_301_out, OP0);
  not not_302 (not_302_out, F5);
  not not_303 (not_303_out, F4);
  not not_304 (not_304_out, F1);
  not not_305 (not_305_out, F0);
  not not_306 (not_306_out, OP5);
  not not_307 (not_307_out, OP4);
  not not_308 (not_308_out, OP3);
  not not_309 (not_309_out, OP1);
  not not_310 (not_310_out, OP0);
  not not_311 (not_311_out, OP5);
  not not_312 (not_312_out, OP4);
  not not_313 (not_313_out, OP3);
  not not_314 (not_314_out, OP1);
  not not_315 (not_315_out, OP4);
  not not_316 (not_316_out, OP2);
  not not_317 (not_317_out, OP5);
  not not_318 (not_318_out, OP4);
  not not_319 (not_319_out, OP3);
  not not_320 (not_320_out, OP2);
  not not_321 (not_321_out, OP1);
  not not_322 (not_322_out, OP0);
  not not_323 (not_323_out, F5);
  not not_324 (not_324_out, F4);
  not not_325 (not_325_out, F3);
  not not_326 (not_326_out, OP5);
  not not_327 (not_327_out, OP4);
  not not_328 (not_328_out, OP3);
  not not_329 (not_329_out, OP2);
  not not_330 (not_330_out, OP1);
  not not_331 (not_331_out, OP0);
  not not_332 (not_332_out, F4);
  not not_333 (not_333_out, F3);
  not not_334 (not_334_out, F2);
  not not_335 (not_335_out, OP5);
  not not_336 (not_336_out, OP4);
  not not_337 (not_337_out, OP3);
  and and_1 (and_1_out, not_1_out, not_2_out, not_3_out, not_4_out, not_5_out, not_6_out, not_7_out, not_8_out, not_9_out, not_10_out, not_11_out, not_12_out);
  and and_2 (and_2_out, not_13_out, not_14_out, not_15_out, not_16_out, not_17_out, not_18_out, not_19_out, not_20_out, not_21_out, not_22_out, F1, F0);
  and and_3 (and_3_out, not_23_out, not_24_out, not_25_out, not_26_out, not_27_out, not_28_out, not_29_out, not_30_out, not_31_out, not_32_out, F1, not_33_out);
  and and_4 (and_4_out, not_34_out, not_35_out, not_36_out, not_37_out, not_38_out, not_39_out, F5, not_40_out, not_41_out, not_42_out, not_43_out, not_44_out);
  and and_5 (and_5_out, not_45_out, not_46_out, not_47_out, not_48_out, not_49_out, not_50_out, F5, not_51_out, not_52_out, not_53_out, not_54_out, F0);
  and and_6 (and_6_out, not_55_out, not_56_out, not_57_out, not_58_out, not_59_out, not_60_out, F5, not_61_out, not_62_out, not_63_out, F1, not_64_out);
  and and_7 (and_7_out, not_65_out, not_66_out, not_67_out, not_68_out, not_69_out, not_70_out, F5, not_71_out, not_72_out, F2, not_73_out, not_74_out);
  and and_8 (and_8_out, not_75_out, not_76_out, not_77_out, not_78_out, not_79_out, not_80_out, F5, not_81_out, not_82_out, F2, not_83_out, F0);
  and and_9 (and_9_out, not_84_out, not_85_out, not_86_out, not_87_out, not_88_out, not_89_out, F5, not_90_out, not_91_out, F2, F1, F0);
  and and_10 (and_10_out, not_92_out, not_93_out, not_94_out, not_95_out, not_96_out, not_97_out, F5, not_98_out, F3, not_99_out, F1, not_100_out);
  and and_11 (and_11_out, not_101_out, not_102_out, not_103_out, not_104_out, not_105_out, not_106_out, F5, not_107_out, F3, not_108_out, F1, F0);
  and and_12 (and_12_out, not_109_out, not_110_out, not_111_out, not_112_out, not_113_out, not_114_out, not_115_out, not_116_out, F3, not_117_out, not_118_out, not_119_out);
  and and_13 (and_13_out, not_120_out, not_121_out, not_122_out, not_123_out, not_124_out, not_125_out, not_126_out, not_127_out, F3, F2, not_128_out, not_129_out);
  and and_14 (and_14_out, not_130_out, not_131_out, not_132_out, OP2, not_133_out, not_134_out);
  and and_15 (and_15_out, not_135_out, not_136_out, not_137_out, OP2, not_138_out, OP0);
  and and_16 (and_16_out, not_139_out, not_140_out, OP3, not_141_out, not_142_out, not_143_out);
  and and_17 (and_17_out, not_144_out, not_145_out, OP3, OP2, not_146_out, not_147_out);
  and and_18 (and_18_out, not_148_out, not_149_out, OP3, not_150_out, not_151_out, OP0);
  and and_19 (and_19_out, not_152_out, not_153_out, OP3, not_154_out, OP1, not_155_out);
  and and_20 (and_20_out, not_156_out, not_157_out, OP3, OP2, not_158_out, OP0);
  and and_21 (and_21_out, OP5, not_159_out, not_160_out, not_161_out, OP1, OP0);
  and and_22 (and_22_out, OP5, not_162_out, OP3, not_163_out, OP1, OP0);
  and and_23 (and_23_out, not_164_out, not_165_out, not_166_out, not_167_out, not_168_out, not_169_out, not_170_out, not_171_out, not_172_out, F2, F1, F0);
  and and_24 (and_24_out, not_173_out, not_174_out, not_175_out, not_176_out, not_177_out, not_178_out, F5, not_179_out, not_180_out, not_181_out, F1, F0);
  and and_25 (and_25_out, OP5, not_182_out, not_183_out, OP2, not_184_out, OP0);
  and and_26 (and_26_out, not_185_out, not_186_out, not_187_out, OP2, OP1, OP0);
  and and_27 (and_27_out, not_188_out, not_189_out, not_190_out, not_191_out, not_192_out, not_193_out, not_194_out, not_195_out, not_196_out, not_197_out, not_198_out, not_199_out);
  and and_28 (and_28_out, not_200_out, not_201_out, not_202_out, not_203_out, not_204_out, not_205_out, not_206_out, not_207_out, not_208_out, not_209_out, F1, F0);
  and and_29 (and_29_out, not_210_out, not_211_out, not_212_out, not_213_out, not_214_out, not_215_out, not_216_out, not_217_out, not_218_out, not_219_out, F1, not_220_out);
  and and_30 (and_30_out, not_221_out, not_222_out, not_223_out, not_224_out, not_225_out, not_226_out, F5, not_227_out, not_228_out, not_229_out, not_230_out, not_231_out);
  and and_31 (and_31_out, not_232_out, not_233_out, not_234_out, not_235_out, not_236_out, not_237_out, F5, not_238_out, not_239_out, not_240_out, not_241_out, F0);
  and and_32 (and_32_out, not_242_out, not_243_out, not_244_out, not_245_out, not_246_out, not_247_out, F5, not_248_out, not_249_out, not_250_out, F1, not_251_out);
  and and_33 (and_33_out, not_252_out, not_253_out, not_254_out, not_255_out, not_256_out, not_257_out, F5, not_258_out, not_259_out, F2, not_260_out, not_261_out);
  and and_34 (and_34_out, not_262_out, not_263_out, not_264_out, not_265_out, not_266_out, not_267_out, F5, not_268_out, not_269_out, F2, not_270_out, F0);
  and and_35 (and_35_out, not_271_out, not_272_out, not_273_out, not_274_out, not_275_out, not_276_out, F5, not_277_out, not_278_out, F2, F1, F0);
  and and_36 (and_36_out, not_279_out, not_280_out, not_281_out, not_282_out, not_283_out, not_284_out, F5, not_285_out, F3, not_286_out, F1, not_287_out);
  and and_37 (and_37_out, not_288_out, not_289_out, not_290_out, not_291_out, not_292_out, not_293_out, F5, not_294_out, F3, not_295_out, F1, F0);
  and and_38 (and_38_out, not_296_out, not_297_out, not_298_out, not_299_out, not_300_out, not_301_out, not_302_out, not_303_out, F3, F2, not_304_out, not_305_out);
  and and_39 (and_39_out, not_306_out, not_307_out, not_308_out, OP2, not_309_out, not_310_out);
  and and_40 (and_40_out, not_311_out, not_312_out, not_313_out, OP2, not_314_out, OP0);
  and and_41 (and_41_out, OP5, not_315_out, OP3, not_316_out, OP1, OP0);
  and and_42 (and_42_out, not_317_out, not_318_out, not_319_out, not_320_out, not_321_out, not_322_out, not_323_out, not_324_out, not_325_out, F2, F1, F0);
  and and_43 (and_43_out, not_326_out, not_327_out, not_328_out, not_329_out, not_330_out, not_331_out, F5, not_332_out, not_333_out, not_334_out, F1, F0);
  and and_44 (and_44_out, not_335_out, not_336_out, not_337_out, OP2, OP1, OP0);
  or or_1 (R1_Used, and_1_out, and_2_out, and_3_out, and_4_out, and_5_out, and_6_out, and_7_out, and_8_out, and_9_out, and_10_out, and_11_out, and_12_out, and_13_out, and_14_out, and_15_out, and_16_out, and_17_out, and_18_out, and_19_out, and_20_out, and_21_out, and_22_out, and_23_out, and_24_out, and_25_out, and_26_out);
  or or_2 (R2_Used, and_27_out, and_28_out, and_29_out, and_30_out, and_31_out, and_32_out, and_33_out, and_34_out, and_35_out, and_36_out, and_37_out, and_38_out, and_39_out, and_40_out, and_41_out, and_42_out, and_43_out, and_44_out);
endmodule

module \数据相关检测  (
  input  [5:0] OP,
  input  [4:0] EX_WriteReg_num,
  input  EX_RegWrite,
  input  [4:0] MEM_WriteReg_num,
  input  MEM_RegWrite,
  input  [5:0] Func,
  input  [4:0] ID_R1_num,
  input  [4:0] ID_R2_num,
  output \数据相关 
);

  wire and_1_out, and_2_out, and_3_out, and_4_out, and_5_out, and_6_out, comparator_1_eq, comparator_2_eq,
       comparator_3_eq, comparator_4_eq, comparator_5_eq, comparator_6_eq, or_1_out, or_2_out, R1_used,
       R2_used;

  \源寄存器使用情况  \u_源寄存器使用情况_1  (
    .OP0(OP[0]), .OP1(OP[1]), .OP2(OP[2]), .OP3(OP[3]), .OP4(OP[4]), .OP5(OP[5]), .F0(Func[0]), .F1(Func[1]),
    .F2(Func[2]), .F3(Func[3]), .F4(Func[4]), .F5(Func[5]), .R1_Used(R1_used), .R2_Used(R2_used));
  Comparator #(.width(5)) comparator_1 (.a({5{1'b0}}), .b(ID_R1_num), .eq(comparator_1_eq));  // open: gt, lt
  Comparator #(.width(5)) comparator_2 (.a(ID_R1_num), .b(EX_WriteReg_num), .eq(comparator_2_eq));  // open: gt, lt
  Comparator #(.width(5)) comparator_3 (.a(ID_R1_num), .b(MEM_WriteReg_num), .eq(comparator_3_eq));  // open: gt, lt
  Comparator #(.width(5)) comparator_4 (.a({5{1'b0}}), .b(ID_R2_num), .eq(comparator_4_eq));  // open: gt, lt
  Comparator #(.width(5)) comparator_5 (.a(ID_R2_num), .b(EX_WriteReg_num), .eq(comparator_5_eq));  // open: gt, lt
  Comparator #(.width(5)) comparator_6 (.a(ID_R2_num), .b(MEM_WriteReg_num), .eq(comparator_6_eq));  // open: gt, lt
  and and_1 (and_1_out, EX_RegWrite, comparator_2_eq);
  and and_2 (and_2_out, MEM_RegWrite, comparator_3_eq);
  and and_3 (and_3_out, EX_RegWrite, comparator_5_eq);
  and and_4 (and_4_out, MEM_RegWrite, comparator_6_eq);
  or or_1 (or_1_out, and_1_out, and_2_out);
  or or_2 (or_2_out, and_3_out, and_4_out);
  and and_5 (and_5_out, R1_used, ~comparator_1_eq, or_1_out);  // AND_Gate
  and and_6 (and_6_out, R2_used, ~comparator_4_eq, or_2_out);  // AND_Gate
  or or_3 (\数据相关 , and_5_out, and_6_out);

  // Other names for the same wires on the sheet: OP_CODE[5:0] = OP
endmodule

module IF_ID (
  input  [31:0] instruction,
  input  [31:0] pc4,
  input  [31:0] pc,
  input  hit,
  input  jump_att,
  input  [2:0] hit_pos,
  input  stop,
  input  clk,
  input  rst,
  output [31:0] instruction_2,
  output [31:0] pc4_2,
  output [31:0] pc_2,
  output hit_2,
  output jump_att_2,
  output [2:0] hit_pos_2
);

  wire multiplexer_4_out, multiplexer_5_out;
  wire [2:0] multiplexer_6_out;
  wire [31:0] multiplexer_1_out, multiplexer_2_out, multiplexer_3_out;

  Multiplexer #(.width(32), .enable("false")) multiplexer_1 (
    .in0(instruction), .in1({32{1'b0}}), .out(multiplexer_1_out), .sel(rst));
  Multiplexer #(.width(32), .enable("false")) multiplexer_2 (
    .in0(pc4), .in1({32{1'b0}}), .out(multiplexer_2_out), .sel(rst));
  Multiplexer #(.width(32), .enable("false")) multiplexer_3 (
    .in0(pc), .in1({32{1'b0}}), .out(multiplexer_3_out), .sel(rst));
  Multiplexer #(.enable("false")) multiplexer_4 (.in0(hit), .in1(1'b0), .out(multiplexer_4_out), .sel(rst));
  Multiplexer #(.enable("false")) multiplexer_5 (.in0(jump_att), .in1(1'b0), .out(multiplexer_5_out), .sel(rst));
  Multiplexer #(.width(3), .enable("false")) multiplexer_6 (
    .in0(hit_pos), .in1(3'b000), .out(multiplexer_6_out), .sel(rst));
  Register #(.width(32)) register_1 (.D(multiplexer_1_out), .en(stop), .Q(instruction_2), .clk(clk));  // open: clr
  Register #(.width(32)) register_2 (.D(multiplexer_2_out), .en(stop), .Q(pc4_2), .clk(clk));  // open: clr
  Register #(.width(32)) register_3 (.D(multiplexer_3_out), .en(stop), .Q(pc_2), .clk(clk));  // open: clr
  Register #(.width(1)) register_4 (.D(multiplexer_4_out), .en(stop), .Q(hit_2), .clk(clk));  // open: clr
  Register #(.width(1)) register_5 (.D(multiplexer_5_out), .en(stop), .Q(jump_att_2), .clk(clk));  // open: clr
  Register #(.width(3)) register_6 (.D(multiplexer_6_out), .en(stop), .Q(hit_pos_2), .clk(clk));  // open: clr
endmodule

// 10signed
module ID_EX (
  input  [18:0] control,
  input  [31:0] instruction,
  input  [31:0] pc4,
  input  [31:0] R1,
  input  [31:0] R2,
  input  [31:0] pc,
  input  [4:0] shamt,
  input  [31:0] imm,
  input  [31:0] signimm,
  input  hit,
  input  jump_att,
  input  [2:0] hit_pos,
  input  stop,
  input  clk,
  input  rst,
  output [18:0] control_2,
  output [31:0] instruction_2,
  output [31:0] pc4_2,
  output [31:0] R1_2,
  output [31:0] R2_2,
  output [31:0] pc_2,
  output [4:0] shamt_2,
  output [31:0] imm_2,
  output [31:0] signimm_2,
  output hit_2,
  output jump_att_2,
  output [2:0] hit_pos_2
);

  wire multiplexer_10_out, multiplexer_11_out;
  wire [2:0] multiplexer_12_out;
  wire [4:0] multiplexer_7_out;
  wire [18:0] multiplexer_1_out;
  wire [31:0] multiplexer_2_out, multiplexer_3_out, multiplexer_4_out, multiplexer_5_out, multiplexer_6_out,
       multiplexer_8_out, multiplexer_9_out;

  Multiplexer #(.width(19), .enable("false")) multiplexer_1 (
    .in0(control), .in1({19{1'b0}}), .out(multiplexer_1_out), .sel(rst));
  Multiplexer #(.width(32), .enable("false")) multiplexer_2 (
    .in0(instruction), .in1({32{1'b0}}), .out(multiplexer_2_out), .sel(rst));
  Multiplexer #(.width(32), .enable("false")) multiplexer_3 (
    .in0(pc4), .in1({32{1'b0}}), .out(multiplexer_3_out), .sel(rst));
  Multiplexer #(.width(32), .enable("false")) multiplexer_4 (
    .in0(R1), .in1({32{1'b0}}), .out(multiplexer_4_out), .sel(rst));
  Multiplexer #(.width(32), .enable("false")) multiplexer_5 (
    .in0(R2), .in1({32{1'b0}}), .out(multiplexer_5_out), .sel(rst));
  Multiplexer #(.width(32), .enable("false")) multiplexer_6 (
    .in0(pc), .in1({32{1'b0}}), .out(multiplexer_6_out), .sel(rst));
  Multiplexer #(.width(5), .enable("false")) multiplexer_7 (
    .in0(shamt), .in1({5{1'b0}}), .out(multiplexer_7_out), .sel(rst));
  Multiplexer #(.width(32), .enable("false")) multiplexer_8 (
    .in0(imm), .in1({32{1'b0}}), .out(multiplexer_8_out), .sel(rst));
  Multiplexer #(.width(32), .enable("false")) multiplexer_9 (
    .in0(signimm), .in1({32{1'b0}}), .out(multiplexer_9_out), .sel(rst));
  Multiplexer #(.enable("false")) multiplexer_10 (.in0(hit), .in1(1'b0), .out(multiplexer_10_out), .sel(rst));
  Multiplexer #(.enable("false")) multiplexer_11 (.in0(jump_att), .in1(1'b0), .out(multiplexer_11_out), .sel(rst));
  Multiplexer #(.width(3), .enable("false")) multiplexer_12 (
    .in0(hit_pos), .in1(3'b000), .out(multiplexer_12_out), .sel(rst));
  Register #(.width(19)) register_1 (.D(multiplexer_1_out), .en(stop), .Q(control_2), .clk(clk));  // open: clr
  Register #(.width(32)) register_2 (.D(multiplexer_2_out), .en(stop), .Q(instruction_2), .clk(clk));  // open: clr
  Register #(.width(32)) register_3 (.D(multiplexer_3_out), .en(stop), .Q(pc4_2), .clk(clk));  // open: clr
  Register #(.width(32)) register_4 (.D(multiplexer_4_out), .en(stop), .Q(R1_2), .clk(clk));  // open: clr
  Register #(.width(32)) register_5 (.D(multiplexer_5_out), .en(stop), .Q(R2_2), .clk(clk));  // open: clr
  Register #(.width(32)) register_6 (.D(multiplexer_6_out), .en(stop), .Q(pc_2), .clk(clk));  // open: clr
  Register #(.width(5)) register_7 (.D(multiplexer_7_out), .en(stop), .Q(shamt_2), .clk(clk));  // open: clr
  Register #(.width(32)) register_8 (.D(multiplexer_8_out), .en(stop), .Q(imm_2), .clk(clk));  // open: clr
  Register #(.width(32)) register_9 (.D(multiplexer_9_out), .en(stop), .Q(signimm_2), .clk(clk));  // open: clr
  Register #(.width(1)) register_10 (.D(multiplexer_10_out), .en(stop), .Q(hit_2), .clk(clk));  // open: clr
  Register #(.width(1)) register_11 (.D(multiplexer_11_out), .en(stop), .Q(jump_att_2), .clk(clk));  // open: clr
  Register #(.width(3)) register_12 (.D(multiplexer_12_out), .en(stop), .Q(hit_pos_2), .clk(clk));  // open: clr
endmodule
module EX_MEM (
  input  [18:0] control,
  input  [31:0] instruction,
  input  [31:0] pc4,
  input  [31:0] R2,
  input  [31:0] alu,
  input  equal,
  input  [31:0] R1,
  input  stop,
  input  rst,
  input  clk,
  output [18:0] control_2,
  output [31:0] instruction_2,
  output [31:0] pc4_2,
  output [31:0] R2_2,
  output [31:0] alu_2,
  output equal_2,
  output [31:0] R1_2
);

  wire multiplexer_6_out;
  wire [18:0] multiplexer_1_out;
  wire [31:0] multiplexer_2_out, multiplexer_3_out, multiplexer_4_out, multiplexer_5_out, multiplexer_7_out;

  Multiplexer #(.width(19), .enable("false")) multiplexer_1 (
    .in0(control), .in1({19{1'b0}}), .out(multiplexer_1_out), .sel(rst));
  Multiplexer #(.width(32), .enable("false")) multiplexer_2 (
    .in0(instruction), .in1({32{1'b0}}), .out(multiplexer_2_out), .sel(rst));
  Multiplexer #(.width(32), .enable("false")) multiplexer_3 (
    .in0(pc4), .in1({32{1'b0}}), .out(multiplexer_3_out), .sel(rst));
  Multiplexer #(.width(32), .enable("false")) multiplexer_4 (
    .in0(R2), .in1({32{1'b0}}), .out(multiplexer_4_out), .sel(rst));
  Multiplexer #(.width(32), .enable("false")) multiplexer_5 (
    .in0(alu), .in1({32{1'b0}}), .out(multiplexer_5_out), .sel(rst));
  Multiplexer #(.enable("false")) multiplexer_6 (.in0(equal), .in1(1'b0), .out(multiplexer_6_out), .sel(rst));
  Multiplexer #(.width(32), .enable("false")) multiplexer_7 (
    .in0(R1), .in1({32{1'b0}}), .out(multiplexer_7_out), .sel(rst));
  Register #(.width(19)) register_1 (.D(multiplexer_1_out), .en(stop), .Q(control_2), .clk(clk));  // open: clr
  Register #(.width(32)) register_2 (.D(multiplexer_2_out), .en(stop), .Q(instruction_2), .clk(clk));  // open: clr
  Register #(.width(32)) register_3 (.D(multiplexer_3_out), .en(stop), .Q(pc4_2), .clk(clk));  // open: clr
  Register #(.width(32)) register_4 (.D(multiplexer_4_out), .en(stop), .Q(R2_2), .clk(clk));  // open: clr
  Register #(.width(32)) register_5 (.D(multiplexer_5_out), .en(stop), .Q(alu_2), .clk(clk));  // open: clr
  Register #(.width(1)) register_6 (.D(multiplexer_6_out), .en(stop), .Q(equal_2), .clk(clk));  // open: clr
  Register #(.width(32)) register_7 (.D(multiplexer_7_out), .en(stop), .Q(R1_2), .clk(clk));  // open: clr
endmodule

module MEM_WB (
  input  [18:0] control,
  input  [31:0] instruction,
  input  [31:0] pc4,
  input  [31:0] md,
  input  [31:0] alu,
  input  equal,
  input  [31:0] R1,
  input  stop,
  input  clk,
  input  rst,
  output [18:0] control_2,
  output [31:0] instruction_2,
  output [31:0] pc4_2,
  output [31:0] md_2,
  output [31:0] alu_2,
  output equal_2,
  output [31:0] R1_2
);

  wire multiplexer_6_out;
  wire [18:0] multiplexer_1_out;
  wire [31:0] multiplexer_2_out, multiplexer_3_out, multiplexer_4_out, multiplexer_5_out, multiplexer_7_out;

  Multiplexer #(.width(19), .enable("false")) multiplexer_1 (
    .in0(control), .in1({19{1'b0}}), .out(multiplexer_1_out), .sel(rst));
  Multiplexer #(.width(32), .enable("false")) multiplexer_2 (
    .in0(instruction), .in1({32{1'b0}}), .out(multiplexer_2_out), .sel(rst));
  Multiplexer #(.width(32), .enable("false")) multiplexer_3 (
    .in0(pc4), .in1({32{1'b0}}), .out(multiplexer_3_out), .sel(rst));
  Multiplexer #(.width(32), .enable("false")) multiplexer_4 (
    .in0(md), .in1({32{1'b0}}), .out(multiplexer_4_out), .sel(rst));
  Multiplexer #(.width(32), .enable("false")) multiplexer_5 (
    .in0(alu), .in1({32{1'b0}}), .out(multiplexer_5_out), .sel(rst));
  Multiplexer #(.enable("false")) multiplexer_6 (.in0(equal), .in1(1'b0), .out(multiplexer_6_out), .sel(rst));
  Multiplexer #(.width(32), .enable("false")) multiplexer_7 (
    .in0(R1), .in1({32{1'b0}}), .out(multiplexer_7_out), .sel(rst));
  Register #(.width(19)) register_1 (.D(multiplexer_1_out), .en(stop), .Q(control_2), .clk(clk));  // open: clr
  Register #(.width(32)) register_2 (.D(multiplexer_2_out), .en(stop), .Q(instruction_2), .clk(clk));  // open: clr
  Register #(.width(32)) register_3 (.D(multiplexer_3_out), .en(stop), .Q(pc4_2), .clk(clk));  // open: clr
  Register #(.width(32)) register_4 (.D(multiplexer_4_out), .en(stop), .Q(md_2), .clk(clk));  // open: clr
  Register #(.width(32)) register_5 (.D(multiplexer_5_out), .en(stop), .Q(alu_2), .clk(clk));  // open: clr
  Register #(.width(1)) register_6 (.D(multiplexer_6_out), .en(stop), .Q(equal_2), .clk(clk));  // open: clr
  Register #(.width(32)) register_7 (.D(multiplexer_7_out), .en(stop), .Q(R1_2), .clk(clk));  // open: clr
endmodule

module \分支相关流水线  (
);

  wire and_1_out, and_2_out, and_3_out, and_4_out, and_5_out, CLK, equal5, ex_mem_1_equal_2, Go, IR1, IR2,
       IR3, jal5, lhu, mips_alu_1_equal, not_1_out, or_1_out, or_2_out, regdst5, regwrite5, RST, SignedExt,
       srav, stop, syscall3, syscall5, W1, W2, W3;
  wire [2:2] or_3_out;
  wire [3:0] \硬布线控制器_1_alu_op ;
  wire [4:0] id_ex_1_shamt_2, multiplexer_3_out, multiplexer_4_out, multiplexer_5_out, multiplexer_6_out,
       multiplexer_10_out, rd5, rt5;
  wire [15:0] \LoadUse次数 , multiplexer_14_out, \总周期数 , \插入气泡数 , \无条件分支数 , \条件分支成功数 ;
  wire [17:0] mem_wb_1_control_2;
  wire [18:0] ex_mem_1_control_2, id_ex_1_control_2, \硬布线控制器_1_jmp ;
  wire [31:0] a3, a5, adder_1_out, adder_2_out, bit_extender_1_out, bit_extender_2_out, ex_mem_1_alu_2,
       ex_mem_1_instruction_2, ex_mem_1_r1_2, ex_mem_1_r2_2, EX_PC, id_ex_1_imm_2, id_ex_1_instruction_2,
       id_ex_1_r2_2, id_ex_1_signimm_2, ID_PC, if_id_1_instruction_2, IF_PC, LedData, MEM_PC,
       mem_wb_1_instruction_2, mem_wb_1_md_2, mips_alu_1_result, mips_regifile_1_r1, mips_regifile_1_r2,
       multiplexer_1_out, multiplexer_7_out, multiplexer_8_out, multiplexer_9_out, multiplexer_11_out,
       multiplexer_12_out, multiplexer_13_out, ram_1_data, result5, rom_1_data, shifter_1_out, WB_PC;

  Button \u_总复位  (.out(RST));
  Button _1 (.out(IR1));
  Button _2 (.out(IR2));
  Button _3 (.out(IR3));
  Button \u_继续运行  (.out(Go));
  LED led_1 (.in(W1));
  LED led_2 (.in(W2));
  LED led_3 (.in(W3));
  Hex_Digit_Display hex_digit_display_1 (.value(LedData[31:28]));  // open: dp
  Multiplexer #(.select(3), .width(32), .enable("false")) multiplexer_1 (
    .in0(adder_1_out), .in1({32{1'b0}}), .in2({EX_PC[31:28], id_ex_1_instruction_2[25:0], 2'b00}), .in3(a3),
    .in4(adder_2_out), .in5({32{1'b0}}), .in6({32{1'b0}}), .in7({32{1'b0}}), .out(multiplexer_1_out),
    .sel({or_3_out[2], id_ex_1_control_2[0], id_ex_1_control_2[1]}));
  Hex_Digit_Display hex_digit_display_2 (.value(LedData[27:24]));  // open: dp
  Hex_Digit_Display hex_digit_display_3 (.value(LedData[23:20]));  // open: dp
  Register #(.width(32)) PC (.D(multiplexer_1_out), .en(stop), .Q(IF_PC), .clk(CLK), .clr(RST));
  Hex_Digit_Display hex_digit_display_4 (.value(LedData[19:16]));  // open: dp
  Hex_Digit_Display hex_digit_display_5 (.value(LedData[15:12]));  // open: dp
  Adder #(.width(32)) adder_1 (.a(IF_PC), .b(32'h4), .out(adder_1_out));  // open: cin, cout
  and and_1 (and_1_out, syscall5, equal5);
  Hex_Digit_Display hex_digit_display_6 (.value(LedData[11:8]));  // open: dp
  Hex_Digit_Display hex_digit_display_7 (.value(LedData[7:4]));  // open: dp
  Clock clock_1 (.out(CLK));
  ROM #(.addrWidth(10), .dataWidth(32)) rom_1 (.addr(IF_PC[11:2]), .data(rom_1_data));  // open: sel
  Register #(.width(32)) register_1 (.D(a5), .en(and_1_out), .Q(LedData), .clk(CLK), .clr(RST));
  Hex_Digit_Display hex_digit_display_8 (.value(LedData[3:0]));  // open: dp
  IF_ID if_id_1 (
    .instruction(rom_1_data), .pc4(adder_1_out), .instruction_2(if_id_1_instruction_2), .pc4_2(ID_PC),
    .rst(or_1_out), .clk(CLK), .stop(stop));  // open: hit, hit_2, jump_att, jump_att_2, hit_pos, hit_pos_2, pc, pc_2
  and and_2 (and_2_out, syscall5, ~equal5);  // AND_Gate
  // Probe on \总周期数 
  // Probe on \无条件分支数 
  // Probe on \条件分支成功数 
  // Probe on \插入气泡数 
  // Probe on \LoadUse次数 
  Multiplexer #(.enable("false")) multiplexer_2 (.in0(1'b1), .in1(Go), .out(stop), .sel(and_2_out));
  // Probe on IF_PC[11:0]
  \硬布线控制器  \u_硬布线控制器_1  (
    .Func(if_id_1_instruction_2[5:0]), .OP(if_id_1_instruction_2[31:26]), .ALU_OP(\硬布线控制器_1_alu_op ),
    .MemToReg(\硬布线控制器_1_jmp [5]), .MemWrite(\硬布线控制器_1_jmp [6]), .ALU_SRC(\硬布线控制器_1_jmp [11]),
    .RegWrite(\硬布线控制器_1_jmp [12]), .SysCALL(\硬布线控制器_1_jmp [16]), .SignedExt(SignedExt),
    .RegDst(\硬布线控制器_1_jmp [14]), .JR(\硬布线控制器_1_jmp [1]), .JMP(\硬布线控制器_1_jmp [0]), .Beq(\硬布线控制器_1_jmp [3]),
    .JAL(\硬布线控制器_1_jmp [13]), .Bne(\硬布线控制器_1_jmp [4]), .SRAV(\硬布线控制器_1_jmp [15]), .LHU(\硬布线控制器_1_jmp [18]),
    .BGTZ(\硬布线控制器_1_jmp [17]));
  Multiplexer #(.width(5), .enable("false")) multiplexer_3 (
    .in0(if_id_1_instruction_2[25:21]), .in1(5'b00100), .out(multiplexer_3_out), .sel(\硬布线控制器_1_jmp [16]));
  Multiplexer #(.width(5), .enable("false")) multiplexer_4 (
    .in0(if_id_1_instruction_2[20:16]), .in1(5'b00010), .out(multiplexer_4_out), .sel(\硬布线控制器_1_jmp [16]));
  Counter #(.width(16), .max('hffff)) counter_1 (
    .count(stop), .Q(\总周期数 ), .clk(CLK), .clr(RST));  // open: load, D, carry
  // Probe on ID_PC[11:0]
  Multiplexer #(.width(5), .enable("false")) multiplexer_5 (
    .in0(rt5), .in1(rd5), .out(multiplexer_5_out), .sel(regdst5));
  Multiplexer #(.width(5), .enable("false")) multiplexer_6 (
    .in0(multiplexer_5_out), .in1({5{1'b1}}), .out(multiplexer_6_out), .sel(jal5));
  assign bit_extender_1_out = {{16{1'b0}}, if_id_1_instruction_2[15:0]};  // Bit_Extender bit_extender_1
  assign bit_extender_2_out = {{16{if_id_1_instruction_2[15]}}, if_id_1_instruction_2[15:0]};  // Bit_Extender bit_extender_2
  // Probe on MEM_PC[11:0]
  // Probe on EX_PC[11:0]
  MIPS_Regifile mips_regifile_1 (
    .Din(multiplexer_12_out), .Clk(CLK), .R1(mips_regifile_1_r1), .R2(mips_regifile_1_r2), .WE(regwrite5),
    .W_num(multiplexer_6_out), .R1_num(multiplexer_3_out), .R2_num(multiplexer_4_out));
  Multiplexer #(.width(32), .enable("false")) multiplexer_7 (
    .in0(bit_extender_1_out), .in1(bit_extender_2_out), .out(multiplexer_7_out), .sel(SignedExt));
  // Probe on WB_PC[11:0]
  or or_1 (or_1_out, RST, or_2_out);
  ID_EX id_ex_1 (
    .control({\硬布线控制器_1_jmp [18:11], \硬布线控制器_1_alu_op , \硬布线控制器_1_jmp [6:3], SignedExt, \硬布线控制器_1_jmp [1:0]}),
    .instruction(if_id_1_instruction_2), .pc4(ID_PC), .R1(mips_regifile_1_r1), .R2(mips_regifile_1_r2),
    .imm(multiplexer_7_out), .control_2({id_ex_1_control_2[18:17], syscall3, srav, id_ex_1_control_2[14:0]}),
    .instruction_2(id_ex_1_instruction_2), .pc4_2(EX_PC), .R1_2(a3), .R2_2(id_ex_1_r2_2),
    .imm_2(id_ex_1_imm_2), .rst(or_1_out), .stop(stop), .clk(CLK), .shamt(if_id_1_instruction_2[10:6]),
    .shamt_2(id_ex_1_shamt_2), .signimm(bit_extender_2_out), .signimm_2(id_ex_1_signimm_2));  // open: hit, hit_2, jump_att, jump_att_2, hit_pos, hit_pos_2, pc, pc_2
  or or_2 (or_2_out, id_ex_1_control_2[0], or_3_out[2]);
  Multiplexer #(.width(32), .enable("false")) multiplexer_8 (
    .in0(a3), .in1(32'h22), .out(multiplexer_8_out), .sel(syscall3));
  Multiplexer #(.width(32), .enable("false")) multiplexer_9 (
    .in0(id_ex_1_r2_2), .in1(id_ex_1_imm_2), .out(multiplexer_9_out), .sel(id_ex_1_control_2[11]));
  Shifter #(.width(32)) shifter_1 (.in(id_ex_1_signimm_2), .\dist (5'b00010), .out(shifter_1_out));
  MIPS_ALU mips_alu_1 (
    .X(multiplexer_8_out), .Y(multiplexer_9_out), .AluOP(id_ex_1_control_2[10:7]), .Equal(mips_alu_1_equal),
    .Result(mips_alu_1_result), .shamt(multiplexer_10_out));  // open: Result_2
  Multiplexer #(.width(5), .enable("false")) multiplexer_10 (
    .in0(id_ex_1_shamt_2), .in1(a3[4:0]), .out(multiplexer_10_out), .sel(srav));
  Adder #(.width(32)) adder_2 (.a(EX_PC), .b(shifter_1_out), .out(adder_2_out));  // open: cin, cout
  and and_3 (and_3_out, id_ex_1_control_2[3], mips_alu_1_equal);
  and and_4 (and_4_out, id_ex_1_control_2[4], ~mips_alu_1_equal);  // AND_Gate
  and and_5 (and_5_out, id_ex_1_control_2[17], ~mips_alu_1_equal, ~mips_alu_1_result[0]);  // AND_Gate
  or or_3 (or_3_out[2], and_3_out, and_4_out, and_5_out);
  Counter #(.width(16), .max('hffff)) counter_2 (
    .count(id_ex_1_control_2[0]), .Q(\无条件分支数 ), .clk(CLK), .clr(RST));  // open: load, D, carry
  Counter #(.width(16), .max('hffff)) counter_3 (
    .count(or_3_out[2]), .Q(\条件分支成功数 ), .clk(CLK), .clr(RST));  // open: load, D, carry
  EX_MEM ex_mem_1 (
    .control({id_ex_1_control_2[18:17], syscall3, srav, id_ex_1_control_2[14:0]}),
    .instruction(id_ex_1_instruction_2), .pc4(EX_PC), .R2(id_ex_1_r2_2), .alu(mips_alu_1_result),
    .control_2(ex_mem_1_control_2), .instruction_2(ex_mem_1_instruction_2), .pc4_2(MEM_PC),
    .R2_2(ex_mem_1_r2_2), .alu_2(ex_mem_1_alu_2), .rst(RST), .stop(stop), .clk(CLK),
    .equal(mips_alu_1_equal), .equal_2(ex_mem_1_equal_2), .R1(a3), .R1_2(ex_mem_1_r1_2));
  RAM #(.addrWidth(10), .dataWidth(32), .bus("separate")) ram_1 (
    .addr(ex_mem_1_alu_2[11:2]), .din(ex_mem_1_r2_2), .data(ram_1_data), .str(ex_mem_1_control_2[6]),
    .clk(CLK), .ld(not_1_out), .clr(RST));  // open: sel
  not not_1 (not_1_out, ex_mem_1_control_2[6]);
  MEM_WB mem_wb_1 (
    .control(ex_mem_1_control_2), .instruction(ex_mem_1_instruction_2), .pc4(MEM_PC), .md(ram_1_data),
    .alu(ex_mem_1_alu_2),
    .control_2({lhu, mem_wb_1_control_2[17], syscall5, mem_wb_1_control_2[15], regdst5, jal5, regwrite5, mem_wb_1_control_2[11:0]}),
    .instruction_2({mem_wb_1_instruction_2[31:21], rt5, rd5, mem_wb_1_instruction_2[10:0]}), .pc4_2(WB_PC),
    .md_2(mem_wb_1_md_2), .alu_2(result5), .rst(RST), .stop(stop), .clk(CLK), .equal(ex_mem_1_equal_2),
    .equal_2(equal5), .R1(ex_mem_1_r1_2), .R1_2(a5));
  Multiplexer #(.width(32), .enable("false")) multiplexer_11 (
    .in0(result5), .in1(mem_wb_1_md_2), .out(multiplexer_11_out), .sel(mem_wb_1_control_2[5]));
  Multiplexer #(.width(32), .enable("false")) multiplexer_12 (
    .in0(multiplexer_13_out), .in1(WB_PC), .out(multiplexer_12_out), .sel(jal5));
  Multiplexer #(.width(32), .enable("false")) multiplexer_13 (
    .in0(multiplexer_11_out), .in1({{16{1'b0}}, multiplexer_14_out}), .out(multiplexer_13_out), .sel(lhu));
  Multiplexer #(.width(16), .enable("false")) multiplexer_14 (
    .in0(multiplexer_11_out[15:0]), .in1(multiplexer_11_out[31:16]), .out(multiplexer_14_out),
    .sel(result5[1]));

  // Notes on the sheet:
  //   中断源
  //   中断等待指示
  //   数码管输出
  //   指令存储器
  //   contents of rom_1 (hex, n*v repeats v):
  //   20110020 20020022 8000c06 20110000 20110000 2002000a 10000003 20110000 20110000 2002000a 14110003
  //   20110000 20110000 2002000a c000c14 2002000a 0 0 0 c 2231ffff 0 0 0 112020 0 0 0 c 1620fff6 3e00008
  //   指令字
  //   OP
  //   Func
  //   rs
  //   rt
  //   rd
  //   shamt
  //   imm
  //   JMP
  //   JR
  //   OP
  //   Func
  //   Beq
  //   Bne
  //   MemToReg
  //   MemWrite
  //   AluOP
  //   AluSrcB
  //   RegWrite
  //   JAL
  //   RegDst
  //   流水调试日志用
  //   rt
  //   rd
endmodule

module \气泡流水线  (
);

  wire and_1_out, and_2_out, and_3_out, and_4_out, and_5_out, and_6_out, CLK, equal5, ex_mem_1_equal_2,
       EX_RegWrite, Go, IR1, IR2, IR3, jal3, jal4, jal5, lhu, MEM_RegWrite, mips_alu_1_equal, not_1_out,
       not_2_out, or_1_out, or_2_out, or_3_out, regdst3, regdst4, regdst5, regwrite5, RST, SignedExt, srav,
       stop, syscall3, syscall5, W1, W2, W3, \数据相关 ;
  wire [2:2] or_4_out;
  wire [3:0] \硬布线控制器_1_alu_op ;
  wire [4:0] EX_WriteReg_num, id_ex_1_shamt_2, ID_R1_num, ID_R2_num, MEM_WriteReg_num, multiplexer_5_out,
       multiplexer_6_out, multiplexer_10_out, multiplexer_11_out, multiplexer_13_out, rd3, rd4, rd5, rt3,
       rt4, rt5;
  wire [5:0] func, op;
  wire [15:0] \LoadUse次数 , multiplexer_18_out, \总周期数 , \插入气泡数 , \无条件分支数 , \条件分支成功数 ;
  wire [17:0] mem_wb_1_control_2;
  wire [18:0] ex_mem_1_control_2, id_ex_1_control_2, \硬布线控制器_1_jmp ;
  wire [25:6] if_id_1_instruction_2;
  wire [27:2] id_ex_1_instruction_2;
  wire [31:0] a3, a5, adder_1_out, adder_2_out, bit_extender_1_out, bit_extender_2_out, ex_mem_1_alu_2,
       ex_mem_1_instruction_2, ex_mem_1_r1_2, ex_mem_1_r2_2, EX_PC, id_ex_1_imm_2, id_ex_1_r2_2,
       id_ex_1_signimm_2, ID_PC, IF_PC, LedData, MEM_PC, mem_wb_1_instruction_2, mem_wb_1_md_2,
       mips_alu_1_result, mips_regifile_1_r1, mips_regifile_1_r2, multiplexer_1_out, multiplexer_7_out,
       multiplexer_8_out, multiplexer_9_out, multiplexer_15_out, multiplexer_16_out, multiplexer_17_out,
       ram_1_data, result5, rom_1_data, shifter_1_out, WB_PC;
  wire [31:26] id_ex_1_instruction_2_2;

  Button \u_总复位  (.out(RST));
  Button _1 (.out(IR1));
  Button _2 (.out(IR2));
  Button _3 (.out(IR3));
  Button \u_继续运行  (.out(Go));
  LED led_1 (.in(W1));
  LED led_2 (.in(W2));
  LED led_3 (.in(W3));
  Hex_Digit_Display hex_digit_display_1 (.value(LedData[31:28]));  // open: dp
  Multiplexer #(.select(3), .width(32), .enable("false")) multiplexer_1 (
    .in0(adder_1_out), .in1({32{1'b0}}),
    .in2({EX_PC[31:28], id_ex_1_instruction_2[27:23], rt3, rd3, id_ex_1_instruction_2[12:2], 2'b00}),
    .in3(a3), .in4(adder_2_out), .in5({32{1'b0}}), .in6({32{1'b0}}), .in7({32{1'b0}}),
    .out(multiplexer_1_out), .sel({or_4_out[2], id_ex_1_control_2[0], id_ex_1_control_2[1]}));
  and and_1 (and_1_out, stop, ~\数据相关 );  // AND_Gate
  Hex_Digit_Display hex_digit_display_2 (.value(LedData[23:20]));  // open: dp
  Hex_Digit_Display hex_digit_display_3 (.value(LedData[27:24]));  // open: dp
  Register #(.width(32)) PC (.D(multiplexer_1_out), .en(and_1_out), .Q(IF_PC), .clk(CLK), .clr(RST));
  Hex_Digit_Display hex_digit_display_4 (.value(LedData[19:16]));  // open: dp
  Hex_Digit_Display hex_digit_display_5 (.value(LedData[15:12]));  // open: dp
  Adder #(.width(32)) adder_1 (.a(IF_PC), .b(32'h4), .out(adder_1_out));  // open: cin, cout
  and and_2 (and_2_out, syscall5, equal5);
  Hex_Digit_Display hex_digit_display_6 (.value(LedData[11:8]));  // open: dp
  Hex_Digit_Display hex_digit_display_7 (.value(LedData[7:4]));  // open: dp
  Clock clock_1 (.out(CLK));
  ROM #(.addrWidth(10), .dataWidth(32)) rom_1 (.addr(IF_PC[11:2]), .data(rom_1_data));  // open: sel
  Register #(.width(32)) register_1 (.D(a5), .en(and_2_out), .Q(LedData), .clk(CLK), .clr(RST));
  Hex_Digit_Display hex_digit_display_8 (.value(LedData[3:0]));  // open: dp
  or or_1 (or_1_out, RST, or_3_out);
  IF_ID if_id_1 (
    .instruction(rom_1_data), .pc4(adder_1_out), .instruction_2({op, if_id_1_instruction_2, func}),
    .pc4_2(ID_PC), .rst(or_1_out), .clk(CLK), .stop(and_1_out));  // open: hit, hit_2, jump_att, jump_att_2, hit_pos, hit_pos_2, pc, pc_2
  and and_3 (and_3_out, syscall5, ~equal5);  // AND_Gate
  // Probe on \总周期数 
  // Probe on \无条件分支数 
  // Probe on \条件分支成功数 
  // Probe on \插入气泡数 
  // Probe on \LoadUse次数 
  Multiplexer #(.enable("false")) multiplexer_2 (.in0(1'b1), .in1(Go), .out(stop), .sel(and_3_out));
  // Probe on IF_PC[11:0]
  \硬布线控制器  \u_硬布线控制器_1  (
    .Func(func), .OP(op), .ALU_OP(\硬布线控制器_1_alu_op ), .MemToReg(\硬布线控制器_1_jmp [5]),
    .MemWrite(\硬布线控制器_1_jmp [6]), .ALU_SRC(\硬布线控制器_1_jmp [11]), .RegWrite(\硬布线控制器_1_jmp [12]),
    .SysCALL(\硬布线控制器_1_jmp [16]), .SignedExt(SignedExt), .RegDst(\硬布线控制器_1_jmp [14]), .JR(\硬布线控制器_1_jmp [1]),
    .JMP(\硬布线控制器_1_jmp [0]), .Beq(\硬布线控制器_1_jmp [3]), .JAL(\硬布线控制器_1_jmp [13]), .Bne(\硬布线控制器_1_jmp [4]),
    .SRAV(\硬布线控制器_1_jmp [15]), .LHU(\硬布线控制器_1_jmp [18]), .BGTZ(\硬布线控制器_1_jmp [17]));
  Multiplexer #(.width(5), .enable("false")) multiplexer_3 (
    .in0(if_id_1_instruction_2[25:21]), .in1(5'b00100), .out(ID_R1_num), .sel(\硬布线控制器_1_jmp [16]));
  Multiplexer #(.width(5), .enable("false")) multiplexer_4 (
    .in0(if_id_1_instruction_2[20:16]), .in1(5'b00010), .out(ID_R2_num), .sel(\硬布线控制器_1_jmp [16]));
  Counter #(.width(16), .max('hffff)) counter_1 (
    .count(stop), .Q(\总周期数 ), .clk(CLK), .clr(RST));  // open: load, D, carry
  // Probe on ID_PC[11:0]
  Multiplexer #(.width(5), .enable("false")) multiplexer_5 (
    .in0(rt5), .in1(rd5), .out(multiplexer_5_out), .sel(regdst5));
  Multiplexer #(.width(5), .enable("false")) multiplexer_6 (
    .in0(multiplexer_5_out), .in1({5{1'b1}}), .out(multiplexer_6_out), .sel(jal5));
  assign bit_extender_1_out = {{16{1'b0}}, {if_id_1_instruction_2[15:6], func}};  // Bit_Extender bit_extender_1
  assign bit_extender_2_out = {{16{if_id_1_instruction_2[15]}}, {if_id_1_instruction_2[15:6], func}};  // Bit_Extender bit_extender_2
  // Probe on EX_PC[11:0]
  // Probe on MEM_PC[11:0]
  not not_1 (not_1_out, CLK);
  Multiplexer #(.width(32), .enable("false")) multiplexer_7 (
    .in0(bit_extender_1_out), .in1(bit_extender_2_out), .out(multiplexer_7_out), .sel(SignedExt));
  // Probe on WB_PC[11:0]
  MIPS_Regifile mips_regifile_1 (
    .Din(multiplexer_15_out), .Clk(not_1_out), .R1(mips_regifile_1_r1), .R2(mips_regifile_1_r2),
    .WE(regwrite5), .W_num(multiplexer_6_out), .R1_num(ID_R1_num), .R2_num(ID_R2_num));
  or or_2 (or_2_out, RST, \数据相关 , or_3_out);
  ID_EX id_ex_1 (
    .control({\硬布线控制器_1_jmp [18:11], \硬布线控制器_1_alu_op , \硬布线控制器_1_jmp [6:3], SignedExt, \硬布线控制器_1_jmp [1:0]}),
    .instruction({op, if_id_1_instruction_2, func}), .pc4(ID_PC), .R1(mips_regifile_1_r1),
    .R2(mips_regifile_1_r2), .imm(multiplexer_7_out),
    .control_2({id_ex_1_control_2[18:17], syscall3, srav, regdst3, jal3, EX_RegWrite, id_ex_1_control_2[11:0]}),
    .instruction_2({id_ex_1_instruction_2_2, id_ex_1_instruction_2[27:23], rt3, rd3, id_ex_1_instruction_2[12:2]}),
    .pc4_2(EX_PC), .R1_2(a3), .R2_2(id_ex_1_r2_2), .imm_2(id_ex_1_imm_2), .rst(or_2_out), .stop(stop),
    .clk(CLK), .shamt(if_id_1_instruction_2[10:6]), .shamt_2(id_ex_1_shamt_2), .signimm(bit_extender_2_out),
    .signimm_2(id_ex_1_signimm_2));  // open: hit, hit_2, jump_att, jump_att_2, hit_pos, hit_pos_2, pc, pc_2
  or or_3 (or_3_out, id_ex_1_control_2[0], or_4_out[2]);
  Multiplexer #(.width(32), .enable("false")) multiplexer_8 (
    .in0(id_ex_1_r2_2), .in1(id_ex_1_imm_2), .out(multiplexer_8_out), .sel(id_ex_1_control_2[11]));
  \数据相关检测  \u_数据相关检测_1  (
    .OP(op), .EX_WriteReg_num(EX_WriteReg_num), .EX_RegWrite(EX_RegWrite),
    .MEM_WriteReg_num(MEM_WriteReg_num), .MEM_RegWrite(MEM_RegWrite), .\数据相关 (\数据相关 ), .Func(func),
    .ID_R1_num(ID_R1_num), .ID_R2_num(ID_R2_num));
  Multiplexer #(.width(32), .enable("false")) multiplexer_9 (
    .in0(a3), .in1(32'h22), .out(multiplexer_9_out), .sel(syscall3));
  Multiplexer #(.width(5), .enable("false")) multiplexer_10 (
    .in0(id_ex_1_shamt_2), .in1(a3[4:0]), .out(multiplexer_10_out), .sel(srav));
  Shifter #(.width(32)) shifter_1 (.in(id_ex_1_signimm_2), .\dist (5'b00010), .out(shifter_1_out));
  and and_4 (and_4_out, id_ex_1_control_2[3], mips_alu_1_equal);
  and and_5 (and_5_out, id_ex_1_control_2[4], ~mips_alu_1_equal);  // AND_Gate
  and and_6 (and_6_out, id_ex_1_control_2[17], ~mips_alu_1_equal, ~mips_alu_1_result[0]);  // AND_Gate
  MIPS_ALU mips_alu_1 (
    .X(multiplexer_9_out), .Y(multiplexer_8_out), .AluOP(id_ex_1_control_2[10:7]), .Equal(mips_alu_1_equal),
    .Result(mips_alu_1_result), .shamt(multiplexer_10_out));  // open: Result_2
  Adder #(.width(32)) adder_2 (.a(EX_PC), .b(shifter_1_out), .out(adder_2_out));  // open: cin, cout
  or or_4 (or_4_out[2], and_4_out, and_5_out, and_6_out);
  Multiplexer #(.width(5), .enable("false")) multiplexer_11 (
    .in0(rt3), .in1(rd3), .out(multiplexer_11_out), .sel(regdst3));
  Multiplexer #(.width(5), .enable("false")) multiplexer_12 (
    .in0(multiplexer_11_out), .in1({5{1'b1}}), .out(EX_WriteReg_num), .sel(jal3));
  Counter #(.width(16), .max('hffff)) counter_2 (
    .count(\数据相关 ), .Q(\插入气泡数 ), .clk(CLK), .clr(RST));  // open: load, D, carry
  Counter #(.width(16), .max('hffff)) counter_3 (
    .count(id_ex_1_control_2[0]), .Q(\无条件分支数 ), .clk(CLK), .clr(RST));  // open: load, D, carry
  Counter #(.width(16), .max('hffff)) counter_4 (
    .count(or_4_out[2]), .Q(\条件分支成功数 ), .clk(CLK), .clr(RST));  // open: load, D, carry
  EX_MEM ex_mem_1 (
    .control({id_ex_1_control_2[18:17], syscall3, srav, regdst3, jal3, EX_RegWrite, id_ex_1_control_2[11:0]}),
    .instruction({id_ex_1_instruction_2_2, id_ex_1_instruction_2[27:23], rt3, rd3, id_ex_1_instruction_2[12:2]}),
    .pc4(EX_PC), .R2(id_ex_1_r2_2), .alu(mips_alu_1_result),
    .control_2({ex_mem_1_control_2[18:15], regdst4, jal4, MEM_RegWrite, ex_mem_1_control_2[11:0]}),
    .instruction_2({ex_mem_1_instruction_2[31:21], rt4, rd4, ex_mem_1_instruction_2[10:0]}), .pc4_2(MEM_PC),
    .R2_2(ex_mem_1_r2_2), .alu_2(ex_mem_1_alu_2), .rst(RST), .stop(stop), .clk(CLK),
    .equal(mips_alu_1_equal), .equal_2(ex_mem_1_equal_2), .R1(a3), .R1_2(ex_mem_1_r1_2));
  not not_2 (not_2_out, ex_mem_1_control_2[6]);
  RAM #(.addrWidth(10), .dataWidth(32), .bus("separate")) ram_1 (
    .addr(ex_mem_1_alu_2[11:2]), .din(ex_mem_1_r2_2), .data(ram_1_data), .str(ex_mem_1_control_2[6]),
    .clk(CLK), .ld(not_2_out), .clr(RST));  // open: sel
  Multiplexer #(.width(5), .enable("false")) multiplexer_13 (
    .in0(rt4), .in1(rd4), .out(multiplexer_13_out), .sel(regdst4));
  Multiplexer #(.width(5), .enable("false")) multiplexer_14 (
    .in0(multiplexer_13_out), .in1({5{1'b1}}), .out(MEM_WriteReg_num), .sel(jal4));
  MEM_WB mem_wb_1 (
    .control({ex_mem_1_control_2[18:15], regdst4, jal4, MEM_RegWrite, ex_mem_1_control_2[11:0]}),
    .instruction({ex_mem_1_instruction_2[31:21], rt4, rd4, ex_mem_1_instruction_2[10:0]}), .pc4(MEM_PC),
    .md(ram_1_data), .alu(ex_mem_1_alu_2),
    .control_2({lhu, mem_wb_1_control_2[17], syscall5, mem_wb_1_control_2[15], regdst5, jal5, regwrite5, mem_wb_1_control_2[11:0]}),
    .instruction_2({mem_wb_1_instruction_2[31:21], rt5, rd5, mem_wb_1_instruction_2[10:0]}), .pc4_2(WB_PC),
    .md_2(mem_wb_1_md_2), .alu_2(result5), .rst(RST), .stop(stop), .clk(CLK), .equal(ex_mem_1_equal_2),
    .equal_2(equal5), .R1(ex_mem_1_r1_2), .R1_2(a5));
  Multiplexer #(.width(32), .enable("false")) multiplexer_15 (
    .in0(multiplexer_17_out), .in1(WB_PC), .out(multiplexer_15_out), .sel(jal5));
  Multiplexer #(.width(32), .enable("false")) multiplexer_16 (
    .in0(result5), .in1(mem_wb_1_md_2), .out(multiplexer_16_out), .sel(mem_wb_1_control_2[5]));
  Multiplexer #(.width(32), .enable("false")) multiplexer_17 (
    .in0(multiplexer_16_out), .in1({{16{1'b0}}, multiplexer_18_out}), .out(multiplexer_17_out), .sel(lhu));
  Multiplexer #(.width(16), .enable("false")) multiplexer_18 (
    .in0(multiplexer_16_out[15:0]), .in1(multiplexer_16_out[31:16]), .out(multiplexer_18_out),
    .sel(result5[1]));

  // Notes on the sheet:
  //   中断源
  //   中断等待指示
  //   数码管输出
  //   指令存储器
  //   contents of rom_1 (hex, n*v repeats v):
  //   20110004 ae310000 8e320000 2252fffc 20100000 22110001 2118020 22520004 ae500000 22310001 2118020
  //   22520004 ae500000 22310001 2118020 22520004 ae500000 22310001 2118020 22520004 ae500000 22310001
  //   2118020 22520004 ae500000 22310001 2118020 22520004 ae500000 22310001 2118020 22520004 ae500000
  //   2002000a 20100000 20100000 20100000 c
  //   指令字
  //   OP
  //   Func
  //   rs
  //   rt
  //   rd
  //   shamt
  //   imm
  //   JMP
  //   JR
  //   OP
  //   Func
  //   Beq
  //   Bne
  //   AluOP
  //   AluSrcB
  //   RegWrite
  //   JAL
  //   RegDst
  //   MemToReg
  //   MemWrite
  //   流水调试日志用
  //   rt
  //   rd
  //   rt
  //   rd
  //   rt
  //   rd
endmodule

module \重定向流水线  (
);

  wire and_1_out, and_2_out, and_3_out, and_4_out, and_5_out, and_6_out, CLK, comparator_1_eq,
       comparator_2_eq, equal5, EX_LW, ex_mem_1_equal_2, Go, IR1, IR2, IR3, jal3, jal4, jal5, lhu,
       MEM_RegWrite, mips_alu_1_equal, not_1_out, not_2_out, or_1_out, or_2_out, or_4_out, regdst3, regdst4,
       regdst5, regwrite5, RST, SignedExt, srav, stall, stop, syscall3, syscall5, W1, W2, W3;
  wire [1:0] R1_sel, R2_sel;
  wire [2:2] or_5_out;
  wire [3:0] \硬布线控制器_1_alu_op ;
  wire [4:0] EX_R1_num, EX_R2_num, EX_WriteReg_num, id_ex_1_shamt_2, ID_R1_num, ID_R2_num, MEM_WriteReg_num,
       multiplexer_5_out, multiplexer_12_out, multiplexer_15_out, multiplexer_16_out, rd4, rd5, rt4, rt5,
       WB_WriteReg_num;
  wire [5:0] func2, func3, op2;
  wire [15:0] \LoadUse次数 , multiplexer_22_out, \总周期数 , \插入气泡数 , \无条件分支数 , \条件分支成功数 ;
  wire [17:0] mem_wb_1_control_2;
  wire [18:0] ex_mem_1_control_2, id_ex_1_control_2, \硬布线控制器_1_jmp ;
  wire [25:6] if_id_1_instruction_2;
  wire [31:0] a3, a5, adder_1_out, adder_2_out, alu4, bit_extender_1_out, bit_extender_2_out,
       ex_mem_1_instruction_2, ex_mem_1_r1_2, ex_mem_1_r2_2, EX_PC, id_ex_1_imm_2, id_ex_1_r1_2,
       id_ex_1_r2_2, id_ex_1_signimm_2, ID_PC, IF_PC, LedData, MEM_PC, mem_wb_1_instruction_2, mem_wb_1_md_2,
       mips_alu_1_result, mips_regifile_1_r1, mips_regifile_1_r2, multiplexer_1_out, multiplexer_7_out,
       multiplexer_9_out, multiplexer_10_out, multiplexer_11_out, multiplexer_19_out, multiplexer_20_out,
       multiplexer_21_out, ram_1_data, result5, rom_1_data, shifter_1_out, WB_PC;
  wire [31:6] instruction3;

  Button \u_总复位  (.out(RST));
  Button _1 (.out(IR1));
  Button _2 (.out(IR2));
  Button _3 (.out(IR3));
  Button \u_继续运行  (.out(Go));
  LED led_1 (.in(W1));
  LED led_2 (.in(W2));
  LED led_3 (.in(W3));
  Hex_Digit_Display hex_digit_display_1 (.value(LedData[31:28]));  // open: dp
  Multiplexer #(.select(3), .width(32), .enable("false")) multiplexer_1 (
    .in0(adder_1_out), .in1({32{1'b0}}), .in2({EX_PC[31:28], instruction3[25:6], func3, 2'b00}), .in3(a3),
    .in4(adder_2_out), .in5({32{1'b0}}), .in6({32{1'b0}}), .in7({32{1'b0}}), .out(multiplexer_1_out),
    .sel({or_5_out[2], id_ex_1_control_2[0], id_ex_1_control_2[1]}));
  and and_1 (and_1_out, stop, ~stall);  // AND_Gate
  Hex_Digit_Display hex_digit_display_2 (.value(LedData[27:24]));  // open: dp
  Hex_Digit_Display hex_digit_display_3 (.value(LedData[23:20]));  // open: dp
  Register #(.width(32)) PC (.D(multiplexer_1_out), .en(and_1_out), .Q(IF_PC), .clk(CLK), .clr(RST));
  Hex_Digit_Display hex_digit_display_4 (.value(LedData[15:12]));  // open: dp
  Hex_Digit_Display hex_digit_display_5 (.value(LedData[19:16]));  // open: dp
  Adder #(.width(32)) adder_1 (.a(IF_PC), .b(32'h4), .out(adder_1_out));  // open: cin, cout
  and and_2 (and_2_out, syscall5, equal5);
  Hex_Digit_Display hex_digit_display_6 (.value(LedData[11:8]));  // open: dp
  Hex_Digit_Display hex_digit_display_7 (.value(LedData[7:4]));  // open: dp
  Clock clock_1 (.out(CLK));
  ROM #(.addrWidth(10), .dataWidth(32)) rom_1 (.addr(IF_PC[11:2]), .data(rom_1_data));  // open: sel
  Register #(.width(32)) register_1 (.D(a5), .en(and_2_out), .Q(LedData), .clk(CLK), .clr(RST));
  Hex_Digit_Display hex_digit_display_8 (.value(LedData[3:0]));  // open: dp
  or or_1 (or_1_out, RST, or_4_out);
  IF_ID if_id_1 (
    .instruction(rom_1_data), .pc4(adder_1_out), .instruction_2({op2, if_id_1_instruction_2, func2}),
    .pc4_2(ID_PC), .rst(or_1_out), .clk(CLK), .stop(and_1_out));  // open: hit, hit_2, jump_att, jump_att_2, hit_pos, hit_pos_2, pc, pc_2
  load_use load_use_1 (
    .ID_OP(op2), .EX_WriteReg_num(EX_WriteReg_num), .EX_LW(EX_LW), .ID_R1_num(ID_R1_num), .STALL(stall),
    .ID_Func(func2), .ID_R2_num(ID_R2_num));
  // Probe on \总周期数 
  // Probe on \无条件分支数 
  // Probe on \条件分支成功数 
  // Probe on \插入气泡数 
  // Probe on \LoadUse次数 
  Multiplexer #(.enable("false")) multiplexer_2 (.in0(1'b1), .in1(Go), .out(stop), .sel(and_3_out));
  and and_3 (and_3_out, syscall5, ~equal5);  // AND_Gate
  // Probe on IF_PC[11:0]
  \硬布线控制器  \u_硬布线控制器_1  (
    .Func(func2), .OP(op2), .ALU_OP(\硬布线控制器_1_alu_op ), .MemToReg(\硬布线控制器_1_jmp [5]),
    .MemWrite(\硬布线控制器_1_jmp [6]), .ALU_SRC(\硬布线控制器_1_jmp [11]), .RegWrite(\硬布线控制器_1_jmp [12]),
    .SysCALL(\硬布线控制器_1_jmp [16]), .SignedExt(SignedExt), .RegDst(\硬布线控制器_1_jmp [14]), .JR(\硬布线控制器_1_jmp [1]),
    .JMP(\硬布线控制器_1_jmp [0]), .Beq(\硬布线控制器_1_jmp [3]), .JAL(\硬布线控制器_1_jmp [13]), .Bne(\硬布线控制器_1_jmp [4]),
    .SRAV(\硬布线控制器_1_jmp [15]), .LHU(\硬布线控制器_1_jmp [18]), .BGTZ(\硬布线控制器_1_jmp [17]));
  Multiplexer #(.width(5), .enable("false")) multiplexer_3 (
    .in0(if_id_1_instruction_2[25:21]), .in1(5'b00100), .out(ID_R1_num), .sel(\硬布线控制器_1_jmp [16]));
  Multiplexer #(.width(5), .enable("false")) multiplexer_4 (
    .in0(if_id_1_instruction_2[20:16]), .in1(5'b00010), .out(ID_R2_num), .sel(\硬布线控制器_1_jmp [16]));
  Counter #(.width(16), .max('hffff)) counter_1 (
    .count(stop), .Q(\总周期数 ), .clk(CLK), .clr(RST));  // open: load, D, carry
  // Probe on ID_PC[11:0]
  Multiplexer #(.width(5), .enable("false")) multiplexer_5 (
    .in0(rt5), .in1(rd5), .out(multiplexer_5_out), .sel(regdst5));
  Multiplexer #(.width(5), .enable("false")) multiplexer_6 (
    .in0(multiplexer_5_out), .in1({5{1'b1}}), .out(WB_WriteReg_num), .sel(jal5));
  assign bit_extender_1_out = {{16{1'b0}}, {if_id_1_instruction_2[15:6], func2}};  // Bit_Extender bit_extender_1
  assign bit_extender_2_out = {{16{if_id_1_instruction_2[15]}}, {if_id_1_instruction_2[15:6], func2}};  // Bit_Extender bit_extender_2
  // Probe on MEM_PC[11:0]
  // Probe on EX_PC[11:0]
  not not_1 (not_1_out, CLK);
  Multiplexer #(.width(32), .enable("false")) multiplexer_7 (
    .in0(bit_extender_1_out), .in1(bit_extender_2_out), .out(multiplexer_7_out), .sel(SignedExt));
  // Probe on WB_PC[11:0]
  MIPS_Regifile mips_regifile_1 (
    .Din(multiplexer_19_out), .Clk(not_1_out), .R1(mips_regifile_1_r1), .R2(mips_regifile_1_r2),
    .WE(regwrite5), .W_num(WB_WriteReg_num), .R1_num(ID_R1_num), .R2_num(ID_R2_num));
  or or_2 (or_2_out, RST, stall, or_4_out);
  ID_EX id_ex_1 (
    .control({\硬布线控制器_1_jmp [18:11], \硬布线控制器_1_alu_op , \硬布线控制器_1_jmp [6:3], SignedExt, \硬布线控制器_1_jmp [1:0]}),
    .instruction({op2, if_id_1_instruction_2, func2}), .pc4(ID_PC), .R1(mips_regifile_1_r1),
    .R2(mips_regifile_1_r2), .imm(multiplexer_7_out),
    .control_2({id_ex_1_control_2[18:17], syscall3, srav, regdst3, jal3, id_ex_1_control_2[12:0]}),
    .instruction_2({instruction3, func3}), .pc4_2(EX_PC), .R1_2(id_ex_1_r1_2), .R2_2(id_ex_1_r2_2),
    .imm_2(id_ex_1_imm_2), .rst(or_2_out), .stop(stop), .clk(CLK), .shamt(if_id_1_instruction_2[10:6]),
    .shamt_2(id_ex_1_shamt_2), .signimm(bit_extender_2_out), .signimm_2(id_ex_1_signimm_2));  // open: hit, hit_2, jump_att, jump_att_2, hit_pos, hit_pos_2, pc, pc_2
  \重定向判断  \u_重定向判断_1  (
    .EX_OP(instruction3[31:26]), .WB_WriteReg_num(WB_WriteReg_num), .WB_RegWrite(regwrite5), .R1_sel(R1_sel),
    .MEM_WriteReg_num(MEM_WriteReg_num), .MEM_RegWrite(MEM_RegWrite), .R2_sel(R2_sel), .EX_Func(func3),
    .EX_R1_num(EX_R1_num), .EX_R2_num(EX_R2_num));
  Comparator #(.width(6)) comparator_1 (.a(instruction3[31:26]), .b(6'b100011), .eq(comparator_1_eq));  // open: gt, lt
  Comparator #(.width(6)) comparator_2 (.a(instruction3[31:26]), .b(6'b100101), .eq(comparator_2_eq));  // open: gt, lt
  Counter #(.width(16), .max('hffff)) counter_2 (
    .count(stall), .Q(\LoadUse次数 ), .clk(CLK), .clr(RST));  // open: load, D, carry
  Counter #(.width(16), .max('hffff)) counter_3 (
    .count(stall), .Q(\插入气泡数 ), .clk(CLK), .clr(RST));  // open: load, D, carry
  Multiplexer #(.select(2), .width(32), .enable("false")) multiplexer_8 (
    .in0(id_ex_1_r1_2), .in1(multiplexer_19_out), .in2(alu4), .in3(alu4), .out(a3), .sel(R1_sel));
  Multiplexer #(.select(2), .width(32), .enable("false")) multiplexer_9 (
    .in0(id_ex_1_r2_2), .in1(multiplexer_19_out), .in2(alu4), .in3(alu4), .out(multiplexer_9_out),
    .sel(R2_sel));
  or or_3 (EX_LW, comparator_1_eq, comparator_2_eq);
  or or_4 (or_4_out, id_ex_1_control_2[0], or_5_out[2]);
  Multiplexer #(.width(32), .enable("false")) multiplexer_10 (
    .in0(multiplexer_9_out), .in1(id_ex_1_imm_2), .out(multiplexer_10_out), .sel(id_ex_1_control_2[11]));
  Shifter #(.width(32)) shifter_1 (.in(id_ex_1_signimm_2), .\dist (5'b00010), .out(shifter_1_out));
  Multiplexer #(.width(32), .enable("false")) multiplexer_11 (
    .in0(a3), .in1(32'h22), .out(multiplexer_11_out), .sel(syscall3));
  Multiplexer #(.width(5), .enable("false")) multiplexer_12 (
    .in0(id_ex_1_shamt_2), .in1(a3[4:0]), .out(multiplexer_12_out), .sel(srav));
  and and_4 (and_4_out, id_ex_1_control_2[3], mips_alu_1_equal);
  and and_5 (and_5_out, id_ex_1_control_2[4], ~mips_alu_1_equal);  // AND_Gate
  and and_6 (and_6_out, id_ex_1_control_2[17], ~mips_alu_1_equal, ~mips_alu_1_result[0]);  // AND_Gate
  MIPS_ALU mips_alu_1 (
    .X(multiplexer_11_out), .Y(multiplexer_10_out), .AluOP(id_ex_1_control_2[10:7]),
    .Equal(mips_alu_1_equal), .Result(mips_alu_1_result), .shamt(multiplexer_12_out));  // open: Result_2
  Adder #(.width(32)) adder_2 (.a(EX_PC), .b(shifter_1_out), .out(adder_2_out));  // open: cin, cout
  Multiplexer #(.width(5), .enable("false")) multiplexer_13 (
    .in0(instruction3[25:21]), .in1(5'b00100), .out(EX_R1_num), .sel(syscall3));
  Multiplexer #(.width(5), .enable("false")) multiplexer_14 (
    .in0(instruction3[20:16]), .in1(5'b00010), .out(EX_R2_num), .sel(syscall3));
  or or_5 (or_5_out[2], and_4_out, and_5_out, and_6_out);
  Counter #(.width(16), .max('hffff)) counter_4 (
    .count(id_ex_1_control_2[0]), .Q(\无条件分支数 ), .clk(CLK), .clr(RST));  // open: load, D, carry
  Counter #(.width(16), .max('hffff)) counter_5 (
    .count(or_5_out[2]), .Q(\条件分支成功数 ), .clk(CLK), .clr(RST));  // open: load, D, carry
  EX_MEM ex_mem_1 (
    .control({id_ex_1_control_2[18:17], syscall3, srav, regdst3, jal3, id_ex_1_control_2[12:0]}),
    .instruction({instruction3, func3}), .pc4(EX_PC), .R2(multiplexer_9_out), .alu(mips_alu_1_result),
    .control_2({ex_mem_1_control_2[18:15], regdst4, jal4, MEM_RegWrite, ex_mem_1_control_2[11:0]}),
    .instruction_2({ex_mem_1_instruction_2[31:21], rt4, rd4, ex_mem_1_instruction_2[10:0]}), .pc4_2(MEM_PC),
    .R2_2(ex_mem_1_r2_2), .alu_2(alu4), .rst(RST), .stop(stop), .clk(CLK), .equal(mips_alu_1_equal),
    .equal_2(ex_mem_1_equal_2), .R1(a3), .R1_2(ex_mem_1_r1_2));
  Multiplexer #(.width(5), .enable("false")) multiplexer_15 (
    .in0(rt4), .in1(rd4), .out(multiplexer_15_out), .sel(regdst4));
  Multiplexer #(.width(5), .enable("false")) multiplexer_16 (
    .in0(instruction3[20:16]), .in1(instruction3[15:11]), .out(multiplexer_16_out), .sel(regdst3));
  Multiplexer #(.width(5), .enable("false")) multiplexer_17 (
    .in0(multiplexer_15_out), .in1({5{1'b1}}), .out(MEM_WriteReg_num), .sel(jal4));
  Multiplexer #(.width(5), .enable("false")) multiplexer_18 (
    .in0(multiplexer_16_out), .in1({5{1'b1}}), .out(EX_WriteReg_num), .sel(jal3));
  RAM #(.addrWidth(10), .dataWidth(32), .bus("separate")) ram_1 (
    .addr(alu4[11:2]), .din(ex_mem_1_r2_2), .data(ram_1_data), .str(ex_mem_1_control_2[6]), .clk(CLK),
    .ld(not_2_out), .clr(RST));  // open: sel
  not not_2 (not_2_out, ex_mem_1_control_2[6]);
  MEM_WB mem_wb_1 (
    .control({ex_mem_1_control_2[18:15], regdst4, jal4, MEM_RegWrite, ex_mem_1_control_2[11:0]}),
    .instruction({ex_mem_1_instruction_2[31:21], rt4, rd4, ex_mem_1_instruction_2[10:0]}), .pc4(MEM_PC),
    .md(ram_1_data), .alu(alu4),
    .control_2({lhu, mem_wb_1_control_2[17], syscall5, mem_wb_1_control_2[15], regdst5, jal5, regwrite5, mem_wb_1_control_2[11:0]}),
    .instruction_2({mem_wb_1_instruction_2[31:21], rt5, rd5, mem_wb_1_instruction_2[10:0]}), .pc4_2(WB_PC),
    .md_2(mem_wb_1_md_2), .alu_2(result5), .rst(RST), .stop(stop), .clk(CLK), .equal(ex_mem_1_equal_2),
    .equal_2(equal5), .R1(ex_mem_1_r1_2), .R1_2(a5));
  Multiplexer #(.width(32), .enable("false")) multiplexer_19 (
    .in0(multiplexer_21_out), .in1(WB_PC), .out(multiplexer_19_out), .sel(jal5));
  Multiplexer #(.width(32), .enable("false")) multiplexer_20 (
    .in0(result5), .in1(mem_wb_1_md_2), .out(multiplexer_20_out), .sel(mem_wb_1_control_2[5]));
  Multiplexer #(.width(32), .enable("false")) multiplexer_21 (
    .in0(multiplexer_20_out), .in1({{16{1'b0}}, multiplexer_22_out}), .out(multiplexer_21_out), .sel(lhu));
  Multiplexer #(.width(16), .enable("false")) multiplexer_22 (
    .in0(multiplexer_20_out[15:0]), .in1(multiplexer_20_out[31:16]), .out(multiplexer_22_out),
    .sel(result5[1]));

  // Other names for the same wires on the sheet: instruction3[5:0] = func3; rd3[4:0] = instruction3[15:11];
  //   rt3[4:0] = instruction3[20:16]; rs3[4:0] = instruction3[25:21]; op3[5:0] = instruction3[31:26]

  // Notes on the sheet:
  //   中断源
  //   中断等待指示
  //   数码管输出
  //   指令存储器
  //   contents of rom_1 (hex, n*v repeats v):
  //   20110001 8100005 20110001 20120002 20130003 8100009 20110001 20120002 20130003 810000d 20110001
  //   20120002 20130003 8100011 20110001 20120002 20130003 c1000f9 20100001 20110001 118fc0 112020
  //   20020022 c 118882 12200001 8100015 112020 20020022 c 20110001 118880 112020 20020022 c 12200001
  //   810001f 20110001 118fc0 112020 20020022 c 1188c3 112020 20020022 c 118903 112020 20020022 c 118903
  //   112020 20020022 c 118903 112020 20020022 c 118903 112020 20020022 c 118903 112020 20020022 c 118903
  //   112020 20020022 c 118903 112020 20020022 c 20100001 109fc0 139fc3 8021 2012000c 24160003 26100001
  //   3210000f 20080008 20090001 139900 2709825 132020 20020022 c 1094022 1500fff9 22100001 2018000f
  //   2188024 108700 20080008 20090001 139902 2709825 132021 20020022 c 1094022 1500fff9 108702 2c9b022
  //   12c00001 8100050 4020 1084027 84400 3508ffff 82021 20020022 c 2010ffff 20110000 ae300000 22100001
  //   22310004 ae300000 22100001 22310004 ae300000 22100001 22310004 ae300000 22100001 22310004 ae300000
  //   22100001 22310004 ae300000 22100001 22310004 ae300000 22100001 22310004 ae300000 22100001 22310004
  //   ae300000 22100001 22310004 ae300000 22100001 22310004 ae300000 22100001 22310004 ae300000 22100001
  //   22310004 ae300000 22100001 22310004 ae300000 22100001 22310004 ae300000 22100001 22310004 ae300000
  //   22100001 22310004 22100001 8020 2011003c 8e130000 8e340000 274402a 11000002 ae330000 ae140000
  //   2231fffc 1611fff8 102020 20020022 c 22100004 2011003c 1611fff2 20020032 c 20080001 20090003 20110876
  //   118d00 112020 20020022 c 200b0008 1118807 1318807 112020 20020022 c 216bffff 1560fff9 2002000a c
  //   20080001 20110010 112020 20020022 c 200b0020 2288823 112020 20020022 c 216bffff 1560fffa 2002000a c
  //   20090000 200b0010 34118483 20120404 118c00 129400 36318281 22520404 ad310000 2328820 21290004
  //   216bffff 1560fffb 200b0020 20090000 95310000 112020 20020022 c 21290002 216bffff 1560fff9 2002000a c
  //   2011000f 112020 20020022 c 2231ffff 1e20fffb 2002000a c 2002000a c 20100000 22100001 102020 20020022
  //   c 22100002 102020 20020022 c 22100003 102020 20020022 c 22100004 102020 20020022 c 22100005 102020
  //   20020022 c 22100006 102020 20020022 c 22100007 102020 20020022 c 22100008 102020 20020022 20020022 c
  //   3e00008
  //   指令字
  //   OP
  //   Func
  //   rs
  //   rt
  //   rd
  //   shamt
  //   imm
  //   JMP
  //   JR
  //   OP
  //   Func
  //   Beq
  //   Bne
  //   AluOP
  //   AluSrcB
  //   RegWrite
  //   JAL
  //   RegDst
  //   MemToReg
  //   MemWrite
  //   流水调试日志用
  //   lw
  //   lhu
  //   OP
  //   Func
  //   rs
  //   rt
  //   rd
  //   rt
  //   rd
  //   rt
  //   rd
endmodule

module \动态分组预测  (
);

  wire and_1_out, and_2_out, and_3_out, and_4_out, and_5_out, and_7_out, and_8_out, and_9_out, and_10_out,
       att_fail, att_suc, branch, CLK, comparator_1_eq, comparator_2_eq, comparator_3_eq, equal5, EX_LW,
       ex_mem_1_equal_2, Go, hit, hit2, hit3, IR1, IR2, IR3, jal3, jal4, jal5, jb_3, jmp3, jr3, jump_att,
       jump_att2, jump_att3, jump_suc, lhu, MEM_RegWrite, mips_alu_1_equal, not_1_out, not_2_out, or_1_out,
       or_3_out, regdst3, regdst4, regdst5, regwrite5, RST, SignedExt, srav, stall, stop, syscall3, syscall5,
       W1, W2, W3;
  wire [1:0] R1_sel, R2_sel;
  wire [2:0] hit_pos, hit_pos2, hit_pos3;
  wire [3:0] \硬布线控制器_1_alu_op ;
  wire [4:0] EX_R1_num, EX_R2_num, EX_WriteReg_num, id_ex_1_shamt_2, ID_R1_num, ID_R2_num, MEM_WriteReg_num,
       multiplexer_7_out, multiplexer_15_out, multiplexer_19_out, multiplexer_20_out, rd4, rd5, rt4, rt5,
       WB_WriteReg_num;
  wire [5:0] func2, func3, op2;
  wire [15:0] \LoadUse次数 , multiplexer_26_out, \总周期数 , \插入气泡数 , \无条件分支数 , \条件分支成功数 , \预测失败数 , \预测成功数 ;
  wire [17:0] mem_wb_1_control_2;
  wire [18:0] ex_mem_1_control_2, \硬布线控制器_1_jmp ;
  wire [18:2] id_ex_1_control_2;
  wire [25:6] if_id_1_instruction_2;
  wire [31:0] a3, a5, adder_1_out, adder_2_out, alu4, bit_extender_1_out, bit_extender_2_out, dest_addr,
       ex_mem_1_instruction_2, ex_mem_1_r1_2, ex_mem_1_r2_2, EX_PC, id_ex_1_imm_2, id_ex_1_pc4_2,
       id_ex_1_r1_2, id_ex_1_r2_2, id_ex_1_signimm_2, ID_PC, if_id_1_pc4_2, IF_PC, LedData, MEM_PC,
       mem_wb_1_instruction_2, mem_wb_1_md_2, mips_alu_1_result, mips_regifile_1_r1, mips_regifile_1_r2,
       multiplexer_1_out, multiplexer_2_out, multiplexer_3_out, multiplexer_9_out, multiplexer_11_out,
       multiplexer_12_out, multiplexer_13_out, multiplexer_14_out, multiplexer_23_out, multiplexer_24_out,
       multiplexer_25_out, pc_att, ram_1_data, result5, rom_1_data, shifter_1_out, WB_PC;
  wire [31:6] instruction3;

  Button \u_总复位  (.out(RST));
  Button _1 (.out(IR1));
  Button _2 (.out(IR2));
  Button _3 (.out(IR3));
  Button \u_继续运行  (.out(Go));
  LED led_1 (.in(W1));
  LED led_2 (.in(W2));
  LED led_3 (.in(W3));
  Multiplexer #(.width(32), .enable("false")) multiplexer_1 (
    .in0(multiplexer_2_out), .in1(a3), .out(multiplexer_1_out), .sel(jr3));
  Hex_Digit_Display hex_digit_display_1 (.value(LedData[31:28]));  // open: dp
  and and_1 (and_1_out, stop, ~stall);  // AND_Gate
  Multiplexer #(.width(32), .enable("false")) multiplexer_2 (
    .in0(multiplexer_3_out), .in1(multiplexer_12_out), .out(multiplexer_2_out), .sel(att_fail));
  Hex_Digit_Display hex_digit_display_2 (.value(LedData[23:20]));  // open: dp
  Hex_Digit_Display hex_digit_display_3 (.value(LedData[27:24]));  // open: dp
  Register #(.width(32)) PC (.D(multiplexer_1_out), .en(and_1_out), .Q(IF_PC), .clk(CLK), .clr(RST));
  and and_2 (and_2_out, hit, jump_att);
  Multiplexer #(.width(32), .enable("false")) multiplexer_3 (
    .in0(adder_1_out), .in1(pc_att), .out(multiplexer_3_out), .sel(and_2_out));
  BHT bht_1 (
    .clk(CLK), .jump_suc_3(jump_suc), .jump_att(jump_att), .pc(IF_PC), .pc_3(EX_PC), .hit_3(hit3), .hit(hit),
    .pc_att(pc_att), .rst(RST), .jb_3(jb_3), .hit_pos(hit_pos), .hit_pos_3(hit_pos3), .dest_addr(dest_addr));
  Hex_Digit_Display hex_digit_display_4 (.value(LedData[15:12]));  // open: dp
  Hex_Digit_Display hex_digit_display_5 (.value(LedData[19:16]));  // open: dp
  Adder #(.width(32)) adder_1 (.a(IF_PC), .b(32'h4), .out(adder_1_out));  // open: cin, cout
  Hex_Digit_Display hex_digit_display_6 (.value(LedData[7:4]));  // open: dp
  Hex_Digit_Display hex_digit_display_7 (.value(LedData[11:8]));  // open: dp
  Clock clock_1 (.out(CLK));
  ROM #(.addrWidth(10), .dataWidth(32)) rom_1 (.addr(IF_PC[11:2]), .data(rom_1_data));  // open: sel
  and and_3 (and_3_out, syscall5, equal5);
  Hex_Digit_Display hex_digit_display_8 (.value(LedData[3:0]));  // open: dp
  or or_1 (or_1_out, RST, att_fail);
  IF_ID if_id_1 (
    .instruction(rom_1_data), .pc4(adder_1_out), .instruction_2({op2, if_id_1_instruction_2, func2}),
    .pc4_2(if_id_1_pc4_2), .rst(or_1_out), .clk(CLK), .stop(and_1_out), .hit(hit), .hit_2(hit2),
    .jump_att(jump_att), .jump_att_2(jump_att2), .hit_pos(hit_pos), .hit_pos_2(hit_pos2), .pc(IF_PC),
    .pc_2(ID_PC));
  Register #(.width(32)) register_1 (.D(a5), .en(and_3_out), .Q(LedData), .clk(CLK), .clr(RST));
  load_use load_use_1 (
    .ID_OP(op2), .EX_WriteReg_num(EX_WriteReg_num), .EX_LW(EX_LW), .ID_R1_num(ID_R1_num), .STALL(stall),
    .ID_Func(func2), .ID_R2_num(ID_R2_num));
  // Probe on \总周期数 
  // Probe on \无条件分支数 
  // Probe on \条件分支成功数 
  // Probe on \插入气泡数 
  // Probe on \LoadUse次数 
  // Probe on \预测失败数 
  Multiplexer #(.enable("false")) multiplexer_4 (.in0(1'b1), .in1(Go), .out(stop), .sel(and_4_out));
  and and_4 (and_4_out, syscall5, ~equal5);  // AND_Gate
  Comparator #(.width(1)) comparator_1 (.a(jump_att3), .b(jump_suc), .eq(comparator_1_eq));  // open: gt, lt
  // Probe on IF_PC[11:0]
  \硬布线控制器  \u_硬布线控制器_1  (
    .Func(func2), .OP(op2), .ALU_OP(\硬布线控制器_1_alu_op ), .MemToReg(\硬布线控制器_1_jmp [5]),
    .MemWrite(\硬布线控制器_1_jmp [6]), .ALU_SRC(\硬布线控制器_1_jmp [11]), .RegWrite(\硬布线控制器_1_jmp [12]),
    .SysCALL(\硬布线控制器_1_jmp [16]), .SignedExt(SignedExt), .RegDst(\硬布线控制器_1_jmp [14]), .JR(\硬布线控制器_1_jmp [1]),
    .JMP(\硬布线控制器_1_jmp [0]), .Beq(\硬布线控制器_1_jmp [3]), .JAL(\硬布线控制器_1_jmp [13]), .Bne(\硬布线控制器_1_jmp [4]),
    .SRAV(\硬布线控制器_1_jmp [15]), .LHU(\硬布线控制器_1_jmp [18]), .BGTZ(\硬布线控制器_1_jmp [17]));
  Multiplexer #(.width(5), .enable("false")) multiplexer_5 (
    .in0(if_id_1_instruction_2[25:21]), .in1(5'b00100), .out(ID_R1_num), .sel(\硬布线控制器_1_jmp [16]));
  Multiplexer #(.width(5), .enable("false")) multiplexer_6 (
    .in0(if_id_1_instruction_2[20:16]), .in1(5'b00010), .out(ID_R2_num), .sel(\硬布线控制器_1_jmp [16]));
  Counter #(.width(16), .max('hffff)) counter_1 (
    .count(stop), .Q(\总周期数 ), .clk(CLK), .clr(RST));  // open: load, D, carry
  and and_5 (and_5_out, hit3, ~comparator_1_eq);  // AND_Gate
  and and_6 (att_suc, comparator_1_eq, hit3);
  // Probe on ID_PC[11:0]
  // Probe on \预测成功数 
  Multiplexer #(.width(5), .enable("false")) multiplexer_7 (
    .in0(rt5), .in1(rd5), .out(multiplexer_7_out), .sel(regdst5));
  Multiplexer #(.width(5), .enable("false")) multiplexer_8 (
    .in0(multiplexer_7_out), .in1({5{1'b1}}), .out(WB_WriteReg_num), .sel(jal5));
  assign bit_extender_1_out = {{16{1'b0}}, {if_id_1_instruction_2[15:6], func2}};  // Bit_Extender bit_extender_1
  assign bit_extender_2_out = {{16{if_id_1_instruction_2[15]}}, {if_id_1_instruction_2[15:6], func2}};  // Bit_Extender bit_extender_2
  and and_7 (and_7_out, jump_suc, ~hit3);  // AND_Gate
  // Probe on EX_PC[11:0]
  // Probe on MEM_PC[11:0]
  not not_1 (not_1_out, CLK);
  Multiplexer #(.width(32), .enable("false")) multiplexer_9 (
    .in0(bit_extender_1_out), .in1(bit_extender_2_out), .out(multiplexer_9_out), .sel(SignedExt));
  or or_2 (att_fail, and_5_out, and_7_out);
  // Probe on WB_PC[11:0]
  MIPS_Regifile mips_regifile_1 (
    .Din(multiplexer_23_out), .Clk(not_1_out), .R1(mips_regifile_1_r1), .R2(mips_regifile_1_r2),
    .WE(regwrite5), .W_num(WB_WriteReg_num), .R1_num(ID_R1_num), .R2_num(ID_R2_num));
  or or_3 (or_3_out, RST, stall, att_fail);
  ID_EX id_ex_1 (
    .control({\硬布线控制器_1_jmp [18:11], \硬布线控制器_1_alu_op , \硬布线控制器_1_jmp [6:3], SignedExt, \硬布线控制器_1_jmp [1:0]}),
    .instruction({op2, if_id_1_instruction_2, func2}), .pc4(if_id_1_pc4_2), .R1(mips_regifile_1_r1),
    .R2(mips_regifile_1_r2), .imm(multiplexer_9_out),
    .control_2({id_ex_1_control_2[18:17], syscall3, srav, regdst3, jal3, id_ex_1_control_2[12:2], jr3, jmp3}),
    .instruction_2({instruction3, func3}), .pc4_2(id_ex_1_pc4_2), .R1_2(id_ex_1_r1_2), .R2_2(id_ex_1_r2_2),
    .imm_2(id_ex_1_imm_2), .rst(or_3_out), .stop(stop), .clk(CLK), .shamt(if_id_1_instruction_2[10:6]),
    .shamt_2(id_ex_1_shamt_2), .signimm(bit_extender_2_out), .signimm_2(id_ex_1_signimm_2), .hit(hit2),
    .hit_2(hit3), .jump_att(jump_att2), .jump_att_2(jump_att3), .hit_pos(hit_pos2), .hit_pos_2(hit_pos3),
    .pc(ID_PC), .pc_2(EX_PC));
  \重定向判断  \u_重定向判断_1  (
    .EX_OP(instruction3[31:26]), .WB_WriteReg_num(WB_WriteReg_num), .WB_RegWrite(regwrite5), .R1_sel(R1_sel),
    .MEM_WriteReg_num(MEM_WriteReg_num), .MEM_RegWrite(MEM_RegWrite), .R2_sel(R2_sel), .EX_Func(func3),
    .EX_R1_num(EX_R1_num), .EX_R2_num(EX_R2_num));
  Counter #(.width(16), .max('hffff)) counter_2 (
    .count(att_suc), .Q(\预测成功数 ), .clk(CLK), .clr(RST));  // open: load, D, carry
  Comparator #(.width(6)) comparator_2 (.a(instruction3[31:26]), .b(6'b100011), .eq(comparator_2_eq));  // open: gt, lt
  Comparator #(.width(6)) comparator_3 (.a(instruction3[31:26]), .b(6'b100101), .eq(comparator_3_eq));  // open: gt, lt
  Counter #(.width(16), .max('hffff)) counter_3 (
    .count(stall), .Q(\LoadUse次数 ), .clk(CLK), .clr(RST));  // open: load, D, carry
  Counter #(.width(16), .max('hffff)) counter_4 (
    .count(stall), .Q(\插入气泡数 ), .clk(CLK), .clr(RST));  // open: load, D, carry
  Multiplexer #(.select(2), .width(32), .enable("false")) multiplexer_10 (
    .in0(id_ex_1_r1_2), .in1(multiplexer_23_out), .in2(alu4), .in3(alu4), .out(a3), .sel(R1_sel));
  Multiplexer #(.select(2), .width(32), .enable("false")) multiplexer_11 (
    .in0(id_ex_1_r2_2), .in1(multiplexer_23_out), .in2(alu4), .in3(alu4), .out(multiplexer_11_out),
    .sel(R2_sel));
  or or_4 (EX_LW, comparator_2_eq, comparator_3_eq);
  or or_5 (jump_suc, branch, jmp3);
  or or_6 (jb_3, jmp3, id_ex_1_control_2[17], id_ex_1_control_2[4], id_ex_1_control_2[3]);
  Multiplexer #(.width(32), .enable("false")) multiplexer_12 (
    .in0(id_ex_1_pc4_2), .in1(dest_addr), .out(multiplexer_12_out), .sel(jump_suc));
  Counter #(.width(16), .max('hffff)) counter_5 (
    .count(att_fail), .Q(\预测失败数 ), .clk(CLK), .clr(RST));  // open: load, D, carry
  Multiplexer #(.width(32), .enable("false")) multiplexer_13 (
    .in0(multiplexer_11_out), .in1(id_ex_1_imm_2), .out(multiplexer_13_out), .sel(id_ex_1_control_2[11]));
  Shifter #(.width(32)) shifter_1 (.in(id_ex_1_signimm_2), .\dist (5'b00010), .out(shifter_1_out));
  Multiplexer #(.width(32), .enable("false")) multiplexer_14 (
    .in0(a3), .in1(32'h22), .out(multiplexer_14_out), .sel(syscall3));
  Multiplexer #(.width(5), .enable("false")) multiplexer_15 (
    .in0(id_ex_1_shamt_2), .in1(a3[4:0]), .out(multiplexer_15_out), .sel(srav));
  Multiplexer #(.width(32), .enable("false")) multiplexer_16 (
    .in0(adder_2_out), .in1({EX_PC[31:28], instruction3[25:6], func3, 2'b00}), .out(dest_addr), .sel(jmp3));
  MIPS_ALU mips_alu_1 (
    .X(multiplexer_14_out), .Y(multiplexer_13_out), .AluOP(id_ex_1_control_2[10:7]),
    .Equal(mips_alu_1_equal), .Result(mips_alu_1_result), .shamt(multiplexer_15_out));  // open: Result_2
  Adder #(.width(32)) adder_2 (.a(id_ex_1_pc4_2), .b(shifter_1_out), .out(adder_2_out));  // open: cin, cout
  Multiplexer #(.width(5), .enable("false")) multiplexer_17 (
    .in0(instruction3[25:21]), .in1(5'b00100), .out(EX_R1_num), .sel(syscall3));
  Multiplexer #(.width(5), .enable("false")) multiplexer_18 (
    .in0(instruction3[20:16]), .in1(5'b00010), .out(EX_R2_num), .sel(syscall3));
  and and_8 (and_8_out, id_ex_1_control_2[3], mips_alu_1_equal);
  and and_9 (and_9_out, id_ex_1_control_2[4], ~mips_alu_1_equal);  // AND_Gate
  or or_7 (branch, and_8_out, and_9_out, and_10_out);
  and and_10 (and_10_out, id_ex_1_control_2[17], ~mips_alu_1_equal, ~mips_alu_1_result[0]);  // AND_Gate
  Counter #(.width(16), .max('hffff)) counter_6 (
    .count(jmp3), .Q(\无条件分支数 ), .clk(CLK), .clr(RST));  // open: load, D, carry
  Counter #(.width(16), .max('hffff)) counter_7 (
    .count(branch), .Q(\条件分支成功数 ), .clk(CLK), .clr(RST));  // open: load, D, carry
  EX_MEM ex_mem_1 (
    .control({id_ex_1_control_2[18:17], syscall3, srav, regdst3, jal3, id_ex_1_control_2[12:2], jr3, jmp3}),
    .instruction({instruction3, func3}), .pc4(id_ex_1_pc4_2), .R2(multiplexer_11_out),
    .alu(mips_alu_1_result),
    .control_2({ex_mem_1_control_2[18:15], regdst4, jal4, MEM_RegWrite, ex_mem_1_control_2[11:0]}),
    .instruction_2({ex_mem_1_instruction_2[31:21], rt4, rd4, ex_mem_1_instruction_2[10:0]}), .pc4_2(MEM_PC),
    .R2_2(ex_mem_1_r2_2), .alu_2(alu4), .rst(RST), .stop(stop), .clk(CLK), .equal(mips_alu_1_equal),
    .equal_2(ex_mem_1_equal_2), .R1(a3), .R1_2(ex_mem_1_r1_2));
  Multiplexer #(.width(5), .enable("false")) multiplexer_19 (
    .in0(rt4), .in1(rd4), .out(multiplexer_19_out), .sel(regdst4));
  Multiplexer #(.width(5), .enable("false")) multiplexer_20 (
    .in0(instruction3[20:16]), .in1(instruction3[15:11]), .out(multiplexer_20_out), .sel(regdst3));
  Multiplexer #(.width(5), .enable("false")) multiplexer_21 (
    .in0(multiplexer_19_out), .in1({5{1'b1}}), .out(MEM_WriteReg_num), .sel(jal4));
  Multiplexer #(.width(5), .enable("false")) multiplexer_22 (
    .in0(multiplexer_20_out), .in1({5{1'b1}}), .out(EX_WriteReg_num), .sel(jal3));
  RAM #(.addrWidth(10), .dataWidth(32), .bus("separate")) ram_1 (
    .addr(alu4[11:2]), .din(ex_mem_1_r2_2), .data(ram_1_data), .str(ex_mem_1_control_2[6]), .clk(CLK),
    .ld(not_2_out), .clr(RST));  // open: sel
  not not_2 (not_2_out, ex_mem_1_control_2[6]);
  MEM_WB mem_wb_1 (
    .control({ex_mem_1_control_2[18:15], regdst4, jal4, MEM_RegWrite, ex_mem_1_control_2[11:0]}),
    .instruction({ex_mem_1_instruction_2[31:21], rt4, rd4, ex_mem_1_instruction_2[10:0]}), .pc4(MEM_PC),
    .md(ram_1_data), .alu(alu4),
    .control_2({lhu, mem_wb_1_control_2[17], syscall5, mem_wb_1_control_2[15], regdst5, jal5, regwrite5, mem_wb_1_control_2[11:0]}),
    .instruction_2({mem_wb_1_instruction_2[31:21], rt5, rd5, mem_wb_1_instruction_2[10:0]}), .pc4_2(WB_PC),
    .md_2(mem_wb_1_md_2), .alu_2(result5), .rst(RST), .stop(stop), .clk(CLK), .equal(ex_mem_1_equal_2),
    .equal_2(equal5), .R1(ex_mem_1_r1_2), .R1_2(a5));
  Multiplexer #(.width(32), .enable("false")) multiplexer_23 (
    .in0(multiplexer_25_out), .in1(WB_PC), .out(multiplexer_23_out), .sel(jal5));
  Multiplexer #(.width(32), .enable("false")) multiplexer_24 (
    .in0(result5), .in1(mem_wb_1_md_2), .out(multiplexer_24_out), .sel(mem_wb_1_control_2[5]));
  Multiplexer #(.width(32), .enable("false")) multiplexer_25 (
    .in0(multiplexer_24_out), .in1({{16{1'b0}}, multiplexer_26_out}), .out(multiplexer_25_out), .sel(lhu));
  Multiplexer #(.width(16), .enable("false")) multiplexer_26 (
    .in0(multiplexer_24_out[15:0]), .in1(multiplexer_24_out[31:16]), .out(multiplexer_26_out),
    .sel(result5[1]));

  // Other names for the same wires on the sheet: instruction3[5:0] = func3; rd3[4:0] = instruction3[15:11];
  //   rt3[4:0] = instruction3[20:16]; rs3[4:0] = instruction3[25:21]; op3[5:0] = instruction3[31:26]

  // Notes on the sheet:
  //   中断源
  //   中断等待指示
  //   数码管输出
  //   指令存储器
  //   contents of rom_1 (hex, n*v repeats v):
  //   20110001 8100005 20110001 20120002 20130003 8100009 20110001 20120002 20130003 810000d 20110001
  //   20120002 20130003 8100011 20110001 20120002 20130003 c1000f9 20100001 20110001 118fc0 112020
  //   20020022 c 118882 12200001 8100015 112020 20020022 c 20110001 118880 112020 20020022 c 12200001
  //   810001f 20110001 118fc0 112020 20020022 c 1188c3 112020 20020022 c 118903 112020 20020022 c 118903
  //   112020 20020022 c 118903 112020 20020022 c 118903 112020 20020022 c 118903 112020 20020022 c 118903
  //   112020 20020022 c 118903 112020 20020022 c 20100001 109fc0 139fc3 8021 2012000c 24160003 26100001
  //   3210000f 20080008 20090001 139900 2709825 132020 20020022 c 1094022 1500fff9 22100001 2018000f
  //   2188024 108700 20080008 20090001 139902 2709825 132021 20020022 c 1094022 1500fff9 108702 2c9b022
  //   12c00001 8100050 4020 1084027 84400 3508ffff 82021 20020022 c 2010ffff 20110000 ae300000 22100001
  //   22310004 ae300000 22100001 22310004 ae300000 22100001 22310004 ae300000 22100001 22310004 ae300000
  //   22100001 22310004 ae300000 22100001 22310004 ae300000 22100001 22310004 ae300000 22100001 22310004
  //   ae300000 22100001 22310004 ae300000 22100001 22310004 ae300000 22100001 22310004 ae300000 22100001
  //   22310004 ae300000 22100001 22310004 ae300000 22100001 22310004 ae300000 22100001 22310004 ae300000
  //   22100001 22310004 22100001 8020 2011003c 8e130000 8e340000 274402a 11000002 ae330000 ae140000
  //   2231fffc 1611fff8 102020 20020022 c 22100004 2011003c 1611fff2 20020032 c 20080001 20090003 20110876
  //   118d00 112020 20020022 c 200b0008 1118807 1318807 112020 20020022 c 216bffff 1560fff9 2002000a c
  //   20080001 20110010 112020 20020022 c 200b0020 2288823 112020 20020022 c 216bffff 1560fffa 2002000a c
  //   20090000 200b0010 34118483 20120404 118c00 129400 36318281 22520404 ad310000 2328820 21290004
  //   216bffff 1560fffb 200b0020 20090000 95310000 112020 20020022 c 21290002 216bffff 1560fff9 2002000a c
  //   2011000f 112020 20020022 c 2231ffff 1e20fffb 2002000a c 2002000a c 20100000 22100001 102020 20020022
  //   c 22100002 102020 20020022 c 22100003 102020 20020022 c 22100004 102020 20020022 c 22100005 102020
  //   20020022 c 22100006 102020 20020022 c 22100007 102020 20020022 c 22100008 102020 20020022 20020022 c
  //   3e00008
  //   指令字
  //   OP
  //   Func
  //   rs
  //   rt
  //   rd
  //   shamt
  //   imm
  //   JMP
  //   JR
  //   OP
  //   Func
  //   Beq
  //   Bne
  //   AluOP
  //   AluSrcB
  //   RegWrite
  //   JAL
  //   RegDst
  //   MemToReg
  //   MemWrite
  //   流水调试日志用
  //   lw
  //   lhu
  //   OP
  //   Func
  //   rs
  //   rt
  //   rd
  //   rt
  //   rd
  //   rt
  //   rd
endmodule

module \重定向判断  (
  input  [5:0] EX_OP,
  input  [4:0] WB_WriteReg_num,
  input  WB_RegWrite,
  input  [4:0] MEM_WriteReg_num,
  input  MEM_RegWrite,
  input  [5:0] EX_Func,
  input  [4:0] EX_R1_num,
  input  [4:0] EX_R2_num,
  output [1:0] R1_sel,
  output [1:0] R2_sel
);

  wire comparator_1_eq, comparator_2_eq, comparator_3_eq, comparator_4_eq, comparator_5_eq, comparator_6_eq,
       comparator_7_eq, comparator_8_eq, R1_used, R2_used;

  \源寄存器使用情况  \u_源寄存器使用情况_1  (
    .OP0(EX_OP[0]), .OP1(EX_OP[1]), .OP2(EX_OP[2]), .OP3(EX_OP[3]), .OP4(EX_OP[4]), .OP5(EX_OP[5]),
    .F0(EX_Func[0]), .F1(EX_Func[1]), .F2(EX_Func[2]), .F3(EX_Func[3]), .F4(EX_Func[4]), .F5(EX_Func[5]),
    .R1_Used(R1_used), .R2_Used(R2_used));
  Comparator #(.width(5)) comparator_1 (.a({5{1'b0}}), .b(EX_R1_num), .eq(comparator_1_eq));  // open: gt, lt
  Comparator #(.width(5)) comparator_2 (.a(EX_R1_num), .b(MEM_WriteReg_num), .eq(comparator_2_eq));  // open: gt, lt
  Comparator #(.width(5)) comparator_3 (.a({5{1'b0}}), .b(EX_R1_num), .eq(comparator_3_eq));  // open: gt, lt
  Comparator #(.width(5)) comparator_4 (.a(EX_R1_num), .b(WB_WriteReg_num), .eq(comparator_4_eq));  // open: gt, lt
  Comparator #(.width(5)) comparator_5 (.a({5{1'b0}}), .b(EX_R2_num), .eq(comparator_5_eq));  // open: gt, lt
  Comparator #(.width(5)) comparator_6 (.a(EX_R2_num), .b(MEM_WriteReg_num), .eq(comparator_6_eq));  // open: gt, lt
  Comparator #(.width(5)) comparator_7 (.a({5{1'b0}}), .b(EX_R2_num), .eq(comparator_7_eq));  // open: gt, lt
  Comparator #(.width(5)) comparator_8 (.a(EX_R2_num), .b(WB_WriteReg_num), .eq(comparator_8_eq));  // open: gt, lt
  and and_1 (R1_sel[1], R1_used, ~comparator_1_eq, comparator_2_eq, MEM_RegWrite);  // AND_Gate
  and and_2 (R1_sel[0], R1_used, ~comparator_3_eq, comparator_4_eq, WB_RegWrite);  // AND_Gate
  and and_3 (R2_sel[1], R2_used, ~comparator_5_eq, comparator_6_eq, MEM_RegWrite);  // AND_Gate
  and and_4 (R2_sel[0], R2_used, ~comparator_7_eq, comparator_8_eq, WB_RegWrite);  // AND_Gate

  // Notes on the sheet:
  //   sel1,to 4
  //   sel0,to 5
  //   sel1,to 4
  //   sel0,to 5
endmodule

module load_use (
  input  [5:0] ID_OP,
  input  [4:0] EX_WriteReg_num,
  input  EX_LW,
  input  [4:0] ID_R1_num,
  input  [5:0] ID_Func,
  input  [4:0] ID_R2_num,
  output STALL
);

  wire and_1_out, and_2_out, comparator_1_eq, comparator_2_eq, comparator_3_eq, comparator_4_eq, or_1_out,
       R1_used, R2_used;

  \源寄存器使用情况  \u_源寄存器使用情况_1  (
    .OP0(ID_OP[0]), .OP1(ID_OP[1]), .OP2(ID_OP[2]), .OP3(ID_OP[3]), .OP4(ID_OP[4]), .OP5(ID_OP[5]),
    .F0(ID_Func[0]), .F1(ID_Func[1]), .F2(ID_Func[2]), .F3(ID_Func[3]), .F4(ID_Func[4]), .F5(ID_Func[5]),
    .R1_Used(R1_used), .R2_Used(R2_used));
  Comparator #(.width(5)) comparator_1 (.a({5{1'b0}}), .b(ID_R1_num), .eq(comparator_1_eq));  // open: gt, lt
  Comparator #(.width(5)) comparator_2 (.a(ID_R1_num), .b(EX_WriteReg_num), .eq(comparator_2_eq));  // open: gt, lt
  Comparator #(.width(5)) comparator_3 (.a({5{1'b0}}), .b(ID_R2_num), .eq(comparator_3_eq));  // open: gt, lt
  Comparator #(.width(5)) comparator_4 (.a(ID_R2_num), .b(EX_WriteReg_num), .eq(comparator_4_eq));  // open: gt, lt
  and and_1 (and_1_out, ~comparator_1_eq, R1_used, comparator_2_eq);  // AND_Gate
  and and_2 (and_2_out, ~comparator_3_eq, R2_used, comparator_4_eq);  // AND_Gate
  or or_1 (or_1_out, and_1_out, and_2_out);
  and and_3 (STALL, or_1_out, EX_LW);
endmodule

module \状态机  (
  input  [1:0] state,
  input  [1:0] hit_jump,
  output [1:0] nextstate
);

  wire [1:0] state_1_next_status, state_2_next_status;

  state state_1 (.status(state), .jump(1'b0), .next_status(state_1_next_status));
  state state_2 (.status(state), .jump(1'b1), .next_status(state_2_next_status));
  Multiplexer #(.select(2), .width(2), .enable("false")) multiplexer_1 (
    .in0(2'b00), .in1(2'b01), .in2(state_1_next_status), .in3(state_2_next_status), .out(nextstate),
    .sel(hit_jump));
endmodule

module \最大数  (
  input  [31:0] _000,
  input  [31:0] _001,
  input  [31:0] _010,
  input  [31:0] _011,
  input  [31:0] _100,
  input  [31:0] _101,
  input  [31:0] _110,
  input  [31:0] _111,
  output [31:0] \最大数 ,
  output [2:0] \最大编号 
);

  wire comparator_1_lt, comparator_2_lt, comparator_3_lt, comparator_4_lt, comparator_5_lt, comparator_6_lt,
       comparator_7_lt;
  wire [2:0] multiplexer_2_out, multiplexer_4_out, multiplexer_6_out, multiplexer_8_out, multiplexer_10_out,
       multiplexer_12_out;
  wire [31:0] multiplexer_1_out, multiplexer_3_out, multiplexer_5_out, multiplexer_7_out, multiplexer_9_out,
       multiplexer_11_out;

  Comparator #(.width(32)) comparator_1 (.a(_000), .b(_001), .lt(comparator_1_lt));  // open: gt, eq
  Comparator #(.width(32)) comparator_2 (.a(_010), .b(_011), .lt(comparator_2_lt));  // open: gt, eq
  Comparator #(.width(32)) comparator_3 (.a(_100), .b(_101), .lt(comparator_3_lt));  // open: gt, eq
  Comparator #(.width(32)) comparator_4 (.a(_110), .b(_111), .lt(comparator_4_lt));  // open: gt, eq
  Multiplexer #(.width(32), .enable("false")) multiplexer_1 (
    .in0(_000), .in1(_001), .out(multiplexer_1_out), .sel(comparator_1_lt));
  Multiplexer #(.width(3), .enable("false")) multiplexer_2 (
    .in0(3'b000), .in1(3'b001), .out(multiplexer_2_out), .sel(comparator_1_lt));
  Multiplexer #(.width(32), .enable("false")) multiplexer_3 (
    .in0(_010), .in1(_011), .out(multiplexer_3_out), .sel(comparator_2_lt));
  Multiplexer #(.width(3), .enable("false")) multiplexer_4 (
    .in0(3'b010), .in1(3'b011), .out(multiplexer_4_out), .sel(comparator_2_lt));
  Multiplexer #(.width(32), .enable("false")) multiplexer_5 (
    .in0(_100), .in1(_101), .out(multiplexer_5_out), .sel(comparator_3_lt));
  Multiplexer #(.width(3), .enable("false")) multiplexer_6 (
    .in0(3'b100), .in1(3'b101), .out(multiplexer_6_out), .sel(comparator_3_lt));
  Multiplexer #(.width(32), .enable("false")) multiplexer_7 (
    .in0(_110), .in1(_111), .out(multiplexer_7_out), .sel(comparator_4_lt));
  Multiplexer #(.width(3), .enable("false")) multiplexer_8 (
    .in0(3'b110), .in1(3'b111), .out(multiplexer_8_out), .sel(comparator_4_lt));
  Comparator #(.width(32)) comparator_5 (
    .a(multiplexer_1_out), .b(multiplexer_3_out), .lt(comparator_5_lt));  // open: gt, eq
  Comparator #(.width(32)) comparator_6 (
    .a(multiplexer_5_out), .b(multiplexer_7_out), .lt(comparator_6_lt));  // open: gt, eq
  Multiplexer #(.width(32), .enable("false")) multiplexer_9 (
    .in0(multiplexer_1_out), .in1(multiplexer_3_out), .out(multiplexer_9_out), .sel(comparator_5_lt));
  Multiplexer #(.width(3), .enable("false")) multiplexer_10 (
    .in0(multiplexer_2_out), .in1(multiplexer_4_out), .out(multiplexer_10_out), .sel(comparator_5_lt));
  Multiplexer #(.width(32), .enable("false")) multiplexer_11 (
    .in0(multiplexer_5_out), .in1(multiplexer_7_out), .out(multiplexer_11_out), .sel(comparator_6_lt));
  Multiplexer #(.width(3), .enable("false")) multiplexer_12 (
    .in0(multiplexer_6_out), .in1(multiplexer_8_out), .out(multiplexer_12_out), .sel(comparator_6_lt));
  Comparator #(.width(32)) comparator_7 (
    .a(multiplexer_9_out), .b(multiplexer_11_out), .lt(comparator_7_lt));  // open: gt, eq
  Multiplexer #(.width(32), .enable("false")) multiplexer_13 (
    .in0(multiplexer_9_out), .in1(multiplexer_11_out), .out(\最大数 ), .sel(comparator_7_lt));
  Multiplexer #(.width(3), .enable("false")) multiplexer_14 (
    .in0(multiplexer_10_out), .in1(multiplexer_12_out), .out(\最大编号 ), .sel(comparator_7_lt));
endmodule

module BHT (
  input  clk,
  input  jump_suc_3,
  input  [31:0] pc,
  input  [31:0] pc_3,
  input  hit_3,
  input  rst,
  input  jb_3,
  input  [2:0] hit_pos_3,
  input  [31:0] dest_addr,
  output jump_att,
  output hit,
  output [31:0] pc_att,
  output [2:0] hit_pos
);

  wire and_1_out, and_2_out, and_3_out, and_4_out, and_5_out, and_6_out, and_7_out, and_16_out,
       comparator_1_eq, comparator_2_eq, comparator_3_eq, comparator_4_eq, comparator_5_eq, comparator_6_eq,
       comparator_7_eq, comparator_8_eq, decoder_1_out0, decoder_1_out1, decoder_1_out2, decoder_1_out3,
       decoder_1_out4, decoder_1_out5, decoder_1_out6, decoder_1_out7, empty, en0, en0addr, en1, en1addr,
       en2, en2addr, en3, en3addr, en4, en4addr, en5, en5addr, en6, en6addr, en7, en7addr, nhit_3, not_1_out,
       not_2_out, not_3_out, not_4_out, not_5_out, not_6_out, not_7_out, not_8_out, priority_encoder_2_gs,
       register_1_q, register_2_q, register_3_q, register_4_q, register_5_q, register_6_q, register_7_q,
       register_8_q;
  wire [0:0] multiplexer_5_out;
  wire [1:0] register_25_q, register_26_q, register_27_q, register_28_q, register_29_q, register_30_q,
       register_31_q, register_32_q, \状态机_1_nextstate , \状态机_2_nextstate , \状态机_3_nextstate ,
       \状态机_4_nextstate , \状态机_5_nextstate , \状态机_6_nextstate , \状态机_7_nextstate , \状态机_8_nextstate ;
  wire [2:0] big_num, invalid, multiplexer_1_out, multiplexer_2_out, multiplexer_3_out;
  wire [31:0] adder_1_out, adder_2_out, adder_3_out, adder_4_out, adder_5_out, adder_6_out, adder_7_out,
       adder_8_out, multiplexer_6_out, multiplexer_7_out, multiplexer_8_out, multiplexer_9_out,
       multiplexer_10_out, multiplexer_11_out, multiplexer_12_out, multiplexer_13_out, register_9_q,
       register_10_q, register_11_q, register_12_q, register_13_q, register_14_q, register_15_q,
       register_16_q, register_17_q, register_18_q, register_19_q, register_20_q, register_21_q,
       register_22_q, register_23_q, register_24_q, register_33_q, register_34_q, register_35_q,
       register_36_q, register_37_q, register_38_q, register_39_q, register_40_q, \最大数 ;

  Register #(.width(1)) register_1 (.D(1'b1), .en(en0), .Q(register_1_q), .clk(clk), .clr(rst));
  Register #(.width(1)) register_2 (.D(1'b1), .en(en1), .Q(register_2_q), .clk(clk), .clr(rst));
  Register #(.width(1)) register_3 (.D(1'b1), .en(en2), .Q(register_3_q), .clk(clk), .clr(rst));
  Register #(.width(1)) register_4 (.D(1'b1), .en(en3), .Q(register_4_q), .clk(clk), .clr(rst));
  Register #(.width(1)) register_5 (.D(1'b1), .en(en4), .Q(register_5_q), .clk(clk), .clr(rst));
  Register #(.width(1)) register_6 (.D(1'b1), .en(en5), .Q(register_6_q), .clk(clk), .clr(rst));
  Register #(.width(1)) register_7 (.D(1'b1), .en(en6), .Q(register_7_q), .clk(clk), .clr(rst));
  Register #(.width(1)) register_8 (.D(1'b1), .en(en7), .Q(register_8_q), .clk(clk), .clr(rst));
  Multiplexer #(.width(3), .enable("false")) multiplexer_1 (
    .in0(big_num), .in1(invalid), .out(multiplexer_1_out), .sel(empty));
  not not_1 (not_1_out, register_1_q);
  not not_2 (not_2_out, register_2_q);
  not not_3 (not_3_out, register_3_q);
  not not_4 (not_4_out, register_4_q);
  not not_5 (not_5_out, register_5_q);
  not not_6 (not_6_out, register_6_q);
  not not_7 (not_7_out, register_7_q);
  not not_8 (not_8_out, register_8_q);
  Multiplexer #(.width(3), .enable("false")) multiplexer_2 (
    .in0(multiplexer_1_out), .in1(hit_pos_3), .out(multiplexer_2_out), .sel(hit_3));
  Priority_Encoder priority_encoder_1 (
    .in0(not_1_out), .in1(not_2_out), .in2(not_3_out), .in3(not_4_out), .in4(not_5_out), .in5(not_6_out),
    .in6(not_7_out), .in7(not_8_out), .out(invalid), .gs(empty));  // open: en_in, en_out
  and and_1 (and_1_out, register_8_q, comparator_8_eq);
  and and_2 (and_2_out, register_7_q, comparator_7_eq);
  Decoder #(.select(3), .enable("false")) decoder_1 (
    .out0(decoder_1_out0), .out1(decoder_1_out1), .out2(decoder_1_out2), .out3(decoder_1_out3),
    .out4(decoder_1_out4), .out5(decoder_1_out5), .out6(decoder_1_out6), .out7(decoder_1_out7),
    .sel(multiplexer_2_out));
  not not_9 (nhit_3, hit_3);
  and and_3 (and_3_out, register_5_q, comparator_5_eq);
  and and_4 (and_4_out, register_6_q, comparator_6_eq);
  or or_1 (hit, and_1_out, and_2_out, and_4_out, and_3_out, and_5_out, and_7_out, and_6_out, and_16_out);
  Register #(.width(32)) register_9 (.D(pc_3), .en(en0addr), .Q(register_9_q), .clk(clk), .clr(rst));
  Register #(.width(32)) register_10 (.D(pc_3), .en(en1addr), .Q(register_10_q), .clk(clk), .clr(rst));
  Register #(.width(32)) register_11 (.D(pc_3), .en(en2addr), .Q(register_11_q), .clk(clk), .clr(rst));
  Register #(.width(32)) register_12 (.D(pc_3), .en(en3addr), .Q(register_12_q), .clk(clk), .clr(rst));
  Register #(.width(32)) register_13 (.D(pc_3), .en(en4addr), .Q(register_13_q), .clk(clk), .clr(rst));
  Register #(.width(32)) register_14 (.D(pc_3), .en(en5addr), .Q(register_14_q), .clk(clk), .clr(rst));
  Register #(.width(32)) register_15 (.D(pc_3), .en(en6addr), .Q(register_15_q), .clk(clk), .clr(rst));
  Register #(.width(32)) register_16 (.D(pc_3), .en(en7addr), .Q(register_16_q), .clk(clk), .clr(rst));
  and and_5 (and_5_out, register_4_q, comparator_4_eq);
  and and_6 (and_6_out, register_2_q, comparator_2_eq);
  and and_7 (and_7_out, register_3_q, comparator_3_eq);
  and and_8 (en0, jb_3, decoder_1_out0);
  and and_9 (en1, decoder_1_out1, jb_3);
  and and_10 (en2, decoder_1_out2, jb_3);
  and and_11 (en3, decoder_1_out3, jb_3);
  and and_12 (en4, decoder_1_out4, jb_3);
  and and_13 (en5, decoder_1_out5, jb_3);
  and and_14 (en6, decoder_1_out6, jb_3);
  and and_15 (en7, decoder_1_out7, jb_3);
  Comparator #(.width(32)) comparator_1 (.a(pc), .b(register_9_q), .eq(comparator_1_eq));  // open: gt, lt
  Comparator #(.width(32)) comparator_2 (.a(pc), .b(register_10_q), .eq(comparator_2_eq));  // open: gt, lt
  Comparator #(.width(32)) comparator_3 (.a(pc), .b(register_11_q), .eq(comparator_3_eq));  // open: gt, lt
  Comparator #(.width(32)) comparator_4 (.a(pc), .b(register_12_q), .eq(comparator_4_eq));  // open: gt, lt
  Comparator #(.width(32)) comparator_5 (.a(pc), .b(register_13_q), .eq(comparator_5_eq));  // open: gt, lt
  Comparator #(.width(32)) comparator_6 (.a(pc), .b(register_14_q), .eq(comparator_6_eq));  // open: gt, lt
  Comparator #(.width(32)) comparator_7 (.a(pc), .b(register_15_q), .eq(comparator_7_eq));  // open: gt, lt
  Comparator #(.width(32)) comparator_8 (.a(pc), .b(register_16_q), .eq(comparator_8_eq));  // open: gt, lt
  and and_16 (and_16_out, register_1_q, comparator_1_eq);
  Priority_Encoder priority_encoder_2 (
    .in0(and_16_out), .in1(and_6_out), .in2(and_7_out), .in3(and_5_out), .in4(and_3_out), .in5(and_4_out),
    .in6(and_2_out), .in7(and_1_out), .out(hit_pos), .gs(priority_encoder_2_gs));  // open: en_in, en_out
  and and_17 (en0addr, nhit_3, en0);
  and and_18 (en1addr, nhit_3, en1);
  and and_19 (en2addr, nhit_3, en2);
  and and_20 (en3addr, nhit_3, en3);
  and and_21 (en4addr, nhit_3, en4);
  and and_22 (en5addr, nhit_3, en5);
  and and_23 (en6addr, nhit_3, en6);
  and and_24 (en7addr, nhit_3, en7);
  Register #(.width(32)) register_17 (.D(dest_addr), .en(en0addr), .Q(register_17_q), .clk(clk), .clr(rst));
  Register #(.width(32)) register_18 (.D(dest_addr), .en(en1addr), .Q(register_18_q), .clk(clk), .clr(rst));
  Register #(.width(32)) register_19 (.D(dest_addr), .en(en2addr), .Q(register_19_q), .clk(clk), .clr(rst));
  Register #(.width(32)) register_20 (.D(dest_addr), .en(en3addr), .Q(register_20_q), .clk(clk), .clr(rst));
  Register #(.width(32)) register_21 (.D(dest_addr), .en(en4addr), .Q(register_21_q), .clk(clk), .clr(rst));
  Register #(.width(32)) register_22 (.D(dest_addr), .en(en5addr), .Q(register_22_q), .clk(clk), .clr(rst));
  Register #(.width(32)) register_23 (.D(dest_addr), .en(en6addr), .Q(register_23_q), .clk(clk), .clr(rst));
  Register #(.width(32)) register_24 (.D(dest_addr), .en(en7addr), .Q(register_24_q), .clk(clk), .clr(rst));
  Multiplexer #(.width(3), .enable("false")) multiplexer_3 (
    .in0(3'b000), .in1(hit_pos), .out(multiplexer_3_out), .sel(priority_encoder_2_gs));
  Multiplexer #(.select(3), .width(32), .enable("false")) multiplexer_4 (
    .in0(register_17_q), .in1(register_18_q), .in2(register_19_q), .in3(register_20_q), .in4(register_21_q),
    .in5(register_22_q), .in6(register_23_q), .in7(register_24_q), .out(pc_att), .sel(multiplexer_3_out));
  \状态机  \u_状态机_1  (.state(register_25_q), .nextstate(\状态机_1_nextstate ), .hit_jump({hit_3, jump_suc_3}));
  \状态机  \u_状态机_2  (.state(register_26_q), .nextstate(\状态机_2_nextstate ), .hit_jump({hit_3, jump_suc_3}));
  \状态机  \u_状态机_3  (.state(register_27_q), .nextstate(\状态机_3_nextstate ), .hit_jump({hit_3, jump_suc_3}));
  \状态机  \u_状态机_4  (.state(register_28_q), .nextstate(\状态机_4_nextstate ), .hit_jump({hit_3, jump_suc_3}));
  \状态机  \u_状态机_5  (.state(register_29_q), .nextstate(\状态机_5_nextstate ), .hit_jump({hit_3, jump_suc_3}));
  \状态机  \u_状态机_6  (.state(register_30_q), .nextstate(\状态机_6_nextstate ), .hit_jump({hit_3, jump_suc_3}));
  \状态机  \u_状态机_7  (.state(register_31_q), .nextstate(\状态机_7_nextstate ), .hit_jump({hit_3, jump_suc_3}));
  \状态机  \u_状态机_8  (.state(register_32_q), .nextstate(\状态机_8_nextstate ), .hit_jump({hit_3, jump_suc_3}));
  Register #(.width(2)) register_25 (.D(\状态机_1_nextstate ), .en(en0), .Q(register_25_q), .clk(clk), .clr(rst));
  Register #(.width(2)) register_26 (.D(\状态机_2_nextstate ), .en(en1), .Q(register_26_q), .clk(clk), .clr(rst));
  Register #(.width(2)) register_27 (.D(\状态机_3_nextstate ), .en(en2), .Q(register_27_q), .clk(clk), .clr(rst));
  Register #(.width(2)) register_28 (.D(\状态机_4_nextstate ), .en(en3), .Q(register_28_q), .clk(clk), .clr(rst));
  Register #(.width(2)) register_29 (.D(\状态机_5_nextstate ), .en(en4), .Q(register_29_q), .clk(clk), .clr(rst));
  Register #(.width(2)) register_30 (.D(\状态机_6_nextstate ), .en(en5), .Q(register_30_q), .clk(clk), .clr(rst));
  Register #(.width(2)) register_31 (.D(\状态机_7_nextstate ), .en(en6), .Q(register_31_q), .clk(clk), .clr(rst));
  Register #(.width(2)) register_32 (.D(\状态机_8_nextstate ), .en(en7), .Q(register_32_q), .clk(clk), .clr(rst));
  Multiplexer #(.select(3), .width(2), .enable("false")) multiplexer_5 (
    .in0(register_25_q), .in1(register_26_q), .in2(register_27_q), .in3(register_28_q), .in4(register_29_q),
    .in5(register_30_q), .in6(register_31_q), .in7(register_32_q), .out({jump_att, multiplexer_5_out[0]}),
    .sel(multiplexer_3_out));
  Multiplexer #(.width(32), .enable("false")) multiplexer_6 (
    .in0(adder_1_out), .in1({32{1'b0}}), .out(multiplexer_6_out), .sel(en0));
  Multiplexer #(.width(32), .enable("false")) multiplexer_7 (
    .in0(adder_2_out), .in1({32{1'b0}}), .out(multiplexer_7_out), .sel(en1));
  Multiplexer #(.width(32), .enable("false")) multiplexer_8 (
    .in0(adder_3_out), .in1({32{1'b0}}), .out(multiplexer_8_out), .sel(en2));
  Multiplexer #(.width(32), .enable("false")) multiplexer_9 (
    .in0(adder_4_out), .in1({32{1'b0}}), .out(multiplexer_9_out), .sel(en3));
  Multiplexer #(.width(32), .enable("false")) multiplexer_10 (
    .in0(adder_5_out), .in1({32{1'b0}}), .out(multiplexer_10_out), .sel(en4));
  Multiplexer #(.width(32), .enable("false")) multiplexer_11 (
    .in0(adder_6_out), .in1({32{1'b0}}), .out(multiplexer_11_out), .sel(en5));
  Multiplexer #(.width(32), .enable("false")) multiplexer_12 (
    .in0(adder_7_out), .in1({32{1'b0}}), .out(multiplexer_12_out), .sel(en6));
  Multiplexer #(.width(32), .enable("false")) multiplexer_13 (
    .in0(adder_8_out), .in1({32{1'b0}}), .out(multiplexer_13_out), .sel(en7));
  Adder #(.width(32)) adder_1 (.a(32'h1), .b(register_33_q), .out(adder_1_out));  // open: cin, cout
  Register #(.width(32)) register_33 (.D(multiplexer_6_out), .en(jb_3), .Q(register_33_q), .clk(clk), .clr(rst));
  Adder #(.width(32)) adder_2 (.a(32'h1), .b(register_34_q), .out(adder_2_out));  // open: cin, cout
  Register #(.width(32)) register_34 (.D(multiplexer_7_out), .en(jb_3), .Q(register_34_q), .clk(clk), .clr(rst));
  Adder #(.width(32)) adder_3 (.a(32'h1), .b(register_35_q), .out(adder_3_out));  // open: cin, cout
  Register #(.width(32)) register_35 (.D(multiplexer_8_out), .en(jb_3), .Q(register_35_q), .clk(clk), .clr(rst));
  Adder #(.width(32)) adder_4 (.a(32'h1), .b(register_36_q), .out(adder_4_out));  // open: cin, cout
  Register #(.width(32)) register_36 (.D(multiplexer_9_out), .en(jb_3), .Q(register_36_q), .clk(clk), .clr(rst));
  Adder #(.width(32)) adder_5 (.a(32'h1), .b(register_37_q), .out(adder_5_out));  // open: cin, cout
  Register #(.width(32)) register_37 (.D(multiplexer_10_out), .en(jb_3), .Q(register_37_q), .clk(clk), .clr(rst));
  Adder #(.width(32)) adder_6 (.a(32'h1), .b(register_38_q), .out(adder_6_out));  // open: cin, cout
  Register #(.width(32)) register_38 (.D(multiplexer_11_out), .en(jb_3), .Q(register_38_q), .clk(clk), .clr(rst));
  Adder #(.width(32)) adder_7 (.a(32'h1), .b(register_39_q), .out(adder_7_out));  // open: cin, cout
  Register #(.width(32)) register_39 (.D(multiplexer_12_out), .en(jb_3), .Q(register_39_q), .clk(clk), .clr(rst));
  Adder #(.width(32)) adder_8 (.a(32'h1), .b(register_40_q), .out(adder_8_out));  // open: cin, cout
  Register #(.width(32)) register_40 (.D(multiplexer_13_out), .en(jb_3), .Q(register_40_q), .clk(clk), .clr(rst));
  \最大数  \u_最大数_1  (
    ._000(register_33_q), ._001(register_34_q), ._010(register_35_q), ._011(register_36_q),
    ._100(register_37_q), ._101(register_38_q), ._110(register_39_q), ._111(register_40_q), .\最大数 (\最大数 ),
    .\最大编号 (big_num));

  // Notes on the sheet:
  //   valid
  //   指令addr
  //   目标addr
  //   预测历史
  //   LRU
endmodule

module state (
  input  [1:0] status,
  input  jump,
  output [1:0] next_status
);

  wire and_1_out, and_2_out, and_3_out, and_4_out, and_5_out, and_6_out;

  and and_1 (and_1_out, ~status[1], ~status[0], jump);  // AND_Gate
  and and_2 (and_2_out, status[1], ~status[0], ~jump);  // AND_Gate
  and and_3 (and_3_out, ~status[1], status[0], jump);  // AND_Gate
  and and_4 (and_4_out, status[1], ~status[0], ~jump);  // AND_Gate
  and and_5 (and_5_out, status[1], ~status[0], jump);  // AND_Gate
  and and_6 (and_6_out, status[1], status[0], jump);
  or or_1 (next_status[0], and_1_out, and_2_out);
  or or_2 (next_status[1], and_3_out, and_4_out, and_5_out, and_6_out);
endmodule

module \单级中断  (
);

  wire and_2_out, and_3_out, and_4_out, and_5_out, and_6_out, and_8_out, and_10_out, and_11_out, and_12_out,
       BGTZ, CLK, comparator_1_eq, comparator_2_eq, d_ff_1_q, d_ff_2_q, d_ff_3_q, d_ff_4_q, decoder_1_out1,
       decoder_1_out2, decoder_1_out3, dk, equal, eret, Go, IE_q, IR, IR1, IR1_q, IR2, IR2_q, IR3, IR3_q,
       JAL, LHU, not_1_out, not_2_out, not_3_out, not_4_out, or_4_out, or_5_out, or_6_out, or_7_out,
       or_8_out, RST, rst1, rst2, rst3, SignedExt, SRAV, stop, syscall, W1, W2, W3, \中断请求 ,
       \硬布线控制器_1_alu_src , \硬布线控制器_1_beq , \硬布线控制器_1_bne , \硬布线控制器_1_memtoreg , \硬布线控制器_1_memwrite ,
       \硬布线控制器_1_regdst , \硬布线控制器_1_regwrite ;
  wire [1:0] priority_encoder_1_out, register_2_q;
  wire [2:0] \硬布线控制器_1_jr ;
  wire [3:0] \硬布线控制器_1_alu_op ;
  wire [4:0] multiplexer_4_out, multiplexer_5_out, multiplexer_7_out, multiplexer_8_out, multiplexer_13_out;
  wire [5:0] rom_1_data, rom_1_data_2;
  wire [15:0] multiplexer_16_out, multiplexer_17_out, multiplexer_17_out_2, \总周期数 , \无条件分支数 , \条件分支成功数 ;
  wire [25:6] rom_1_data_3;
  wire [31:0] a0, adder_1_out, adder_2_out, bit_extender_1_out, bit_extender_2_out, epc, LedData,
       mips_regifile_1_r2, multiplexer_1_out, multiplexer_2_out, multiplexer_3_out, multiplexer_6_out,
       multiplexer_10_out, multiplexer_11_out, multiplexer_12_out, multiplexer_15_out, pc, ram_1_data,
       result, shifter_1_out, \中断入口 ;

  Button \u_总复位  (.out(RST));
  Button _1 (.out(IR1));
  Button _2 (.out(IR2));
  Button _3 (.out(IR3));
  Button \u_继续运行  (.out(Go));
  LED led_1 (.in(W1));
  LED led_2 (.in(W2));
  LED led_3 (.in(W3));
  Multiplexer #(.select(3), .width(32), .enable("false")) multiplexer_1 (
    .in0(adder_1_out), .in1({32{1'b0}}), .in2({pc[31:28], rom_1_data_3, rom_1_data_2, 2'b00}), .in3(a0),
    .in4(adder_2_out), .in5({32{1'b0}}), .in6({32{1'b0}}), .in7({32{1'b0}}), .out(multiplexer_1_out),
    .sel(\硬布线控制器_1_jr ));
  Hex_Digit_Display hex_digit_display_1 (.value(LedData[31:28]));  // open: dp
  Multiplexer #(.width(32), .enable("false")) multiplexer_2 (
    .in0(multiplexer_1_out), .in1(\中断入口 ), .out(multiplexer_2_out), .sel(\中断请求 ));
  Multiplexer #(.width(32), .enable("false")) multiplexer_3 (
    .in0(multiplexer_2_out), .in1(epc), .out(multiplexer_3_out), .sel(eret));
  Hex_Digit_Display hex_digit_display_2 (.value(LedData[27:24]));  // open: dp
  Hex_Digit_Display hex_digit_display_3 (.value(LedData[23:20]));  // open: dp
  D_Flip_Flop d_ff_1 (.clk(IR1), .D(1'b1), .Q(d_ff_1_q), .reset(IR1_q));  // open: Qn, preset, en
  or or_1 (W1, IR1_q, d_ff_1_q);
  D_Flip_Flop d_ff_2 (.clk(IR2), .D(1'b1), .Q(d_ff_2_q), .reset(IR2_q));  // open: Qn, preset, en
  or or_2 (W2, IR2_q, d_ff_2_q);
  D_Flip_Flop d_ff_3 (.clk(IR3), .D(1'b1), .Q(d_ff_3_q), .reset(IR3_q));  // open: Qn, preset, en
  or or_3 (W3, IR3_q, d_ff_3_q);
  Hex_Digit_Display hex_digit_display_4 (.value(LedData[19:16]));  // open: dp
  Hex_Digit_Display hex_digit_display_5 (.value(LedData[15:12]));  // open: dp
  Comparator #(.width(6)) comparator_1 (.a(rom_1_data), .b(6'b010000), .eq(comparator_1_eq));  // open: gt, lt
  Comparator #(.width(6)) comparator_2 (.a(rom_1_data_2), .b(6'b011000), .eq(comparator_2_eq));  // open: gt, lt
  Register #(.width(32)) u_PC (.D(multiplexer_3_out), .en(stop), .Q(pc), .clk(CLK), .clr(RST));
  Hex_Digit_Display hex_digit_display_6 (.value(LedData[11:8]));  // open: dp
  Hex_Digit_Display hex_digit_display_7 (.value(LedData[7:4]));  // open: dp
  Clock clock_1 (.out(CLK));
  and and_1 (eret, comparator_1_eq, comparator_2_eq);
  Adder #(.width(32)) adder_1 (.a(pc), .b(32'h4), .out(adder_1_out));  // open: cin, cout
  Register #(.width(32)) register_1 (.D(a0), .en(and_2_out), .Q(LedData), .clk(CLK), .clr(RST));
  and and_2 (and_2_out, syscall, equal);
  or or_4 (or_4_out, d_ff_1_q, IR1_q);
  or or_5 (or_5_out, d_ff_2_q, IR2_q);
  or or_6 (or_6_out, d_ff_3_q, IR3_q);
  Hex_Digit_Display hex_digit_display_8 (.value(LedData[3:0]));  // open: dp
  Counter #(.width(16), .max('hffff)) counter_1 (
    .count(\硬布线控制器_1_jr [1]), .Q(\无条件分支数 ), .clk(CLK), .clr(RST));  // open: load, D, carry
  ROM #(.addrWidth(10), .dataWidth(32)) rom_1 (
    .addr(pc[11:2]), .data({rom_1_data, rom_1_data_3, rom_1_data_2}));  // open: sel
  and and_3 (and_3_out, or_4_out, not_1_out);
  not not_1 (not_1_out, rst1);
  and and_4 (and_4_out, or_5_out, not_2_out);
  not not_2 (not_2_out, rst2);
  and and_5 (and_5_out, or_6_out, not_3_out);
  not not_3 (not_3_out, rst3);
  D_Flip_Flop u_IR1 (.clk(CLK), .D(and_3_out), .Q(IR1_q));  // open: Qn, preset, en, reset
  D_Flip_Flop u_IR2 (.clk(CLK), .D(and_4_out), .Q(IR2_q));  // open: Qn, preset, en, reset
  D_Flip_Flop u_IR3 (.clk(CLK), .D(and_5_out), .Q(IR3_q));  // open: Qn, preset, en, reset
  // Probe on \总周期数 
  // Probe on \无条件分支数 
  // Probe on \条件分支成功数 
  \硬布线控制器  \u_硬布线控制器_1  (
    .Func(rom_1_data_2), .OP(rom_1_data), .ALU_OP(\硬布线控制器_1_alu_op ), .MemToReg(\硬布线控制器_1_memtoreg ),
    .MemWrite(\硬布线控制器_1_memwrite ), .ALU_SRC(\硬布线控制器_1_alu_src ), .RegWrite(\硬布线控制器_1_regwrite ),
    .SysCALL(syscall), .SignedExt(SignedExt), .RegDst(\硬布线控制器_1_regdst ), .JR(\硬布线控制器_1_jr [0]),
    .JMP(\硬布线控制器_1_jr [1]), .Beq(\硬布线控制器_1_beq ), .JAL(JAL), .Bne(\硬布线控制器_1_bne ), .SRAV(SRAV), .LHU(LHU),
    .BGTZ(BGTZ));
  Multiplexer #(.width(5), .enable("false")) multiplexer_4 (
    .in0(rom_1_data_3[25:21]), .in1(5'b00100), .out(multiplexer_4_out), .sel(syscall));
  Multiplexer #(.width(5), .enable("false")) multiplexer_5 (
    .in0(rom_1_data_3[20:16]), .in1(5'b00010), .out(multiplexer_5_out), .sel(syscall));
  Multiplexer #(.width(32), .enable("false")) multiplexer_6 (
    .in0(multiplexer_15_out), .in1(adder_1_out), .out(multiplexer_6_out), .sel(JAL));
  and and_6 (and_6_out, syscall, ~equal);  // AND_Gate
  Multiplexer #(.width(5), .enable("false")) multiplexer_7 (
    .in0(rom_1_data_3[20:16]), .in1(rom_1_data_3[15:11]), .out(multiplexer_7_out), .sel(\硬布线控制器_1_regdst ));
  Multiplexer #(.width(5), .enable("false")) multiplexer_8 (
    .in0(multiplexer_7_out), .in1({5{1'b1}}), .out(multiplexer_8_out), .sel(JAL));
  assign bit_extender_1_out = {{16{1'b0}}, {rom_1_data_3[15:6], rom_1_data_2}};  // Bit_Extender bit_extender_1
  assign bit_extender_2_out = {{16{rom_1_data_3[15]}}, {rom_1_data_3[15:6], rom_1_data_2}};  // Bit_Extender bit_extender_2
  Multiplexer #(.enable("false")) multiplexer_9 (.in0(1'b1), .in1(Go), .out(stop), .sel(and_6_out));
  Priority_Encoder #(.select(2)) priority_encoder_1 (
    .in0(1'b0), .in1(IR1_q), .in2(IR2_q), .in3(IR3_q), .out(priority_encoder_1_out), .gs(IR));  // open: en_out, en_in
  Multiplexer #(.width(32), .enable("false")) multiplexer_10 (
    .in0(bit_extender_1_out), .in1(bit_extender_2_out), .out(multiplexer_10_out), .sel(SignedExt));
  Counter #(.width(16), .max('hffff)) counter_2 (
    .count(stop), .Q(\总周期数 ), .clk(CLK), .clr(RST));  // open: load, D, carry
  or or_7 (or_7_out, ~IE_q, eret);  // OR_Gate
  and and_7 (dk, ~eret, \中断请求 );  // AND_Gate
  or or_8 (or_8_out, eret, \中断请求 );
  MIPS_Regifile mips_regifile_1 (
    .Din(multiplexer_6_out), .Clk(CLK), .R1(a0), .R2(mips_regifile_1_r2), .WE(\硬布线控制器_1_regwrite ),
    .W_num(multiplexer_8_out), .R1_num(multiplexer_4_out), .R2_num(multiplexer_5_out));
  Register #(.width(1)) IE (.D(1'b1), .en(or_7_out), .Q(IE_q), .clk(CLK), .clr(and_8_out));
  and and_8 (and_8_out, ~eret, d_ff_4_q);  // AND_Gate
  D_Flip_Flop d_ff_4 (.clk(CLK), .D(dk), .Q(d_ff_4_q), .en(or_8_out));  // open: Qn, preset, reset
  Register #(.width(32)) u_EPC (.D(pc), .en(dk), .Q(epc), .clk(CLK));  // open: clr
  Multiplexer #(.width(32), .enable("false")) multiplexer_11 (
    .in0(a0), .in1(32'h22), .out(multiplexer_11_out), .sel(syscall));
  Multiplexer #(.width(32), .enable("false")) multiplexer_12 (
    .in0(mips_regifile_1_r2), .in1(multiplexer_10_out), .out(multiplexer_12_out), .sel(\硬布线控制器_1_alu_src ));
  Multiplexer #(.width(5), .enable("false")) multiplexer_13 (
    .in0(rom_1_data_3[10:6]), .in1(a0[4:0]), .out(multiplexer_13_out), .sel(SRAV));
  Shifter #(.width(32)) shifter_1 (.in(bit_extender_2_out), .\dist (5'b00010), .out(shifter_1_out));
  Multiplexer #(.select(2), .width(32), .enable("false")) multiplexer_14 (
    .in1(32'h4), .in2(32'hc8), .in3(32'h18c), .out(\中断入口 ), .sel(priority_encoder_1_out));  // open: in0
  and and_9 (\中断请求 , IR, IE_q);
  MIPS_ALU mips_alu_1 (
    .X(multiplexer_11_out), .Y(multiplexer_12_out), .AluOP(\硬布线控制器_1_alu_op ), .Equal(equal),
    .Result(result), .shamt(multiplexer_13_out));  // open: Result_2
  Adder #(.width(32)) adder_2 (.a(shifter_1_out), .b(adder_1_out), .out(adder_2_out));  // open: cin, cout
  Decoder #(.select(2), .enable("false")) decoder_1 (
    .out1(decoder_1_out1), .out2(decoder_1_out2), .out3(decoder_1_out3), .sel(register_2_q));  // open: out0
  Register #(.width(2)) register_2 (.D(priority_encoder_1_out), .en(dk), .Q(register_2_q), .clk(CLK));  // open: clr
  and and_10 (and_10_out, \硬布线控制器_1_beq , equal);
  and and_11 (and_11_out, ~equal, \硬布线控制器_1_bne );  // AND_Gate
  and and_12 (and_12_out, ~result[0], ~equal, BGTZ);  // AND_Gate
  Multiplexer #(.width(32), .enable("false")) multiplexer_15 (
    .in0({multiplexer_17_out_2, multiplexer_17_out}), .in1({{16{1'b0}}, multiplexer_16_out}),
    .out(multiplexer_15_out), .sel(LHU));
  or or_9 (\硬布线控制器_1_jr [2], and_10_out, and_11_out, and_12_out);
  not not_4 (not_4_out, \硬布线控制器_1_memwrite );
  and and_13 (rst1, decoder_1_out1, eret);
  and and_14 (rst2, decoder_1_out2, eret);
  and and_15 (rst3, decoder_1_out3, eret);
  RAM #(.addrWidth(10), .dataWidth(32), .bus("separate")) ram_1 (
    .addr(result[11:2]), .din(mips_regifile_1_r2), .data(ram_1_data), .str(\硬布线控制器_1_memwrite ), .clk(CLK),
    .ld(not_4_out), .clr(RST));  // open: sel
  Multiplexer #(.width(16), .enable("false")) multiplexer_16 (
    .in0(multiplexer_17_out), .in1(multiplexer_17_out_2), .out(multiplexer_16_out), .sel(result[1]));
  Counter #(.width(16), .max('hffff)) counter_3 (
    .count(\硬布线控制器_1_jr [2]), .Q(\条件分支成功数 ), .clk(CLK), .clr(RST));  // open: load, D, carry
  Multiplexer #(.width(32), .enable("false")) multiplexer_17 (
    .in0(result), .in1(ram_1_data), .out({multiplexer_17_out_2, multiplexer_17_out}),
    .sel(\硬布线控制器_1_memtoreg ));

  // Notes on the sheet:
  //   中断源
  //   中断等待指示
  //   数码管输出应该用寄存器锁存，否则显示数据只能一闪而过
  //   数码管输出
  //   指令存储器
  //   指令字
  //   contents of rom_1 (hex, n*v repeats v):
  //   8100094 23bdfffc afa20000 23bdfffc afa40000 23bdfffc afb00000 23bdfffc afb10000 23bdfffc afb20000
  //   23bdfffc afb30000 23bdfffc afb40000 23bdfffc afb50000 23bdfffc afb60000 20160001 20140006 20150001
  //   168020 108100 2149825 132020 20020022 c 1600fffa 295a022 1680fff7 8fb60000 23bd0004 8fb50000
  //   23bd0004 8fb40000 23bd0004 8fb30000 23bd0004 8fb20000 23bd0004 8fb10000 23bd0004 8fb00000 23bd0004
  //   8fa40000 23bd0004 8fa20000 23bd0004 42000018 23bdfffc afa20000 23bdfffc afa40000 23bdfffc afb00000
  //   23bdfffc afb10000 23bdfffc afb20000 23bdfffc afb30000 23bdfffc afb40000 23bdfffc afb50000 23bdfffc
  //   afb60000 20160002 20140006 20150001 168020 108100 2149825 132020 20020022 c 1600fffa 295a022
  //   1680fff7 8fb60000 23bd0004 8fb50000 23bd0004 8fb40000 23bd0004 8fb30000 23bd0004 8fb20000 23bd0004
  //   8fb10000 23bd0004 8fb00000 23bd0004 8fa40000 23bd0004 8fa20000 23bd0004 42000018 23bdfffc afa20000
  //   23bdfffc afa40000 23bdfffc afb00000 23bdfffc afb10000 23bdfffc afb20000 23bdfffc afb30000 23bdfffc
  //   afb40000 23bdfffc afb50000 23bdfffc afb60000 20160003 20140006 20150001 168020 108100 2149825 132020
  //   20020022 c 1600fffa 295a022 1680fff7 8fb60000 23bd0004 8fb50000 23bd0004 8fb40000 23bd0004 8fb30000
  //   23bd0004 8fb20000 23bd0004 8fb10000 23bd0004 8fb00000 23bd0004 8fa40000 23bd0004 8fa20000 23bd0004
  //   42000018 20110200 20020022 112020 c 2231ffff 1620fffc 4*0 2002000a c 2002000a c
  //   shamt
  //   imm
  //   OP
  //   Func
  //   rs
  //   rt
  //   rd
  //   Beq
  //   JMP
  //   JR
  //   Bne
  //   OP
  //   JAL
  //   Func
  //   Syscall
  //   MemToReg
  //   MemWrite
  //   AluOP
  //   AluSrcB
  //   RegWrite
  //   RegDst
endmodule
module \流水中断  (
);

  wire _1, _2, _3, and_1_out, and_2_out, and_3_out, and_4_out, and_5_out, and_6_out, and_7_out, and_10_out,
       and_11_out, and_16_out, and_17_out, and_18_out, CLK, comparator_1_eq, comparator_2_eq,
       comparator_3_eq, comparator_4_eq, comparator_5_eq, d_ff_1_q, d_ff_2_q, d_ff_3_q, d_ff_4_q,
       decoder_1_out1, decoder_1_out2, decoder_1_out3, dk, equal5, eret, EX_LW, ex_mem_1_equal_2, Go, IE_q,
       IR, IR1, IR2, IR3, jal3, jal4, jal5, lhu, MEM_RegWrite, mips_alu_1_equal, not_1_out, not_2_out,
       not_3_out, not_4_out, not_5_out, or_4_out, or_5_out, or_6_out, or_7_out, or_8_out, or_9_out,
       or_10_out, or_11_out, or_13_out, or_15_out, regdst3, regdst4, regdst5, regwrite5, RST, rst1, rst2,
       rst3, SignedExt, srav, stall, stop, syscall3, syscall5, W1, W2, W3, \中断请求 ;
  wire [1:0] priority_encoder_1_out, R1_sel, R2_sel, register_2_q;
  wire [2:2] or_14_out;
  wire [3:0] counter_2_q, \硬布线控制器_1_alu_op ;
  wire [4:0] EX_R1_num, EX_R2_num, EX_WriteReg_num, id_ex_1_shamt_2, ID_R1_num, ID_R2_num, MEM_WriteReg_num,
       multiplexer_7_out, multiplexer_15_out, multiplexer_18_out, multiplexer_19_out, rd4, rd5, rt4, rt5,
       WB_WriteReg_num;
  wire [5:0] func2, func3, op2;
  wire [15:0] \LoadUse次数 , multiplexer_25_out, \总周期数 , \插入气泡数 , \无条件分支数 , \条件分支成功数 ;
  wire [17:0] mem_wb_1_control_2;
  wire [18:0] ex_mem_1_control_2, id_ex_1_control_2, \硬布线控制器_1_jmp ;
  wire [25:6] if_id_1_instruction_2;
  wire [31:0] a3, a5, adder_1_out, adder_2_out, alu4, bit_extender_1_out, bit_extender_2_out, epc,
       ex_mem_1_instruction_2, ex_mem_1_r1_2, ex_mem_1_r2_2, EX_PC, id_ex_1_imm_2, id_ex_1_pc4_2,
       id_ex_1_r1_2, id_ex_1_r2_2, id_ex_1_signimm_2, ID_PC, if_id_1_pc4_2, IF_PC, LedData, MEM_PC,
       mem_wb_1_instruction_2, mem_wb_1_md_2, mips_alu_1_result, mips_regifile_1_r1, mips_regifile_1_r2,
       multiplexer_1_out, multiplexer_2_out, multiplexer_3_out, multiplexer_9_out, multiplexer_12_out,
       multiplexer_13_out, multiplexer_14_out, multiplexer_22_out, multiplexer_23_out, multiplexer_24_out,
       ram_1_data, result5, rom_1_data, shifter_1_out, WB_PC, \中断入口 ;
  wire [31:6] instruction3;

  Button \u_总复位  (.out(RST));
  Button u__1 (.out(IR1));
  Button u__2 (.out(IR2));
  Button u__3 (.out(IR3));
  Button \u_继续运行  (.out(Go));
  LED led_1 (.in(W1));
  LED led_2 (.in(W2));
  LED led_3 (.in(W3));
  Hex_Digit_Display hex_digit_display_1 (.value(LedData[31:28]));  // open: dp
  Multiplexer #(.select(3), .width(32), .enable("false")) multiplexer_1 (
    .in0(adder_1_out), .in1({32{1'b0}}), .in2({EX_PC[31:28], instruction3[25:6], func3, 2'b00}), .in3(a3),
    .in4(adder_2_out), .in5({32{1'b0}}), .in6({32{1'b0}}), .in7({32{1'b0}}), .out(multiplexer_1_out),
    .sel({or_14_out[2], id_ex_1_control_2[0], id_ex_1_control_2[1]}));
  and and_1 (and_1_out, stop, ~stall);  // AND_Gate
  Hex_Digit_Display hex_digit_display_2 (.value(LedData[27:24]));  // open: dp
  Hex_Digit_Display hex_digit_display_3 (.value(LedData[23:20]));  // open: dp
  Multiplexer #(.width(32), .enable("false")) multiplexer_2 (
    .in0(multiplexer_1_out), .in1(\中断入口 ), .out(multiplexer_2_out), .sel(\中断请求 ));
  Register #(.width(32)) PC (.D(multiplexer_3_out), .en(and_1_out), .Q(IF_PC), .clk(CLK), .clr(RST));
  Hex_Digit_Display hex_digit_display_4 (.value(LedData[19:16]));  // open: dp
  Hex_Digit_Display hex_digit_display_5 (.value(LedData[15:12]));  // open: dp
  Multiplexer #(.width(32), .enable("false")) multiplexer_3 (
    .in0(multiplexer_2_out), .in1(epc), .out(multiplexer_3_out), .sel(eret));
  Adder #(.width(32)) adder_1 (.a(IF_PC), .b(32'h4), .out(adder_1_out));  // open: cin, cout
  and and_2 (and_2_out, syscall5, equal5);
  or or_1 (W1, _1, d_ff_1_q);
  or or_2 (W2, _2, d_ff_2_q);
  or or_3 (W3, _3, d_ff_3_q);
  Hex_Digit_Display hex_digit_display_6 (.value(LedData[7:4]));  // open: dp
  Hex_Digit_Display hex_digit_display_7 (.value(LedData[11:8]));  // open: dp
  Clock clock_1 (.out(CLK));
  ROM #(.addrWidth(10), .dataWidth(32)) rom_1 (.addr(IF_PC[11:2]), .data(rom_1_data));  // open: sel
  Register #(.width(32)) register_1 (.D(a5), .en(and_2_out), .Q(LedData), .clk(CLK), .clr(RST));
  D_Flip_Flop d_ff_1 (.clk(IR1), .D(1'b1), .Q(d_ff_1_q), .reset(_1));  // open: Qn, preset, en
  D_Flip_Flop d_ff_2 (.clk(IR2), .D(1'b1), .Q(d_ff_2_q), .reset(_2));  // open: Qn, preset, en
  D_Flip_Flop d_ff_3 (.clk(IR3), .D(1'b1), .Q(d_ff_3_q), .reset(_3));  // open: Qn, preset, en
  Hex_Digit_Display hex_digit_display_8 (.value(LedData[3:0]));  // open: dp
  or or_4 (or_4_out, eret, RST, or_13_out, \中断请求 );
  IF_ID if_id_1 (
    .instruction(rom_1_data), .pc4(adder_1_out), .instruction_2({op2, if_id_1_instruction_2, func2}),
    .pc4_2(if_id_1_pc4_2), .rst(or_4_out), .clk(CLK), .stop(and_1_out), .pc(IF_PC), .pc_2(ID_PC));  // open: hit, hit_2, jump_att, jump_att_2, hit_pos, hit_pos_2
  load_use load_use_1 (
    .ID_OP(op2), .EX_WriteReg_num(EX_WriteReg_num), .EX_LW(EX_LW), .ID_R1_num(ID_R1_num), .STALL(stall),
    .ID_Func(func2), .ID_R2_num(ID_R2_num));
  or or_5 (or_5_out, d_ff_1_q, _1);
  or or_6 (or_6_out, d_ff_2_q, _2);
  or or_7 (or_7_out, d_ff_3_q, _3);
  not not_1 (not_1_out, rst1);
  not not_2 (not_2_out, rst2);
  not not_3 (not_3_out, rst3);
  // Probe on \总周期数 
  // Probe on \无条件分支数 
  // Probe on \条件分支成功数 
  // Probe on \插入气泡数 
  // Probe on \LoadUse次数 
  Multiplexer #(.enable("false")) multiplexer_4 (.in0(1'b1), .in1(Go), .out(stop), .sel(and_3_out));
  and and_3 (and_3_out, syscall5, ~equal5);  // AND_Gate
  D_Flip_Flop u_IR1 (.clk(CLK), .D(and_4_out), .Q(_1));  // open: Qn, preset, en, reset
  and and_4 (and_4_out, or_5_out, not_1_out);
  D_Flip_Flop u_IR2 (.clk(CLK), .D(and_5_out), .Q(_2));  // open: Qn, preset, en, reset
  and and_5 (and_5_out, or_6_out, not_2_out);
  D_Flip_Flop u_IR3 (.clk(CLK), .D(and_6_out), .Q(_3));  // open: Qn, preset, en, reset
  and and_6 (and_6_out, or_7_out, not_3_out);
  or or_8 (or_8_out, IR1, IR2, IR3);
  // Probe on IF_PC[11:0]
  \硬布线控制器  \u_硬布线控制器_1  (
    .Func(func2), .OP(op2), .ALU_OP(\硬布线控制器_1_alu_op ), .MemToReg(\硬布线控制器_1_jmp [5]),
    .MemWrite(\硬布线控制器_1_jmp [6]), .ALU_SRC(\硬布线控制器_1_jmp [11]), .RegWrite(\硬布线控制器_1_jmp [12]),
    .SysCALL(\硬布线控制器_1_jmp [16]), .SignedExt(SignedExt), .RegDst(\硬布线控制器_1_jmp [14]), .JR(\硬布线控制器_1_jmp [1]),
    .JMP(\硬布线控制器_1_jmp [0]), .Beq(\硬布线控制器_1_jmp [3]), .JAL(\硬布线控制器_1_jmp [13]), .Bne(\硬布线控制器_1_jmp [4]),
    .SRAV(\硬布线控制器_1_jmp [15]), .LHU(\硬布线控制器_1_jmp [18]), .BGTZ(\硬布线控制器_1_jmp [17]));
  Multiplexer #(.width(5), .enable("false")) multiplexer_5 (
    .in0(if_id_1_instruction_2[25:21]), .in1(5'b00100), .out(ID_R1_num), .sel(\硬布线控制器_1_jmp [16]));
  Multiplexer #(.width(5), .enable("false")) multiplexer_6 (
    .in0(if_id_1_instruction_2[20:16]), .in1(5'b00010), .out(ID_R2_num), .sel(\硬布线控制器_1_jmp [16]));
  Counter #(.width(16), .max('hffff)) counter_1 (
    .count(stop), .Q(\总周期数 ), .clk(CLK), .clr(RST));  // open: load, D, carry
  Counter #(.width(4), .max('hf)) counter_2 (
    .count(1'b1), .Q(counter_2_q), .clk(or_8_out), .clr(and_7_out));  // open: load, D, carry
  and and_7 (and_7_out, ~_1, ~_2, ~_3);  // AND_Gate
  // Probe on ID_PC[11:0]
  Multiplexer #(.width(5), .enable("false")) multiplexer_7 (
    .in0(rt5), .in1(rd5), .out(multiplexer_7_out), .sel(regdst5));
  Multiplexer #(.width(5), .enable("false")) multiplexer_8 (
    .in0(multiplexer_7_out), .in1({5{1'b1}}), .out(WB_WriteReg_num), .sel(jal5));
  assign bit_extender_1_out = {{16{1'b0}}, {if_id_1_instruction_2[15:6], func2}};  // Bit_Extender bit_extender_1
  assign bit_extender_2_out = {{16{if_id_1_instruction_2[15]}}, {if_id_1_instruction_2[15:6], func2}};  // Bit_Extender bit_extender_2
  Comparator #(.width(6)) comparator_1 (.a(op2), .b(6'b010000), .eq(comparator_1_eq));  // open: gt, lt
  Comparator #(.width(6)) comparator_2 (.a(func2), .b(6'b011000), .eq(comparator_2_eq));  // open: gt, lt
  Comparator #(.width(4)) comparator_3 (.a(counter_2_q), .b(4'b0000), .eq(comparator_3_eq));  // open: gt, lt
  // Probe on MEM_PC[11:0]
  // Probe on EX_PC[11:0]
  not not_4 (not_4_out, CLK);
  Multiplexer #(.width(32), .enable("false")) multiplexer_9 (
    .in0(bit_extender_1_out), .in1(bit_extender_2_out), .out(multiplexer_9_out), .sel(SignedExt));
  and and_8 (eret, comparator_1_eq, comparator_2_eq);
  Priority_Encoder #(.select(2)) priority_encoder_1 (
    .in0(1'b0), .in1(_1), .in2(_2), .in3(_3), .out(priority_encoder_1_out), .gs(IR));  // open: en_out, en_in
  and and_9 (dk, ~eret, \中断请求 );  // AND_Gate
  or or_9 (or_9_out, eret, \中断请求 );
  and and_10 (and_10_out, dk, comparator_3_eq);
  // Probe on WB_PC[11:0]
  MIPS_Regifile mips_regifile_1 (
    .Din(multiplexer_22_out), .Clk(not_4_out), .R1(mips_regifile_1_r1), .R2(mips_regifile_1_r2),
    .WE(regwrite5), .W_num(WB_WriteReg_num), .R1_num(ID_R1_num), .R2_num(ID_R2_num));
  or or_10 (or_10_out, ~IE_q, eret);  // OR_Gate
  or or_11 (or_11_out, \中断请求 , RST, stall, or_13_out);
  ID_EX id_ex_1 (
    .control({\硬布线控制器_1_jmp [18:11], \硬布线控制器_1_alu_op , \硬布线控制器_1_jmp [6:3], SignedExt, \硬布线控制器_1_jmp [1:0]}),
    .instruction({op2, if_id_1_instruction_2, func2}), .pc4(if_id_1_pc4_2), .R1(mips_regifile_1_r1),
    .R2(mips_regifile_1_r2), .imm(multiplexer_9_out),
    .control_2({id_ex_1_control_2[18:17], syscall3, srav, regdst3, jal3, id_ex_1_control_2[12:0]}),
    .instruction_2({instruction3, func3}), .pc4_2(id_ex_1_pc4_2), .R1_2(id_ex_1_r1_2), .R2_2(id_ex_1_r2_2),
    .imm_2(id_ex_1_imm_2), .rst(or_11_out), .stop(stop), .clk(CLK), .shamt(if_id_1_instruction_2[10:6]),
    .shamt_2(id_ex_1_shamt_2), .signimm(bit_extender_2_out), .signimm_2(id_ex_1_signimm_2), .pc(ID_PC),
    .pc_2(EX_PC));  // open: hit, hit_2, jump_att, jump_att_2, hit_pos, hit_pos_2
  \重定向判断  \u_重定向判断_1  (
    .EX_OP(instruction3[31:26]), .WB_WriteReg_num(WB_WriteReg_num), .WB_RegWrite(regwrite5), .R1_sel(R1_sel),
    .MEM_WriteReg_num(MEM_WriteReg_num), .MEM_RegWrite(MEM_RegWrite), .R2_sel(R2_sel), .EX_Func(func3),
    .EX_R1_num(EX_R1_num), .EX_R2_num(EX_R2_num));
  Multiplexer #(.select(2), .width(32), .enable("false")) multiplexer_10 (
    .in1(32'h4), .in2(32'hc8), .in3(32'h18c), .out(\中断入口 ), .sel(priority_encoder_1_out));  // open: in0
  Register #(.width(1)) IE (.D(1'b1), .en(or_10_out), .Q(IE_q), .clk(CLK), .clr(and_11_out));
  and and_11 (and_11_out, ~eret, d_ff_4_q);  // AND_Gate
  D_Flip_Flop d_ff_4 (.clk(CLK), .D(dk), .Q(d_ff_4_q), .en(or_9_out));  // open: Qn, preset, reset
  Register #(.width(32)) u_EPC (.D(EX_PC), .en(and_10_out), .Q(epc), .clk(CLK));  // open: clr
  and and_12 (\中断请求 , IR, IE_q);
  Comparator #(.width(6)) comparator_4 (.a(instruction3[31:26]), .b(6'b100011), .eq(comparator_4_eq));  // open: gt, lt
  Comparator #(.width(6)) comparator_5 (.a(instruction3[31:26]), .b(6'b100101), .eq(comparator_5_eq));  // open: gt, lt
  Decoder #(.select(2), .enable("false")) decoder_1 (
    .out1(decoder_1_out1), .out2(decoder_1_out2), .out3(decoder_1_out3), .sel(register_2_q));  // open: out0
  Register #(.width(2)) register_2 (.D(priority_encoder_1_out), .en(dk), .Q(register_2_q), .clk(CLK));  // open: clr
  Counter #(.width(16), .max('hffff)) counter_3 (
    .count(stall), .Q(\LoadUse次数 ), .clk(CLK), .clr(RST));  // open: load, D, carry
  Counter #(.width(16), .max('hffff)) counter_4 (
    .count(stall), .Q(\插入气泡数 ), .clk(CLK), .clr(RST));  // open: load, D, carry
  Multiplexer #(.select(2), .width(32), .enable("false")) multiplexer_11 (
    .in0(id_ex_1_r1_2), .in1(multiplexer_22_out), .in2(alu4), .in3(alu4), .out(a3), .sel(R1_sel));
  Multiplexer #(.select(2), .width(32), .enable("false")) multiplexer_12 (
    .in0(id_ex_1_r2_2), .in1(multiplexer_22_out), .in2(alu4), .in3(alu4), .out(multiplexer_12_out),
    .sel(R2_sel));
  or or_12 (EX_LW, comparator_4_eq, comparator_5_eq);
  and and_13 (rst1, decoder_1_out1, eret);
  and and_14 (rst2, decoder_1_out2, eret);
  and and_15 (rst3, decoder_1_out3, eret);
  or or_13 (or_13_out, id_ex_1_control_2[0], or_14_out[2]);
  Multiplexer #(.width(32), .enable("false")) multiplexer_13 (
    .in0(multiplexer_12_out), .in1(id_ex_1_imm_2), .out(multiplexer_13_out), .sel(id_ex_1_control_2[11]));
  Shifter #(.width(32)) shifter_1 (.in(id_ex_1_signimm_2), .\dist (5'b00010), .out(shifter_1_out));
  Multiplexer #(.width(32), .enable("false")) multiplexer_14 (
    .in0(a3), .in1(32'h22), .out(multiplexer_14_out), .sel(syscall3));
  Multiplexer #(.width(5), .enable("false")) multiplexer_15 (
    .in0(id_ex_1_shamt_2), .in1(a3[4:0]), .out(multiplexer_15_out), .sel(srav));
  and and_16 (and_16_out, id_ex_1_control_2[3], mips_alu_1_equal);
  and and_17 (and_17_out, id_ex_1_control_2[4], ~mips_alu_1_equal);  // AND_Gate
  and and_18 (and_18_out, id_ex_1_control_2[17], ~mips_alu_1_equal, ~mips_alu_1_result[0]);  // AND_Gate
  MIPS_ALU mips_alu_1 (
    .X(multiplexer_14_out), .Y(multiplexer_13_out), .AluOP(id_ex_1_control_2[10:7]),
    .Equal(mips_alu_1_equal), .Result(mips_alu_1_result), .shamt(multiplexer_15_out));  // open: Result_2
  Adder #(.width(32)) adder_2 (.a(id_ex_1_pc4_2), .b(shifter_1_out), .out(adder_2_out));  // open: cin, cout
  Multiplexer #(.width(5), .enable("false")) multiplexer_16 (
    .in0(instruction3[25:21]), .in1(5'b00100), .out(EX_R1_num), .sel(syscall3));
  Multiplexer #(.width(5), .enable("false")) multiplexer_17 (
    .in0(instruction3[20:16]), .in1(5'b00010), .out(EX_R2_num), .sel(syscall3));
  or or_14 (or_14_out[2], and_16_out, and_17_out, and_18_out);
  Counter #(.width(16), .max('hffff)) counter_5 (
    .count(id_ex_1_control_2[0]), .Q(\无条件分支数 ), .clk(CLK), .clr(RST));  // open: load, D, carry
  Counter #(.width(16), .max('hffff)) counter_6 (
    .count(or_14_out[2]), .Q(\条件分支成功数 ), .clk(CLK), .clr(RST));  // open: load, D, carry
  or or_15 (or_15_out, RST, \中断请求 );
  EX_MEM ex_mem_1 (
    .control({id_ex_1_control_2[18:17], syscall3, srav, regdst3, jal3, id_ex_1_control_2[12:0]}),
    .instruction({instruction3, func3}), .pc4(id_ex_1_pc4_2), .R2(multiplexer_12_out),
    .alu(mips_alu_1_result),
    .control_2({ex_mem_1_control_2[18:15], regdst4, jal4, MEM_RegWrite, ex_mem_1_control_2[11:0]}),
    .instruction_2({ex_mem_1_instruction_2[31:21], rt4, rd4, ex_mem_1_instruction_2[10:0]}), .pc4_2(MEM_PC),
    .R2_2(ex_mem_1_r2_2), .alu_2(alu4), .rst(or_15_out), .stop(stop), .clk(CLK), .equal(mips_alu_1_equal),
    .equal_2(ex_mem_1_equal_2), .R1(a3), .R1_2(ex_mem_1_r1_2));
  Multiplexer #(.width(5), .enable("false")) multiplexer_18 (
    .in0(rt4), .in1(rd4), .out(multiplexer_18_out), .sel(regdst4));
  Multiplexer #(.width(5), .enable("false")) multiplexer_19 (
    .in0(instruction3[20:16]), .in1(instruction3[15:11]), .out(multiplexer_19_out), .sel(regdst3));
  Multiplexer #(.width(5), .enable("false")) multiplexer_20 (
    .in0(multiplexer_18_out), .in1({5{1'b1}}), .out(MEM_WriteReg_num), .sel(jal4));
  Multiplexer #(.width(5), .enable("false")) multiplexer_21 (
    .in0(multiplexer_19_out), .in1({5{1'b1}}), .out(EX_WriteReg_num), .sel(jal3));
  RAM #(.addrWidth(10), .dataWidth(32), .bus("separate")) ram_1 (
    .addr(alu4[11:2]), .din(ex_mem_1_r2_2), .data(ram_1_data), .str(ex_mem_1_control_2[6]), .clk(CLK),
    .ld(not_5_out), .clr(RST));  // open: sel
  not not_5 (not_5_out, ex_mem_1_control_2[6]);
  MEM_WB mem_wb_1 (
    .control({ex_mem_1_control_2[18:15], regdst4, jal4, MEM_RegWrite, ex_mem_1_control_2[11:0]}),
    .instruction({ex_mem_1_instruction_2[31:21], rt4, rd4, ex_mem_1_instruction_2[10:0]}), .pc4(MEM_PC),
    .md(ram_1_data), .alu(alu4),
    .control_2({lhu, mem_wb_1_control_2[17], syscall5, mem_wb_1_control_2[15], regdst5, jal5, regwrite5, mem_wb_1_control_2[11:0]}),
    .instruction_2({mem_wb_1_instruction_2[31:21], rt5, rd5, mem_wb_1_instruction_2[10:0]}), .pc4_2(WB_PC),
    .md_2(mem_wb_1_md_2), .alu_2(result5), .rst(RST), .stop(stop), .clk(CLK), .equal(ex_mem_1_equal_2),
    .equal_2(equal5), .R1(ex_mem_1_r1_2), .R1_2(a5));
  Multiplexer #(.width(32), .enable("false")) multiplexer_22 (
    .in0(multiplexer_24_out), .in1(WB_PC), .out(multiplexer_22_out), .sel(jal5));
  Multiplexer #(.width(32), .enable("false")) multiplexer_23 (
    .in0(result5), .in1(mem_wb_1_md_2), .out(multiplexer_23_out), .sel(mem_wb_1_control_2[5]));
  Multiplexer #(.width(32), .enable("false")) multiplexer_24 (
    .in0(multiplexer_23_out), .in1({{16{1'b0}}, multiplexer_25_out}), .out(multiplexer_24_out), .sel(lhu));
  Multiplexer #(.width(16), .enable("false")) multiplexer_25 (
    .in0(multiplexer_23_out[15:0]), .in1(multiplexer_23_out[31:16]), .out(multiplexer_25_out),
    .sel(result5[1]));

  // Other names for the same wires on the sheet: instruction3[5:0] = func3; rd3[4:0] = instruction3[15:11];
  //   rt3[4:0] = instruction3[20:16]; rs3[4:0] = instruction3[25:21]; op3[5:0] = instruction3[31:26]

  // Notes on the sheet:
  //   中断源
  //   中断等待指示
  //   数码管输出
  //   指令存储器
  //   contents of rom_1 (hex, n*v repeats v):
  //   8100094 23bdfffc afa20000 23bdfffc afa40000 23bdfffc afb00000 23bdfffc afb10000 23bdfffc afb20000
  //   23bdfffc afb30000 23bdfffc afb40000 23bdfffc afb50000 23bdfffc afb60000 20160001 20140006 20150001
  //   168020 108100 2149825 132020 20020022 c 1600fffa 295a022 1680fff7 8fb60000 23bd0004 8fb50000
  //   23bd0004 8fb40000 23bd0004 8fb30000 23bd0004 8fb20000 23bd0004 8fb10000 23bd0004 8fb00000 23bd0004
  //   8fa40000 23bd0004 8fa20000 23bd0004 42000018 23bdfffc afa20000 23bdfffc afa40000 23bdfffc afb00000
  //   23bdfffc afb10000 23bdfffc afb20000 23bdfffc afb30000 23bdfffc afb40000 23bdfffc afb50000 23bdfffc
  //   afb60000 20160002 20140006 20150001 168020 108100 2149825 132020 20020022 c 1600fffa 295a022
  //   1680fff7 8fb60000 23bd0004 8fb50000 23bd0004 8fb40000 23bd0004 8fb30000 23bd0004 8fb20000 23bd0004
  //   8fb10000 23bd0004 8fb00000 23bd0004 8fa40000 23bd0004 8fa20000 23bd0004 42000018 23bdfffc afa20000
  //   23bdfffc afa40000 23bdfffc afb00000 23bdfffc afb10000 23bdfffc afb20000 23bdfffc afb30000 23bdfffc
  //   afb40000 23bdfffc afb50000 23bdfffc afb60000 20160003 20140006 20150001 168020 108100 2149825 132020
  //   20020022 c 1600fffa 295a022 1680fff7 8fb60000 23bd0004 8fb50000 23bd0004 8fb40000 23bd0004 8fb30000
  //   23bd0004 8fb20000 23bd0004 8fb10000 23bd0004 8fb00000 23bd0004 8fa40000 23bd0004 8fa20000 23bd0004
  //   42000018 20110200 20020022 112020 c 2231ffff 1620fffc 4*0 2002000a c 2002000a c
  //   指令字
  //   OP
  //   Func
  //   rs
  //   rt
  //   rd
  //   shamt
  //   imm
  //   JMP
  //   JR
  //   OP
  //   Func
  //   Beq
  //   Bne
  //   AluOP
  //   AluSrcB
  //   RegWrite
  //   JAL
  //   RegDst
  //   MemToReg
  //   MemWrite
  //   流水调试日志用
  //   lw
  //   lhu
  //   OP
  //   Func
  //   rs
  //   rt
  //   rd
  //   rt
  //   rd
  //   rt
  //   rd
endmodule

module \多级中断  (
);

  wire _1, _2, _3, and_1_out, and_2_out, and_3_out, and_7_out, and_8_out, and_9_out, and_10_out, and_11_out,
       and_12_out, and_13_out, and_14_out, and_18_out, and_19_out, and_20_out, and_21_out, and_22_out,
       and_23_out, and_24_out, BGTZ, CLK, comparator_1_eq, comparator_2_eq, comparator_3_eq, comparator_3_gt,
       comparator_4_eq, comparator_5_eq, comparator_6_eq, comparator_7_eq, comparator_8_eq, comparator_9_eq,
       comparator_10_eq, comparator_11_eq, comparator_11_gt, d_ff_1_q, d_ff_2_q, d_ff_3_q, d_ff_4_qn,
       d_ff_5_qn, d_ff_6_qn, d_ff_7_qn, decoder_1_out1, decoder_1_out2, decoder_1_out3, EPC_c, equal, eret,
       Go, IE_c, IE_q, IR, IR1, IR2, IR3, IR_c, JAL, LHU, mfc0, mtc0, multiplexer_12_out, multiplexer_13_out,
       multiplexer_14_out, multiplexer_15_out, multiplexer_16_out, multiplexer_20_out, not_1_out, not_2_out,
       not_3_out, not_4_out, not_5_out, or_1_out, or_5_out, or_6_out, or_7_out, or_8_out, or_9_out,
       or_10_out, or_11_out, RST, rst1, rst2, rst3, SignedExt, SRAV, stop, syscall, W1, W2, W3, \中断请求 ,
       \初始化_q , \硬布线控制器_1_alu_src , \硬布线控制器_1_beq , \硬布线控制器_1_bne , \硬布线控制器_1_memtoreg , \硬布线控制器_1_memwrite ,
       \硬布线控制器_1_regdst , \硬布线控制器_1_regwrite ;
  wire [1:0] mfc_sel, mtc_sel, priority_encoder_1_out, priority_encoder_2_out;
  wire [2:0] \硬布线控制器_1_jr ;
  wire [3:0] \中断字 , \硬布线控制器_1_alu_op ;
  wire [4:0] multiplexer_4_out, multiplexer_5_out, multiplexer_7_out, multiplexer_8_out, multiplexer_19_out,
       rd, rs;
  wire [5:0] op, rom_1_data;
  wire [15:0] multiplexer_24_out, multiplexer_25_out, multiplexer_25_out_2, \总周期数 , \无条件分支数 , \条件分支成功数 ;
  wire [20:6] rom_1_data_2;
  wire [31:0] a0, adder_1_out, adder_2_out, bit_extender_1_out, bit_extender_2_out, cp0_rw, epc, EPC_write,
       IE, LedData, multiplexer_1_out, multiplexer_2_out, multiplexer_3_out, multiplexer_6_out,
       multiplexer_9_out, multiplexer_11_out, multiplexer_17_out, multiplexer_18_out, multiplexer_21_out,
       multiplexer_23_out, pc, R2, ram_1_data, result, shifter_1_out, \中断入口 , \开中断 ;

  Button \u_总复位  (.out(RST));
  Button u__1 (.out(IR1));
  Button u__2 (.out(IR2));
  Button u__3 (.out(IR3));
  Button \u_继续运行  (.out(Go));
  LED led_1 (.in(W1));
  LED led_2 (.in(W2));
  LED led_3 (.in(W3));
  Multiplexer #(.select(3), .width(32), .enable("false")) multiplexer_1 (
    .in0(adder_1_out), .in1({32{1'b0}}),
    .in2({pc[31:28], rs, rom_1_data_2[20:16], rd, rom_1_data_2[10:6], rom_1_data, 2'b00}), .in3(a0),
    .in4(adder_2_out), .in5({32{1'b0}}), .in6({32{1'b0}}), .in7({32{1'b0}}), .out(multiplexer_1_out),
    .sel(\硬布线控制器_1_jr ));
  Comparator #(.width(5)) comparator_1 (.a(rd), .b(5'b00001), .eq(comparator_1_eq));  // open: gt, lt
  Comparator #(.width(5)) comparator_2 (.a(rd), .b(5'b00010), .eq(comparator_2_eq));  // open: gt, lt
  Comparator #(.width(5)) comparator_3 (.a(rd), .b(5'b00011), .gt(comparator_3_gt), .eq(comparator_3_eq));  // open: lt
  Hex_Digit_Display hex_digit_display_1 (.value(LedData[31:28]));  // open: dp
  Multiplexer #(.width(32), .enable("false")) multiplexer_2 (
    .in0(multiplexer_1_out), .in1(\中断入口 ), .out(multiplexer_2_out), .sel(\中断请求 ));
  Multiplexer #(.width(32), .enable("false")) multiplexer_3 (
    .in0(multiplexer_2_out), .in1(epc), .out(multiplexer_3_out), .sel(eret));
  Comparator #(.width(6)) comparator_4 (.a(op), .b(6'b010000), .eq(comparator_4_eq));  // open: gt, lt
  Comparator #(.width(5)) comparator_5 (.a(rs), .b({5{1'b0}}), .eq(comparator_5_eq));  // open: gt, lt
  Comparator #(.width(5)) comparator_6 (.a(rs), .b(5'b00100), .eq(comparator_6_eq));  // open: gt, lt
  and and_1 (and_1_out, comparator_1_eq, mfc0);
  and and_2 (and_2_out, comparator_2_eq, mfc0);
  and and_3 (and_3_out, comparator_3_eq, mfc0);
  or or_1 (or_1_out, ~mfc0, comparator_3_gt);  // OR_Gate
  Hex_Digit_Display hex_digit_display_2 (.value(LedData[23:20]));  // open: dp
  Hex_Digit_Display hex_digit_display_3 (.value(LedData[27:24]));  // open: dp
  and and_4 (mfc0, comparator_4_eq, comparator_5_eq);
  and and_5 (mtc0, comparator_4_eq, comparator_6_eq);
  D_Flip_Flop d_ff_1 (.clk(IR1), .D(1'b1), .Q(d_ff_1_q), .reset(_1));  // open: Qn, preset, en
  or or_2 (W1, _1, d_ff_1_q);
  D_Flip_Flop d_ff_2 (.clk(IR2), .D(1'b1), .Q(d_ff_2_q), .reset(_2));  // open: Qn, preset, en
  or or_3 (W2, _2, d_ff_2_q);
  D_Flip_Flop d_ff_3 (.clk(IR3), .D(1'b1), .Q(d_ff_3_q), .reset(_3));  // open: Qn, preset, en
  or or_4 (W3, _3, d_ff_3_q);
  assign mfc_sel = and_1_out ? 2'b00 : 2'bz;  // Controlled_Buffer controlled_buffer_1
  assign mfc_sel = and_2_out ? 2'b01 : 2'bz;  // Controlled_Buffer controlled_buffer_2
  assign mfc_sel = and_3_out ? 2'b10 : 2'bz;  // Controlled_Buffer controlled_buffer_3
  assign mfc_sel = or_1_out ? 2'b11 : 2'bz;  // Controlled_Buffer controlled_buffer_4
  Hex_Digit_Display hex_digit_display_4 (.value(LedData[19:16]));  // open: dp
  Hex_Digit_Display hex_digit_display_5 (.value(LedData[15:12]));  // open: dp
  Comparator #(.width(6)) comparator_7 (.a(op), .b(6'b010000), .eq(comparator_7_eq));  // open: gt, lt
  Comparator #(.width(6)) comparator_8 (.a(rom_1_data), .b(6'b011000), .eq(comparator_8_eq));  // open: gt, lt
  Register #(.width(32)) u_PC (.D(multiplexer_3_out), .en(stop), .Q(pc), .clk(CLK), .clr(RST));
  Hex_Digit_Display hex_digit_display_6 (.value(LedData[11:8]));  // open: dp
  Hex_Digit_Display hex_digit_display_7 (.value(LedData[7:4]));  // open: dp
  Clock clock_1 (.out(CLK));
  and and_6 (eret, comparator_7_eq, comparator_8_eq);
  Adder #(.width(32)) adder_1 (.a(pc), .b(32'h4), .out(adder_1_out));  // open: cin, cout
  Register #(.width(32)) register_1 (.D(a0), .en(and_7_out), .Q(LedData), .clk(CLK), .clr(RST));
  and and_7 (and_7_out, syscall, equal);
  or or_5 (or_5_out, d_ff_1_q, _1);
  or or_6 (or_6_out, d_ff_2_q, _2);
  or or_7 (or_7_out, d_ff_3_q, _3);
  Comparator #(.width(5)) comparator_9 (.a(rd), .b(5'b00001), .eq(comparator_9_eq));  // open: gt, lt
  Comparator #(.width(5)) comparator_10 (.a(rd), .b(5'b00010), .eq(comparator_10_eq));  // open: gt, lt
  Comparator #(.width(5)) comparator_11 (
    .a(rd), .b(5'b00011), .gt(comparator_11_gt), .eq(comparator_11_eq));  // open: lt
  Hex_Digit_Display hex_digit_display_8 (.value(LedData[3:0]));  // open: dp
  Counter #(.width(16), .max('hffff)) counter_1 (
    .count(\硬布线控制器_1_jr [1]), .Q(\无条件分支数 ), .clk(CLK), .clr(RST));  // open: load, D, carry
  ROM #(.addrWidth(10), .dataWidth(32)) rom_1 (
    .addr(pc[11:2]), .data({op, rs, rom_1_data_2[20:16], rd, rom_1_data_2[10:6], rom_1_data}));  // open: sel
  and and_8 (and_8_out, or_5_out, not_1_out);
  not not_1 (not_1_out, rst1);
  and and_9 (and_9_out, or_6_out, not_2_out);
  not not_2 (not_2_out, rst2);
  and and_10 (and_10_out, or_7_out, not_3_out);
  not not_3 (not_3_out, rst3);
  and and_11 (and_11_out, comparator_9_eq, mtc0);
  and and_12 (and_12_out, comparator_10_eq, mtc0);
  and and_13 (and_13_out, comparator_11_eq, mtc0);
  or or_8 (or_8_out, ~mtc0, comparator_11_gt);  // OR_Gate
  D_Flip_Flop u_IR1 (.clk(CLK), .D(and_8_out), .Q(_1));  // open: Qn, preset, en, reset
  D_Flip_Flop u_IR2 (.clk(CLK), .D(and_9_out), .Q(_2));  // open: Qn, preset, en, reset
  D_Flip_Flop u_IR3 (.clk(CLK), .D(and_10_out), .Q(_3));  // open: Qn, preset, en, reset
  assign mtc_sel = and_11_out ? 2'b00 : 2'bz;  // Controlled_Buffer controlled_buffer_5
  assign mtc_sel = and_12_out ? 2'b01 : 2'bz;  // Controlled_Buffer controlled_buffer_6
  assign mtc_sel = and_13_out ? 2'b10 : 2'bz;  // Controlled_Buffer controlled_buffer_7
  assign mtc_sel = or_8_out ? 2'b11 : 2'bz;  // Controlled_Buffer controlled_buffer_8
  // Probe on \总周期数 
  // Probe on \无条件分支数 
  // Probe on \条件分支成功数 
  \硬布线控制器  \u_硬布线控制器_1  (
    .Func(rom_1_data), .OP(op), .ALU_OP(\硬布线控制器_1_alu_op ), .MemToReg(\硬布线控制器_1_memtoreg ),
    .MemWrite(\硬布线控制器_1_memwrite ), .ALU_SRC(\硬布线控制器_1_alu_src ), .RegWrite(\硬布线控制器_1_regwrite ),
    .SysCALL(syscall), .SignedExt(SignedExt), .RegDst(\硬布线控制器_1_regdst ), .JR(\硬布线控制器_1_jr [0]),
    .JMP(\硬布线控制器_1_jr [1]), .Beq(\硬布线控制器_1_beq ), .JAL(JAL), .Bne(\硬布线控制器_1_bne ), .SRAV(SRAV), .LHU(LHU),
    .BGTZ(BGTZ));
  Multiplexer #(.width(5), .enable("false")) multiplexer_4 (
    .in0(rs), .in1(5'b00100), .out(multiplexer_4_out), .sel(syscall));
  Multiplexer #(.width(5), .enable("false")) multiplexer_5 (
    .in0(rom_1_data_2[20:16]), .in1(5'b00010), .out(multiplexer_5_out), .sel(syscall));
  Multiplexer #(.width(32), .enable("false")) multiplexer_6 (
    .in0(multiplexer_9_out), .in1(cp0_rw), .out(multiplexer_6_out), .sel(mfc0));
  and and_14 (and_14_out, syscall, ~equal);  // AND_Gate
  Multiplexer #(.width(5), .enable("false")) multiplexer_7 (
    .in0(rom_1_data_2[20:16]), .in1(rd), .out(multiplexer_7_out), .sel(\硬布线控制器_1_regdst ));
  Multiplexer #(.width(5), .enable("false")) multiplexer_8 (
    .in0(multiplexer_7_out), .in1({5{1'b1}}), .out(multiplexer_8_out), .sel(JAL));
  assign bit_extender_1_out = {{16{1'b0}}, {rd, rom_1_data_2[10:6], rom_1_data}};  // Bit_Extender bit_extender_1
  assign bit_extender_2_out = {{16{rd[4]}}, {rd, rom_1_data_2[10:6], rom_1_data}};  // Bit_Extender bit_extender_2
  Multiplexer #(.width(32), .enable("false")) multiplexer_9 (
    .in0(multiplexer_23_out), .in1(adder_1_out), .out(multiplexer_9_out), .sel(JAL));
  Multiplexer #(.enable("false")) multiplexer_10 (.in0(1'b1), .in1(Go), .out(stop), .sel(and_14_out));
  Priority_Encoder #(.select(2)) priority_encoder_1 (
    .in0(1'b0), .in1(_1), .in2(_2), .in3(_3), .out(priority_encoder_1_out));  // open: gs, en_out, en_in
  or or_9 (or_9_out, \硬布线控制器_1_regwrite , mfc0);
  Multiplexer #(.width(32), .enable("false")) multiplexer_11 (
    .in0(bit_extender_1_out), .in1(bit_extender_2_out), .out(multiplexer_11_out), .sel(SignedExt));
  Counter #(.width(16), .max('hffff)) counter_2 (
    .count(stop), .Q(\总周期数 ), .clk(CLK), .clr(RST));  // open: load, D, carry
  Multiplexer #(.enable("false")) multiplexer_12 (.in0(1'b0), .in1(\开中断 [0]), .out(multiplexer_12_out), .sel(IR_c));
  Multiplexer #(.enable("false")) multiplexer_13 (.in0(1'b0), .in1(\开中断 [1]), .out(multiplexer_13_out), .sel(IR_c));
  Multiplexer #(.enable("false")) multiplexer_14 (.in0(1'b0), .in1(\开中断 [2]), .out(multiplexer_14_out), .sel(IR_c));
  Multiplexer #(.enable("false")) multiplexer_15 (.in0(1'b0), .in1(\开中断 [3]), .out(multiplexer_15_out), .sel(IR_c));
  MIPS_Regifile mips_regifile_1 (
    .Din(multiplexer_6_out), .Clk(CLK), .R1(a0), .R2(R2), .WE(or_9_out), .W_num(multiplexer_8_out),
    .R1_num(multiplexer_4_out), .R2_num(multiplexer_5_out));
  Multiplexer #(.select(2), .enable("false")) multiplexer_16 (
    .in0(1'b0), .in1(1'b1), .in2(IE[0]), .in3(1'b0), .out(multiplexer_16_out), .sel({IE_c, eret}));
  D_Flip_Flop \u_初始化  (.clk(CLK), .D(1'b1), .Q(\初始化_q ));  // open: Qn, preset, en, reset
  Multiplexer #(.width(32), .enable("false")) multiplexer_17 (
    .in0(a0), .in1(32'h22), .out(multiplexer_17_out), .sel(syscall));
  Multiplexer #(.width(32), .enable("false")) multiplexer_18 (
    .in0(R2), .in1(multiplexer_11_out), .out(multiplexer_18_out), .sel(\硬布线控制器_1_alu_src ));
  Multiplexer #(.width(5), .enable("false")) multiplexer_19 (
    .in0(rom_1_data_2[10:6]), .in1(a0[4:0]), .out(multiplexer_19_out), .sel(SRAV));
  Shifter #(.width(32)) shifter_1 (.in(bit_extender_2_out), .\dist (5'b00010), .out(shifter_1_out));
  Decoder #(.select(2), .enable("false")) decoder_1 (
    .out1(decoder_1_out1), .out2(decoder_1_out2), .out3(decoder_1_out3), .sel(priority_encoder_1_out));  // open: out0
  D_Flip_Flop d_ff_4 (
    .clk(CLK), .D(multiplexer_12_out), .Q(\中断字 [0]), .Qn(d_ff_4_qn), .en(IR_c));  // open: preset, reset
  D_Flip_Flop d_ff_5 (
    .clk(CLK), .D(multiplexer_13_out), .Q(\中断字 [1]), .Qn(d_ff_5_qn), .en(IR_c));  // open: preset, reset
  D_Flip_Flop d_ff_6 (
    .clk(CLK), .D(multiplexer_14_out), .Q(\中断字 [2]), .Qn(d_ff_6_qn), .en(IR_c));  // open: preset, reset
  D_Flip_Flop d_ff_7 (
    .clk(CLK), .D(multiplexer_15_out), .Q(\中断字 [3]), .Qn(d_ff_7_qn), .en(IR_c));  // open: preset, reset
  Multiplexer #(.enable("false")) multiplexer_20 (
    .in0(multiplexer_16_out), .in1(1'b1), .out(multiplexer_20_out), .sel(not_4_out));
  or or_10 (or_10_out, not_4_out, IE_c, eret, \中断请求 );
  not not_4 (not_4_out, \初始化_q );
  Multiplexer #(.width(32), .enable("false")) multiplexer_21 (
    .in0(pc), .in1(EPC_write), .out(multiplexer_21_out), .sel(EPC_c));
  or or_11 (or_11_out, EPC_c, \中断请求 );
  MIPS_ALU mips_alu_1 (
    .X(multiplexer_17_out), .Y(multiplexer_18_out), .AluOP(\硬布线控制器_1_alu_op ), .Equal(equal),
    .Result(result), .shamt(multiplexer_19_out));  // open: Result_2
  Adder #(.width(32)) adder_2 (.a(shifter_1_out), .b(adder_1_out), .out(adder_2_out));  // open: cin, cout
  Multiplexer #(.select(2), .width(32), .enable("false")) multiplexer_22 (
    .in0({{28{1'b0}}, \中断字 }), .in1(epc), .in2({32{1'b0}}), .in3({32{1'b0}}), .out(cp0_rw), .sel(mfc_sel));
  and and_15 (rst1, decoder_1_out1, eret);
  and and_16 (rst2, decoder_1_out2, eret);
  and and_17 (rst3, decoder_1_out3, eret);
  and and_18 (and_18_out, 1'b0, d_ff_4_qn);
  and and_19 (and_19_out, _1, d_ff_5_qn);
  and and_20 (and_20_out, _2, d_ff_6_qn);
  and and_21 (and_21_out, _3, d_ff_7_qn);
  Register #(.width(1)) u_IE (.D(multiplexer_20_out), .en(or_10_out), .Q(IE_q), .clk(CLK));  // open: clr
  Register #(.width(32)) u_EPC (.D(multiplexer_21_out), .en(or_11_out), .Q(epc), .clk(CLK));  // open: clr
  and and_22 (and_22_out, \硬布线控制器_1_beq , equal);
  and and_23 (and_23_out, ~equal, \硬布线控制器_1_bne );  // AND_Gate
  and and_24 (and_24_out, ~result[0], ~equal, BGTZ);  // AND_Gate
  Multiplexer #(.width(32), .enable("false")) multiplexer_23 (
    .in0({multiplexer_25_out_2, multiplexer_25_out}), .in1({{16{1'b0}}, multiplexer_24_out}),
    .out(multiplexer_23_out), .sel(LHU));
  Priority_Encoder #(.select(2)) priority_encoder_2 (
    .in0(and_18_out), .in1(and_19_out), .in2(and_20_out), .in3(and_21_out), .out(priority_encoder_2_out),
    .gs(IR));  // open: en_out, en_in
  and and_25 (\中断请求 , IR, IE_q);
  or or_12 (\硬布线控制器_1_jr [2], and_22_out, and_23_out, and_24_out);
  not not_5 (not_5_out, \硬布线控制器_1_memwrite );
  Demultiplexer #(.select(2), .width(32), .enable("false")) demultiplexer_1 (
    .out0(\开中断 ), .out1(EPC_write), .out2(IE), .in(R2), .sel(mtc_sel));  // open: out3
  Decoder #(.select(2), .enable("false")) decoder_2 (
    .out0(IR_c), .out1(EPC_c), .out2(IE_c), .sel(mtc_sel));  // open: out3
  RAM #(.addrWidth(10), .dataWidth(32), .bus("separate")) ram_1 (
    .addr(result[11:2]), .din(R2), .data(ram_1_data), .str(\硬布线控制器_1_memwrite ), .clk(CLK), .ld(not_5_out),
    .clr(RST));  // open: sel
  Multiplexer #(.width(16), .enable("false")) multiplexer_24 (
    .in0(multiplexer_25_out), .in1(multiplexer_25_out_2), .out(multiplexer_24_out), .sel(result[1]));
  Counter #(.width(16), .max('hffff)) counter_3 (
    .count(\硬布线控制器_1_jr [2]), .Q(\条件分支成功数 ), .clk(CLK), .clr(RST));  // open: load, D, carry
  Multiplexer #(.width(32), .enable("false")) multiplexer_25 (
    .in0(result), .in1(ram_1_data), .out({multiplexer_25_out_2, multiplexer_25_out}),
    .sel(\硬布线控制器_1_memtoreg ));
  Multiplexer #(.select(2), .width(32), .enable("false")) multiplexer_26 (
    .in1(32'h4), .in2(32'h12c), .in3(32'h254), .out(\中断入口 ), .sel(priority_encoder_2_out));  // open: in0

  // Notes on the sheet:
  //   中断源
  //   中断等待指示
  //   数码管输出应该用寄存器锁存，否则显示数据只能一闪而过
  //   数码管输出
  //   指令存储器
  //   指令字
  //   contents of rom_1 (hex, n*v repeats v):
  //   81000df 23bdfffc afa10000 23bdfffc afa20000 23bdfffc afa30000 23bdfffc afa40000 23bdfffc afb00000
  //   23bdfffc afb10000 23bdfffc afb20000 23bdfffc afb30000 23bdfffc afb40000 23bdfffc afb50000 23bdfffc
  //   afb60000 40010800 23bdfffc afa10000 40021000 23bdfffc afa20000 20010003 40810800 20030001 40831800
  //   20160001 20140006 20150001 168020 108100 2149825 132020 20020022 c 1600fffa 295a022 1680fff7
  //   40801800 8fa20000 23bd0004 40821000 8fa10000 23bd0004 40810800 8fb60000 23bd0004 8fb50000 23bd0004
  //   8fb40000 23bd0004 8fb30000 23bd0004 8fb20000 23bd0004 8fb10000 23bd0004 8fb00000 23bd0004 8fa40000
  //   23bd0004 8fa30000 23bd0004 8fa20000 23bd0004 8fa10000 23bd0004 42000018 23bdfffc afa10000 23bdfffc
  //   afa20000 23bdfffc afa30000 23bdfffc afa40000 23bdfffc afb00000 23bdfffc afb10000 23bdfffc afb20000
  //   23bdfffc afb30000 23bdfffc afb40000 23bdfffc afb50000 23bdfffc afb60000 40010800 23bdfffc afa10000
  //   40021000 23bdfffc afa20000 20010007 40810800 20030001 40831800 20160002 20140006 20150001 168020
  //   108100 2149825 132020 20020022 c 1600fffa 295a022 1680fff7 40801800 8fa20000 23bd0004 40821000
  //   8fa10000 23bd0004 40810800 8fb60000 23bd0004 8fb50000 23bd0004 8fb40000 23bd0004 8fb30000 23bd0004
  //   8fb20000 23bd0004 8fb10000 23bd0004 8fb00000 23bd0004 8fa40000 23bd0004 8fa30000 23bd0004 8fa20000
  //   23bd0004 8fa10000 23bd0004 42000018 23bdfffc afa10000 23bdfffc afa20000 23bdfffc afa30000 23bdfffc
  //   afa40000 23bdfffc afb00000 23bdfffc afb10000 23bdfffc afb20000 23bdfffc afb30000 23bdfffc afb40000
  //   23bdfffc afb50000 23bdfffc afb60000 40010800 23bdfffc afa10000 40021000 23bdfffc afa20000 2001000f
  //   40810800 20030001 40831800 20160003 20140006 20150001 168020 108100 2149825 132020 20020022 c
  //   1600fffa 295a022 1680fff7 40801800 8fa20000 23bd0004 40821000 8fa10000 23bd0004 40810800 8fb60000
  //   23bd0004 8fb50000 23bd0004 8fb40000 23bd0004 8fb30000 23bd0004 8fb20000 23bd0004 8fb10000 23bd0004
  //   8fb00000 23bd0004 8fa40000 23bd0004 8fa30000 23bd0004 8fa20000 23bd0004 8fa10000 23bd0004 42000018
  //   20110200 20020022 112020 c 2231ffff 1620fffc 4*0 2002000a c 2002000a c
  //   shamt
  //   imm
  //   OP
  //   Func
  //   rs
  //   rt
  //   rd
  //   Beq
  //   JMP
  //   JR
  //   Bne
  //   OP
  //   JAL
  //   Func
  //   Syscall
  //   MemToReg
  //   MemWrite
  //   AluOP
  //   AluSrcB
  //   RegWrite
  //   RegDst
endmodule
