// Logisim project cpu28.circ as structural Verilog: 17 circuits, main circuit ◇单周期MIPS
module \单周期MIPS  (
);

  wire AluSrcB, and_1_out, and_2_out, and_3_out, and_4_out, Beq, Bi_Jiao, BLEZ, Bne, CLK, comparator_1_eq,
       Go, JAL, JMP, JR, LOCK, MemToReg, MemWrite, mips_alu_1_equal, multiplexer_1_out, multiplexer_10_out,
       or_1_out, RegDst, RegWrite, RST, SH, SignedExt, Syscall, V;
  wire [3:0] AluOP, multiplexer_18_out, multiplexer_19_out;
  wire [4:0] multiplexer_8_out, multiplexer_9_out, multiplexer_11_out, multiplexer_13_out, multiplexer_14_out;
  wire [5:0] OP;
  wire [15:0] _0_15, _16, \总周期数 , \无条件分支数 , \条件分支成功数 ;
  wire [25:16] _25_0;
  wire [31:0] adder_1_out, adder_2_out, ALU_Result, bit_extender_1_out, bit_extender_2_out,
       bit_extender_3_out, LedData, multiplexer_2_out, multiplexer_3_out, multiplexer_4_out,
       multiplexer_5_out, multiplexer_6_out, multiplexer_7_out, multiplexer_12_out, multiplexer_15_out,
       multiplexer_16_out, multiplexer_17_out, multiplexer_20_out, PC_q, R1, RAM_Out, shifter_1_out;
  wire [31:16] R2;

  Button \u_总复位  (.out(RST));
  Button \u_继续运行  (.out(Go));
  Clock clock_1 (.out(CLK));
  Multiplexer #(.enable("false")) multiplexer_1 (.in0(1'b1), .in1(1'b0), .out(multiplexer_1_out), .sel(and_1_out));
  Register #(.width(32)) PC (.D(multiplexer_7_out), .en(multiplexer_1_out), .Q(PC_q), .clk(CLK), .clr(RST));
  assign bit_extender_1_out = {{16{_0_15[15]}}, _0_15};  // Bit_Extender bit_extender_1
  and and_1 (and_1_out, LOCK, ~Go);  // AND_Gate
  Counter #(.width(16), .max('hffff)) counter_1 (
    .count(multiplexer_1_out), .Q(\总周期数 ), .clk(CLK), .clr(RST));  // open: load, D, carry
  Hex_Digit_Display hex_digit_display_1 (.value(LedData[31:28]));  // open: dp
  Hex_Digit_Display hex_digit_display_2 (.value(LedData[27:24]));  // open: dp
  Adder #(.width(32)) adder_1 (.a(PC_q), .b(32'h4), .out(adder_1_out));  // open: cin, cout
  Shifter #(.width(32)) shifter_1 (.in(bit_extender_1_out), .\dist (5'b00010), .out(shifter_1_out));
  assign bit_extender_2_out = {{16{_0_15[15]}}, _0_15};  // Bit_Extender bit_extender_2
  Hex_Digit_Display hex_digit_display_3 (.value(LedData[19:16]));  // open: dp
  Hex_Digit_Display hex_digit_display_4 (.value(LedData[23:20]));  // open: dp
  ROM #(.addrWidth(10), .dataWidth(32)) rom_1 (.addr(PC_q[11:2]), .data({OP, _25_0, _0_15}));  // open: sel
  assign bit_extender_3_out = {{16{1'b0}}, _0_15};  // Bit_Extender bit_extender_3
  Multiplexer #(.width(32), .enable("false")) multiplexer_2 (
    .in0(bit_extender_3_out), .in1(bit_extender_2_out), .out(multiplexer_2_out), .sel(SignedExt));
  Hex_Digit_Display hex_digit_display_5 (.value(LedData[11:8]));  // open: dp
  Hex_Digit_Display hex_digit_display_6 (.value(LedData[15:12]));  // open: dp
  Adder #(.width(32)) adder_2 (.a(adder_1_out), .b(shifter_1_out), .out(adder_2_out));  // open: cin, cout
  Multiplexer #(.width(32), .enable("false")) multiplexer_3 (
    .in0({4'b0000, _25_0, _0_15, 2'b00}), .in1(R1), .out(multiplexer_3_out), .sel(JR));
  Hex_Digit_Display hex_digit_display_7 (.value(LedData[3:0]));  // open: dp
  Hex_Digit_Display hex_digit_display_8 (.value(LedData[7:4]));  // open: dp
  Multiplexer #(.width(32), .enable("false")) multiplexer_4 (
    .in0(adder_1_out), .in1(adder_2_out), .out(multiplexer_4_out), .sel(Bi_Jiao));
  Multiplexer #(.width(32), .enable("false")) multiplexer_5 (
    .in0({R2, _16}), .in1(multiplexer_2_out), .out(multiplexer_5_out), .sel(AluSrcB));
  Multiplexer #(.width(32), .enable("false")) multiplexer_6 (
    .in0(multiplexer_5_out), .in1({32{1'b0}}), .out(multiplexer_6_out), .sel(BLEZ));
  Multiplexer #(.width(32), .enable("false")) multiplexer_7 (
    .in0(multiplexer_4_out), .in1(multiplexer_3_out), .out(multiplexer_7_out), .sel(JMP));
  Multiplexer #(.width(5), .enable("false")) multiplexer_8 (
    .in0(_0_15[10:6]), .in1(R1[4:0]), .out(multiplexer_8_out), .sel(V));
  and and_2 (and_2_out, Beq, mips_alu_1_equal);
  and and_3 (and_3_out, Bne, ~mips_alu_1_equal);  // AND_Gate
  or or_1 (or_1_out, mips_alu_1_equal, ALU_Result[0]);
  MIPS_ALU mips_alu_1 (
    .X(R1), .Y(multiplexer_6_out), .AluOP(AluOP), .Equal(mips_alu_1_equal), .Result(ALU_Result),
    .shamt(multiplexer_8_out));  // open: Result_2
  // Probe on \总周期数 
  // Probe on \无条件分支数 
  // Probe on \条件分支成功数 
  Multiplexer #(.width(5), .enable("false")) multiplexer_9 (
    .in0(_25_0[25:21]), .in1(5'b00010), .out(multiplexer_9_out), .sel(Syscall));
  Multiplexer #(.enable("false")) multiplexer_10 (.in0(1'b0), .in1(or_1_out), .out(multiplexer_10_out), .sel(BLEZ));
  Multiplexer #(.width(5), .enable("false")) multiplexer_11 (
    .in0(_25_0[20:16]), .in1(_0_15[15:11]), .out(multiplexer_11_out), .sel(RegDst));
  Multiplexer #(.width(32), .enable("false")) multiplexer_12 (
    .in0(ALU_Result), .in1(RAM_Out), .out(multiplexer_12_out), .sel(MemToReg));
  or or_2 (Bi_Jiao, and_2_out, and_3_out, multiplexer_10_out);
  Multiplexer #(.width(5), .enable("false")) multiplexer_13 (
    .in0(_25_0[20:16]), .in1(5'b00100), .out(multiplexer_13_out), .sel(Syscall));
  Multiplexer #(.width(5), .enable("false")) multiplexer_14 (
    .in0(multiplexer_11_out), .in1({5{1'b1}}), .out(multiplexer_14_out), .sel(JAL));
  Multiplexer #(.width(32), .enable("false")) multiplexer_15 (
    .in0(multiplexer_12_out), .in1(adder_1_out), .out(multiplexer_15_out), .sel(JAL));
  Multiplexer #(.width(32), .enable("false")) multiplexer_16 (
    .in0({{16{1'b0}}, _16}), .in1({_16, {16{1'b0}}}), .out(multiplexer_16_out), .sel(ALU_Result[1]));
  \硬布线控制器  \u_硬布线控制器_1  (
    .Func(_0_15[5:0]), .OP(OP), .ALU_OP(AluOP), .MemToReg(MemToReg), .MemWrite(MemWrite), .ALU_SRC(AluSrcB),
    .RegWrite(RegWrite), .SysCALL(Syscall), .SignedExt(SignedExt), .RegDst(RegDst), .JR(JR), .JMP(JMP),
    .Beq(Beq), .JAL(JAL), .Bne(Bne), .V(V), .SH(SH), .BLEZ(BLEZ));
  MIPS_Regifile mips_regifile_1 (
    .Din(multiplexer_15_out), .Clk(CLK), .R1(R1), .R2({R2, _16}), .WE(RegWrite), .W_num(multiplexer_14_out),
    .R1_num(multiplexer_9_out), .R2_num(multiplexer_13_out));
  Multiplexer #(.width(32), .enable("false")) multiplexer_17 (
    .in0({R2, _16}), .in1(multiplexer_16_out), .out(multiplexer_17_out), .sel(SH));
  Multiplexer #(.width(4), .enable("false")) multiplexer_18 (
    .in0(4'b1111), .in1(multiplexer_19_out), .out(multiplexer_18_out), .sel(SH));
  Multiplexer #(.width(4), .enable("false")) multiplexer_19 (
    .in0(4'b0011), .in1(4'b1100), .out(multiplexer_19_out), .sel(ALU_Result[1]));
  Counter #(.width(16), .max('hffff)) counter_2 (
    .count(JMP), .Q(\无条件分支数 ), .clk(CLK), .clr(RST));  // open: load, D, carry
  Counter #(.width(16), .max('hffff)) counter_3 (
    .count(Bi_Jiao), .Q(\条件分支成功数 ), .clk(CLK), .clr(RST));  // open: load, D, carry
  // MIPS_RAM mips_ram_1: pin names not known; wires that end beside it: ALU_Result[21:2], multiplexer_17_out, MemWrite, multiplexer_18_out, CLK, RST, RAM_Out
  Comparator #(.width(32)) comparator_1 (.a(R1), .b(32'h22), .eq(comparator_1_eq));  // open: gt, lt
  and and_4 (and_4_out, comparator_1_eq, Syscall);
  and and_5 (LOCK, ~comparator_1_eq, Syscall);  // AND_Gate
  Multiplexer #(.width(32)) multiplexer_20 (
    .in1({R2, _16}), .out(multiplexer_20_out), .sel(and_4_out), .en(and_4_out));  // open: in0
  Register #(.width(32)) register_1 (.D(multiplexer_20_out), .Q(LedData), .clk(CLK), .clr(RST));  // open: en

  // Other names for the same wires on the sheet: _25_0[15:0] = _0_15; Func[5:0] = _0_15[5:0];
  //   shamt[4:0] = _0_15[10:6]; rd[4:0] = _0_15[15:11]; rt[4:0] = _25_0[20:16]; rs[4:0] = _25_0[25:21];
  //   半字选择 = ALU_Result[1]; R2[15:0] = _16

  // Notes on the sheet:
  //   数码管输出应该用寄存器锁存，否则显示数据只能一闪而过
  //   指令存储器
  //   可以通过项目增加Logisim库的方式将前几次实验完成的电路作为子电路引入到本电路中使用
  //   contents of rom_1 (hex, n*v repeats v):
  //   20110001 8000c05 20110001 20120002 20130003 8000c09 20110001 20120002 20130003 8000c0d 20110001
  //   20120002 20130003 8000c11 20110001 20120002 20130003 c000cfa 20100001 20110001 118fc0 112020
  //   20020022 c 118882 12200001 8000c15 112020 20020022 c 20110001 118880 112020 20020022 c 12200001
  //   8000c1f 20110001 118fc0 112020 20020022 c 1188c3 112020 20020022 c 118903 112020 20020022 c 118903
  //   112020 20020022 c 118903 112020 20020022 c 118903 112020 20020022 c 118903 112020 20020022 c 118903
  //   112020 20020022 c 118903 112020 20020022 c 20100001 109fc0 139fc3 8021 2012000c 24160003 26100001
  //   3210000f 20080008 20090001 139900 2709825 132020 20020022 c 1094022 1500fff9 22100001 2018000f
  //   2188024 108700 20080008 20090001 139902 2709825 132021 20020022 c 1094022 1500fff9 108702 2c9b022
  //   12c00001 8000c50 4020 1084027 84400 3508ffff 82021 20020022 c 2010ffff 20110000 ae300000 22100001
  //   22310004 ae300000 22100001 22310004 ae300000 22100001 22310004 ae300000 22100001 22310004 ae300000
  //   22100001 22310004 ae300000 22100001 22310004 ae300000 22100001 22310004 ae300000 22100001 22310004
  //   ae300000 22100001 22310004 ae300000 22100001 22310004 ae300000 22100001 22310004 ae300000 22100001
  //   22310004 ae300000 22100001 22310004 ae300000 22100001 22310004 ae300000 22100001 22310004 ae300000
  //   22100001 22310004 22100001 8020 2011003c 8e130000 8e340000 274402a 11000002 ae330000 ae140000
  //   2231fffc 1611fff8 102020 20020022 c 22100004 2011003c 1611fff2 2002000a c 20080001 20090003 20110876
  //   112020 20020022 c 200b0008 1118804 1318804 112020 20020022 c 216bffff 1560fff9 2002000a c 20080001
  //   20090003 20110876 118d00 112020 20020022 c 200b0008 1118807 1318807 112020 20020022 c 216bffff
  //   1560fff9 2002000a c 20090000 200b0020 20110001 20120001 a5310000 112020 20020022 c 2328820 21290002
  //   216bffff 1560fff8 200b0010 20090000 8d310000 112020 20020022 c 21290004 216bffff 1560fff9 2002000a c
  //   2011fff1 112020 20020022 c 22310001 1a20fffb 2002000a c 2002000a c 20100000 22100001 102020 20020022
  //   c 22100002 102020 20020022 c 22100003 102020 20020022 c 22100004 102020 20020022 c 22100005 102020
  //   20020022 c 22100006 102020 20020022 c 22100007 102020 20020022 c 22100008 102020 20020022 20020022 c
  //   3e00008
  //   OP
  //   Func
  //   rs
  //   指令字
  //   rt
  //   rd
  //   数码管输出
  //   总复位信号应将除ROM以外所有存储组件全部清零
  //   JMP
  //   JR
  //   OP
  //   Func
  //   Beq
  //   Bne
  //   MemToReg
  //   MemWrite
  //   AluOP
  //   AluSrcB
  //   RegWrite
  //   JAL
  //   RegDst
  //   Syscall
endmodule

// 单周期硬布线控制器
module \硬布线控制器  (
  input  [5:0] OP,
  input  [5:0] Func,
  output [3:0] ALU_OP,
  output MemToReg,
  output MemWrite,
  output ALU_SRC,
  output RegWrite,
  output SysCALL,
  output SignedExt,
  output RegDst,
  output Beq,
  output Bne,
  output JR,
  output JMP,
  output JAL,
  output V,
  output SH,
  output BLEZ
);

  \运算控制器  \u_运算控制器_1  (
    .OP0(OP[0]), .OP1(OP[1]), .OP2(OP[2]), .OP3(OP[3]), .OP4(OP[4]), .OP5(OP[5]), .F0(Func[0]), .F1(Func[1]),
    .F2(Func[2]), .F3(Func[3]), .F4(Func[4]), .F5(Func[5]), .S0(ALU_OP[0]), .S1(ALU_OP[1]), .S2(ALU_OP[2]),
    .S3(ALU_OP[3]));
  \控制信号生成  \u_控制信号生成_1  (
    .OP0(OP[0]), .MemToReg(MemToReg), .OP1(OP[1]), .OP2(OP[2]), .OP3(OP[3]), .OP4(OP[4]),
    .MemWrite(MemWrite), .OP5(OP[5]), .F0(Func[0]), .F1(Func[1]), .F2(Func[2]), .F3(Func[3]), .F4(Func[4]),
    .F5(Func[5]), .ALU_SRC(ALU_SRC), .RegWrite(RegWrite), .SysCALL(SysCALL), .SignedExt(SignedExt),
    .RegDst(RegDst), .BEQ(Beq), .BNE(Bne), .JR(JR), .JMP(JMP), .JAL(JAL));
  CCMB ccmb_1 (
    .OP0(OP[0]), .OP1(OP[1]), .OP2(OP[2]), .OP3(OP[3]), .OP4(OP[4]), .OP5(OP[5]), .F0(Func[0]), .F1(Func[1]),
    .F2(Func[2]), .F3(Func[3]), .F4(Func[4]), .F5(Func[5]), .V(V), .SH(SH), .BLEZ(BLEZ));

  // Other names for the same wires on the sheet: OP_CODE[5:0] = OP

  // Notes on the sheet:
  //   运算器控制器，根据指令生成运算器功能选择信号
  //   控制信号生成，产生数据通路需要的其他控制信号
endmodule

// 运算器控制器
module \运算控制器  (
  input  OP0,
  input  OP1,
  input  OP2,
  input  OP3,
  input  OP4,
  input  OP5,
  input  F0,
  input  F1,
  input  F2,
  input  F3,
  input  F4,
  input  F5,
  output S0,
  output S1,
  output S2,
  output S3
);

  wire and_1_out, and_2_out, and_3_out, and_4_out, and_5_out, and_6_out, and_7_out, and_8_out, and_9_out,
       and_10_out, and_11_out, and_12_out, and_13_out, and_14_out, and_15_out, and_16_out, and_17_out,
       and_18_out, and_19_out, and_20_out, and_21_out, and_22_out, and_23_out, and_24_out, and_25_out,
       and_26_out, and_27_out, and_28_out, and_29_out, and_30_out, and_31_out, and_32_out, and_33_out,
       and_34_out, and_35_out, and_36_out, and_37_out, and_38_out, and_39_out, and_40_out, not_1_out,
       not_2_out, not_3_out, not_4_out, not_5_out, not_6_out, not_7_out, not_8_out, not_9_out, not_10_out,
       not_11_out, not_12_out, not_13_out, not_14_out, not_15_out, not_16_out, not_17_out, not_18_out,
       not_19_out, not_20_out, not_21_out, not_22_out, not_23_out, not_24_out, not_25_out, not_26_out,
       not_27_out, not_28_out, not_29_out, not_30_out, not_31_out, not_32_out, not_33_out, not_34_out,
       not_35_out, not_36_out, not_37_out, not_38_out, not_39_out, not_40_out, not_41_out, not_42_out,
       not_43_out, not_44_out, not_45_out, not_46_out, not_47_out, not_48_out, not_49_out, not_50_out,
       not_51_out, not_52_out, not_53_out, not_54_out, not_55_out, not_56_out, not_57_out, not_58_out,
       not_59_out, not_60_out, not_61_out, not_62_out, not_63_out, not_64_out, not_65_out, not_66_out,
       not_67_out, not_68_out, not_69_out, not_70_out, not_71_out, not_72_out, not_73_out, not_74_out,
       not_75_out, not_76_out, not_77_out, not_78_out, not_79_out, not_80_out, not_81_out, not_82_out,
       not_83_out, not_84_out, not_85_out, not_86_out, not_87_out, not_88_out, not_89_out, not_90_out,
       not_91_out, not_92_out, not_93_out, not_94_out, not_95_out, not_96_out, not_97_out, not_98_out,
       not_99_out, not_100_out, not_101_out, not_102_out, not_103_out, not_104_out, not_105_out, not_106_out,
       not_107_out, not_108_out, not_109_out, not_110_out, not_111_out, not_112_out, not_113_out,
       not_114_out, not_115_out, not_116_out, not_117_out, not_118_out, not_119_out, not_120_out,
       not_121_out, not_122_out, not_123_out, not_124_out, not_125_out, not_126_out, not_127_out,
       not_128_out, not_129_out, not_130_out, not_131_out, not_132_out, not_133_out, not_134_out,
       not_135_out, not_136_out, not_137_out, not_138_out, not_139_out, not_140_out, not_141_out,
       not_142_out, not_143_out, not_144_out, not_145_out, not_146_out, not_147_out, not_148_out,
       not_149_out, not_150_out, not_151_out, not_152_out, not_153_out, not_154_out, not_155_out,
       not_156_out, not_157_out, not_158_out, not_159_out, not_160_out, not_161_out, not_162_out,
       not_163_out, not_164_out, not_165_out, not_166_out, not_167_out, not_168_out, not_169_out,
       not_170_out, not_171_out, not_172_out, not_173_out, not_174_out, not_175_out, not_176_out,
       not_177_out, not_178_out, not_179_out, not_180_out, not_181_out, not_182_out, not_183_out,
       not_184_out, not_185_out, not_186_out, not_187_out, not_188_out, not_189_out, not_190_out,
       not_191_out, not_192_out, not_193_out, not_194_out, not_195_out, not_196_out, not_197_out,
       not_198_out, not_199_out, not_200_out, not_201_out, not_202_out, not_203_out, not_204_out,
       not_205_out, not_206_out, not_207_out, not_208_out, not_209_out, not_210_out, not_211_out,
       not_212_out, not_213_out, not_214_out, not_215_out, not_216_out, not_217_out, not_218_out,
       not_219_out, not_220_out, not_221_out, not_222_out, not_223_out, not_224_out, not_225_out,
       not_226_out, not_227_out, not_228_out, not_229_out, not_230_out, not_231_out, not_232_out,
       not_233_out, not_234_out, not_235_out, not_236_out, not_237_out, not_238_out, not_239_out,
       not_240_out, not_241_out, not_242_out, not_243_out, not_244_out, not_245_out, not_246_out,
       not_247_out, not_248_out, not_249_out, not_250_out, not_251_out, not_252_out, not_253_out,
       not_254_out, not_255_out, not_256_out, not_257_out, not_258_out, not_259_out, not_260_out,
       not_261_out, not_262_out, not_263_out;

  not not_1 (not_1_out, OP5);
  not not_2 (not_2_out, OP4);
  not not_3 (not_3_out, OP3);
  not not_4 (not_4_out, OP2);
  not not_5 (not_5_out, OP1);
  not not_6 (not_6_out, OP0);
  not not_7 (not_7_out, F5);
  not not_8 (not_8_out, F4);
  not not_9 (not_9_out, F3);
  not not_10 (not_10_out, F2);
  not not_11 (not_11_out, OP5);
  not not_12 (not_12_out, OP4);
  not not_13 (not_13_out, OP3);
  not not_14 (not_14_out, OP2);
  not not_15 (not_15_out, OP1);
  not not_16 (not_16_out, OP0);
  not not_17 (not_17_out, F4);
  not not_18 (not_18_out, F3);
  not not_19 (not_19_out, F2);
  not not_20 (not_20_out, F1);
  not not_21 (not_21_out, F0);
  not not_22 (not_22_out, OP5);
  not not_23 (not_23_out, OP4);
  not not_24 (not_24_out, OP3);
  not not_25 (not_25_out, OP2);
  not not_26 (not_26_out, OP1);
  not not_27 (not_27_out, OP0);
  not not_28 (not_28_out, F4);
  not not_29 (not_29_out, F3);
  not not_30 (not_30_out, F2);
  not not_31 (not_31_out, F1);
  not not_32 (not_32_out, OP5);
  not not_33 (not_33_out, OP4);
  not not_34 (not_34_out, OP3);
  not not_35 (not_35_out, OP2);
  not not_36 (not_36_out, OP1);
  not not_37 (not_37_out, OP0);
  not not_38 (not_38_out, F4);
  not not_39 (not_39_out, F3);
  not not_40 (not_40_out, F1);
  not not_41 (not_41_out, F0);
  not not_42 (not_42_out, OP5);
  not not_43 (not_43_out, OP4);
  not not_44 (not_44_out, OP3);
  not not_45 (not_45_out, OP2);
  not not_46 (not_46_out, OP1);
  not not_47 (not_47_out, OP0);
  not not_48 (not_48_out, F4);
  not not_49 (not_49_out, F2);
  not not_50 (not_50_out, F0);
  not not_51 (not_51_out, OP5);
  not not_52 (not_52_out, OP4);
  not not_53 (not_53_out, OP2);
  not not_54 (not_54_out, OP1);
  not not_55 (not_55_out, OP0);
  not not_56 (not_56_out, OP5);
  not not_57 (not_57_out, OP4);
  not not_58 (not_58_out, OP1);
  not not_59 (not_59_out, OP0);
  not not_60 (not_60_out, OP5);
  not not_61 (not_61_out, OP4);
  not not_62 (not_62_out, OP2);
  not not_63 (not_63_out, OP1);
  not not_64 (not_64_out, OP5);
  not not_65 (not_65_out, OP4);
  not not_66 (not_66_out, OP2);
  not not_67 (not_67_out, OP0);
  not not_68 (not_68_out, OP4);
  not not_69 (not_69_out, OP3);
  not not_70 (not_70_out, OP2);
  not not_71 (not_71_out, OP4);
  not not_72 (not_72_out, OP2);
  not not_73 (not_73_out, OP5);
  not not_74 (not_74_out, OP4);
  not not_75 (not_75_out, OP3);
  not not_76 (not_76_out, OP2);
  not not_77 (not_77_out, OP1);
  not not_78 (not_78_out, OP0);
  not not_79 (not_79_out, F5);
  not not_80 (not_80_out, F4);
  not not_81 (not_81_out, F3);
  not not_82 (not_82_out, OP4);
  not not_83 (not_83_out, OP2);
  not not_84 (not_84_out, OP1);
  not not_85 (not_85_out, OP5);
  not not_86 (not_86_out, OP4);
  not not_87 (not_87_out, OP3);
  not not_88 (not_88_out, OP0);
  not not_89 (not_89_out, OP5);
  not not_90 (not_90_out, OP4);
  not not_91 (not_91_out, OP3);
  not not_92 (not_92_out, OP2);
  not not_93 (not_93_out, OP1);
  not not_94 (not_94_out, OP0);
  not not_95 (not_95_out, F5);
  not not_96 (not_96_out, F4);
  not not_97 (not_97_out, F3);
  not not_98 (not_98_out, F2);
  not not_99 (not_99_out, F0);
  not not_100 (not_100_out, OP5);
  not not_101 (not_101_out, OP4);
  not not_102 (not_102_out, OP3);
  not not_103 (not_103_out, OP2);
  not not_104 (not_104_out, OP1);
  not not_105 (not_105_out, OP0);
  not not_106 (not_106_out, F4);
  not not_107 (not_107_out, F3);
  not not_108 (not_108_out, F2);
  not not_109 (not_109_out, F0);
  not not_110 (not_110_out, OP5);
  not not_111 (not_111_out, OP4);
  not not_112 (not_112_out, OP3);
  not not_113 (not_113_out, OP2);
  not not_114 (not_114_out, OP1);
  not not_115 (not_115_out, OP0);
  not not_116 (not_116_out, F4);
  not not_117 (not_117_out, F3);
  not not_118 (not_118_out, F1);
  not not_119 (not_119_out, F0);
  not not_120 (not_120_out, OP5);
  not not_121 (not_121_out, OP4);
  not not_122 (not_122_out, OP3);
  not not_123 (not_123_out, OP2);
  not not_124 (not_124_out, OP1);
  not not_125 (not_125_out, OP0);
  not not_126 (not_126_out, F4);
  not not_127 (not_127_out, F3);
  not not_128 (not_128_out, OP5);
  not not_129 (not_129_out, OP4);
  not not_130 (not_130_out, OP3);
  not not_131 (not_131_out, OP2);
  not not_132 (not_132_out, OP1);
  not not_133 (not_133_out, OP0);
  not not_134 (not_134_out, F4);
  not not_135 (not_135_out, F2);
  not not_136 (not_136_out, F0);
  not not_137 (not_137_out, OP5);
  not not_138 (not_138_out, OP4);
  not not_139 (not_139_out, OP1);
  not not_140 (not_140_out, OP0);
  not not_141 (not_141_out, OP5);
  not not_142 (not_142_out, OP4);
  not not_143 (not_143_out, OP2);
  not not_144 (not_144_out, OP0);
  not not_145 (not_145_out, OP5);
  not not_146 (not_146_out, OP4);
  not not_147 (not_147_out, OP3);
  not not_148 (not_148_out, OP0);
  not not_149 (not_149_out, OP5);
  not not_150 (not_150_out, OP4);
  not not_151 (not_151_out, OP3);
  not not_152 (not_152_out, OP2);
  not not_153 (not_153_out, OP1);
  not not_154 (not_154_out, OP0);
  not not_155 (not_155_out, F4);
  not not_156 (not_156_out, F3);
  not not_157 (not_157_out, F2);
  not not_158 (not_158_out, F1);
  not not_159 (not_159_out, F0);
  not not_160 (not_160_out, OP5);
  not not_161 (not_161_out, OP4);
  not not_162 (not_162_out, OP3);
  not not_163 (not_163_out, OP2);
  not not_164 (not_164_out, OP1);
  not not_165 (not_165_out, OP0);
  not not_166 (not_166_out, F4);
  not not_167 (not_167_out, F3);
  not not_168 (not_168_out, F2);
  not not_169 (not_169_out, F1);
  not not_170 (not_170_out, OP5);
  not not_171 (not_171_out, OP4);
  not not_172 (not_172_out, OP3);
  not not_173 (not_173_out, OP2);
  not not_174 (not_174_out, OP1);
  not not_175 (not_175_out, OP0);
  not not_176 (not_176_out, F4);
  not not_177 (not_177_out, F3);
  not not_178 (not_178_out, F2);
  not not_179 (not_179_out, F0);
  not not_180 (not_180_out, OP5);
  not not_181 (not_181_out, OP4);
  not not_182 (not_182_out, OP3);
  not not_183 (not_183_out, OP2);
  not not_184 (not_184_out, OP1);
  not not_185 (not_185_out, OP0);
  not not_186 (not_186_out, F4);
  not not_187 (not_187_out, F3);
  not not_188 (not_188_out, F1);
  not not_189 (not_189_out, F0);
  not not_190 (not_190_out, OP5);
  not not_191 (not_191_out, OP4);
  not not_192 (not_192_out, OP3);
  not not_193 (not_193_out, OP2);
  not not_194 (not_194_out, OP1);
  not not_195 (not_195_out, OP0);
  not not_196 (not_196_out, F4);
  not not_197 (not_197_out, F2);
  not not_198 (not_198_out, OP5);
  not not_199 (not_199_out, OP4);
  not not_200 (not_200_out, OP2);
  not not_201 (not_201_out, OP1);
  not not_202 (not_202_out, OP0);
  not not_203 (not_203_out, OP5);
  not not_204 (not_204_out, OP4);
  not not_205 (not_205_out, OP1);
  not not_206 (not_206_out, OP0);
  not not_207 (not_207_out, OP5);
  not not_208 (not_208_out, OP4);
  not not_209 (not_209_out, OP2);
  not not_210 (not_210_out, OP1);
  not not_211 (not_211_out, OP4);
  not not_212 (not_212_out, OP3);
  not not_213 (not_213_out, OP2);
  not not_214 (not_214_out, OP4);
  not not_215 (not_215_out, OP2);
  not not_216 (not_216_out, OP4);
  not not_217 (not_217_out, OP2);
  not not_218 (not_218_out, OP1);
  not not_219 (not_219_out, OP5);
  not not_220 (not_220_out, OP4);
  not not_221 (not_221_out, OP3);
  not not_222 (not_222_out, OP2);
  not not_223 (not_223_out, OP1);
  not not_224 (not_224_out, OP0);
  not not_225 (not_225_out, F4);
  not not_226 (not_226_out, F3);
  not not_227 (not_227_out, F1);
  not not_228 (not_228_out, OP5);
  not not_229 (not_229_out, OP4);
  not not_230 (not_230_out, OP3);
  not not_231 (not_231_out, OP2);
  not not_232 (not_232_out, OP1);
  not not_233 (not_233_out, OP0);
  not not_234 (not_234_out, F4);
  not not_235 (not_235_out, F3);
  not not_236 (not_236_out, OP5);
  not not_237 (not_237_out, OP4);
  not not_238 (not_238_out, OP3);
  not not_239 (not_239_out, OP2);
  not not_240 (not_240_out, OP1);
  not not_241 (not_241_out, OP0);
  not not_242 (not_242_out, F4);
  not not_243 (not_243_out, F2);
  not not_244 (not_244_out, F0);
  not not_245 (not_245_out, OP5);
  not not_246 (not_246_out, OP4);
  not not_247 (not_247_out, OP3);
  not not_248 (not_248_out, OP2);
  not not_249 (not_249_out, OP1);
  not not_250 (not_250_out, OP0);
  not not_251 (not_251_out, F4);
  not not_252 (not_252_out, F2);
  not not_253 (not_253_out, OP5);
  not not_254 (not_254_out, OP4);
  not not_255 (not_255_out, OP2);
  not not_256 (not_256_out, OP0);
  not not_257 (not_257_out, OP5);
  not not_258 (not_258_out, OP4);
  not not_259 (not_259_out, OP1);
  not not_260 (not_260_out, OP5);
  not not_261 (not_261_out, OP4);
  not not_262 (not_262_out, OP3);
  not not_263 (not_263_out, OP0);
  and and_1 (and_1_out, not_1_out, not_2_out, not_3_out, not_4_out, not_5_out, not_6_out, not_7_out, not_8_out, not_9_out, not_10_out, F1, F0);
  and and_2 (and_2_out, not_11_out, not_12_out, not_13_out, not_14_out, not_15_out, not_16_out, F5, not_17_out, not_18_out, not_19_out, not_20_out, not_21_out);
  and and_3 (and_3_out, not_22_out, not_23_out, not_24_out, not_25_out, not_26_out, not_27_out, F5, not_28_out, not_29_out, not_30_out, not_31_out, F0);
  and and_4 (and_4_out, not_32_out, not_33_out, not_34_out, not_35_out, not_36_out, not_37_out, F5, not_38_out, not_39_out, F2, not_40_out, not_41_out);
  and and_5 (and_5_out, not_42_out, not_43_out, not_44_out, not_45_out, not_46_out, not_47_out, F5, not_48_out, F3, not_49_out, F1, not_50_out);
  and and_6 (and_6_out, not_51_out, not_52_out, OP3, not_53_out, not_54_out, not_55_out);
  and and_7 (and_7_out, not_56_out, not_57_out, OP3, OP2, not_58_out, not_59_out);
  and and_8 (and_8_out, not_60_out, not_61_out, OP3, not_62_out, not_63_out, OP0);
  and and_9 (and_9_out, not_64_out, not_65_out, OP3, not_66_out, OP1, not_67_out);
  and and_10 (and_10_out, OP5, not_68_out, not_69_out, not_70_out, OP1, OP0);
  and and_11 (and_11_out, OP5, not_71_out, OP3, not_72_out, OP1, OP0);
  and and_12 (and_12_out, not_73_out, not_74_out, not_75_out, not_76_out, not_77_out, not_78_out, not_79_out, not_80_out, not_81_out, F2, F1, F0);
  and and_13 (and_13_out, OP5, not_82_out, OP3, not_83_out, not_84_out, OP0);
  and and_14 (and_14_out, not_85_out, not_86_out, not_87_out, OP2, OP1, not_88_out);
  and and_15 (and_15_out, not_89_out, not_90_out, not_91_out, not_92_out, not_93_out, not_94_out, not_95_out, not_96_out, not_97_out, not_98_out, F1, not_99_out);
  and and_16 (and_16_out, not_100_out, not_101_out, not_102_out, not_103_out, not_104_out, not_105_out, F5, not_106_out, not_107_out, not_108_out, F1, not_109_out);
  and and_17 (and_17_out, not_110_out, not_111_out, not_112_out, not_113_out, not_114_out, not_115_out, F5, not_116_out, not_117_out, F2, not_118_out, not_119_out);
  and and_18 (and_18_out, not_120_out, not_121_out, not_122_out, not_123_out, not_124_out, not_125_out, F5, not_126_out, not_127_out, F2, F1, F0);
  and and_19 (and_19_out, not_128_out, not_129_out, not_130_out, not_131_out, not_132_out, not_133_out, F5, not_134_out, F3, not_135_out, F1, not_136_out);
  and and_20 (and_20_out, not_137_out, not_138_out, OP3, OP2, not_139_out, not_140_out);
  and and_21 (and_21_out, not_141_out, not_142_out, OP3, not_143_out, OP1, not_144_out);
  and and_22 (and_22_out, not_145_out, not_146_out, not_147_out, OP2, OP1, not_148_out);
  and and_23 (and_23_out, not_149_out, not_150_out, not_151_out, not_152_out, not_153_out, not_154_out, F5, not_155_out, not_156_out, not_157_out, not_158_out, not_159_out);
  and and_24 (and_24_out, not_160_out, not_161_out, not_162_out, not_163_out, not_164_out, not_165_out, F5, not_166_out, not_167_out, not_168_out, not_169_out, F0);
  and and_25 (and_25_out, not_170_out, not_171_out, not_172_out, not_173_out, not_174_out, not_175_out, F5, not_176_out, not_177_out, not_178_out, F1, not_179_out);
  and and_26 (and_26_out, not_180_out, not_181_out, not_182_out, not_183_out, not_184_out, not_185_out, F5, not_186_out, not_187_out, F2, not_188_out, not_189_out);
  and and_27 (and_27_out, not_190_out, not_191_out, not_192_out, not_193_out, not_194_out, not_195_out, F5, not_196_out, F3, not_197_out, F1, F0);
  and and_28 (and_28_out, not_198_out, not_199_out, OP3, not_200_out, not_201_out, not_202_out);
  and and_29 (and_29_out, not_203_out, not_204_out, OP3, OP2, not_205_out, not_206_out);
  and and_30 (and_30_out, not_207_out, not_208_out, OP3, not_209_out, not_210_out, OP0);
  and and_31 (and_31_out, OP5, not_211_out, not_212_out, not_213_out, OP1, OP0);
  and and_32 (and_32_out, OP5, not_214_out, OP3, not_215_out, OP1, OP0);
  and and_33 (and_33_out, OP5, not_216_out, OP3, not_217_out, not_218_out, OP0);
  and and_34 (and_34_out, not_219_out, not_220_out, not_221_out, not_222_out, not_223_out, not_224_out, F5, not_225_out, not_226_out, F2, not_227_out, F0);
  and and_35 (and_35_out, not_228_out, not_229_out, not_230_out, not_231_out, not_232_out, not_233_out, F5, not_234_out, not_235_out, F2, F1, F0);
  and and_36 (and_36_out, not_236_out, not_237_out, not_238_out, not_239_out, not_240_out, not_241_out, F5, not_242_out, F3, not_243_out, F1, not_244_out);
  and and_37 (and_37_out, not_245_out, not_246_out, not_247_out, not_248_out, not_249_out, not_250_out, F5, not_251_out, F3, not_252_out, F1, F0);
  and and_38 (and_38_out, not_253_out, not_254_out, OP3, not_255_out, OP1, not_256_out);
  and and_39 (and_39_out, not_257_out, not_258_out, OP3, OP2, not_259_out, OP0);
  and and_40 (and_40_out, not_260_out, not_261_out, not_262_out, OP2, OP1, not_263_out);
  or or_1 (S1, and_15_out, and_16_out, and_17_out, and_18_out, and_19_out, and_20_out, and_21_out, and_22_out);
  or or_2 (S2, and_23_out, and_24_out, and_25_out, and_26_out, and_27_out, and_28_out, and_29_out, and_30_out, and_31_out, and_32_out, and_33_out);
  or or_3 (S3, and_34_out, and_35_out, and_36_out, and_37_out, and_38_out, and_39_out, and_40_out);
  or or_4 (S0, and_1_out, and_2_out, and_3_out, and_4_out, and_5_out, and_6_out, and_7_out, and_8_out, and_9_out, and_10_out, and_11_out, and_12_out, and_13_out, and_14_out);
endmodule

// 控制信号生成
module \控制信号生成  (
  input  OP0,
  input  OP1,
  input  OP2,
  input  OP3,
  input  OP4,
  input  OP5,
  input  F0,
  input  F1,
  input  F2,
  input  F3,
  input  F4,
  input  F5,
  output MemToReg,
  output MemWrite,
  output ALU_SRC,
  output RegWrite,
  output SysCALL,
  output SignedExt,
  output RegDst,
  output BEQ,
  output BNE,
  output JR,
  output JMP,
  output JAL
);

  wire and_2_out, and_3_out, and_4_out, and_5_out, and_6_out, and_7_out, and_8_out, and_9_out, and_10_out,
       and_11_out, and_12_out, and_13_out, and_14_out, and_15_out, and_16_out, and_17_out, and_18_out,
       and_19_out, and_20_out, and_21_out, and_22_out, and_23_out, and_24_out, and_25_out, and_26_out,
       and_27_out, and_28_out, and_29_out, and_30_out, and_31_out, and_33_out, and_34_out, and_35_out,
       and_36_out, and_37_out, and_38_out, and_39_out, and_40_out, and_41_out, and_42_out, and_43_out,
       and_44_out, and_45_out, and_46_out, and_47_out, and_48_out, and_49_out, and_50_out, and_51_out,
       and_55_out, and_56_out, and_57_out, not_1_out, not_2_out, not_3_out, not_4_out, not_5_out, not_6_out,
       not_7_out, not_8_out, not_9_out, not_10_out, not_11_out, not_12_out, not_13_out, not_14_out,
       not_15_out, not_16_out, not_17_out, not_18_out, not_19_out, not_20_out, not_21_out, not_22_out,
       not_23_out, not_24_out, not_25_out, not_26_out, not_27_out, not_28_out, not_29_out, not_30_out,
       not_31_out, not_32_out, not_33_out, not_34_out, not_35_out, not_36_out, not_37_out, not_38_out,
       not_39_out, not_40_out, not_41_out, not_42_out, not_43_out, not_44_out, not_45_out, not_46_out,
       not_47_out, not_48_out, not_49_out, not_50_out, not_51_out, not_52_out, not_53_out, not_54_out,
       not_55_out, not_56_out, not_57_out, not_58_out, not_59_out, not_60_out, not_61_out, not_62_out,
       not_63_out, not_64_out, not_65_out, not_66_out, not_67_out, not_68_out, not_69_out, not_70_out,
       not_71_out, not_72_out, not_73_out, not_74_out, not_75_out, not_76_out, not_77_out, not_78_out,
       not_79_out, not_80_out, not_81_out, not_82_out, not_83_out, not_84_out, not_85_out, not_86_out,
       not_87_out, not_88_out, not_89_out, not_90_out, not_91_out, not_92_out, not_93_out, not_94_out,
       not_95_out, not_96_out, not_97_out, not_98_out, not_99_out, not_100_out, not_101_out, not_102_out,
       not_103_out, not_104_out, not_105_out, not_106_out, not_107_out, not_108_out, not_109_out,
       not_110_out, not_111_out, not_112_out, not_113_out, not_114_out, not_115_out, not_116_out,
       not_117_out, not_118_out, not_119_out, not_120_out, not_121_out, not_122_out, not_123_out,
       not_124_out, not_125_out, not_126_out, not_127_out, not_128_out, not_129_out, not_130_out,
       not_131_out, not_132_out, not_133_out, not_134_out, not_135_out, not_136_out, not_137_out,
       not_138_out, not_139_out, not_140_out, not_141_out, not_142_out, not_143_out, not_144_out,
       not_145_out, not_146_out, not_147_out, not_148_out, not_149_out, not_150_out, not_151_out,
       not_152_out, not_153_out, not_154_out, not_155_out, not_156_out, not_157_out, not_158_out,
       not_159_out, not_160_out, not_161_out, not_162_out, not_163_out, not_164_out, not_165_out,
       not_166_out, not_167_out, not_168_out, not_169_out, not_170_out, not_171_out, not_172_out,
       not_173_out, not_174_out, not_175_out, not_176_out, not_177_out, not_178_out, not_179_out,
       not_180_out, not_181_out, not_182_out, not_183_out, not_184_out, not_185_out, not_186_out,
       not_187_out, not_188_out, not_189_out, not_190_out, not_191_out, not_192_out, not_193_out,
       not_194_out, not_195_out, not_196_out, not_197_out, not_198_out, not_199_out, not_200_out,
       not_201_out, not_202_out, not_203_out, not_204_out, not_205_out, not_206_out, not_207_out,
       not_208_out, not_209_out, not_210_out, not_211_out, not_212_out, not_213_out, not_214_out,
       not_215_out, not_216_out, not_217_out, not_218_out, not_219_out, not_220_out, not_221_out,
       not_222_out, not_223_out, not_224_out, not_225_out, not_226_out, not_227_out, not_228_out,
       not_229_out, not_230_out, not_231_out, not_232_out, not_233_out, not_234_out, not_235_out,
       not_236_out, not_237_out, not_238_out, not_239_out, not_240_out, not_241_out, not_242_out,
       not_243_out, not_244_out, not_245_out, not_246_out, not_247_out, not_248_out, not_249_out,
       not_250_out, not_251_out, not_252_out, not_253_out, not_254_out, not_255_out, not_256_out,
       not_257_out, not_258_out, not_259_out, not_260_out, not_261_out, not_262_out, not_263_out,
       not_264_out, not_265_out, not_266_out, not_267_out, not_268_out, not_269_out, not_270_out,
       not_271_out, not_272_out, not_273_out, not_274_out, not_275_out, not_276_out, not_277_out,
       not_278_out, not_279_out, not_280_out, not_281_out, not_282_out, not_283_out, not_284_out,
       not_285_out, not_286_out, not_287_out, not_288_out, not_289_out, not_290_out, not_291_out,
       not_292_out, not_293_out, not_294_out, not_295_out, not_296_out, not_297_out, not_298_out,
       not_299_out, not_300_out, not_301_out, not_302_out, not_303_out, not_304_out, not_305_out,
       not_306_out, not_307_out, not_308_out, not_309_out, not_310_out, not_311_out, not_312_out,
       not_313_out, not_314_out, not_315_out, not_316_out, not_317_out, not_318_out, not_319_out,
       not_320_out, not_321_out, not_322_out, not_323_out, not_324_out, not_325_out, not_326_out,
       not_327_out, not_328_out, not_329_out, not_330_out, not_331_out, not_332_out, not_333_out,
       not_334_out, not_335_out, not_336_out, not_337_out, not_338_out, not_339_out, not_340_out,
       not_341_out, not_342_out, not_343_out, not_344_out, not_345_out, not_346_out, not_347_out,
       not_348_out, not_349_out, not_350_out, not_351_out, not_352_out, not_353_out, not_354_out,
       not_355_out, not_356_out, not_357_out, not_358_out, not_359_out, not_360_out, not_361_out,
       not_362_out, not_363_out, not_364_out, not_365_out, not_366_out, not_367_out, not_368_out,
       not_369_out, not_370_out, not_371_out, not_372_out, not_373_out, not_374_out, not_375_out,
       not_376_out, not_377_out, not_378_out, not_379_out, not_380_out, not_381_out, not_382_out,
       not_383_out, not_384_out, not_385_out, not_386_out, not_387_out, not_388_out, not_389_out,
       not_390_out, not_391_out, not_392_out, not_393_out, not_394_out;

  not not_1 (not_1_out, OP4);
  not not_2 (not_2_out, OP3);
  not not_3 (not_3_out, OP2);
  not not_4 (not_4_out, OP4);
  not not_5 (not_5_out, OP2);
  not not_6 (not_6_out, OP4);
  not not_7 (not_7_out, OP2);
  not not_8 (not_8_out, OP1);
  not not_9 (not_9_out, OP5);
  not not_10 (not_10_out, OP4);
  not not_11 (not_11_out, OP2);
  not not_12 (not_12_out, OP1);
  not not_13 (not_13_out, OP0);
  not not_14 (not_14_out, OP5);
  not not_15 (not_15_out, OP4);
  not not_16 (not_16_out, OP1);
  not not_17 (not_17_out, OP0);
  not not_18 (not_18_out, OP5);
  not not_19 (not_19_out, OP4);
  not not_20 (not_20_out, OP2);
  not not_21 (not_21_out, OP1);
  not not_22 (not_22_out, OP5);
  not not_23 (not_23_out, OP4);
  not not_24 (not_24_out, OP2);
  not not_25 (not_25_out, OP0);
  not not_26 (not_26_out, OP5);
  not not_27 (not_27_out, OP4);
  not not_28 (not_28_out, OP1);
  not not_29 (not_29_out, OP4);
  not not_30 (not_30_out, OP3);
  not not_31 (not_31_out, OP2);
  not not_32 (not_32_out, OP4);
  not not_33 (not_33_out, OP2);
  not not_34 (not_34_out, OP4);
  not not_35 (not_35_out, OP2);
  not not_36 (not_36_out, OP1);
  not not_37 (not_37_out, OP5);
  not not_38 (not_38_out, OP4);
  not not_39 (not_39_out, OP3);
  not not_40 (not_40_out, OP2);
  not not_41 (not_41_out, OP1);
  not not_42 (not_42_out, OP0);
  not not_43 (not_43_out, F5);
  not not_44 (not_44_out, F4);
  not not_45 (not_45_out, F3);
  not not_46 (not_46_out, F2);
  not not_47 (not_47_out, F1);
  not not_48 (not_48_out, F0);
  not not_49 (not_49_out, OP5);
  not not_50 (not_50_out, OP4);
  not not_51 (not_51_out, OP3);
  not not_52 (not_52_out, OP2);
  not not_53 (not_53_out, OP1);
  not not_54 (not_54_out, OP0);
  not not_55 (not_55_out, F5);
  not not_56 (not_56_out, F4);
  not not_57 (not_57_out, F3);
  not not_58 (not_58_out, F2);
  not not_59 (not_59_out, OP5);
  not not_60 (not_60_out, OP4);
  not not_61 (not_61_out, OP3);
  not not_62 (not_62_out, OP2);
  not not_63 (not_63_out, OP1);
  not not_64 (not_64_out, OP0);
  not not_65 (not_65_out, F5);
  not not_66 (not_66_out, F4);
  not not_67 (not_67_out, F3);
  not not_68 (not_68_out, F2);
  not not_69 (not_69_out, F0);
  not not_70 (not_70_out, OP5);
  not not_71 (not_71_out, OP4);
  not not_72 (not_72_out, OP3);
  not not_73 (not_73_out, OP2);
  not not_74 (not_74_out, OP1);
  not not_75 (not_75_out, OP0);
  not not_76 (not_76_out, F4);
  not not_77 (not_77_out, F3);
  not not_78 (not_78_out, F2);
  not not_79 (not_79_out, F1);
  not not_80 (not_80_out, F0);
  not not_81 (not_81_out, OP5);
  not not_82 (not_82_out, OP4);
  not not_83 (not_83_out, OP3);
  not not_84 (not_84_out, OP2);
  not not_85 (not_85_out, OP1);
  not not_86 (not_86_out, OP0);
  not not_87 (not_87_out, F4);
  not not_88 (not_88_out, F3);
  not not_89 (not_89_out, F2);
  not not_90 (not_90_out, F1);
  not not_91 (not_91_out, OP5);
  not not_92 (not_92_out, OP4);
  not not_93 (not_93_out, OP3);
  not not_94 (not_94_out, OP2);
  not not_95 (not_95_out, OP1);
  not not_96 (not_96_out, OP0);
  not not_97 (not_97_out, F4);
  not not_98 (not_98_out, F3);
  not not_99 (not_99_out, F2);
  not not_100 (not_100_out, F0);
  not not_101 (not_101_out, OP5);
  not not_102 (not_102_out, OP4);
  not not_103 (not_103_out, OP3);
  not not_104 (not_104_out, OP2);
  not not_105 (not_105_out, OP1);
  not not_106 (not_106_out, OP0);
  not not_107 (not_107_out, F4);
  not not_108 (not_108_out, F3);
  not not_109 (not_109_out, F1);
  not not_110 (not_110_out, F0);
  not not_111 (not_111_out, OP5);
  not not_112 (not_112_out, OP4);
  not not_113 (not_113_out, OP3);
  not not_114 (not_114_out, OP2);
  not not_115 (not_115_out, OP1);
  not not_116 (not_116_out, OP0);
  not not_117 (not_117_out, F4);
  not not_118 (not_118_out, F3);
  not not_119 (not_119_out, F1);
  not not_120 (not_120_out, OP5);
  not not_121 (not_121_out, OP4);
  not not_122 (not_122_out, OP3);
  not not_123 (not_123_out, OP2);
  not not_124 (not_124_out, OP1);
  not not_125 (not_125_out, OP0);
  not not_126 (not_126_out, F4);
  not not_127 (not_127_out, F3);
  not not_128 (not_128_out, OP5);
  not not_129 (not_129_out, OP4);
  not not_130 (not_130_out, OP3);
  not not_131 (not_131_out, OP2);
  not not_132 (not_132_out, OP1);
  not not_133 (not_133_out, OP0);
  not not_134 (not_134_out, F4);
  not not_135 (not_135_out, F2);
  not not_136 (not_136_out, F0);
  not not_137 (not_137_out, OP5);
  not not_138 (not_138_out, OP4);
  not not_139 (not_139_out, OP3);
  not not_140 (not_140_out, OP2);
  not not_141 (not_141_out, OP1);
  not not_142 (not_142_out, OP0);
  not not_143 (not_143_out, F4);
  not not_144 (not_144_out, F2);
  not not_145 (not_145_out, OP5);
  not not_146 (not_146_out, OP4);
  not not_147 (not_147_out, OP3);
  not not_148 (not_148_out, OP2);
  not not_149 (not_149_out, OP5);
  not not_150 (not_150_out, OP4);
  not not_151 (not_151_out, OP2);
  not not_152 (not_152_out, OP1);
  not not_153 (not_153_out, OP0);
  not not_154 (not_154_out, OP5);
  not not_155 (not_155_out, OP4);
  not not_156 (not_156_out, OP1);
  not not_157 (not_157_out, OP0);
  not not_158 (not_158_out, OP5);
  not not_159 (not_159_out, OP4);
  not not_160 (not_160_out, OP2);
  not not_161 (not_161_out, OP1);
  not not_162 (not_162_out, OP5);
  not not_163 (not_163_out, OP4);
  not not_164 (not_164_out, OP2);
  not not_165 (not_165_out, OP0);
  not not_166 (not_166_out, OP5);
  not not_167 (not_167_out, OP4);
  not not_168 (not_168_out, OP1);
  not not_169 (not_169_out, OP4);
  not not_170 (not_170_out, OP3);
  not not_171 (not_171_out, OP2);
  not not_172 (not_172_out, OP5);
  not not_173 (not_173_out, OP4);
  not not_174 (not_174_out, OP3);
  not not_175 (not_175_out, OP2);
  not not_176 (not_176_out, OP1);
  not not_177 (not_177_out, OP0);
  not not_178 (not_178_out, F5);
  not not_179 (not_179_out, F4);
  not not_180 (not_180_out, F3);
  not not_181 (not_181_out, F1);
  not not_182 (not_182_out, F0);
  not not_183 (not_183_out, OP5);
  not not_184 (not_184_out, OP4);
  not not_185 (not_185_out, OP3);
  not not_186 (not_186_out, OP2);
  not not_187 (not_187_out, OP1);
  not not_188 (not_188_out, OP0);
  not not_189 (not_189_out, F5);
  not not_190 (not_190_out, F4);
  not not_191 (not_191_out, F3);
  not not_192 (not_192_out, OP5);
  not not_193 (not_193_out, OP4);
  not not_194 (not_194_out, OP3);
  not not_195 (not_195_out, OP2);
  not not_196 (not_196_out, OP1);
  not not_197 (not_197_out, OP0);
  not not_198 (not_198_out, F5);
  not not_199 (not_199_out, F4);
  not not_200 (not_200_out, F1);
  not not_201 (not_201_out, F0);
  not not_202 (not_202_out, OP5);
  not not_203 (not_203_out, OP4);
  not not_204 (not_204_out, OP2);
  not not_205 (not_205_out, OP1);
  not not_206 (not_206_out, OP0);
  not not_207 (not_207_out, OP5);
  not not_208 (not_208_out, OP4);
  not not_209 (not_209_out, OP2);
  not not_210 (not_210_out, OP1);
  not not_211 (not_211_out, OP5);
  not not_212 (not_212_out, OP4);
  not not_213 (not_213_out, OP2);
  not not_214 (not_214_out, OP0);
  not not_215 (not_215_out, OP4);
  not not_216 (not_216_out, OP3);
  not not_217 (not_217_out, OP2);
  not not_218 (not_218_out, OP4);
  not not_219 (not_219_out, OP2);
  not not_220 (not_220_out, OP4);
  not not_221 (not_221_out, OP2);
  not not_222 (not_222_out, OP1);
  not not_223 (not_223_out, OP5);
  not not_224 (not_224_out, OP4);
  not not_225 (not_225_out, OP3);
  not not_226 (not_226_out, OP2);
  not not_227 (not_227_out, OP1);
  not not_228 (not_228_out, OP0);
  not not_229 (not_229_out, F5);
  not not_230 (not_230_out, F4);
  not not_231 (not_231_out, F3);
  not not_232 (not_232_out, F2);
  not not_233 (not_233_out, F1);
  not not_234 (not_234_out, F0);
  not not_235 (not_235_out, OP5);
  not not_236 (not_236_out, OP4);
  not not_237 (not_237_out, OP3);
  not not_238 (not_238_out, OP2);
  not not_239 (not_239_out, OP1);
  not not_240 (not_240_out, OP0);
  not not_241 (not_241_out, F5);
  not not_242 (not_242_out, F4);
  not not_243 (not_243_out, F3);
  not not_244 (not_244_out, F2);
  not not_245 (not_245_out, OP5);
  not not_246 (not_246_out, OP4);
  not not_247 (not_247_out, OP3);
  not not_248 (not_248_out, OP2);
  not not_249 (not_249_out, OP1);
  not not_250 (not_250_out, OP0);
  not not_251 (not_251_out, F5);
  not not_252 (not_252_out, F4);
  not not_253 (not_253_out, F3);
  not not_254 (not_254_out, F2);
  not not_255 (not_255_out, F0);
  not not_256 (not_256_out, OP5);
  not not_257 (not_257_out, OP4);
  not not_258 (not_258_out, OP3);
  not not_259 (not_259_out, OP2);
  not not_260 (not_260_out, OP1);
  not not_261 (not_261_out, OP0);
  not not_262 (not_262_out, F4);
  not not_263 (not_263_out, F3);
  not not_264 (not_264_out, F2);
  not not_265 (not_265_out, F1);
  not not_266 (not_266_out, F0);
  not not_267 (not_267_out, OP5);
  not not_268 (not_268_out, OP4);
  not not_269 (not_269_out, OP3);
  not not_270 (not_270_out, OP2);
  not not_271 (not_271_out, OP1);
  not not_272 (not_272_out, OP0);
  not not_273 (not_273_out, F4);
  not not_274 (not_274_out, F3);
  not not_275 (not_275_out, F2);
  not not_276 (not_276_out, F1);
  not not_277 (not_277_out, OP5);
  not not_278 (not_278_out, OP4);
  not not_279 (not_279_out, OP3);
  not not_280 (not_280_out, OP2);
  not not_281 (not_281_out, OP1);
  not not_282 (not_282_out, OP0);
  not not_283 (not_283_out, F4);
  not not_284 (not_284_out, F3);
  not not_285 (not_285_out, F2);
  not not_286 (not_286_out, F0);
  not not_287 (not_287_out, OP5);
  not not_288 (not_288_out, OP4);
  not not_289 (not_289_out, OP3);
  not not_290 (not_290_out, OP2);
  not not_291 (not_291_out, OP1);
  not not_292 (not_292_out, OP0);
  not not_293 (not_293_out, F4);
  not not_294 (not_294_out, F3);
  not not_295 (not_295_out, F1);
  not not_296 (not_296_out, F0);
  not not_297 (not_297_out, OP5);
  not not_298 (not_298_out, OP4);
  not not_299 (not_299_out, OP3);
  not not_300 (not_300_out, OP2);
  not not_301 (not_301_out, OP1);
  not not_302 (not_302_out, OP0);
  not not_303 (not_303_out, F4);
  not not_304 (not_304_out, F3);
  not not_305 (not_305_out, F1);
  not not_306 (not_306_out, OP5);
  not not_307 (not_307_out, OP4);
  not not_308 (not_308_out, OP3);
  not not_309 (not_309_out, OP2);
  not not_310 (not_310_out, OP1);
  not not_311 (not_311_out, OP0);
  not not_312 (not_312_out, F4);
  not not_313 (not_313_out, F3);
  not not_314 (not_314_out, OP5);
  not not_315 (not_315_out, OP4);
  not not_316 (not_316_out, OP3);
  not not_317 (not_317_out, OP2);
  not not_318 (not_318_out, OP1);
  not not_319 (not_319_out, OP0);
  not not_320 (not_320_out, F4);
  not not_321 (not_321_out, F2);
  not not_322 (not_322_out, F0);
  not not_323 (not_323_out, OP5);
  not not_324 (not_324_out, OP4);
  not not_325 (not_325_out, OP3);
  not not_326 (not_326_out, OP2);
  not not_327 (not_327_out, OP1);
  not not_328 (not_328_out, OP0);
  not not_329 (not_329_out, F4);
  not not_330 (not_330_out, F2);
  not not_331 (not_331_out, OP5);
  not not_332 (not_332_out, OP4);
  not not_333 (not_333_out, OP3);
  not not_334 (not_334_out, OP2);
  not not_335 (not_335_out, OP1);
  not not_336 (not_336_out, OP0);
  not not_337 (not_337_out, F5);
  not not_338 (not_338_out, F4);
  not not_339 (not_339_out, F3);
  not not_340 (not_340_out, F1);
  not not_341 (not_341_out, F0);
  not not_342 (not_342_out, OP5);
  not not_343 (not_343_out, OP4);
  not not_344 (not_344_out, OP3);
  not not_345 (not_345_out, OP2);
  not not_346 (not_346_out, OP1);
  not not_347 (not_347_out, OP0);
  not not_348 (not_348_out, F5);
  not not_349 (not_349_out, F4);
  not not_350 (not_350_out, F3);
  not not_351 (not_351_out, OP5);
  not not_352 (not_352_out, OP4);
  not not_353 (not_353_out, OP3);
  not not_354 (not_354_out, OP1);
  not not_355 (not_355_out, OP0);
  not not_356 (not_356_out, OP5);
  not not_357 (not_357_out, OP4);
  not not_358 (not_358_out, OP3);
  not not_359 (not_359_out, OP1);
  not not_360 (not_360_out, OP5);
  not not_361 (not_361_out, OP4);
  not not_362 (not_362_out, OP3);
  not not_363 (not_363_out, OP2);
  not not_364 (not_364_out, OP1);
  not not_365 (not_365_out, OP0);
  not not_366 (not_366_out, F5);
  not not_367 (not_367_out, F4);
  not not_368 (not_368_out, F2);
  not not_369 (not_369_out, F1);
  not not_370 (not_370_out, F0);
  not not_371 (not_371_out, OP5);
  not not_372 (not_372_out, OP4);
  not not_373 (not_373_out, OP3);
  not not_374 (not_374_out, OP2);
  not not_375 (not_375_out, OP1);
  not not_376 (not_376_out, OP0);
  not not_377 (not_377_out, F5);
  not not_378 (not_378_out, F4);
  not not_379 (not_379_out, F2);
  not not_380 (not_380_out, F1);
  not not_381 (not_381_out, F0);
  not not_382 (not_382_out, OP5);
  not not_383 (not_383_out, OP4);
  not not_384 (not_384_out, OP3);
  not not_385 (not_385_out, OP2);
  not not_386 (not_386_out, OP0);
  not not_387 (not_387_out, OP5);
  not not_388 (not_388_out, OP4);
  not not_389 (not_389_out, OP3);
  not not_390 (not_390_out, OP2);
  not not_391 (not_391_out, OP5);
  not not_392 (not_392_out, OP4);
  not not_393 (not_393_out, OP3);
  not not_394 (not_394_out, OP2);
  and and_1 (MemToReg, OP5, not_1_out, not_2_out, not_3_out, OP1, OP0);
  and and_2 (and_2_out, OP5, not_4_out, OP3, not_5_out, OP1, OP0);
  and and_3 (and_3_out, OP5, not_6_out, OP3, not_7_out, not_8_out, OP0);
  and and_4 (and_4_out, not_9_out, not_10_out, OP3, not_11_out, not_12_out, not_13_out);
  and and_5 (and_5_out, not_14_out, not_15_out, OP3, OP2, not_16_out, not_17_out);
  and and_6 (and_6_out, not_18_out, not_19_out, OP3, not_20_out, not_21_out, OP0);
  and and_7 (and_7_out, not_22_out, not_23_out, OP3, not_24_out, OP1, not_25_out);
  and and_8 (and_8_out, not_26_out, not_27_out, OP3, OP2, not_28_out, OP0);
  and and_9 (and_9_out, OP5, not_29_out, not_30_out, not_31_out, OP1, OP0);
  and and_10 (and_10_out, OP5, not_32_out, OP3, not_33_out, OP1, OP0);
  and and_11 (and_11_out, OP5, not_34_out, OP3, not_35_out, not_36_out, OP0);
  and and_12 (and_12_out, not_37_out, not_38_out, not_39_out, not_40_out, not_41_out, not_42_out, not_43_out, not_44_out, not_45_out, not_46_out, not_47_out, not_48_out);
  and and_13 (and_13_out, not_49_out, not_50_out, not_51_out, not_52_out, not_53_out, not_54_out, not_55_out, not_56_out, not_57_out, not_58_out, F1, F0);
  and and_14 (and_14_out, not_59_out, not_60_out, not_61_out, not_62_out, not_63_out, not_64_out, not_65_out, not_66_out, not_67_out, not_68_out, F1, not_69_out);
  and and_15 (and_15_out, not_70_out, not_71_out, not_72_out, not_73_out, not_74_out, not_75_out, F5, not_76_out, not_77_out, not_78_out, not_79_out, not_80_out);
  and and_16 (and_16_out, not_81_out, not_82_out, not_83_out, not_84_out, not_85_out, not_86_out, F5, not_87_out, not_88_out, not_89_out, not_90_out, F0);
  and and_17 (and_17_out, not_91_out, not_92_out, not_93_out, not_94_out, not_95_out, not_96_out, F5, not_97_out, not_98_out, not_99_out, F1, not_100_out);
  and and_18 (and_18_out, not_101_out, not_102_out, not_103_out, not_104_out, not_105_out, not_106_out, F5, not_107_out, not_108_out, F2, not_109_out, not_110_out);
  and and_19 (and_19_out, not_111_out, not_112_out, not_113_out, not_114_out, not_115_out, not_116_out, F5, not_117_out, not_118_out, F2, not_119_out, F0);
  and and_20 (and_20_out, not_120_out, not_121_out, not_122_out, not_123_out, not_124_out, not_125_out, F5, not_126_out, not_127_out, F2, F1, F0);
  and and_21 (and_21_out, not_128_out, not_129_out, not_130_out, not_131_out, not_132_out, not_133_out, F5, not_134_out, F3, not_135_out, F1, not_136_out);
  and and_22 (and_22_out, not_137_out, not_138_out, not_139_out, not_140_out, not_141_out, not_142_out, F5, not_143_out, F3, not_144_out, F1, F0);
  and and_23 (and_23_out, not_145_out, not_146_out, not_147_out, not_148_out, OP1, OP0);
  and and_24 (and_24_out, not_149_out, not_150_out, OP3, not_151_out, not_152_out, not_153_out);
  and and_25 (and_25_out, not_154_out, not_155_out, OP3, OP2, not_156_out, not_157_out);
  and and_26 (and_26_out, not_158_out, not_159_out, OP3, not_160_out, not_161_out, OP0);
  and and_27 (and_27_out, not_162_out, not_163_out, OP3, not_164_out, OP1, not_165_out);
  and and_28 (and_28_out, not_166_out, not_167_out, OP3, OP2, not_168_out, OP0);
  and and_29 (and_29_out, OP5, not_169_out, not_170_out, not_171_out, OP1, OP0);
  and and_30 (and_30_out, not_172_out, not_173_out, not_174_out, not_175_out, not_176_out, not_177_out, not_178_out, not_179_out, not_180_out, F2, not_181_out, not_182_out);
  and and_31 (and_31_out, not_183_out, not_184_out, not_185_out, not_186_out, not_187_out, not_188_out, not_189_out, not_190_out, not_191_out, F2, F1, F0);
  and and_32 (SysCALL, not_192_out, not_193_out, not_194_out, not_195_out, not_196_out, not_197_out, not_198_out, not_199_out, F3, F2, not_200_out, not_201_out);
  and and_33 (and_33_out, not_202_out, not_203_out, OP3, not_204_out, not_205_out, not_206_out);
  and and_34 (and_34_out, not_207_out, not_208_out, OP3, not_209_out, not_210_out, OP0);
  and and_35 (and_35_out, not_211_out, not_212_out, OP3, not_213_out, OP1, not_214_out);
  and and_36 (and_36_out, OP5, not_215_out, not_216_out, not_217_out, OP1, OP0);
  and and_37 (and_37_out, OP5, not_218_out, OP3, not_219_out, OP1, OP0);
  and and_38 (and_38_out, OP5, not_220_out, OP3, not_221_out, not_222_out, OP0);
  and and_39 (and_39_out, not_223_out, not_224_out, not_225_out, not_226_out, not_227_out, not_228_out, not_229_out, not_230_out, not_231_out, not_232_out, not_233_out, not_234_out);
  and and_40 (and_40_out, not_235_out, not_236_out, not_237_out, not_238_out, not_239_out, not_240_out, not_241_out, not_242_out, not_243_out, not_244_out, F1, F0);
  and and_41 (and_41_out, not_245_out, not_246_out, not_247_out, not_248_out, not_249_out, not_250_out, not_251_out, not_252_out, not_253_out, not_254_out, F1, not_255_out);
  and and_42 (and_42_out, not_256_out, not_257_out, not_258_out, not_259_out, not_260_out, not_261_out, F5, not_262_out, not_263_out, not_264_out, not_265_out, not_266_out);
  and and_43 (and_43_out, not_267_out, not_268_out, not_269_out, not_270_out, not_271_out, not_272_out, F5, not_273_out, not_274_out, not_275_out, not_276_out, F0);
  and and_44 (and_44_out, not_277_out, not_278_out, not_279_out, not_280_out, not_281_out, not_282_out, F5, not_283_out, not_284_out, not_285_out, F1, not_286_out);
  and and_45 (and_45_out, not_287_out, not_288_out, not_289_out, not_290_out, not_291_out, not_292_out, F5, not_293_out, not_294_out, F2, not_295_out, not_296_out);
  and and_46 (and_46_out, not_297_out, not_298_out, not_299_out, not_300_out, not_301_out, not_302_out, F5, not_303_out, not_304_out, F2, not_305_out, F0);
  and and_47 (and_47_out, not_306_out, not_307_out, not_308_out, not_309_out, not_310_out, not_311_out, F5, not_312_out, not_313_out, F2, F1, F0);
  and and_48 (and_48_out, not_314_out, not_315_out, not_316_out, not_317_out, not_318_out, not_319_out, F5, not_320_out, F3, not_321_out, F1, not_322_out);
  and and_49 (and_49_out, not_323_out, not_324_out, not_325_out, not_326_out, not_327_out, not_328_out, F5, not_329_out, F3, not_330_out, F1, F0);
  and and_50 (and_50_out, not_331_out, not_332_out, not_333_out, not_334_out, not_335_out, not_336_out, not_337_out, not_338_out, not_339_out, F2, not_340_out, not_341_out);
  and and_51 (and_51_out, not_342_out, not_343_out, not_344_out, not_345_out, not_346_out, not_347_out, not_348_out, not_349_out, not_350_out, F2, F1, F0);
  and and_52 (BEQ, not_351_out, not_352_out, not_353_out, OP2, not_354_out, not_355_out);
  and and_53 (BNE, not_356_out, not_357_out, not_358_out, OP2, not_359_out, OP0);
  and and_54 (JR, not_360_out, not_361_out, not_362_out, not_363_out, not_364_out, not_365_out, not_366_out, not_367_out, F3, not_368_out, not_369_out, not_370_out);
  and and_55 (and_55_out, not_371_out, not_372_out, not_373_out, not_374_out, not_375_out, not_376_out, not_377_out, not_378_out, F3, not_379_out, not_380_out, not_381_out);
  and and_56 (and_56_out, not_382_out, not_383_out, not_384_out, not_385_out, OP1, not_386_out);
  and and_57 (and_57_out, not_387_out, not_388_out, not_389_out, not_390_out, OP1, OP0);
  and and_58 (JAL, not_391_out, not_392_out, not_393_out, not_394_out, OP1, OP0);
  or or_1 (MemWrite, and_2_out, and_3_out);
  or or_2 (ALU_SRC, and_4_out, and_5_out, and_6_out, and_7_out, and_8_out, and_9_out, and_10_out, and_11_out);
  or or_3 (SignedExt, and_33_out, and_34_out, and_35_out, and_36_out, and_37_out, and_38_out);
  or or_4 (JMP, and_55_out, and_56_out, and_57_out);
  or or_5 (RegWrite, and_12_out, and_13_out, and_14_out, and_15_out, and_16_out, and_17_out, and_18_out, and_19_out, and_20_out, and_21_out, and_22_out, and_23_out, and_24_out, and_25_out, and_26_out, and_27_out, and_28_out, and_29_out, and_30_out, and_31_out);
  or or_6 (RegDst, and_39_out, and_40_out, and_41_out, and_42_out, and_43_out, and_44_out, and_45_out, and_46_out, and_47_out, and_48_out, and_49_out, and_50_out, and_51_out);
endmodule

// ALU
module MIPS_ALU (
  input  [4:0] shamt,
  input  [31:0] X,
  input  [31:0] Y,
  input  [3:0] AluOP,
  output Equal,
  output [31:0] Result,
  output [31:0] Result_2
);

  wire [0:0] comparator_1_lt, comparator_2_lt;
  wire [31:0] adder_1_out, AND_out, divider_1_out, divider_1_rem, multiplier_1_cout, multiplier_1_out,
       NOR_out, OR_out, shifter_1_out, shifter_2_out, shifter_3_out, subtractor_1_out, XOR_out;

  assign AND_out = X & Y;  // AND_Gate AND, 32 bits wide
  assign OR_out = X | Y;  // OR_Gate OR, 32 bits wide
  Shifter #(.width(32)) shifter_1 (.in(Y), .\dist (shamt), .out(shifter_1_out));
  Shifter #(.width(32), .shift("ar")) shifter_2 (.in(Y), .\dist (shamt), .out(shifter_2_out));
  Shifter #(.width(32), .shift("lr")) shifter_3 (.in(Y), .\dist (shamt), .out(shifter_3_out));
  Multiplier #(.width(32)) multiplier_1 (.a(X), .b(Y), .out(multiplier_1_out), .cout(multiplier_1_cout));  // open: cin
  Divider #(.width(32)) divider_1 (.a(X), .b(Y), .out(divider_1_out), .rem(divider_1_rem));  // open: upper
  Adder #(.width(32)) adder_1 (.a(X), .b(Y), .out(adder_1_out));  // open: cin, cout
  Subtractor #(.width(32)) subtractor_1 (.a(X), .b(Y), .out(subtractor_1_out));  // open: bin, bout
  assign XOR_out = X ^ Y;  // XOR_Gate XOR, 32 bits wide
  assign NOR_out = ~(X | Y);  // NOR_Gate NOR, 32 bits wide
  Comparator #(.width(32)) comparator_1 (.a(X), .b(Y), .eq(Equal), .lt(comparator_1_lt[0]));  // open: gt
  Comparator #(.width(32), .mode("unsigned")) comparator_2 (.a(X), .b(Y), .lt(comparator_2_lt[0]));  // open: gt, eq
  Multiplexer #(.select(4), .width(32), .enable("false")) multiplexer_1 (
    .in0(shifter_1_out), .in1(shifter_2_out), .in2(shifter_3_out), .in3(multiplier_1_out),
    .in4(divider_1_out), .in5(adder_1_out), .in6(subtractor_1_out), .in7(AND_out), .in8(OR_out),
    .in9(XOR_out), .in10(NOR_out), .in11({{31{1'b0}}, comparator_1_lt[0]}),
    .in12({{31{1'b0}}, comparator_2_lt[0]}), .in13({32{1'b0}}), .in14({32{1'b0}}), .in15({32{1'b0}}),
    .out(Result), .sel(AluOP));
  Multiplexer #(.select(4), .width(32), .enable("false")) multiplexer_2 (
    .in0({32{1'b0}}), .in1({32{1'b0}}), .in2({32{1'b0}}), .in3(multiplier_1_cout), .in4(divider_1_rem),
    .in5({32{1'b0}}), .in6({32{1'b0}}), .in7({32{1'b0}}), .in8({32{1'b0}}), .in9({32{1'b0}}),
    .in10({32{1'b0}}), .in11({32{1'b0}}), .in12({32{1'b0}}), .in13({32{1'b0}}), .in14({32{1'b0}}),
    .in15({32{1'b0}}), .out(Result_2), .sel(AluOP));

  // Other names for the same wires on the sheet: Result2[31:0] = Result_2; S[3:0] = AluOP

  // Notes on the sheet:
  //   不要改变此引脚区域内容，也不要改变ALU封装形式
  //   输入引脚
  //   输出引脚
endmodule

module MIPS_Regifile (
  input  [31:0] Din,
  input  Clk,
  input  WE,
  input  [4:0] R1_num,
  input  [4:0] W_num,
  input  [4:0] R2_num,
  output [31:0] R1,
  output [31:0] R2
);

  // RegisterFile registerfile_1: pin names not known; wires that end beside it: Din, Clk, WE, W_num, R1_num, R2_num, R1, R2
endmodule

module \理想流水线  (
  output [4:0] out_1
);

  wire AluSrcB, and_1_out, and_2_out, and_3_out, and_4_out, Beq, Bi_Jiao, BLEZ, Bne, CLK, comparator_1_eq,
       EN, Go, IR1, IR2, IR3, JAL, JMP, JR, LOCK, MEM_JAL, MEM_JMP, MEM_JR, MEM_MemToReg, MEM_MemWrite,
       MEM_RegDst, MEM_RegWrite, MEM_SH, Mem_Syscall, MemToReg, MemWrite, mips_alu_1_equal,
       multiplexer_10_out, or_1_out, RegDst, RegWrite, RST, SH, SignedExt, Syscall, V, W1, W2, W3, WB_JAL,
       WB_JMP, WB_JR, WB_MemToReg, WB_RegDst, WB_RegWrite, WB_SH, WB_Syscall, \硬布线控制器_1_alu_src ,
       \硬布线控制器_1_beq , \硬布线控制器_1_blez , \硬布线控制器_1_bne , \硬布线控制器_1_jal , \硬布线控制器_1_jmp , \硬布线控制器_1_jr ,
       \硬布线控制器_1_memtoreg , \硬布线控制器_1_memwrite , \硬布线控制器_1_regdst , \硬布线控制器_1_regwrite , \硬布线控制器_1_sh ,
       \硬布线控制器_1_signedext , \硬布线控制器_1_syscall , \硬布线控制器_1_v ;
  wire [3:0] AluOP, multiplexer_18_out, multiplexer_19_out, \硬布线控制器_1_alu_op ;
  wire [4:0] multiplexer_8_out, multiplexer_9_out, multiplexer_11_out, multiplexer_13_out;
  wire [15:0] _0_15, _0_15D, _16, \LoadUse次数 , \总周期数 , \插入气泡数 , \无条件分支数 , \条件分支成功数 ;
  wire [25:16] _25_0;
  wire [31:0] adder_2_out, ALU_Result, bit_extender_2_out, bit_extender_3_out, EX_PC, ID_PC, IF_PC, Imm,
       Imm1, LedData, MEM_ALU_Result, MEM_IR, MEM_PC, Mem_R1, multiplexer_2_out, multiplexer_3_out,
       multiplexer_4_out, multiplexer_5_out, multiplexer_6_out, multiplexer_7_out, multiplexer_12_out,
       multiplexer_15_out, multiplexer_16_out, multiplexer_17_out, multiplexer_20_out, PC_q, R1, R2, R11,
       R22, RAM_Out, rom_1_data, shifter_1_out, WB_ALU_Result, WB_IR, WB_PC, WB_R1, WB_R2, WB_RAM_Out;
  wire [31:16] EX_IR, MEM_R2;
  wire [31:26] ID_IR;

  Button \u_总复位  (.out(RST));
  Button _1 (.out(IR1));
  Button _2 (.out(IR2));
  Button _3 (.out(IR3));
  Multiplexer #(.enable("false")) multiplexer_1 (.in0(1'b1), .in1(1'b0), .out(EN), .sel(and_1_out));
  Button \u_继续运行  (.out(Go));
  LED led_1 (.in(W1));
  LED led_2 (.in(W2));
  LED led_3 (.in(W3));
  Register #(.width(32)) PC (.D(multiplexer_6_out), .en(EN), .Q(PC_q), .clk(CLK), .clr(RST));
  and and_1 (and_1_out, LOCK, ~Go);  // AND_Gate
  Counter #(.width(16), .max('hffff)) counter_1 (.count(EN), .Q(\总周期数 ), .clk(CLK), .clr(RST));  // open: load, D, carry
  Hex_Digit_Display hex_digit_display_1 (.value(LedData[31:28]));  // open: dp
  assign Imm = {{16{_0_15D[15]}}, _0_15D};  // Bit_Extender bit_extender_1
  Adder #(.width(32)) adder_1 (.a(PC_q), .b(32'h4), .out(IF_PC));  // open: cin, cout
  assign bit_extender_2_out = {{16{_0_15[15]}}, _0_15};  // Bit_Extender bit_extender_2
  Hex_Digit_Display hex_digit_display_2 (.value(LedData[27:24]));  // open: dp
  Hex_Digit_Display hex_digit_display_3 (.value(LedData[23:20]));  // open: dp
  ROM #(.addrWidth(10), .dataWidth(32)) rom_1 (.addr(PC_q[11:2]), .data(rom_1_data));  // open: sel
  Shifter #(.width(32)) shifter_1 (.in(Imm1), .\dist (5'b00010), .out(shifter_1_out));
  assign bit_extender_3_out = {{16{1'b0}}, _0_15};  // Bit_Extender bit_extender_3
  Hex_Digit_Display hex_digit_display_4 (.value(LedData[19:16]));  // open: dp
  Hex_Digit_Display hex_digit_display_5 (.value(LedData[15:12]));  // open: dp
  Adder #(.width(32)) adder_2 (.a(EX_PC), .b(shifter_1_out), .out(adder_2_out));  // open: cin, cout
  Multiplexer #(.width(32), .enable("false")) multiplexer_2 (
    .in0({4'b0000, _25_0, _0_15D, 2'b00}), .in1(R1), .out(multiplexer_2_out), .sel(JR));
  Multiplexer #(.width(32), .enable("false")) multiplexer_3 (
    .in0(bit_extender_3_out), .in1(bit_extender_2_out), .out(multiplexer_3_out), .sel(SignedExt));
  Hex_Digit_Display hex_digit_display_6 (.value(LedData[11:8]));  // open: dp
  Hex_Digit_Display hex_digit_display_7 (.value(LedData[7:4]));  // open: dp
  Clock clock_1 (.out(CLK));
  IF_ID if_id_1 (
    .IR(rom_1_data), .PC(IF_PC), .IR_2({ID_IR, _25_0, _0_15D}), .PC_2(ID_PC), .RST(RST), .EN(EN), .CLK(CLK));
  Multiplexer #(.width(32), .enable("false")) multiplexer_4 (
    .in0(IF_PC), .in1(adder_2_out), .out(multiplexer_4_out), .sel(Bi_Jiao));
  Multiplexer #(.width(32), .enable("false")) multiplexer_5 (
    .in0(R22), .in1(multiplexer_3_out), .out(multiplexer_5_out), .sel(AluSrcB));
  Hex_Digit_Display hex_digit_display_8 (.value(LedData[3:0]));  // open: dp
  Multiplexer #(.width(32), .enable("false")) multiplexer_6 (
    .in0(multiplexer_4_out), .in1(multiplexer_2_out), .out(multiplexer_6_out), .sel(JMP));
  Multiplexer #(.width(32), .enable("false")) multiplexer_7 (
    .in0(multiplexer_5_out), .in1({32{1'b0}}), .out(multiplexer_7_out), .sel(BLEZ));
  Multiplexer #(.width(5), .enable("false")) multiplexer_8 (
    .in0(_0_15[10:6]), .in1(R11[4:0]), .out(multiplexer_8_out), .sel(V));
  and and_2 (and_2_out, Beq, mips_alu_1_equal);
  and and_3 (and_3_out, Bne, ~mips_alu_1_equal);  // AND_Gate
  MIPS_ALU mips_alu_1 (
    .X(R11), .Y(multiplexer_7_out), .AluOP(AluOP), .Equal(mips_alu_1_equal), .Result(ALU_Result),
    .shamt(multiplexer_8_out));  // open: Result_2
  // Probe on \总周期数 
  // Probe on \无条件分支数 
  // Probe on \条件分支成功数 
  // Probe on \插入气泡数 
  // Probe on \LoadUse次数 
  Multiplexer #(.width(5), .enable("false")) multiplexer_9 (
    .in0(_25_0[25:21]), .in1(5'b00010), .out(multiplexer_9_out), .sel(\硬布线控制器_1_syscall ));
  Multiplexer #(.enable("false")) multiplexer_10 (.in0(1'b0), .in1(or_1_out), .out(multiplexer_10_out), .sel(BLEZ));
  or or_1 (or_1_out, mips_alu_1_equal, ALU_Result[0]);
  // Probe on IF_PC[11:0]
  Counter #(.width(16), .max('hffff)) counter_2 (
    .count(JMP), .Q(\无条件分支数 ), .clk(CLK), .clr(RST));  // open: load, D, carry
  Counter #(.width(16), .max('hffff)) counter_3 (
    .count(Bi_Jiao), .Q(\条件分支成功数 ), .clk(CLK), .clr(RST));  // open: load, D, carry
  Multiplexer #(.width(5), .enable("false")) multiplexer_11 (
    .in0(WB_IR[20:16]), .in1(WB_IR[15:11]), .out(multiplexer_11_out), .sel(WB_RegDst));
  Multiplexer #(.width(32), .enable("false")) multiplexer_12 (
    .in0(WB_ALU_Result), .in1(WB_RAM_Out), .out(multiplexer_12_out), .sel(WB_MemToReg));
  or or_2 (Bi_Jiao, and_2_out, and_3_out, multiplexer_10_out);
  // Probe on ID_PC[11:0]
  Multiplexer #(.width(5), .enable("false")) multiplexer_13 (
    .in0(_25_0[20:16]), .in1(5'b00100), .out(multiplexer_13_out), .sel(\硬布线控制器_1_syscall ));
  Multiplexer #(.width(5), .enable("false")) multiplexer_14 (
    .in0(multiplexer_11_out), .in1({5{1'b1}}), .out(out_1), .sel(WB_JAL));
  Multiplexer #(.width(32), .enable("false")) multiplexer_15 (
    .in0(multiplexer_12_out), .in1(IF_PC), .out(multiplexer_15_out), .sel(WB_JAL));
  // Probe on MEM_PC[11:0]
  // Probe on EX_PC[11:0]
  Multiplexer #(.width(32), .enable("false")) multiplexer_16 (
    .in0({{16{1'b0}}, _16}), .in1({_16, {16{1'b0}}}), .out(multiplexer_16_out), .sel(MEM_ALU_Result[1]));
  // Probe on WB_PC[11:0]
  MIPS_Regifile mips_regifile_1 (
    .Din(multiplexer_15_out), .Clk(CLK), .R1(R1), .R2(R2), .WE(WB_RegWrite), .W_num(out_1),
    .R1_num(multiplexer_9_out), .R2_num(multiplexer_13_out));
  Multiplexer #(.width(32), .enable("false")) multiplexer_17 (
    .in0({MEM_R2, _16}), .in1(multiplexer_16_out), .out(multiplexer_17_out), .sel(MEM_SH));
  Multiplexer #(.width(4), .enable("false")) multiplexer_18 (
    .in0(4'b1111), .in1(multiplexer_19_out), .out(multiplexer_18_out), .sel(MEM_SH));
  Multiplexer #(.width(4), .enable("false")) multiplexer_19 (
    .in0(4'b0011), .in1(4'b1100), .out(multiplexer_19_out), .sel(MEM_ALU_Result[1]));
  // MIPS_RAM mips_ram_1: pin names not known; wires that end beside it: MEM_ALU_Result[21:2], multiplexer_17_out, MEM_MemWrite, multiplexer_18_out, CLK, RST, RAM_Out, WB_IR[31:26], WB_IR[5:0], WB_IR[25:21]
  \硬布线控制器  \u_硬布线控制器_1  (
    .Func(_0_15D[5:0]), .OP(ID_IR), .ALU_OP(\硬布线控制器_1_alu_op ), .MemToReg(\硬布线控制器_1_memtoreg ),
    .MemWrite(\硬布线控制器_1_memwrite ), .ALU_SRC(\硬布线控制器_1_alu_src ), .RegWrite(\硬布线控制器_1_regwrite ),
    .SysCALL(\硬布线控制器_1_syscall ), .SignedExt(\硬布线控制器_1_signedext ), .RegDst(\硬布线控制器_1_regdst ),
    .JR(\硬布线控制器_1_jr ), .JMP(\硬布线控制器_1_jmp ), .Beq(\硬布线控制器_1_beq ), .JAL(\硬布线控制器_1_jal ),
    .Bne(\硬布线控制器_1_bne ), .V(\硬布线控制器_1_v ), .SH(\硬布线控制器_1_sh ), .BLEZ(\硬布线控制器_1_blez ));
  EX_MEM ex_mem_1 (
    .IR({EX_IR, _0_15}), .SH(SH), .JR(JR), .PC(EX_PC), .JMP(JMP), .B(R22), .MenToReg(MemToReg),
    .MenWrite(MemWrite), .ALU(ALU_Result), .JAL(JAL), .IR_2(MEM_IR), .SH_2(MEM_SH), .JR_2(MEM_JR),
    .PC_2(MEM_PC), .JMP_2(MEM_JMP), .B_2({MEM_R2, _16}), .MenToReg_2(MEM_MemToReg),
    .MenWrite_2(MEM_MemWrite), .ALU_2(MEM_ALU_Result), .JAL_2(MEM_JAL), .RST(RST), .EN(EN), .CLK(CLK),
    .RegWrite(RegWrite), .RegWrite_2(MEM_RegWrite), .RegDst(RegDst), .RegDst_2(MEM_RegDst),
    .Syscall(Syscall), .Syscall_2(Mem_Syscall), .A(R11), .A_2(Mem_R1));
  ID_EX id_ex_1 (
    .IR({ID_IR, _25_0, _0_15D}), .BLEZ(\硬布线控制器_1_blez ), .SH(\硬布线控制器_1_sh ), .PC(ID_PC), .V(\硬布线控制器_1_v ),
    .SigedExt(\硬布线控制器_1_signedext ), .A(R1), .JR(\硬布线控制器_1_jr ), .JMP(\硬布线控制器_1_jmp ), .Beq(\硬布线控制器_1_beq ),
    .B(R2), .Bne(\硬布线控制器_1_bne ), .MenToReg(\硬布线控制器_1_memtoreg ), .Imm(Imm), .MenWrite(\硬布线控制器_1_memwrite ),
    .AluOP(\硬布线控制器_1_alu_op ), .AluSrcB(\硬布线控制器_1_alu_src ), .RegWrite(\硬布线控制器_1_regwrite ),
    .JAL(\硬布线控制器_1_jal ), .RegDst(\硬布线控制器_1_regdst ), .Syscall(\硬布线控制器_1_syscall ), .IR_2({EX_IR, _0_15}),
    .BLEZ_2(BLEZ), .SH_2(SH), .PC_2(EX_PC), .V_2(V), .SigedExt_2(SignedExt), .A_2(R11), .JR_2(JR),
    .JMP_2(JMP), .Beq_2(Beq), .B_2(R22), .Bne_2(Bne), .MenToReg_2(MemToReg), .Imm_2(Imm1),
    .MenWrite_2(MemWrite), .AluOP_2(AluOP), .AluSrcB_2(AluSrcB), .RegWrite_2(RegWrite), .JAL_2(JAL),
    .RegDst_2(RegDst), .Syscall_2(Syscall), .RST(RST), .EN(EN), .CLK(CLK));
  Comparator #(.width(32)) comparator_1 (.a(WB_R1), .b(32'h22), .eq(comparator_1_eq));  // open: gt, lt
  MEM_WB mem_wb_1 (
    .IR(MEM_IR), .SH(MEM_SH), .JR(MEM_JR), .PC(MEM_PC), .JMP(MEM_JMP), .MEMOUT(RAM_Out),
    .MenToReg(MEM_MemToReg), .ALU(MEM_ALU_Result), .JAL(MEM_JAL), .RegWrite(MEM_RegWrite),
    .RegDst(MEM_RegDst), .IR_2(WB_IR), .SH_2(WB_SH), .JR_2(WB_JR), .PC_2(WB_PC), .JMP_2(WB_JMP),
    .MEMOUT_2(WB_RAM_Out), .ALU_2(WB_ALU_Result), .JAL_2(WB_JAL), .RegWrite_2(WB_RegWrite),
    .RegDst_2(WB_RegDst), .RST(RST), .EN(EN), .CLK(CLK), .MenToReg_2(WB_MemToReg), .Syscall_2(WB_Syscall),
    .Syscall(Mem_Syscall), .A(Mem_R1), .A_2(WB_R1), .B({MEM_R2, _16}), .B_2(WB_R2));
  and and_4 (and_4_out, comparator_1_eq, WB_Syscall);
  Multiplexer #(.width(32)) multiplexer_20 (
    .in1(WB_R2), .out(multiplexer_20_out), .sel(and_4_out), .en(and_4_out));  // open: in0
  and and_5 (LOCK, ~comparator_1_eq, WB_Syscall);  // AND_Gate
  Register #(.width(32)) register_1 (.D(multiplexer_20_out), .Q(LedData), .clk(CLK), .clr(RST));  // open: en

  // Other names for the same wires on the sheet: EX_IR[15:0] = _0_15; shamt[4:0] = _0_15[10:6]; _25_0[15:0] = _0_15D;
  //   Func[5:0] = _0_15D[5:0]; ID_IR[25:0] = {_25_0, _0_15D}; rd[4:0] = _0_15D[15:11]; rt[4:0] = _25_0[20:16];
  //   rs[4:0] = _25_0[25:21]; OP[5:0] = ID_IR; 半字选择 = MEM_ALU_Result[1]; MEM_R2[15:0] = _16;
  //   WB_rd[4:0] = WB_IR[15:11]; WB_rt[4:0] = WB_IR[20:16]

  // Notes on the sheet:
  //   中断源
  //   中断等待指示
  //   指令存储器
  //   contents of rom_1 (hex, n*v repeats v):
  //   20100000 20110001 20120002 20130003 36100000 36310001 36520002 36730003 ae100000 ae110004 ae120008
  //   ae13000c 2002000a 0 0 0 c
  //   数码管输出
  //   OP
  //   rd
  //   Func
  //   rs
  //   rt
  //   流水调试日志用
  //   JMP
  //   JR
  //   OP
  //   Func
  //   OP
  //   Func
  //   rs
  //   rt
  //   rd
  //   Beq
  //   Bne
  //   MemToReg
  //   MemWrite
  //   AluOP
  //   AluSrcB
  //   RegWrite
  //   JAL
  //   RegDst
  //   Syscall
endmodule

// 源寄存器使用情况
module \源寄存器使用情况  (
  input  OP0,
  input  OP1,
  input  OP2,
  input  OP3,
  input  OP4,
  input  OP5,
  input  F0,
  input  F1,
  input  F2,
  input  F3,
  input  F4,
  input  F5,
  output R1_Used,
  output R2_Used
);

  wire and_1_out, and_2_out, and_3_out, and_4_out, and_5_out, and_6_out, and_7_out, and_8_out, and_9_out,
       and_10_out, and_11_out, and_12_out, and_13_out, and_14_out, and_15_out, and_16_out, and_17_out,
       and_18_out, and_19_out, and_20_out, and_21_out, and_22_out, and_23_out, and_24_out, and_25_out,
       and_26_out, and_27_out, and_28_out, and_29_out, and_30_out, and_31_out, and_32_out, and_33_out,
       and_34_out, and_35_out, and_36_out, and_37_out, and_38_out, and_39_out, and_40_out, and_41_out,
       and_42_out, and_43_out, and_44_out, not_1_out, not_2_out, not_3_out, not_4_out, not_5_out, not_6_out,
       not_7_out, not_8_out, not_9_out, not_10_out, not_11_out, not_12_out, not_13_out, not_14_out,
       not_15_out, not_16_out, not_17_out, not_18_out, not_19_out, not_20_out, not_21_out, not_22_out,
       not_23_out, not_24_out, not_25_out, not_26_out, not_27_out, not_28_out, not_29_out, not_30_out,
       not_31_out, not_32_out, not_33_out, not_34_out, not_35_out, not_36_out, not_37_out, not_38_out,
       not_39_out, not_40_out, not_41_out, not_42_out, not_43_out, not_44_out, not_45_out, not_46_out,
       not_47_out, not_48_out, not_49_out, not_50_out, not_51_out, not_52_out, not_53_out, not_54_out,
       not_55_out, not_56_out, not_57_out, not_58_out, not_59_out, not_60_out, not_61_out, not_62_out,
       not_63_out, not_64_out, not_65_out, not_66_out, not_67_out, not_68_out, not_69_out, not_70_out,
       not_71_out, not_72_out, not_73_out, not_74_out, not_75_out, not_76_out, not_77_out, not_78_out,
       not_79_out, not_80_out, not_81_out, not_82_out, not_83_out, not_84_out, not_85_out, not_86_out,
       not_87_out, not_88_out, not_89_out, not_90_out, not_91_out, not_92_out, not_93_out, not_94_out,
       not_95_out, not_96_out, not_97_out, not_98_out, not_99_out, not_100_out, not_101_out, not_102_out,
       not_103_out, not_104_out, not_105_out, not_106_out, not_107_out, not_108_out, not_109_out,
       not_110_out, not_111_out, not_112_out, not_113_out, not_114_out, not_115_out, not_116_out,
       not_117_out, not_118_out, not_119_out, not_120_out, not_121_out, not_122_out, not_123_out,
       not_124_out, not_125_out, not_126_out, not_127_out, not_128_out, not_129_out, not_130_out,
       not_131_out, not_132_out, not_133_out, not_134_out, not_135_out, not_136_out, not_137_out,
       not_138_out, not_139_out, not_140_out, not_141_out, not_142_out, not_143_out, not_144_out,
       not_145_out, not_146_out, not_147_out, not_148_out, not_149_out, not_150_out, not_151_out,
       not_152_out, not_153_out, not_154_out, not_155_out, not_156_out, not_157_out, not_158_out,
       not_159_out, not_160_out, not_161_out, not_162_out, not_163_out, not_164_out, not_165_out,
       not_166_out, not_167_out, not_168_out, not_169_out, not_170_out, not_171_out, not_172_out,
       not_173_out, not_174_out, not_175_out, not_176_out, not_177_out, not_178_out, not_179_out,
       not_180_out, not_181_out, not_182_out, not_183_out, not_184_out, not_185_out, not_186_out,
       not_187_out, not_188_out, not_189_out, not_190_out, not_191_out, not_192_out, not_193_out,
       not_194_out, not_195_out, not_196_out, not_197_out, not_198_out, not_199_out, not_200_out,
       not_201_out, not_202_out, not_203_out, not_204_out, not_205_out, not_206_out, not_207_out,
       not_208_out, not_209_out, not_210_out, not_211_out, not_212_out, not_213_out, not_214_out,
       not_215_out, not_216_out, not_217_out, not_218_out, not_219_out, not_220_out, not_221_out,
       not_222_out, not_223_out, not_224_out, not_225_out, not_226_out, not_227_out, not_228_out,
       not_229_out, not_230_out, not_231_out, not_232_out, not_233_out, not_234_out, not_235_out,
       not_236_out, not_237_out, not_238_out, not_239_out, not_240_out, not_241_out, not_242_out,
       not_243_out, not_244_out, not_245_out, not_246_out, not_247_out, not_248_out, not_249_out,
       not_250_out, not_251_out, not_252_out, not_253_out, not_254_out, not_255_out, not_256_out,
       not_257_out, not_258_out, not_259_out, not_260_out, not_261_out, not_262_out, not_263_out,
       not_264_out, not_265_out, not_266_out, not_267_out, not_268_out, not_269_out, not_270_out,
       not_271_out, not_272_out, not_273_out, not_274_out, not_275_out, not_276_out, not_277_out,
       not_278_out, not_279_out, not_280_out, not_281_out, not_282_out, not_283_out, not_284_out,
       not_285_out, not_286_out, not_287_out, not_288_out, not_289_out, not_290_out, not_291_out,
       not_292_out, not_293_out, not_294_out, not_295_out, not_296_out, not_297_out, not_298_out,
       not_299_out, not_300_out, not_301_out, not_302_out, not_303_out, not_304_out, not_305_out,
       not_306_out, not_307_out, not_308_out, not_309_out, not_310_out, not_311_out, not_312_out,
       not_313_out, not_314_out, not_315_out, not_316_out, not_317_out, not_318_out, not_319_out,
       not_320_out, not_321_out, not_322_out, not_323_out, not_324_out, not_325_out, not_326_out,
       not_327_out, not_328_out, not_329_out, not_330_out, not_331_out, not_332_out, not_333_out,
       not_334_out, not_335_out, not_336_out, not_337_out, not_338_out, not_339_out, not_340_out,
       not_341_out, not_342_out;

  not not_1 (not_1_out, OP5);
  not not_2 (not_2_out, OP4);
  not not_3 (not_3_out, OP3);
  not not_4 (not_4_out, OP2);
  not not_5 (not_5_out, OP1);
  not not_6 (not_6_out, OP0);
  not not_7 (not_7_out, F5);
  not not_8 (not_8_out, F4);
  not not_9 (not_9_out, F3);
  not not_10 (not_10_out, F2);
  not not_11 (not_11_out, F1);
  not not_12 (not_12_out, F0);
  not not_13 (not_13_out, OP5);
  not not_14 (not_14_out, OP4);
  not not_15 (not_15_out, OP3);
  not not_16 (not_16_out, OP2);
  not not_17 (not_17_out, OP1);
  not not_18 (not_18_out, OP0);
  not not_19 (not_19_out, F5);
  not not_20 (not_20_out, F4);
  not not_21 (not_21_out, F3);
  not not_22 (not_22_out, F2);
  not not_23 (not_23_out, OP5);
  not not_24 (not_24_out, OP4);
  not not_25 (not_25_out, OP3);
  not not_26 (not_26_out, OP2);
  not not_27 (not_27_out, OP1);
  not not_28 (not_28_out, OP0);
  not not_29 (not_29_out, F5);
  not not_30 (not_30_out, F4);
  not not_31 (not_31_out, F3);
  not not_32 (not_32_out, F2);
  not not_33 (not_33_out, F0);
  not not_34 (not_34_out, OP5);
  not not_35 (not_35_out, OP4);
  not not_36 (not_36_out, OP3);
  not not_37 (not_37_out, OP2);
  not not_38 (not_38_out, OP1);
  not not_39 (not_39_out, OP0);
  not not_40 (not_40_out, F4);
  not not_41 (not_41_out, F3);
  not not_42 (not_42_out, F2);
  not not_43 (not_43_out, F1);
  not not_44 (not_44_out, F0);
  not not_45 (not_45_out, OP5);
  not not_46 (not_46_out, OP4);
  not not_47 (not_47_out, OP3);
  not not_48 (not_48_out, OP2);
  not not_49 (not_49_out, OP1);
  not not_50 (not_50_out, OP0);
  not not_51 (not_51_out, F4);
  not not_52 (not_52_out, F3);
  not not_53 (not_53_out, F2);
  not not_54 (not_54_out, F1);
  not not_55 (not_55_out, OP5);
  not not_56 (not_56_out, OP4);
  not not_57 (not_57_out, OP3);
  not not_58 (not_58_out, OP2);
  not not_59 (not_59_out, OP1);
  not not_60 (not_60_out, OP0);
  not not_61 (not_61_out, F4);
  not not_62 (not_62_out, F3);
  not not_63 (not_63_out, F2);
  not not_64 (not_64_out, F0);
  not not_65 (not_65_out, OP5);
  not not_66 (not_66_out, OP4);
  not not_67 (not_67_out, OP3);
  not not_68 (not_68_out, OP2);
  not not_69 (not_69_out, OP1);
  not not_70 (not_70_out, OP0);
  not not_71 (not_71_out, F4);
  not not_72 (not_72_out, F3);
  not not_73 (not_73_out, F1);
  not not_74 (not_74_out, F0);
  not not_75 (not_75_out, OP5);
  not not_76 (not_76_out, OP4);
  not not_77 (not_77_out, OP3);
  not not_78 (not_78_out, OP2);
  not not_79 (not_79_out, OP1);
  not not_80 (not_80_out, OP0);
  not not_81 (not_81_out, F4);
  not not_82 (not_82_out, F3);
  not not_83 (not_83_out, F1);
  not not_84 (not_84_out, OP5);
  not not_85 (not_85_out, OP4);
  not not_86 (not_86_out, OP3);
  not not_87 (not_87_out, OP2);
  not not_88 (not_88_out, OP1);
  not not_89 (not_89_out, OP0);
  not not_90 (not_90_out, F4);
  not not_91 (not_91_out, F3);
  not not_92 (not_92_out, OP5);
  not not_93 (not_93_out, OP4);
  not not_94 (not_94_out, OP3);
  not not_95 (not_95_out, OP2);
  not not_96 (not_96_out, OP1);
  not not_97 (not_97_out, OP0);
  not not_98 (not_98_out, F4);
  not not_99 (not_99_out, F2);
  not not_100 (not_100_out, F0);
  not not_101 (not_101_out, OP5);
  not not_102 (not_102_out, OP4);
  not not_103 (not_103_out, OP3);
  not not_104 (not_104_out, OP2);
  not not_105 (not_105_out, OP1);
  not not_106 (not_106_out, OP0);
  not not_107 (not_107_out, F4);
  not not_108 (not_108_out, F2);
  not not_109 (not_109_out, OP5);
  not not_110 (not_110_out, OP4);
  not not_111 (not_111_out, OP3);
  not not_112 (not_112_out, OP2);
  not not_113 (not_113_out, OP1);
  not not_114 (not_114_out, OP0);
  not not_115 (not_115_out, F5);
  not not_116 (not_116_out, F4);
  not not_117 (not_117_out, F2);
  not not_118 (not_118_out, F1);
  not not_119 (not_119_out, F0);
  not not_120 (not_120_out, OP5);
  not not_121 (not_121_out, OP4);
  not not_122 (not_122_out, OP3);
  not not_123 (not_123_out, OP2);
  not not_124 (not_124_out, OP1);
  not not_125 (not_125_out, OP0);
  not not_126 (not_126_out, F5);
  not not_127 (not_127_out, F4);
  not not_128 (not_128_out, F1);
  not not_129 (not_129_out, F0);
  not not_130 (not_130_out, OP5);
  not not_131 (not_131_out, OP4);
  not not_132 (not_132_out, OP3);
  not not_133 (not_133_out, OP1);
  not not_134 (not_134_out, OP0);
  not not_135 (not_135_out, OP5);
  not not_136 (not_136_out, OP4);
  not not_137 (not_137_out, OP3);
  not not_138 (not_138_out, OP1);
  not not_139 (not_139_out, OP5);
  not not_140 (not_140_out, OP4);
  not not_141 (not_141_out, OP2);
  not not_142 (not_142_out, OP1);
  not not_143 (not_143_out, OP0);
  not not_144 (not_144_out, OP5);
  not not_145 (not_145_out, OP4);
  not not_146 (not_146_out, OP1);
  not not_147 (not_147_out, OP0);
  not not_148 (not_148_out, OP5);
  not not_149 (not_149_out, OP4);
  not not_150 (not_150_out, OP2);
  not not_151 (not_151_out, OP1);
  not not_152 (not_152_out, OP5);
  not not_153 (not_153_out, OP4);
  not not_154 (not_154_out, OP2);
  not not_155 (not_155_out, OP0);
  not not_156 (not_156_out, OP5);
  not not_157 (not_157_out, OP4);
  not not_158 (not_158_out, OP1);
  not not_159 (not_159_out, OP4);
  not not_160 (not_160_out, OP3);
  not not_161 (not_161_out, OP2);
  not not_162 (not_162_out, OP4);
  not not_163 (not_163_out, OP2);
  not not_164 (not_164_out, OP5);
  not not_165 (not_165_out, OP4);
  not not_166 (not_166_out, OP3);
  not not_167 (not_167_out, OP2);
  not not_168 (not_168_out, OP1);
  not not_169 (not_169_out, OP0);
  not not_170 (not_170_out, F5);
  not not_171 (not_171_out, F4);
  not not_172 (not_172_out, F3);
  not not_173 (not_173_out, F1);
  not not_174 (not_174_out, F0);
  not not_175 (not_175_out, OP5);
  not not_176 (not_176_out, OP4);
  not not_177 (not_177_out, OP3);
  not not_178 (not_178_out, OP2);
  not not_179 (not_179_out, OP1);
  not not_180 (not_180_out, OP0);
  not not_181 (not_181_out, F5);
  not not_182 (not_182_out, F4);
  not not_183 (not_183_out, F3);
  not not_184 (not_184_out, OP4);
  not not_185 (not_185_out, OP2);
  not not_186 (not_186_out, OP1);
  not not_187 (not_187_out, OP5);
  not not_188 (not_188_out, OP4);
  not not_189 (not_189_out, OP3);
  not not_190 (not_190_out, OP0);
  not not_191 (not_191_out, OP5);
  not not_192 (not_192_out, OP4);
  not not_193 (not_193_out, OP3);
  not not_194 (not_194_out, OP2);
  not not_195 (not_195_out, OP1);
  not not_196 (not_196_out, OP0);
  not not_197 (not_197_out, F5);
  not not_198 (not_198_out, F4);
  not not_199 (not_199_out, F3);
  not not_200 (not_200_out, F2);
  not not_201 (not_201_out, F1);
  not not_202 (not_202_out, F0);
  not not_203 (not_203_out, OP5);
  not not_204 (not_204_out, OP4);
  not not_205 (not_205_out, OP3);
  not not_206 (not_206_out, OP2);
  not not_207 (not_207_out, OP1);
  not not_208 (not_208_out, OP0);
  not not_209 (not_209_out, F5);
  not not_210 (not_210_out, F4);
  not not_211 (not_211_out, F3);
  not not_212 (not_212_out, F2);
  not not_213 (not_213_out, OP5);
  not not_214 (not_214_out, OP4);
  not not_215 (not_215_out, OP3);
  not not_216 (not_216_out, OP2);
  not not_217 (not_217_out, OP1);
  not not_218 (not_218_out, OP0);
  not not_219 (not_219_out, F5);
  not not_220 (not_220_out, F4);
  not not_221 (not_221_out, F3);
  not not_222 (not_222_out, F2);
  not not_223 (not_223_out, F0);
  not not_224 (not_224_out, OP5);
  not not_225 (not_225_out, OP4);
  not not_226 (not_226_out, OP3);
  not not_227 (not_227_out, OP2);
  not not_228 (not_228_out, OP1);
  not not_229 (not_229_out, OP0);
  not not_230 (not_230_out, F4);
  not not_231 (not_231_out, F3);
  not not_232 (not_232_out, F2);
  not not_233 (not_233_out, F1);
  not not_234 (not_234_out, F0);
  not not_235 (not_235_out, OP5);
  not not_236 (not_236_out, OP4);
  not not_237 (not_237_out, OP3);
  not not_238 (not_238_out, OP2);
  not not_239 (not_239_out, OP1);
  not not_240 (not_240_out, OP0);
  not not_241 (not_241_out, F4);
  not not_242 (not_242_out, F3);
  not not_243 (not_243_out, F2);
  not not_244 (not_244_out, F1);
  not not_245 (not_245_out, OP5);
  not not_246 (not_246_out, OP4);
  not not_247 (not_247_out, OP3);
  not not_248 (not_248_out, OP2);
  not not_249 (not_249_out, OP1);
  not not_250 (not_250_out, OP0);
  not not_251 (not_251_out, F4);
  not not_252 (not_252_out, F3);
  not not_253 (not_253_out, F2);
  not not_254 (not_254_out, F0);
  not not_255 (not_255_out, OP5);
  not not_256 (not_256_out, OP4);
  not not_257 (not_257_out, OP3);
  not not_258 (not_258_out, OP2);
  not not_259 (not_259_out, OP1);
  not not_260 (not_260_out, OP0);
  not not_261 (not_261_out, F4);
  not not_262 (not_262_out, F3);
  not not_263 (not_263_out, F1);
  not not_264 (not_264_out, F0);
  not not_265 (not_265_out, OP5);
  not not_266 (not_266_out, OP4);
  not not_267 (not_267_out, OP3);
  not not_268 (not_268_out, OP2);
  not not_269 (not_269_out, OP1);
  not not_270 (not_270_out, OP0);
  not not_271 (not_271_out, F4);
  not not_272 (not_272_out, F3);
  not not_273 (not_273_out, F1);
  not not_274 (not_274_out, OP5);
  not not_275 (not_275_out, OP4);
  not not_276 (not_276_out, OP3);
  not not_277 (not_277_out, OP2);
  not not_278 (not_278_out, OP1);
  not not_279 (not_279_out, OP0);
  not not_280 (not_280_out, F4);
  not not_281 (not_281_out, F3);
  not not_282 (not_282_out, OP5);
  not not_283 (not_283_out, OP4);
  not not_284 (not_284_out, OP3);
  not not_285 (not_285_out, OP2);
  not not_286 (not_286_out, OP1);
  not not_287 (not_287_out, OP0);
  not not_288 (not_288_out, F4);
  not not_289 (not_289_out, F2);
  not not_290 (not_290_out, F0);
  not not_291 (not_291_out, OP5);
  not not_292 (not_292_out, OP4);
  not not_293 (not_293_out, OP3);
  not not_294 (not_294_out, OP2);
  not not_295 (not_295_out, OP1);
  not not_296 (not_296_out, OP0);
  not not_297 (not_297_out, F4);
  not not_298 (not_298_out, F2);
  not not_299 (not_299_out, OP5);
  not not_300 (not_300_out, OP4);
  not not_301 (not_301_out, OP3);
  not not_302 (not_302_out, OP2);
  not not_303 (not_303_out, OP1);
  not not_304 (not_304_out, OP0);
  not not_305 (not_305_out, F5);
  not not_306 (not_306_out, F4);
  not not_307 (not_307_out, F1);
  not not_308 (not_308_out, F0);
  not not_309 (not_309_out, OP5);
  not not_310 (not_310_out, OP4);
  not not_311 (not_311_out, OP3);
  not not_312 (not_312_out, OP1);
  not not_313 (not_313_out, OP0);
  not not_314 (not_314_out, OP5);
  not not_315 (not_315_out, OP4);
  not not_316 (not_316_out, OP3);
  not not_317 (not_317_out, OP1);
  not not_318 (not_318_out, OP4);
  not not_319 (not_319_out, OP2);
  not not_320 (not_320_out, OP5);
  not not_321 (not_321_out, OP4);
  not not_322 (not_322_out, OP3);
  not not_323 (not_323_out, OP2);
  not not_324 (not_324_out, OP1);
  not not_325 (not_325_out, OP0);
  not not_326 (not_326_out, F5);
  not not_327 (not_327_out, F4);
  not not_328 (not_328_out, F3);
  not not_329 (not_329_out, F1);
  not not_330 (not_330_out, F0);
  not not_331 (not_331_out, OP5);
  not not_332 (not_332_out, OP4);
  not not_333 (not_333_out, OP3);
  not not_334 (not_334_out, OP2);
  not not_335 (not_335_out, OP1);
  not not_336 (not_336_out, OP0);
  not not_337 (not_337_out, F5);
  not not_338 (not_338_out, F4);
  not not_339 (not_339_out, F3);
  not not_340 (not_340_out, OP4);
  not not_341 (not_341_out, OP2);
  not not_342 (not_342_out, OP1);
  and and_1 (and_1_out, not_1_out, not_2_out, not_3_out, not_4_out, not_5_out, not_6_out, not_7_out, not_8_out, not_9_out, not_10_out, not_11_out, not_12_out);
  and and_2 (and_2_out, not_13_out, not_14_out, not_15_out, not_16_out, not_17_out, not_18_out, not_19_out, not_20_out, not_21_out, not_22_out, F1, F0);
  and and_3 (and_3_out, not_23_out, not_24_out, not_25_out, not_26_out, not_27_out, not_28_out, not_29_out, not_30_out, not_31_out, not_32_out, F1, not_33_out);
  and and_4 (and_4_out, not_34_out, not_35_out, not_36_out, not_37_out, not_38_out, not_39_out, F5, not_40_out, not_41_out, not_42_out, not_43_out, not_44_out);
  and and_5 (and_5_out, not_45_out, not_46_out, not_47_out, not_48_out, not_49_out, not_50_out, F5, not_51_out, not_52_out, not_53_out, not_54_out, F0);
  and and_6 (and_6_out, not_55_out, not_56_out, not_57_out, not_58_out, not_59_out, not_60_out, F5, not_61_out, not_62_out, not_63_out, F1, not_64_out);
  and and_7 (and_7_out, not_65_out, not_66_out, not_67_out, not_68_out, not_69_out, not_70_out, F5, not_71_out, not_72_out, F2, not_73_out, not_74_out);
  and and_8 (and_8_out, not_75_out, not_76_out, not_77_out, not_78_out, not_79_out, not_80_out, F5, not_81_out, not_82_out, F2, not_83_out, F0);
  and and_9 (and_9_out, not_84_out, not_85_out, not_86_out, not_87_out, not_88_out, not_89_out, F5, not_90_out, not_91_out, F2, F1, F0);
  and and_10 (and_10_out, not_92_out, not_93_out, not_94_out, not_95_out, not_96_out, not_97_out, F5, not_98_out, F3, not_99_out, F1, not_100_out);
  and and_11 (and_11_out, not_101_out, not_102_out, not_103_out, not_104_out, not_105_out, not_106_out, F5, not_107_out, F3, not_108_out, F1, F0);
  and and_12 (and_12_out, not_109_out, not_110_out, not_111_out, not_112_out, not_113_out, not_114_out, not_115_out, not_116_out, F3, not_117_out, not_118_out, not_119_out);
  and and_13 (and_13_out, not_120_out, not_121_out, not_122_out, not_123_out, not_124_out, not_125_out, not_126_out, not_127_out, F3, F2, not_128_out, not_129_out);
  and and_14 (and_14_out, not_130_out, not_131_out, not_132_out, OP2, not_133_out, not_134_out);
  and and_15 (and_15_out, not_135_out, not_136_out, not_137_out, OP2, not_138_out, OP0);
  and and_16 (and_16_out, not_139_out, not_140_out, OP3, not_141_out, not_142_out, not_143_out);
  and and_17 (and_17_out, not_144_out, not_145_out, OP3, OP2, not_146_out, not_147_out);
  and and_18 (and_18_out, not_148_out, not_149_out, OP3, not_150_out, not_151_out, OP0);
  and and_19 (and_19_out, not_152_out, not_153_out, OP3, not_154_out, OP1, not_155_out);
  and and_20 (and_20_out, not_156_out, not_157_out, OP3, OP2, not_158_out, OP0);
  and and_21 (and_21_out, OP5, not_159_out, not_160_out, not_161_out, OP1, OP0);
  and and_22 (and_22_out, OP5, not_162_out, OP3, not_163_out, OP1, OP0);
  and and_23 (and_23_out, not_164_out, not_165_out, not_166_out, not_167_out, not_168_out, not_169_out, not_170_out, not_171_out, not_172_out, F2, not_173_out, not_174_out);
  and and_24 (and_24_out, not_175_out, not_176_out, not_177_out, not_178_out, not_179_out, not_180_out, not_181_out, not_182_out, not_183_out, F2, F1, F0);
  and and_25 (and_25_out, OP5, not_184_out, OP3, not_185_out, not_186_out, OP0);
  and and_26 (and_26_out, not_187_out, not_188_out, not_189_out, OP2, OP1, not_190_out);
  and and_27 (and_27_out, not_191_out, not_192_out, not_193_out, not_194_out, not_195_out, not_196_out, not_197_out, not_198_out, not_199_out, not_200_out, not_201_out, not_202_out);
  and and_28 (and_28_out, not_203_out, not_204_out, not_205_out, not_206_out, not_207_out, not_208_out, not_209_out, not_210_out, not_211_out, not_212_out, F1, F0);
  and and_29 (and_29_out, not_213_out, not_214_out, not_215_out, not_216_out, not_217_out, not_218_out, not_219_out, not_220_out, not_221_out, not_222_out, F1, not_223_out);
  and and_30 (and_30_out, not_224_out, not_225_out, not_226_out, not_227_out, not_228_out, not_229_out, F5, not_230_out, not_231_out, not_232_out, not_233_out, not_234_out);
  and and_31 (and_31_out, not_235_out, not_236_out, not_237_out, not_238_out, not_239_out, not_240_out, F5, not_241_out, not_242_out, not_243_out, not_244_out, F0);
  and and_32 (and_32_out, not_245_out, not_246_out, not_247_out, not_248_out, not_249_out, not_250_out, F5, not_251_out, not_252_out, not_253_out, F1, not_254_out);
  and and_33 (and_33_out, not_255_out, not_256_out, not_257_out, not_258_out, not_259_out, not_260_out, F5, not_261_out, not_262_out, F2, not_263_out, not_264_out);
  and and_34 (and_34_out, not_265_out, not_266_out, not_267_out, not_268_out, not_269_out, not_270_out, F5, not_271_out, not_272_out, F2, not_273_out, F0);
  and and_35 (and_35_out, not_274_out, not_275_out, not_276_out, not_277_out, not_278_out, not_279_out, F5, not_280_out, not_281_out, F2, F1, F0);
  and and_36 (and_36_out, not_282_out, not_283_out, not_284_out, not_285_out, not_286_out, not_287_out, F5, not_288_out, F3, not_289_out, F1, not_290_out);
  and and_37 (and_37_out, not_291_out, not_292_out, not_293_out, not_294_out, not_295_out, not_296_out, F5, not_297_out, F3, not_298_out, F1, F0);
  and and_38 (and_38_out, not_299_out, not_300_out, not_301_out, not_302_out, not_303_out, not_304_out, not_305_out, not_306_out, F3, F2, not_307_out, not_308_out);
  and and_39 (and_39_out, not_309_out, not_310_out, not_311_out, OP2, not_312_out, not_313_out);
  and and_40 (and_40_out, not_314_out, not_315_out, not_316_out, OP2, not_317_out, OP0);
  and and_41 (and_41_out, OP5, not_318_out, OP3, not_319_out, OP1, OP0);
  and and_42 (and_42_out, not_320_out, not_321_out, not_322_out, not_323_out, not_324_out, not_325_out, not_326_out, not_327_out, not_328_out, F2, not_329_out, not_330_out);
  and and_43 (and_43_out, not_331_out, not_332_out, not_333_out, not_334_out, not_335_out, not_336_out, not_337_out, not_338_out, not_339_out, F2, F1, F0);
  and and_44 (and_44_out, OP5, not_340_out, OP3, not_341_out, not_342_out, OP0);
  or or_1 (R1_Used, and_1_out, and_2_out, and_3_out, and_4_out, and_5_out, and_6_out, and_7_out, and_8_out, and_9_out, and_10_out, and_11_out, and_12_out, and_13_out, and_14_out, and_15_out, and_16_out, and_17_out, and_18_out, and_19_out, and_20_out, and_21_out, and_22_out, and_23_out, and_24_out, and_25_out, and_26_out);
  or or_2 (R2_Used, and_27_out, and_28_out, and_29_out, and_30_out, and_31_out, and_32_out, and_33_out, and_34_out, and_35_out, and_36_out, and_37_out, and_38_out, and_39_out, and_40_out, and_41_out, and_42_out, and_43_out, and_44_out);
endmodule

module \数据相关检测  (
  input  [5:0] OP,
  input  [4:0] EX_WriteReg_num,
  input  EX_RegWrite,
  input  [4:0] MEM_WriteReg_num,
  input  MEM_RegWrite,
  input  [5:0] Func,
  input  [4:0] ID_R1_num,
  input  [4:0] ID_R2_num,
  output \数据相关 
);

  wire and_1_out, and_2_out, and_3_out, and_4_out, and_5_out, and_6_out, comparator_1_eq, comparator_2_eq,
       comparator_3_eq, comparator_4_eq, comparator_5_eq, comparator_6_eq, not_1_out, not_2_out, or_1_out,
       or_2_out, R1_Used, R2_Used;

  \源寄存器使用情况  \u_源寄存器使用情况_1  (
    .OP0(OP[0]), .OP1(OP[1]), .OP2(OP[2]), .OP3(OP[3]), .OP4(OP[4]), .OP5(OP[5]), .F0(Func[0]), .F1(Func[1]),
    .F2(Func[2]), .F3(Func[3]), .F4(Func[4]), .F5(Func[5]), .R1_Used(R1_Used), .R2_Used(R2_Used));
  Comparator #(.width(5)) comparator_1 (.a(ID_R1_num), .b(EX_WriteReg_num), .eq(comparator_1_eq));  // open: gt, lt
  Comparator #(.width(5)) comparator_2 (.a(ID_R2_num), .b(EX_WriteReg_num), .eq(comparator_2_eq));  // open: gt, lt
  Comparator #(.width(5)) comparator_3 (.a(ID_R1_num), .b(MEM_WriteReg_num), .eq(comparator_3_eq));  // open: gt, lt
  Comparator #(.width(5)) comparator_4 (.a(ID_R2_num), .b(MEM_WriteReg_num), .eq(comparator_4_eq));  // open: gt, lt
  and and_1 (and_1_out, R1_Used, comparator_1_eq);
  and and_2 (and_2_out, comparator_2_eq, R2_Used);
  and and_3 (and_3_out, R1_Used, comparator_3_eq);
  and and_4 (and_4_out, comparator_4_eq, R2_Used);
  or or_1 (or_1_out, and_1_out, and_2_out);
  not not_1 (not_1_out, comparator_5_eq);
  Comparator #(.width(5)) comparator_5 (.a(EX_WriteReg_num), .b({5{1'b0}}), .eq(comparator_5_eq));  // open: gt, lt
  or or_2 (or_2_out, and_3_out, and_4_out);
  not not_2 (not_2_out, comparator_6_eq);
  Comparator #(.width(5)) comparator_6 (.a(MEM_WriteReg_num), .b({5{1'b0}}), .eq(comparator_6_eq));  // open: gt, lt
  and and_5 (and_5_out, or_1_out, EX_RegWrite, not_1_out);
  and and_6 (and_6_out, or_2_out, MEM_RegWrite, not_2_out);
  or or_3 (\数据相关 , and_5_out, and_6_out);

  // Other names for the same wires on the sheet: OP_CODE[5:0] = OP
endmodule

module IF_ID (
  input  [31:0] IR,
  input  [31:0] PC,
  input  RST,
  input  EN,
  input  CLK,
  output [31:0] IR_2,
  output [31:0] PC_2
);

  wire [31:0] multiplexer_1_out, multiplexer_2_out;

  Multiplexer #(.width(32), .enable("false")) multiplexer_1 (
    .in0(IR), .in1({32{1'b0}}), .out(multiplexer_1_out), .sel(RST));
  Multiplexer #(.width(32), .enable("false")) multiplexer_2 (
    .in0(PC), .in1({32{1'b0}}), .out(multiplexer_2_out), .sel(RST));
  Register #(.width(32)) u_IR (.D(multiplexer_1_out), .en(EN), .Q(IR_2), .clk(CLK));  // open: clr
  Register #(.width(32)) u_PC (.D(multiplexer_2_out), .en(EN), .Q(PC_2), .clk(CLK));  // open: clr
endmodule
module ID_EX (
  input  [31:0] IR,
  input  BLEZ,
  input  SH,
  input  [31:0] PC,
  input  V,
  input  SigedExt,
  input  [31:0] A,
  input  JR,
  input  JMP,
  input  Beq,
  input  [31:0] B,
  input  Bne,
  input  MenToReg,
  input  [31:0] Imm,
  input  MenWrite,
  input  [3:0] AluOP,
  input  AluSrcB,
  input  RegWrite,
  input  JAL,
  input  RegDst,
  input  Syscall,
  input  RST,
  input  EN,
  input  CLK,
  output [31:0] IR_2,
  output BLEZ_2,
  output SH_2,
  output [31:0] PC_2,
  output V_2,
  output SigedExt_2,
  output [31:0] A_2,
  output JR_2,
  output JMP_2,
  output Beq_2,
  output [31:0] B_2,
  output Bne_2,
  output MenToReg_2,
  output [31:0] Imm_2,
  output MenWrite_2,
  output [3:0] AluOP_2,
  output AluSrcB_2,
  output RegWrite_2,
  output JAL_2,
  output RegDst_2,
  output Syscall_2
);

  wire multiplexer_6_out, multiplexer_7_out, multiplexer_8_out, multiplexer_9_out, multiplexer_10_out,
       multiplexer_11_out, multiplexer_12_out, multiplexer_13_out, multiplexer_14_out, multiplexer_15_out,
       multiplexer_17_out, multiplexer_18_out, multiplexer_19_out, multiplexer_20_out, multiplexer_21_out;
  wire [3:0] multiplexer_16_out;
  wire [31:0] multiplexer_1_out, multiplexer_2_out, multiplexer_3_out, multiplexer_4_out, multiplexer_5_out;

  Multiplexer #(.width(32), .enable("false")) multiplexer_1 (
    .in0(IR), .in1({32{1'b0}}), .out(multiplexer_1_out), .sel(RST));
  Multiplexer #(.width(32), .enable("false")) multiplexer_2 (
    .in0(PC), .in1({32{1'b0}}), .out(multiplexer_2_out), .sel(RST));
  Multiplexer #(.width(32), .enable("false")) multiplexer_3 (
    .in0(A), .in1({32{1'b0}}), .out(multiplexer_3_out), .sel(RST));
  Multiplexer #(.width(32), .enable("false")) multiplexer_4 (
    .in0(B), .in1({32{1'b0}}), .out(multiplexer_4_out), .sel(RST));
  Multiplexer #(.width(32), .enable("false")) multiplexer_5 (
    .in0(Imm), .in1({32{1'b0}}), .out(multiplexer_5_out), .sel(RST));
  Register #(.width(32)) u_IR (.D(multiplexer_1_out), .en(EN), .Q(IR_2), .clk(CLK));  // open: clr
  Register #(.width(32)) u_PC (.D(multiplexer_2_out), .en(EN), .Q(PC_2), .clk(CLK));  // open: clr
  Register #(.width(32)) u_A (.D(multiplexer_3_out), .en(EN), .Q(A_2), .clk(CLK));  // open: clr
  Register #(.width(32)) u_B (.D(multiplexer_4_out), .en(EN), .Q(B_2), .clk(CLK));  // open: clr
  Register #(.width(32)) u_Imm (.D(multiplexer_5_out), .en(EN), .Q(Imm_2), .clk(CLK));  // open: clr
  Multiplexer #(.enable("false")) multiplexer_6 (.in0(BLEZ), .in1(1'b0), .out(multiplexer_6_out), .sel(RST));
  Multiplexer #(.enable("false")) multiplexer_7 (.in0(SH), .in1(1'b0), .out(multiplexer_7_out), .sel(RST));
  Multiplexer #(.enable("false")) multiplexer_8 (.in0(V), .in1(1'b0), .out(multiplexer_8_out), .sel(RST));
  Multiplexer #(.enable("false")) multiplexer_9 (.in0(SigedExt), .in1(1'b0), .out(multiplexer_9_out), .sel(RST));
  Multiplexer #(.enable("false")) multiplexer_10 (.in0(JR), .in1(1'b0), .out(multiplexer_10_out), .sel(RST));
  Multiplexer #(.enable("false")) multiplexer_11 (.in0(JMP), .in1(1'b0), .out(multiplexer_11_out), .sel(RST));
  Multiplexer #(.enable("false")) multiplexer_12 (.in0(Beq), .in1(1'b0), .out(multiplexer_12_out), .sel(RST));
  Multiplexer #(.enable("false")) multiplexer_13 (.in0(Bne), .in1(1'b0), .out(multiplexer_13_out), .sel(RST));
  Multiplexer #(.enable("false")) multiplexer_14 (.in0(MenToReg), .in1(1'b0), .out(multiplexer_14_out), .sel(RST));
  Multiplexer #(.enable("false")) multiplexer_15 (.in0(MenWrite), .in1(1'b0), .out(multiplexer_15_out), .sel(RST));
  Multiplexer #(.width(4), .enable("false")) multiplexer_16 (
    .in0(AluOP), .in1(4'b0000), .out(multiplexer_16_out), .sel(RST));
  Multiplexer #(.enable("false")) multiplexer_17 (.in0(AluSrcB), .in1(1'b0), .out(multiplexer_17_out), .sel(RST));
  Multiplexer #(.enable("false")) multiplexer_18 (.in0(RegWrite), .in1(1'b0), .out(multiplexer_18_out), .sel(RST));
  Multiplexer #(.enable("false")) multiplexer_19 (.in0(JAL), .in1(1'b0), .out(multiplexer_19_out), .sel(RST));
  Multiplexer #(.enable("false")) multiplexer_20 (.in0(RegDst), .in1(1'b0), .out(multiplexer_20_out), .sel(RST));
  Multiplexer #(.enable("false")) multiplexer_21 (.in0(Syscall), .in1(1'b0), .out(multiplexer_21_out), .sel(RST));
  Register #(.width(1)) register_1 (.D(multiplexer_6_out), .en(EN), .Q(BLEZ_2), .clk(CLK));  // open: clr
  Register #(.width(1)) register_2 (.D(multiplexer_7_out), .en(EN), .Q(SH_2), .clk(CLK));  // open: clr
  Register #(.width(1)) register_3 (.D(multiplexer_8_out), .en(EN), .Q(V_2), .clk(CLK));  // open: clr
  Register #(.width(1)) register_4 (.D(multiplexer_9_out), .en(EN), .Q(SigedExt_2), .clk(CLK));  // open: clr
  Register #(.width(1)) register_5 (.D(multiplexer_10_out), .en(EN), .Q(JR_2), .clk(CLK));  // open: clr
  Register #(.width(1)) register_6 (.D(multiplexer_11_out), .en(EN), .Q(JMP_2), .clk(CLK));  // open: clr
  Register #(.width(1)) register_7 (.D(multiplexer_12_out), .en(EN), .Q(Beq_2), .clk(CLK));  // open: clr
  Register #(.width(1)) register_8 (.D(multiplexer_13_out), .en(EN), .Q(Bne_2), .clk(CLK));  // open: clr
  Register #(.width(1)) register_9 (.D(multiplexer_14_out), .en(EN), .Q(MenToReg_2), .clk(CLK));  // open: clr
  Register #(.width(1)) register_10 (.D(multiplexer_15_out), .en(EN), .Q(MenWrite_2), .clk(CLK));  // open: clr
  Register #(.width(4)) register_11 (.D(multiplexer_16_out), .en(EN), .Q(AluOP_2), .clk(CLK));  // open: clr
  Register #(.width(1)) register_12 (.D(multiplexer_17_out), .en(EN), .Q(AluSrcB_2), .clk(CLK));  // open: clr
  Register #(.width(1)) register_13 (.D(multiplexer_18_out), .en(EN), .Q(RegWrite_2), .clk(CLK));  // open: clr
  Register #(.width(1)) register_14 (.D(multiplexer_19_out), .en(EN), .Q(JAL_2), .clk(CLK));  // open: clr
  Register #(.width(1)) register_15 (.D(multiplexer_20_out), .en(EN), .Q(RegDst_2), .clk(CLK));  // open: clr
  Register #(.width(1)) register_16 (.D(multiplexer_21_out), .en(EN), .Q(Syscall_2), .clk(CLK));  // open: clr
endmodule

module EX_MEM (
  input  [31:0] IR,
  input  SH,
  input  JR,
  input  [31:0] PC,
  input  JMP,
  input  [31:0] B,
  input  MenToReg,
  input  MenWrite,
  input  [31:0] ALU,
  input  JAL,
  input  RegWrite,
  input  RST,
  input  RegDst,
  input  CLK,
  input  EN,
  input  Syscall,
  input  [31:0] A,
  output [31:0] IR_2,
  output SH_2,
  output JR_2,
  output [31:0] PC_2,
  output JMP_2,
  output [31:0] B_2,
  output MenToReg_2,
  output MenWrite_2,
  output [31:0] ALU_2,
  output JAL_2,
  output RegWrite_2,
  output RegDst_2,
  output Syscall_2,
  output [31:0] A_2
);

  wire multiplexer_6_out, multiplexer_7_out, multiplexer_8_out, multiplexer_9_out, multiplexer_10_out,
       multiplexer_11_out, multiplexer_12_out, multiplexer_13_out, multiplexer_14_out;
  wire [31:0] multiplexer_1_out, multiplexer_2_out, multiplexer_3_out, multiplexer_4_out, multiplexer_5_out;

  Multiplexer #(.width(32), .enable("false")) multiplexer_1 (
    .in0(IR), .in1({32{1'b0}}), .out(multiplexer_1_out), .sel(RST));
  Multiplexer #(.width(32), .enable("false")) multiplexer_2 (
    .in0(PC), .in1({32{1'b0}}), .out(multiplexer_2_out), .sel(RST));
  Multiplexer #(.width(32), .enable("false")) multiplexer_3 (
    .in0(B), .in1({32{1'b0}}), .out(multiplexer_3_out), .sel(RST));
  Multiplexer #(.width(32), .enable("false")) multiplexer_4 (
    .in0(ALU), .in1({32{1'b0}}), .out(multiplexer_4_out), .sel(RST));
  Multiplexer #(.width(32), .enable("false")) multiplexer_5 (
    .in0(A), .in1({32{1'b0}}), .out(multiplexer_5_out), .sel(RST));
  Register #(.width(32)) u_IR (.D(multiplexer_1_out), .en(EN), .Q(IR_2), .clk(CLK));  // open: clr
  Register #(.width(32)) u_PC (.D(multiplexer_2_out), .en(EN), .Q(PC_2), .clk(CLK));  // open: clr
  Register #(.width(32)) u_B (.D(multiplexer_3_out), .en(EN), .Q(B_2), .clk(CLK));  // open: clr
  Register #(.width(32)) u_ALU (.D(multiplexer_4_out), .en(EN), .Q(ALU_2), .clk(CLK));  // open: clr
  Register #(.width(32)) u_B_2 (.D(multiplexer_5_out), .en(EN), .Q(A_2), .clk(CLK));  // open: clr
  Multiplexer #(.enable("false")) multiplexer_6 (.in0(SH), .in1(1'b0), .out(multiplexer_6_out), .sel(RST));
  Multiplexer #(.enable("false")) multiplexer_7 (.in0(JR), .in1(1'b0), .out(multiplexer_7_out), .sel(RST));
  Multiplexer #(.enable("false")) multiplexer_8 (.in0(JMP), .in1(1'b0), .out(multiplexer_8_out), .sel(RST));
  Multiplexer #(.enable("false")) multiplexer_9 (.in0(MenToReg), .in1(1'b0), .out(multiplexer_9_out), .sel(RST));
  Multiplexer #(.enable("false")) multiplexer_10 (.in0(MenWrite), .in1(1'b0), .out(multiplexer_10_out), .sel(RST));
  Multiplexer #(.enable("false")) multiplexer_11 (.in0(JAL), .in1(1'b0), .out(multiplexer_11_out), .sel(RST));
  Multiplexer #(.enable("false")) multiplexer_12 (.in0(RegWrite), .in1(1'b0), .out(multiplexer_12_out), .sel(RST));
  Multiplexer #(.enable("false")) multiplexer_13 (.in0(RegDst), .in1(1'b0), .out(multiplexer_13_out), .sel(RST));
  Multiplexer #(.enable("false")) multiplexer_14 (.in0(Syscall), .in1(1'b0), .out(multiplexer_14_out), .sel(RST));
  Register #(.width(1)) register_1 (.D(multiplexer_6_out), .en(EN), .Q(SH_2), .clk(CLK));  // open: clr
  Register #(.width(1)) register_2 (.D(multiplexer_7_out), .en(EN), .Q(JR_2), .clk(CLK));  // open: clr
  Register #(.width(1)) register_3 (.D(multiplexer_8_out), .en(EN), .Q(JMP_2), .clk(CLK));  // open: clr
  Register #(.width(1)) register_4 (.D(multiplexer_9_out), .en(EN), .Q(MenToReg_2), .clk(CLK));  // open: clr
  Register #(.width(1)) register_5 (.D(multiplexer_10_out), .en(EN), .Q(MenWrite_2), .clk(CLK));  // open: clr
  Register #(.width(1)) register_6 (.D(multiplexer_11_out), .en(EN), .Q(JAL_2), .clk(CLK));  // open: clr
  Register #(.width(1)) register_7 (.D(multiplexer_12_out), .en(EN), .Q(RegWrite_2), .clk(CLK));  // open: clr
  Register #(.width(1)) register_8 (.D(multiplexer_13_out), .en(EN), .Q(RegDst_2), .clk(CLK));  // open: clr
  Register #(.width(1)) register_9 (.D(multiplexer_14_out), .en(EN), .Q(Syscall_2), .clk(CLK));  // open: clr
endmodule

module MEM_WB (
  input  [31:0] IR,
  input  SH,
  input  JR,
  input  [31:0] PC,
  input  JMP,
  input  [31:0] MEMOUT,
  input  MenToReg,
  input  [31:0] ALU,
  input  JAL,
  input  RegWrite,
  input  RegDst,
  input  RST,
  input  EN,
  input  CLK,
  input  Syscall,
  input  [31:0] A,
  input  [31:0] B,
  output [31:0] IR_2,
  output SH_2,
  output JR_2,
  output [31:0] PC_2,
  output JMP_2,
  output [31:0] MEMOUT_2,
  output MenToReg_2,
  output [31:0] ALU_2,
  output JAL_2,
  output RegWrite_2,
  output RegDst_2,
  output Syscall_2,
  output [31:0] A_2,
  output [31:0] B_2
);

  wire multiplexer_7_out, multiplexer_8_out, multiplexer_9_out, multiplexer_10_out, multiplexer_11_out,
       multiplexer_12_out, multiplexer_13_out, multiplexer_14_out;
  wire [31:0] multiplexer_1_out, multiplexer_2_out, multiplexer_3_out, multiplexer_4_out, multiplexer_5_out,
       multiplexer_6_out;

  Multiplexer #(.width(32), .enable("false")) multiplexer_1 (
    .in0(A), .in1({32{1'b0}}), .out(multiplexer_1_out), .sel(RST));
  Multiplexer #(.width(32), .enable("false")) multiplexer_2 (
    .in0(B), .in1({32{1'b0}}), .out(multiplexer_2_out), .sel(RST));
  Multiplexer #(.width(32), .enable("false")) multiplexer_3 (
    .in0(IR), .in1({32{1'b0}}), .out(multiplexer_3_out), .sel(RST));
  Multiplexer #(.width(32), .enable("false")) multiplexer_4 (
    .in0(PC), .in1({32{1'b0}}), .out(multiplexer_4_out), .sel(RST));
  Multiplexer #(.width(32), .enable("false")) multiplexer_5 (
    .in0(MEMOUT), .in1({32{1'b0}}), .out(multiplexer_5_out), .sel(RST));
  Multiplexer #(.width(32), .enable("false")) multiplexer_6 (
    .in0(ALU), .in1({32{1'b0}}), .out(multiplexer_6_out), .sel(RST));
  Register #(.width(32)) u_B (.D(multiplexer_1_out), .en(EN), .Q(A_2), .clk(CLK));  // open: clr
  Register #(.width(32)) u_B_2 (.D(multiplexer_2_out), .en(EN), .Q(B_2), .clk(CLK));  // open: clr
  Register #(.width(32)) u_IR (.D(multiplexer_3_out), .en(EN), .Q(IR_2), .clk(CLK));  // open: clr
  Register #(.width(32)) u_PC (.D(multiplexer_4_out), .en(EN), .Q(PC_2), .clk(CLK));  // open: clr
  Register #(.width(32)) B_3 (.D(multiplexer_5_out), .en(EN), .Q(MEMOUT_2), .clk(CLK));  // open: clr
  Register #(.width(32)) u_ALU (.D(multiplexer_6_out), .en(EN), .Q(ALU_2), .clk(CLK));  // open: clr
  Multiplexer #(.enable("false")) multiplexer_7 (.in0(SH), .in1(1'b0), .out(multiplexer_7_out), .sel(RST));
  Multiplexer #(.enable("false")) multiplexer_8 (.in0(JR), .in1(1'b0), .out(multiplexer_8_out), .sel(RST));
  Multiplexer #(.enable("false")) multiplexer_9 (.in0(JMP), .in1(1'b0), .out(multiplexer_9_out), .sel(RST));
  Multiplexer #(.enable("false")) multiplexer_10 (.in0(MenToReg), .in1(1'b0), .out(multiplexer_10_out), .sel(RST));
  Multiplexer #(.enable("false")) multiplexer_11 (.in0(JAL), .in1(1'b0), .out(multiplexer_11_out), .sel(RST));
  Multiplexer #(.enable("false")) multiplexer_12 (.in0(RegWrite), .in1(1'b0), .out(multiplexer_12_out), .sel(RST));
  Multiplexer #(.enable("false")) multiplexer_13 (.in0(RegDst), .in1(1'b0), .out(multiplexer_13_out), .sel(RST));
  Multiplexer #(.enable("false")) multiplexer_14 (.in0(Syscall), .in1(1'b0), .out(multiplexer_14_out), .sel(RST));
  Register #(.width(1)) register_1 (.D(multiplexer_7_out), .en(EN), .Q(SH_2), .clk(CLK));  // open: clr
  Register #(.width(1)) register_2 (.D(multiplexer_8_out), .en(EN), .Q(JR_2), .clk(CLK));  // open: clr
  Register #(.width(1)) register_3 (.D(multiplexer_9_out), .en(EN), .Q(JMP_2), .clk(CLK));  // open: clr
  Register #(.width(1)) register_4 (.D(multiplexer_10_out), .en(EN), .Q(MenToReg_2), .clk(CLK));  // open: clr
  Register #(.width(1)) register_5 (.D(multiplexer_11_out), .en(EN), .Q(JAL_2), .clk(CLK));  // open: clr
  Register #(.width(1)) register_6 (.D(multiplexer_12_out), .en(EN), .Q(RegWrite_2), .clk(CLK));  // open: clr
  Register #(.width(1)) register_7 (.D(multiplexer_13_out), .en(EN), .Q(RegDst_2), .clk(CLK));  // open: clr
  Register #(.width(1)) register_8 (.D(multiplexer_14_out), .en(EN), .Q(Syscall_2), .clk(CLK), .clr(RST));
endmodule

module \分支相关流水线  (
  output [4:0] out_1,
  output [4:0] out_2
);

  wire AluSrcB, and_1_out, and_2_out, and_3_out, and_4_out, Beq, Bi_Jiao, BLEZ, Bne, CLK, comparator_1_eq,
       EN, Go, IR1, IR2, IR3, JAL, JMP, JR, LOCK, MEM_JAL, MEM_JMP, MEM_JR, MEM_MemToReg, MEM_MemWrite,
       MEM_RegDst, MEM_RegWrite, MEM_SH, Mem_Syscall, MemToReg, MemWrite, mips_alu_1_equal,
       multiplexer_10_out, or_1_out, or_2_out, or_4_out, RegDst, RegWrite, RST, SH, SignedExt, Syscall, V,
       W1, W2, W3, WB_JAL, WB_JMP, WB_JR, WB_MemToReg, WB_RegDst, WB_RegWrite, WB_SH, WB_Syscall,
       \硬布线控制器_1_alu_src , \硬布线控制器_1_beq , \硬布线控制器_1_blez , \硬布线控制器_1_bne , \硬布线控制器_1_jal , \硬布线控制器_1_jmp ,
       \硬布线控制器_1_jr , \硬布线控制器_1_memtoreg , \硬布线控制器_1_memwrite , \硬布线控制器_1_regdst , \硬布线控制器_1_regwrite ,
       \硬布线控制器_1_sh , \硬布线控制器_1_signedext , \硬布线控制器_1_syscall , \硬布线控制器_1_v ;
  wire [3:0] AluOP, multiplexer_18_out, multiplexer_19_out, \硬布线控制器_1_alu_op ;
  wire [4:0] multiplexer_8_out, multiplexer_11_out, multiplexer_13_out;
  wire [11:0] KUO;
  wire [15:0] _0_15, _0_15D, _16, \LoadUse次数 , \总周期数 , \插入气泡数 , \无条件分支数 , \条件分支成功数 ;
  wire [19:0] multiplexer_7_out;
  wire [25:16] _25_0;
  wire [31:0] adder_2_out, ALU_Result, bit_extender_2_out, bit_extender_3_out, EX_PC, ID_PC, IF_PC, Imm,
       Imm1, LedData, MEM_ALU_Result, MEM_IR, MEM_PC, Mem_R1, multiplexer_2_out, multiplexer_3_out,
       multiplexer_4_out, multiplexer_5_out, multiplexer_6_out, multiplexer_12_out, multiplexer_15_out,
       multiplexer_16_out, multiplexer_17_out, multiplexer_20_out, PC_q, R1, R2, R11, R22, RAM_Out,
       rom_1_data, shifter_1_out, WB_ALU_Result, WB_IR, WB_PC, WB_R1, WB_R2, WB_RAM_Out;
  wire [31:16] ID_IR, MEM_R2;
  wire [31:26] EX_IR;

  Button \u_总复位  (.out(RST));
  Button _1 (.out(IR1));
  Button _2 (.out(IR2));
  Button _3 (.out(IR3));
  Multiplexer #(.enable("false")) multiplexer_1 (.in0(1'b1), .in1(1'b0), .out(EN), .sel(and_1_out));
  Button \u_继续运行  (.out(Go));
  LED led_1 (.in(W1));
  LED led_2 (.in(W2));
  LED led_3 (.in(W3));
  assign Imm = {{16{_0_15D[15]}}, _0_15D};  // Bit_Extender bit_extender_1
  Register #(.width(32)) PC (.D({{20{1'b0}}, KUO}), .en(EN), .Q(PC_q), .clk(CLK), .clr(RST));
  and and_1 (and_1_out, LOCK, ~Go);  // AND_Gate
  Counter #(.width(16), .max('hffff)) counter_1 (.count(EN), .Q(\总周期数 ), .clk(CLK), .clr(RST));  // open: load, D, carry
  Hex_Digit_Display hex_digit_display_1 (.value(LedData[31:28]));  // open: dp
  Adder #(.width(32)) adder_1 (.a(PC_q), .b(32'h4), .out(IF_PC));  // open: cin, cout
  Shifter #(.width(32)) shifter_1 (.in(Imm1), .\dist (5'b00010), .out(shifter_1_out));
  assign bit_extender_2_out = {{16{_0_15[15]}}, _0_15};  // Bit_Extender bit_extender_2
  Hex_Digit_Display hex_digit_display_2 (.value(LedData[23:20]));  // open: dp
  Hex_Digit_Display hex_digit_display_3 (.value(LedData[27:24]));  // open: dp
  ROM #(.addrWidth(10), .dataWidth(32)) rom_1 (.addr(PC_q[11:2]), .data(rom_1_data));  // open: sel
  assign bit_extender_3_out = {{16{1'b0}}, _0_15};  // Bit_Extender bit_extender_3
  Multiplexer #(.width(32), .enable("false")) multiplexer_2 (
    .in0(bit_extender_3_out), .in1(bit_extender_2_out), .out(multiplexer_2_out), .sel(SignedExt));
  Hex_Digit_Display hex_digit_display_4 (.value(LedData[15:12]));  // open: dp
  Hex_Digit_Display hex_digit_display_5 (.value(LedData[19:16]));  // open: dp
  or or_1 (or_1_out, Bi_Jiao, JMP);
  Adder #(.width(32)) adder_2 (.a(EX_PC), .b(shifter_1_out), .out(adder_2_out));  // open: cin, cout
  Multiplexer #(.width(32), .enable("false")) multiplexer_3 (
    .in0({4'b0000, _25_0, _0_15, 2'b00}), .in1(R11), .out(multiplexer_3_out), .sel(JR));
  Hex_Digit_Display hex_digit_display_6 (.value(LedData[7:4]));  // open: dp
  Hex_Digit_Display hex_digit_display_7 (.value(LedData[11:8]));  // open: dp
  Clock clock_1 (.out(CLK));
  IF_ID if_id_1 (.IR(rom_1_data), .PC(IF_PC), .IR_2({ID_IR, _0_15D}), .PC_2(ID_PC), .RST(or_1_out), .EN(EN), .CLK(CLK));
  Multiplexer #(.width(32), .enable("false")) multiplexer_4 (
    .in0(IF_PC), .in1(adder_2_out), .out(multiplexer_4_out), .sel(Bi_Jiao));
  Multiplexer #(.width(32), .enable("false")) multiplexer_5 (
    .in0(R22), .in1(multiplexer_2_out), .out(multiplexer_5_out), .sel(AluSrcB));
  Multiplexer #(.width(32), .enable("false")) multiplexer_6 (
    .in0(multiplexer_5_out), .in1({32{1'b0}}), .out(multiplexer_6_out), .sel(BLEZ));
  Hex_Digit_Display hex_digit_display_8 (.value(LedData[3:0]));  // open: dp
  Multiplexer #(.width(32), .enable("false")) multiplexer_7 (
    .in0(multiplexer_4_out), .in1(multiplexer_3_out), .out({multiplexer_7_out, KUO}), .sel(JMP));
  Multiplexer #(.width(5), .enable("false")) multiplexer_8 (
    .in0(_0_15[10:6]), .in1(R11[4:0]), .out(multiplexer_8_out), .sel(V));
  and and_2 (and_2_out, Beq, mips_alu_1_equal);
  and and_3 (and_3_out, Bne, ~mips_alu_1_equal);  // AND_Gate
  or or_2 (or_2_out, mips_alu_1_equal, ALU_Result[0]);
  MIPS_ALU mips_alu_1 (
    .X(R11), .Y(multiplexer_6_out), .AluOP(AluOP), .Equal(mips_alu_1_equal), .Result(ALU_Result),
    .shamt(multiplexer_8_out));  // open: Result_2
  // Probe on \总周期数 
  // Probe on \无条件分支数 
  // Probe on \条件分支成功数 
  // Probe on \插入气泡数 
  // Probe on \LoadUse次数 
  Multiplexer #(.width(5), .enable("false")) multiplexer_9 (
    .in0(ID_IR[25:21]), .in1(5'b00010), .out(out_1), .sel(\硬布线控制器_1_syscall ));
  Multiplexer #(.enable("false")) multiplexer_10 (.in0(1'b0), .in1(or_2_out), .out(multiplexer_10_out), .sel(BLEZ));
  // Probe on IF_PC[11:0]
  Counter #(.width(16), .max('hffff)) counter_2 (
    .count(JMP), .Q(\无条件分支数 ), .clk(CLK), .clr(RST));  // open: load, D, carry
  Counter #(.width(16), .max('hffff)) counter_3 (
    .count(Bi_Jiao), .Q(\条件分支成功数 ), .clk(CLK), .clr(RST));  // open: load, D, carry
  Multiplexer #(.width(5), .enable("false")) multiplexer_11 (
    .in0(WB_IR[20:16]), .in1(WB_IR[15:11]), .out(multiplexer_11_out), .sel(WB_RegDst));
  Multiplexer #(.width(32), .enable("false")) multiplexer_12 (
    .in0(WB_ALU_Result), .in1(WB_RAM_Out), .out(multiplexer_12_out), .sel(WB_MemToReg));
  or or_3 (Bi_Jiao, and_2_out, and_3_out, multiplexer_10_out);
  // Probe on ID_PC[11:0]
  Multiplexer #(.width(5), .enable("false")) multiplexer_13 (
    .in0(ID_IR[20:16]), .in1(5'b00100), .out(multiplexer_13_out), .sel(\硬布线控制器_1_syscall ));
  Multiplexer #(.width(5), .enable("false")) multiplexer_14 (
    .in0(multiplexer_11_out), .in1({5{1'b1}}), .out(out_2), .sel(WB_JAL));
  Multiplexer #(.width(32), .enable("false")) multiplexer_15 (
    .in0(multiplexer_12_out), .in1(WB_PC), .out(multiplexer_15_out), .sel(WB_JAL));
  // Probe on EX_PC[11:0]
  // Probe on MEM_PC[11:0]
  Multiplexer #(.width(32), .enable("false")) multiplexer_16 (
    .in0({{16{1'b0}}, _16}), .in1({_16, {16{1'b0}}}), .out(multiplexer_16_out), .sel(MEM_ALU_Result[1]));
  // Probe on WB_PC[11:0]
  MIPS_Regifile mips_regifile_1 (
    .Din(multiplexer_15_out), .Clk(CLK), .R1(R1), .R2(R2), .WE(WB_RegWrite), .W_num(out_2), .R1_num(out_1),
    .R2_num(multiplexer_13_out));
  Multiplexer #(.width(32), .enable("false")) multiplexer_17 (
    .in0({MEM_R2, _16}), .in1(multiplexer_16_out), .out(multiplexer_17_out), .sel(MEM_SH));
  Multiplexer #(.width(4), .enable("false")) multiplexer_18 (
    .in0(4'b1111), .in1(multiplexer_19_out), .out(multiplexer_18_out), .sel(MEM_SH));
  Multiplexer #(.width(4), .enable("false")) multiplexer_19 (
    .in0(4'b0011), .in1(4'b1100), .out(multiplexer_19_out), .sel(MEM_ALU_Result[1]));
  // MIPS_RAM mips_ram_1: pin names not known; wires that end beside it: MEM_ALU_Result[21:2], multiplexer_17_out, MEM_MemWrite, multiplexer_18_out, CLK, RST, RAM_Out, WB_IR[31:26], WB_IR[5:0], WB_IR[25:21]
  \硬布线控制器  \u_硬布线控制器_1  (
    .Func(_0_15D[5:0]), .OP(ID_IR[31:26]), .ALU_OP(\硬布线控制器_1_alu_op ), .MemToReg(\硬布线控制器_1_memtoreg ),
    .MemWrite(\硬布线控制器_1_memwrite ), .ALU_SRC(\硬布线控制器_1_alu_src ), .RegWrite(\硬布线控制器_1_regwrite ),
    .SysCALL(\硬布线控制器_1_syscall ), .SignedExt(\硬布线控制器_1_signedext ), .RegDst(\硬布线控制器_1_regdst ),
    .JR(\硬布线控制器_1_jr ), .JMP(\硬布线控制器_1_jmp ), .Beq(\硬布线控制器_1_beq ), .JAL(\硬布线控制器_1_jal ),
    .Bne(\硬布线控制器_1_bne ), .V(\硬布线控制器_1_v ), .SH(\硬布线控制器_1_sh ), .BLEZ(\硬布线控制器_1_blez ));
  EX_MEM ex_mem_1 (
    .IR({EX_IR, _25_0, _0_15}), .SH(SH), .JR(JR), .PC(EX_PC), .JMP(JMP), .B(R22), .MenToReg(MemToReg),
    .MenWrite(MemWrite), .ALU(ALU_Result), .JAL(JAL), .IR_2(MEM_IR), .SH_2(MEM_SH), .JR_2(MEM_JR),
    .PC_2(MEM_PC), .JMP_2(MEM_JMP), .B_2({MEM_R2, _16}), .MenToReg_2(MEM_MemToReg),
    .MenWrite_2(MEM_MemWrite), .ALU_2(MEM_ALU_Result), .JAL_2(MEM_JAL), .RST(RST), .EN(EN), .CLK(CLK),
    .RegWrite(RegWrite), .RegWrite_2(MEM_RegWrite), .RegDst(RegDst), .RegDst_2(MEM_RegDst),
    .Syscall(Syscall), .Syscall_2(Mem_Syscall), .A(R11), .A_2(Mem_R1));
  or or_4 (or_4_out, Bi_Jiao, JMP);
  ID_EX id_ex_1 (
    .IR({ID_IR, _0_15D}), .BLEZ(\硬布线控制器_1_blez ), .SH(\硬布线控制器_1_sh ), .PC(ID_PC), .V(\硬布线控制器_1_v ),
    .SigedExt(\硬布线控制器_1_signedext ), .A(R1), .JR(\硬布线控制器_1_jr ), .JMP(\硬布线控制器_1_jmp ), .Beq(\硬布线控制器_1_beq ),
    .B(R2), .Bne(\硬布线控制器_1_bne ), .MenToReg(\硬布线控制器_1_memtoreg ), .Imm(Imm), .MenWrite(\硬布线控制器_1_memwrite ),
    .AluOP(\硬布线控制器_1_alu_op ), .AluSrcB(\硬布线控制器_1_alu_src ), .RegWrite(\硬布线控制器_1_regwrite ),
    .JAL(\硬布线控制器_1_jal ), .RegDst(\硬布线控制器_1_regdst ), .Syscall(\硬布线控制器_1_syscall ),
    .IR_2({EX_IR, _25_0, _0_15}), .BLEZ_2(BLEZ), .SH_2(SH), .PC_2(EX_PC), .V_2(V), .SigedExt_2(SignedExt),
    .A_2(R11), .JR_2(JR), .JMP_2(JMP), .Beq_2(Beq), .B_2(R22), .Bne_2(Bne), .MenToReg_2(MemToReg),
    .Imm_2(Imm1), .MenWrite_2(MemWrite), .AluOP_2(AluOP), .AluSrcB_2(AluSrcB), .RegWrite_2(RegWrite),
    .JAL_2(JAL), .RegDst_2(RegDst), .Syscall_2(Syscall), .RST(or_4_out), .EN(EN), .CLK(CLK));
  Comparator #(.width(32)) comparator_1 (.a(WB_R1), .b(32'h22), .eq(comparator_1_eq));  // open: gt, lt
  MEM_WB mem_wb_1 (
    .IR(MEM_IR), .SH(MEM_SH), .JR(MEM_JR), .PC(MEM_PC), .JMP(MEM_JMP), .MEMOUT(RAM_Out),
    .MenToReg(MEM_MemToReg), .ALU(MEM_ALU_Result), .JAL(MEM_JAL), .RegWrite(MEM_RegWrite),
    .RegDst(MEM_RegDst), .IR_2(WB_IR), .SH_2(WB_SH), .JR_2(WB_JR), .PC_2(WB_PC), .JMP_2(WB_JMP),
    .MEMOUT_2(WB_RAM_Out), .ALU_2(WB_ALU_Result), .JAL_2(WB_JAL), .RegWrite_2(WB_RegWrite),
    .RegDst_2(WB_RegDst), .RST(RST), .EN(EN), .CLK(CLK), .MenToReg_2(WB_MemToReg), .Syscall_2(WB_Syscall),
    .Syscall(Mem_Syscall), .A(Mem_R1), .A_2(WB_R1), .B({MEM_R2, _16}), .B_2(WB_R2));
  and and_4 (and_4_out, comparator_1_eq, WB_Syscall);
  and and_5 (LOCK, ~comparator_1_eq, WB_Syscall);  // AND_Gate
  Multiplexer #(.width(32)) multiplexer_20 (
    .in1(WB_R2), .out(multiplexer_20_out), .sel(and_4_out), .en(and_4_out));  // open: in0
  Register #(.width(32)) register_1 (.D(multiplexer_20_out), .Q(LedData), .clk(CLK), .clr(RST));  // open: en

  // Other names for the same wires on the sheet: _25_0[15:0] = _0_15; EX_IR[25:0] = {_25_0, _0_15};
  //   shamt[4:0] = _0_15[10:6]; Func[5:0] = _0_15D[5:0]; ID_IR[15:0] = _0_15D; rd[4:0] = _0_15D[15:11];
  //   rt[4:0] = ID_IR[20:16]; rs[4:0] = ID_IR[25:21]; OP[5:0] = ID_IR[31:26]; 半字选择 = MEM_ALU_Result[1];
  //   MEM_R2[15:0] = _16; WB_rd[4:0] = WB_IR[15:11]; WB_rt[4:0] = WB_IR[20:16]

  // Notes on the sheet:
  //   中断源
  //   中断等待指示
  //   指令存储器
  //   contents of rom_1 (hex, n*v repeats v):
  //   20110020 20020022 8000c06 20110000 20110000 2002000a 10000003 20110000 20110000 2002000a 14110003
  //   20110000 20110000 2002000a c000c14 2002000a 0 0 0 c 2231ffff 0 0 0 112020 0 0 0 c 1620fff6 3e00008
  //   数码管输出
  //   OP
  //   rs
  //   rt
  //   rd
  //   Func
  //   流水调试日志用
  //   JMP
  //   JR
  //   OP
  //   Func
  //   OP
  //   Func
  //   rs
  //   rt
  //   rd
  //   Beq
  //   Bne
  //   MemToReg
  //   MemWrite
  //   AluOP
  //   AluSrcB
  //   RegWrite
  //   JAL
  //   RegDst
  //   Syscall
endmodule

module \气泡流水线  (
);

  wire AluSrcB, and_1_out, and_2_out, and_3_out, and_4_out, and_5_out, and_6_out, Beq, Bi_Jiao, BLEZ, Bne,
       CLK, comparator_1_eq, EN, Go, IR1, IR2, IR3, JAL, JMP, JR, LOCK, MEM_JAL, MEM_JMP, MEM_JR,
       MEM_MemToReg, MEM_MemWrite, MEM_RegDst, MEM_RegWrite, MEM_SH, Mem_Syscall, MemToReg, MemWrite,
       mips_alu_1_equal, multiplexer_10_out, or_1_out, or_2_out, or_4_out, RegDst, RegWrite, RST, SH,
       SignedExt, Syscall, V, W1, W2, W3, WB_JAL, WB_JMP, WB_JR, WB_MemToReg, WB_RegDst, WB_RegWrite, WB_SH,
       WB_Syscall, \数据相关 , \硬布线控制器_1_alu_src , \硬布线控制器_1_beq , \硬布线控制器_1_blez , \硬布线控制器_1_bne ,
       \硬布线控制器_1_jal , \硬布线控制器_1_jmp , \硬布线控制器_1_jr , \硬布线控制器_1_memtoreg , \硬布线控制器_1_memwrite ,
       \硬布线控制器_1_regdst , \硬布线控制器_1_regwrite , \硬布线控制器_1_sh , \硬布线控制器_1_signedext , \硬布线控制器_1_syscall ,
       \硬布线控制器_1_v ;
  wire [3:0] AluOP, multiplexer_18_out, multiplexer_19_out, \硬布线控制器_1_alu_op ;
  wire [4:0] EX_WriteReg, ID_R1_num, ID_R2_num, Mem_WriteReg, multiplexer_8_out, multiplexer_11_out,
       multiplexer_14_out, multiplexer_20_out, multiplexer_22_out;
  wire [11:0] KUO;
  wire [15:0] _0_15, _0_15D, _16, \LoadUse次数 , \总周期数 , \插入气泡数 , \无条件分支数 , \条件分支成功数 ;
  wire [19:0] multiplexer_7_out;
  wire [25:16] _25_0;
  wire [31:0] adder_2_out, ALU_Result, bit_extender_2_out, bit_extender_3_out, EX_PC, ID_PC, IF_PC, Imm,
       Imm1, LedData, MEM_ALU_Result, MEM_IR, MEM_PC, Mem_R1, multiplexer_2_out, multiplexer_3_out,
       multiplexer_4_out, multiplexer_5_out, multiplexer_6_out, multiplexer_12_out, multiplexer_15_out,
       multiplexer_16_out, multiplexer_17_out, multiplexer_23_out, PC_q, R1, R2, R11, R22, RAM_Out,
       rom_1_data, shifter_1_out, WB_ALU_Result, WB_IR, WB_PC, WB_R1, WB_R2, WB_RAM_Out;
  wire [31:16] ID_IR, MEM_R2;
  wire [31:26] EX_IR;

  Button \u_总复位  (.out(RST));
  Button _1 (.out(IR1));
  Button _2 (.out(IR2));
  Button _3 (.out(IR3));
  Multiplexer #(.enable("false")) multiplexer_1 (.in0(1'b1), .in1(1'b0), .out(EN), .sel(and_2_out));
  Button \u_继续运行  (.out(Go));
  LED led_1 (.in(W1));
  LED led_2 (.in(W2));
  LED led_3 (.in(W3));
  assign Imm = {{16{_0_15D[15]}}, _0_15D};  // Bit_Extender bit_extender_1
  Register #(.width(32)) PC (.D({{20{1'b0}}, KUO}), .en(and_1_out), .Q(PC_q), .clk(CLK), .clr(RST));
  and and_1 (and_1_out, EN, ~\数据相关 );  // AND_Gate
  and and_2 (and_2_out, LOCK, ~Go);  // AND_Gate
  Counter #(.width(16), .max('hffff)) counter_1 (.count(EN), .Q(\总周期数 ), .clk(CLK), .clr(RST));  // open: load, D, carry
  Hex_Digit_Display hex_digit_display_1 (.value(LedData[31:28]));  // open: dp
  Adder #(.width(32)) adder_1 (.a(PC_q), .b(32'h4), .out(IF_PC));  // open: cin, cout
  Shifter #(.width(32)) shifter_1 (.in(Imm1), .\dist (5'b00010), .out(shifter_1_out));
  assign bit_extender_2_out = {{16{_0_15[15]}}, _0_15};  // Bit_Extender bit_extender_2
  Hex_Digit_Display hex_digit_display_2 (.value(LedData[23:20]));  // open: dp
  Hex_Digit_Display hex_digit_display_3 (.value(LedData[27:24]));  // open: dp
  \数据相关检测  \u_数据相关检测_1  (
    .OP(ID_IR[31:26]), .EX_WriteReg_num(EX_WriteReg), .EX_RegWrite(RegWrite),
    .MEM_WriteReg_num(Mem_WriteReg), .MEM_RegWrite(MEM_RegWrite), .\数据相关 (\数据相关 ), .Func(_0_15D[5:0]),
    .ID_R1_num(ID_R1_num), .ID_R2_num(ID_R2_num));
  ROM #(.addrWidth(10), .dataWidth(32)) rom_1 (.addr(PC_q[11:2]), .data(rom_1_data));  // open: sel
  assign bit_extender_3_out = {{16{1'b0}}, _0_15};  // Bit_Extender bit_extender_3
  Multiplexer #(.width(32), .enable("false")) multiplexer_2 (
    .in0(bit_extender_3_out), .in1(bit_extender_2_out), .out(multiplexer_2_out), .sel(SignedExt));
  Hex_Digit_Display hex_digit_display_4 (.value(LedData[15:12]));  // open: dp
  Hex_Digit_Display hex_digit_display_5 (.value(LedData[19:16]));  // open: dp
  and and_3 (and_3_out, EN, ~\数据相关 );  // AND_Gate
  or or_1 (or_1_out, Bi_Jiao, JMP);
  Adder #(.width(32)) adder_2 (.a(EX_PC), .b(shifter_1_out), .out(adder_2_out));  // open: cin, cout
  Multiplexer #(.width(32), .enable("false")) multiplexer_3 (
    .in0({4'b0000, _25_0, _0_15, 2'b00}), .in1(R11), .out(multiplexer_3_out), .sel(JR));
  Hex_Digit_Display hex_digit_display_6 (.value(LedData[7:4]));  // open: dp
  Hex_Digit_Display hex_digit_display_7 (.value(LedData[11:8]));  // open: dp
  Clock clock_1 (.out(CLK));
  IF_ID if_id_1 (
    .IR(rom_1_data), .PC(IF_PC), .IR_2({ID_IR, _0_15D}), .PC_2(ID_PC), .RST(or_1_out), .EN(and_3_out),
    .CLK(CLK));
  Multiplexer #(.width(32), .enable("false")) multiplexer_4 (
    .in0(IF_PC), .in1(adder_2_out), .out(multiplexer_4_out), .sel(Bi_Jiao));
  Multiplexer #(.width(32), .enable("false")) multiplexer_5 (
    .in0(R22), .in1(multiplexer_2_out), .out(multiplexer_5_out), .sel(AluSrcB));
  Multiplexer #(.width(32), .enable("false")) multiplexer_6 (
    .in0(multiplexer_5_out), .in1({32{1'b0}}), .out(multiplexer_6_out), .sel(BLEZ));
  Hex_Digit_Display hex_digit_display_8 (.value(LedData[3:0]));  // open: dp
  Counter #(.width(16), .max('hffff)) counter_2 (
    .count(\数据相关 ), .Q(\插入气泡数 ), .clk(CLK), .clr(RST));  // open: load, D, carry
  Multiplexer #(.width(32), .enable("false")) multiplexer_7 (
    .in0(multiplexer_4_out), .in1(multiplexer_3_out), .out({multiplexer_7_out, KUO}), .sel(JMP));
  Multiplexer #(.width(5), .enable("false")) multiplexer_8 (
    .in0(_0_15[10:6]), .in1(R11[4:0]), .out(multiplexer_8_out), .sel(V));
  and and_4 (and_4_out, Beq, mips_alu_1_equal);
  and and_5 (and_5_out, Bne, ~mips_alu_1_equal);  // AND_Gate
  or or_2 (or_2_out, mips_alu_1_equal, ALU_Result[0]);
  MIPS_ALU mips_alu_1 (
    .X(R11), .Y(multiplexer_6_out), .AluOP(AluOP), .Equal(mips_alu_1_equal), .Result(ALU_Result),
    .shamt(multiplexer_8_out));  // open: Result_2
  // Probe on \总周期数 
  // Probe on \无条件分支数 
  // Probe on \条件分支成功数 
  // Probe on \插入气泡数 
  // Probe on \LoadUse次数 
  Multiplexer #(.width(5), .enable("false")) multiplexer_9 (
    .in0(ID_IR[25:21]), .in1(5'b00010), .out(ID_R1_num), .sel(\硬布线控制器_1_syscall ));
  Multiplexer #(.enable("false")) multiplexer_10 (.in0(1'b0), .in1(or_2_out), .out(multiplexer_10_out), .sel(BLEZ));
  // Probe on IF_PC[11:0]
  Counter #(.width(16), .max('hffff)) counter_3 (
    .count(WB_JMP), .Q(\无条件分支数 ), .clk(CLK), .clr(RST));  // open: load, D, carry
  Counter #(.width(16), .max('hffff)) counter_4 (
    .count(Bi_Jiao), .Q(\条件分支成功数 ), .clk(CLK), .clr(RST));  // open: load, D, carry
  Multiplexer #(.width(5), .enable("false")) multiplexer_11 (
    .in0(WB_IR[20:16]), .in1(WB_IR[15:11]), .out(multiplexer_11_out), .sel(WB_RegDst));
  Multiplexer #(.width(32), .enable("false")) multiplexer_12 (
    .in0(WB_ALU_Result), .in1(WB_RAM_Out), .out(multiplexer_12_out), .sel(WB_MemToReg));
  or or_3 (Bi_Jiao, and_4_out, and_5_out, multiplexer_10_out);
  // Probe on ID_PC[11:0]
  Multiplexer #(.width(5), .enable("false")) multiplexer_13 (
    .in0(ID_IR[20:16]), .in1(5'b00100), .out(ID_R2_num), .sel(\硬布线控制器_1_syscall ));
  Multiplexer #(.width(5), .enable("false")) multiplexer_14 (
    .in0(multiplexer_11_out), .in1({5{1'b1}}), .out(multiplexer_14_out), .sel(WB_JAL));
  Multiplexer #(.width(32), .enable("false")) multiplexer_15 (
    .in0(multiplexer_12_out), .in1(WB_PC), .out(multiplexer_15_out), .sel(WB_JAL));
  // Probe on MEM_PC[11:0]
  // Probe on EX_PC[11:0]
  Multiplexer #(.width(32), .enable("false")) multiplexer_16 (
    .in0({{16{1'b0}}, _16}), .in1({_16, {16{1'b0}}}), .out(multiplexer_16_out), .sel(MEM_ALU_Result[1]));
  // Probe on WB_PC[11:0]
  MIPS_Regifile mips_regifile_1 (
    .Din(multiplexer_15_out), .Clk(CLK), .R1(R1), .R2(R2), .WE(WB_RegWrite), .W_num(multiplexer_14_out),
    .R1_num(ID_R1_num), .R2_num(ID_R2_num));
  Multiplexer #(.width(32), .enable("false")) multiplexer_17 (
    .in0({MEM_R2, _16}), .in1(multiplexer_16_out), .out(multiplexer_17_out), .sel(MEM_SH));
  Multiplexer #(.width(4), .enable("false")) multiplexer_18 (
    .in0(4'b1111), .in1(multiplexer_19_out), .out(multiplexer_18_out), .sel(MEM_SH));
  Multiplexer #(.width(4), .enable("false")) multiplexer_19 (
    .in0(4'b0011), .in1(4'b1100), .out(multiplexer_19_out), .sel(MEM_ALU_Result[1]));
  // MIPS_RAM mips_ram_1: pin names not known; wires that end beside it: MEM_ALU_Result[21:2], multiplexer_17_out, MEM_MemWrite, multiplexer_18_out, CLK, RST, RAM_Out, WB_IR[31:26], WB_IR[5:0], WB_IR[25:21]
  \硬布线控制器  \u_硬布线控制器_1  (
    .Func(_0_15D[5:0]), .OP(ID_IR[31:26]), .ALU_OP(\硬布线控制器_1_alu_op ), .MemToReg(\硬布线控制器_1_memtoreg ),
    .MemWrite(\硬布线控制器_1_memwrite ), .ALU_SRC(\硬布线控制器_1_alu_src ), .RegWrite(\硬布线控制器_1_regwrite ),
    .SysCALL(\硬布线控制器_1_syscall ), .SignedExt(\硬布线控制器_1_signedext ), .RegDst(\硬布线控制器_1_regdst ),
    .JR(\硬布线控制器_1_jr ), .JMP(\硬布线控制器_1_jmp ), .Beq(\硬布线控制器_1_beq ), .JAL(\硬布线控制器_1_jal ),
    .Bne(\硬布线控制器_1_bne ), .V(\硬布线控制器_1_v ), .SH(\硬布线控制器_1_sh ), .BLEZ(\硬布线控制器_1_blez ));
  EX_MEM ex_mem_1 (
    .IR({EX_IR, _25_0, _0_15}), .SH(SH), .JR(JR), .PC(EX_PC), .JMP(JMP), .B(R22), .MenToReg(MemToReg),
    .MenWrite(MemWrite), .ALU(ALU_Result), .JAL(JAL), .IR_2(MEM_IR), .SH_2(MEM_SH), .JR_2(MEM_JR),
    .PC_2(MEM_PC), .JMP_2(MEM_JMP), .B_2({MEM_R2, _16}), .MenToReg_2(MEM_MemToReg),
    .MenWrite_2(MEM_MemWrite), .ALU_2(MEM_ALU_Result), .JAL_2(MEM_JAL), .RST(RST), .EN(EN), .CLK(CLK),
    .RegWrite(RegWrite), .RegWrite_2(MEM_RegWrite), .RegDst(RegDst), .RegDst_2(MEM_RegDst),
    .Syscall(Syscall), .Syscall_2(Mem_Syscall), .A(R11), .A_2(Mem_R1));
  Multiplexer #(.width(5), .enable("false")) multiplexer_20 (
    .in0(MEM_IR[20:16]), .in1(MEM_IR[15:11]), .out(multiplexer_20_out), .sel(MEM_RegDst));
  Multiplexer #(.width(5), .enable("false")) multiplexer_21 (
    .in0(multiplexer_20_out), .in1({5{1'b1}}), .out(Mem_WriteReg), .sel(MEM_JAL));
  or or_4 (or_4_out, Bi_Jiao, \数据相关 , JMP);
  ID_EX id_ex_1 (
    .IR({ID_IR, _0_15D}), .BLEZ(\硬布线控制器_1_blez ), .SH(\硬布线控制器_1_sh ), .PC(ID_PC), .V(\硬布线控制器_1_v ),
    .SigedExt(\硬布线控制器_1_signedext ), .A(R1), .JR(\硬布线控制器_1_jr ), .JMP(\硬布线控制器_1_jmp ), .Beq(\硬布线控制器_1_beq ),
    .B(R2), .Bne(\硬布线控制器_1_bne ), .MenToReg(\硬布线控制器_1_memtoreg ), .Imm(Imm), .MenWrite(\硬布线控制器_1_memwrite ),
    .AluOP(\硬布线控制器_1_alu_op ), .AluSrcB(\硬布线控制器_1_alu_src ), .RegWrite(\硬布线控制器_1_regwrite ),
    .JAL(\硬布线控制器_1_jal ), .RegDst(\硬布线控制器_1_regdst ), .Syscall(\硬布线控制器_1_syscall ),
    .IR_2({EX_IR, _25_0, _0_15}), .BLEZ_2(BLEZ), .SH_2(SH), .PC_2(EX_PC), .V_2(V), .SigedExt_2(SignedExt),
    .A_2(R11), .JR_2(JR), .JMP_2(JMP), .Beq_2(Beq), .B_2(R22), .Bne_2(Bne), .MenToReg_2(MemToReg),
    .Imm_2(Imm1), .MenWrite_2(MemWrite), .AluOP_2(AluOP), .AluSrcB_2(AluSrcB), .RegWrite_2(RegWrite),
    .JAL_2(JAL), .RegDst_2(RegDst), .Syscall_2(Syscall), .RST(or_4_out), .EN(EN), .CLK(CLK));
  Comparator #(.width(32)) comparator_1 (.a(WB_R1), .b(32'h22), .eq(comparator_1_eq));  // open: gt, lt
  MEM_WB mem_wb_1 (
    .IR(MEM_IR), .SH(MEM_SH), .JR(MEM_JR), .PC(MEM_PC), .JMP(MEM_JMP), .MEMOUT(RAM_Out),
    .MenToReg(MEM_MemToReg), .ALU(MEM_ALU_Result), .JAL(MEM_JAL), .RegWrite(MEM_RegWrite),
    .RegDst(MEM_RegDst), .IR_2(WB_IR), .SH_2(WB_SH), .JR_2(WB_JR), .PC_2(WB_PC), .JMP_2(WB_JMP),
    .MEMOUT_2(WB_RAM_Out), .ALU_2(WB_ALU_Result), .JAL_2(WB_JAL), .RegWrite_2(WB_RegWrite),
    .RegDst_2(WB_RegDst), .RST(RST), .EN(EN), .CLK(CLK), .MenToReg_2(WB_MemToReg), .Syscall_2(WB_Syscall),
    .Syscall(Mem_Syscall), .A(Mem_R1), .A_2(WB_R1), .B({MEM_R2, _16}), .B_2(WB_R2));
  and and_6 (and_6_out, comparator_1_eq, WB_Syscall);
  and and_7 (LOCK, ~comparator_1_eq, WB_Syscall);  // AND_Gate
  Multiplexer #(.width(5), .enable("false")) multiplexer_22 (
    .in0(_25_0[20:16]), .in1(_0_15[15:11]), .out(multiplexer_22_out), .sel(RegDst));
  Multiplexer #(.width(32)) multiplexer_23 (
    .in1(WB_R2), .out(multiplexer_23_out), .sel(and_6_out), .en(and_6_out));  // open: in0
  Multiplexer #(.width(5), .enable("false")) multiplexer_24 (
    .in0(multiplexer_22_out), .in1({5{1'b1}}), .out(EX_WriteReg), .sel(JAL));
  Register #(.width(32)) register_1 (.D(multiplexer_23_out), .Q(LedData), .clk(CLK), .clr(RST));  // open: en

  // Other names for the same wires on the sheet: _25_0[15:0] = _0_15; EX_IR[25:0] = {_25_0, _0_15};
  //   shamt[4:0] = _0_15[10:6]; EX_rd[4:0] = _0_15[15:11]; EX_rt[4:0] = _25_0[20:16]; Func[5:0] = _0_15D[5:0];
  //   ID_IR[15:0] = _0_15D; rd[4:0] = _0_15D[15:11]; rt[4:0] = ID_IR[20:16]; rs[4:0] = ID_IR[25:21];
  //   OP[5:0] = ID_IR[31:26]; 半字选择 = MEM_ALU_Result[1]; MEM_rd[4:0] = MEM_IR[15:11]; MEM_rt[4:0] = MEM_IR[20:16];
  //   MEM_R2[15:0] = _16; WB_rd[4:0] = WB_IR[15:11]; WB_rt[4:0] = WB_IR[20:16]

  // Notes on the sheet:
  //   中断源
  //   中断等待指示
  //   指令存储器
  //   contents of rom_1 (hex, n*v repeats v):
  //   20110001 8000c05 20110001 20120002 20130003 8000c09 20110001 20120002 20130003 8000c0d 20110001
  //   20120002 20130003 8000c11 20110001 20120002 20130003 c000cbb 20100001 20110001 118fc0 112020
  //   20020022 c 118882 12200001 8000c15 112020 20020022 c 20110001 118880 112020 20020022 c 12200001
  //   8000c1f 20110001 118fc0 112020 20020022 c 1188c3 112020 20020022 c 118903 112020 20020022 c 118903
  //   112020 20020022 c 118903 112020 20020022 c 118903 112020 20020022 c 118903 112020 20020022 c 118903
  //   112020 20020022 c 118903 112020 20020022 c 20100001 109fc0 139fc3 8021 2012000c 24160003 26100001
  //   3210000f 20080008 20090001 139900 2709825 132020 20020022 c 1094022 1500fff9 22100001 2018000f
  //   2188024 108700 20080008 20090001 139902 2709825 132021 20020022 c 1094022 1500fff9 108702 2c9b022
  //   12c00001 8000c50 4020 1084027 84400 3508ffff 82021 20020022 c 2010ffff 20110000 ae300000 22100001
  //   22310004 ae300000 22100001 22310004 ae300000 22100001 22310004 ae300000 22100001 22310004 ae300000
  //   22100001 22310004 ae300000 22100001 22310004 ae300000 22100001 22310004 ae300000 22100001 22310004
  //   ae300000 22100001 22310004 ae300000 22100001 22310004 ae300000 22100001 22310004 ae300000 22100001
  //   22310004 ae300000 22100001 22310004 ae300000 22100001 22310004 ae300000 22100001 22310004 ae300000
  //   22100001 22310004 22100001 8020 2011003c 8e130000 8e340000 274402a 11000002 ae330000 ae140000
  //   2231fffc 1611fff8 102020 20020022 c 22100004 2011003c 1611fff2 20020032 c 8000c00 2002000a c
  //   20100000 22100001 102020 20020022 c 22100002 102020 20020022 c 22100003 102020 20020022 c 22100004
  //   102020 20020022 c 22100005 102020 20020022 c 22100006 102020 20020022 c 22100007 102020 20020022 c
  //   22100008 102020 20020022 20020022 c 3e00008
  //   数码管输出
  //   OP
  //   rs
  //   rt
  //   rd
  //   Func
  //   流水调试日志用
  //   JMP
  //   JR
  //   OP
  //   Func
  //   OP
  //   Func
  //   rs
  //   rt
  //   rd
  //   Beq
  //   Bne
  //   MemToReg
  //   MemWrite
  //   AluOP
  //   AluSrcB
  //   RegWrite
  //   JAL
  //   RegDst
  //   Syscall
  //   rt
  //   rd
  //   rt
  //   rd
endmodule

module \重定向流水线  (
);

  wire CLK, Go, IR1, IR2, IR3, RST, W1, W2, W3;
  wire [11:0] EX_PC, ID_PC, IF_PC, MEM_PC, WB_PC;
  wire [15:0] \LoadUse次数 , \总周期数 , \插入气泡数 , \无条件分支数 , \条件分支成功数 ;
  wire [31:0] LedData;

  Button \u_总复位  (.out(RST));
  Button _1 (.out(IR1));
  Button _2 (.out(IR2));
  Button _3 (.out(IR3));
  Button \u_继续运行  (.out(Go));
  LED led_1 (.in(W1));
  LED led_2 (.in(W2));
  LED led_3 (.in(W3));
  Hex_Digit_Display hex_digit_display_1 (.value(LedData[31:28]));  // open: dp
  Hex_Digit_Display hex_digit_display_2 (.value(LedData[27:24]));  // open: dp
  Hex_Digit_Display hex_digit_display_3 (.value(LedData[23:20]));  // open: dp
  Hex_Digit_Display hex_digit_display_4 (.value(LedData[15:12]));  // open: dp
  Hex_Digit_Display hex_digit_display_5 (.value(LedData[19:16]));  // open: dp
  Hex_Digit_Display hex_digit_display_6 (.value(LedData[7:4]));  // open: dp
  Hex_Digit_Display hex_digit_display_7 (.value(LedData[11:8]));  // open: dp
  Clock clock_1 (.out(CLK));
  Hex_Digit_Display hex_digit_display_8 (.value(LedData[3:0]));  // open: dp
  // Probe on \总周期数 
  // Probe on \无条件分支数 
  // Probe on \条件分支成功数 
  // Probe on \插入气泡数 
  // Probe on \LoadUse次数 
  // Probe on IF_PC
  // Probe on ID_PC
  // Probe on MEM_PC
  // Probe on EX_PC
  // Probe on WB_PC

  // Notes on the sheet:
  //   中断源
  //   中断等待指示
  //   数码管输出
  //   流水调试日志用
endmodule

module CCMB (
  input  OP0,
  input  OP1,
  input  OP2,
  input  OP3,
  input  OP4,
  input  OP5,
  input  F0,
  input  F1,
  input  F2,
  input  F3,
  input  F4,
  input  F5,
  output V,
  output SH,
  output BLEZ
);

  wire and_1_out, and_2_out, not_1_out, not_2_out, not_3_out, not_4_out, not_5_out, not_6_out, not_7_out,
       not_8_out, not_9_out, not_10_out, not_11_out, not_12_out, not_13_out, not_14_out, not_15_out,
       not_16_out, not_17_out, not_18_out, not_19_out, not_20_out, not_21_out, not_22_out, not_23_out,
       not_24_out, not_25_out, not_26_out, not_27_out;

  not not_1 (not_1_out, OP5);
  not not_2 (not_2_out, OP4);
  not not_3 (not_3_out, OP3);
  not not_4 (not_4_out, OP2);
  not not_5 (not_5_out, OP1);
  not not_6 (not_6_out, OP0);
  not not_7 (not_7_out, F5);
  not not_8 (not_8_out, F4);
  not not_9 (not_9_out, F3);
  not not_10 (not_10_out, F1);
  not not_11 (not_11_out, F0);
  not not_12 (not_12_out, OP5);
  not not_13 (not_13_out, OP4);
  not not_14 (not_14_out, OP3);
  not not_15 (not_15_out, OP2);
  not not_16 (not_16_out, OP1);
  not not_17 (not_17_out, OP0);
  not not_18 (not_18_out, F5);
  not not_19 (not_19_out, F4);
  not not_20 (not_20_out, F3);
  not not_21 (not_21_out, OP4);
  not not_22 (not_22_out, OP2);
  not not_23 (not_23_out, OP1);
  not not_24 (not_24_out, OP5);
  not not_25 (not_25_out, OP4);
  not not_26 (not_26_out, OP3);
  not not_27 (not_27_out, OP0);
  and and_1 (and_1_out, not_1_out, not_2_out, not_3_out, not_4_out, not_5_out, not_6_out, not_7_out, not_8_out, not_9_out, F2, not_10_out, not_11_out);
  and and_2 (and_2_out, not_12_out, not_13_out, not_14_out, not_15_out, not_16_out, not_17_out, not_18_out, not_19_out, not_20_out, F2, F1, F0);
  and and_3 (SH, OP5, not_21_out, OP3, not_22_out, not_23_out, OP0);
  and and_4 (BLEZ, not_24_out, not_25_out, not_26_out, OP2, OP1, not_27_out);
  or or_1 (V, and_1_out, and_2_out);
endmodule
