// Logisim project cpu28_7.circ as structural Verilog: 25 circuits, main circuit ◇单周期MIPS
module \单周期MIPS  (
);

  wire and_1_out, and_2_out, and_3_out, and_4_out, and_5_out, BLTZ, CLK, comparator_1_lt, comparator_2_eq,
       Go, InUse, JAL, lh, mips_alu_1_equal, not_1_out, or_1_out, or_2_out, or_3_out, register_2_q, RST,
       SignedExt, SRAV, syscall, \片选 , \硬布线控制器_1_alu_src , \硬布线控制器_1_beq , \硬布线控制器_1_bne , \硬布线控制器_1_jmp ,
       \硬布线控制器_1_jr , \硬布线控制器_1_memtoreg , \硬布线控制器_1_memwrite , \硬布线控制器_1_regdst , \硬布线控制器_1_regwrite ;
  wire [3:0] adder_1_out_2, \硬布线控制器_1_alu_op ;
  wire [4:0] multiplexer_4_out, multiplexer_5_out, multiplexer_6_out, multiplexer_8_out, multiplexer_12_out;
  wire [15:0] multiplexer_13_out, multiplexer_13_out_2, \总周期数 , \无条件分支数 , \条件分支成功数 ;
  wire [25:0] Adress;
  wire [27:0] adder_1_out;
  wire [31:0] adder_2_out, adder_3_out, bit_extender_1_out, bit_extender_2_out, bit_extender_3_out,
       bit_extender_4_out, branch0, branch1, LedData, mips_alu_1_result, mips_regifile_1_r2,
       multiplexer_2_out, multiplexer_3_out, multiplexer_7_out, multiplexer_9_out, multiplexer_11_out,
       multiplexer_14_out, multiplexer_15_out, PC_q, ram_1_data, rs, shifter_1_out, shifter_2_out;
  wire [31:26] rom_1_data;

  Button \u_总复位  (.out(RST));
  Button \u_继续运行  (.out(Go));
  Clock clock_1 (.out(CLK));
  Multiplexer #(.width(32), .enable("false")) multiplexer_1 (
    .in0({adder_1_out_2, adder_1_out}), .in1(adder_3_out), .out(branch0), .sel(or_2_out));
  Multiplexer #(.width(32), .enable("false")) multiplexer_2 (
    .in0(branch1), .in1({adder_1_out_2, Adress, 2'b00}), .out(multiplexer_2_out), .sel(\硬布线控制器_1_jmp ));
  Hex_Digit_Display hex_digit_display_1 (.value(LedData[31:28]));  // open: dp
  Hex_Digit_Display hex_digit_display_2 (.value(LedData[27:24]));  // open: dp
  Multiplexer #(.width(32), .enable("false")) multiplexer_3 (
    .in0(multiplexer_2_out), .in1(rs), .out(multiplexer_3_out), .sel(\硬布线控制器_1_jr ));
  Hex_Digit_Display hex_digit_display_3 (.value(LedData[19:16]));  // open: dp
  Hex_Digit_Display hex_digit_display_4 (.value(LedData[23:20]));  // open: dp
  or or_1 (or_1_out, \硬布线控制器_1_jr , \硬布线控制器_1_jmp , JAL);
  Register #(.width(32)) PC (.D(multiplexer_3_out), .en(InUse), .Q(PC_q), .clk(CLK), .clr(RST));
  Hex_Digit_Display hex_digit_display_5 (.value(LedData[15:12]));  // open: dp
  Hex_Digit_Display hex_digit_display_6 (.value(LedData[11:8]));  // open: dp
  Counter #(.width(16), .max('hffff)) counter_1 (
    .count(or_1_out), .Q(\无条件分支数 ), .clk(CLK), .clr(RST));  // open: load, D, carry
  Counter #(.width(16), .max('hffff)) counter_2 (
    .count(InUse), .Q(\总周期数 ), .clk(CLK), .clr(RST));  // open: load, D, carry
  Hex_Digit_Display hex_digit_display_7 (.value(LedData[7:4]));  // open: dp
  Hex_Digit_Display hex_digit_display_8 (.value(LedData[3:0]));  // open: dp
  ROM #(.addrWidth(10), .dataWidth(32)) rom_1 (.addr(PC_q[11:2]), .data({rom_1_data, Adress}));  // open: sel
  Adder #(.width(32)) adder_1 (.a(PC_q), .b(32'h4), .out({adder_1_out_2, adder_1_out}));  // open: cin, cout
  assign bit_extender_1_out = {{16{1'b0}}, Adress[15:0]};  // Bit_Extender bit_extender_1
  assign bit_extender_2_out = {{16{Adress[15]}}, Adress[15:0]};  // Bit_Extender bit_extender_2
  // Probe on \总周期数 
  // Probe on \无条件分支数 
  // Probe on \条件分支成功数 
  \硬布线控制器  \u_硬布线控制器_1  (
    .Func(Adress[5:0]), .OP(rom_1_data), .ALU_OP(\硬布线控制器_1_alu_op ), .MemToReg(\硬布线控制器_1_memtoreg ),
    .MemWrite(\硬布线控制器_1_memwrite ), .ALU_SRC(\硬布线控制器_1_alu_src ), .RegWrite(\硬布线控制器_1_regwrite ),
    .SysCALL(syscall), .SignedExt(SignedExt), .RegDst(\硬布线控制器_1_regdst ), .JR(\硬布线控制器_1_jr ),
    .JMP(\硬布线控制器_1_jmp ), .Beq(\硬布线控制器_1_beq ), .JAL(JAL), .Bne(\硬布线控制器_1_bne ), .SRAV(SRAV), .LH(lh),
    .BLTZ(BLTZ));  // open: ERET
  Multiplexer #(.width(5), .enable("false")) multiplexer_4 (
    .in0(Adress[25:21]), .in1(5'b00100), .out(multiplexer_4_out), .sel(syscall));
  Multiplexer #(.width(5), .enable("false")) multiplexer_5 (
    .in0(Adress[20:16]), .in1(5'b00010), .out(multiplexer_5_out), .sel(syscall));
  Multiplexer #(.width(5), .enable("false")) multiplexer_6 (
    .in0(Adress[20:16]), .in1(Adress[15:11]), .out(multiplexer_6_out), .sel(\硬布线控制器_1_regdst ));
  Multiplexer #(.width(32), .enable("false")) multiplexer_7 (
    .in0(bit_extender_1_out), .in1(bit_extender_2_out), .out(multiplexer_7_out), .sel(SignedExt));
  Shifter #(.width(32)) shifter_1 (.in(bit_extender_2_out), .\dist (5'b00010), .out(shifter_1_out));
  Adder #(.width(32)) adder_2 (
    .a(shifter_1_out), .b({adder_1_out_2, adder_1_out}), .out(adder_2_out));  // open: cin, cout
  Comparator #(.width(32)) comparator_1 (.a(rs), .b({32{1'b0}}), .lt(comparator_1_lt));  // open: gt, eq
  Multiplexer #(.width(5), .enable("false")) multiplexer_8 (
    .in0(multiplexer_6_out), .in1({5{1'b1}}), .out(multiplexer_8_out), .sel(JAL));
  Multiplexer #(.width(32), .enable("false")) multiplexer_9 (
    .in0(multiplexer_15_out), .in1({adder_1_out_2, adder_1_out}), .out(multiplexer_9_out), .sel(JAL));
  Multiplexer #(.width(32), .enable("false")) multiplexer_10 (
    .in0(branch0), .in1(adder_2_out), .out(branch1), .sel(and_1_out));
  and and_1 (and_1_out, comparator_1_lt, BLTZ);
  MIPS_Regifile mips_regifile_1 (
    .Din(multiplexer_9_out), .Clk(CLK), .R1(rs), .R2(mips_regifile_1_r2), .WE(\硬布线控制器_1_regwrite ),
    .W_num(multiplexer_8_out), .R1_num(multiplexer_4_out), .R2_num(multiplexer_5_out));
  Multiplexer #(.width(32), .enable("false")) multiplexer_11 (
    .in0(mips_regifile_1_r2), .in1(multiplexer_7_out), .out(multiplexer_11_out), .sel(\硬布线控制器_1_alu_src ));
  Multiplexer #(.width(5), .enable("false")) multiplexer_12 (
    .in0(Adress[10:6]), .in1(rs[4:0]), .out(multiplexer_12_out), .sel(SRAV));
  Shifter #(.width(32)) shifter_2 (.in(bit_extender_2_out), .\dist (5'b00010), .out(shifter_2_out));
  and and_2 (and_2_out, syscall, comparator_2_eq);
  Comparator #(.width(32)) comparator_2 (.a(mips_regifile_1_r2), .b(32'h22), .eq(comparator_2_eq));  // open: gt, lt
  and and_3 (and_3_out, mips_alu_1_equal, \硬布线控制器_1_beq );
  and and_4 (and_4_out, \硬布线控制器_1_bne , ~mips_alu_1_equal);  // AND_Gate
  MIPS_ALU mips_alu_1 (
    .X(rs), .Y(multiplexer_11_out), .AluOP(\硬布线控制器_1_alu_op ), .Equal(mips_alu_1_equal),
    .Result({mips_alu_1_result[31:2], \片选 , mips_alu_1_result[0]}), .shamt(multiplexer_12_out));  // open: Result_2
  Adder #(.width(32)) adder_3 (
    .a(shifter_2_out), .b({adder_1_out_2, adder_1_out}), .out(adder_3_out));  // open: cin, cout
  not not_1 (not_1_out, comparator_2_eq);
  or or_2 (or_2_out, and_3_out, and_4_out);
  Register #(.width(32)) register_1 (.D(rs), .en(and_2_out), .Q(LedData), .clk(CLK), .clr(RST));
  and and_5 (and_5_out, syscall, not_1_out);
  Counter #(.width(16), .max('hffff)) counter_3 (
    .count(or_2_out), .Q(\条件分支成功数 ), .clk(CLK), .clr(RST));  // open: load, D, carry
  Register #(.width(1)) register_2 (.D(syscall), .en(and_5_out), .Q(register_2_q), .clk(CLK), .clr(or_3_out));
  or or_3 (or_3_out, RST, Go);
  RAM #(.addrWidth(10), .dataWidth(32), .bus("separate")) ram_1 (
    .addr(mips_alu_1_result[11:2]), .din(mips_regifile_1_r2), .data(ram_1_data), .str(\硬布线控制器_1_memwrite ),
    .sel(1'b1), .clk(CLK), .ld(\硬布线控制器_1_memtoreg ), .clr(RST));
  assign bit_extender_3_out = {{16{multiplexer_13_out[15]}}, multiplexer_13_out};  // Bit_Extender bit_extender_3
  assign bit_extender_4_out = {{16{multiplexer_13_out_2[15]}}, multiplexer_13_out_2};  // Bit_Extender bit_extender_4
  not not_2 (InUse, register_2_q);
  Multiplexer #(.width(32), .enable("false")) multiplexer_13 (
    .in0({mips_alu_1_result[31:2], \片选 , mips_alu_1_result[0]}), .in1(ram_1_data),
    .out({multiplexer_13_out_2, multiplexer_13_out}), .sel(\硬布线控制器_1_memtoreg ));
  Multiplexer #(.width(32), .enable("false")) multiplexer_14 (
    .in0(bit_extender_3_out), .in1(bit_extender_4_out), .out(multiplexer_14_out), .sel(\片选 ));
  Multiplexer #(.width(32), .enable("false")) multiplexer_15 (
    .in0({multiplexer_13_out_2, multiplexer_13_out}), .in1(multiplexer_14_out), .out(multiplexer_15_out),
    .sel(lh));

  // Other names for the same wires on the sheet: shamt[4:0] = Adress[10:6]

  // Notes on the sheet:
  //   数码管输出应该用寄存器锁存，否则显示数据只能一闪而过
  //   可以通过项目增加Logisim库的方式将前几次实验完成的电路作为子电路引入到本电路中使用
  //   指令存储器
  //   数码管输出
  //   contents of rom_1 (hex, n*v repeats v):
  //   20110020 20020022 8100006 20110000 20110000 2002000a 10000003 20110000 20110000 2002000a 14110003
  //   20110000 20110000 2002000a c100014 2002000a 0 0 0 c 2231ffff 0 0 0 112020 0 0 0 c 1620fff6 3e00008
  //   Shamt
  //   OP
  //   Func
  //   rs
  //   指令字
  //   rt
  //   rd
  //   Adress
  //   JMP
  //   JR
  //   OP
  //   Func
  //   总复位信号应将除ROM以外所有存储组件全部清零
  //   Beq
  //   AluOP
  //   AluSrcB
  //   RegWrite
  //   JAL
  //   RegDst
  //   Syscall
  //   MemToReg
  //   MemWrite
endmodule

// 单周期硬布线控制器
module \硬布线控制器  (
  input  [5:0] OP,
  input  [5:0] Func,
  output [3:0] ALU_OP,
  output MemToReg,
  output MemWrite,
  output ALU_SRC,
  output RegWrite,
  output SysCALL,
  output SignedExt,
  output RegDst,
  output Beq,
  output Bne,
  output JR,
  output JMP,
  output JAL,
  output SRAV,
  output LH,
  output BLTZ,
  output ERET
);

  \运算控制器  \u_运算控制器_1  (
    .OP0(OP[0]), .OP1(OP[1]), .OP2(OP[2]), .OP3(OP[3]), .OP4(OP[4]), .OP5(OP[5]), .F0(Func[0]), .F1(Func[1]),
    .F2(Func[2]), .F3(Func[3]), .F4(Func[4]), .F5(Func[5]), .S0(ALU_OP[0]), .S1(ALU_OP[1]), .S2(ALU_OP[2]),
    .S3(ALU_OP[3]));
  \控制信号生成  \u_控制信号生成_1  (
    .OP0(OP[0]), .OP1(OP[1]), .OP2(OP[2]), .OP3(OP[3]), .OP4(OP[4]), .OP5(OP[5]), .F0(Func[0]), .F1(Func[1]),
    .F2(Func[2]), .F3(Func[3]), .F4(Func[4]), .F5(Func[5]), .MemToReg(MemToReg), .MemWrite(MemWrite),
    .ALU_SRC(ALU_SRC), .RegWrite(RegWrite), .SysCALL(SysCALL), .SignedExt(SignedExt), .RegDst(RegDst),
    .BEQ(Beq), .BNE(Bne), .JR(JR), .JMP(JMP), .JAL(JAL));
  \CCMB和中断控制信号  \ccmb和中断控制信号_1  (
    .OP0(OP[0]), .OP1(OP[1]), .OP2(OP[2]), .OP3(OP[3]), .OP4(OP[4]), .OP5(OP[5]), .F0(Func[0]), .F1(Func[1]),
    .F2(Func[2]), .F3(Func[3]), .F4(Func[4]), .F5(Func[5]), .SRAV(SRAV), .LH(LH), .BLTZ(BLTZ), .ERET(ERET));

  // Other names for the same wires on the sheet: OP_CODE[5:0] = OP

  // Notes on the sheet:
  //   运算器控制器，根据指令生成运算器功能选择信号
  //   控制信号生成，产生数据通路需要的其他控制信号
endmodule

// 运算器控制器
module \运算控制器  (
  input  OP0,
  input  OP1,
  input  OP2,
  input  OP3,
  input  OP4,
  input  OP5,
  input  F0,
  input  F1,
  input  F2,
  input  F3,
  input  F4,
  input  F5,
  output S0,
  output S1,
  output S2,
  output S3
);

  wire and_1_out, and_2_out, and_3_out, and_4_out, and_5_out, and_6_out, and_7_out, and_8_out, and_9_out,
       and_10_out, and_11_out, and_12_out, and_13_out, and_14_out, and_15_out, and_16_out, and_17_out,
       and_18_out, and_19_out, and_20_out, and_21_out, and_22_out, and_23_out, and_24_out, and_25_out,
       and_26_out, and_27_out, and_28_out, and_29_out, and_30_out, and_31_out, and_32_out, and_33_out,
       and_34_out, and_35_out, and_36_out, and_37_out, and_38_out, and_39_out, and_40_out, and_41_out,
       and_42_out, not_1_out, not_2_out, not_3_out, not_4_out, not_5_out, not_6_out, not_7_out, not_8_out,
       not_9_out, not_10_out, not_11_out, not_12_out, not_13_out, not_14_out, not_15_out, not_16_out,
       not_17_out, not_18_out, not_19_out, not_20_out, not_21_out, not_22_out, not_23_out, not_24_out,
       not_25_out, not_26_out, not_27_out, not_28_out, not_29_out, not_30_out, not_31_out, not_32_out,
       not_33_out, not_34_out, not_35_out, not_36_out, not_37_out, not_38_out, not_39_out, not_40_out,
       not_41_out, not_42_out, not_43_out, not_44_out, not_45_out, not_46_out, not_47_out, not_48_out,
       not_49_out, not_50_out, not_51_out, not_52_out, not_53_out, not_54_out, not_55_out, not_56_out,
       not_57_out, not_58_out, not_59_out, not_60_out, not_61_out, not_62_out, not_63_out, not_64_out,
       not_65_out, not_66_out, not_67_out, not_68_out, not_69_out, not_70_out, not_71_out, not_72_out,
       not_73_out, not_74_out, not_75_out, not_76_out, not_77_out, not_78_out, not_79_out, not_80_out,
       not_81_out, not_82_out, not_83_out, not_84_out, not_85_out, not_86_out, not_87_out, not_88_out,
       not_89_out, not_90_out, not_91_out, not_92_out, not_93_out, not_94_out, not_95_out, not_96_out,
       not_97_out, not_98_out, not_99_out, not_100_out, not_101_out, not_102_out, not_103_out, not_104_out,
       not_105_out, not_106_out, not_107_out, not_108_out, not_109_out, not_110_out, not_111_out,
       not_112_out, not_113_out, not_114_out, not_115_out, not_116_out, not_117_out, not_118_out,
       not_119_out, not_120_out, not_121_out, not_122_out, not_123_out, not_124_out, not_125_out,
       not_126_out, not_127_out, not_128_out, not_129_out, not_130_out, not_131_out, not_132_out,
       not_133_out, not_134_out, not_135_out, not_136_out, not_137_out, not_138_out, not_139_out,
       not_140_out, not_141_out, not_142_out, not_143_out, not_144_out, not_145_out, not_146_out,
       not_147_out, not_148_out, not_149_out, not_150_out, not_151_out, not_152_out, not_153_out,
       not_154_out, not_155_out, not_156_out, not_157_out, not_158_out, not_159_out, not_160_out,
       not_161_out, not_162_out, not_163_out, not_164_out, not_165_out, not_166_out, not_167_out,
       not_168_out, not_169_out, not_170_out, not_171_out, not_172_out, not_173_out, not_174_out,
       not_175_out, not_176_out, not_177_out, not_178_out, not_179_out, not_180_out, not_181_out,
       not_182_out, not_183_out, not_184_out, not_185_out, not_186_out, not_187_out, not_188_out,
       not_189_out, not_190_out, not_191_out, not_192_out, not_193_out, not_194_out, not_195_out,
       not_196_out, not_197_out, not_198_out, not_199_out, not_200_out, not_201_out, not_202_out,
       not_203_out, not_204_out, not_205_out, not_206_out, not_207_out, not_208_out, not_209_out,
       not_210_out, not_211_out, not_212_out, not_213_out, not_214_out, not_215_out, not_216_out,
       not_217_out, not_218_out, not_219_out, not_220_out, not_221_out, not_222_out, not_223_out,
       not_224_out, not_225_out, not_226_out, not_227_out, not_228_out, not_229_out, not_230_out,
       not_231_out, not_232_out, not_233_out, not_234_out, not_235_out, not_236_out, not_237_out,
       not_238_out, not_239_out, not_240_out, not_241_out, not_242_out, not_243_out, not_244_out,
       not_245_out, not_246_out, not_247_out, not_248_out, not_249_out, not_250_out, not_251_out,
       not_252_out, not_253_out, not_254_out, not_255_out, not_256_out, not_257_out, not_258_out,
       not_259_out, not_260_out, not_261_out, not_262_out, not_263_out, not_264_out, not_265_out,
       not_266_out, not_267_out, not_268_out, not_269_out, not_270_out, not_271_out, not_272_out,
       not_273_out, not_274_out;

  not not_1 (not_1_out, OP5);
  not not_2 (not_2_out, OP4);
  not not_3 (not_3_out, OP3);
  not not_4 (not_4_out, OP2);
  not not_5 (not_5_out, OP1);
  not not_6 (not_6_out, OP0);
  not not_7 (not_7_out, F5);
  not not_8 (not_8_out, F4);
  not not_9 (not_9_out, F3);
  not not_10 (not_10_out, F2);
  not not_11 (not_11_out, OP5);
  not not_12 (not_12_out, OP4);
  not not_13 (not_13_out, OP3);
  not not_14 (not_14_out, OP2);
  not not_15 (not_15_out, OP1);
  not not_16 (not_16_out, OP0);
  not not_17 (not_17_out, F4);
  not not_18 (not_18_out, F3);
  not not_19 (not_19_out, F2);
  not not_20 (not_20_out, F1);
  not not_21 (not_21_out, F0);
  not not_22 (not_22_out, OP5);
  not not_23 (not_23_out, OP4);
  not not_24 (not_24_out, OP3);
  not not_25 (not_25_out, OP2);
  not not_26 (not_26_out, OP1);
  not not_27 (not_27_out, OP0);
  not not_28 (not_28_out, F4);
  not not_29 (not_29_out, F3);
  not not_30 (not_30_out, F2);
  not not_31 (not_31_out, F1);
  not not_32 (not_32_out, OP5);
  not not_33 (not_33_out, OP4);
  not not_34 (not_34_out, OP3);
  not not_35 (not_35_out, OP2);
  not not_36 (not_36_out, OP1);
  not not_37 (not_37_out, OP0);
  not not_38 (not_38_out, F4);
  not not_39 (not_39_out, F3);
  not not_40 (not_40_out, F1);
  not not_41 (not_41_out, F0);
  not not_42 (not_42_out, OP5);
  not not_43 (not_43_out, OP4);
  not not_44 (not_44_out, OP3);
  not not_45 (not_45_out, OP2);
  not not_46 (not_46_out, OP1);
  not not_47 (not_47_out, OP0);
  not not_48 (not_48_out, F4);
  not not_49 (not_49_out, F2);
  not not_50 (not_50_out, F0);
  not not_51 (not_51_out, OP5);
  not not_52 (not_52_out, OP4);
  not not_53 (not_53_out, OP2);
  not not_54 (not_54_out, OP1);
  not not_55 (not_55_out, OP0);
  not not_56 (not_56_out, OP5);
  not not_57 (not_57_out, OP4);
  not not_58 (not_58_out, OP1);
  not not_59 (not_59_out, OP0);
  not not_60 (not_60_out, OP5);
  not not_61 (not_61_out, OP4);
  not not_62 (not_62_out, OP2);
  not not_63 (not_63_out, OP1);
  not not_64 (not_64_out, OP5);
  not not_65 (not_65_out, OP4);
  not not_66 (not_66_out, OP2);
  not not_67 (not_67_out, OP0);
  not not_68 (not_68_out, OP4);
  not not_69 (not_69_out, OP3);
  not not_70 (not_70_out, OP2);
  not not_71 (not_71_out, OP4);
  not not_72 (not_72_out, OP2);
  not not_73 (not_73_out, OP5);
  not not_74 (not_74_out, OP4);
  not not_75 (not_75_out, OP3);
  not not_76 (not_76_out, OP2);
  not not_77 (not_77_out, OP1);
  not not_78 (not_78_out, OP0);
  not not_79 (not_79_out, F5);
  not not_80 (not_80_out, F4);
  not not_81 (not_81_out, F3);
  not not_82 (not_82_out, OP4);
  not not_83 (not_83_out, OP3);
  not not_84 (not_84_out, OP2);
  not not_85 (not_85_out, OP1);
  not not_86 (not_86_out, OP5);
  not not_87 (not_87_out, OP4);
  not not_88 (not_88_out, OP3);
  not not_89 (not_89_out, OP2);
  not not_90 (not_90_out, OP1);
  not not_91 (not_91_out, OP5);
  not not_92 (not_92_out, OP4);
  not not_93 (not_93_out, OP3);
  not not_94 (not_94_out, OP2);
  not not_95 (not_95_out, OP1);
  not not_96 (not_96_out, OP5);
  not not_97 (not_97_out, OP4);
  not not_98 (not_98_out, OP0);
  not not_99 (not_99_out, OP5);
  not not_100 (not_100_out, OP4);
  not not_101 (not_101_out, OP3);
  not not_102 (not_102_out, OP2);
  not not_103 (not_103_out, OP1);
  not not_104 (not_104_out, OP0);
  not not_105 (not_105_out, F5);
  not not_106 (not_106_out, F4);
  not not_107 (not_107_out, F3);
  not not_108 (not_108_out, F2);
  not not_109 (not_109_out, F0);
  not not_110 (not_110_out, OP5);
  not not_111 (not_111_out, OP4);
  not not_112 (not_112_out, OP3);
  not not_113 (not_113_out, OP2);
  not not_114 (not_114_out, OP1);
  not not_115 (not_115_out, OP0);
  not not_116 (not_116_out, F4);
  not not_117 (not_117_out, F3);
  not not_118 (not_118_out, F2);
  not not_119 (not_119_out, F0);
  not not_120 (not_120_out, OP5);
  not not_121 (not_121_out, OP4);
  not not_122 (not_122_out, OP3);
  not not_123 (not_123_out, OP2);
  not not_124 (not_124_out, OP1);
  not not_125 (not_125_out, OP0);
  not not_126 (not_126_out, F4);
  not not_127 (not_127_out, F3);
  not not_128 (not_128_out, F1);
  not not_129 (not_129_out, F0);
  not not_130 (not_130_out, OP5);
  not not_131 (not_131_out, OP4);
  not not_132 (not_132_out, OP3);
  not not_133 (not_133_out, OP2);
  not not_134 (not_134_out, OP1);
  not not_135 (not_135_out, OP0);
  not not_136 (not_136_out, F4);
  not not_137 (not_137_out, F3);
  not not_138 (not_138_out, OP5);
  not not_139 (not_139_out, OP4);
  not not_140 (not_140_out, OP3);
  not not_141 (not_141_out, OP2);
  not not_142 (not_142_out, OP1);
  not not_143 (not_143_out, OP0);
  not not_144 (not_144_out, F4);
  not not_145 (not_145_out, F2);
  not not_146 (not_146_out, F0);
  not not_147 (not_147_out, OP5);
  not not_148 (not_148_out, OP4);
  not not_149 (not_149_out, OP1);
  not not_150 (not_150_out, OP0);
  not not_151 (not_151_out, OP5);
  not not_152 (not_152_out, OP4);
  not not_153 (not_153_out, OP2);
  not not_154 (not_154_out, OP0);
  not not_155 (not_155_out, OP5);
  not not_156 (not_156_out, OP4);
  not not_157 (not_157_out, OP3);
  not not_158 (not_158_out, OP2);
  not not_159 (not_159_out, OP1);
  not not_160 (not_160_out, OP0);
  not not_161 (not_161_out, F4);
  not not_162 (not_162_out, F3);
  not not_163 (not_163_out, F2);
  not not_164 (not_164_out, F1);
  not not_165 (not_165_out, F0);
  not not_166 (not_166_out, OP5);
  not not_167 (not_167_out, OP4);
  not not_168 (not_168_out, OP3);
  not not_169 (not_169_out, OP2);
  not not_170 (not_170_out, OP1);
  not not_171 (not_171_out, OP0);
  not not_172 (not_172_out, F4);
  not not_173 (not_173_out, F3);
  not not_174 (not_174_out, F2);
  not not_175 (not_175_out, F1);
  not not_176 (not_176_out, OP5);
  not not_177 (not_177_out, OP4);
  not not_178 (not_178_out, OP3);
  not not_179 (not_179_out, OP2);
  not not_180 (not_180_out, OP1);
  not not_181 (not_181_out, OP0);
  not not_182 (not_182_out, F4);
  not not_183 (not_183_out, F3);
  not not_184 (not_184_out, F2);
  not not_185 (not_185_out, F0);
  not not_186 (not_186_out, OP5);
  not not_187 (not_187_out, OP4);
  not not_188 (not_188_out, OP3);
  not not_189 (not_189_out, OP2);
  not not_190 (not_190_out, OP1);
  not not_191 (not_191_out, OP0);
  not not_192 (not_192_out, F4);
  not not_193 (not_193_out, F3);
  not not_194 (not_194_out, F1);
  not not_195 (not_195_out, F0);
  not not_196 (not_196_out, OP5);
  not not_197 (not_197_out, OP4);
  not not_198 (not_198_out, OP3);
  not not_199 (not_199_out, OP2);
  not not_200 (not_200_out, OP1);
  not not_201 (not_201_out, OP0);
  not not_202 (not_202_out, F4);
  not not_203 (not_203_out, F2);
  not not_204 (not_204_out, OP5);
  not not_205 (not_205_out, OP4);
  not not_206 (not_206_out, OP2);
  not not_207 (not_207_out, OP1);
  not not_208 (not_208_out, OP0);
  not not_209 (not_209_out, OP5);
  not not_210 (not_210_out, OP4);
  not not_211 (not_211_out, OP1);
  not not_212 (not_212_out, OP0);
  not not_213 (not_213_out, OP5);
  not not_214 (not_214_out, OP4);
  not not_215 (not_215_out, OP2);
  not not_216 (not_216_out, OP1);
  not not_217 (not_217_out, OP4);
  not not_218 (not_218_out, OP3);
  not not_219 (not_219_out, OP2);
  not not_220 (not_220_out, OP4);
  not not_221 (not_221_out, OP2);
  not not_222 (not_222_out, OP4);
  not not_223 (not_223_out, OP3);
  not not_224 (not_224_out, OP2);
  not not_225 (not_225_out, OP1);
  not not_226 (not_226_out, OP5);
  not not_227 (not_227_out, OP4);
  not not_228 (not_228_out, OP3);
  not not_229 (not_229_out, OP2);
  not not_230 (not_230_out, OP1);
  not not_231 (not_231_out, OP0);
  not not_232 (not_232_out, F4);
  not not_233 (not_233_out, F3);
  not not_234 (not_234_out, F1);
  not not_235 (not_235_out, OP5);
  not not_236 (not_236_out, OP4);
  not not_237 (not_237_out, OP3);
  not not_238 (not_238_out, OP2);
  not not_239 (not_239_out, OP1);
  not not_240 (not_240_out, OP0);
  not not_241 (not_241_out, F4);
  not not_242 (not_242_out, F3);
  not not_243 (not_243_out, OP5);
  not not_244 (not_244_out, OP4);
  not not_245 (not_245_out, OP3);
  not not_246 (not_246_out, OP2);
  not not_247 (not_247_out, OP1);
  not not_248 (not_248_out, OP0);
  not not_249 (not_249_out, F4);
  not not_250 (not_250_out, F2);
  not not_251 (not_251_out, F0);
  not not_252 (not_252_out, OP5);
  not not_253 (not_253_out, OP4);
  not not_254 (not_254_out, OP3);
  not not_255 (not_255_out, OP2);
  not not_256 (not_256_out, OP1);
  not not_257 (not_257_out, OP0);
  not not_258 (not_258_out, F4);
  not not_259 (not_259_out, F2);
  not not_260 (not_260_out, OP5);
  not not_261 (not_261_out, OP4);
  not not_262 (not_262_out, OP2);
  not not_263 (not_263_out, OP0);
  not not_264 (not_264_out, OP5);
  not not_265 (not_265_out, OP4);
  not not_266 (not_266_out, OP1);
  not not_267 (not_267_out, OP5);
  not not_268 (not_268_out, OP4);
  not not_269 (not_269_out, OP0);
  not not_270 (not_270_out, OP5);
  not not_271 (not_271_out, OP4);
  not not_272 (not_272_out, OP3);
  not not_273 (not_273_out, OP2);
  not not_274 (not_274_out, OP1);
  and and_1 (and_1_out, not_1_out, not_2_out, not_3_out, not_4_out, not_5_out, not_6_out, not_7_out, not_8_out, not_9_out, not_10_out, F1, F0);
  and and_2 (and_2_out, not_11_out, not_12_out, not_13_out, not_14_out, not_15_out, not_16_out, F5, not_17_out, not_18_out, not_19_out, not_20_out, not_21_out);
  and and_3 (and_3_out, not_22_out, not_23_out, not_24_out, not_25_out, not_26_out, not_27_out, F5, not_28_out, not_29_out, not_30_out, not_31_out, F0);
  and and_4 (and_4_out, not_32_out, not_33_out, not_34_out, not_35_out, not_36_out, not_37_out, F5, not_38_out, not_39_out, F2, not_40_out, not_41_out);
  and and_5 (and_5_out, not_42_out, not_43_out, not_44_out, not_45_out, not_46_out, not_47_out, F5, not_48_out, F3, not_49_out, F1, not_50_out);
  and and_6 (and_6_out, not_51_out, not_52_out, OP3, not_53_out, not_54_out, not_55_out);
  and and_7 (and_7_out, not_56_out, not_57_out, OP3, OP2, not_58_out, not_59_out);
  and and_8 (and_8_out, not_60_out, not_61_out, OP3, not_62_out, not_63_out, OP0);
  and and_9 (and_9_out, not_64_out, not_65_out, OP3, not_66_out, OP1, not_67_out);
  and and_10 (and_10_out, OP5, not_68_out, not_69_out, not_70_out, OP1, OP0);
  and and_11 (and_11_out, OP5, not_71_out, OP3, not_72_out, OP1, OP0);
  and and_12 (and_12_out, not_73_out, not_74_out, not_75_out, not_76_out, not_77_out, not_78_out, not_79_out, not_80_out, not_81_out, F2, F1, F0);
  and and_13 (and_13_out, OP5, not_82_out, not_83_out, not_84_out, not_85_out, OP0);
  and and_14 (and_14_out, not_86_out, not_87_out, not_88_out, not_89_out, not_90_out, OP0);
  and and_15 (and_15_out, not_91_out, not_92_out, not_93_out, not_94_out, not_95_out, OP0);
  and and_16 (and_16_out, not_96_out, not_97_out, OP3, OP2, OP1, not_98_out);
  and and_17 (and_17_out, not_99_out, not_100_out, not_101_out, not_102_out, not_103_out, not_104_out, not_105_out, not_106_out, not_107_out, not_108_out, F1, not_109_out);
  and and_18 (and_18_out, not_110_out, not_111_out, not_112_out, not_113_out, not_114_out, not_115_out, F5, not_116_out, not_117_out, not_118_out, F1, not_119_out);
  and and_19 (and_19_out, not_120_out, not_121_out, not_122_out, not_123_out, not_124_out, not_125_out, F5, not_126_out, not_127_out, F2, not_128_out, not_129_out);
  and and_20 (and_20_out, not_130_out, not_131_out, not_132_out, not_133_out, not_134_out, not_135_out, F5, not_136_out, not_137_out, F2, F1, F0);
  and and_21 (and_21_out, not_138_out, not_139_out, not_140_out, not_141_out, not_142_out, not_143_out, F5, not_144_out, F3, not_145_out, F1, not_146_out);
  and and_22 (and_22_out, not_147_out, not_148_out, OP3, OP2, not_149_out, not_150_out);
  and and_23 (and_23_out, not_151_out, not_152_out, OP3, not_153_out, OP1, not_154_out);
  and and_24 (and_24_out, not_155_out, not_156_out, not_157_out, not_158_out, not_159_out, not_160_out, F5, not_161_out, not_162_out, not_163_out, not_164_out, not_165_out);
  and and_25 (and_25_out, not_166_out, not_167_out, not_168_out, not_169_out, not_170_out, not_171_out, F5, not_172_out, not_173_out, not_174_out, not_175_out, F0);
  and and_26 (and_26_out, not_176_out, not_177_out, not_178_out, not_179_out, not_180_out, not_181_out, F5, not_182_out, not_183_out, not_184_out, F1, not_185_out);
  and and_27 (and_27_out, not_186_out, not_187_out, not_188_out, not_189_out, not_190_out, not_191_out, F5, not_192_out, not_193_out, F2, not_194_out, not_195_out);
  and and_28 (and_28_out, not_196_out, not_197_out, not_198_out, not_199_out, not_200_out, not_201_out, F5, not_202_out, F3, not_203_out, F1, F0);
  and and_29 (and_29_out, not_204_out, not_205_out, OP3, not_206_out, not_207_out, not_208_out);
  and and_30 (and_30_out, not_209_out, not_210_out, OP3, OP2, not_211_out, not_212_out);
  and and_31 (and_31_out, not_213_out, not_214_out, OP3, not_215_out, not_216_out, OP0);
  and and_32 (and_32_out, OP5, not_217_out, not_218_out, not_219_out, OP1, OP0);
  and and_33 (and_33_out, OP5, not_220_out, OP3, not_221_out, OP1, OP0);
  and and_34 (and_34_out, OP5, not_222_out, not_223_out, not_224_out, not_225_out, OP0);
  and and_35 (and_35_out, not_226_out, not_227_out, not_228_out, not_229_out, not_230_out, not_231_out, F5, not_232_out, not_233_out, F2, not_234_out, F0);
  and and_36 (and_36_out, not_235_out, not_236_out, not_237_out, not_238_out, not_239_out, not_240_out, F5, not_241_out, not_242_out, F2, F1, F0);
  and and_37 (and_37_out, not_243_out, not_244_out, not_245_out, not_246_out, not_247_out, not_248_out, F5, not_249_out, F3, not_250_out, F1, not_251_out);
  and and_38 (and_38_out, not_252_out, not_253_out, not_254_out, not_255_out, not_256_out, not_257_out, F5, not_258_out, F3, not_259_out, F1, F0);
  and and_39 (and_39_out, not_260_out, not_261_out, OP3, not_262_out, OP1, not_263_out);
  and and_40 (and_40_out, not_264_out, not_265_out, OP3, OP2, not_266_out, OP0);
  and and_41 (and_41_out, not_267_out, not_268_out, OP3, OP2, OP1, not_269_out);
  and and_42 (and_42_out, not_270_out, not_271_out, not_272_out, not_273_out, not_274_out, OP0);
  or or_1 (S1, and_17_out, and_18_out, and_19_out, and_20_out, and_21_out, and_22_out, and_23_out);
  or or_2 (S2, and_24_out, and_25_out, and_26_out, and_27_out, and_28_out, and_29_out, and_30_out, and_31_out, and_32_out, and_33_out, and_34_out);
  or or_3 (S3, and_35_out, and_36_out, and_37_out, and_38_out, and_39_out, and_40_out, and_41_out, and_42_out);
  or or_4 (S0, and_1_out, and_2_out, and_3_out, and_4_out, and_5_out, and_6_out, and_7_out, and_8_out, and_9_out, and_10_out, and_11_out, and_12_out, and_13_out, and_14_out, and_15_out, and_16_out);
endmodule

// 控制信号生成
module \控制信号生成  (
  input  OP0,
  input  OP1,
  input  OP2,
  input  OP3,
  input  OP4,
  input  OP5,
  input  F0,
  input  F1,
  input  F2,
  input  F3,
  input  F4,
  input  F5,
  output MemToReg,
  output MemWrite,
  output ALU_SRC,
  output RegWrite,
  output SysCALL,
  output SignedExt,
  output RegDst,
  output BEQ,
  output BNE,
  output JR,
  output JMP,
  output JAL
);

  wire and_1_out, and_2_out, and_4_out, and_5_out, and_6_out, and_7_out, and_8_out, and_9_out, and_10_out,
       and_11_out, and_12_out, and_13_out, and_14_out, and_15_out, and_16_out, and_17_out, and_18_out,
       and_19_out, and_20_out, and_21_out, and_22_out, and_23_out, and_24_out, and_25_out, and_26_out,
       and_27_out, and_28_out, and_29_out, and_30_out, and_31_out, and_32_out, and_33_out, and_34_out,
       and_35_out, and_37_out, and_38_out, and_39_out, and_40_out, and_41_out, and_42_out, and_43_out,
       and_44_out, and_45_out, and_46_out, and_47_out, and_48_out, and_49_out, and_50_out, and_51_out,
       and_52_out, and_53_out, and_54_out, and_58_out, and_59_out, not_1_out, not_2_out, not_3_out,
       not_4_out, not_5_out, not_6_out, not_7_out, not_8_out, not_9_out, not_10_out, not_11_out, not_12_out,
       not_13_out, not_14_out, not_15_out, not_16_out, not_17_out, not_18_out, not_19_out, not_20_out,
       not_21_out, not_22_out, not_23_out, not_24_out, not_25_out, not_26_out, not_27_out, not_28_out,
       not_29_out, not_30_out, not_31_out, not_32_out, not_33_out, not_34_out, not_35_out, not_36_out,
       not_37_out, not_38_out, not_39_out, not_40_out, not_41_out, not_42_out, not_43_out, not_44_out,
       not_45_out, not_46_out, not_47_out, not_48_out, not_49_out, not_50_out, not_51_out, not_52_out,
       not_53_out, not_54_out, not_55_out, not_56_out, not_57_out, not_58_out, not_59_out, not_60_out,
       not_61_out, not_62_out, not_63_out, not_64_out, not_65_out, not_66_out, not_67_out, not_68_out,
       not_69_out, not_70_out, not_71_out, not_72_out, not_73_out, not_74_out, not_75_out, not_76_out,
       not_77_out, not_78_out, not_79_out, not_80_out, not_81_out, not_82_out, not_83_out, not_84_out,
       not_85_out, not_86_out, not_87_out, not_88_out, not_89_out, not_90_out, not_91_out, not_92_out,
       not_93_out, not_94_out, not_95_out, not_96_out, not_97_out, not_98_out, not_99_out, not_100_out,
       not_101_out, not_102_out, not_103_out, not_104_out, not_105_out, not_106_out, not_107_out,
       not_108_out, not_109_out, not_110_out, not_111_out, not_112_out, not_113_out, not_114_out,
       not_115_out, not_116_out, not_117_out, not_118_out, not_119_out, not_120_out, not_121_out,
       not_122_out, not_123_out, not_124_out, not_125_out, not_126_out, not_127_out, not_128_out,
       not_129_out, not_130_out, not_131_out, not_132_out, not_133_out, not_134_out, not_135_out,
       not_136_out, not_137_out, not_138_out, not_139_out, not_140_out, not_141_out, not_142_out,
       not_143_out, not_144_out, not_145_out, not_146_out, not_147_out, not_148_out, not_149_out,
       not_150_out, not_151_out, not_152_out, not_153_out, not_154_out, not_155_out, not_156_out,
       not_157_out, not_158_out, not_159_out, not_160_out, not_161_out, not_162_out, not_163_out,
       not_164_out, not_165_out, not_166_out, not_167_out, not_168_out, not_169_out, not_170_out,
       not_171_out, not_172_out, not_173_out, not_174_out, not_175_out, not_176_out, not_177_out,
       not_178_out, not_179_out, not_180_out, not_181_out, not_182_out, not_183_out, not_184_out,
       not_185_out, not_186_out, not_187_out, not_188_out, not_189_out, not_190_out, not_191_out,
       not_192_out, not_193_out, not_194_out, not_195_out, not_196_out, not_197_out, not_198_out,
       not_199_out, not_200_out, not_201_out, not_202_out, not_203_out, not_204_out, not_205_out,
       not_206_out, not_207_out, not_208_out, not_209_out, not_210_out, not_211_out, not_212_out,
       not_213_out, not_214_out, not_215_out, not_216_out, not_217_out, not_218_out, not_219_out,
       not_220_out, not_221_out, not_222_out, not_223_out, not_224_out, not_225_out, not_226_out,
       not_227_out, not_228_out, not_229_out, not_230_out, not_231_out, not_232_out, not_233_out,
       not_234_out, not_235_out, not_236_out, not_237_out, not_238_out, not_239_out, not_240_out,
       not_241_out, not_242_out, not_243_out, not_244_out, not_245_out, not_246_out, not_247_out,
       not_248_out, not_249_out, not_250_out, not_251_out, not_252_out, not_253_out, not_254_out,
       not_255_out, not_256_out, not_257_out, not_258_out, not_259_out, not_260_out, not_261_out,
       not_262_out, not_263_out, not_264_out, not_265_out, not_266_out, not_267_out, not_268_out,
       not_269_out, not_270_out, not_271_out, not_272_out, not_273_out, not_274_out, not_275_out,
       not_276_out, not_277_out, not_278_out, not_279_out, not_280_out, not_281_out, not_282_out,
       not_283_out, not_284_out, not_285_out, not_286_out, not_287_out, not_288_out, not_289_out,
       not_290_out, not_291_out, not_292_out, not_293_out, not_294_out, not_295_out, not_296_out,
       not_297_out, not_298_out, not_299_out, not_300_out, not_301_out, not_302_out, not_303_out,
       not_304_out, not_305_out, not_306_out, not_307_out, not_308_out, not_309_out, not_310_out,
       not_311_out, not_312_out, not_313_out, not_314_out, not_315_out, not_316_out, not_317_out,
       not_318_out, not_319_out, not_320_out, not_321_out, not_322_out, not_323_out, not_324_out,
       not_325_out, not_326_out, not_327_out, not_328_out, not_329_out, not_330_out, not_331_out,
       not_332_out, not_333_out, not_334_out, not_335_out, not_336_out, not_337_out, not_338_out,
       not_339_out, not_340_out, not_341_out, not_342_out, not_343_out, not_344_out, not_345_out,
       not_346_out, not_347_out, not_348_out, not_349_out, not_350_out, not_351_out, not_352_out,
       not_353_out, not_354_out, not_355_out, not_356_out, not_357_out, not_358_out, not_359_out,
       not_360_out, not_361_out, not_362_out, not_363_out, not_364_out, not_365_out, not_366_out,
       not_367_out, not_368_out, not_369_out, not_370_out, not_371_out, not_372_out, not_373_out,
       not_374_out, not_375_out, not_376_out, not_377_out, not_378_out, not_379_out, not_380_out;

  not not_1 (not_1_out, OP4);
  not not_2 (not_2_out, OP3);
  not not_3 (not_3_out, OP2);
  not not_4 (not_4_out, OP4);
  not not_5 (not_5_out, OP3);
  not not_6 (not_6_out, OP2);
  not not_7 (not_7_out, OP1);
  not not_8 (not_8_out, OP4);
  not not_9 (not_9_out, OP2);
  not not_10 (not_10_out, OP5);
  not not_11 (not_11_out, OP4);
  not not_12 (not_12_out, OP2);
  not not_13 (not_13_out, OP1);
  not not_14 (not_14_out, OP0);
  not not_15 (not_15_out, OP5);
  not not_16 (not_16_out, OP4);
  not not_17 (not_17_out, OP1);
  not not_18 (not_18_out, OP0);
  not not_19 (not_19_out, OP5);
  not not_20 (not_20_out, OP4);
  not not_21 (not_21_out, OP2);
  not not_22 (not_22_out, OP1);
  not not_23 (not_23_out, OP5);
  not not_24 (not_24_out, OP4);
  not not_25 (not_25_out, OP2);
  not not_26 (not_26_out, OP0);
  not not_27 (not_27_out, OP5);
  not not_28 (not_28_out, OP4);
  not not_29 (not_29_out, OP1);
  not not_30 (not_30_out, OP4);
  not not_31 (not_31_out, OP3);
  not not_32 (not_32_out, OP2);
  not not_33 (not_33_out, OP4);
  not not_34 (not_34_out, OP2);
  not not_35 (not_35_out, OP5);
  not not_36 (not_36_out, OP4);
  not not_37 (not_37_out, OP4);
  not not_38 (not_38_out, OP3);
  not not_39 (not_39_out, OP1);
  not not_40 (not_40_out, OP0);
  not not_41 (not_41_out, OP5);
  not not_42 (not_42_out, OP4);
  not not_43 (not_43_out, OP0);
  not not_44 (not_44_out, OP4);
  not not_45 (not_45_out, OP3);
  not not_46 (not_46_out, OP2);
  not not_47 (not_47_out, OP1);
  not not_48 (not_48_out, OP5);
  not not_49 (not_49_out, OP4);
  not not_50 (not_50_out, OP3);
  not not_51 (not_51_out, OP2);
  not not_52 (not_52_out, OP1);
  not not_53 (not_53_out, OP0);
  not not_54 (not_54_out, F5);
  not not_55 (not_55_out, F4);
  not not_56 (not_56_out, F3);
  not not_57 (not_57_out, F2);
  not not_58 (not_58_out, F1);
  not not_59 (not_59_out, F0);
  not not_60 (not_60_out, OP5);
  not not_61 (not_61_out, OP4);
  not not_62 (not_62_out, OP3);
  not not_63 (not_63_out, OP2);
  not not_64 (not_64_out, OP1);
  not not_65 (not_65_out, OP0);
  not not_66 (not_66_out, F5);
  not not_67 (not_67_out, F4);
  not not_68 (not_68_out, F3);
  not not_69 (not_69_out, F2);
  not not_70 (not_70_out, OP5);
  not not_71 (not_71_out, OP4);
  not not_72 (not_72_out, OP3);
  not not_73 (not_73_out, OP2);
  not not_74 (not_74_out, OP1);
  not not_75 (not_75_out, OP0);
  not not_76 (not_76_out, F5);
  not not_77 (not_77_out, F4);
  not not_78 (not_78_out, F3);
  not not_79 (not_79_out, F2);
  not not_80 (not_80_out, F0);
  not not_81 (not_81_out, OP5);
  not not_82 (not_82_out, OP4);
  not not_83 (not_83_out, OP3);
  not not_84 (not_84_out, OP2);
  not not_85 (not_85_out, OP1);
  not not_86 (not_86_out, OP0);
  not not_87 (not_87_out, F4);
  not not_88 (not_88_out, F3);
  not not_89 (not_89_out, F2);
  not not_90 (not_90_out, F1);
  not not_91 (not_91_out, F0);
  not not_92 (not_92_out, OP5);
  not not_93 (not_93_out, OP4);
  not not_94 (not_94_out, OP3);
  not not_95 (not_95_out, OP2);
  not not_96 (not_96_out, OP1);
  not not_97 (not_97_out, OP0);
  not not_98 (not_98_out, F4);
  not not_99 (not_99_out, F3);
  not not_100 (not_100_out, F2);
  not not_101 (not_101_out, F1);
  not not_102 (not_102_out, OP5);
  not not_103 (not_103_out, OP4);
  not not_104 (not_104_out, OP3);
  not not_105 (not_105_out, OP2);
  not not_106 (not_106_out, OP1);
  not not_107 (not_107_out, OP0);
  not not_108 (not_108_out, F4);
  not not_109 (not_109_out, F3);
  not not_110 (not_110_out, F2);
  not not_111 (not_111_out, F0);
  not not_112 (not_112_out, OP5);
  not not_113 (not_113_out, OP4);
  not not_114 (not_114_out, OP3);
  not not_115 (not_115_out, OP2);
  not not_116 (not_116_out, OP1);
  not not_117 (not_117_out, OP0);
  not not_118 (not_118_out, F4);
  not not_119 (not_119_out, F3);
  not not_120 (not_120_out, F1);
  not not_121 (not_121_out, F0);
  not not_122 (not_122_out, OP5);
  not not_123 (not_123_out, OP4);
  not not_124 (not_124_out, OP3);
  not not_125 (not_125_out, OP2);
  not not_126 (not_126_out, OP1);
  not not_127 (not_127_out, OP0);
  not not_128 (not_128_out, F4);
  not not_129 (not_129_out, F3);
  not not_130 (not_130_out, F1);
  not not_131 (not_131_out, OP5);
  not not_132 (not_132_out, OP4);
  not not_133 (not_133_out, OP3);
  not not_134 (not_134_out, OP2);
  not not_135 (not_135_out, OP1);
  not not_136 (not_136_out, OP0);
  not not_137 (not_137_out, F4);
  not not_138 (not_138_out, F3);
  not not_139 (not_139_out, OP5);
  not not_140 (not_140_out, OP4);
  not not_141 (not_141_out, OP3);
  not not_142 (not_142_out, OP2);
  not not_143 (not_143_out, OP1);
  not not_144 (not_144_out, OP0);
  not not_145 (not_145_out, F4);
  not not_146 (not_146_out, F2);
  not not_147 (not_147_out, F0);
  not not_148 (not_148_out, OP5);
  not not_149 (not_149_out, OP4);
  not not_150 (not_150_out, OP3);
  not not_151 (not_151_out, OP2);
  not not_152 (not_152_out, OP1);
  not not_153 (not_153_out, OP0);
  not not_154 (not_154_out, F4);
  not not_155 (not_155_out, F2);
  not not_156 (not_156_out, OP5);
  not not_157 (not_157_out, OP4);
  not not_158 (not_158_out, OP3);
  not not_159 (not_159_out, OP2);
  not not_160 (not_160_out, OP5);
  not not_161 (not_161_out, OP4);
  not not_162 (not_162_out, OP2);
  not not_163 (not_163_out, OP1);
  not not_164 (not_164_out, OP0);
  not not_165 (not_165_out, OP5);
  not not_166 (not_166_out, OP4);
  not not_167 (not_167_out, OP1);
  not not_168 (not_168_out, OP0);
  not not_169 (not_169_out, OP5);
  not not_170 (not_170_out, OP4);
  not not_171 (not_171_out, OP2);
  not not_172 (not_172_out, OP1);
  not not_173 (not_173_out, OP5);
  not not_174 (not_174_out, OP4);
  not not_175 (not_175_out, OP2);
  not not_176 (not_176_out, OP0);
  not not_177 (not_177_out, OP5);
  not not_178 (not_178_out, OP4);
  not not_179 (not_179_out, OP1);
  not not_180 (not_180_out, OP4);
  not not_181 (not_181_out, OP3);
  not not_182 (not_182_out, OP2);
  not not_183 (not_183_out, OP5);
  not not_184 (not_184_out, OP4);
  not not_185 (not_185_out, OP3);
  not not_186 (not_186_out, OP2);
  not not_187 (not_187_out, OP1);
  not not_188 (not_188_out, OP0);
  not not_189 (not_189_out, F5);
  not not_190 (not_190_out, F4);
  not not_191 (not_191_out, F3);
  not not_192 (not_192_out, OP5);
  not not_193 (not_193_out, OP4);
  not not_194 (not_194_out, OP0);
  not not_195 (not_195_out, OP4);
  not not_196 (not_196_out, OP3);
  not not_197 (not_197_out, OP2);
  not not_198 (not_198_out, OP1);
  not not_199 (not_199_out, OP5);
  not not_200 (not_200_out, OP4);
  not not_201 (not_201_out, OP3);
  not not_202 (not_202_out, OP2);
  not not_203 (not_203_out, OP1);
  not not_204 (not_204_out, OP0);
  not not_205 (not_205_out, F5);
  not not_206 (not_206_out, F4);
  not not_207 (not_207_out, F1);
  not not_208 (not_208_out, F0);
  not not_209 (not_209_out, OP5);
  not not_210 (not_210_out, OP4);
  not not_211 (not_211_out, OP2);
  not not_212 (not_212_out, OP1);
  not not_213 (not_213_out, OP0);
  not not_214 (not_214_out, OP5);
  not not_215 (not_215_out, OP4);
  not not_216 (not_216_out, OP2);
  not not_217 (not_217_out, OP1);
  not not_218 (not_218_out, OP5);
  not not_219 (not_219_out, OP4);
  not not_220 (not_220_out, OP2);
  not not_221 (not_221_out, OP0);
  not not_222 (not_222_out, OP4);
  not not_223 (not_223_out, OP3);
  not not_224 (not_224_out, OP2);
  not not_225 (not_225_out, OP4);
  not not_226 (not_226_out, OP2);
  not not_227 (not_227_out, OP4);
  not not_228 (not_228_out, OP3);
  not not_229 (not_229_out, OP2);
  not not_230 (not_230_out, OP1);
  not not_231 (not_231_out, OP5);
  not not_232 (not_232_out, OP4);
  not not_233 (not_233_out, OP3);
  not not_234 (not_234_out, OP2);
  not not_235 (not_235_out, OP1);
  not not_236 (not_236_out, OP0);
  not not_237 (not_237_out, F5);
  not not_238 (not_238_out, F4);
  not not_239 (not_239_out, F3);
  not not_240 (not_240_out, F2);
  not not_241 (not_241_out, F1);
  not not_242 (not_242_out, F0);
  not not_243 (not_243_out, OP5);
  not not_244 (not_244_out, OP4);
  not not_245 (not_245_out, OP3);
  not not_246 (not_246_out, OP2);
  not not_247 (not_247_out, OP1);
  not not_248 (not_248_out, OP0);
  not not_249 (not_249_out, F5);
  not not_250 (not_250_out, F4);
  not not_251 (not_251_out, F3);
  not not_252 (not_252_out, F2);
  not not_253 (not_253_out, OP5);
  not not_254 (not_254_out, OP4);
  not not_255 (not_255_out, OP3);
  not not_256 (not_256_out, OP2);
  not not_257 (not_257_out, OP1);
  not not_258 (not_258_out, OP0);
  not not_259 (not_259_out, F5);
  not not_260 (not_260_out, F4);
  not not_261 (not_261_out, F3);
  not not_262 (not_262_out, F2);
  not not_263 (not_263_out, F0);
  not not_264 (not_264_out, OP5);
  not not_265 (not_265_out, OP4);
  not not_266 (not_266_out, OP3);
  not not_267 (not_267_out, OP2);
  not not_268 (not_268_out, OP1);
  not not_269 (not_269_out, OP0);
  not not_270 (not_270_out, F4);
  not not_271 (not_271_out, F3);
  not not_272 (not_272_out, F2);
  not not_273 (not_273_out, F1);
  not not_274 (not_274_out, F0);
  not not_275 (not_275_out, OP5);
  not not_276 (not_276_out, OP4);
  not not_277 (not_277_out, OP3);
  not not_278 (not_278_out, OP2);
  not not_279 (not_279_out, OP1);
  not not_280 (not_280_out, OP0);
  not not_281 (not_281_out, F4);
  not not_282 (not_282_out, F3);
  not not_283 (not_283_out, F2);
  not not_284 (not_284_out, F1);
  not not_285 (not_285_out, OP5);
  not not_286 (not_286_out, OP4);
  not not_287 (not_287_out, OP3);
  not not_288 (not_288_out, OP2);
  not not_289 (not_289_out, OP1);
  not not_290 (not_290_out, OP0);
  not not_291 (not_291_out, F4);
  not not_292 (not_292_out, F3);
  not not_293 (not_293_out, F2);
  not not_294 (not_294_out, F0);
  not not_295 (not_295_out, OP5);
  not not_296 (not_296_out, OP4);
  not not_297 (not_297_out, OP3);
  not not_298 (not_298_out, OP2);
  not not_299 (not_299_out, OP1);
  not not_300 (not_300_out, OP0);
  not not_301 (not_301_out, F4);
  not not_302 (not_302_out, F3);
  not not_303 (not_303_out, F1);
  not not_304 (not_304_out, F0);
  not not_305 (not_305_out, OP5);
  not not_306 (not_306_out, OP4);
  not not_307 (not_307_out, OP3);
  not not_308 (not_308_out, OP2);
  not not_309 (not_309_out, OP1);
  not not_310 (not_310_out, OP0);
  not not_311 (not_311_out, F4);
  not not_312 (not_312_out, F3);
  not not_313 (not_313_out, F1);
  not not_314 (not_314_out, OP5);
  not not_315 (not_315_out, OP4);
  not not_316 (not_316_out, OP3);
  not not_317 (not_317_out, OP2);
  not not_318 (not_318_out, OP1);
  not not_319 (not_319_out, OP0);
  not not_320 (not_320_out, F4);
  not not_321 (not_321_out, F3);
  not not_322 (not_322_out, OP5);
  not not_323 (not_323_out, OP4);
  not not_324 (not_324_out, OP3);
  not not_325 (not_325_out, OP2);
  not not_326 (not_326_out, OP1);
  not not_327 (not_327_out, OP0);
  not not_328 (not_328_out, F4);
  not not_329 (not_329_out, F2);
  not not_330 (not_330_out, F0);
  not not_331 (not_331_out, OP5);
  not not_332 (not_332_out, OP4);
  not not_333 (not_333_out, OP3);
  not not_334 (not_334_out, OP2);
  not not_335 (not_335_out, OP1);
  not not_336 (not_336_out, OP0);
  not not_337 (not_337_out, F4);
  not not_338 (not_338_out, F2);
  not not_339 (not_339_out, OP5);
  not not_340 (not_340_out, OP4);
  not not_341 (not_341_out, OP3);
  not not_342 (not_342_out, OP2);
  not not_343 (not_343_out, OP1);
  not not_344 (not_344_out, OP0);
  not not_345 (not_345_out, F5);
  not not_346 (not_346_out, F4);
  not not_347 (not_347_out, F3);
  not not_348 (not_348_out, OP5);
  not not_349 (not_349_out, OP4);
  not not_350 (not_350_out, OP3);
  not not_351 (not_351_out, OP1);
  not not_352 (not_352_out, OP0);
  not not_353 (not_353_out, OP5);
  not not_354 (not_354_out, OP4);
  not not_355 (not_355_out, OP3);
  not not_356 (not_356_out, OP1);
  not not_357 (not_357_out, OP5);
  not not_358 (not_358_out, OP4);
  not not_359 (not_359_out, OP3);
  not not_360 (not_360_out, OP2);
  not not_361 (not_361_out, OP1);
  not not_362 (not_362_out, OP0);
  not not_363 (not_363_out, F5);
  not not_364 (not_364_out, F4);
  not not_365 (not_365_out, F2);
  not not_366 (not_366_out, F1);
  not not_367 (not_367_out, F0);
  not not_368 (not_368_out, OP5);
  not not_369 (not_369_out, OP4);
  not not_370 (not_370_out, OP3);
  not not_371 (not_371_out, OP2);
  not not_372 (not_372_out, OP0);
  not not_373 (not_373_out, OP5);
  not not_374 (not_374_out, OP4);
  not not_375 (not_375_out, OP3);
  not not_376 (not_376_out, OP2);
  not not_377 (not_377_out, OP5);
  not not_378 (not_378_out, OP4);
  not not_379 (not_379_out, OP3);
  not not_380 (not_380_out, OP2);
  and and_1 (and_1_out, OP5, not_1_out, not_2_out, not_3_out, OP1, OP0);
  and and_2 (and_2_out, OP5, not_4_out, not_5_out, not_6_out, not_7_out, OP0);
  and and_3 (MemWrite, OP5, not_8_out, OP3, not_9_out, OP1, OP0);
  and and_4 (and_4_out, not_10_out, not_11_out, OP3, not_12_out, not_13_out, not_14_out);
  and and_5 (and_5_out, not_15_out, not_16_out, OP3, OP2, not_17_out, not_18_out);
  and and_6 (and_6_out, not_19_out, not_20_out, OP3, not_21_out, not_22_out, OP0);
  and and_7 (and_7_out, not_23_out, not_24_out, OP3, not_25_out, OP1, not_26_out);
  and and_8 (and_8_out, not_27_out, not_28_out, OP3, OP2, not_29_out, OP0);
  and and_9 (and_9_out, OP5, not_30_out, not_31_out, not_32_out, OP1, OP0);
  and and_10 (and_10_out, OP5, not_33_out, OP3, not_34_out, OP1, OP0);
  and and_11 (and_11_out, not_35_out, not_36_out, OP3, OP2, OP1, OP0);
  and and_12 (and_12_out, OP5, not_37_out, not_38_out, OP2, not_39_out, not_40_out);
  and and_13 (and_13_out, not_41_out, not_42_out, OP3, OP2, OP1, not_43_out);
  and and_14 (and_14_out, OP5, not_44_out, not_45_out, not_46_out, not_47_out, OP0);
  and and_15 (and_15_out, not_48_out, not_49_out, not_50_out, not_51_out, not_52_out, not_53_out, not_54_out, not_55_out, not_56_out, not_57_out, not_58_out, not_59_out);
  and and_16 (and_16_out, not_60_out, not_61_out, not_62_out, not_63_out, not_64_out, not_65_out, not_66_out, not_67_out, not_68_out, not_69_out, F1, F0);
  and and_17 (and_17_out, not_70_out, not_71_out, not_72_out, not_73_out, not_74_out, not_75_out, not_76_out, not_77_out, not_78_out, not_79_out, F1, not_80_out);
  and and_18 (and_18_out, not_81_out, not_82_out, not_83_out, not_84_out, not_85_out, not_86_out, F5, not_87_out, not_88_out, not_89_out, not_90_out, not_91_out);
  and and_19 (and_19_out, not_92_out, not_93_out, not_94_out, not_95_out, not_96_out, not_97_out, F5, not_98_out, not_99_out, not_100_out, not_101_out, F0);
  and and_20 (and_20_out, not_102_out, not_103_out, not_104_out, not_105_out, not_106_out, not_107_out, F5, not_108_out, not_109_out, not_110_out, F1, not_111_out);
  and and_21 (and_21_out, not_112_out, not_113_out, not_114_out, not_115_out, not_116_out, not_117_out, F5, not_118_out, not_119_out, F2, not_120_out, not_121_out);
  and and_22 (and_22_out, not_122_out, not_123_out, not_124_out, not_125_out, not_126_out, not_127_out, F5, not_128_out, not_129_out, F2, not_130_out, F0);
  and and_23 (and_23_out, not_131_out, not_132_out, not_133_out, not_134_out, not_135_out, not_136_out, F5, not_137_out, not_138_out, F2, F1, F0);
  and and_24 (and_24_out, not_139_out, not_140_out, not_141_out, not_142_out, not_143_out, not_144_out, F5, not_145_out, F3, not_146_out, F1, not_147_out);
  and and_25 (and_25_out, not_148_out, not_149_out, not_150_out, not_151_out, not_152_out, not_153_out, F5, not_154_out, F3, not_155_out, F1, F0);
  and and_26 (and_26_out, not_156_out, not_157_out, not_158_out, not_159_out, OP1, OP0);
  and and_27 (and_27_out, not_160_out, not_161_out, OP3, not_162_out, not_163_out, not_164_out);
  and and_28 (and_28_out, not_165_out, not_166_out, OP3, OP2, not_167_out, not_168_out);
  and and_29 (and_29_out, not_169_out, not_170_out, OP3, not_171_out, not_172_out, OP0);
  and and_30 (and_30_out, not_173_out, not_174_out, OP3, not_175_out, OP1, not_176_out);
  and and_31 (and_31_out, not_177_out, not_178_out, OP3, OP2, not_179_out, OP0);
  and and_32 (and_32_out, OP5, not_180_out, not_181_out, not_182_out, OP1, OP0);
  and and_33 (and_33_out, not_183_out, not_184_out, not_185_out, not_186_out, not_187_out, not_188_out, not_189_out, not_190_out, not_191_out, F2, F1, F0);
  and and_34 (and_34_out, not_192_out, not_193_out, OP3, OP2, OP1, not_194_out);
  and and_35 (and_35_out, OP5, not_195_out, not_196_out, not_197_out, not_198_out, OP0);
  and and_36 (SysCALL, not_199_out, not_200_out, not_201_out, not_202_out, not_203_out, not_204_out, not_205_out, not_206_out, F3, F2, not_207_out, not_208_out);
  and and_37 (and_37_out, not_209_out, not_210_out, OP3, not_211_out, not_212_out, not_213_out);
  and and_38 (and_38_out, not_214_out, not_215_out, OP3, not_216_out, not_217_out, OP0);
  and and_39 (and_39_out, not_218_out, not_219_out, OP3, not_220_out, OP1, not_221_out);
  and and_40 (and_40_out, OP5, not_222_out, not_223_out, not_224_out, OP1, OP0);
  and and_41 (and_41_out, OP5, not_225_out, OP3, not_226_out, OP1, OP0);
  and and_42 (and_42_out, OP5, not_227_out, not_228_out, not_229_out, not_230_out, OP0);
  and and_43 (and_43_out, not_231_out, not_232_out, not_233_out, not_234_out, not_235_out, not_236_out, not_237_out, not_238_out, not_239_out, not_240_out, not_241_out, not_242_out);
  and and_44 (and_44_out, not_243_out, not_244_out, not_245_out, not_246_out, not_247_out, not_248_out, not_249_out, not_250_out, not_251_out, not_252_out, F1, F0);
  and and_45 (and_45_out, not_253_out, not_254_out, not_255_out, not_256_out, not_257_out, not_258_out, not_259_out, not_260_out, not_261_out, not_262_out, F1, not_263_out);
  and and_46 (and_46_out, not_264_out, not_265_out, not_266_out, not_267_out, not_268_out, not_269_out, F5, not_270_out, not_271_out, not_272_out, not_273_out, not_274_out);
  and and_47 (and_47_out, not_275_out, not_276_out, not_277_out, not_278_out, not_279_out, not_280_out, F5, not_281_out, not_282_out, not_283_out, not_284_out, F0);
  and and_48 (and_48_out, not_285_out, not_286_out, not_287_out, not_288_out, not_289_out, not_290_out, F5, not_291_out, not_292_out, not_293_out, F1, not_294_out);
  and and_49 (and_49_out, not_295_out, not_296_out, not_297_out, not_298_out, not_299_out, not_300_out, F5, not_301_out, not_302_out, F2, not_303_out, not_304_out);
  and and_50 (and_50_out, not_305_out, not_306_out, not_307_out, not_308_out, not_309_out, not_310_out, F5, not_311_out, not_312_out, F2, not_313_out, F0);
  and and_51 (and_51_out, not_314_out, not_315_out, not_316_out, not_317_out, not_318_out, not_319_out, F5, not_320_out, not_321_out, F2, F1, F0);
  and and_52 (and_52_out, not_322_out, not_323_out, not_324_out, not_325_out, not_326_out, not_327_out, F5, not_328_out, F3, not_329_out, F1, not_330_out);
  and and_53 (and_53_out, not_331_out, not_332_out, not_333_out, not_334_out, not_335_out, not_336_out, F5, not_337_out, F3, not_338_out, F1, F0);
  and and_54 (and_54_out, not_339_out, not_340_out, not_341_out, not_342_out, not_343_out, not_344_out, not_345_out, not_346_out, not_347_out, F2, F1, F0);
  and and_55 (BEQ, not_348_out, not_349_out, not_350_out, OP2, not_351_out, not_352_out);
  and and_56 (BNE, not_353_out, not_354_out, not_355_out, OP2, not_356_out, OP0);
  and and_57 (JR, not_357_out, not_358_out, not_359_out, not_360_out, not_361_out, not_362_out, not_363_out, not_364_out, F3, not_365_out, not_366_out, not_367_out);
  and and_58 (and_58_out, not_368_out, not_369_out, not_370_out, not_371_out, OP1, not_372_out);
  and and_59 (and_59_out, not_373_out, not_374_out, not_375_out, not_376_out, OP1, OP0);
  and and_60 (JAL, not_377_out, not_378_out, not_379_out, not_380_out, OP1, OP0);
  or or_1 (MemToReg, and_1_out, and_2_out);
  or or_2 (ALU_SRC, and_4_out, and_5_out, and_6_out, and_7_out, and_8_out, and_9_out, and_10_out, and_11_out, and_12_out, and_13_out, and_14_out);
  or or_3 (SignedExt, and_37_out, and_38_out, and_39_out, and_40_out, and_41_out, and_42_out);
  or or_4 (JMP, and_58_out, and_59_out);
  or or_5 (RegWrite, and_15_out, and_16_out, and_17_out, and_18_out, and_19_out, and_20_out, and_21_out, and_22_out, and_23_out, and_24_out, and_25_out, and_26_out, and_27_out, and_28_out, and_29_out, and_30_out, and_31_out, and_32_out, and_33_out, and_34_out, and_35_out);
  or or_6 (RegDst, and_43_out, and_44_out, and_45_out, and_46_out, and_47_out, and_48_out, and_49_out, and_50_out, and_51_out, and_52_out, and_53_out, and_54_out);
endmodule

// CCMB和中断控制信号
module \CCMB和中断控制信号  (
  input  OP0,
  input  OP1,
  input  OP2,
  input  OP3,
  input  OP4,
  input  OP5,
  input  F0,
  input  F1,
  input  F2,
  input  F3,
  input  F4,
  input  F5,
  output SRAV,
  output LH,
  output BLTZ,
  output ERET
);

  wire comparator_1_eq, comparator_2_eq, not_1_out, not_2_out, not_3_out, not_4_out, not_5_out, not_6_out,
       not_7_out, not_8_out, not_9_out, not_10_out, not_11_out, not_12_out, not_13_out, not_14_out,
       not_15_out, not_16_out, not_17_out, not_18_out;

  not not_1 (not_1_out, OP5);
  not not_2 (not_2_out, OP4);
  not not_3 (not_3_out, OP3);
  not not_4 (not_4_out, OP2);
  not not_5 (not_5_out, OP1);
  not not_6 (not_6_out, OP0);
  not not_7 (not_7_out, F5);
  not not_8 (not_8_out, F4);
  not not_9 (not_9_out, F3);
  not not_10 (not_10_out, OP4);
  not not_11 (not_11_out, OP3);
  not not_12 (not_12_out, OP2);
  not not_13 (not_13_out, OP1);
  not not_14 (not_14_out, OP5);
  not not_15 (not_15_out, OP4);
  not not_16 (not_16_out, OP3);
  not not_17 (not_17_out, OP2);
  not not_18 (not_18_out, OP1);
  and and_1 (SRAV, not_1_out, not_2_out, not_3_out, not_4_out, not_5_out, not_6_out, not_7_out, not_8_out, not_9_out, F2, F1, F0);
  and and_2 (LH, OP5, not_10_out, not_11_out, not_12_out, not_13_out, OP0);
  and and_3 (BLTZ, not_14_out, not_15_out, not_16_out, not_17_out, not_18_out, OP0);
  Comparator #(.width(6)) comparator_1 (
    .a(6'b010000), .b({OP5, OP4, OP3, OP2, OP1, OP0}), .eq(comparator_1_eq));  // open: gt, lt
  and and_4 (ERET, comparator_1_eq, comparator_2_eq);
  Comparator #(.width(6)) comparator_2 (
    .a(6'b011000), .b({F5, F4, F3, F2, F1, F0}), .eq(comparator_2_eq));  // open: gt, lt
endmodule

// ALU
module MIPS_ALU (
  input  [4:0] shamt,
  input  [31:0] X,
  input  [31:0] Y,
  input  [3:0] AluOP,
  output Equal,
  output [31:0] Result,
  output [31:0] Result_2
);

  wire [0:0] comparator_1_lt, comparator_2_lt;
  wire [31:0] adder_1_out, AND_out, divider_1_out, divider_1_rem, multiplier_1_cout, multiplier_1_out,
       NOR_out, OR_out, shifter_1_out, shifter_2_out, shifter_3_out, subtractor_1_out, XOR_out;

  assign AND_out = X & Y;  // AND_Gate AND, 32 bits wide
  assign OR_out = X | Y;  // OR_Gate OR, 32 bits wide
  Shifter #(.width(32)) shifter_1 (.in(Y), .\dist (shamt), .out(shifter_1_out));
  Shifter #(.width(32), .shift("ar")) shifter_2 (.in(Y), .\dist (shamt), .out(shifter_2_out));
  Shifter #(.width(32), .shift("lr")) shifter_3 (.in(Y), .\dist (shamt), .out(shifter_3_out));
  Multiplier #(.width(32)) multiplier_1 (.a(X), .b(Y), .out(multiplier_1_out), .cout(multiplier_1_cout));  // open: cin
  Divider #(.width(32)) divider_1 (.a(X), .b(Y), .out(divider_1_out), .rem(divider_1_rem));  // open: upper
  Adder #(.width(32)) adder_1 (.a(X), .b(Y), .out(adder_1_out));  // open: cin, cout
  Subtractor #(.width(32)) subtractor_1 (.a(X), .b(Y), .out(subtractor_1_out));  // open: bin, bout
  assign XOR_out = X ^ Y;  // XOR_Gate XOR, 32 bits wide
  assign NOR_out = ~(X | Y);  // NOR_Gate NOR, 32 bits wide
  Comparator #(.width(32)) comparator_1 (.a(X), .b(Y), .eq(Equal), .lt(comparator_1_lt[0]));  // open: gt
  Comparator #(.width(32), .mode("unsigned")) comparator_2 (.a(X), .b(Y), .lt(comparator_2_lt[0]));  // open: gt, eq
  Multiplexer #(.select(4), .width(32), .enable("false")) multiplexer_1 (
    .in0(shifter_1_out), .in1(shifter_2_out), .in2(shifter_3_out), .in3(multiplier_1_out),
    .in4(divider_1_out), .in5(adder_1_out), .in6(subtractor_1_out), .in7(AND_out), .in8(OR_out),
    .in9(XOR_out), .in10(NOR_out), .in11({{31{1'b0}}, comparator_1_lt[0]}),
    .in12({{31{1'b0}}, comparator_2_lt[0]}), .in13({32{1'b0}}), .in14({32{1'b0}}), .in15({32{1'b0}}),
    .out(Result), .sel(AluOP));
  Multiplexer #(.select(4), .width(32), .enable("false")) multiplexer_2 (
    .in0({32{1'b0}}), .in1({32{1'b0}}), .in2({32{1'b0}}), .in3(multiplier_1_cout), .in4(divider_1_rem),
    .in5({32{1'b0}}), .in6({32{1'b0}}), .in7({32{1'b0}}), .in8({32{1'b0}}), .in9({32{1'b0}}),
    .in10({32{1'b0}}), .in11({32{1'b0}}), .in12({32{1'b0}}), .in13({32{1'b0}}), .in14({32{1'b0}}),
    .in15({32{1'b0}}), .out(Result_2), .sel(AluOP));

  // Other names for the same wires on the sheet: Result2[31:0] = Result_2; S[3:0] = AluOP

  // Notes on the sheet:
  //   不要改变此引脚区域内容，也不要改变ALU封装形式
  //   输入引脚
  //   输出引脚
endmodule

module MIPS_Regifile (
  input  [31:0] Din,
  input  Clk,
  input  WE,
  input  [4:0] R1_num,
  input  [4:0] W_num,
  input  [4:0] R2_num,
  output [31:0] R1,
  output [31:0] R2
);

  // RegisterFile registerfile_1: pin names not known; wires that end beside it: Din, Clk, WE, W_num, R1_num, R2_num, R1, R2
endmodule

module \理想流水线  (
);

  wire CLK, ex_mem_1_memwrite_2, ex_mem_1_syscall_2, Go, halt, IR1, IR2, IR3, mem_wb_1_syscall_2, MemToReg,
       MemToReg_1, MemToReg_2, MemWrite, MemWrite_1, or_1_out, RegDst, RegDst_1, RegDst_2, RegDst_r,
       register_2_q, RegWrite, RegWrite_1, RegWrite_2, RST, SignedExt, Sys, Sys_1, W1, W2, W3, WE,
       \硬布线控制器_1_alu_src ;
  wire [3:0] ALUOP, ALUOP_1;
  wire [4:0] multiplexer_1_out, multiplexer_3_out, multiplexer_4_out, rd, rt, shamt_1;
  wire [15:0] \LoadUse次数 , \总周期数 , \插入气泡数 , \无条件分支数 , \条件分支成功数 ;
  wire [31:0] B_1, bit_extender_1_out, bit_extender_2_out, ex_mem_1_a_2, ex_mem_1_alu_2, ex_mem_1_b_2,
       ex_mem_1_ir_2, EX_PC, id_ex_1_a_2, id_ex_1_b_2, id_ex_1_ir_2, ID_PC, IF_PC, IR, LedData, MEM_PC,
       mem_wb_1_a_2, mem_wb_1_ir_2, mem_wb_1_md_2, mips_alu_1_result, mips_regifile_1_r1, mips_regifile_1_r2,
       multiplexer_2_out, multiplexer_5_out, multiplexer_6_out, PC_q, ram_1_data, rom_1_data, WB_PC;

  Button \u_总复位  (.out(RST));
  Button _1 (.out(IR1));
  Button _2 (.out(IR2));
  Button _3 (.out(IR3));
  Button \u_继续运行  (.out(Go));
  LED led_1 (.in(W1));
  LED led_2 (.in(W2));
  LED led_3 (.in(W3));
  Register #(.width(32)) PC (.D(IF_PC), .en(halt), .Q(PC_q), .clk(CLK), .clr(RST));
  Hex_Digit_Display hex_digit_display_1 (.value(LedData[31:28]));  // open: dp
  Hex_Digit_Display hex_digit_display_2 (.value(LedData[23:20]));  // open: dp
  Hex_Digit_Display hex_digit_display_3 (.value(LedData[27:24]));  // open: dp
  ROM #(.addrWidth(10), .dataWidth(32)) rom_1 (.addr(PC_q[11:2]), .data(rom_1_data));  // open: sel
  Adder #(.width(32)) adder_1 (.a(PC_q), .b(32'h4), .out(IF_PC));  // open: cin, cout
  Hex_Digit_Display hex_digit_display_4 (.value(LedData[19:16]));  // open: dp
  Hex_Digit_Display hex_digit_display_5 (.value(LedData[15:12]));  // open: dp
  IF_ID if_id_1 (
    .IR(rom_1_data), .IR_2(IR), .clk(CLK), .halt(halt), .rst(RST), .PC(IF_PC), .PC_2(ID_PC));  // open: 预测跳转, 预测跳转_2, 预测地址, 预测地址_2, Hit, Hit_2, HitPos, HitPos_2
  Hex_Digit_Display hex_digit_display_6 (.value(LedData[11:8]));  // open: dp
  Hex_Digit_Display hex_digit_display_7 (.value(LedData[7:4]));  // open: dp
  Clock clock_1 (.out(CLK));
  Hex_Digit_Display hex_digit_display_8 (.value(LedData[3:0]));  // open: dp
  assign bit_extender_1_out = {{16{1'b0}}, IR[15:0]};  // Bit_Extender bit_extender_1
  assign bit_extender_2_out = {{16{IR[15]}}, IR[15:0]};  // Bit_Extender bit_extender_2
  \硬布线控制器  \u_硬布线控制器_1  (
    .Func(IR[5:0]), .OP(IR[31:26]), .ALU_OP(ALUOP), .MemToReg(MemToReg), .MemWrite(MemWrite),
    .ALU_SRC(\硬布线控制器_1_alu_src ), .RegWrite(RegWrite), .SysCALL(Sys), .SignedExt(SignedExt), .RegDst(RegDst));  // open: JR, JMP, Beq, JAL, Bne, SRAV, LH, BLTZ, ERET
  Multiplexer #(.width(5), .enable("false")) multiplexer_1 (
    .in0(IR[25:21]), .in1(5'b00100), .out(multiplexer_1_out), .sel(Sys));
  Multiplexer #(.width(32), .enable("false")) multiplexer_2 (
    .in0(bit_extender_1_out), .in1(bit_extender_2_out), .out(multiplexer_2_out), .sel(SignedExt));
  // Probe on \总周期数 
  // Probe on \无条件分支数 
  // Probe on \条件分支成功数 
  // Probe on \插入气泡数 
  // Probe on \LoadUse次数 
  Multiplexer #(.width(5), .enable("false")) multiplexer_3 (
    .in0(IR[20:16]), .in1(5'b00010), .out(multiplexer_3_out), .sel(Sys));
  Multiplexer #(.width(5), .enable("false")) multiplexer_4 (
    .in0(rt), .in1(rd), .out(multiplexer_4_out), .sel(RegDst_r));
  // Probe on IF_PC[11:0]
  // Probe on ID_PC[11:0]
  Counter #(.width(16), .max('hffff)) counter_1 (
    .count(halt), .Q(\总周期数 ), .clk(CLK), .clr(RST));  // open: load, D, carry
  MIPS_Regifile mips_regifile_1 (
    .Din(mem_wb_1_md_2), .Clk(CLK), .R1(mips_regifile_1_r1), .R2(mips_regifile_1_r2), .WE(WE),
    .W_num(multiplexer_4_out), .R1_num(multiplexer_1_out), .R2_num(multiplexer_3_out));
  Multiplexer #(.width(32), .enable("false")) multiplexer_5 (
    .in0(mips_regifile_1_r2), .in1(multiplexer_2_out), .out(multiplexer_5_out), .sel(\硬布线控制器_1_alu_src ));
  // Probe on EX_PC[11:0]
  // Probe on MEM_PC[11:0]
  // Probe on WB_PC[11:0]
  ID_EX id_ex_1 (
    .IR(IR), .PC(ID_PC), .A(mips_regifile_1_r1), .B(multiplexer_5_out), .Shamt(IR[10:6]),
    .MemToReg(MemToReg), .MemWrite(MemWrite), .ALUOP(ALUOP), .RegWrite(RegWrite), .RegDst(RegDst),
    .R2(mips_regifile_1_r2), .Syscall(Sys), .IR_2(id_ex_1_ir_2), .PC_2(EX_PC), .A_2(id_ex_1_a_2),
    .B_2(id_ex_1_b_2), .Shamt_2(shamt_1), .MemToReg_2(MemToReg_1), .MemWrite_2(MemWrite_1),
    .ALUOP_2(ALUOP_1), .RegWrite_2(RegWrite_1), .RegDst_2(RegDst_1), .R2_2(B_1), .Syscall_2(Sys_1),
    .clk(CLK), .halt(halt), .rst(RST));  // open: Beq, Beq_2, Bne, Bne_2, Jal, Jal_2, JMP, JMP_2, JR, JR_2, Addr_有, Addr_有_2, Addr_26, Addr_26_2, SRAV, SRAV_2, LH, LH_2, BLTZ, BLTZ_2, ALU_SRC, ALU_SRC_2, IMM, IMM_2, 预测跳转, 预测跳转_2, 预测地址, 预测地址_2, Hit, Hit_2, HitPos, HitPos_2, ERET, ERET_2
  MIPS_ALU mips_alu_1 (
    .X(id_ex_1_a_2), .Y(id_ex_1_b_2), .AluOP(ALUOP_1), .Result(mips_alu_1_result), .shamt(shamt_1));  // open: Equal, Result_2
  EX_MEM ex_mem_1 (
    .IR(id_ex_1_ir_2), .PC(EX_PC), .Alu(mips_alu_1_result), .A(id_ex_1_a_2), .B(B_1), .MemToReg(MemToReg_1),
    .MemWrite(MemWrite_1), .RegWrite(RegWrite_1), .RegDst(RegDst_1), .Syscall(Sys_1), .IR_2(ex_mem_1_ir_2),
    .PC_2(MEM_PC), .Alu_2(ex_mem_1_alu_2), .A_2(ex_mem_1_a_2), .B_2(ex_mem_1_b_2), .MemToReg_2(MemToReg_2),
    .MemWrite_2(ex_mem_1_memwrite_2), .RegWrite_2(RegWrite_2), .RegDst_2(RegDst_2),
    .Syscall_2(ex_mem_1_syscall_2), .clk(CLK), .halt(halt), .rst(RST));  // open: Jal, Jal_2, Addr_26, Addr_26_2, LH, LH_2
  Multiplexer #(.width(32), .enable("false")) multiplexer_6 (
    .in0(ex_mem_1_alu_2), .in1(ram_1_data), .out(multiplexer_6_out), .sel(MemToReg_2));
  RAM #(.addrWidth(10), .dataWidth(32), .bus("separate")) ram_1 (
    .addr(ex_mem_1_alu_2[11:2]), .din(ex_mem_1_b_2), .data(ram_1_data), .str(ex_mem_1_memwrite_2),
    .sel(1'b1), .clk(CLK), .ld(MemToReg_2));  // open: clr
  MEM_WB mem_wb_1 (
    .IR(ex_mem_1_ir_2), .PC(MEM_PC), .A(ex_mem_1_a_2), .MD(multiplexer_6_out), .RegWrite(RegWrite_2),
    .RegDst(RegDst_2), .Syscall(ex_mem_1_syscall_2),
    .IR_2({mem_wb_1_ir_2[31:21], rt, rd, mem_wb_1_ir_2[10:0]}), .PC_2(WB_PC), .A_2(mem_wb_1_a_2),
    .MD_2(mem_wb_1_md_2), .RegWrite_2(WE), .RegDst_2(RegDst_r), .Syscall_2(mem_wb_1_syscall_2), .clk(CLK),
    .halt(halt), .rst(RST));  // open: Jal, Jal_2, Addr_26, Addr_26_2, B, B_2
  Register #(.width(32)) register_1 (.D(mem_wb_1_a_2), .en(mem_wb_1_syscall_2), .Q(LedData), .clk(CLK));  // open: clr
  Register #(.width(1)) register_2 (
    .D(mem_wb_1_syscall_2), .en(mem_wb_1_syscall_2), .Q(register_2_q), .clk(CLK), .clr(or_1_out));
  or or_1 (or_1_out, RST, Go);
  not not_1 (halt, register_2_q);

  // Other names for the same wires on the sheet: shamt[4:0] = IR[10:6]; PC[31:0] = ID_PC

  // Notes on the sheet:
  //   中断源
  //   中断等待指示
  //   指令存储器
  //   contents of rom_1 (hex, n*v repeats v):
  //   20100000 20110001 20120002 20130003 36100000 36310001 36520002 36730003 ae100000 ae110004 ae120008
  //   ae13000c 2002000a 0 0 0 c
  //   数码管输出
  //   Shamt
  //   OP
  //   Func
  //   rs
  //   rt
  //   Imm
  //   流水调试日志用
  //   rd
  //   rt
endmodule

// 源寄存器使用情况
module \源寄存器使用情况  (
  input  OP0,
  input  OP1,
  input  OP2,
  input  OP3,
  input  OP4,
  input  OP5,
  input  F0,
  input  F1,
  input  F2,
  input  F3,
  input  F4,
  input  F5,
  output R1_Used,
  output R2_Used
);

  wire and_1_out, and_2_out, and_3_out, and_4_out, and_5_out, and_6_out, and_7_out, and_8_out, and_9_out,
       and_10_out, and_11_out, and_12_out, and_13_out, and_14_out, and_15_out, and_16_out, and_17_out,
       and_18_out, and_19_out, and_20_out, and_21_out, and_22_out, and_23_out, and_24_out, and_25_out,
       and_26_out, and_27_out, and_28_out, and_29_out, and_30_out, and_31_out, and_32_out, and_33_out,
       and_34_out, and_35_out, and_36_out, and_37_out, and_38_out, and_39_out, and_40_out, and_41_out,
       and_42_out, not_1_out, not_2_out, not_3_out, not_4_out, not_5_out, not_6_out, not_7_out, not_8_out,
       not_9_out, not_10_out, not_11_out, not_12_out, not_13_out, not_14_out, not_15_out, not_16_out,
       not_17_out, not_18_out, not_19_out, not_20_out, not_21_out, not_22_out, not_23_out, not_24_out,
       not_25_out, not_26_out, not_27_out, not_28_out, not_29_out, not_30_out, not_31_out, not_32_out,
       not_33_out, not_34_out, not_35_out, not_36_out, not_37_out, not_38_out, not_39_out, not_40_out,
       not_41_out, not_42_out, not_43_out, not_44_out, not_45_out, not_46_out, not_47_out, not_48_out,
       not_49_out, not_50_out, not_51_out, not_52_out, not_53_out, not_54_out, not_55_out, not_56_out,
       not_57_out, not_58_out, not_59_out, not_60_out, not_61_out, not_62_out, not_63_out, not_64_out,
       not_65_out, not_66_out, not_67_out, not_68_out, not_69_out, not_70_out, not_71_out, not_72_out,
       not_73_out, not_74_out, not_75_out, not_76_out, not_77_out, not_78_out, not_79_out, not_80_out,
       not_81_out, not_82_out, not_83_out, not_84_out, not_85_out, not_86_out, not_87_out, not_88_out,
       not_89_out, not_90_out, not_91_out, not_92_out, not_93_out, not_94_out, not_95_out, not_96_out,
       not_97_out, not_98_out, not_99_out, not_100_out, not_101_out, not_102_out, not_103_out, not_104_out,
       not_105_out, not_106_out, not_107_out, not_108_out, not_109_out, not_110_out, not_111_out,
       not_112_out, not_113_out, not_114_out, not_115_out, not_116_out, not_117_out, not_118_out,
       not_119_out, not_120_out, not_121_out, not_122_out, not_123_out, not_124_out, not_125_out,
       not_126_out, not_127_out, not_128_out, not_129_out, not_130_out, not_131_out, not_132_out,
       not_133_out, not_134_out, not_135_out, not_136_out, not_137_out, not_138_out, not_139_out,
       not_140_out, not_141_out, not_142_out, not_143_out, not_144_out, not_145_out, not_146_out,
       not_147_out, not_148_out, not_149_out, not_150_out, not_151_out, not_152_out, not_153_out,
       not_154_out, not_155_out, not_156_out, not_157_out, not_158_out, not_159_out, not_160_out,
       not_161_out, not_162_out, not_163_out, not_164_out, not_165_out, not_166_out, not_167_out,
       not_168_out, not_169_out, not_170_out, not_171_out, not_172_out, not_173_out, not_174_out,
       not_175_out, not_176_out, not_177_out, not_178_out, not_179_out, not_180_out, not_181_out,
       not_182_out, not_183_out, not_184_out, not_185_out, not_186_out, not_187_out, not_188_out,
       not_189_out, not_190_out, not_191_out, not_192_out, not_193_out, not_194_out, not_195_out,
       not_196_out, not_197_out, not_198_out, not_199_out, not_200_out, not_201_out, not_202_out,
       not_203_out, not_204_out, not_205_out, not_206_out, not_207_out, not_208_out, not_209_out,
       not_210_out, not_211_out, not_212_out, not_213_out, not_214_out, not_215_out, not_216_out,
       not_217_out, not_218_out, not_219_out, not_220_out, not_221_out, not_222_out, not_223_out,
       not_224_out, not_225_out, not_226_out, not_227_out, not_228_out, not_229_out, not_230_out,
       not_231_out, not_232_out, not_233_out, not_234_out, not_235_out, not_236_out, not_237_out,
       not_238_out, not_239_out, not_240_out, not_241_out, not_242_out, not_243_out, not_244_out,
       not_245_out, not_246_out, not_247_out, not_248_out, not_249_out, not_250_out, not_251_out,
       not_252_out, not_253_out, not_254_out, not_255_out, not_256_out, not_257_out, not_258_out,
       not_259_out, not_260_out, not_261_out, not_262_out, not_263_out, not_264_out, not_265_out,
       not_266_out, not_267_out, not_268_out, not_269_out, not_270_out, not_271_out, not_272_out,
       not_273_out, not_274_out, not_275_out, not_276_out, not_277_out, not_278_out, not_279_out,
       not_280_out, not_281_out, not_282_out, not_283_out, not_284_out, not_285_out, not_286_out,
       not_287_out, not_288_out, not_289_out, not_290_out, not_291_out, not_292_out, not_293_out,
       not_294_out, not_295_out, not_296_out, not_297_out, not_298_out, not_299_out, not_300_out,
       not_301_out, not_302_out, not_303_out, not_304_out, not_305_out, not_306_out, not_307_out,
       not_308_out, not_309_out, not_310_out, not_311_out, not_312_out, not_313_out, not_314_out,
       not_315_out, not_316_out, not_317_out, not_318_out, not_319_out, not_320_out, not_321_out, not_322_out;

  not not_1 (not_1_out, OP5);
  not not_2 (not_2_out, OP4);
  not not_3 (not_3_out, OP3);
  not not_4 (not_4_out, OP2);
  not not_5 (not_5_out, OP1);
  not not_6 (not_6_out, OP0);
  not not_7 (not_7_out, F5);
  not not_8 (not_8_out, F4);
  not not_9 (not_9_out, F3);
  not not_10 (not_10_out, F2);
  not not_11 (not_11_out, F1);
  not not_12 (not_12_out, F0);
  not not_13 (not_13_out, OP5);
  not not_14 (not_14_out, OP4);
  not not_15 (not_15_out, OP3);
  not not_16 (not_16_out, OP2);
  not not_17 (not_17_out, OP1);
  not not_18 (not_18_out, OP0);
  not not_19 (not_19_out, F5);
  not not_20 (not_20_out, F4);
  not not_21 (not_21_out, F3);
  not not_22 (not_22_out, F2);
  not not_23 (not_23_out, OP5);
  not not_24 (not_24_out, OP4);
  not not_25 (not_25_out, OP3);
  not not_26 (not_26_out, OP2);
  not not_27 (not_27_out, OP1);
  not not_28 (not_28_out, OP0);
  not not_29 (not_29_out, F5);
  not not_30 (not_30_out, F4);
  not not_31 (not_31_out, F3);
  not not_32 (not_32_out, F2);
  not not_33 (not_33_out, F0);
  not not_34 (not_34_out, OP5);
  not not_35 (not_35_out, OP4);
  not not_36 (not_36_out, OP3);
  not not_37 (not_37_out, OP2);
  not not_38 (not_38_out, OP1);
  not not_39 (not_39_out, OP0);
  not not_40 (not_40_out, F4);
  not not_41 (not_41_out, F3);
  not not_42 (not_42_out, F2);
  not not_43 (not_43_out, F1);
  not not_44 (not_44_out, F0);
  not not_45 (not_45_out, OP5);
  not not_46 (not_46_out, OP4);
  not not_47 (not_47_out, OP3);
  not not_48 (not_48_out, OP2);
  not not_49 (not_49_out, OP1);
  not not_50 (not_50_out, OP0);
  not not_51 (not_51_out, F4);
  not not_52 (not_52_out, F3);
  not not_53 (not_53_out, F2);
  not not_54 (not_54_out, F1);
  not not_55 (not_55_out, OP5);
  not not_56 (not_56_out, OP4);
  not not_57 (not_57_out, OP3);
  not not_58 (not_58_out, OP2);
  not not_59 (not_59_out, OP1);
  not not_60 (not_60_out, OP0);
  not not_61 (not_61_out, F4);
  not not_62 (not_62_out, F3);
  not not_63 (not_63_out, F2);
  not not_64 (not_64_out, F0);
  not not_65 (not_65_out, OP5);
  not not_66 (not_66_out, OP4);
  not not_67 (not_67_out, OP3);
  not not_68 (not_68_out, OP2);
  not not_69 (not_69_out, OP1);
  not not_70 (not_70_out, OP0);
  not not_71 (not_71_out, F4);
  not not_72 (not_72_out, F3);
  not not_73 (not_73_out, F1);
  not not_74 (not_74_out, F0);
  not not_75 (not_75_out, OP5);
  not not_76 (not_76_out, OP4);
  not not_77 (not_77_out, OP3);
  not not_78 (not_78_out, OP2);
  not not_79 (not_79_out, OP1);
  not not_80 (not_80_out, OP0);
  not not_81 (not_81_out, F4);
  not not_82 (not_82_out, F3);
  not not_83 (not_83_out, F1);
  not not_84 (not_84_out, OP5);
  not not_85 (not_85_out, OP4);
  not not_86 (not_86_out, OP3);
  not not_87 (not_87_out, OP2);
  not not_88 (not_88_out, OP1);
  not not_89 (not_89_out, OP0);
  not not_90 (not_90_out, F4);
  not not_91 (not_91_out, F3);
  not not_92 (not_92_out, OP5);
  not not_93 (not_93_out, OP4);
  not not_94 (not_94_out, OP3);
  not not_95 (not_95_out, OP2);
  not not_96 (not_96_out, OP1);
  not not_97 (not_97_out, OP0);
  not not_98 (not_98_out, F4);
  not not_99 (not_99_out, F2);
  not not_100 (not_100_out, F0);
  not not_101 (not_101_out, OP5);
  not not_102 (not_102_out, OP4);
  not not_103 (not_103_out, OP3);
  not not_104 (not_104_out, OP2);
  not not_105 (not_105_out, OP1);
  not not_106 (not_106_out, OP0);
  not not_107 (not_107_out, F4);
  not not_108 (not_108_out, F2);
  not not_109 (not_109_out, OP5);
  not not_110 (not_110_out, OP4);
  not not_111 (not_111_out, OP3);
  not not_112 (not_112_out, OP2);
  not not_113 (not_113_out, OP1);
  not not_114 (not_114_out, OP0);
  not not_115 (not_115_out, F5);
  not not_116 (not_116_out, F4);
  not not_117 (not_117_out, F2);
  not not_118 (not_118_out, F1);
  not not_119 (not_119_out, F0);
  not not_120 (not_120_out, OP5);
  not not_121 (not_121_out, OP4);
  not not_122 (not_122_out, OP3);
  not not_123 (not_123_out, OP2);
  not not_124 (not_124_out, OP1);
  not not_125 (not_125_out, OP0);
  not not_126 (not_126_out, F5);
  not not_127 (not_127_out, F4);
  not not_128 (not_128_out, F1);
  not not_129 (not_129_out, F0);
  not not_130 (not_130_out, OP5);
  not not_131 (not_131_out, OP4);
  not not_132 (not_132_out, OP3);
  not not_133 (not_133_out, OP1);
  not not_134 (not_134_out, OP0);
  not not_135 (not_135_out, OP5);
  not not_136 (not_136_out, OP4);
  not not_137 (not_137_out, OP3);
  not not_138 (not_138_out, OP1);
  not not_139 (not_139_out, OP5);
  not not_140 (not_140_out, OP4);
  not not_141 (not_141_out, OP2);
  not not_142 (not_142_out, OP1);
  not not_143 (not_143_out, OP0);
  not not_144 (not_144_out, OP5);
  not not_145 (not_145_out, OP4);
  not not_146 (not_146_out, OP1);
  not not_147 (not_147_out, OP0);
  not not_148 (not_148_out, OP5);
  not not_149 (not_149_out, OP4);
  not not_150 (not_150_out, OP2);
  not not_151 (not_151_out, OP1);
  not not_152 (not_152_out, OP5);
  not not_153 (not_153_out, OP4);
  not not_154 (not_154_out, OP2);
  not not_155 (not_155_out, OP0);
  not not_156 (not_156_out, OP5);
  not not_157 (not_157_out, OP4);
  not not_158 (not_158_out, OP1);
  not not_159 (not_159_out, OP4);
  not not_160 (not_160_out, OP3);
  not not_161 (not_161_out, OP2);
  not not_162 (not_162_out, OP4);
  not not_163 (not_163_out, OP2);
  not not_164 (not_164_out, OP5);
  not not_165 (not_165_out, OP4);
  not not_166 (not_166_out, OP3);
  not not_167 (not_167_out, OP2);
  not not_168 (not_168_out, OP1);
  not not_169 (not_169_out, OP0);
  not not_170 (not_170_out, F5);
  not not_171 (not_171_out, F4);
  not not_172 (not_172_out, F3);
  not not_173 (not_173_out, OP5);
  not not_174 (not_174_out, OP4);
  not not_175 (not_175_out, OP0);
  not not_176 (not_176_out, OP4);
  not not_177 (not_177_out, OP3);
  not not_178 (not_178_out, OP2);
  not not_179 (not_179_out, OP1);
  not not_180 (not_180_out, OP5);
  not not_181 (not_181_out, OP4);
  not not_182 (not_182_out, OP3);
  not not_183 (not_183_out, OP2);
  not not_184 (not_184_out, OP1);
  not not_185 (not_185_out, OP5);
  not not_186 (not_186_out, OP4);
  not not_187 (not_187_out, OP3);
  not not_188 (not_188_out, OP2);
  not not_189 (not_189_out, OP1);
  not not_190 (not_190_out, OP0);
  not not_191 (not_191_out, F5);
  not not_192 (not_192_out, F4);
  not not_193 (not_193_out, F3);
  not not_194 (not_194_out, F2);
  not not_195 (not_195_out, F1);
  not not_196 (not_196_out, F0);
  not not_197 (not_197_out, OP5);
  not not_198 (not_198_out, OP4);
  not not_199 (not_199_out, OP3);
  not not_200 (not_200_out, OP2);
  not not_201 (not_201_out, OP1);
  not not_202 (not_202_out, OP0);
  not not_203 (not_203_out, F5);
  not not_204 (not_204_out, F4);
  not not_205 (not_205_out, F3);
  not not_206 (not_206_out, F2);
  not not_207 (not_207_out, OP5);
  not not_208 (not_208_out, OP4);
  not not_209 (not_209_out, OP3);
  not not_210 (not_210_out, OP2);
  not not_211 (not_211_out, OP1);
  not not_212 (not_212_out, OP0);
  not not_213 (not_213_out, F5);
  not not_214 (not_214_out, F4);
  not not_215 (not_215_out, F3);
  not not_216 (not_216_out, F2);
  not not_217 (not_217_out, F0);
  not not_218 (not_218_out, OP5);
  not not_219 (not_219_out, OP4);
  not not_220 (not_220_out, OP3);
  not not_221 (not_221_out, OP2);
  not not_222 (not_222_out, OP1);
  not not_223 (not_223_out, OP0);
  not not_224 (not_224_out, F4);
  not not_225 (not_225_out, F3);
  not not_226 (not_226_out, F2);
  not not_227 (not_227_out, F1);
  not not_228 (not_228_out, F0);
  not not_229 (not_229_out, OP5);
  not not_230 (not_230_out, OP4);
  not not_231 (not_231_out, OP3);
  not not_232 (not_232_out, OP2);
  not not_233 (not_233_out, OP1);
  not not_234 (not_234_out, OP0);
  not not_235 (not_235_out, F4);
  not not_236 (not_236_out, F3);
  not not_237 (not_237_out, F2);
  not not_238 (not_238_out, F1);
  not not_239 (not_239_out, OP5);
  not not_240 (not_240_out, OP4);
  not not_241 (not_241_out, OP3);
  not not_242 (not_242_out, OP2);
  not not_243 (not_243_out, OP1);
  not not_244 (not_244_out, OP0);
  not not_245 (not_245_out, F4);
  not not_246 (not_246_out, F3);
  not not_247 (not_247_out, F2);
  not not_248 (not_248_out, F0);
  not not_249 (not_249_out, OP5);
  not not_250 (not_250_out, OP4);
  not not_251 (not_251_out, OP3);
  not not_252 (not_252_out, OP2);
  not not_253 (not_253_out, OP1);
  not not_254 (not_254_out, OP0);
  not not_255 (not_255_out, F4);
  not not_256 (not_256_out, F3);
  not not_257 (not_257_out, F1);
  not not_258 (not_258_out, F0);
  not not_259 (not_259_out, OP5);
  not not_260 (not_260_out, OP4);
  not not_261 (not_261_out, OP3);
  not not_262 (not_262_out, OP2);
  not not_263 (not_263_out, OP1);
  not not_264 (not_264_out, OP0);
  not not_265 (not_265_out, F4);
  not not_266 (not_266_out, F3);
  not not_267 (not_267_out, F1);
  not not_268 (not_268_out, OP5);
  not not_269 (not_269_out, OP4);
  not not_270 (not_270_out, OP3);
  not not_271 (not_271_out, OP2);
  not not_272 (not_272_out, OP1);
  not not_273 (not_273_out, OP0);
  not not_274 (not_274_out, F4);
  not not_275 (not_275_out, F3);
  not not_276 (not_276_out, OP5);
  not not_277 (not_277_out, OP4);
  not not_278 (not_278_out, OP3);
  not not_279 (not_279_out, OP2);
  not not_280 (not_280_out, OP1);
  not not_281 (not_281_out, OP0);
  not not_282 (not_282_out, F4);
  not not_283 (not_283_out, F2);
  not not_284 (not_284_out, F0);
  not not_285 (not_285_out, OP5);
  not not_286 (not_286_out, OP4);
  not not_287 (not_287_out, OP3);
  not not_288 (not_288_out, OP2);
  not not_289 (not_289_out, OP1);
  not not_290 (not_290_out, OP0);
  not not_291 (not_291_out, F4);
  not not_292 (not_292_out, F2);
  not not_293 (not_293_out, OP5);
  not not_294 (not_294_out, OP4);
  not not_295 (not_295_out, OP3);
  not not_296 (not_296_out, OP2);
  not not_297 (not_297_out, OP1);
  not not_298 (not_298_out, OP0);
  not not_299 (not_299_out, F5);
  not not_300 (not_300_out, F4);
  not not_301 (not_301_out, F1);
  not not_302 (not_302_out, F0);
  not not_303 (not_303_out, OP5);
  not not_304 (not_304_out, OP4);
  not not_305 (not_305_out, OP3);
  not not_306 (not_306_out, OP1);
  not not_307 (not_307_out, OP0);
  not not_308 (not_308_out, OP5);
  not not_309 (not_309_out, OP4);
  not not_310 (not_310_out, OP3);
  not not_311 (not_311_out, OP1);
  not not_312 (not_312_out, OP4);
  not not_313 (not_313_out, OP2);
  not not_314 (not_314_out, OP5);
  not not_315 (not_315_out, OP4);
  not not_316 (not_316_out, OP3);
  not not_317 (not_317_out, OP2);
  not not_318 (not_318_out, OP1);
  not not_319 (not_319_out, OP0);
  not not_320 (not_320_out, F5);
  not not_321 (not_321_out, F4);
  not not_322 (not_322_out, F3);
  and and_1 (and_1_out, not_1_out, not_2_out, not_3_out, not_4_out, not_5_out, not_6_out, not_7_out, not_8_out, not_9_out, not_10_out, not_11_out, not_12_out);
  and and_2 (and_2_out, not_13_out, not_14_out, not_15_out, not_16_out, not_17_out, not_18_out, not_19_out, not_20_out, not_21_out, not_22_out, F1, F0);
  and and_3 (and_3_out, not_23_out, not_24_out, not_25_out, not_26_out, not_27_out, not_28_out, not_29_out, not_30_out, not_31_out, not_32_out, F1, not_33_out);
  and and_4 (and_4_out, not_34_out, not_35_out, not_36_out, not_37_out, not_38_out, not_39_out, F5, not_40_out, not_41_out, not_42_out, not_43_out, not_44_out);
  and and_5 (and_5_out, not_45_out, not_46_out, not_47_out, not_48_out, not_49_out, not_50_out, F5, not_51_out, not_52_out, not_53_out, not_54_out, F0);
  and and_6 (and_6_out, not_55_out, not_56_out, not_57_out, not_58_out, not_59_out, not_60_out, F5, not_61_out, not_62_out, not_63_out, F1, not_64_out);
  and and_7 (and_7_out, not_65_out, not_66_out, not_67_out, not_68_out, not_69_out, not_70_out, F5, not_71_out, not_72_out, F2, not_73_out, not_74_out);
  and and_8 (and_8_out, not_75_out, not_76_out, not_77_out, not_78_out, not_79_out, not_80_out, F5, not_81_out, not_82_out, F2, not_83_out, F0);
  and and_9 (and_9_out, not_84_out, not_85_out, not_86_out, not_87_out, not_88_out, not_89_out, F5, not_90_out, not_91_out, F2, F1, F0);
  and and_10 (and_10_out, not_92_out, not_93_out, not_94_out, not_95_out, not_96_out, not_97_out, F5, not_98_out, F3, not_99_out, F1, not_100_out);
  and and_11 (and_11_out, not_101_out, not_102_out, not_103_out, not_104_out, not_105_out, not_106_out, F5, not_107_out, F3, not_108_out, F1, F0);
  and and_12 (and_12_out, not_109_out, not_110_out, not_111_out, not_112_out, not_113_out, not_114_out, not_115_out, not_116_out, F3, not_117_out, not_118_out, not_119_out);
  and and_13 (and_13_out, not_120_out, not_121_out, not_122_out, not_123_out, not_124_out, not_125_out, not_126_out, not_127_out, F3, F2, not_128_out, not_129_out);
  and and_14 (and_14_out, not_130_out, not_131_out, not_132_out, OP2, not_133_out, not_134_out);
  and and_15 (and_15_out, not_135_out, not_136_out, not_137_out, OP2, not_138_out, OP0);
  and and_16 (and_16_out, not_139_out, not_140_out, OP3, not_141_out, not_142_out, not_143_out);
  and and_17 (and_17_out, not_144_out, not_145_out, OP3, OP2, not_146_out, not_147_out);
  and and_18 (and_18_out, not_148_out, not_149_out, OP3, not_150_out, not_151_out, OP0);
  and and_19 (and_19_out, not_152_out, not_153_out, OP3, not_154_out, OP1, not_155_out);
  and and_20 (and_20_out, not_156_out, not_157_out, OP3, OP2, not_158_out, OP0);
  and and_21 (and_21_out, OP5, not_159_out, not_160_out, not_161_out, OP1, OP0);
  and and_22 (and_22_out, OP5, not_162_out, OP3, not_163_out, OP1, OP0);
  and and_23 (and_23_out, not_164_out, not_165_out, not_166_out, not_167_out, not_168_out, not_169_out, not_170_out, not_171_out, not_172_out, F2, F1, F0);
  and and_24 (and_24_out, not_173_out, not_174_out, OP3, OP2, OP1, not_175_out);
  and and_25 (and_25_out, OP5, not_176_out, not_177_out, not_178_out, not_179_out, OP0);
  and and_26 (and_26_out, not_180_out, not_181_out, not_182_out, not_183_out, not_184_out, OP0);
  and and_27 (and_27_out, not_185_out, not_186_out, not_187_out, not_188_out, not_189_out, not_190_out, not_191_out, not_192_out, not_193_out, not_194_out, not_195_out, not_196_out);
  and and_28 (and_28_out, not_197_out, not_198_out, not_199_out, not_200_out, not_201_out, not_202_out, not_203_out, not_204_out, not_205_out, not_206_out, F1, F0);
  and and_29 (and_29_out, not_207_out, not_208_out, not_209_out, not_210_out, not_211_out, not_212_out, not_213_out, not_214_out, not_215_out, not_216_out, F1, not_217_out);
  and and_30 (and_30_out, not_218_out, not_219_out, not_220_out, not_221_out, not_222_out, not_223_out, F5, not_224_out, not_225_out, not_226_out, not_227_out, not_228_out);
  and and_31 (and_31_out, not_229_out, not_230_out, not_231_out, not_232_out, not_233_out, not_234_out, F5, not_235_out, not_236_out, not_237_out, not_238_out, F0);
  and and_32 (and_32_out, not_239_out, not_240_out, not_241_out, not_242_out, not_243_out, not_244_out, F5, not_245_out, not_246_out, not_247_out, F1, not_248_out);
  and and_33 (and_33_out, not_249_out, not_250_out, not_251_out, not_252_out, not_253_out, not_254_out, F5, not_255_out, not_256_out, F2, not_257_out, not_258_out);
  and and_34 (and_34_out, not_259_out, not_260_out, not_261_out, not_262_out, not_263_out, not_264_out, F5, not_265_out, not_266_out, F2, not_267_out, F0);
  and and_35 (and_35_out, not_268_out, not_269_out, not_270_out, not_271_out, not_272_out, not_273_out, F5, not_274_out, not_275_out, F2, F1, F0);
  and and_36 (and_36_out, not_276_out, not_277_out, not_278_out, not_279_out, not_280_out, not_281_out, F5, not_282_out, F3, not_283_out, F1, not_284_out);
  and and_37 (and_37_out, not_285_out, not_286_out, not_287_out, not_288_out, not_289_out, not_290_out, F5, not_291_out, F3, not_292_out, F1, F0);
  and and_38 (and_38_out, not_293_out, not_294_out, not_295_out, not_296_out, not_297_out, not_298_out, not_299_out, not_300_out, F3, F2, not_301_out, not_302_out);
  and and_39 (and_39_out, not_303_out, not_304_out, not_305_out, OP2, not_306_out, not_307_out);
  and and_40 (and_40_out, not_308_out, not_309_out, not_310_out, OP2, not_311_out, OP0);
  and and_41 (and_41_out, OP5, not_312_out, OP3, not_313_out, OP1, OP0);
  and and_42 (and_42_out, not_314_out, not_315_out, not_316_out, not_317_out, not_318_out, not_319_out, not_320_out, not_321_out, not_322_out, F2, F1, F0);
  or or_1 (R1_Used, and_1_out, and_2_out, and_3_out, and_4_out, and_5_out, and_6_out, and_7_out, and_8_out, and_9_out, and_10_out, and_11_out, and_12_out, and_13_out, and_14_out, and_15_out, and_16_out, and_17_out, and_18_out, and_19_out, and_20_out, and_21_out, and_22_out, and_23_out, and_24_out, and_25_out, and_26_out);
  or or_2 (R2_Used, and_27_out, and_28_out, and_29_out, and_30_out, and_31_out, and_32_out, and_33_out, and_34_out, and_35_out, and_36_out, and_37_out, and_38_out, and_39_out, and_40_out, and_41_out, and_42_out);
endmodule

module \数据相关检测  (
  input  [5:0] OP,
  input  [4:0] EX_WriteReg_num,
  input  EX_RegWrite,
  input  [4:0] MEM_WriteReg_num,
  input  MEM_RegWrite,
  input  [5:0] Func,
  input  [4:0] ID_R1_num,
  input  [4:0] ID_R2_num,
  output \数据相关 
);

  wire and_1_out, and_2_out, and_3_out, and_4_out, and_5_out, and_6_out, comparator_1_eq, comparator_2_eq,
       comparator_3_eq, comparator_4_eq, comparator_5_eq, comparator_6_eq, or_1_out, or_2_out,
       \源寄存器使用情况_1_r1_used , \源寄存器使用情况_1_r2_used ;

  \源寄存器使用情况  \u_源寄存器使用情况_1  (
    .OP0(OP[0]), .OP1(OP[1]), .OP2(OP[2]), .OP3(OP[3]), .OP4(OP[4]), .OP5(OP[5]), .F0(Func[0]), .F1(Func[1]),
    .F2(Func[2]), .F3(Func[3]), .F4(Func[4]), .F5(Func[5]), .R1_Used(\源寄存器使用情况_1_r1_used ),
    .R2_Used(\源寄存器使用情况_1_r2_used ));
  Comparator #(.width(5)) comparator_1 (.a(ID_R1_num), .b(EX_WriteReg_num), .eq(comparator_1_eq));  // open: gt, lt
  Comparator #(.width(5)) comparator_2 (.a(ID_R1_num), .b(MEM_WriteReg_num), .eq(comparator_2_eq));  // open: gt, lt
  Comparator #(.width(5)) comparator_3 (.a(ID_R2_num), .b(MEM_WriteReg_num), .eq(comparator_3_eq));  // open: gt, lt
  Comparator #(.width(5)) comparator_4 (.a(ID_R2_num), .b(EX_WriteReg_num), .eq(comparator_4_eq));  // open: gt, lt
  and and_1 (and_1_out, comparator_1_eq, EX_RegWrite, \源寄存器使用情况_1_r1_used );
  and and_2 (and_2_out, comparator_2_eq, MEM_RegWrite, \源寄存器使用情况_1_r1_used );
  and and_3 (and_3_out, comparator_3_eq, MEM_RegWrite, \源寄存器使用情况_1_r2_used );
  and and_4 (and_4_out, comparator_4_eq, EX_RegWrite, \源寄存器使用情况_1_r2_used );
  or or_1 (or_1_out, and_1_out, and_2_out);
  or or_2 (or_2_out, and_3_out, and_4_out);
  Comparator #(.width(5)) comparator_5 (.a(ID_R1_num), .b({5{1'b0}}), .eq(comparator_5_eq));  // open: gt, lt
  Comparator #(.width(5)) comparator_6 (.a(ID_R2_num), .b({5{1'b0}}), .eq(comparator_6_eq));  // open: gt, lt
  and and_5 (and_5_out, ~comparator_5_eq, or_1_out);  // AND_Gate
  and and_6 (and_6_out, ~comparator_6_eq, or_2_out);  // AND_Gate
  or or_3 (\数据相关 , and_5_out, and_6_out);

  // Other names for the same wires on the sheet: OP_CODE[5:0] = OP
endmodule

// IF/ID
module IF_ID (
  input  [31:0] IR,
  input  [31:0] PC,
  input  \预测跳转 ,
  input  [31:0] \预测地址 ,
  input  Hit,
  input  [2:0] HitPos,
  input  rst,
  input  clk,
  input  halt,
  output [31:0] IR_2,
  output [31:0] PC_2,
  output \预测跳转_2 ,
  output [31:0] \预测地址_2 ,
  output Hit_2,
  output [2:0] HitPos_2
);

  wire multiplexer_3_out, multiplexer_5_out;
  wire [2:0] multiplexer_6_out;
  wire [31:0] multiplexer_1_out, multiplexer_2_out, multiplexer_4_out;

  Multiplexer #(.width(32), .enable("false")) multiplexer_1 (
    .in0(IR), .in1({32{1'b0}}), .out(multiplexer_1_out), .sel(rst));
  Multiplexer #(.width(32), .enable("false")) multiplexer_2 (
    .in0(PC), .in1({32{1'b0}}), .out(multiplexer_2_out), .sel(rst));
  Multiplexer #(.enable("false")) multiplexer_3 (.in0(\预测跳转 ), .in1(1'b0), .out(multiplexer_3_out), .sel(rst));
  Multiplexer #(.width(32), .enable("false")) multiplexer_4 (
    .in0(\预测地址 ), .in1({32{1'b0}}), .out(multiplexer_4_out), .sel(rst));
  Multiplexer #(.enable("false")) multiplexer_5 (.in0(Hit), .in1(1'b0), .out(multiplexer_5_out), .sel(rst));
  Multiplexer #(.width(3), .enable("false")) multiplexer_6 (
    .in0(HitPos), .in1(3'b000), .out(multiplexer_6_out), .sel(rst));
  Register #(.width(32)) register_1 (.D(multiplexer_1_out), .en(halt), .Q(IR_2), .clk(clk));  // open: clr
  Register #(.width(32)) register_2 (.D(multiplexer_2_out), .en(halt), .Q(PC_2), .clk(clk));  // open: clr
  Register #(.width(1)) register_3 (.D(multiplexer_3_out), .en(halt), .Q(\预测跳转_2 ), .clk(clk));  // open: clr
  Register #(.width(32)) register_4 (.D(multiplexer_4_out), .en(halt), .Q(\预测地址_2 ), .clk(clk));  // open: clr
  Register #(.width(1)) register_5 (.D(multiplexer_5_out), .en(halt), .Q(Hit_2), .clk(clk));  // open: clr
  Register #(.width(3)) register_6 (.D(multiplexer_6_out), .en(halt), .Q(HitPos_2), .clk(clk));  // open: clr
endmodule
// ID.EX
module ID_EX (
  input  [31:0] IR,
  input  [31:0] PC,
  input  [31:0] A,
  input  [31:0] B,
  input  [4:0] Shamt,
  input  MemToReg,
  input  MemWrite,
  input  [3:0] ALUOP,
  input  RegWrite,
  input  RegDst,
  input  [31:0] R2,
  input  Syscall,
  input  Beq,
  input  Bne,
  input  Jal,
  input  JMP,
  input  JR,
  input  [31:0] \Addr_有 ,
  input  [25:0] Addr_26,
  input  SRAV,
  input  LH,
  input  BLTZ,
  input  ALU_SRC,
  input  [31:0] IMM,
  input  \预测跳转 ,
  input  [31:0] \预测地址 ,
  input  Hit,
  input  [2:0] HitPos,
  input  ERET,
  input  rst,
  input  clk,
  input  halt,
  output [31:0] IR_2,
  output [31:0] PC_2,
  output [31:0] A_2,
  output [31:0] B_2,
  output [4:0] Shamt_2,
  output MemToReg_2,
  output MemWrite_2,
  output [3:0] ALUOP_2,
  output RegWrite_2,
  output RegDst_2,
  output [31:0] R2_2,
  output Syscall_2,
  output Beq_2,
  output Bne_2,
  output Jal_2,
  output JMP_2,
  output JR_2,
  output [31:0] \Addr_有_2 ,
  output [25:0] Addr_26_2,
  output SRAV_2,
  output LH_2,
  output BLTZ_2,
  output ALU_SRC_2,
  output [31:0] IMM_2,
  output \预测跳转_2 ,
  output [31:0] \预测地址_2 ,
  output Hit_2,
  output [2:0] HitPos_2,
  output ERET_2
);

  wire multiplexer_6_out, multiplexer_7_out, multiplexer_9_out, multiplexer_10_out, multiplexer_12_out,
       multiplexer_13_out, multiplexer_14_out, multiplexer_15_out, multiplexer_16_out, multiplexer_17_out,
       multiplexer_20_out, multiplexer_21_out, multiplexer_22_out, multiplexer_23_out, multiplexer_25_out,
       multiplexer_27_out, multiplexer_29_out;
  wire [2:0] multiplexer_28_out;
  wire [3:0] multiplexer_8_out;
  wire [4:0] multiplexer_5_out;
  wire [25:0] multiplexer_19_out;
  wire [31:0] multiplexer_1_out, multiplexer_2_out, multiplexer_3_out, multiplexer_4_out, multiplexer_11_out,
       multiplexer_18_out, multiplexer_24_out, multiplexer_26_out;

  Multiplexer #(.width(32), .enable("false")) multiplexer_1 (
    .in0(IR), .in1({32{1'b0}}), .out(multiplexer_1_out), .sel(rst));
  Multiplexer #(.width(32), .enable("false")) multiplexer_2 (
    .in0(PC), .in1({32{1'b0}}), .out(multiplexer_2_out), .sel(rst));
  Multiplexer #(.width(32), .enable("false")) multiplexer_3 (
    .in0(A), .in1({32{1'b0}}), .out(multiplexer_3_out), .sel(rst));
  Multiplexer #(.width(32), .enable("false")) multiplexer_4 (
    .in0(B), .in1({32{1'b0}}), .out(multiplexer_4_out), .sel(rst));
  Multiplexer #(.width(5), .enable("false")) multiplexer_5 (
    .in0(Shamt), .in1({5{1'b0}}), .out(multiplexer_5_out), .sel(rst));
  Multiplexer #(.enable("false")) multiplexer_6 (.in0(MemToReg), .in1(1'b0), .out(multiplexer_6_out), .sel(rst));
  Multiplexer #(.enable("false")) multiplexer_7 (.in0(MemWrite), .in1(1'b0), .out(multiplexer_7_out), .sel(rst));
  Multiplexer #(.width(4), .enable("false")) multiplexer_8 (
    .in0(ALUOP), .in1(4'b0000), .out(multiplexer_8_out), .sel(rst));
  Multiplexer #(.enable("false")) multiplexer_9 (.in0(RegWrite), .in1(1'b0), .out(multiplexer_9_out), .sel(rst));
  Multiplexer #(.enable("false")) multiplexer_10 (.in0(RegDst), .in1(1'b0), .out(multiplexer_10_out), .sel(rst));
  Multiplexer #(.width(32), .enable("false")) multiplexer_11 (
    .in0(R2), .in1({32{1'b0}}), .out(multiplexer_11_out), .sel(rst));
  Multiplexer #(.enable("false")) multiplexer_12 (.in0(Syscall), .in1(1'b0), .out(multiplexer_12_out), .sel(rst));
  Multiplexer #(.enable("false")) multiplexer_13 (.in0(Beq), .in1(1'b0), .out(multiplexer_13_out), .sel(rst));
  Multiplexer #(.enable("false")) multiplexer_14 (.in0(Bne), .in1(1'b0), .out(multiplexer_14_out), .sel(rst));
  Multiplexer #(.enable("false")) multiplexer_15 (.in0(Jal), .in1(1'b0), .out(multiplexer_15_out), .sel(rst));
  Multiplexer #(.enable("false")) multiplexer_16 (.in0(JMP), .in1(1'b0), .out(multiplexer_16_out), .sel(rst));
  Multiplexer #(.enable("false")) multiplexer_17 (.in0(JR), .in1(1'b0), .out(multiplexer_17_out), .sel(rst));
  Multiplexer #(.width(32), .enable("false")) multiplexer_18 (
    .in0(\Addr_有 ), .in1({32{1'b0}}), .out(multiplexer_18_out), .sel(rst));
  Multiplexer #(.width(26), .enable("false")) multiplexer_19 (
    .in0(Addr_26), .in1({26{1'b0}}), .out(multiplexer_19_out), .sel(rst));
  Multiplexer #(.enable("false")) multiplexer_20 (.in0(SRAV), .in1(1'b0), .out(multiplexer_20_out), .sel(rst));
  Multiplexer #(.enable("false")) multiplexer_21 (.in0(LH), .in1(1'b0), .out(multiplexer_21_out), .sel(rst));
  Multiplexer #(.enable("false")) multiplexer_22 (.in0(BLTZ), .in1(1'b0), .out(multiplexer_22_out), .sel(rst));
  Multiplexer #(.enable("false")) multiplexer_23 (.in0(ALU_SRC), .in1(1'b0), .out(multiplexer_23_out), .sel(rst));
  Multiplexer #(.width(32), .enable("false")) multiplexer_24 (
    .in0(IMM), .in1({32{1'b0}}), .out(multiplexer_24_out), .sel(rst));
  Multiplexer #(.enable("false")) multiplexer_25 (.in0(\预测跳转 ), .in1(1'b0), .out(multiplexer_25_out), .sel(rst));
  Multiplexer #(.width(32), .enable("false")) multiplexer_26 (
    .in0(\预测地址 ), .in1({32{1'b0}}), .out(multiplexer_26_out), .sel(rst));
  Multiplexer #(.enable("false")) multiplexer_27 (.in0(Hit), .in1(1'b0), .out(multiplexer_27_out), .sel(rst));
  Multiplexer #(.width(3), .enable("false")) multiplexer_28 (
    .in0(HitPos), .in1(3'b000), .out(multiplexer_28_out), .sel(rst));
  Multiplexer #(.enable("false")) multiplexer_29 (.in0(ERET), .in1(1'b0), .out(multiplexer_29_out), .sel(rst));
  Register #(.width(32)) register_1 (.D(multiplexer_1_out), .en(halt), .Q(IR_2), .clk(clk));  // open: clr
  Register #(.width(32)) register_2 (.D(multiplexer_2_out), .en(halt), .Q(PC_2), .clk(clk));  // open: clr
  Register #(.width(32)) register_3 (.D(multiplexer_3_out), .en(halt), .Q(A_2), .clk(clk));  // open: clr
  Register #(.width(32)) register_4 (.D(multiplexer_4_out), .en(halt), .Q(B_2), .clk(clk));  // open: clr
  Register #(.width(5)) register_5 (.D(multiplexer_5_out), .en(halt), .Q(Shamt_2), .clk(clk));  // open: clr
  Register #(.width(1)) register_6 (.D(multiplexer_6_out), .en(halt), .Q(MemToReg_2), .clk(clk));  // open: clr
  Register #(.width(1)) register_7 (.D(multiplexer_7_out), .en(halt), .Q(MemWrite_2), .clk(clk));  // open: clr
  Register #(.width(4)) register_8 (.D(multiplexer_8_out), .en(halt), .Q(ALUOP_2), .clk(clk));  // open: clr
  Register #(.width(1)) register_9 (.D(multiplexer_9_out), .en(halt), .Q(RegWrite_2), .clk(clk));  // open: clr
  Register #(.width(1)) register_10 (.D(multiplexer_10_out), .en(halt), .Q(RegDst_2), .clk(clk));  // open: clr
  Register #(.width(32)) register_11 (.D(multiplexer_11_out), .en(halt), .Q(R2_2), .clk(clk));  // open: clr
  Register #(.width(1)) register_12 (.D(multiplexer_12_out), .en(halt), .Q(Syscall_2), .clk(clk));  // open: clr
  Register #(.width(1)) register_13 (.D(multiplexer_13_out), .en(halt), .Q(Beq_2), .clk(clk));  // open: clr
  Register #(.width(1)) register_14 (.D(multiplexer_14_out), .en(halt), .Q(Bne_2), .clk(clk));  // open: clr
  Register #(.width(1)) register_15 (.D(multiplexer_15_out), .en(halt), .Q(Jal_2), .clk(clk));  // open: clr
  Register #(.width(1)) register_16 (.D(multiplexer_16_out), .en(halt), .Q(JMP_2), .clk(clk));  // open: clr
  Register #(.width(1)) register_17 (.D(multiplexer_17_out), .en(halt), .Q(JR_2), .clk(clk));  // open: clr
  Register #(.width(32)) register_18 (.D(multiplexer_18_out), .en(halt), .Q(\Addr_有_2 ), .clk(clk));  // open: clr
  Register #(.width(26)) register_19 (.D(multiplexer_19_out), .en(halt), .Q(Addr_26_2), .clk(clk));  // open: clr
  Register #(.width(1)) register_20 (.D(multiplexer_20_out), .en(halt), .Q(SRAV_2), .clk(clk));  // open: clr
  Register #(.width(1)) register_21 (.D(multiplexer_21_out), .en(halt), .Q(LH_2), .clk(clk));  // open: clr
  Register #(.width(1)) register_22 (.D(multiplexer_22_out), .en(halt), .Q(BLTZ_2), .clk(clk));  // open: clr
  Register #(.width(1)) register_23 (.D(multiplexer_23_out), .en(halt), .Q(ALU_SRC_2), .clk(clk));  // open: clr
  Register #(.width(32)) register_24 (.D(multiplexer_24_out), .en(halt), .Q(IMM_2), .clk(clk));  // open: clr
  Register #(.width(1)) register_25 (.D(multiplexer_25_out), .en(halt), .Q(\预测跳转_2 ), .clk(clk));  // open: clr
  Register #(.width(32)) register_26 (.D(multiplexer_26_out), .en(halt), .Q(\预测地址_2 ), .clk(clk));  // open: clr
  Register #(.width(1)) register_27 (.D(multiplexer_27_out), .en(halt), .Q(Hit_2), .clk(clk));  // open: clr
  Register #(.width(3)) register_28 (.D(multiplexer_28_out), .en(halt), .Q(HitPos_2), .clk(clk));  // open: clr
  Register #(.width(1)) register_29 (.D(multiplexer_29_out), .en(halt), .Q(ERET_2), .clk(clk));  // open: clr
endmodule

// EX/MEM
module EX_MEM (
  input  [31:0] IR,
  input  [31:0] PC,
  input  [31:0] Alu,
  input  [31:0] A,
  input  [31:0] B,
  input  MemToReg,
  input  MemWrite,
  input  RegWrite,
  input  RegDst,
  input  Jal,
  input  Syscall,
  input  [25:0] Addr_26,
  input  LH,
  input  rst,
  input  clk,
  input  halt,
  output [31:0] IR_2,
  output [31:0] PC_2,
  output [31:0] Alu_2,
  output [31:0] A_2,
  output [31:0] B_2,
  output MemToReg_2,
  output MemWrite_2,
  output RegWrite_2,
  output RegDst_2,
  output Jal_2,
  output Syscall_2,
  output [25:0] Addr_26_2,
  output LH_2
);

  wire multiplexer_6_out, multiplexer_7_out, multiplexer_8_out, multiplexer_9_out, multiplexer_10_out,
       multiplexer_11_out, multiplexer_13_out;
  wire [25:0] multiplexer_12_out;
  wire [31:0] multiplexer_1_out, multiplexer_2_out, multiplexer_3_out, multiplexer_4_out, multiplexer_5_out;

  Multiplexer #(.width(32), .enable("false")) multiplexer_1 (
    .in0(IR), .in1({32{1'b0}}), .out(multiplexer_1_out), .sel(rst));
  Multiplexer #(.width(32), .enable("false")) multiplexer_2 (
    .in0(PC), .in1({32{1'b0}}), .out(multiplexer_2_out), .sel(rst));
  Multiplexer #(.width(32), .enable("false")) multiplexer_3 (
    .in0(Alu), .in1({32{1'b0}}), .out(multiplexer_3_out), .sel(rst));
  Multiplexer #(.width(32), .enable("false")) multiplexer_4 (
    .in0(A), .in1({32{1'b0}}), .out(multiplexer_4_out), .sel(rst));
  Multiplexer #(.width(32), .enable("false")) multiplexer_5 (
    .in0(B), .in1({32{1'b0}}), .out(multiplexer_5_out), .sel(rst));
  Multiplexer #(.enable("false")) multiplexer_6 (.in0(MemToReg), .in1(1'b0), .out(multiplexer_6_out), .sel(rst));
  Multiplexer #(.enable("false")) multiplexer_7 (.in0(MemWrite), .in1(1'b0), .out(multiplexer_7_out), .sel(rst));
  Multiplexer #(.enable("false")) multiplexer_8 (.in0(RegWrite), .in1(1'b0), .out(multiplexer_8_out), .sel(rst));
  Multiplexer #(.enable("false")) multiplexer_9 (.in0(RegDst), .in1(1'b0), .out(multiplexer_9_out), .sel(rst));
  Multiplexer #(.enable("false")) multiplexer_10 (.in0(Jal), .in1(1'b0), .out(multiplexer_10_out), .sel(rst));
  Multiplexer #(.enable("false")) multiplexer_11 (.in0(Syscall), .in1(1'b0), .out(multiplexer_11_out), .sel(rst));
  Multiplexer #(.width(26), .enable("false")) multiplexer_12 (
    .in0(Addr_26), .in1({26{1'b0}}), .out(multiplexer_12_out), .sel(rst));
  Multiplexer #(.enable("false")) multiplexer_13 (.in0(LH), .in1(1'b0), .out(multiplexer_13_out), .sel(rst));
  Register #(.width(32)) register_1 (.D(multiplexer_1_out), .en(halt), .Q(IR_2), .clk(clk));  // open: clr
  Register #(.width(32)) register_2 (.D(multiplexer_2_out), .en(halt), .Q(PC_2), .clk(clk));  // open: clr
  Register #(.width(32)) register_3 (.D(multiplexer_3_out), .en(halt), .Q(Alu_2), .clk(clk));  // open: clr
  Register #(.width(32)) register_4 (.D(multiplexer_4_out), .en(halt), .Q(A_2), .clk(clk));  // open: clr
  Register #(.width(32)) register_5 (.D(multiplexer_5_out), .en(halt), .Q(B_2), .clk(clk));  // open: clr
  Register #(.width(1)) register_6 (.D(multiplexer_6_out), .en(halt), .Q(MemToReg_2), .clk(clk));  // open: clr
  Register #(.width(1)) register_7 (.D(multiplexer_7_out), .en(halt), .Q(MemWrite_2), .clk(clk));  // open: clr
  Register #(.width(1)) register_8 (.D(multiplexer_8_out), .en(halt), .Q(RegWrite_2), .clk(clk));  // open: clr
  Register #(.width(1)) register_9 (.D(multiplexer_9_out), .en(halt), .Q(RegDst_2), .clk(clk));  // open: clr
  Register #(.width(1)) register_10 (.D(multiplexer_10_out), .en(halt), .Q(Jal_2), .clk(clk));  // open: clr
  Register #(.width(1)) register_11 (.D(multiplexer_11_out), .en(halt), .Q(Syscall_2), .clk(clk));  // open: clr
  Register #(.width(26)) register_12 (.D(multiplexer_12_out), .en(halt), .Q(Addr_26_2), .clk(clk));  // open: clr
  Register #(.width(1)) register_13 (.D(multiplexer_13_out), .en(halt), .Q(LH_2), .clk(clk));  // open: clr
endmodule

// MEN/WB
module MEM_WB (
  input  [31:0] IR,
  input  [31:0] PC,
  input  [31:0] A,
  input  [31:0] MD,
  input  RegWrite,
  input  RegDst,
  input  Jal,
  input  Syscall,
  input  [25:0] Addr_26,
  input  [31:0] B,
  input  rst,
  input  clk,
  input  halt,
  output [31:0] IR_2,
  output [31:0] PC_2,
  output [31:0] A_2,
  output [31:0] MD_2,
  output RegWrite_2,
  output RegDst_2,
  output Jal_2,
  output Syscall_2,
  output [25:0] Addr_26_2,
  output [31:0] B_2
);

  wire multiplexer_5_out, multiplexer_6_out, multiplexer_7_out, multiplexer_8_out;
  wire [25:0] multiplexer_9_out;
  wire [31:0] multiplexer_1_out, multiplexer_2_out, multiplexer_3_out, multiplexer_4_out, multiplexer_10_out;

  Multiplexer #(.width(32), .enable("false")) multiplexer_1 (
    .in0(IR), .in1({32{1'b0}}), .out(multiplexer_1_out), .sel(rst));
  Multiplexer #(.width(32), .enable("false")) multiplexer_2 (
    .in0(PC), .in1({32{1'b0}}), .out(multiplexer_2_out), .sel(rst));
  Multiplexer #(.width(32), .enable("false")) multiplexer_3 (
    .in0(A), .in1({32{1'b0}}), .out(multiplexer_3_out), .sel(rst));
  Multiplexer #(.width(32), .enable("false")) multiplexer_4 (
    .in0(MD), .in1({32{1'b0}}), .out(multiplexer_4_out), .sel(rst));
  Multiplexer #(.enable("false")) multiplexer_5 (.in0(RegWrite), .in1(1'b0), .out(multiplexer_5_out), .sel(rst));
  Multiplexer #(.enable("false")) multiplexer_6 (.in0(RegDst), .in1(1'b0), .out(multiplexer_6_out), .sel(rst));
  Multiplexer #(.enable("false")) multiplexer_7 (.in0(Jal), .in1(1'b0), .out(multiplexer_7_out), .sel(rst));
  Multiplexer #(.enable("false")) multiplexer_8 (.in0(Syscall), .in1(1'b0), .out(multiplexer_8_out), .sel(rst));
  Multiplexer #(.width(26), .enable("false")) multiplexer_9 (
    .in0(Addr_26), .in1({26{1'b0}}), .out(multiplexer_9_out), .sel(rst));
  Multiplexer #(.width(32), .enable("false")) multiplexer_10 (
    .in0(B), .in1({32{1'b0}}), .out(multiplexer_10_out), .sel(rst));
  Register #(.width(32)) register_1 (.D(multiplexer_1_out), .en(halt), .Q(IR_2), .clk(clk));  // open: clr
  Register #(.width(32)) register_2 (.D(multiplexer_2_out), .en(halt), .Q(PC_2), .clk(clk));  // open: clr
  Register #(.width(32)) register_3 (.D(multiplexer_3_out), .en(halt), .Q(A_2), .clk(clk));  // open: clr
  Register #(.width(32)) register_4 (.D(multiplexer_4_out), .en(halt), .Q(MD_2), .clk(clk));  // open: clr
  Register #(.width(1)) register_5 (.D(multiplexer_5_out), .en(halt), .Q(RegWrite_2), .clk(clk));  // open: clr
  Register #(.width(1)) register_6 (.D(multiplexer_6_out), .en(halt), .Q(RegDst_2), .clk(clk));  // open: clr
  Register #(.width(1)) register_7 (.D(multiplexer_7_out), .en(halt), .Q(Jal_2), .clk(clk));  // open: clr
  Register #(.width(1)) register_8 (.D(multiplexer_8_out), .en(halt), .Q(Syscall_2), .clk(clk));  // open: clr
  Register #(.width(26)) register_9 (.D(multiplexer_9_out), .en(halt), .Q(Addr_26_2), .clk(clk));  // open: clr
  Register #(.width(32)) register_10 (.D(multiplexer_10_out), .en(halt), .Q(B_2), .clk(clk));  // open: clr
endmodule

module \分支相关流水线  (
);

  wire and_2_out, and_3_out, and_4_out, Beq, BLTZ, Bne, CLK, comparator_1_lt, comparator_2_eq, EX_Beq,
       EX_BLTZ, EX_BLTZ_s, EX_Bne, EX_Branch, \EX_Branch_有 , EX_JMP, EX_JR, EX_LH, ex_mem_1_jal_2,
       ex_mem_1_lh_2, ex_mem_1_memwrite_2, ex_mem_1_syscall_2, EX_SRAV, Go, halt, id_ex_1_jal_2,
       id_ex_1_memtoreg_2, id_ex_1_memwrite_2, id_ex_1_regdst_2, id_ex_1_regwrite_2, id_ex_1_syscall_2,
       InUse, IR1, IR2, IR3, Jal, JMP, JR, LH, mem_wb_1_jal_2, mem_wb_1_syscall_2, MemToReg, MemToReg_2,
       MemWrite, mips_alu_1_equal, not_1_out, or_1_out, or_2_out, or_5_out, RegDst, RegDst_2, RegDst_r,
       RegWrite, RegWrite_2, RST, SignedExt, SRAV, Sys, W1, W2, W3, WE, \片选 , \硬布线控制器_1_alu_src ;
  wire [3:0] ALUOP, ALUOP_1;
  wire [4:0] multiplexer_5_out, multiplexer_6_out, multiplexer_7_out, multiplexer_9_out, multiplexer_12_out,
       rd, rt, shamt_1;
  wire [15:0] counter_2_q, \LoadUse次数 , multiplexer_13_out, multiplexer_13_out_2, \总周期数 , \插入气泡数 , \无条件分支数 ,
       \条件分支成功数 ;
  wire [25:0] ex_mem_1_addr_26_2;
  wire [27:2] id_ex_1_addr_26_2;
  wire [31:0] adder_1_out, adder_4_out, bit_extender_1_out, bit_extender_2_out, bit_extender_3_out,
       bit_extender_4_out, bit_extender_5_out, EX__rs, EX_IMM, ex_mem_1_a_2, ex_mem_1_alu_2, ex_mem_1_b_2,
       ex_mem_1_ir_2, EX_PC, \id_ex_1_addr_有_2 , id_ex_1_b_2, id_ex_1_ir_2, id_ex_1_r2_2, ID_PC, IF_PC, IR,
       LedData, MEM_PC, mem_wb_1_a_2, mem_wb_1_b_2, mem_wb_1_ir_2, mem_wb_1_md_2, mips_alu_1_result,
       mips_regifile_1_r1, mips_regifile_1_r2, multiplexer_1_out, multiplexer_2_out, multiplexer_3_out,
       multiplexer_4_out, multiplexer_8_out, multiplexer_10_out, multiplexer_11_out, multiplexer_14_out,
       multiplexer_15_out, PC_q, ram_1_data, rom_1_data, shifter_1_out, WB_PC;

  Button \u_总复位  (.out(RST));
  Button _1 (.out(IR1));
  Button _2 (.out(IR2));
  Button _3 (.out(IR3));
  Button \u_继续运行  (.out(Go));
  LED led_1 (.in(W1));
  LED led_2 (.in(W2));
  LED led_3 (.in(W3));
  Multiplexer #(.width(32), .enable("false")) multiplexer_1 (
    .in0(IF_PC), .in1(\id_ex_1_addr_有_2 ), .out(multiplexer_1_out), .sel(\EX_Branch_有 ));
  Hex_Digit_Display hex_digit_display_1 (.value(LedData[31:28]));  // open: dp
  or or_1 (or_1_out, EX_JMP, EX_JR);
  Multiplexer #(.width(32), .enable("false")) multiplexer_2 (
    .in0(multiplexer_4_out), .in1({EX_PC[31:28], id_ex_1_addr_26_2, 2'b00}), .out(multiplexer_2_out),
    .sel(EX_JMP));
  Multiplexer #(.width(32), .enable("false")) multiplexer_3 (
    .in0(multiplexer_2_out), .in1(EX__rs), .out(multiplexer_3_out), .sel(EX_JR));
  Comparator #(.width(32)) comparator_1 (.a(EX__rs), .b({32{1'b0}}), .lt(comparator_1_lt));  // open: gt, eq
  Hex_Digit_Display hex_digit_display_2 (.value(LedData[27:24]));  // open: dp
  Hex_Digit_Display hex_digit_display_3 (.value(LedData[23:20]));  // open: dp
  Counter #(.width(16), .max('hffff), .ongoal("stay")) counter_1 (
    .count(or_1_out), .Q(\无条件分支数 ), .clk(CLK), .clr(RST));  // open: load, D, carry
  Counter #(.width(16), .max('hffff), .ongoal("stay")) counter_2 (
    .count(EX_Branch), .Q(counter_2_q), .clk(CLK), .clr(RST));  // open: load, D, carry
  Register #(.width(32)) PC (.D(multiplexer_3_out), .en(InUse), .Q(PC_q), .clk(CLK), .clr(RST));
  Adder #(.width(32)) adder_1 (.a(EX_IMM), .b(EX_PC), .out(adder_1_out));  // open: cin, cout
  and and_1 (EX_BLTZ_s, comparator_1_lt, EX_BLTZ);
  Hex_Digit_Display hex_digit_display_4 (.value(LedData[19:16]));  // open: dp
  Hex_Digit_Display hex_digit_display_5 (.value(LedData[15:12]));  // open: dp
  Adder #(.width(16)) adder_2 (.a(counter_2_q), .b(counter_2_q), .out(\插入气泡数 ));  // open: cin, cout
  Multiplexer #(.width(32), .enable("false")) multiplexer_4 (
    .in0(multiplexer_1_out), .in1(adder_1_out), .out(multiplexer_4_out), .sel(EX_BLTZ_s));
  Hex_Digit_Display hex_digit_display_6 (.value(LedData[7:4]));  // open: dp
  Hex_Digit_Display hex_digit_display_7 (.value(LedData[11:8]));  // open: dp
  Clock clock_1 (.out(CLK));
  ROM #(.addrWidth(10), .dataWidth(32)) rom_1 (.addr(PC_q[11:2]), .data(rom_1_data));  // open: sel
  Adder #(.width(32)) adder_3 (.a(PC_q), .b(32'h4), .out(IF_PC));  // open: cin, cout
  not not_1 (not_1_out, halt);
  Hex_Digit_Display hex_digit_display_8 (.value(LedData[3:0]));  // open: dp
  IF_ID if_id_1 (
    .IR(rom_1_data), .IR_2(IR), .clk(CLK), .halt(not_1_out), .rst(or_2_out), .PC(IF_PC), .PC_2(ID_PC));  // open: 预测跳转, 预测跳转_2, 预测地址, 预测地址_2, Hit, Hit_2, HitPos, HitPos_2
  // Probe on \总周期数 
  // Probe on \无条件分支数 
  // Probe on \条件分支成功数 
  // Probe on \插入气泡数 
  // Probe on \LoadUse次数 
  // Probe on IF_PC[11:0]
  \硬布线控制器  \u_硬布线控制器_1  (
    .Func(IR[5:0]), .OP(IR[31:26]), .ALU_OP(ALUOP), .MemToReg(MemToReg), .MemWrite(MemWrite),
    .ALU_SRC(\硬布线控制器_1_alu_src ), .RegWrite(RegWrite), .SysCALL(Sys), .SignedExt(SignedExt), .RegDst(RegDst),
    .JR(JR), .JMP(JMP), .Beq(Beq), .JAL(Jal), .Bne(Bne), .SRAV(SRAV), .LH(LH), .BLTZ(BLTZ));  // open: ERET
  Multiplexer #(.width(5), .enable("false")) multiplexer_5 (
    .in0(IR[25:21]), .in1(5'b00100), .out(multiplexer_5_out), .sel(Sys));
  // Probe on ID_PC[11:0]
  Multiplexer #(.width(5), .enable("false")) multiplexer_6 (
    .in0(IR[20:16]), .in1(5'b00010), .out(multiplexer_6_out), .sel(Sys));
  Multiplexer #(.width(5), .enable("false")) multiplexer_7 (
    .in0(rt), .in1(rd), .out(multiplexer_7_out), .sel(RegDst_r));
  assign bit_extender_1_out = {{16{1'b0}}, IR[15:0]};  // Bit_Extender bit_extender_1
  Multiplexer #(.width(32), .enable("false")) multiplexer_8 (
    .in0(bit_extender_1_out), .in1(bit_extender_2_out), .out(multiplexer_8_out), .sel(SignedExt));
  assign bit_extender_2_out = {{16{IR[15]}}, IR[15:0]};  // Bit_Extender bit_extender_2
  // Probe on MEM_PC[11:0]
  // Probe on EX_PC[11:0]
  Multiplexer #(.width(5), .enable("false")) multiplexer_9 (
    .in0(multiplexer_7_out), .in1({5{1'b1}}), .out(multiplexer_9_out), .sel(mem_wb_1_jal_2));
  // Probe on WB_PC[11:0]
  Multiplexer #(.width(32), .enable("false")) multiplexer_10 (
    .in0(mem_wb_1_md_2), .in1(WB_PC), .out(multiplexer_10_out), .sel(mem_wb_1_jal_2));
  Shifter #(.width(32)) shifter_1 (.in(bit_extender_2_out), .\dist (5'b00010), .out(shifter_1_out));
  or or_2 (or_2_out, EX_Branch, RST);
  Adder #(.width(32)) adder_4 (.a(shifter_1_out), .b(ID_PC), .out(adder_4_out));  // open: cin, cout
  MIPS_Regifile mips_regifile_1 (
    .Din(multiplexer_10_out), .Clk(CLK), .R1(mips_regifile_1_r1), .R2(mips_regifile_1_r2), .WE(WE),
    .W_num(multiplexer_9_out), .R1_num(multiplexer_5_out), .R2_num(multiplexer_6_out));
  Multiplexer #(.width(32), .enable("false")) multiplexer_11 (
    .in0(mips_regifile_1_r2), .in1(multiplexer_8_out), .out(multiplexer_11_out), .sel(\硬布线控制器_1_alu_src ));
  ID_EX id_ex_1 (
    .IR(IR), .PC(ID_PC), .A(mips_regifile_1_r1), .B(multiplexer_11_out), .Shamt(IR[10:6]),
    .MemToReg(MemToReg), .MemWrite(MemWrite), .ALUOP(ALUOP), .RegWrite(RegWrite), .RegDst(RegDst),
    .R2(mips_regifile_1_r2), .Syscall(Sys), .IR_2(id_ex_1_ir_2), .PC_2(EX_PC), .A_2(EX__rs),
    .B_2(id_ex_1_b_2), .Shamt_2(shamt_1), .MemToReg_2(id_ex_1_memtoreg_2), .MemWrite_2(id_ex_1_memwrite_2),
    .ALUOP_2(ALUOP_1), .RegWrite_2(id_ex_1_regwrite_2), .RegDst_2(id_ex_1_regdst_2), .R2_2(id_ex_1_r2_2),
    .Syscall_2(id_ex_1_syscall_2), .clk(CLK), .halt(not_1_out), .rst(or_2_out), .Beq(Beq), .Beq_2(EX_Beq),
    .Bne(Bne), .Bne_2(EX_Bne), .Jal(Jal), .Jal_2(id_ex_1_jal_2), .JMP(JMP), .JMP_2(EX_JMP), .JR(JR),
    .JR_2(EX_JR), .\Addr_有 (adder_4_out), .\Addr_有_2 (\id_ex_1_addr_有_2 ), .Addr_26(IR[25:0]),
    .Addr_26_2(id_ex_1_addr_26_2), .SRAV(SRAV), .SRAV_2(EX_SRAV), .LH(LH), .LH_2(EX_LH), .BLTZ(BLTZ),
    .BLTZ_2(EX_BLTZ));  // open: ALU_SRC, ALU_SRC_2, IMM, IMM_2, 预测跳转, 预测跳转_2, 预测地址, 预测地址_2, Hit, Hit_2, HitPos, HitPos_2, ERET, ERET_2
  or or_3 (EX_Branch, EX_JMP, \EX_Branch_有 , EX_JR);
  Counter #(.width(16), .max('hffff)) counter_3 (
    .count(InUse), .Q(\总周期数 ), .clk(CLK), .clr(RST));  // open: load, D, carry
  assign bit_extender_3_out = {{16{id_ex_1_ir_2[15]}}, id_ex_1_ir_2[15:0]};  // Bit_Extender bit_extender_3
  MIPS_ALU mips_alu_1 (
    .X(EX__rs), .Y(id_ex_1_b_2), .AluOP(ALUOP_1), .Equal(mips_alu_1_equal), .Result(mips_alu_1_result),
    .shamt(multiplexer_12_out));  // open: Result_2
  Shifter #(.width(32)) shifter_2 (.in(bit_extender_3_out), .\dist (5'b00010), .out(EX_IMM));
  and and_2 (and_2_out, EX_Beq, mips_alu_1_equal);
  and and_3 (and_3_out, EX_Bne, ~mips_alu_1_equal);  // AND_Gate
  Multiplexer #(.width(5), .enable("false")) multiplexer_12 (
    .in0(shamt_1), .in1(EX__rs[4:0]), .out(multiplexer_12_out), .sel(EX_SRAV));
  or or_4 (\EX_Branch_有 , and_2_out, EX_BLTZ_s, and_3_out);
  Counter #(.width(16), .max('hffff)) counter_4 (
    .count(\EX_Branch_有 ), .Q(\条件分支成功数 ), .clk(CLK), .clr(RST));  // open: load, D, carry
  EX_MEM ex_mem_1 (
    .IR(id_ex_1_ir_2), .PC(EX_PC), .Alu(mips_alu_1_result), .A(EX__rs), .B(id_ex_1_r2_2),
    .MemToReg(id_ex_1_memtoreg_2), .MemWrite(id_ex_1_memwrite_2), .RegWrite(id_ex_1_regwrite_2),
    .RegDst(id_ex_1_regdst_2), .Syscall(id_ex_1_syscall_2), .IR_2(ex_mem_1_ir_2), .PC_2(MEM_PC),
    .Alu_2({ex_mem_1_alu_2[31:2], \片选 , ex_mem_1_alu_2[0]}), .A_2(ex_mem_1_a_2), .B_2(ex_mem_1_b_2),
    .MemToReg_2(MemToReg_2), .MemWrite_2(ex_mem_1_memwrite_2), .RegWrite_2(RegWrite_2), .RegDst_2(RegDst_2),
    .Syscall_2(ex_mem_1_syscall_2), .clk(CLK), .halt(not_1_out), .rst(RST), .Jal(id_ex_1_jal_2),
    .Jal_2(ex_mem_1_jal_2), .Addr_26(id_ex_1_addr_26_2), .Addr_26_2(ex_mem_1_addr_26_2), .LH(EX_LH),
    .LH_2(ex_mem_1_lh_2));
  Multiplexer #(.width(32), .enable("false")) multiplexer_13 (
    .in0({ex_mem_1_alu_2[31:2], \片选 , ex_mem_1_alu_2[0]}), .in1(ram_1_data),
    .out({multiplexer_13_out_2, multiplexer_13_out}), .sel(MemToReg_2));
  RAM #(.addrWidth(10), .dataWidth(32), .bus("separate")) ram_1 (
    .addr(ex_mem_1_alu_2[11:2]), .din(ex_mem_1_b_2), .data(ram_1_data), .str(ex_mem_1_memwrite_2),
    .sel(1'b1), .clk(CLK), .ld(MemToReg_2));  // open: clr
  assign bit_extender_4_out = {{16{multiplexer_13_out[15]}}, multiplexer_13_out};  // Bit_Extender bit_extender_4
  assign bit_extender_5_out = {{16{multiplexer_13_out_2[15]}}, multiplexer_13_out_2};  // Bit_Extender bit_extender_5
  Multiplexer #(.width(32), .enable("false")) multiplexer_14 (
    .in0(bit_extender_4_out), .in1(bit_extender_5_out), .out(multiplexer_14_out), .sel(\片选 ));
  Multiplexer #(.width(32), .enable("false")) multiplexer_15 (
    .in0({multiplexer_13_out_2, multiplexer_13_out}), .in1(multiplexer_14_out), .out(multiplexer_15_out),
    .sel(ex_mem_1_lh_2));
  MEM_WB mem_wb_1 (
    .IR(ex_mem_1_ir_2), .PC(MEM_PC), .A(ex_mem_1_a_2), .MD(multiplexer_15_out), .RegWrite(RegWrite_2),
    .RegDst(RegDst_2), .Syscall(ex_mem_1_syscall_2),
    .IR_2({mem_wb_1_ir_2[31:21], rt, rd, mem_wb_1_ir_2[10:0]}), .PC_2(WB_PC), .A_2(mem_wb_1_a_2),
    .MD_2(mem_wb_1_md_2), .RegWrite_2(WE), .RegDst_2(RegDst_r), .Syscall_2(mem_wb_1_syscall_2), .clk(CLK),
    .halt(not_1_out), .rst(RST), .Jal(ex_mem_1_jal_2), .Jal_2(mem_wb_1_jal_2), .Addr_26(ex_mem_1_addr_26_2),
    .B(ex_mem_1_b_2), .B_2(mem_wb_1_b_2));  // open: Addr_26_2
  Register #(.width(32)) register_1 (.D(mem_wb_1_a_2), .en(mem_wb_1_syscall_2), .Q(LedData), .clk(CLK));  // open: clr
  Comparator #(.width(32)) comparator_2 (.a(mem_wb_1_b_2), .b(32'h22), .eq(comparator_2_eq));  // open: gt, lt
  and and_4 (and_4_out, mem_wb_1_syscall_2, ~comparator_2_eq);  // AND_Gate
  Register #(.width(1)) register_2 (.D(mem_wb_1_syscall_2), .en(and_4_out), .Q(halt), .clk(CLK), .clr(or_5_out));
  not not_2 (InUse, halt);
  or or_5 (or_5_out, RST, Go);

  // Other names for the same wires on the sheet: shamt[4:0] = IR[10:6]; PC[31:0] = ID_PC

  // Notes on the sheet:
  //   中断源
  //   中断等待指示
  //   数码管输出
  //   指令存储器
  //   contents of rom_1 (hex, n*v repeats v):
  //   20110020 20020022 8100006 20110000 20110000 2002000a 10000003 20110000 20110000 2002000a 14110003
  //   20110000 20110000 2002000a c100014 2002000a 0 0 0 c 2231ffff 0 0 0 112020 0 0 0 c 1620fff6 3e00008
  //   Shamt
  //   OP
  //   Func
  //   rs
  //   rt
  //   Imm
  //   流水调试日志用
  //   rd
  //   rt
endmodule

module \气泡流水线  (
);

  wire and_1_out, and_3_out, and_4_out, and_5_out, and_6_out, and_7_out, Beq, BLTZ, Bne, CLK,
       comparator_1_lt, comparator_2_eq, EX_Beq, EX_BLTZ, EX_BLTZ_s, EX_Bne, EX_Branch, \EX_Branch_有 ,
       EX_Jal, EX_JMP, EX_JR, EX_LH, ex_mem_1_lh_2, ex_mem_1_memwrite_2, ex_mem_1_syscall_2, EX_RegDst,
       EX_RegWrite, EX_SRAV, Go, halt, id_ex_1_memtoreg_2, id_ex_1_memwrite_2, id_ex_1_syscall_2, InUse, IR1,
       IR2, IR3, Jal, JMP, JR, LH, MEM_Jal, mem_wb_1_jal_2, mem_wb_1_syscall_2, MemToReg, MemToReg_2,
       MemWrite, mips_alu_1_equal, not_1_out, not_2_out, not_3_out, or_1_out, or_2_out, or_3_out, or_5_out,
       or_7_out, RegDst, RegDst_2, RegDst_r, RegWrite, RegWrite_2, RST, SignedExt, SRAV, Sys, W1, W2, W3, WE,
       \数据相关 , \片选 , \硬布线控制器_1_alu_src ;
  wire [3:0] ALUOP, ALUOP_1;
  wire [4:0] EX_rd, EX_rt, EX_WriteReg_num, ID_R1_num, ID_R2_num, MEM_rd, MEM_rt, MEM_WriteReg_num,
       multiplexer_7_out, multiplexer_9_out, multiplexer_12_out, multiplexer_14_out, multiplexer_15_out, rd,
       rt, shamt_1;
  wire [5:0] Func;
  wire [15:0] \LoadUse次数 , multiplexer_17_out, multiplexer_17_out_2, \总周期数 , \插入气泡数 , \无条件分支数 , \条件分支成功数 ;
  wire [25:0] ex_mem_1_addr_26_2;
  wire [27:2] id_ex_1_addr_26_2;
  wire [31:0] adder_1_out, adder_3_out, bit_extender_1_out, bit_extender_2_out, bit_extender_3_out,
       bit_extender_4_out, bit_extender_5_out, EX__rs, EX_IMM, ex_mem_1_a_2, ex_mem_1_alu_2, ex_mem_1_b_2,
       ex_mem_1_ir_2, EX_PC, \id_ex_1_addr_有_2 , id_ex_1_b_2, id_ex_1_ir_2, id_ex_1_r2_2, ID_PC, IF_PC,
       LedData, MEM_PC, mem_wb_1_a_2, mem_wb_1_b_2, mem_wb_1_ir_2, mem_wb_1_md_2, mips_alu_1_result,
       mips_regifile_1_r1, mips_regifile_1_r2, multiplexer_1_out, multiplexer_2_out, multiplexer_3_out,
       multiplexer_4_out, multiplexer_8_out, multiplexer_10_out, multiplexer_11_out, multiplexer_18_out,
       multiplexer_19_out, PC_q, ram_1_data, rom_1_data, shifter_1_out, WB_PC;
  wire [31:6] IR;

  Button \u_总复位  (.out(RST));
  Button _1 (.out(IR1));
  Button _2 (.out(IR2));
  Button _3 (.out(IR3));
  Button \u_继续运行  (.out(Go));
  LED led_1 (.in(W1));
  LED led_2 (.in(W2));
  LED led_3 (.in(W3));
  Multiplexer #(.width(32), .enable("false")) multiplexer_1 (
    .in0(IF_PC), .in1(\id_ex_1_addr_有_2 ), .out(multiplexer_1_out), .sel(\EX_Branch_有 ));
  Hex_Digit_Display hex_digit_display_1 (.value(LedData[31:28]));  // open: dp
  or or_1 (or_1_out, EX_JMP, EX_JR);
  Multiplexer #(.width(32), .enable("false")) multiplexer_2 (
    .in0(multiplexer_4_out), .in1({EX_PC[31:28], id_ex_1_addr_26_2, 2'b00}), .out(multiplexer_2_out),
    .sel(EX_JMP));
  Multiplexer #(.width(32), .enable("false")) multiplexer_3 (
    .in0(multiplexer_2_out), .in1(EX__rs), .out(multiplexer_3_out), .sel(EX_JR));
  Comparator #(.width(32)) comparator_1 (.a(EX__rs), .b({32{1'b0}}), .lt(comparator_1_lt));  // open: gt, eq
  Hex_Digit_Display hex_digit_display_2 (.value(LedData[23:20]));  // open: dp
  Hex_Digit_Display hex_digit_display_3 (.value(LedData[27:24]));  // open: dp
  Counter #(.width(16), .max('hffff), .ongoal("stay")) counter_1 (
    .count(or_1_out), .Q(\无条件分支数 ), .clk(CLK), .clr(RST));  // open: load, D, carry
  Counter #(.width(16), .max('hffff), .ongoal("stay")) counter_2 (
    .count(and_1_out), .Q(\插入气泡数 ), .clk(CLK), .clr(RST));  // open: load, D, carry
  and and_1 (and_1_out, \数据相关 , ~halt);  // AND_Gate
  Register #(.width(32)) PC (.D(multiplexer_3_out), .en(InUse), .Q(PC_q), .clk(CLK), .clr(RST));
  Multiplexer #(.width(32), .enable("false")) multiplexer_4 (
    .in0(multiplexer_1_out), .in1(adder_1_out), .out(multiplexer_4_out), .sel(EX_BLTZ_s));
  Adder #(.width(32)) adder_1 (.a(EX_IMM), .b(EX_PC), .out(adder_1_out));  // open: cin, cout
  and and_2 (EX_BLTZ_s, comparator_1_lt, EX_BLTZ);
  Hex_Digit_Display hex_digit_display_4 (.value(LedData[15:12]));  // open: dp
  Hex_Digit_Display hex_digit_display_5 (.value(LedData[19:16]));  // open: dp
  Hex_Digit_Display hex_digit_display_6 (.value(LedData[7:4]));  // open: dp
  Hex_Digit_Display hex_digit_display_7 (.value(LedData[11:8]));  // open: dp
  Clock clock_1 (.out(CLK));
  ROM #(.addrWidth(10), .dataWidth(32)) rom_1 (.addr(PC_q[11:2]), .data(rom_1_data));  // open: sel
  Adder #(.width(32)) adder_2 (.a(PC_q), .b(32'h4), .out(IF_PC));  // open: cin, cout
  not not_1 (not_1_out, \数据相关 );
  and and_3 (and_3_out, not_1_out, not_2_out);
  not not_2 (not_2_out, halt);
  Hex_Digit_Display hex_digit_display_8 (.value(LedData[3:0]));  // open: dp
  IF_ID if_id_1 (
    .IR(rom_1_data), .IR_2({IR, Func}), .clk(CLK), .halt(and_3_out), .rst(or_2_out), .PC(IF_PC), .PC_2(ID_PC));  // open: 预测跳转, 预测跳转_2, 预测地址, 预测地址_2, Hit, Hit_2, HitPos, HitPos_2
  // Probe on \总周期数 
  // Probe on \无条件分支数 
  // Probe on \条件分支成功数 
  // Probe on \插入气泡数 
  // Probe on \LoadUse次数 
  or or_2 (or_2_out, EX_Branch, RST);
  // Probe on IF_PC[11:0]
  \硬布线控制器  \u_硬布线控制器_1  (
    .Func(Func), .OP(IR[31:26]), .ALU_OP(ALUOP), .MemToReg(MemToReg), .MemWrite(MemWrite),
    .ALU_SRC(\硬布线控制器_1_alu_src ), .RegWrite(RegWrite), .SysCALL(Sys), .SignedExt(SignedExt), .RegDst(RegDst),
    .JR(JR), .JMP(JMP), .Beq(Beq), .JAL(Jal), .Bne(Bne), .SRAV(SRAV), .LH(LH), .BLTZ(BLTZ));  // open: ERET
  Multiplexer #(.width(5), .enable("false")) multiplexer_5 (
    .in0(IR[25:21]), .in1(5'b00100), .out(ID_R1_num), .sel(Sys));
  // Probe on ID_PC[11:0]
  Multiplexer #(.width(5), .enable("false")) multiplexer_6 (
    .in0(IR[20:16]), .in1(5'b00010), .out(ID_R2_num), .sel(Sys));
  Multiplexer #(.width(5), .enable("false")) multiplexer_7 (
    .in0(rt), .in1(rd), .out(multiplexer_7_out), .sel(RegDst_r));
  assign bit_extender_1_out = {{16{1'b0}}, {IR[15:6], Func}};  // Bit_Extender bit_extender_1
  Multiplexer #(.width(32), .enable("false")) multiplexer_8 (
    .in0(bit_extender_1_out), .in1(bit_extender_2_out), .out(multiplexer_8_out), .sel(SignedExt));
  assign bit_extender_2_out = {{16{IR[15]}}, {IR[15:6], Func}};  // Bit_Extender bit_extender_2
  // Probe on EX_PC[11:0]
  // Probe on MEM_PC[11:0]
  Multiplexer #(.width(5), .enable("false")) multiplexer_9 (
    .in0(multiplexer_7_out), .in1({5{1'b1}}), .out(multiplexer_9_out), .sel(mem_wb_1_jal_2));
  // Probe on WB_PC[11:0]
  Multiplexer #(.width(32), .enable("false")) multiplexer_10 (
    .in0(mem_wb_1_md_2), .in1(WB_PC), .out(multiplexer_10_out), .sel(mem_wb_1_jal_2));
  Shifter #(.width(32)) shifter_1 (.in(bit_extender_2_out), .\dist (5'b00010), .out(shifter_1_out));
  not not_3 (not_3_out, CLK);
  Adder #(.width(32)) adder_3 (.a(shifter_1_out), .b(ID_PC), .out(adder_3_out));  // open: cin, cout
  or or_3 (or_3_out, or_2_out, \数据相关 );
  MIPS_Regifile mips_regifile_1 (
    .Din(multiplexer_10_out), .Clk(not_3_out), .R1(mips_regifile_1_r1), .R2(mips_regifile_1_r2), .WE(WE),
    .W_num(multiplexer_9_out), .R1_num(ID_R1_num), .R2_num(ID_R2_num));
  Multiplexer #(.width(32), .enable("false")) multiplexer_11 (
    .in0(mips_regifile_1_r2), .in1(multiplexer_8_out), .out(multiplexer_11_out), .sel(\硬布线控制器_1_alu_src ));
  \数据相关检测  \u_数据相关检测_1  (
    .OP(IR[31:26]), .EX_WriteReg_num(EX_WriteReg_num), .EX_RegWrite(EX_RegWrite),
    .MEM_WriteReg_num(MEM_WriteReg_num), .MEM_RegWrite(RegWrite_2), .\数据相关 (\数据相关 ), .Func(Func),
    .ID_R1_num(ID_R1_num), .ID_R2_num(ID_R2_num));
  ID_EX id_ex_1 (
    .IR({IR, Func}), .PC(ID_PC), .A(mips_regifile_1_r1), .B(multiplexer_11_out), .Shamt(IR[10:6]),
    .MemToReg(MemToReg), .MemWrite(MemWrite), .ALUOP(ALUOP), .RegWrite(RegWrite), .RegDst(RegDst),
    .R2(mips_regifile_1_r2), .Syscall(Sys), .IR_2({id_ex_1_ir_2[31:21], EX_rt, EX_rd, id_ex_1_ir_2[10:0]}),
    .PC_2(EX_PC), .A_2(EX__rs), .B_2(id_ex_1_b_2), .Shamt_2(shamt_1), .MemToReg_2(id_ex_1_memtoreg_2),
    .MemWrite_2(id_ex_1_memwrite_2), .ALUOP_2(ALUOP_1), .RegWrite_2(EX_RegWrite), .RegDst_2(EX_RegDst),
    .R2_2(id_ex_1_r2_2), .Syscall_2(id_ex_1_syscall_2), .clk(CLK), .halt(not_2_out), .rst(or_3_out),
    .Beq(Beq), .Beq_2(EX_Beq), .Bne(Bne), .Bne_2(EX_Bne), .Jal(Jal), .Jal_2(EX_Jal), .JMP(JMP),
    .JMP_2(EX_JMP), .JR(JR), .JR_2(EX_JR), .\Addr_有 (adder_3_out), .\Addr_有_2 (\id_ex_1_addr_有_2 ),
    .Addr_26({IR[25:6], Func}), .Addr_26_2(id_ex_1_addr_26_2), .SRAV(SRAV), .SRAV_2(EX_SRAV), .LH(LH),
    .LH_2(EX_LH), .BLTZ(BLTZ), .BLTZ_2(EX_BLTZ));  // open: ALU_SRC, ALU_SRC_2, IMM, IMM_2, 预测跳转, 预测跳转_2, 预测地址, 预测地址_2, Hit, Hit_2, HitPos, HitPos_2, ERET, ERET_2
  or or_4 (EX_Branch, EX_JMP, \EX_Branch_有 , EX_JR);
  Multiplexer #(.width(5), .enable("false")) multiplexer_12 (
    .in0(EX_rt), .in1(EX_rd), .out(multiplexer_12_out), .sel(EX_RegDst));
  Counter #(.width(16), .max('hffff)) counter_3 (
    .count(or_5_out), .Q(\总周期数 ), .clk(CLK), .clr(RST));  // open: load, D, carry
  or or_5 (or_5_out, ~halt, InUse);  // OR_Gate
  assign bit_extender_3_out = {{16{EX_rd[4]}}, {EX_rd, id_ex_1_ir_2[10:0]}};  // Bit_Extender bit_extender_3
  MIPS_ALU mips_alu_1 (
    .X(EX__rs), .Y(id_ex_1_b_2), .AluOP(ALUOP_1), .Equal(mips_alu_1_equal), .Result(mips_alu_1_result),
    .shamt(multiplexer_14_out));  // open: Result_2
  Multiplexer #(.width(5), .enable("false")) multiplexer_13 (
    .in0(multiplexer_12_out), .in1({5{1'b1}}), .out(EX_WriteReg_num), .sel(EX_Jal));
  Shifter #(.width(32)) shifter_2 (.in(bit_extender_3_out), .\dist (5'b00010), .out(EX_IMM));
  and and_4 (and_4_out, EX_Beq, mips_alu_1_equal);
  and and_5 (and_5_out, EX_Bne, ~mips_alu_1_equal);  // AND_Gate
  Multiplexer #(.width(5), .enable("false")) multiplexer_14 (
    .in0(shamt_1), .in1(EX__rs[4:0]), .out(multiplexer_14_out), .sel(EX_SRAV));
  or or_6 (\EX_Branch_有 , and_4_out, EX_BLTZ_s, and_5_out);
  Counter #(.width(16), .max('hffff)) counter_4 (
    .count(\EX_Branch_有 ), .Q(\条件分支成功数 ), .clk(CLK), .clr(RST));  // open: load, D, carry
  Multiplexer #(.width(5), .enable("false")) multiplexer_15 (
    .in0(MEM_rt), .in1(MEM_rd), .out(multiplexer_15_out), .sel(RegDst_2));
  EX_MEM ex_mem_1 (
    .IR({id_ex_1_ir_2[31:21], EX_rt, EX_rd, id_ex_1_ir_2[10:0]}), .PC(EX_PC), .Alu(mips_alu_1_result),
    .A(EX__rs), .B(id_ex_1_r2_2), .MemToReg(id_ex_1_memtoreg_2), .MemWrite(id_ex_1_memwrite_2),
    .RegWrite(EX_RegWrite), .RegDst(EX_RegDst), .Syscall(id_ex_1_syscall_2),
    .IR_2({ex_mem_1_ir_2[31:21], MEM_rt, MEM_rd, ex_mem_1_ir_2[10:0]}), .PC_2(MEM_PC),
    .Alu_2({ex_mem_1_alu_2[31:2], \片选 , ex_mem_1_alu_2[0]}), .A_2(ex_mem_1_a_2), .B_2(ex_mem_1_b_2),
    .MemToReg_2(MemToReg_2), .MemWrite_2(ex_mem_1_memwrite_2), .RegWrite_2(RegWrite_2), .RegDst_2(RegDst_2),
    .Syscall_2(ex_mem_1_syscall_2), .clk(CLK), .halt(not_2_out), .rst(RST), .Jal(EX_Jal), .Jal_2(MEM_Jal),
    .Addr_26(id_ex_1_addr_26_2), .Addr_26_2(ex_mem_1_addr_26_2), .LH(EX_LH), .LH_2(ex_mem_1_lh_2));
  Multiplexer #(.width(5), .enable("false")) multiplexer_16 (
    .in0(multiplexer_15_out), .in1({5{1'b1}}), .out(MEM_WriteReg_num), .sel(MEM_Jal));
  Multiplexer #(.width(32), .enable("false")) multiplexer_17 (
    .in0({ex_mem_1_alu_2[31:2], \片选 , ex_mem_1_alu_2[0]}), .in1(ram_1_data),
    .out({multiplexer_17_out_2, multiplexer_17_out}), .sel(MemToReg_2));
  RAM #(.addrWidth(10), .dataWidth(32), .bus("separate")) ram_1 (
    .addr(ex_mem_1_alu_2[11:2]), .din(ex_mem_1_b_2), .data(ram_1_data), .str(ex_mem_1_memwrite_2),
    .sel(1'b1), .clk(CLK), .ld(MemToReg_2));  // open: clr
  assign bit_extender_4_out = {{16{multiplexer_17_out[15]}}, multiplexer_17_out};  // Bit_Extender bit_extender_4
  assign bit_extender_5_out = {{16{multiplexer_17_out_2[15]}}, multiplexer_17_out_2};  // Bit_Extender bit_extender_5
  Multiplexer #(.width(32), .enable("false")) multiplexer_18 (
    .in0(bit_extender_4_out), .in1(bit_extender_5_out), .out(multiplexer_18_out), .sel(\片选 ));
  Multiplexer #(.width(32), .enable("false")) multiplexer_19 (
    .in0({multiplexer_17_out_2, multiplexer_17_out}), .in1(multiplexer_18_out), .out(multiplexer_19_out),
    .sel(ex_mem_1_lh_2));
  MEM_WB mem_wb_1 (
    .IR({ex_mem_1_ir_2[31:21], MEM_rt, MEM_rd, ex_mem_1_ir_2[10:0]}), .PC(MEM_PC), .A(ex_mem_1_a_2),
    .MD(multiplexer_19_out), .RegWrite(RegWrite_2), .RegDst(RegDst_2), .Syscall(ex_mem_1_syscall_2),
    .IR_2({mem_wb_1_ir_2[31:21], rt, rd, mem_wb_1_ir_2[10:0]}), .PC_2(WB_PC), .A_2(mem_wb_1_a_2),
    .MD_2(mem_wb_1_md_2), .RegWrite_2(WE), .RegDst_2(RegDst_r), .Syscall_2(mem_wb_1_syscall_2), .clk(CLK),
    .halt(not_2_out), .rst(RST), .Jal(MEM_Jal), .Jal_2(mem_wb_1_jal_2), .Addr_26(ex_mem_1_addr_26_2),
    .B(ex_mem_1_b_2), .B_2(mem_wb_1_b_2));  // open: Addr_26_2
  and and_6 (and_6_out, mem_wb_1_syscall_2, comparator_2_eq);
  Register #(.width(32)) register_1 (.D(mem_wb_1_a_2), .en(and_6_out), .Q(LedData), .clk(CLK));  // open: clr
  Comparator #(.width(32)) comparator_2 (.a(mem_wb_1_b_2), .b(32'h22), .eq(comparator_2_eq));  // open: gt, lt
  and and_7 (and_7_out, mem_wb_1_syscall_2, ~comparator_2_eq);  // AND_Gate
  Register #(.width(1)) register_2 (.D(mem_wb_1_syscall_2), .en(and_7_out), .Q(halt), .clk(CLK), .clr(or_7_out));
  or or_7 (or_7_out, RST, Go);
  and and_8 (InUse, ~halt, ~\数据相关 );  // AND_Gate

  // Other names for the same wires on the sheet: IR[5:0] = Func; shamt[4:0] = IR[10:6]; OP[5:0] = IR[31:26];
  //   PC[31:0] = ID_PC

  // Notes on the sheet:
  //   中断源
  //   中断等待指示
  //   数码管输出
  //   指令存储器
  //   contents of rom_1 (hex, n*v repeats v):
  //   20110005 8100006 20110001 20120002 20130003 20140004 810000b 20110001 20120002 20130003 20140004
  //   8100010 20110001 20120002 20130003 20140004 8100015 20110001 20120002 20130003 20140004 810001a
  //   20110001 20120002 20130003 20140004 810001f 20110001 20120002 20130003 20140004 8100024 20110001
  //   20120002 20130003 20140004 8100029 20110001 20120002 20130003 20140004 2231ffff 1620ffe0 20100001
  //   201200ff 20110001 20130003 12120005 12100004 20110001 20120002 20130003 20140004 16310004 16320003
  //   20110001 20120002 20130003 c10003d 2002000a c 20100000 22100001 102020 20020022 c 3e00008
  //   Shamt
  //   OP
  //   Func
  //   rs
  //   rt
  //   Imm
  //   流水调试日志用
  //   rd
  //   rt
endmodule

module \重定向流水线  (
);

  wire and_1_out, and_3_out, and_4_out, and_5_out, and_6_out, and_7_out, Beq, BLTZ, Bne, CLK,
       comparator_1_lt, comparator_2_eq, EX_ALU_SRC, EX_Beq, EX_BLTZ, EX_BLTZ_s, EX_Bne, EX_Branch,
       \EX_Branch_有 , EX_JMP, EX_JR, EX_LH, ex_mem_1_lh_2, ex_mem_1_memwrite_2, ex_mem_1_syscall_2,
       EX_MemToReg, EX_SRAV, EX_Sys, Go, halt, id_ex_1_jal_2, id_ex_1_memwrite_2, id_ex_1_regdst_2,
       id_ex_1_regwrite_2, InUse, IR1, IR2, IR3, Jal, JMP, JR, LH, \LoadUse相关 , MEM_Jal, mem_wb_1_syscall_2,
       MemToReg, MemToReg_2, MemWrite, mips_alu_1_equal, not_1_out, not_2_out, not_3_out, or_1_out, or_2_out,
       or_3_out, or_4_out, or_7_out, RegDst, RegDst_2, RegDst_r, RegWrite, RegWrite_2, RST, SignedExt, SRAV,
       Sys, W1, W2, W3, WB_Jal, WE, \硬布线控制器_1_alu_src ;
  wire [1:0] forward_1_forward_r1, forward_1_forward_r2;
  wire [3:0] ALUOP, ALUOP_1;
  wire [4:0] EX_rt, ID_R1_num, ID_R2_num, MEM_rd, MEM_rt, MEM_WriteReg_num, multiplexer_7_out,
       multiplexer_9_out, multiplexer_12_out, multiplexer_13_out, multiplexer_14_out, multiplexer_18_out,
       multiplexer_19_out, rd, rt, shamt_1, WB_WriteReg_num;
  wire [5:0] ID_Func, ID_OP;
  wire [15:0] \LoadUse次数 , multiplexer_17_out, multiplexer_17_out_2, \总周期数 , \无条件分支数 , \条件分支成功数 ;
  wire [25:0] ex_mem_1_addr_26_2;
  wire [25:6] IR;
  wire [27:2] id_ex_1_addr_26_2;
  wire [31:0] adder_1_out, adder_3_out, ALU_Result, bit_extender_1_out, bit_extender_2_out,
       bit_extender_3_out, bit_extender_4_out, bit_extender_5_out, EX__rs, EX_IMM, EX_IMM_1, ex_mem_1_a_2,
       ex_mem_1_b_2, ex_mem_1_ir_2, EX_PC, EX_R2, \id_ex_1_addr_有_2 , id_ex_1_ir_2, ID_PC, IF_PC, LedData,
       MEM_PC, MEM_ReadData, mem_wb_1_a_2, mem_wb_1_b_2, mem_wb_1_ir_2, mem_wb_1_md_2, mips_alu_1_result,
       mips_regifile_1_r1, mips_regifile_1_r2, multiplexer_1_out, multiplexer_2_out, multiplexer_3_out,
       multiplexer_4_out, multiplexer_8_out, multiplexer_20_out, multiplexer_23_out, PC_q, R1_Final,
       R2_Final, R2_Final_1, ram_1_data, rom_1_data, shifter_1_out, WB_PC;

  Button \u_总复位  (.out(RST));
  Button _1 (.out(IR1));
  Button _2 (.out(IR2));
  Button _3 (.out(IR3));
  Button \u_继续运行  (.out(Go));
  LED led_1 (.in(W1));
  LED led_2 (.in(W2));
  LED led_3 (.in(W3));
  Multiplexer #(.width(32), .enable("false")) multiplexer_1 (
    .in0(IF_PC), .in1(\id_ex_1_addr_有_2 ), .out(multiplexer_1_out), .sel(\EX_Branch_有 ));
  Hex_Digit_Display hex_digit_display_1 (.value(LedData[31:28]));  // open: dp
  or or_1 (or_1_out, EX_JMP, EX_JR);
  and and_1 (and_1_out, \LoadUse相关 , ~halt);  // AND_Gate
  Multiplexer #(.width(32), .enable("false")) multiplexer_2 (
    .in0(multiplexer_4_out), .in1({EX_PC[31:28], id_ex_1_addr_26_2, 2'b00}), .out(multiplexer_2_out),
    .sel(EX_JMP));
  Multiplexer #(.width(32), .enable("false")) multiplexer_3 (
    .in0(multiplexer_2_out), .in1(R1_Final), .out(multiplexer_3_out), .sel(EX_JR));
  Comparator #(.width(32)) comparator_1 (.a(R1_Final), .b({32{1'b0}}), .lt(comparator_1_lt));  // open: gt, eq
  Hex_Digit_Display hex_digit_display_2 (.value(LedData[23:20]));  // open: dp
  Hex_Digit_Display hex_digit_display_3 (.value(LedData[27:24]));  // open: dp
  Counter #(.width(16), .max('hffff), .ongoal("stay")) counter_1 (
    .count(or_1_out), .Q(\无条件分支数 ), .clk(CLK), .clr(RST));  // open: load, D, carry
  Counter #(.width(16), .max('hffff), .ongoal("stay")) counter_2 (
    .count(and_1_out), .Q(\LoadUse次数 ), .clk(CLK), .clr(RST));  // open: load, D, carry
  Register #(.width(32)) PC (.D(multiplexer_3_out), .en(InUse), .Q(PC_q), .clk(CLK), .clr(RST));
  Adder #(.width(32)) adder_1 (.a(EX_IMM), .b(EX_PC), .out(adder_1_out));  // open: cin, cout
  and and_2 (EX_BLTZ_s, comparator_1_lt, EX_BLTZ);
  Hex_Digit_Display hex_digit_display_4 (.value(LedData[15:12]));  // open: dp
  Hex_Digit_Display hex_digit_display_5 (.value(LedData[19:16]));  // open: dp
  Multiplexer #(.width(32), .enable("false")) multiplexer_4 (
    .in0(multiplexer_1_out), .in1(adder_1_out), .out(multiplexer_4_out), .sel(EX_BLTZ_s));
  Hex_Digit_Display hex_digit_display_6 (.value(LedData[7:4]));  // open: dp
  Hex_Digit_Display hex_digit_display_7 (.value(LedData[11:8]));  // open: dp
  Clock clock_1 (.out(CLK));
  ROM #(.addrWidth(10), .dataWidth(32)) rom_1 (.addr(PC_q[11:2]), .data(rom_1_data));  // open: sel
  Adder #(.width(32)) adder_2 (.a(PC_q), .b(32'h4), .out(IF_PC));  // open: cin, cout
  not not_1 (not_1_out, \LoadUse相关 );
  and and_3 (and_3_out, not_1_out, not_2_out);
  not not_2 (not_2_out, halt);
  Hex_Digit_Display hex_digit_display_8 (.value(LedData[3:0]));  // open: dp
  IF_ID if_id_1 (
    .IR(rom_1_data), .IR_2({ID_OP, IR, ID_Func}), .clk(CLK), .halt(and_3_out), .rst(or_3_out), .PC(IF_PC),
    .PC_2(ID_PC));  // open: 预测跳转, 预测跳转_2, 预测地址, 预测地址_2, Hit, Hit_2, HitPos, HitPos_2
  // Probe on \总周期数 
  // Probe on \无条件分支数 
  // Probe on \条件分支成功数 
  // Probe on \LoadUse次数 
  // Probe on \LoadUse次数 
  or or_2 (or_2_out, ~halt, InUse);  // OR_Gate
  // Probe on IF_PC[11:0]
  Counter #(.width(16), .max('hffff)) counter_3 (
    .count(or_2_out), .Q(\总周期数 ), .clk(CLK), .clr(RST));  // open: load, D, carry
  \硬布线控制器  \u_硬布线控制器_1  (
    .Func(ID_Func), .OP(ID_OP), .ALU_OP(ALUOP), .MemToReg(MemToReg), .MemWrite(MemWrite),
    .ALU_SRC(\硬布线控制器_1_alu_src ), .RegWrite(RegWrite), .SysCALL(Sys), .SignedExt(SignedExt), .RegDst(RegDst),
    .JR(JR), .JMP(JMP), .Beq(Beq), .JAL(Jal), .Bne(Bne), .SRAV(SRAV), .LH(LH), .BLTZ(BLTZ));  // open: ERET
  Multiplexer #(.width(5), .enable("false")) multiplexer_5 (
    .in0(IR[25:21]), .in1(5'b00100), .out(ID_R1_num), .sel(Sys));
  // Probe on ID_PC[11:0]
  Multiplexer #(.width(5), .enable("false")) multiplexer_6 (
    .in0(IR[20:16]), .in1(5'b00010), .out(ID_R2_num), .sel(Sys));
  Multiplexer #(.width(5), .enable("false")) multiplexer_7 (
    .in0(rt), .in1(rd), .out(multiplexer_7_out), .sel(RegDst_r));
  assign bit_extender_1_out = {{16{1'b0}}, {IR[15:6], ID_Func}};  // Bit_Extender bit_extender_1
  Multiplexer #(.width(32), .enable("false")) multiplexer_8 (
    .in0(bit_extender_1_out), .in1(bit_extender_2_out), .out(multiplexer_8_out), .sel(SignedExt));
  assign bit_extender_2_out = {{16{IR[15]}}, {IR[15:6], ID_Func}};  // Bit_Extender bit_extender_2
  // Probe on MEM_PC[11:0]
  // Probe on EX_PC[11:0]
  or or_3 (or_3_out, EX_Branch, RST);
  Multiplexer #(.width(5), .enable("false")) multiplexer_9 (
    .in0(multiplexer_7_out), .in1({5{1'b1}}), .out(multiplexer_9_out), .sel(WB_Jal));
  // Probe on WB_PC[11:0]
  Multiplexer #(.width(32), .enable("false")) multiplexer_10 (
    .in0(mem_wb_1_md_2), .in1(WB_PC), .out(MEM_ReadData), .sel(WB_Jal));
  Shifter #(.width(32)) shifter_1 (.in(bit_extender_2_out), .\dist (5'b00010), .out(shifter_1_out));
  or or_4 (or_4_out, \LoadUse相关 , or_3_out);
  LoadUse loaduse_1 (
    .OP(ID_OP), .EX_MemToReg(EX_MemToReg), .EX_rt(EX_rt), .\数据相关 (\LoadUse相关 ), .Func(ID_Func),
    .ID_R1_num(ID_R1_num), .ID_R2_num(ID_R2_num));
  not not_3 (not_3_out, CLK);
  Adder #(.width(32)) adder_3 (.a(shifter_1_out), .b(ID_PC), .out(adder_3_out));  // open: cin, cout
  MIPS_Regifile mips_regifile_1 (
    .Din(MEM_ReadData), .Clk(not_3_out), .R1(mips_regifile_1_r1), .R2(mips_regifile_1_r2), .WE(WE),
    .W_num(multiplexer_9_out), .R1_num(ID_R1_num), .R2_num(ID_R2_num));
  Multiplexer #(.width(32), .enable("false")) multiplexer_11 (
    .in0(R2_Final_1), .in1(EX_IMM_1), .out(R2_Final), .sel(EX_ALU_SRC));
  ID_EX id_ex_1 (
    .IR({ID_OP, IR, ID_Func}), .PC(ID_PC), .A(mips_regifile_1_r1), .Shamt(IR[10:6]), .MemToReg(MemToReg),
    .MemWrite(MemWrite), .ALUOP(ALUOP), .RegWrite(RegWrite), .RegDst(RegDst), .R2(mips_regifile_1_r2),
    .Syscall(Sys), .IR_2({id_ex_1_ir_2[31:21], EX_rt, id_ex_1_ir_2[15:0]}), .PC_2(EX_PC), .A_2(EX__rs),
    .Shamt_2(shamt_1), .MemToReg_2(EX_MemToReg), .MemWrite_2(id_ex_1_memwrite_2), .ALUOP_2(ALUOP_1),
    .RegWrite_2(id_ex_1_regwrite_2), .RegDst_2(id_ex_1_regdst_2), .R2_2(EX_R2), .Syscall_2(EX_Sys),
    .clk(CLK), .halt(not_2_out), .rst(or_4_out), .Beq(Beq), .Beq_2(EX_Beq), .Bne(Bne), .Bne_2(EX_Bne),
    .Jal(Jal), .Jal_2(id_ex_1_jal_2), .JMP(JMP), .JMP_2(EX_JMP), .JR(JR), .JR_2(EX_JR),
    .\Addr_有 (adder_3_out), .\Addr_有_2 (\id_ex_1_addr_有_2 ), .Addr_26({IR, ID_Func}),
    .Addr_26_2(id_ex_1_addr_26_2), .SRAV(SRAV), .SRAV_2(EX_SRAV), .LH(LH), .LH_2(EX_LH), .BLTZ(BLTZ),
    .BLTZ_2(EX_BLTZ), .ALU_SRC(\硬布线控制器_1_alu_src ), .ALU_SRC_2(EX_ALU_SRC), .IMM(multiplexer_8_out),
    .IMM_2(EX_IMM_1));  // open: B, B_2, 预测跳转, 预测跳转_2, 预测地址, 预测地址_2, Hit, Hit_2, HitPos, HitPos_2, ERET, ERET_2
  Multiplexer #(.width(5), .enable("false")) multiplexer_12 (
    .in0(id_ex_1_ir_2[25:21]), .in1(5'b00100), .out(multiplexer_12_out), .sel(EX_Sys));
  or or_5 (EX_Branch, EX_JMP, \EX_Branch_有 , EX_JR);
  Forward forward_1 (
    .OP(id_ex_1_ir_2[31:26]), .WB_WriteReg_num(WB_WriteReg_num), .WB_RegWrite(WE),
    .MEM_WriteReg_num(MEM_WriteReg_num), .MEM_RegWrite(RegWrite_2), .Forward_R1(forward_1_forward_r1),
    .Func(id_ex_1_ir_2[5:0]), .EX_R1_num(multiplexer_12_out), .EX_R2_num(multiplexer_13_out),
    .Forward_R2(forward_1_forward_r2));
  Multiplexer #(.width(5), .enable("false")) multiplexer_13 (
    .in0(EX_rt), .in1(5'b00010), .out(multiplexer_13_out), .sel(EX_Sys));
  assign bit_extender_3_out = {{16{id_ex_1_ir_2[15]}}, id_ex_1_ir_2[15:0]};  // Bit_Extender bit_extender_3
  Shifter #(.width(32)) shifter_2 (.in(bit_extender_3_out), .\dist (5'b00010), .out(EX_IMM));
  and and_4 (and_4_out, EX_Beq, mips_alu_1_equal);
  and and_5 (and_5_out, EX_Bne, ~mips_alu_1_equal);  // AND_Gate
  MIPS_ALU mips_alu_1 (
    .X(R1_Final), .Y(R2_Final), .AluOP(ALUOP_1), .Equal(mips_alu_1_equal), .Result(mips_alu_1_result),
    .shamt(multiplexer_14_out));  // open: Result_2
  Multiplexer #(.width(5), .enable("false")) multiplexer_14 (
    .in0(shamt_1), .in1(EX__rs[4:0]), .out(multiplexer_14_out), .sel(EX_SRAV));
  or or_6 (\EX_Branch_有 , and_4_out, EX_BLTZ_s, and_5_out);
  Counter #(.width(16), .max('hffff)) counter_4 (
    .count(\EX_Branch_有 ), .Q(\条件分支成功数 ), .clk(CLK), .clr(RST));  // open: load, D, carry
  Multiplexer #(.select(2), .width(32), .enable("false")) multiplexer_15 (
    .in0(EX__rs), .in1(ALU_Result), .in2(MEM_ReadData), .out(R1_Final), .sel(forward_1_forward_r1));  // open: in3
  EX_MEM ex_mem_1 (
    .IR({id_ex_1_ir_2[31:21], EX_rt, id_ex_1_ir_2[15:0]}), .PC(EX_PC), .Alu(mips_alu_1_result), .A(R1_Final),
    .B(R2_Final_1), .MemToReg(EX_MemToReg), .MemWrite(id_ex_1_memwrite_2), .RegWrite(id_ex_1_regwrite_2),
    .RegDst(id_ex_1_regdst_2), .Syscall(EX_Sys),
    .IR_2({ex_mem_1_ir_2[31:21], MEM_rt, MEM_rd, ex_mem_1_ir_2[10:0]}), .PC_2(MEM_PC), .Alu_2(ALU_Result),
    .A_2(ex_mem_1_a_2), .B_2(ex_mem_1_b_2), .MemToReg_2(MemToReg_2), .MemWrite_2(ex_mem_1_memwrite_2),
    .RegWrite_2(RegWrite_2), .RegDst_2(RegDst_2), .Syscall_2(ex_mem_1_syscall_2), .clk(CLK),
    .halt(not_2_out), .rst(RST), .Jal(id_ex_1_jal_2), .Jal_2(MEM_Jal), .Addr_26(id_ex_1_addr_26_2),
    .Addr_26_2(ex_mem_1_addr_26_2), .LH(EX_LH), .LH_2(ex_mem_1_lh_2));
  Multiplexer #(.select(2), .width(32), .enable("false")) multiplexer_16 (
    .in0(EX_R2), .in1(ALU_Result), .in2(MEM_ReadData), .out(R2_Final_1), .sel(forward_1_forward_r2));  // open: in3
  Multiplexer #(.width(32), .enable("false")) multiplexer_17 (
    .in0(ALU_Result), .in1(ram_1_data), .out({multiplexer_17_out_2, multiplexer_17_out}), .sel(MemToReg_2));
  RAM #(.addrWidth(10), .dataWidth(32), .bus("separate")) ram_1 (
    .addr(ALU_Result[11:2]), .din(ex_mem_1_b_2), .data(ram_1_data), .str(ex_mem_1_memwrite_2), .sel(1'b1),
    .clk(CLK), .ld(MemToReg_2));  // open: clr
  assign bit_extender_4_out = {{16{multiplexer_17_out[15]}}, multiplexer_17_out};  // Bit_Extender bit_extender_4
  assign bit_extender_5_out = {{16{multiplexer_17_out_2[15]}}, multiplexer_17_out_2};  // Bit_Extender bit_extender_5
  Multiplexer #(.width(5), .enable("false")) multiplexer_18 (
    .in0(rt), .in1(rd), .out(multiplexer_18_out), .sel(RegDst_r));
  Multiplexer #(.width(5), .enable("false")) multiplexer_19 (
    .in0(MEM_rt), .in1(MEM_rd), .out(multiplexer_19_out), .sel(RegDst_2));
  Multiplexer #(.width(32), .enable("false")) multiplexer_20 (
    .in0(bit_extender_4_out), .in1(bit_extender_5_out), .out(multiplexer_20_out), .sel(ALU_Result[1]));
  Multiplexer #(.width(5), .enable("false")) multiplexer_21 (
    .in0(multiplexer_18_out), .in1({5{1'b1}}), .out(WB_WriteReg_num), .sel(WB_Jal));
  Multiplexer #(.width(5), .enable("false")) multiplexer_22 (
    .in0(multiplexer_19_out), .in1({5{1'b1}}), .out(MEM_WriteReg_num), .sel(MEM_Jal));
  Multiplexer #(.width(32), .enable("false")) multiplexer_23 (
    .in0({multiplexer_17_out_2, multiplexer_17_out}), .in1(multiplexer_20_out), .out(multiplexer_23_out),
    .sel(ex_mem_1_lh_2));
  MEM_WB mem_wb_1 (
    .IR({ex_mem_1_ir_2[31:21], MEM_rt, MEM_rd, ex_mem_1_ir_2[10:0]}), .PC(MEM_PC), .A(ex_mem_1_a_2),
    .MD(multiplexer_23_out), .RegWrite(RegWrite_2), .RegDst(RegDst_2), .Syscall(ex_mem_1_syscall_2),
    .IR_2({mem_wb_1_ir_2[31:21], rt, rd, mem_wb_1_ir_2[10:0]}), .PC_2(WB_PC), .A_2(mem_wb_1_a_2),
    .MD_2(mem_wb_1_md_2), .RegWrite_2(WE), .RegDst_2(RegDst_r), .Syscall_2(mem_wb_1_syscall_2), .clk(CLK),
    .halt(not_2_out), .rst(RST), .Jal(MEM_Jal), .Jal_2(WB_Jal), .Addr_26(ex_mem_1_addr_26_2),
    .B(ex_mem_1_b_2), .B_2(mem_wb_1_b_2));  // open: Addr_26_2
  and and_6 (and_6_out, mem_wb_1_syscall_2, comparator_2_eq);
  Register #(.width(32)) register_1 (.D(mem_wb_1_a_2), .en(and_6_out), .Q(LedData), .clk(CLK));  // open: clr
  Comparator #(.width(32)) comparator_2 (.a(mem_wb_1_b_2), .b(32'h22), .eq(comparator_2_eq));  // open: gt, lt
  and and_7 (and_7_out, mem_wb_1_syscall_2, ~comparator_2_eq);  // AND_Gate
  Register #(.width(1)) register_2 (.D(mem_wb_1_syscall_2), .en(and_7_out), .Q(halt), .clk(CLK), .clr(or_7_out));
  or or_7 (or_7_out, RST, Go);
  and and_8 (InUse, ~halt, ~\LoadUse相关 );  // AND_Gate

  // Other names for the same wires on the sheet: 片选 = ALU_Result[1]; IR (some bits) = {ID_OP, ID_Func};
  //   shamt[4:0] = IR[10:6]; PC[31:0] = ID_PC; 插入气泡数[15:0] = \LoadUse次数 

  // Notes on the sheet:
  //   中断源
  //   中断等待指示
  //   数码管输出
  //   指令存储器
  //   contents of rom_1 (hex, n*v repeats v):
  //   20110005 8100006 20110001 20120002 20130003 20140004 810000b 20110001 20120002 20130003 20140004
  //   8100010 20110001 20120002 20130003 20140004 8100015 20110001 20120002 20130003 20140004 810001a
  //   20110001 20120002 20130003 20140004 810001f 20110001 20120002 20130003 20140004 8100024 20110001
  //   20120002 20130003 20140004 8100029 20110001 20120002 20130003 20140004 2231ffff 1620ffe0 20100001
  //   201200ff 20110001 20130003 12120005 12100004 20110001 20120002 20130003 20140004 16310004 16320003
  //   20110001 20120002 20130003 c10003d 2002000a c 20100000 22100001 102020 20020022 c 3e00008
  //   Shamt
  //   OP
  //   Func
  //   rs
  //   rt
  //   Imm
  //   流水调试日志用
  //   OP
  //   Func
  //   rs
  //   rt
  //   rd
  //   rt
endmodule

module Forward (
  input  [5:0] OP,
  input  [4:0] WB_WriteReg_num,
  input  WB_RegWrite,
  input  [4:0] MEM_WriteReg_num,
  input  MEM_RegWrite,
  input  [5:0] Func,
  input  [4:0] EX_R1_num,
  input  [4:0] EX_R2_num,
  output [1:0] Forward_R1,
  output [1:0] Forward_R2
);

  wire comparator_1_eq, comparator_2_eq, comparator_3_eq, comparator_4_eq, comparator_5_eq, comparator_6_eq,
       \源寄存器使用情况_1_r1_used , \源寄存器使用情况_1_r2_used ;
  wire [1:0] and_2_out, and_3_out;

  \源寄存器使用情况  \u_源寄存器使用情况_1  (
    .OP0(OP[0]), .OP1(OP[1]), .OP2(OP[2]), .OP3(OP[3]), .OP4(OP[4]), .OP5(OP[5]), .F0(Func[0]), .F1(Func[1]),
    .F2(Func[2]), .F3(Func[3]), .F4(Func[4]), .F5(Func[5]), .R1_Used(\源寄存器使用情况_1_r1_used ),
    .R2_Used(\源寄存器使用情况_1_r2_used ));
  Comparator #(.width(5)) comparator_1 (.a(EX_R1_num), .b(WB_WriteReg_num), .eq(comparator_1_eq));  // open: gt, lt
  Comparator #(.width(5)) comparator_2 (.a(EX_R1_num), .b(MEM_WriteReg_num), .eq(comparator_2_eq));  // open: gt, lt
  Comparator #(.width(5)) comparator_3 (.a(EX_R2_num), .b(MEM_WriteReg_num), .eq(comparator_3_eq));  // open: gt, lt
  Comparator #(.width(5)) comparator_4 (.a(EX_R2_num), .b(WB_WriteReg_num), .eq(comparator_4_eq));  // open: gt, lt
  and and_1 (and_2_out[1], comparator_1_eq, WB_RegWrite, \源寄存器使用情况_1_r1_used );
  and and_2 (and_2_out[0], comparator_2_eq, MEM_RegWrite, \源寄存器使用情况_1_r1_used );
  and and_3 (and_3_out[0], comparator_3_eq, MEM_RegWrite, \源寄存器使用情况_1_r2_used );
  and and_4 (and_3_out[1], comparator_4_eq, WB_RegWrite, \源寄存器使用情况_1_r2_used );
  Comparator #(.width(5)) comparator_5 (.a(EX_R1_num), .b({5{1'b0}}), .eq(comparator_5_eq));  // open: gt, lt
  Comparator #(.width(5)) comparator_6 (.a(EX_R2_num), .b({5{1'b0}}), .eq(comparator_6_eq));  // open: gt, lt
  Multiplexer #(.width(2), .enable("false")) multiplexer_1 (
    .in0(and_2_out), .in1(2'b00), .out(Forward_R1), .sel(comparator_5_eq));
  Multiplexer #(.width(2), .enable("false")) multiplexer_2 (
    .in0(and_3_out), .in1(2'b00), .out(Forward_R2), .sel(comparator_6_eq));

  // Other names for the same wires on the sheet: OP_CODE[5:0] = OP
endmodule

module LoadUse (
  input  [5:0] OP,
  input  EX_MemToReg,
  input  [4:0] EX_rt,
  input  [5:0] Func,
  input  [4:0] ID_R1_num,
  input  [4:0] ID_R2_num,
  output \数据相关 
);

  wire and_1_out, and_2_out, and_3_out, and_4_out, comparator_1_eq, comparator_2_eq, comparator_3_eq,
       comparator_4_eq, \源寄存器使用情况_1_r1_used , \源寄存器使用情况_1_r2_used ;

  \源寄存器使用情况  \u_源寄存器使用情况_1  (
    .OP0(OP[0]), .OP1(OP[1]), .OP2(OP[2]), .OP3(OP[3]), .OP4(OP[4]), .OP5(OP[5]), .F0(Func[0]), .F1(Func[1]),
    .F2(Func[2]), .F3(Func[3]), .F4(Func[4]), .F5(Func[5]), .R1_Used(\源寄存器使用情况_1_r1_used ),
    .R2_Used(\源寄存器使用情况_1_r2_used ));
  Comparator #(.width(5)) comparator_1 (.a(ID_R2_num), .b(EX_rt), .eq(comparator_1_eq));  // open: gt, lt
  Comparator #(.width(5)) comparator_2 (.a(ID_R1_num), .b(EX_rt), .eq(comparator_2_eq));  // open: gt, lt
  and and_1 (and_1_out, comparator_2_eq, EX_MemToReg, \源寄存器使用情况_1_r1_used );
  and and_2 (and_2_out, comparator_1_eq, EX_MemToReg, \源寄存器使用情况_1_r2_used );
  Comparator #(.width(5)) comparator_3 (.a(ID_R1_num), .b({5{1'b0}}), .eq(comparator_3_eq));  // open: gt, lt
  Comparator #(.width(5)) comparator_4 (.a(ID_R2_num), .b({5{1'b0}}), .eq(comparator_4_eq));  // open: gt, lt
  and and_3 (and_3_out, ~comparator_3_eq, and_1_out);  // AND_Gate
  and and_4 (and_4_out, ~comparator_4_eq, and_2_out);  // AND_Gate
  or or_1 (\数据相关 , and_3_out, and_4_out);

  // Other names for the same wires on the sheet: LoadUse相关 = \数据相关 ; OP_CODE[5:0] = OP
endmodule

module \分支预测  (
);

  wire and_1_out, and_2_out, and_4_out, and_6_out, and_7_out, and_8_out, and_9_out, and_10_out, and_11_out,
       Beq, BLTZ, Bne, CLK, comparator_1_lt, comparator_2_eq, comparator_3_eq, EX_ALU_SRC, EX_Beq, EX_BLTZ,
       EX_BLTZ_s, EX_Bne, EX_Branch, \EX_Branch_有 , EX_Hit, EX_JMP, EX_JR, EX_LH, ex_mem_1_lh_2,
       ex_mem_1_memwrite_2, ex_mem_1_syscall_2, EX_MemToReg, EX_SRAV, EX_Sys, \EX_预测跳转 , Go, halt, Hit,
       id_ex_1_jal_2, id_ex_1_memwrite_2, id_ex_1_regdst_2, id_ex_1_regwrite_2, if_id_1_hit_2,
       \if_id_1_预测跳转_2 , InUse, IR1, IR2, IR3, Jal, JMP, JR, LH, \LoadUse相关 , MEM_Jal, mem_wb_1_syscall_2,
       MemToReg, MemToReg_2, MemWrite, mips_alu_1_equal, not_1_out, not_2_out, not_3_out, not_4_out,
       not_5_out, or_1_out, or_2_out, or_3_out, or_4_out, or_8_out, RegDst, RegDst_2, RegDst_r, RegWrite,
       RegWrite_2, RST, SignedExt, SRAV, Sys, W1, W2, W3, WB_Jal, WE, \硬布线控制器_1_alu_src , \预测失败 , \预测成功 ,
       \预测跳转 ;
  wire [1:0] forward_1_forward_r1, forward_1_forward_r2;
  wire [2:0] bht_1_hitpos, EX_HitPos, if_id_1_hitpos_2;
  wire [3:0] ALUOP, ALUOP_1;
  wire [4:0] EX_rt, ID_R1_num, ID_R2_num, MEM_rd, MEM_rt, MEM_WriteReg_num, multiplexer_10_out,
       multiplexer_12_out, multiplexer_15_out, multiplexer_16_out, multiplexer_17_out, multiplexer_21_out,
       multiplexer_22_out, rd, rt, shamt_1, WB_WriteReg_num;
  wire [5:0] ID_Func, ID_OP;
  wire [15:0] \LoadUse次数 , multiplexer_20_out, multiplexer_20_out_2, \总周期数 , \无条件分支数 , \条件分支成功数 , \预测失败数 ,
       \预测成功数 ;
  wire [25:0] ex_mem_1_addr_26_2;
  wire [25:6] IR;
  wire [27:2] id_ex_1_addr_26_2;
  wire [31:0] adder_1_out, adder_3_out, ALU_Result, bit_extender_1_out, bit_extender_2_out,
       bit_extender_3_out, bit_extender_4_out, bit_extender_5_out, DestAddr, EX__rs, EX_IMM, EX_IMM_1,
       ex_mem_1_a_2, ex_mem_1_b_2, ex_mem_1_ir_2, EX_PC, EX_R2, \EX_预测地址 , \id_ex_1_addr_有_2 , id_ex_1_ir_2,
       ID_PC, \if_id_1_预测地址_2 , IF_PC, LedData, MEM_PC, MEM_ReadData, mem_wb_1_a_2, mem_wb_1_b_2,
       mem_wb_1_ir_2, mem_wb_1_md_2, mips_alu_1_result, mips_regifile_1_r1, mips_regifile_1_r2,
       multiplexer_1_out, multiplexer_3_out, multiplexer_4_out, multiplexer_5_out, multiplexer_6_out,
       multiplexer_7_out, multiplexer_11_out, multiplexer_23_out, multiplexer_26_out, PC_q, R1_Final,
       R2_Final, R2_Final_1, ram_1_data, rom_1_data, shifter_1_out, subtractor_1_out, WB_PC, \预测地址 ;

  Button \u_总复位  (.out(RST));
  Button _1 (.out(IR1));
  Button _2 (.out(IR2));
  Button _3 (.out(IR3));
  Button \u_继续运行  (.out(Go));
  LED led_1 (.in(W1));
  LED led_2 (.in(W2));
  LED led_3 (.in(W3));
  Multiplexer #(.width(32), .enable("false")) multiplexer_1 (
    .in0(IF_PC), .in1(\id_ex_1_addr_有_2 ), .out(multiplexer_1_out), .sel(\EX_Branch_有 ));
  Hex_Digit_Display hex_digit_display_1 (.value(LedData[31:28]));  // open: dp
  Multiplexer #(.width(32), .enable("false")) multiplexer_2 (
    .in0(multiplexer_7_out), .in1({EX_PC[31:28], id_ex_1_addr_26_2, 2'b00}), .out(DestAddr), .sel(EX_JMP));
  Multiplexer #(.width(32), .enable("false")) multiplexer_3 (
    .in0(multiplexer_6_out), .in1(R1_Final), .out(multiplexer_3_out), .sel(EX_JR));
  Comparator #(.width(32)) comparator_1 (.a(R1_Final), .b({32{1'b0}}), .lt(comparator_1_lt));  // open: gt, eq
  and and_1 (and_1_out, \LoadUse相关 , ~halt);  // AND_Gate
  or or_1 (or_1_out, EX_JMP, EX_JR);
  Hex_Digit_Display hex_digit_display_2 (.value(LedData[27:24]));  // open: dp
  Hex_Digit_Display hex_digit_display_3 (.value(LedData[23:20]));  // open: dp
  and and_2 (and_2_out, \预测跳转 , Hit);
  Multiplexer #(.width(32), .enable("false")) multiplexer_4 (
    .in0(IF_PC), .in1(\预测地址 ), .out(multiplexer_4_out), .sel(and_2_out));
  Multiplexer #(.width(32), .enable("false")) multiplexer_5 (
    .in0(EX_PC), .in1(DestAddr), .out(multiplexer_5_out), .sel(EX_Branch));
  Register #(.width(32)) PC (.D(multiplexer_3_out), .en(InUse), .Q(PC_q), .clk(CLK), .clr(RST));
  Subtractor #(.width(32)) subtractor_1 (.a(EX_PC), .b(32'h4), .out(subtractor_1_out));  // open: bin, bout
  Adder #(.width(32)) adder_1 (.a(EX_IMM), .b(EX_PC), .out(adder_1_out));  // open: cin, cout
  and and_3 (EX_BLTZ_s, comparator_1_lt, EX_BLTZ);
  Counter #(.width(16), .max('hffff), .ongoal("stay")) counter_1 (
    .count(and_1_out), .Q(\LoadUse次数 ), .clk(CLK), .clr(RST));  // open: load, D, carry
  Counter #(.width(16), .max('hffff), .ongoal("stay")) counter_2 (
    .count(or_1_out), .Q(\无条件分支数 ), .clk(CLK), .clr(RST));  // open: load, D, carry
  Hex_Digit_Display hex_digit_display_4 (.value(LedData[19:16]));  // open: dp
  Hex_Digit_Display hex_digit_display_5 (.value(LedData[15:12]));  // open: dp
  Multiplexer #(.width(32), .enable("false")) multiplexer_6 (
    .in0(multiplexer_4_out), .in1(multiplexer_5_out), .out(multiplexer_6_out), .sel(\预测失败 ));
  Multiplexer #(.width(32), .enable("false")) multiplexer_7 (
    .in0(multiplexer_1_out), .in1(adder_1_out), .out(multiplexer_7_out), .sel(EX_BLTZ_s));
  Hex_Digit_Display hex_digit_display_6 (.value(LedData[7:4]));  // open: dp
  Hex_Digit_Display hex_digit_display_7 (.value(LedData[11:8]));  // open: dp
  Clock clock_1 (.out(CLK));
  ROM #(.addrWidth(10), .dataWidth(32)) rom_1 (.addr(PC_q[11:2]), .data(rom_1_data));  // open: sel
  Adder #(.width(32)) adder_2 (.a(PC_q), .b(32'h4), .out(IF_PC));  // open: cin, cout
  BHT bht_1 (
    .Rst(RST), .HitPos_3(EX_HitPos), .Clk(CLK), .PC_3(subtractor_1_out), .PC(PC_q), .DstAddr(DestAddr),
    .\分支成功 (EX_Branch), .Hit_3(EX_Hit), .JumpBack_3(EX_Branch), .\预测跳转 (\预测跳转 ), .\预测地址 (\预测地址 ), .Hit(Hit),
    .HitPos(bht_1_hitpos));
  not not_1 (not_1_out, \LoadUse相关 );
  and and_4 (and_4_out, not_1_out, not_2_out);
  not not_2 (not_2_out, halt);
  Hex_Digit_Display hex_digit_display_8 (.value(LedData[3:0]));  // open: dp
  IF_ID if_id_1 (
    .IR(rom_1_data), .IR_2({ID_OP, IR, ID_Func}), .clk(CLK), .halt(and_4_out), .rst(or_3_out), .PC(IF_PC),
    .PC_2(ID_PC), .\预测跳转 (\预测跳转 ), .\预测跳转_2 (\if_id_1_预测跳转_2 ), .\预测地址 (\预测地址 ), .\预测地址_2 (\if_id_1_预测地址_2 ),
    .Hit(Hit), .Hit_2(if_id_1_hit_2), .HitPos(bht_1_hitpos), .HitPos_2(if_id_1_hitpos_2));
  // Probe on \总周期数 
  // Probe on \无条件分支数 
  // Probe on \条件分支成功数 
  // Probe on \LoadUse次数 
  // Probe on \LoadUse次数 
  or or_2 (or_2_out, ~halt, InUse);  // OR_Gate
  Counter #(.width(16), .max('hffff)) counter_3 (
    .count(or_2_out), .Q(\总周期数 ), .clk(CLK), .clr(RST));  // open: load, D, carry
  \硬布线控制器  \u_硬布线控制器_1  (
    .Func(ID_Func), .OP(ID_OP), .ALU_OP(ALUOP), .MemToReg(MemToReg), .MemWrite(MemWrite),
    .ALU_SRC(\硬布线控制器_1_alu_src ), .RegWrite(RegWrite), .SysCALL(Sys), .SignedExt(SignedExt), .RegDst(RegDst),
    .JR(JR), .JMP(JMP), .Beq(Beq), .JAL(Jal), .Bne(Bne), .SRAV(SRAV), .LH(LH), .BLTZ(BLTZ));  // open: ERET
  Multiplexer #(.width(5), .enable("false")) multiplexer_8 (
    .in0(IR[25:21]), .in1(5'b00100), .out(ID_R1_num), .sel(Sys));
  // Probe on \预测失败数 
  // Probe on \预测成功数 
  Multiplexer #(.width(5), .enable("false")) multiplexer_9 (
    .in0(IR[20:16]), .in1(5'b00010), .out(ID_R2_num), .sel(Sys));
  Multiplexer #(.width(5), .enable("false")) multiplexer_10 (
    .in0(rt), .in1(rd), .out(multiplexer_10_out), .sel(RegDst_r));
  assign bit_extender_1_out = {{16{1'b0}}, {IR[15:6], ID_Func}};  // Bit_Extender bit_extender_1
  Multiplexer #(.width(32), .enable("false")) multiplexer_11 (
    .in0(bit_extender_1_out), .in1(bit_extender_2_out), .out(multiplexer_11_out), .sel(SignedExt));
  assign bit_extender_2_out = {{16{IR[15]}}, {IR[15:6], ID_Func}};  // Bit_Extender bit_extender_2
  // Probe on IF_PC[11:0]
  // Probe on ID_PC[11:0]
  or or_3 (or_3_out, \预测失败 , RST);
  Multiplexer #(.width(5), .enable("false")) multiplexer_12 (
    .in0(multiplexer_10_out), .in1({5{1'b1}}), .out(multiplexer_12_out), .sel(WB_Jal));
  // Probe on EX_PC[11:0]
  Multiplexer #(.width(32), .enable("false")) multiplexer_13 (
    .in0(mem_wb_1_md_2), .in1(WB_PC), .out(MEM_ReadData), .sel(WB_Jal));
  Shifter #(.width(32)) shifter_1 (.in(bit_extender_2_out), .\dist (5'b00010), .out(shifter_1_out));
  Comparator #(.width(1)) comparator_2 (.a(EX_Branch), .b(\EX_预测跳转 ), .eq(comparator_2_eq));  // open: gt, lt
  // Probe on MEM_PC[11:0]
  // Probe on WB_PC[11:0]
  or or_4 (or_4_out, \LoadUse相关 , or_3_out);
  LoadUse loaduse_1 (
    .OP(ID_OP), .EX_MemToReg(EX_MemToReg), .EX_rt(EX_rt), .\数据相关 (\LoadUse相关 ), .Func(ID_Func),
    .ID_R1_num(ID_R1_num), .ID_R2_num(ID_R2_num));
  not not_3 (not_3_out, CLK);
  Adder #(.width(32)) adder_3 (.a(shifter_1_out), .b(ID_PC), .out(adder_3_out));  // open: cin, cout
  not not_4 (not_4_out, EX_Hit);
  not not_5 (not_5_out, comparator_2_eq);
  and and_5 (\预测成功 , EX_Hit, comparator_2_eq);
  MIPS_Regifile mips_regifile_1 (
    .Din(MEM_ReadData), .Clk(not_3_out), .R1(mips_regifile_1_r1), .R2(mips_regifile_1_r2), .WE(WE),
    .W_num(multiplexer_12_out), .R1_num(ID_R1_num), .R2_num(ID_R2_num));
  and and_6 (and_6_out, EX_Branch, not_4_out);
  and and_7 (and_7_out, EX_Hit, not_5_out);
  Multiplexer #(.width(32), .enable("false")) multiplexer_14 (
    .in0(R2_Final_1), .in1(EX_IMM_1), .out(R2_Final), .sel(EX_ALU_SRC));
  or or_5 (\预测失败 , and_6_out, and_7_out);
  ID_EX id_ex_1 (
    .IR({ID_OP, IR, ID_Func}), .PC(ID_PC), .A(mips_regifile_1_r1), .Shamt(IR[10:6]), .MemToReg(MemToReg),
    .MemWrite(MemWrite), .ALUOP(ALUOP), .RegWrite(RegWrite), .RegDst(RegDst), .R2(mips_regifile_1_r2),
    .Syscall(Sys), .IR_2({id_ex_1_ir_2[31:21], EX_rt, id_ex_1_ir_2[15:0]}), .PC_2(EX_PC), .A_2(EX__rs),
    .Shamt_2(shamt_1), .MemToReg_2(EX_MemToReg), .MemWrite_2(id_ex_1_memwrite_2), .ALUOP_2(ALUOP_1),
    .RegWrite_2(id_ex_1_regwrite_2), .RegDst_2(id_ex_1_regdst_2), .R2_2(EX_R2), .Syscall_2(EX_Sys),
    .clk(CLK), .halt(not_2_out), .rst(or_4_out), .Beq(Beq), .Beq_2(EX_Beq), .Bne(Bne), .Bne_2(EX_Bne),
    .Jal(Jal), .Jal_2(id_ex_1_jal_2), .JMP(JMP), .JMP_2(EX_JMP), .JR(JR), .JR_2(EX_JR),
    .\Addr_有 (adder_3_out), .\Addr_有_2 (\id_ex_1_addr_有_2 ), .Addr_26({IR, ID_Func}),
    .Addr_26_2(id_ex_1_addr_26_2), .SRAV(SRAV), .SRAV_2(EX_SRAV), .LH(LH), .LH_2(EX_LH), .BLTZ(BLTZ),
    .BLTZ_2(EX_BLTZ), .ALU_SRC(\硬布线控制器_1_alu_src ), .ALU_SRC_2(EX_ALU_SRC), .IMM(multiplexer_11_out),
    .IMM_2(EX_IMM_1), .\预测跳转 (\if_id_1_预测跳转_2 ), .\预测跳转_2 (\EX_预测跳转 ), .\预测地址 (\if_id_1_预测地址_2 ),
    .\预测地址_2 (\EX_预测地址 ), .Hit(if_id_1_hit_2), .Hit_2(EX_Hit), .HitPos(if_id_1_hitpos_2), .HitPos_2(EX_HitPos));  // open: B, B_2, ERET, ERET_2
  Counter #(.width(16), .max('hffff)) counter_4 (.count(\预测失败 ), .Q(\预测失败数 ), .clk(CLK));  // open: load, D, carry, clr
  // Probe on \预测失败数 
  Counter #(.width(16), .max('hffff)) counter_5 (.count(\预测成功 ), .Q(\预测成功数 ), .clk(CLK));  // open: load, D, carry, clr
  // Probe on \预测成功数 
  Multiplexer #(.width(5), .enable("false")) multiplexer_15 (
    .in0(id_ex_1_ir_2[25:21]), .in1(5'b00100), .out(multiplexer_15_out), .sel(EX_Sys));
  Forward forward_1 (
    .OP(id_ex_1_ir_2[31:26]), .WB_WriteReg_num(WB_WriteReg_num), .WB_RegWrite(WE),
    .MEM_WriteReg_num(MEM_WriteReg_num), .MEM_RegWrite(RegWrite_2), .Forward_R1(forward_1_forward_r1),
    .Func(id_ex_1_ir_2[5:0]), .EX_R1_num(multiplexer_15_out), .EX_R2_num(multiplexer_16_out),
    .Forward_R2(forward_1_forward_r2));
  Multiplexer #(.width(5), .enable("false")) multiplexer_16 (
    .in0(EX_rt), .in1(5'b00010), .out(multiplexer_16_out), .sel(EX_Sys));
  assign bit_extender_3_out = {{16{id_ex_1_ir_2[15]}}, id_ex_1_ir_2[15:0]};  // Bit_Extender bit_extender_3
  or or_6 (EX_Branch, EX_JR, \EX_Branch_有 , EX_JMP);
  Shifter #(.width(32)) shifter_2 (.in(bit_extender_3_out), .\dist (5'b00010), .out(EX_IMM));
  and and_8 (and_8_out, EX_Beq, mips_alu_1_equal);
  and and_9 (and_9_out, EX_Bne, ~mips_alu_1_equal);  // AND_Gate
  MIPS_ALU mips_alu_1 (
    .X(R1_Final), .Y(R2_Final), .AluOP(ALUOP_1), .Equal(mips_alu_1_equal), .Result(mips_alu_1_result),
    .shamt(multiplexer_17_out));  // open: Result_2
  Multiplexer #(.width(5), .enable("false")) multiplexer_17 (
    .in0(shamt_1), .in1(EX__rs[4:0]), .out(multiplexer_17_out), .sel(EX_SRAV));
  or or_7 (\EX_Branch_有 , and_8_out, EX_BLTZ_s, and_9_out);
  Counter #(.width(16), .max('hffff)) counter_6 (
    .count(\EX_Branch_有 ), .Q(\条件分支成功数 ), .clk(CLK), .clr(RST));  // open: load, D, carry
  Multiplexer #(.select(2), .width(32), .enable("false")) multiplexer_18 (
    .in0(EX__rs), .in1(ALU_Result), .in2(MEM_ReadData), .out(R1_Final), .sel(forward_1_forward_r1));  // open: in3
  EX_MEM ex_mem_1 (
    .IR({id_ex_1_ir_2[31:21], EX_rt, id_ex_1_ir_2[15:0]}), .PC(EX_PC), .Alu(mips_alu_1_result), .A(R1_Final),
    .B(R2_Final_1), .MemToReg(EX_MemToReg), .MemWrite(id_ex_1_memwrite_2), .RegWrite(id_ex_1_regwrite_2),
    .RegDst(id_ex_1_regdst_2), .Syscall(EX_Sys),
    .IR_2({ex_mem_1_ir_2[31:21], MEM_rt, MEM_rd, ex_mem_1_ir_2[10:0]}), .PC_2(MEM_PC), .Alu_2(ALU_Result),
    .A_2(ex_mem_1_a_2), .B_2(ex_mem_1_b_2), .MemToReg_2(MemToReg_2), .MemWrite_2(ex_mem_1_memwrite_2),
    .RegWrite_2(RegWrite_2), .RegDst_2(RegDst_2), .Syscall_2(ex_mem_1_syscall_2), .clk(CLK),
    .halt(not_2_out), .rst(RST), .Jal(id_ex_1_jal_2), .Jal_2(MEM_Jal), .Addr_26(id_ex_1_addr_26_2),
    .Addr_26_2(ex_mem_1_addr_26_2), .LH(EX_LH), .LH_2(ex_mem_1_lh_2));
  Multiplexer #(.select(2), .width(32), .enable("false")) multiplexer_19 (
    .in0(EX_R2), .in1(ALU_Result), .in2(MEM_ReadData), .out(R2_Final_1), .sel(forward_1_forward_r2));  // open: in3
  Multiplexer #(.width(32), .enable("false")) multiplexer_20 (
    .in0(ALU_Result), .in1(ram_1_data), .out({multiplexer_20_out_2, multiplexer_20_out}), .sel(MemToReg_2));
  RAM #(.addrWidth(10), .dataWidth(32), .bus("separate")) ram_1 (
    .addr(ALU_Result[11:2]), .din(ex_mem_1_b_2), .data(ram_1_data), .str(ex_mem_1_memwrite_2), .sel(1'b1),
    .clk(CLK), .ld(MemToReg_2));  // open: clr
  assign bit_extender_4_out = {{16{multiplexer_20_out[15]}}, multiplexer_20_out};  // Bit_Extender bit_extender_4
  assign bit_extender_5_out = {{16{multiplexer_20_out_2[15]}}, multiplexer_20_out_2};  // Bit_Extender bit_extender_5
  Multiplexer #(.width(5), .enable("false")) multiplexer_21 (
    .in0(rt), .in1(rd), .out(multiplexer_21_out), .sel(RegDst_r));
  Multiplexer #(.width(5), .enable("false")) multiplexer_22 (
    .in0(MEM_rt), .in1(MEM_rd), .out(multiplexer_22_out), .sel(RegDst_2));
  Multiplexer #(.width(32), .enable("false")) multiplexer_23 (
    .in0(bit_extender_4_out), .in1(bit_extender_5_out), .out(multiplexer_23_out), .sel(ALU_Result[1]));
  Multiplexer #(.width(5), .enable("false")) multiplexer_24 (
    .in0(multiplexer_21_out), .in1({5{1'b1}}), .out(WB_WriteReg_num), .sel(WB_Jal));
  Multiplexer #(.width(5), .enable("false")) multiplexer_25 (
    .in0(multiplexer_22_out), .in1({5{1'b1}}), .out(MEM_WriteReg_num), .sel(MEM_Jal));
  Multiplexer #(.width(32), .enable("false")) multiplexer_26 (
    .in0({multiplexer_20_out_2, multiplexer_20_out}), .in1(multiplexer_23_out), .out(multiplexer_26_out),
    .sel(ex_mem_1_lh_2));
  MEM_WB mem_wb_1 (
    .IR({ex_mem_1_ir_2[31:21], MEM_rt, MEM_rd, ex_mem_1_ir_2[10:0]}), .PC(MEM_PC), .A(ex_mem_1_a_2),
    .MD(multiplexer_26_out), .RegWrite(RegWrite_2), .RegDst(RegDst_2), .Syscall(ex_mem_1_syscall_2),
    .IR_2({mem_wb_1_ir_2[31:21], rt, rd, mem_wb_1_ir_2[10:0]}), .PC_2(WB_PC), .A_2(mem_wb_1_a_2),
    .MD_2(mem_wb_1_md_2), .RegWrite_2(WE), .RegDst_2(RegDst_r), .Syscall_2(mem_wb_1_syscall_2), .clk(CLK),
    .halt(not_2_out), .rst(RST), .Jal(MEM_Jal), .Jal_2(WB_Jal), .Addr_26(ex_mem_1_addr_26_2),
    .B(ex_mem_1_b_2), .B_2(mem_wb_1_b_2));  // open: Addr_26_2
  and and_10 (and_10_out, mem_wb_1_syscall_2, comparator_3_eq);
  Register #(.width(32)) register_1 (.D(mem_wb_1_a_2), .en(and_10_out), .Q(LedData), .clk(CLK));  // open: clr
  Comparator #(.width(32)) comparator_3 (.a(mem_wb_1_b_2), .b(32'h22), .eq(comparator_3_eq));  // open: gt, lt
  and and_11 (and_11_out, mem_wb_1_syscall_2, ~comparator_3_eq);  // AND_Gate
  Register #(.width(1)) register_2 (.D(mem_wb_1_syscall_2), .en(and_11_out), .Q(halt), .clk(CLK), .clr(or_8_out));
  or or_8 (or_8_out, RST, Go);
  and and_12 (InUse, ~halt, ~\LoadUse相关 );  // AND_Gate

  // Other names for the same wires on the sheet: 片选 = ALU_Result[1]; IR (some bits) = {ID_OP, ID_Func};
  //   shamt[4:0] = IR[10:6]; PC[31:0] = ID_PC; 插入气泡数[15:0] = \LoadUse次数 

  // Notes on the sheet:
  //   中断源
  //   中断等待指示
  //   数码管输出
  //   指令存储器
  //   contents of rom_1 (hex, n*v repeats v):
  //   20110001 8100005 20110001 20120002 20130003 8100009 20110001 20120002 20130003 810000d 20110001
  //   20120002 20130003 8100011 20110001 20120002 20130003 c1000f9 20100001 20110001 118fc0 112020
  //   20020022 c 118882 12200001 8100015 112020 20020022 c 20110001 118880 112020 20020022 c 12200001
  //   810001f 20110001 118fc0 112020 20020022 c 1188c3 112020 20020022 c 118903 112020 20020022 c 118903
  //   112020 20020022 c 118903 112020 20020022 c 118903 112020 20020022 c 118903 112020 20020022 c 118903
  //   112020 20020022 c 118903 112020 20020022 c 20100001 109fc0 139fc3 8021 2012000c 24160003 26100001
  //   3210000f 20080008 20090001 139900 2709825 132020 20020022 c 1094022 1500fff9 22100001 2018000f
  //   2188024 108700 20080008 20090001 139902 2709825 132021 20020022 c 1094022 1500fff9 108702 2c9b022
  //   12c00001 8100050 4020 1084027 84400 3508ffff 82021 20020022 c 2010ffff 20110000 ae300000 22100001
  //   22310004 ae300000 22100001 22310004 ae300000 22100001 22310004 ae300000 22100001 22310004 ae300000
  //   22100001 22310004 ae300000 22100001 22310004 ae300000 22100001 22310004 ae300000 22100001 22310004
  //   ae300000 22100001 22310004 ae300000 22100001 22310004 ae300000 22100001 22310004 ae300000 22100001
  //   22310004 ae300000 22100001 22310004 ae300000 22100001 22310004 ae300000 22100001 22310004 ae300000
  //   22100001 22310004 22100001 8020 2011003c 8e130000 8e340000 274402a 11000002 ae330000 ae140000
  //   2231fffc 1611fff8 102020 20020022 c 22100004 2011003c 1611fff2 20020032 c 20080001 20090003 20110876
  //   118d00 112020 20020022 c 200b0008 1118807 1318807 112020 20020022 c 216bffff 1560fff9 2002000a c
  //   2008ffff 20117777 112020 20020022 c 200b0010 3a31ffff 112020 20020022 c 216bffff 1560fffa 2002000a c
  //   20090000 200b0010 34118483 20120404 118c00 129400 36318281 22520404 ad310000 2328820 21290004
  //   216bffff 1560fffb 200b0020 20090000 85310000 112020 20020022 c 21290002 216bffff 1560fff9 2002000a c
  //   2011fff1 112020 20020022 c 22310001 620fffb 2002000a c 2002000a c 20100000 22100001 102020 20020022
  //   c 22100002 102020 20020022 c 22100003 102020 20020022 c 22100004 102020 20020022 c 22100005 102020
  //   20020022 c 22100006 102020 20020022 c 22100007 102020 20020022 c 22100008 102020 20020022 20020022 c
  //   3e00008
  //   Shamt
  //   OP
  //   Func
  //   rs
  //   rt
  //   Imm
  //   流水调试日志用
  //   OP
  //   Func
  //   rs
  //   rt
  //   rd
  //   rt
endmodule

module \双位预测状态机  (
  input  [1:0] in_1,
  input  \分支成功 ,
  input  Update,
  output [1:0] out_4
);

  wire and_1_out, and_2_out, and_3_out, and_4_out, not_1_out, not_2_out, not_3_out, not_4_out, not_5_out;
  wire [1:0] or_2_out;

  not not_1 (not_1_out, in_1[0]);
  not not_2 (not_2_out, in_1[1]);
  not not_3 (not_3_out, in_1[0]);
  not not_4 (not_4_out, in_1[0]);
  not not_5 (not_5_out, \分支成功 );
  and and_1 (and_1_out, in_1[0], \分支成功 );
  and and_2 (and_2_out, in_1[1], not_1_out);
  and and_3 (and_3_out, not_2_out, not_3_out, \分支成功 );
  and and_4 (and_4_out, in_1[1], not_4_out, not_5_out);
  or or_1 (or_2_out[1], and_1_out, and_2_out);
  or or_2 (or_2_out[0], and_3_out, and_4_out);
  Multiplexer #(.width(2), .enable("false")) multiplexer_1 (.in0(2'b10), .in1(or_2_out), .out(out_4), .sel(Update));
endmodule

module BHT (
  input  Rst,
  input  Clk,
  input  [31:0] PC_3,
  input  [31:0] PC,
  input  [31:0] DstAddr,
  input  \分支成功 ,
  input  Hit_3,
  input  JumpBack_3,
  input  [2:0] HitPos_3,
  output \预测跳转 ,
  output Hit,
  output [31:0] \预测地址 ,
  output [2:0] HitPos
);

  wire Addr_SET0, Addr_SET1, Addr_SET2, Addr_SET3, Addr_SET4, Addr_SET5, Addr_SET6, Addr_SET7, and_1_out,
       and_2_out, and_3_out, and_4_out, and_5_out, and_6_out, and_7_out, and_8_out, decoder_1_out0,
       decoder_1_out1, decoder_1_out2, decoder_1_out3, decoder_1_out4, decoder_1_out5, decoder_1_out6,
       decoder_1_out7, DirAddr0, DirAddr1, DirAddr2, DirAddr3, DirAddr4, DirAddr5, DirAddr6, DirAddr7, Empty,
       Miss, not_2_out, not_3_out, not_4_out, not_5_out, not_6_out, not_7_out, not_8_out, not_9_out,
       not_10_out, priority_encoder_1_gs, SET0, SET1, SET2, SET3, SET4, SET5, SET6, SET7, V0, V1, V2, V3, V4,
       V5, V6, V7;
  wire [0:0] multiplexer_35_out;
  wire [1:0] multiplexer_19_out, multiplexer_20_out, multiplexer_21_out, multiplexer_22_out,
       multiplexer_23_out, multiplexer_24_out, multiplexer_25_out, multiplexer_26_out, State0, State1,
       State2, State3, State4, State5, State6, State7, \预测历史_2_out_4 , \预测历史_3_out_4 , \预测历史_4_out_4 ,
       \预测历史_5_out_4 , \预测历史_6_out_4 , \预测历史_7_out_4 , \预测历史_8_out_4 , \预测历史_out_4 ;
  wire [2:0] Invalid, max_3_1_max_num, max_3_2_max_num, max_3_3_max_num, max_3_4_max_num, max_3_5_max_num,
       max_3_6_max_num, MAX_num, multiplexer_17_out, multiplexer_44_out, multiplexer_45_out;
  wire [31:0] adder_1_out, adder_2_out, adder_3_out, adder_4_out, adder_5_out, adder_6_out, adder_7_out,
       adder_8_out, DstAddr0, DstAddr1, DstAddr2, DstAddr3, DstAddr4, DstAddr5, DstAddr6, DstAddr7, LRU_0,
       LRU_1, LRU_2, LRU_3, LRU_4, LRU_5, LRU_6, LRU_7, max_3_1_max, max_3_2_max, max_3_3_max, max_3_4_max,
       max_3_5_max, max_3_6_max, multiplexer_1_out, multiplexer_2_out, multiplexer_3_out, multiplexer_4_out,
       multiplexer_5_out, multiplexer_6_out, multiplexer_7_out, multiplexer_8_out, multiplexer_9_out,
       multiplexer_10_out, multiplexer_11_out, multiplexer_12_out, multiplexer_13_out, multiplexer_14_out,
       multiplexer_15_out, multiplexer_16_out, multiplexer_27_out, multiplexer_28_out, multiplexer_29_out,
       multiplexer_30_out, multiplexer_31_out, multiplexer_32_out, multiplexer_33_out, multiplexer_34_out,
       multiplexer_36_out, multiplexer_37_out, multiplexer_38_out, multiplexer_39_out, multiplexer_40_out,
       multiplexer_41_out, multiplexer_42_out, multiplexer_43_out, \指令Addr_2_q , \指令Addr_3_q , \指令Addr_4_q ,
       \指令Addr_5_q , \指令Addr_6_q , \指令Addr_7_q , \指令Addr_8_q , \指令Addr_q ;

  Register #(.width(1)) valid (.D(1'b1), .en(SET0), .Q(V0), .clk(Clk));  // open: clr
  Register #(.width(1)) valid_2 (.D(1'b1), .en(SET1), .Q(V1), .clk(Clk));  // open: clr
  Register #(.width(1)) valid_3 (.D(1'b1), .en(SET2), .Q(V2), .clk(Clk));  // open: clr
  Register #(.width(1)) valid_4 (.D(1'b1), .en(SET3), .Q(V3), .clk(Clk));  // open: clr
  Register #(.width(1)) valid_5 (.D(1'b1), .en(SET4), .Q(V4), .clk(Clk));  // open: clr
  Register #(.width(1)) valid_6 (.D(1'b1), .en(SET5), .Q(V5), .clk(Clk));  // open: clr
  Register #(.width(1)) valid_7 (.D(1'b1), .en(SET6), .Q(V6), .clk(Clk));  // open: clr
  Register #(.width(1)) valid_8 (.D(1'b1), .en(SET7), .Q(V7), .clk(Clk));  // open: clr
  MAX_3 max_3_1 (.Y(LRU_0), .X(LRU_1), .Y_num(3'b000), .X_num(3'b001), .MAX(max_3_1_max), .Max_num(max_3_1_max_num));
  MAX_3 max_3_2 (.Y(LRU_2), .X(LRU_3), .Y_num(3'b010), .X_num(3'b011), .MAX(max_3_2_max), .Max_num(max_3_2_max_num));
  MAX_3 max_3_3 (.Y(LRU_4), .X(LRU_5), .Y_num(3'b100), .X_num(3'b101), .MAX(max_3_3_max), .Max_num(max_3_3_max_num));
  MAX_3 max_3_4 (.Y(LRU_6), .X(LRU_7), .Y_num(3'b110), .X_num(3'b111), .MAX(max_3_4_max), .Max_num(max_3_4_max_num));
  MAX_3 max_3_5 (
    .Y(max_3_1_max), .X(max_3_2_max), .Y_num(max_3_1_max_num), .X_num(max_3_2_max_num), .MAX(max_3_5_max),
    .Max_num(max_3_5_max_num));
  MAX_3 max_3_6 (
    .Y(max_3_3_max), .X(max_3_4_max), .Y_num(max_3_3_max_num), .X_num(max_3_4_max_num), .MAX(max_3_6_max),
    .Max_num(max_3_6_max_num));
  Multiplexer #(.width(32), .enable("false")) multiplexer_1 (
    .in0(PC_3), .in1({32{1'b0}}), .out(multiplexer_1_out), .sel(Rst));
  Register #(.width(32)) \u_指令Addr  (.D(multiplexer_1_out), .en(Addr_SET0), .Q(\指令Addr_q ), .clk(Clk));  // open: clr
  Register #(.width(32)) \u_指令Addr_2  (
    .D(multiplexer_2_out), .en(Addr_SET1), .Q(\指令Addr_2_q ), .clk(Clk));  // open: clr
  Multiplexer #(.width(32), .enable("false")) multiplexer_2 (
    .in0(PC_3), .in1({32{1'b0}}), .out(multiplexer_2_out), .sel(Rst));
  Multiplexer #(.width(32), .enable("false")) multiplexer_3 (
    .in0(PC_3), .in1({32{1'b0}}), .out(multiplexer_3_out), .sel(Rst));
  Register #(.width(32)) \u_指令Addr_3  (
    .D(multiplexer_3_out), .en(Addr_SET2), .Q(\指令Addr_3_q ), .clk(Clk));  // open: clr
  Multiplexer #(.width(32), .enable("false")) multiplexer_4 (
    .in0(PC_3), .in1({32{1'b0}}), .out(multiplexer_4_out), .sel(Rst));
  Register #(.width(32)) \u_指令Addr_4  (
    .D(multiplexer_4_out), .en(Addr_SET3), .Q(\指令Addr_4_q ), .clk(Clk));  // open: clr
  Register #(.width(32)) \u_指令Addr_5  (
    .D(multiplexer_5_out), .en(Addr_SET4), .Q(\指令Addr_5_q ), .clk(Clk));  // open: clr
  Multiplexer #(.width(32), .enable("false")) multiplexer_5 (
    .in0(PC_3), .in1({32{1'b0}}), .out(multiplexer_5_out), .sel(Rst));
  Multiplexer #(.width(32), .enable("false")) multiplexer_6 (
    .in0(PC_3), .in1({32{1'b0}}), .out(multiplexer_6_out), .sel(Rst));
  Register #(.width(32)) \u_指令Addr_6  (
    .D(multiplexer_6_out), .en(Addr_SET5), .Q(\指令Addr_6_q ), .clk(Clk));  // open: clr
  Register #(.width(32)) \u_指令Addr_7  (
    .D(multiplexer_7_out), .en(Addr_SET6), .Q(\指令Addr_7_q ), .clk(Clk));  // open: clr
  Multiplexer #(.width(32), .enable("false")) multiplexer_7 (
    .in0(PC_3), .in1({32{1'b0}}), .out(multiplexer_7_out), .sel(Rst));
  Register #(.width(32)) \u_指令Addr_8  (
    .D(multiplexer_8_out), .en(Addr_SET7), .Q(\指令Addr_8_q ), .clk(Clk));  // open: clr
  Multiplexer #(.width(32), .enable("false")) multiplexer_8 (
    .in0(PC_3), .in1({32{1'b0}}), .out(multiplexer_8_out), .sel(Rst));
  MAX_3 max_3_7 (
    .Y(max_3_5_max), .X(max_3_6_max), .Y_num(max_3_5_max_num), .X_num(max_3_6_max_num), .Max_num(MAX_num));  // open: MAX
  Comparator #(.width(32)) comparator_1 (.a(PC), .b(\指令Addr_q ), .eq(DirAddr0));  // open: gt, lt
  Comparator #(.width(32)) comparator_2 (.a(PC), .b(\指令Addr_2_q ), .eq(DirAddr1));  // open: gt, lt
  Comparator #(.width(32)) comparator_3 (.a(PC), .b(\指令Addr_3_q ), .eq(DirAddr2));  // open: gt, lt
  Comparator #(.width(32)) comparator_4 (.a(PC), .b(\指令Addr_4_q ), .eq(DirAddr3));  // open: gt, lt
  Comparator #(.width(32)) comparator_5 (.a(PC), .b(\指令Addr_5_q ), .eq(DirAddr4));  // open: gt, lt
  Comparator #(.width(32)) comparator_6 (.a(PC), .b(\指令Addr_6_q ), .eq(DirAddr5));  // open: gt, lt
  Comparator #(.width(32)) comparator_7 (.a(PC), .b(\指令Addr_7_q ), .eq(DirAddr6));  // open: gt, lt
  Comparator #(.width(32)) comparator_8 (.a(PC), .b(\指令Addr_8_q ), .eq(DirAddr7));  // open: gt, lt
  and and_1 (and_1_out, V0, DirAddr0);
  and and_2 (and_2_out, V1, DirAddr1);
  and and_3 (and_3_out, V2, DirAddr2);
  and and_4 (and_4_out, V3, DirAddr3);
  and and_5 (and_5_out, V4, DirAddr4);
  and and_6 (and_6_out, V5, DirAddr5);
  and and_7 (and_7_out, V6, DirAddr6);
  and and_8 (and_8_out, V7, DirAddr7);
  Register #(.width(32)) Dst_Addr (.D(multiplexer_9_out), .en(Addr_SET0), .Q(DstAddr0), .clk(Clk));  // open: clr
  Multiplexer #(.width(32), .enable("false")) multiplexer_9 (
    .in0(DstAddr), .in1({32{1'b0}}), .out(multiplexer_9_out), .sel(Rst));
  Register #(.width(32)) Dst_Addr_2 (.D(multiplexer_10_out), .en(Addr_SET1), .Q(DstAddr1), .clk(Clk));  // open: clr
  Multiplexer #(.width(32), .enable("false")) multiplexer_10 (
    .in0(DstAddr), .in1({32{1'b0}}), .out(multiplexer_10_out), .sel(Rst));
  Register #(.width(32)) Dst_Addr_3 (.D(multiplexer_11_out), .en(Addr_SET2), .Q(DstAddr2), .clk(Clk));  // open: clr
  Multiplexer #(.width(32), .enable("false")) multiplexer_11 (
    .in0(DstAddr), .in1({32{1'b0}}), .out(multiplexer_11_out), .sel(Rst));
  Register #(.width(32)) Dst_Addr_4 (.D(multiplexer_12_out), .en(Addr_SET3), .Q(DstAddr3), .clk(Clk));  // open: clr
  Multiplexer #(.width(32), .enable("false")) multiplexer_12 (
    .in0(DstAddr), .in1({32{1'b0}}), .out(multiplexer_12_out), .sel(Rst));
  Register #(.width(32)) Dst_Addr_5 (.D(multiplexer_13_out), .en(Addr_SET4), .Q(DstAddr4), .clk(Clk));  // open: clr
  Multiplexer #(.width(32), .enable("false")) multiplexer_13 (
    .in0(DstAddr), .in1({32{1'b0}}), .out(multiplexer_13_out), .sel(Rst));
  Register #(.width(32)) Dst_Addr_6 (.D(multiplexer_14_out), .en(Addr_SET5), .Q(DstAddr5), .clk(Clk));  // open: clr
  Multiplexer #(.width(32), .enable("false")) multiplexer_14 (
    .in0(DstAddr), .in1({32{1'b0}}), .out(multiplexer_14_out), .sel(Rst));
  Multiplexer #(.width(32), .enable("false")) multiplexer_15 (
    .in0(DstAddr), .in1({32{1'b0}}), .out(multiplexer_15_out), .sel(Rst));
  Register #(.width(32)) Dst_Addr_7 (.D(multiplexer_15_out), .en(Addr_SET6), .Q(DstAddr6), .clk(Clk));  // open: clr
  Register #(.width(32)) Dst_Addr_8 (.D(multiplexer_16_out), .en(Addr_SET7), .Q(DstAddr7), .clk(Clk));  // open: clr
  Multiplexer #(.width(32), .enable("false")) multiplexer_16 (
    .in0(DstAddr), .in1({32{1'b0}}), .out(multiplexer_16_out), .sel(Rst));
  or or_1 (Hit, and_1_out, and_2_out, and_3_out, and_4_out, and_5_out, and_6_out, and_7_out, and_8_out);
  Priority_Encoder priority_encoder_1 (
    .in0(and_1_out), .in1(and_2_out), .in2(and_3_out), .in3(and_4_out), .in4(and_5_out), .in5(and_6_out),
    .in6(and_7_out), .in7(and_8_out), .out(HitPos), .gs(priority_encoder_1_gs));  // open: en_in, en_out
  not not_1 (Miss, Hit);
  Multiplexer #(.width(3), .enable("false")) multiplexer_17 (
    .in0(3'b000), .in1(HitPos), .out(multiplexer_17_out), .sel(priority_encoder_1_gs));
  \双位预测状态机  \u_预测历史  (.\分支成功 (\分支成功 ), .Update(Hit_3), .out_4(\预测历史_out_4 ), .in_1(State0));
  \双位预测状态机  \u_预测历史_2  (.\分支成功 (\分支成功 ), .Update(Hit_3), .out_4(\预测历史_2_out_4 ), .in_1(State1));
  \双位预测状态机  \u_预测历史_3  (.\分支成功 (\分支成功 ), .Update(Hit_3), .out_4(\预测历史_3_out_4 ), .in_1(State2));
  \双位预测状态机  \u_预测历史_4  (.\分支成功 (\分支成功 ), .Update(Hit_3), .out_4(\预测历史_4_out_4 ), .in_1(State3));
  \双位预测状态机  \u_预测历史_5  (.\分支成功 (\分支成功 ), .Update(Hit_3), .out_4(\预测历史_5_out_4 ), .in_1(State4));
  \双位预测状态机  \u_预测历史_6  (.\分支成功 (\分支成功 ), .Update(Hit_3), .out_4(\预测历史_6_out_4 ), .in_1(State5));
  \双位预测状态机  \u_预测历史_7  (.\分支成功 (\分支成功 ), .Update(Hit_3), .out_4(\预测历史_7_out_4 ), .in_1(State6));
  \双位预测状态机  \u_预测历史_8  (.\分支成功 (\分支成功 ), .Update(Hit_3), .out_4(\预测历史_8_out_4 ), .in_1(State7));
  Multiplexer #(.select(3), .width(32), .enable("false")) multiplexer_18 (
    .in0(DstAddr0), .in1(DstAddr1), .in2(DstAddr2), .in3(DstAddr3), .in4(DstAddr4), .in5(DstAddr5),
    .in6(DstAddr6), .in7(DstAddr7), .out(\预测地址 ), .sel(multiplexer_17_out));
  Register #(.width(2)) register_1 (.D(multiplexer_19_out), .en(SET0), .Q(State0), .clk(Clk));  // open: clr
  Multiplexer #(.width(2), .enable("false")) multiplexer_19 (
    .in0(\预测历史_out_4 ), .in1(2'b00), .out(multiplexer_19_out), .sel(Rst));
  Register #(.width(2)) register_2 (.D(multiplexer_20_out), .en(SET1), .Q(State1), .clk(Clk));  // open: clr
  Multiplexer #(.width(2), .enable("false")) multiplexer_20 (
    .in0(\预测历史_2_out_4 ), .in1(2'b00), .out(multiplexer_20_out), .sel(Rst));
  Multiplexer #(.width(2), .enable("false")) multiplexer_21 (
    .in0(\预测历史_3_out_4 ), .in1(2'b00), .out(multiplexer_21_out), .sel(Rst));
  Register #(.width(2)) register_3 (.D(multiplexer_21_out), .en(SET2), .Q(State2), .clk(Clk));  // open: clr
  Register #(.width(2)) register_4 (.D(multiplexer_22_out), .en(SET3), .Q(State3), .clk(Clk));  // open: clr
  Multiplexer #(.width(2), .enable("false")) multiplexer_22 (
    .in0(\预测历史_4_out_4 ), .in1(2'b00), .out(multiplexer_22_out), .sel(Rst));
  Register #(.width(2)) register_5 (.D(multiplexer_23_out), .en(SET4), .Q(State4), .clk(Clk));  // open: clr
  Multiplexer #(.width(2), .enable("false")) multiplexer_23 (
    .in0(\预测历史_5_out_4 ), .in1(2'b00), .out(multiplexer_23_out), .sel(Rst));
  Register #(.width(2)) register_6 (.D(multiplexer_24_out), .en(SET5), .Q(State5), .clk(Clk));  // open: clr
  Multiplexer #(.width(2), .enable("false")) multiplexer_24 (
    .in0(\预测历史_6_out_4 ), .in1(2'b00), .out(multiplexer_24_out), .sel(Rst));
  Multiplexer #(.width(2), .enable("false")) multiplexer_25 (
    .in0(\预测历史_7_out_4 ), .in1(2'b00), .out(multiplexer_25_out), .sel(Rst));
  Register #(.width(2)) register_7 (.D(multiplexer_25_out), .en(SET6), .Q(State6), .clk(Clk));  // open: clr
  Multiplexer #(.width(2), .enable("false")) multiplexer_26 (
    .in0(\预测历史_8_out_4 ), .in1(2'b00), .out(multiplexer_26_out), .sel(Rst));
  Register #(.width(2)) register_8 (.D(multiplexer_26_out), .en(SET7), .Q(State7), .clk(Clk));  // open: clr
  Multiplexer #(.width(32), .enable("false")) multiplexer_27 (
    .in0(adder_1_out), .in1({32{1'b0}}), .out(multiplexer_27_out), .sel(SET0));
  Multiplexer #(.width(32), .enable("false")) multiplexer_28 (
    .in0(adder_2_out), .in1({32{1'b0}}), .out(multiplexer_28_out), .sel(SET1));
  Multiplexer #(.width(32), .enable("false")) multiplexer_29 (
    .in0(adder_3_out), .in1({32{1'b0}}), .out(multiplexer_29_out), .sel(SET2));
  Multiplexer #(.width(32), .enable("false")) multiplexer_30 (
    .in0(adder_4_out), .in1({32{1'b0}}), .out(multiplexer_30_out), .sel(SET3));
  Multiplexer #(.width(32), .enable("false")) multiplexer_31 (
    .in0(adder_5_out), .in1({32{1'b0}}), .out(multiplexer_31_out), .sel(SET4));
  Multiplexer #(.width(32), .enable("false")) multiplexer_32 (
    .in0(adder_6_out), .in1({32{1'b0}}), .out(multiplexer_32_out), .sel(SET5));
  Multiplexer #(.width(32), .enable("false")) multiplexer_33 (
    .in0(adder_7_out), .in1({32{1'b0}}), .out(multiplexer_33_out), .sel(SET6));
  Multiplexer #(.width(32), .enable("false")) multiplexer_34 (
    .in0(adder_8_out), .in1({32{1'b0}}), .out(multiplexer_34_out), .sel(SET7));
  Multiplexer #(.select(3), .width(2), .enable("false")) multiplexer_35 (
    .in0(State0), .in1(State1), .in2(State0), .in3(State1), .in4(State0), .in5(State1), .in6(State0),
    .in7(State1), .out({\预测跳转 , multiplexer_35_out[0]}), .sel(multiplexer_17_out));
  Multiplexer #(.width(32), .enable("false")) multiplexer_36 (
    .in0(multiplexer_27_out), .in1({32{1'b0}}), .out(multiplexer_36_out), .sel(Rst));
  Multiplexer #(.width(32), .enable("false")) multiplexer_37 (
    .in0(multiplexer_28_out), .in1({32{1'b0}}), .out(multiplexer_37_out), .sel(Rst));
  Multiplexer #(.width(32), .enable("false")) multiplexer_38 (
    .in0(multiplexer_29_out), .in1({32{1'b0}}), .out(multiplexer_38_out), .sel(Rst));
  Multiplexer #(.width(32), .enable("false")) multiplexer_39 (
    .in0(multiplexer_30_out), .in1({32{1'b0}}), .out(multiplexer_39_out), .sel(Rst));
  Multiplexer #(.width(32), .enable("false")) multiplexer_40 (
    .in0(multiplexer_31_out), .in1({32{1'b0}}), .out(multiplexer_40_out), .sel(Rst));
  Multiplexer #(.width(32), .enable("false")) multiplexer_41 (
    .in0(multiplexer_32_out), .in1({32{1'b0}}), .out(multiplexer_41_out), .sel(Rst));
  Multiplexer #(.width(32), .enable("false")) multiplexer_42 (
    .in0(multiplexer_33_out), .in1({32{1'b0}}), .out(multiplexer_42_out), .sel(Rst));
  Multiplexer #(.width(32), .enable("false")) multiplexer_43 (
    .in0(multiplexer_34_out), .in1({32{1'b0}}), .out(multiplexer_43_out), .sel(Rst));
  Register #(.width(32)) \u_淘汰标志位  (.D(multiplexer_36_out), .en(JumpBack_3), .Q(LRU_0), .clk(Clk));  // open: clr
  Register #(.width(32)) \u_淘汰标志位_2  (.D(multiplexer_37_out), .en(JumpBack_3), .Q(LRU_1), .clk(Clk));  // open: clr
  Register #(.width(32)) \u_淘汰标志位_3  (.D(multiplexer_38_out), .en(JumpBack_3), .Q(LRU_2), .clk(Clk));  // open: clr
  Register #(.width(32)) \u_淘汰标志位_4  (.D(multiplexer_39_out), .en(JumpBack_3), .Q(LRU_3), .clk(Clk));  // open: clr
  Register #(.width(32)) \u_淘汰标志位_5  (.D(multiplexer_40_out), .en(JumpBack_3), .Q(LRU_4), .clk(Clk));  // open: clr
  Register #(.width(32)) \u_淘汰标志位_6  (.D(multiplexer_41_out), .en(JumpBack_3), .Q(LRU_5), .clk(Clk));  // open: clr
  Register #(.width(32)) \u_淘汰标志位_7  (.D(multiplexer_42_out), .en(JumpBack_3), .Q(LRU_6), .clk(Clk));  // open: clr
  Register #(.width(32)) \u_淘汰标志位_8  (.D(multiplexer_43_out), .en(JumpBack_3), .Q(LRU_7), .clk(Clk));  // open: clr
  Adder #(.width(32)) adder_1 (.a(32'h1), .b(LRU_0), .out(adder_1_out));  // open: cin, cout
  Adder #(.width(32)) adder_2 (.a(32'h1), .b(LRU_1), .out(adder_2_out));  // open: cin, cout
  Adder #(.width(32)) adder_3 (.a(32'h1), .b(LRU_2), .out(adder_3_out));  // open: cin, cout
  Adder #(.width(32)) adder_4 (.a(32'h1), .b(LRU_3), .out(adder_4_out));  // open: cin, cout
  Adder #(.width(32)) adder_5 (.a(32'h1), .b(LRU_4), .out(adder_5_out));  // open: cin, cout
  Adder #(.width(32)) adder_6 (.a(32'h1), .b(LRU_5), .out(adder_6_out));  // open: cin, cout
  Adder #(.width(32)) adder_7 (.a(32'h1), .b(LRU_6), .out(adder_7_out));  // open: cin, cout
  Adder #(.width(32)) adder_8 (.a(32'h1), .b(LRU_7), .out(adder_8_out));  // open: cin, cout
  not not_2 (not_2_out, V0);
  not not_3 (not_3_out, V1);
  not not_4 (not_4_out, V2);
  not not_5 (not_5_out, V3);
  not not_6 (not_6_out, V4);
  not not_7 (not_7_out, V5);
  not not_8 (not_8_out, V6);
  not not_9 (not_9_out, V7);
  Priority_Encoder priority_encoder_2 (
    .in0(not_2_out), .in1(not_3_out), .in2(not_4_out), .in3(not_5_out), .in4(not_6_out), .in5(not_7_out),
    .in6(not_8_out), .in7(not_9_out), .out(Invalid), .gs(Empty));  // open: en_in, en_out
  Multiplexer #(.width(3), .enable("false")) multiplexer_44 (
    .in0(MAX_num), .in1(Invalid), .out(multiplexer_44_out), .sel(Empty));
  Decoder #(.select(3), .disabled(0), .enable("false")) decoder_1 (
    .out0(decoder_1_out0), .out1(decoder_1_out1), .out2(decoder_1_out2), .out3(decoder_1_out3),
    .out4(decoder_1_out4), .out5(decoder_1_out5), .out6(decoder_1_out6), .out7(decoder_1_out7),
    .sel(multiplexer_45_out));
  Multiplexer #(.width(3), .enable("false")) multiplexer_45 (
    .in0(multiplexer_44_out), .in1(HitPos_3), .out(multiplexer_45_out), .sel(Hit_3));
  and and_9 (SET0, decoder_1_out0, JumpBack_3);
  and and_10 (SET1, decoder_1_out1, JumpBack_3);
  and and_11 (SET2, decoder_1_out2, JumpBack_3);
  and and_12 (SET3, decoder_1_out3, JumpBack_3);
  and and_13 (SET4, decoder_1_out4, JumpBack_3);
  and and_14 (SET5, decoder_1_out5, JumpBack_3);
  and and_15 (SET6, decoder_1_out6, JumpBack_3);
  and and_16 (SET7, decoder_1_out7, JumpBack_3);
  not not_10 (not_10_out, Hit_3);
  and and_17 (Addr_SET0, SET0, not_10_out);
  and and_18 (Addr_SET1, not_10_out, SET1);
  and and_19 (Addr_SET2, SET2, not_10_out);
  and and_20 (Addr_SET3, SET3, not_10_out);
  and and_21 (Addr_SET4, SET4, not_10_out);
  and and_22 (Addr_SET5, SET5, not_10_out);
  and and_23 (Addr_SET6, SET6, not_10_out);
  and and_24 (Addr_SET7, SET7, not_10_out);

  // Other names for the same wires on the sheet: Jump_Out = \预测跳转 ; DstAddr_Out[31:0] = \预测地址 
endmodule
module MAX_3 (
  input  [31:0] Y,
  input  [31:0] X,
  input  [2:0] Y_num,
  input  [2:0] X_num,
  output [31:0] MAX,
  output [2:0] Max_num
);

  wire comparator_1_eq, comparator_1_gt, or_1_out;

  Multiplexer #(.width(32), .enable("false")) multiplexer_1 (.in0(Y), .in1(X), .out(MAX), .sel(or_1_out));
  Comparator #(.width(32), .mode("unsigned")) comparator_1 (
    .a(X), .b(Y), .gt(comparator_1_gt), .eq(comparator_1_eq));  // open: lt
  or or_1 (or_1_out, comparator_1_gt, comparator_1_eq);
  Multiplexer #(.width(3), .enable("false")) multiplexer_2 (.in0(Y_num), .in1(X_num), .out(Max_num), .sel(or_1_out));

  // Notes on the sheet:
  //   输出两个输入中的较大值，并输出较大值的3位编号
endmodule

module \单级中断  (
);

  wire and_1_out, and_2_out, and_3_out, and_4_out, and_5_out, and_7_out, and_8_out, and_12_out, and_13_out,
       and_14_out, BLTZ, CLK, comparator_1_lt, comparator_2_eq, d_ff_1_q, d_ff_2_q, d_ff_3_q, d_ff_4_q,
       decoder_1_out1, decoder_1_out2, decoder_1_out3, eret, eret1, eret2, eret3, Go, IE_q, INT1, INT2, INT3,
       InUse, IR1, IR2, IR3, IR_CPU, JAL, lh, mips_alu_1_equal, not_1_out, not_2_out, not_3_out, not_4_out,
       not_5_out, not_6_out, not_7_out, or_4_out, or_5_out, or_6_out, or_7_out, or_8_out, or_9_out,
       priority_encoder_1_gs, register_2_q, RST, SignedExt, SRAV, syscall, W1, W2, W3, \片选 ,
       \硬布线控制器_1_alu_src , \硬布线控制器_1_beq , \硬布线控制器_1_bne , \硬布线控制器_1_jmp , \硬布线控制器_1_jr ,
       \硬布线控制器_1_memtoreg , \硬布线控制器_1_memwrite , \硬布线控制器_1_regdst , \硬布线控制器_1_regwrite ;
  wire [1:0] EPC_q, priority_encoder_1_out;
  wire [3:0] adder_1_out_2, \硬布线控制器_1_alu_op ;
  wire [4:0] multiplexer_6_out, multiplexer_7_out, multiplexer_9_out, multiplexer_10_out, multiplexer_15_out;
  wire [15:0] multiplexer_16_out, multiplexer_16_out_2, \总周期数 , \无条件分支数 , \条件分支成功数 ;
  wire [25:0] Adress;
  wire [27:0] adder_1_out;
  wire [31:0] adder_2_out, adder_3_out, Addr, bit_extender_1_out, bit_extender_2_out, bit_extender_3_out,
       bit_extender_4_out, branch0, branch1, EPC, LedData, mips_alu_1_result, mips_regifile_1_r2,
       multiplexer_2_out, multiplexer_3_out, multiplexer_4_out, multiplexer_5_out, multiplexer_8_out,
       multiplexer_12_out, multiplexer_14_out, multiplexer_17_out, multiplexer_18_out, PC, ram_1_data, rs,
       shifter_1_out, shifter_2_out;
  wire [31:26] rom_1_data;

  Button \u_总复位  (.out(RST));
  Button \u_继续运行  (.out(Go));
  Clock clock_1 (.out(CLK));
  Multiplexer #(.width(32), .enable("false")) multiplexer_1 (
    .in0({adder_1_out_2, adder_1_out}), .in1(adder_3_out), .out(branch0), .sel(or_8_out));
  Multiplexer #(.width(32), .enable("false")) multiplexer_2 (
    .in0(branch1), .in1({adder_1_out_2, Adress, 2'b00}), .out(multiplexer_2_out), .sel(\硬布线控制器_1_jmp ));
  Hex_Digit_Display hex_digit_display_1 (.value(LedData[27:24]));  // open: dp
  Hex_Digit_Display hex_digit_display_2 (.value(LedData[31:28]));  // open: dp
  Multiplexer #(.width(32), .enable("false")) multiplexer_3 (
    .in0(multiplexer_2_out), .in1(rs), .out(multiplexer_3_out), .sel(\硬布线控制器_1_jr ));
  or or_1 (W1, INT1, d_ff_1_q);
  or or_2 (W2, INT2, d_ff_2_q);
  or or_3 (W3, INT3, d_ff_3_q);
  Hex_Digit_Display hex_digit_display_3 (.value(LedData[19:16]));  // open: dp
  Hex_Digit_Display hex_digit_display_4 (.value(LedData[23:20]));  // open: dp
  Multiplexer #(.width(32), .enable("false")) multiplexer_4 (
    .in0(multiplexer_3_out), .in1(Addr), .out(multiplexer_4_out), .sel(IR_CPU));
  D_Flip_Flop d_ff_1 (.clk(IR1), .D(1'b1), .Q(d_ff_1_q), .reset(INT1));  // open: Qn, preset, en
  D_Flip_Flop d_ff_2 (.clk(IR2), .D(1'b1), .Q(d_ff_2_q), .reset(INT2));  // open: Qn, preset, en
  D_Flip_Flop d_ff_3 (.clk(IR3), .D(1'b1), .Q(d_ff_3_q), .reset(INT3));  // open: Qn, preset, en
  Hex_Digit_Display hex_digit_display_5 (.value(LedData[15:12]));  // open: dp
  Hex_Digit_Display hex_digit_display_6 (.value(LedData[11:8]));  // open: dp
  Multiplexer #(.width(32), .enable("false")) multiplexer_5 (
    .in0(multiplexer_4_out), .in1(EPC), .out(multiplexer_5_out), .sel(eret));
  or or_4 (or_4_out, d_ff_1_q, INT1);
  or or_5 (or_5_out, d_ff_2_q, INT2);
  or or_6 (or_6_out, d_ff_3_q, INT3);
  Hex_Digit_Display hex_digit_display_7 (.value(LedData[7:4]));  // open: dp
  Hex_Digit_Display hex_digit_display_8 (.value(LedData[3:0]));  // open: dp
  not not_1 (not_1_out, eret1);
  not not_2 (not_2_out, eret2);
  not not_3 (not_3_out, eret3);
  Counter #(.width(16), .max('hffff)) counter_1 (
    .count(or_7_out), .Q(\无条件分支数 ), .clk(CLK), .clr(RST));  // open: load, D, carry
  or or_7 (or_7_out, \硬布线控制器_1_jr , \硬布线控制器_1_jmp , JAL);
  Register #(.width(32)) u_PC (.D(multiplexer_5_out), .en(InUse), .Q(PC), .clk(CLK), .clr(RST));
  D_Flip_Flop u_IR1 (.clk(CLK), .D(and_1_out), .Q(INT1));  // open: Qn, preset, en, reset
  and and_1 (and_1_out, or_4_out, not_1_out);
  D_Flip_Flop u_IR2 (.clk(CLK), .D(and_2_out), .Q(INT2));  // open: Qn, preset, en, reset
  and and_2 (and_2_out, or_5_out, not_2_out);
  D_Flip_Flop u_IR3 (.clk(CLK), .D(and_3_out), .Q(INT3));  // open: Qn, preset, en, reset
  and and_3 (and_3_out, or_6_out, not_3_out);
  Counter #(.width(16), .max('hffff)) counter_2 (
    .count(InUse), .Q(\总周期数 ), .clk(CLK), .clr(RST));  // open: load, D, carry
  // Probe on \总周期数 
  // Probe on \无条件分支数 
  // Probe on \条件分支成功数 
  ROM #(.addrWidth(10), .dataWidth(32)) rom_1 (.addr(PC[11:2]), .data({rom_1_data, Adress}));  // open: sel
  Adder #(.width(32)) adder_1 (.a(PC), .b(32'h4), .out({adder_1_out_2, adder_1_out}));  // open: cin, cout
  Button _1 (.out(IR1));
  Button _2 (.out(IR2));
  Button _3 (.out(IR3));
  LED led_1 (.in(W1));
  LED led_2 (.in(W2));
  LED led_3 (.in(W3));
  assign bit_extender_1_out = {{16{1'b0}}, Adress[15:0]};  // Bit_Extender bit_extender_1
  assign bit_extender_2_out = {{16{Adress[15]}}, Adress[15:0]};  // Bit_Extender bit_extender_2
  not not_4 (not_4_out, eret);
  D_Flip_Flop d_ff_4 (.clk(CLK), .D(and_7_out), .Q(d_ff_4_q), .en(IR_CPU));  // open: Qn, preset, reset
  \硬布线控制器  \u_硬布线控制器_1  (
    .Func(Adress[5:0]), .OP(rom_1_data), .ALU_OP(\硬布线控制器_1_alu_op ), .MemToReg(\硬布线控制器_1_memtoreg ),
    .MemWrite(\硬布线控制器_1_memwrite ), .ALU_SRC(\硬布线控制器_1_alu_src ), .RegWrite(\硬布线控制器_1_regwrite ),
    .SysCALL(syscall), .SignedExt(SignedExt), .RegDst(\硬布线控制器_1_regdst ), .JR(\硬布线控制器_1_jr ),
    .JMP(\硬布线控制器_1_jmp ), .Beq(\硬布线控制器_1_beq ), .JAL(JAL), .Bne(\硬布线控制器_1_bne ), .SRAV(SRAV), .LH(lh),
    .BLTZ(BLTZ), .ERET(eret));
  Multiplexer #(.width(5), .enable("false")) multiplexer_6 (
    .in0(Adress[25:21]), .in1(5'b00100), .out(multiplexer_6_out), .sel(syscall));
  Multiplexer #(.width(5), .enable("false")) multiplexer_7 (
    .in0(Adress[20:16]), .in1(5'b00010), .out(multiplexer_7_out), .sel(syscall));
  Multiplexer #(.width(32), .enable("false")) multiplexer_8 (
    .in0(bit_extender_1_out), .in1(bit_extender_2_out), .out(multiplexer_8_out), .sel(SignedExt));
  Shifter #(.width(32)) shifter_1 (.in(bit_extender_2_out), .\dist (5'b00010), .out(shifter_1_out));
  Priority_Encoder #(.select(2)) priority_encoder_1 (
    .in0(1'b0), .in1(INT1), .in2(INT2), .in3(INT3), .out(priority_encoder_1_out), .gs(priority_encoder_1_gs));  // open: en_out, en_in
  D_Flip_Flop IE (.clk(CLK), .D(1'b1), .Q(IE_q), .preset(eret), .en(not_5_out), .reset(and_4_out));  // open: Qn
  not not_5 (not_5_out, IE_q);
  and and_4 (and_4_out, not_4_out, d_ff_4_q);
  Multiplexer #(.width(5), .enable("false")) multiplexer_9 (
    .in0(Adress[20:16]), .in1(Adress[15:11]), .out(multiplexer_9_out), .sel(\硬布线控制器_1_regdst ));
  Multiplexer #(.width(5), .enable("false")) multiplexer_10 (
    .in0(multiplexer_9_out), .in1({5{1'b1}}), .out(multiplexer_10_out), .sel(JAL));
  Adder #(.width(32)) adder_2 (
    .a(shifter_1_out), .b({adder_1_out_2, adder_1_out}), .out(adder_2_out));  // open: cin, cout
  Comparator #(.width(32)) comparator_1 (.a(rs), .b({32{1'b0}}), .lt(comparator_1_lt));  // open: gt, eq
  and and_5 (and_5_out, comparator_1_lt, BLTZ);
  Multiplexer #(.select(2), .width(32), .enable("false")) multiplexer_11 (
    .in1(32'h4), .in2(32'h78), .in3(32'hec), .out(Addr), .sel(priority_encoder_1_out));  // open: in0
  and and_6 (IR_CPU, priority_encoder_1_gs, IE_q);
  Multiplexer #(.width(32), .enable("false")) multiplexer_12 (
    .in0(multiplexer_18_out), .in1({adder_1_out_2, adder_1_out}), .out(multiplexer_12_out), .sel(JAL));
  Multiplexer #(.width(32), .enable("false")) multiplexer_13 (
    .in0(branch0), .in1(adder_2_out), .out(branch1), .sel(and_5_out));
  not not_6 (not_6_out, eret);
  MIPS_Regifile mips_regifile_1 (
    .Din(multiplexer_12_out), .Clk(CLK), .R1(rs), .R2(mips_regifile_1_r2), .WE(\硬布线控制器_1_regwrite ),
    .W_num(multiplexer_10_out), .R1_num(multiplexer_6_out), .R2_num(multiplexer_7_out));
  Decoder #(.select(2), .enable("false")) decoder_1 (
    .out1(decoder_1_out1), .out2(decoder_1_out2), .out3(decoder_1_out3), .sel(EPC_q));  // open: out0
  Register #(.width(2)) u_EPC (.D(priority_encoder_1_out), .Q(EPC_q), .clk(and_7_out));  // open: en, clr
  and and_7 (and_7_out, IR_CPU, not_6_out);
  Multiplexer #(.width(32), .enable("false")) multiplexer_14 (
    .in0(mips_regifile_1_r2), .in1(multiplexer_8_out), .out(multiplexer_14_out), .sel(\硬布线控制器_1_alu_src ));
  Shifter #(.width(32)) shifter_2 (.in(bit_extender_2_out), .\dist (5'b00010), .out(shifter_2_out));
  Comparator #(.width(32)) comparator_2 (.a(mips_regifile_1_r2), .b(32'h22), .eq(comparator_2_eq));  // open: gt, lt
  Register #(.width(32)) EPC_2 (.D(PC), .en(and_7_out), .Q(EPC), .clk(CLK));  // open: clr
  MIPS_ALU mips_alu_1 (
    .X(rs), .Y(multiplexer_14_out), .AluOP(\硬布线控制器_1_alu_op ), .Equal(mips_alu_1_equal),
    .Result({mips_alu_1_result[31:2], \片选 , mips_alu_1_result[0]}), .shamt(multiplexer_15_out));  // open: Result_2
  Multiplexer #(.width(5), .enable("false")) multiplexer_15 (
    .in0(Adress[10:6]), .in1(rs[4:0]), .out(multiplexer_15_out), .sel(SRAV));
  and and_8 (and_8_out, syscall, comparator_2_eq);
  and and_9 (eret1, eret, decoder_1_out1);
  and and_10 (eret2, decoder_1_out2, eret);
  and and_11 (eret3, decoder_1_out3, eret);
  and and_12 (and_12_out, mips_alu_1_equal, \硬布线控制器_1_beq );
  and and_13 (and_13_out, \硬布线控制器_1_bne , ~mips_alu_1_equal);  // AND_Gate
  Adder #(.width(32)) adder_3 (
    .a(shifter_2_out), .b({adder_1_out_2, adder_1_out}), .out(adder_3_out));  // open: cin, cout
  Register #(.width(32)) register_1 (.D(rs), .en(and_8_out), .Q(LedData), .clk(CLK), .clr(RST));
  not not_7 (not_7_out, comparator_2_eq);
  or or_8 (or_8_out, and_12_out, and_13_out);
  and and_14 (and_14_out, syscall, not_7_out);
  Counter #(.width(16), .max('hffff)) counter_3 (
    .count(or_8_out), .Q(\条件分支成功数 ), .clk(CLK), .clr(RST));  // open: load, D, carry
  RAM #(.addrWidth(10), .dataWidth(32), .bus("separate")) ram_1 (
    .addr(mips_alu_1_result[11:2]), .din(mips_regifile_1_r2), .data(ram_1_data), .str(\硬布线控制器_1_memwrite ),
    .sel(1'b1), .clk(CLK), .ld(\硬布线控制器_1_memtoreg ), .clr(RST));
  assign bit_extender_3_out = {{16{multiplexer_16_out[15]}}, multiplexer_16_out};  // Bit_Extender bit_extender_3
  assign bit_extender_4_out = {{16{multiplexer_16_out_2[15]}}, multiplexer_16_out_2};  // Bit_Extender bit_extender_4
  not not_8 (InUse, register_2_q);
  Register #(.width(1)) register_2 (.D(syscall), .en(and_14_out), .Q(register_2_q), .clk(CLK), .clr(or_9_out));
  or or_9 (or_9_out, RST, Go);
  Multiplexer #(.width(32), .enable("false")) multiplexer_16 (
    .in0({mips_alu_1_result[31:2], \片选 , mips_alu_1_result[0]}), .in1(ram_1_data),
    .out({multiplexer_16_out_2, multiplexer_16_out}), .sel(\硬布线控制器_1_memtoreg ));
  Multiplexer #(.width(32), .enable("false")) multiplexer_17 (
    .in0(bit_extender_3_out), .in1(bit_extender_4_out), .out(multiplexer_17_out), .sel(\片选 ));
  Multiplexer #(.width(32), .enable("false")) multiplexer_18 (
    .in0({multiplexer_16_out_2, multiplexer_16_out}), .in1(multiplexer_17_out), .out(multiplexer_18_out),
    .sel(lh));

  // Other names for the same wires on the sheet: shamt[4:0] = Adress[10:6]

  // Notes on the sheet:
  //   数码管输出应该用寄存器锁存，否则显示数据只能一闪而过
  //   可以通过项目增加Logisim库的方式将前几次实验完成的电路作为子电路引入到本电路中使用
  //   数码管输出
  //   指令存储器
  //   总复位信号应将除ROM以外所有存储组件全部清零
  //   指令字
  //   contents of rom_1 (hex, n*v repeats v):
  //   8100058 23bdfffc afa20000 23bdfffc afa40000 23bdfffc afa80000 23bdfffc afb10000 20160001 20140006
  //   20150001 168020 108100 2149825 132020 20020022 c 1600fffa 295a022 1680fff7 8fb10000 23bd0004
  //   8fa80000 23bd0004 8fa40000 23bd0004 8fa20000 23bd0004 42000018 23bdfffc afa20000 23bdfffc afa40000
  //   23bdfffc afa80000 23bdfffc afb10000 20160002 20140006 20150001 168020 108100 2149825 132020 20020022
  //   c 1600fffa 295a022 1680fff7 8fb10000 23bd0004 8fa80000 23bd0004 8fa40000 23bd0004 8fa20000 23bd0004
  //   42000018 23bdfffc afa20000 23bdfffc afa40000 23bdfffc afa80000 23bdfffc afb10000 20160003 20140006
  //   20150001 168020 108100 2149825 132020 20020022 c 1600fffa 295a022 1680fff7 8fb10000 23bd0004
  //   8fa80000 23bd0004 8fa40000 23bd0004 8fa20000 23bd0004 42000018 20110200 20020022 112020 c 2231ffff
  //   1620fffc 20020032 c 20080001 20090003 20110876 118d00 112020 20020022 c 200b0008 1118807 1318807
  //   112020 20020022 c 216bffff 1560fff9 2002000a c 2008ffff 20117777 112020 20020022 c 200b0010 3a31ffff
  //   112020 20020022 c 216bffff 1560fffa 2002000a c 20090000 200b0010 34118483 20120404 118c00 129400
  //   36318281 22520404 ad310000 2328820 21290004 216bffff 1560fffb 200b0020 20090000 85310000 112020
  //   20020022 c 21290002 216bffff 1560fff9 2002000a c 2011fff1 112020 20020022 c 22310001 620fffb
  //   2002000a c 2002000a c
  //   中断源
  //   Shamt
  //   OP
  //   Func
  //   rs
  //   rt
  //   rd
  //   Adress
  //   中断等待指示
  //   JMP
  //   JR
  //   OP
  //   Func
  //   Beq
  //   MemToReg
  //   MemWrite
  //   AluOP
  //   AluSrcB
  //   RegWrite
  //   JAL
  //   RegDst
  //   Syscall
endmodule

module \流水线中断  (
);

  wire and_2_out, and_3_out, and_4_out, and_5_out, and_6_out, and_7_out, and_8_out, and_9_out, and_13_out,
       and_14_out, and_15_out, and_16_out, and_17_out, and_18_out, and_19_out, Beq, BLTZ, Bne, CLK,
       comparator_1_lt, comparator_2_eq, comparator_3_eq, comparator_4_eq, comparator_5_eq, comparator_6_eq,
       d_ff_1_q, d_ff_2_q, d_ff_3_q, d_ff_4_q, d_ff_5_q, decoder_1_out1, decoder_1_out2, decoder_1_out3,
       eret, eret1, eret2, eret3, EX_ALU_SRC, EX_Beq, EX_BLTZ, EX_BLTZ_s, EX_Bne, EX_Branch, \EX_Branch_有 ,
       EX_eret, EX_JMP, EX_JR, EX_LH, ex_mem_1_lh_2, ex_mem_1_memwrite_2, ex_mem_1_syscall_2, EX_MemToReg,
       EX_SRAV, EX_Sys, Go, halt, id_ex_1_jal_2, id_ex_1_memwrite_2, id_ex_1_regdst_2, id_ex_1_regwrite_2,
       IE_q, INT1, INT2, INT3, InUse, IR1, IR2, IR3, IR_CPU, Jal, JMP, JR, LH, \LoadUse相关 , MEM_Jal,
       mem_wb_1_syscall_2, MemToReg, MemToReg_2, MemWrite, mips_alu_1_equal, NEqual, not_1_out, not_2_out,
       not_3_out, not_4_out, not_5_out, not_6_out, not_7_out, not_8_out, not_9_out, or_1_out, or_5_out,
       or_6_out, or_7_out, or_8_out, or_9_out, or_10_out, or_14_out, priority_encoder_1_gs, RegDst, RegDst_2,
       RegDst_r, RegWrite, RegWrite_2, RST, SignedExt, SRAV, Sys, W1, W2, W3, WB_Jal, WE, \硬布线控制器_1_alu_src ;
  wire [1:0] forward_1_forward_r1, forward_1_forward_r2, priority_encoder_1_out, register_1_q;
  wire [3:0] ALUOP, ALUOP_1;
  wire [4:0] EX_rt, ID_R1_num, ID_R2_num, MEM_rd, MEM_rt, MEM_WriteReg_num, multiplexer_9_out,
       multiplexer_11_out, multiplexer_15_out, multiplexer_16_out, multiplexer_18_out, multiplexer_25_out,
       multiplexer_26_out, rd, rt, shamt_1, WB_WriteReg_num;
  wire [5:0] ID_Func, ID_OP;
  wire [15:0] \LoadUse次数 , multiplexer_24_out, multiplexer_24_out_2, \总周期数 , \无条件分支数 , \条件分支成功数 ;
  wire [25:0] ex_mem_1_addr_26_2;
  wire [25:6] IR;
  wire [27:2] id_ex_1_addr_26_2;
  wire [31:0] adder_1_out, adder_3_out, Addr, ALU_Result, bit_extender_1_out, bit_extender_2_out,
       bit_extender_3_out, bit_extender_4_out, bit_extender_5_out, EPC, EX__rs, EX_IMM, EX_IMM_1,
       ex_mem_1_a_2, ex_mem_1_b_2, ex_mem_1_ir_2, EX_PC, EX_R2, \id_ex_1_addr_有_2 , id_ex_1_ir_2, ID_PC,
       IF_PC, LedData, MEM_PC, MEM_ReadData, mem_wb_1_a_2, mem_wb_1_b_2, mem_wb_1_ir_2, mem_wb_1_md_2,
       mips_alu_1_result, mips_regifile_1_r1, mips_regifile_1_r2, multiplexer_1_out, multiplexer_2_out,
       multiplexer_3_out, multiplexer_4_out, multiplexer_5_out, multiplexer_6_out, multiplexer_10_out,
       multiplexer_17_out, multiplexer_19_out, multiplexer_20_out, multiplexer_22_out, multiplexer_27_out,
       multiplexer_30_out, PC_q, R1_Final, R2_Final, R2_Final_1, ram_1_data, rom_1_data, shifter_1_out, WB_PC;

  Button \u_总复位  (.out(RST));
  Button _1 (.out(IR1));
  Button _2 (.out(IR2));
  Button _3 (.out(IR3));
  Button \u_继续运行  (.out(Go));
  LED led_1 (.in(W1));
  LED led_2 (.in(W2));
  LED led_3 (.in(W3));
  Multiplexer #(.width(32), .enable("false")) multiplexer_1 (
    .in0(IF_PC), .in1(\id_ex_1_addr_有_2 ), .out(multiplexer_1_out), .sel(\EX_Branch_有 ));
  Hex_Digit_Display hex_digit_display_1 (.value(LedData[31:28]));  // open: dp
  or or_1 (or_1_out, EX_JMP, EX_JR);
  Multiplexer #(.width(32), .enable("false")) multiplexer_2 (
    .in0(multiplexer_6_out), .in1({EX_PC[31:28], id_ex_1_addr_26_2, 2'b00}), .out(multiplexer_2_out),
    .sel(EX_JMP));
  Multiplexer #(.width(32), .enable("false")) multiplexer_3 (
    .in0(multiplexer_2_out), .in1(R1_Final), .out(multiplexer_3_out), .sel(EX_JR));
  Comparator #(.width(32)) comparator_1 (.a(R1_Final), .b({32{1'b0}}), .lt(comparator_1_lt));  // open: gt, eq
  or or_2 (W1, INT1, d_ff_1_q);
  or or_3 (W2, INT2, d_ff_2_q);
  or or_4 (W3, INT3, d_ff_3_q);
  Hex_Digit_Display hex_digit_display_2 (.value(LedData[27:24]));  // open: dp
  Hex_Digit_Display hex_digit_display_3 (.value(LedData[23:20]));  // open: dp
  Counter #(.width(16), .max('hffff), .ongoal("stay")) counter_1 (
    .count(or_1_out), .Q(\无条件分支数 ), .clk(CLK), .clr(RST));  // open: load, D, carry
  Multiplexer #(.width(32), .enable("false")) multiplexer_4 (
    .in0(multiplexer_3_out), .in1(Addr), .out(multiplexer_4_out), .sel(IR_CPU));
  Register #(.width(32)) PC (.D(multiplexer_5_out), .en(InUse), .Q(PC_q), .clk(CLK), .clr(RST));
  Adder #(.width(32)) adder_1 (.a(EX_IMM), .b(EX_PC), .out(adder_1_out));  // open: cin, cout
  and and_1 (EX_BLTZ_s, comparator_1_lt, EX_BLTZ);
  D_Flip_Flop d_ff_1 (.clk(IR1), .D(1'b1), .Q(d_ff_1_q), .reset(INT1));  // open: Qn, preset, en
  D_Flip_Flop d_ff_2 (.clk(IR2), .D(1'b1), .Q(d_ff_2_q), .reset(INT2));  // open: Qn, preset, en
  D_Flip_Flop d_ff_3 (.clk(IR3), .D(1'b1), .Q(d_ff_3_q), .reset(INT3));  // open: Qn, preset, en
  Hex_Digit_Display hex_digit_display_4 (.value(LedData[19:16]));  // open: dp
  Hex_Digit_Display hex_digit_display_5 (.value(LedData[15:12]));  // open: dp
  Multiplexer #(.width(32), .enable("false")) multiplexer_5 (
    .in0(multiplexer_4_out), .in1(EPC), .out(multiplexer_5_out), .sel(EX_eret));
  Multiplexer #(.width(32), .enable("false")) multiplexer_6 (
    .in0(multiplexer_1_out), .in1(adder_1_out), .out(multiplexer_6_out), .sel(EX_BLTZ_s));
  or or_5 (or_5_out, d_ff_1_q, INT1);
  or or_6 (or_6_out, d_ff_2_q, INT2);
  or or_7 (or_7_out, d_ff_3_q, INT3);
  Hex_Digit_Display hex_digit_display_6 (.value(LedData[11:8]));  // open: dp
  Hex_Digit_Display hex_digit_display_7 (.value(LedData[7:4]));  // open: dp
  Clock clock_1 (.out(CLK));
  ROM #(.addrWidth(10), .dataWidth(32)) rom_1 (.addr(PC_q[11:2]), .data(rom_1_data));  // open: sel
  Adder #(.width(32)) adder_2 (.a(PC_q), .b(32'h4), .out(IF_PC));  // open: cin, cout
  not not_1 (not_1_out, \LoadUse相关 );
  and and_2 (and_2_out, not_1_out, not_2_out);
  not not_2 (not_2_out, halt);
  not not_3 (not_3_out, eret1);
  not not_4 (not_4_out, eret2);
  not not_5 (not_5_out, eret3);
  Hex_Digit_Display hex_digit_display_8 (.value(LedData[3:0]));  // open: dp
  IF_ID if_id_1 (
    .IR(rom_1_data), .IR_2({ID_OP, IR, ID_Func}), .clk(CLK), .halt(and_2_out), .rst(or_9_out), .PC(IF_PC),
    .PC_2(ID_PC));  // open: 预测跳转, 预测跳转_2, 预测地址, 预测地址_2, Hit, Hit_2, HitPos, HitPos_2
  and and_3 (and_3_out, or_5_out, not_3_out);
  and and_4 (and_4_out, or_6_out, not_4_out);
  and and_5 (and_5_out, or_7_out, not_5_out);
  D_Flip_Flop u_IR1 (.clk(CLK), .D(and_3_out), .Q(INT1));  // open: Qn, preset, en, reset
  D_Flip_Flop u_IR2 (.clk(CLK), .D(and_4_out), .Q(INT2));  // open: Qn, preset, en, reset
  D_Flip_Flop u_IR3 (.clk(CLK), .D(and_5_out), .Q(INT3));  // open: Qn, preset, en, reset
  // Probe on \总周期数 
  // Probe on \无条件分支数 
  // Probe on \条件分支成功数 
  // Probe on \LoadUse次数 
  // Probe on \LoadUse次数 
  or or_8 (or_8_out, ~halt, InUse);  // OR_Gate
  Counter #(.width(16), .max('hffff), .ongoal("stay")) counter_2 (
    .count(and_6_out), .Q(\LoadUse次数 ), .clk(CLK), .clr(RST));  // open: load, D, carry
  and and_6 (and_6_out, \LoadUse相关 , ~halt);  // AND_Gate
  // Probe on IF_PC[11:0]
  Counter #(.width(16), .max('hffff)) counter_3 (
    .count(or_8_out), .Q(\总周期数 ), .clk(CLK), .clr(RST));  // open: load, D, carry
  \硬布线控制器  \u_硬布线控制器_1  (
    .Func(ID_Func), .OP(ID_OP), .ALU_OP(ALUOP), .MemToReg(MemToReg), .MemWrite(MemWrite),
    .ALU_SRC(\硬布线控制器_1_alu_src ), .RegWrite(RegWrite), .SysCALL(Sys), .SignedExt(SignedExt), .RegDst(RegDst),
    .JR(JR), .JMP(JMP), .Beq(Beq), .JAL(Jal), .Bne(Bne), .SRAV(SRAV), .LH(LH), .BLTZ(BLTZ), .ERET(eret));
  Multiplexer #(.width(5), .enable("false")) multiplexer_7 (
    .in0(IR[25:21]), .in1(5'b00100), .out(ID_R1_num), .sel(Sys));
  // Probe on ID_PC[11:0]
  Multiplexer #(.width(5), .enable("false")) multiplexer_8 (
    .in0(IR[20:16]), .in1(5'b00010), .out(ID_R2_num), .sel(Sys));
  Multiplexer #(.width(5), .enable("false")) multiplexer_9 (
    .in0(rt), .in1(rd), .out(multiplexer_9_out), .sel(RegDst_r));
  assign bit_extender_1_out = {{16{1'b0}}, {IR[15:6], ID_Func}};  // Bit_Extender bit_extender_1
  Multiplexer #(.width(32), .enable("false")) multiplexer_10 (
    .in0(bit_extender_1_out), .in1(bit_extender_2_out), .out(multiplexer_10_out), .sel(SignedExt));
  assign bit_extender_2_out = {{16{IR[15]}}, {IR[15:6], ID_Func}};  // Bit_Extender bit_extender_2
  not not_6 (not_6_out, EX_eret);
  D_Flip_Flop d_ff_4 (.clk(CLK), .D(and_9_out), .Q(d_ff_4_q), .en(and_8_out));  // open: Qn, preset, reset
  // Probe on MEM_PC[11:0]
  // Probe on EX_PC[11:0]
  or or_9 (or_9_out, EX_Branch, IR_CPU, RST);
  Multiplexer #(.width(5), .enable("false")) multiplexer_11 (
    .in0(multiplexer_9_out), .in1({5{1'b1}}), .out(multiplexer_11_out), .sel(WB_Jal));
  Priority_Encoder #(.select(2)) priority_encoder_1 (
    .in0(1'b0), .in1(INT1), .in2(INT2), .in3(INT3), .out(priority_encoder_1_out), .gs(priority_encoder_1_gs));  // open: en_out, en_in
  D_Flip_Flop IE (.clk(CLK), .D(1'b1), .Q(IE_q), .preset(EX_eret), .en(not_7_out), .reset(and_7_out));  // open: Qn
  not not_7 (not_7_out, IE_q);
  and and_7 (and_7_out, not_6_out, d_ff_4_q);
  // Probe on WB_PC[11:0]
  Multiplexer #(.width(32), .enable("false")) multiplexer_12 (
    .in0(mem_wb_1_md_2), .in1(WB_PC), .out(MEM_ReadData), .sel(WB_Jal));
  Shifter #(.width(32)) shifter_1 (.in(bit_extender_2_out), .\dist (5'b00010), .out(shifter_1_out));
  Multiplexer #(.select(2), .width(32), .enable("false")) multiplexer_13 (
    .in1(32'h4), .in2(32'h78), .in3(32'hec), .out(Addr), .sel(priority_encoder_1_out));  // open: in0
  and and_8 (and_8_out, priority_encoder_1_gs, IE_q);
  or or_10 (or_10_out, \LoadUse相关 , or_9_out);
  LoadUse loaduse_1 (
    .OP(ID_OP), .EX_MemToReg(EX_MemToReg), .EX_rt(EX_rt), .\数据相关 (\LoadUse相关 ), .Func(ID_Func),
    .ID_R1_num(ID_R1_num), .ID_R2_num(ID_R2_num));
  not not_8 (not_8_out, CLK);
  Adder #(.width(32)) adder_3 (.a(shifter_1_out), .b(ID_PC), .out(adder_3_out));  // open: cin, cout
  or or_11 (IR_CPU, d_ff_5_q, and_8_out);
  D_Flip_Flop d_ff_5 (.clk(CLK), .D(and_8_out), .Q(d_ff_5_q));  // open: Qn, preset, en, reset
  not not_9 (not_9_out, EX_eret);
  MIPS_Regifile mips_regifile_1 (
    .Din(MEM_ReadData), .Clk(not_8_out), .R1(mips_regifile_1_r1), .R2(mips_regifile_1_r2), .WE(WE),
    .W_num(multiplexer_11_out), .R1_num(ID_R1_num), .R2_num(ID_R2_num));
  Register #(.width(2)) register_1 (.D(priority_encoder_1_out), .Q(register_1_q), .clk(and_9_out));  // open: en, clr
  and and_9 (and_9_out, and_8_out, not_9_out);
  Multiplexer #(.width(32), .enable("false")) multiplexer_14 (
    .in0(R2_Final_1), .in1(EX_IMM_1), .out(R2_Final), .sel(EX_ALU_SRC));
  Decoder #(.select(2), .enable("false")) decoder_1 (
    .out1(decoder_1_out1), .out2(decoder_1_out2), .out3(decoder_1_out3), .sel(register_1_q));  // open: out0
  ID_EX id_ex_1 (
    .IR({ID_OP, IR, ID_Func}), .PC(ID_PC), .A(mips_regifile_1_r1), .Shamt(IR[10:6]), .MemToReg(MemToReg),
    .MemWrite(MemWrite), .ALUOP(ALUOP), .RegWrite(RegWrite), .RegDst(RegDst), .R2(mips_regifile_1_r2),
    .Syscall(Sys), .IR_2({id_ex_1_ir_2[31:21], EX_rt, id_ex_1_ir_2[15:0]}), .PC_2(EX_PC), .A_2(EX__rs),
    .Shamt_2(shamt_1), .MemToReg_2(EX_MemToReg), .MemWrite_2(id_ex_1_memwrite_2), .ALUOP_2(ALUOP_1),
    .RegWrite_2(id_ex_1_regwrite_2), .RegDst_2(id_ex_1_regdst_2), .R2_2(EX_R2), .Syscall_2(EX_Sys),
    .clk(CLK), .halt(not_2_out), .rst(or_10_out), .Beq(Beq), .Beq_2(EX_Beq), .Bne(Bne), .Bne_2(EX_Bne),
    .Jal(Jal), .Jal_2(id_ex_1_jal_2), .JMP(JMP), .JMP_2(EX_JMP), .JR(JR), .JR_2(EX_JR),
    .\Addr_有 (adder_3_out), .\Addr_有_2 (\id_ex_1_addr_有_2 ), .Addr_26({IR, ID_Func}),
    .Addr_26_2(id_ex_1_addr_26_2), .SRAV(SRAV), .SRAV_2(EX_SRAV), .LH(LH), .LH_2(EX_LH), .BLTZ(BLTZ),
    .BLTZ_2(EX_BLTZ), .ALU_SRC(\硬布线控制器_1_alu_src ), .ALU_SRC_2(EX_ALU_SRC), .IMM(multiplexer_10_out),
    .IMM_2(EX_IMM_1), .ERET(eret), .ERET_2(EX_eret));  // open: B, B_2, 预测跳转, 预测跳转_2, 预测地址, 预测地址_2, Hit, Hit_2, HitPos, HitPos_2
  and and_10 (eret1, EX_eret, decoder_1_out1);
  and and_11 (eret2, decoder_1_out2, EX_eret);
  and and_12 (eret3, decoder_1_out3, EX_eret);
  Multiplexer #(.width(5), .enable("false")) multiplexer_15 (
    .in0(id_ex_1_ir_2[25:21]), .in1(5'b00100), .out(multiplexer_15_out), .sel(EX_Sys));
  or or_12 (EX_Branch, EX_JMP, \EX_Branch_有 , EX_JR);
  Forward forward_1 (
    .OP(id_ex_1_ir_2[31:26]), .WB_WriteReg_num(WB_WriteReg_num), .WB_RegWrite(WE),
    .MEM_WriteReg_num(MEM_WriteReg_num), .MEM_RegWrite(RegWrite_2), .Forward_R1(forward_1_forward_r1),
    .Func(id_ex_1_ir_2[5:0]), .EX_R1_num(multiplexer_15_out), .EX_R2_num(multiplexer_16_out),
    .Forward_R2(forward_1_forward_r2));
  Multiplexer #(.width(5), .enable("false")) multiplexer_16 (
    .in0(EX_rt), .in1(5'b00010), .out(multiplexer_16_out), .sel(EX_Sys));
  assign bit_extender_3_out = {{16{id_ex_1_ir_2[15]}}, id_ex_1_ir_2[15:0]};  // Bit_Extender bit_extender_3
  Comparator #(.width(32), .mode("unsigned")) comparator_2 (
    .a(ID_PC), .b({32{1'b0}}), .eq(comparator_2_eq));  // open: gt, lt
  Comparator #(.width(32), .mode("unsigned")) comparator_3 (
    .a(EX_PC), .b({32{1'b0}}), .eq(comparator_3_eq));  // open: gt, lt
  Comparator #(.width(32), .mode("unsigned")) comparator_4 (
    .a(MEM_PC), .b({32{1'b0}}), .eq(comparator_4_eq));  // open: gt, lt
  Comparator #(.width(32), .mode("unsigned")) comparator_5 (
    .a(WB_PC), .b({32{1'b0}}), .eq(comparator_5_eq));  // open: gt, lt
  Multiplexer #(.width(32), .enable("false")) multiplexer_17 (
    .in0(MEM_PC), .in1(WB_PC), .out(multiplexer_17_out), .sel(NEqual));
  Shifter #(.width(32)) shifter_2 (.in(bit_extender_3_out), .\dist (5'b00010), .out(EX_IMM));
  and and_13 (and_13_out, EX_Beq, mips_alu_1_equal);
  and and_14 (and_14_out, EX_Bne, ~mips_alu_1_equal);  // AND_Gate
  MIPS_ALU mips_alu_1 (
    .X(R1_Final), .Y(R2_Final), .AluOP(ALUOP_1), .Equal(mips_alu_1_equal), .Result(mips_alu_1_result),
    .shamt(multiplexer_18_out));  // open: Result_2
  Multiplexer #(.width(5), .enable("false")) multiplexer_18 (
    .in0(shamt_1), .in1(EX__rs[4:0]), .out(multiplexer_18_out), .sel(EX_SRAV));
  and and_15 (and_15_out, comparator_2_eq, comparator_3_eq);
  and and_16 (and_16_out, comparator_3_eq, comparator_4_eq);
  and and_17 (and_17_out, comparator_4_eq, comparator_5_eq);
  or or_13 (\EX_Branch_有 , and_13_out, EX_BLTZ_s, and_14_out);
  Multiplexer #(.width(32), .enable("false")) multiplexer_19 (
    .in0(multiplexer_17_out), .in1(EX_PC), .out(multiplexer_19_out), .sel(and_17_out));
  Register #(.width(32)) u_EPC (.D(multiplexer_22_out), .en(and_9_out), .Q(EPC), .clk(CLK));  // open: clr
  Counter #(.width(16), .max('hffff)) counter_4 (
    .count(\EX_Branch_有 ), .Q(\条件分支成功数 ), .clk(CLK), .clr(RST));  // open: load, D, carry
  nor nor_1 (NEqual, and_17_out, and_16_out, and_15_out);
  Multiplexer #(.width(32), .enable("false")) multiplexer_20 (
    .in0(multiplexer_19_out), .in1(ID_PC), .out(multiplexer_20_out), .sel(and_16_out));
  Multiplexer #(.select(2), .width(32), .enable("false")) multiplexer_21 (
    .in0(EX__rs), .in1(ALU_Result), .in2(MEM_ReadData), .out(R1_Final), .sel(forward_1_forward_r1));  // open: in3
  EX_MEM ex_mem_1 (
    .IR({id_ex_1_ir_2[31:21], EX_rt, id_ex_1_ir_2[15:0]}), .PC(EX_PC), .Alu(mips_alu_1_result), .A(R1_Final),
    .B(R2_Final_1), .MemToReg(EX_MemToReg), .MemWrite(id_ex_1_memwrite_2), .RegWrite(id_ex_1_regwrite_2),
    .RegDst(id_ex_1_regdst_2), .Syscall(EX_Sys),
    .IR_2({ex_mem_1_ir_2[31:21], MEM_rt, MEM_rd, ex_mem_1_ir_2[10:0]}), .PC_2(MEM_PC), .Alu_2(ALU_Result),
    .A_2(ex_mem_1_a_2), .B_2(ex_mem_1_b_2), .MemToReg_2(MemToReg_2), .MemWrite_2(ex_mem_1_memwrite_2),
    .RegWrite_2(RegWrite_2), .RegDst_2(RegDst_2), .Syscall_2(ex_mem_1_syscall_2), .clk(CLK),
    .halt(not_2_out), .rst(RST), .Jal(id_ex_1_jal_2), .Jal_2(MEM_Jal), .Addr_26(id_ex_1_addr_26_2),
    .Addr_26_2(ex_mem_1_addr_26_2), .LH(EX_LH), .LH_2(ex_mem_1_lh_2));
  Multiplexer #(.width(32), .enable("false")) multiplexer_22 (
    .in0(multiplexer_20_out), .in1(IF_PC), .out(multiplexer_22_out), .sel(and_15_out));
  Multiplexer #(.select(2), .width(32), .enable("false")) multiplexer_23 (
    .in0(EX_R2), .in1(ALU_Result), .in2(MEM_ReadData), .out(R2_Final_1), .sel(forward_1_forward_r2));  // open: in3
  Multiplexer #(.width(32), .enable("false")) multiplexer_24 (
    .in0(ALU_Result), .in1(ram_1_data), .out({multiplexer_24_out_2, multiplexer_24_out}), .sel(MemToReg_2));
  RAM #(.addrWidth(10), .dataWidth(32), .bus("separate")) ram_1 (
    .addr(ALU_Result[11:2]), .din(ex_mem_1_b_2), .data(ram_1_data), .str(ex_mem_1_memwrite_2), .sel(1'b1),
    .clk(CLK), .ld(MemToReg_2));  // open: clr
  assign bit_extender_4_out = {{16{multiplexer_24_out[15]}}, multiplexer_24_out};  // Bit_Extender bit_extender_4
  assign bit_extender_5_out = {{16{multiplexer_24_out_2[15]}}, multiplexer_24_out_2};  // Bit_Extender bit_extender_5
  Multiplexer #(.width(5), .enable("false")) multiplexer_25 (
    .in0(rt), .in1(rd), .out(multiplexer_25_out), .sel(RegDst_r));
  Multiplexer #(.width(5), .enable("false")) multiplexer_26 (
    .in0(MEM_rt), .in1(MEM_rd), .out(multiplexer_26_out), .sel(RegDst_2));
  Multiplexer #(.width(32), .enable("false")) multiplexer_27 (
    .in0(bit_extender_4_out), .in1(bit_extender_5_out), .out(multiplexer_27_out), .sel(ALU_Result[1]));
  Multiplexer #(.width(5), .enable("false")) multiplexer_28 (
    .in0(multiplexer_25_out), .in1({5{1'b1}}), .out(WB_WriteReg_num), .sel(WB_Jal));
  Multiplexer #(.width(5), .enable("false")) multiplexer_29 (
    .in0(multiplexer_26_out), .in1({5{1'b1}}), .out(MEM_WriteReg_num), .sel(MEM_Jal));
  Multiplexer #(.width(32), .enable("false")) multiplexer_30 (
    .in0({multiplexer_24_out_2, multiplexer_24_out}), .in1(multiplexer_27_out), .out(multiplexer_30_out),
    .sel(ex_mem_1_lh_2));
  MEM_WB mem_wb_1 (
    .IR({ex_mem_1_ir_2[31:21], MEM_rt, MEM_rd, ex_mem_1_ir_2[10:0]}), .PC(MEM_PC), .A(ex_mem_1_a_2),
    .MD(multiplexer_30_out), .RegWrite(RegWrite_2), .RegDst(RegDst_2), .Syscall(ex_mem_1_syscall_2),
    .IR_2({mem_wb_1_ir_2[31:21], rt, rd, mem_wb_1_ir_2[10:0]}), .PC_2(WB_PC), .A_2(mem_wb_1_a_2),
    .MD_2(mem_wb_1_md_2), .RegWrite_2(WE), .RegDst_2(RegDst_r), .Syscall_2(mem_wb_1_syscall_2), .clk(CLK),
    .halt(not_2_out), .rst(RST), .Jal(MEM_Jal), .Jal_2(WB_Jal), .Addr_26(ex_mem_1_addr_26_2),
    .B(ex_mem_1_b_2), .B_2(mem_wb_1_b_2));  // open: Addr_26_2
  and and_18 (and_18_out, mem_wb_1_syscall_2, comparator_6_eq);
  Register #(.width(32)) register_2 (.D(mem_wb_1_a_2), .en(and_18_out), .Q(LedData), .clk(CLK));  // open: clr
  Comparator #(.width(32)) comparator_6 (.a(mem_wb_1_b_2), .b(32'h22), .eq(comparator_6_eq));  // open: gt, lt
  and and_19 (and_19_out, mem_wb_1_syscall_2, ~comparator_6_eq);  // AND_Gate
  Register #(.width(1)) register_3 (.D(mem_wb_1_syscall_2), .en(and_19_out), .Q(halt), .clk(CLK), .clr(or_14_out));
  or or_14 (or_14_out, RST, Go);
  and and_20 (InUse, ~halt, ~\LoadUse相关 );  // AND_Gate

  // Other names for the same wires on the sheet: 片选 = ALU_Result[1]; IR (some bits) = {ID_OP, ID_Func};
  //   shamt[4:0] = IR[10:6]; PC[31:0] = ID_PC; 插入气泡数[15:0] = \LoadUse次数 

  // Notes on the sheet:
  //   中断源
  //   中断等待指示
  //   数码管输出
  //   指令存储器
  //   contents of rom_1 (hex, n*v repeats v):
  //   8100058 23bdfffc afa20000 23bdfffc afa40000 23bdfffc afa80000 23bdfffc afb10000 20160001 20140006
  //   20150001 168020 108100 2149825 132020 20020022 c 1600fffa 295a022 1680fff7 8fb10000 23bd0004
  //   8fa80000 23bd0004 8fa40000 23bd0004 8fa20000 23bd0004 42000018 23bdfffc afa20000 23bdfffc afa40000
  //   23bdfffc afa80000 23bdfffc afb10000 20160002 20140006 20150001 168020 108100 2149825 132020 20020022
  //   c 1600fffa 295a022 1680fff7 8fb10000 23bd0004 8fa80000 23bd0004 8fa40000 23bd0004 8fa20000 23bd0004
  //   42000018 23bdfffc afa20000 23bdfffc afa40000 23bdfffc afa80000 23bdfffc afb10000 20160003 20140006
  //   20150001 168020 108100 2149825 132020 20020022 c 1600fffa 295a022 1680fff7 8fb10000 23bd0004
  //   8fa80000 23bd0004 8fa40000 23bd0004 8fa20000 23bd0004 42000018 20110200 20020022 112020 c 2231ffff
  //   1620fffc 20020032 c 20080001 20090003 20110876 118d00 112020 20020022 c 200b0008 1118807 1318807
  //   112020 20020022 c 216bffff 1560fff9 2002000a c 2008ffff 20117777 112020 20020022 c 200b0010 3a31ffff
  //   112020 20020022 c 216bffff 1560fffa 2002000a c 20090000 200b0010 34118483 20120404 118c00 129400
  //   36318281 22520404 ad310000 2328820 21290004 216bffff 1560fffb 200b0020 20090000 85310000 112020
  //   20020022 c 21290002 216bffff 1560fff9 2002000a c 2011fff1 112020 20020022 c 22310001 620fffb
  //   2002000a c 2002000a c
  //   Shamt
  //   OP
  //   Func
  //   rs
  //   rt
  //   Imm
  //   流水调试日志用
  //   OP
  //   Func
  //   rs
  //   rt
  //   rd
  //   rt
endmodule
